// Logisim project cpu24.circ as structural Verilog: 24 circuits, main circuit ◇单周期MIPS
module \单周期MIPS  (
  output [3:0] out_1,
  output [31:0] out_2,
  output [31:0] out_3,
  output [31:0] out_4,
  output [31:0] out_5,
  output [4:0] out_6,
  output [4:0] out_7
);

  wire \_1号中断 , \_1号中断等待指示 , \_2号中断 , \_2号中断等待指示 , \_3号中断 , \_3号中断等待指示 , Alus, and_4_out, and_5_out,
       and_6_out, and_7_out, and_8_out, and_9_out, and_10_out, and_11_out, Beq, BLEZ, Bne, CLK,
       comparator_1_eq, comparator_2_eq, comparator_4_gt, condi, d_ff_1_q, d_ff_2_q, d_ff_3_q, d_ff_4_q,
       demultiplexer_1_out1, demultiplexer_1_out2, demultiplexer_1_out3, equ, eret, Go, halt, IR1_q, IR2_2_q,
       IR2_q, JAL, JMP, JR, led, MemToReg, MemWrite, mfc0, nor_1_out, nor_2_out, not_1_out, not_2_out,
       or_2_out, or_7_out, or_8_out, or_9_out, pause, pcen, RegDst, RegWrite, RST, SB, SignedExt, SRAV, Sys;
  wire [1:0] intnum, nowint, priority_encoder_1_out, register_4_q;
  wire [1:1] and_12_out, PCSrc;
  wire [3:0] multiplexer_9_out, multiplexer_10_out;
  wire [4:0] CP0, multiplexer_2_out, multiplexer_3_out, multiplexer_4_out, multiplexer_5_out,
       multiplexer_8_out, rd;
  wire [15:0] imm, \总周期数 , \无条件分支数 , \条件分支成功数 ;
  wire [31:0] bit_extender_1_out, bit_extender_2_out, Ext, LedData, MemAddr, MemWrite_Data, mips_ram_1_p8,
       multiplexer_1_out, multiplexer_7_out, multiplexer_11_out, multiplexer_13_out, pc0, pc2, shifter_1_out,
       shifter_2_out, shifter_3_out, shifter_4_out;
  wire [31:26] rom_1_data;

  Comparator #(.width(32)) comparator_1 (.a(out_5), .b(32'h22), .eq(comparator_1_eq));  // open: gt, lt
  Comparator #(.width(32)) comparator_2 (.a(out_5), .b(32'ha), .eq(comparator_2_eq));  // open: gt, lt
  Button \u_总复位  (.out(RST));
  Button \u_继续运行  (.out(Go));
  Clock clock_1 (.out(CLK));
  and and_1 (led, comparator_1_eq, Sys);
  and and_2 (halt, Sys, comparator_2_eq);
  nor nor_1 (nor_1_out, halt, led);
  Multiplexer #(.select(2), .width(32), .enable("false")) multiplexer_1 (
    .in0(pc0), .in1(out_5), .in2(pc2), .in3({pc0[31:28], out_6, out_7, imm, 2'b00}), .out(multiplexer_1_out),
    .sel({PCSrc[1], JMP}));
  and and_3 (pause, nor_1_out, Sys);
  Register #(.width(32)) PC (.D(multiplexer_1_out), .en(pcen), .Q(out_3), .clk(CLK), .clr(RST));
  Hex_Digit_Display hex_digit_display_1 (.value(LedData[31:28]));  // open: dp
  Hex_Digit_Display hex_digit_display_2 (.value(LedData[27:24]));  // open: dp
  Counter #(.width(16), .max('hffff)) counter_1 (
    .count(JMP), .Q(\无条件分支数 ), .clk(CLK), .clr(RST));  // open: load, D, carry
  and and_4 (and_4_out, ~halt, Go);  // AND_Gate
  // Probe on out_3[11:2]
  Adder #(.width(32)) adder_1 (.a(out_3), .b(32'h4), .out(pc0));  // open: cin, cout
  Shifter #(.width(32)) shifter_1 (.in(Ext), .\dist (5'b00010), .out(shifter_1_out));
  or or_1 (PCSrc[1], condi, and_5_out);
  and and_5 (and_5_out, JMP, ~JR);  // AND_Gate
  Hex_Digit_Display hex_digit_display_3 (.value(LedData[19:16]));  // open: dp
  Hex_Digit_Display hex_digit_display_4 (.value(LedData[23:20]));  // open: dp
  Counter #(.width(16), .max('hffff)) counter_2 (
    .count(condi), .Q(\条件分支成功数 ), .clk(CLK), .clr(RST));  // open: load, D, carry
  nor nor_2 (nor_2_out, halt, Go, pause);
  D_Flip_Flop d_ff_1 (.clk(CLK), .D(and_4_out), .Q(d_ff_1_q), .reset(RST));  // open: Qn, preset, en
  or or_2 (or_2_out, halt, pause);
  Adder #(.width(32)) adder_2 (.a(pc0), .b(shifter_1_out), .out(pc2));  // open: cin, cout
  Hex_Digit_Display hex_digit_display_5 (.value(LedData[11:8]));  // open: dp
  Hex_Digit_Display hex_digit_display_6 (.value(LedData[15:12]));  // open: dp
  Counter #(.width(16), .max('hffff)) counter_3 (
    .count(nor_2_out), .Q(\总周期数 ), .clk(CLK), .clr(RST));  // open: load, D, carry
  not not_1 (not_1_out, d_ff_1_q);
  xor xor_1 (pcen, not_1_out, or_2_out);
  // Probe on {rom_1_data, out_6, out_7, imm}
  ROM #(.addrWidth(10), .dataWidth(32)) rom_1 (
    .addr(out_3[11:2]), .data({rom_1_data, out_6, out_7, imm}));  // open: sel
  Hex_Digit_Display hex_digit_display_7 (.value(LedData[7:4]));  // open: dp
  Hex_Digit_Display hex_digit_display_8 (.value(LedData[3:0]));  // open: dp
  Multiplexer #(.width(5), .enable("false")) multiplexer_2 (
    .in0(out_7), .in1(imm[15:11]), .out(multiplexer_2_out), .sel(RegDst));
  Multiplexer #(.width(5), .enable("false")) multiplexer_3 (
    .in0(out_6), .in1(5'b00010), .out(multiplexer_3_out), .sel(Sys));
  Multiplexer #(.width(5), .enable("false")) multiplexer_4 (
    .in0(out_7), .in1(5'b00100), .out(multiplexer_4_out), .sel(Sys));
  // Probe on multiplexer_5_out
  Multiplexer #(.width(5), .enable("false")) multiplexer_5 (
    .in0(multiplexer_2_out), .in1({5{1'b1}}), .out(multiplexer_5_out), .sel(JAL));
  \硬布线控制器  \u_硬布线控制器_1  (
    .Func(imm[5:0]), .OP(rom_1_data), .ALU_OP(out_1), .MemToReg(MemToReg), .MemWrite(MemWrite),
    .ALU_SRC(Alus), .RegWrite(RegWrite), .SysCALL(Sys), .SignedExt(SignedExt), .RegDst(RegDst), .JR(JR),
    .JMP(JMP), .Beq(Beq), .JAL(JAL), .Bne(Bne), .SRAV(SRAV), .BLEZ(BLEZ), .SB(SB), .MFC0(mfc0), .ERET(eret));
  assign bit_extender_1_out = {{16{1'b0}}, imm};  // Bit_Extender bit_extender_1
  assign bit_extender_2_out = {{16{imm[15]}}, imm};  // Bit_Extender bit_extender_2
  // Probe on \总周期数 
  // Probe on \无条件分支数 
  // Probe on \条件分支成功数 
  MIPS_Regifile mips_regifile_1 (
    .Din(out_2), .Clk(CLK), .R1(out_5), .R2(MemWrite_Data), .WE(RegWrite), .W_num(multiplexer_5_out),
    .R1_num(multiplexer_3_out), .R2_num(multiplexer_4_out));
  Multiplexer #(.width(32), .enable("false")) multiplexer_6 (
    .in0(bit_extender_1_out), .in1(bit_extender_2_out), .out(Ext), .sel(SignedExt));
  Multiplexer #(.width(32), .enable("false")) multiplexer_7 (
    .in0(MemWrite_Data), .in1(Ext), .out(multiplexer_7_out), .sel(Alus));
  Multiplexer #(.width(5), .enable("false")) multiplexer_8 (
    .in0(imm[10:6]), .in1(out_5[4:0]), .out(multiplexer_8_out), .sel(SRAV));
  Register #(.width(5)) register_1 (.D(rd), .en(mfc0), .Q(CP0), .clk(CLK), .clr(RST));
  Comparator #(.width(32)) comparator_3 (.a(out_5), .b(32'h22), .eq(led));  // open: gt, lt
  Comparator #(.width(32)) comparator_4 (.a(out_5), .b({32{1'b0}}), .gt(comparator_4_gt));  // open: eq, lt
  MIPS_ALU mips_alu_1 (
    .X(out_5), .Y(multiplexer_7_out), .AluOP(out_1), .Equal(equ), .Result(MemAddr), .shamt(multiplexer_8_out));  // open: Result_2
  and and_6 (and_6_out, Beq, equ);
  and and_7 (and_7_out, Bne, ~equ);  // AND_Gate
  and and_8 (and_8_out, BLEZ, ~comparator_4_gt);  // AND_Gate
  Multiplexer #(.select(2), .width(4), .enable("false")) multiplexer_9 (
    .in0(4'b0001), .in1(4'b0010), .in2(4'b0100), .in3(4'b1000), .out(multiplexer_9_out), .sel(MemAddr[1:0]));
  Register #(.width(32)) register_2 (.D(MemWrite_Data), .en(led), .Q(LedData), .clk(CLK), .clr(RST));
  or or_3 (condi, and_6_out, and_7_out, and_8_out);
  Multiplexer #(.width(4), .enable("false")) multiplexer_10 (
    .in0(4'b1111), .in1(multiplexer_9_out), .out(multiplexer_10_out), .sel(SB));
  Shifter #(.width(32)) shifter_2 (.in(MemWrite_Data), .\dist (5'b01000), .out(shifter_2_out));
  Shifter #(.width(32)) shifter_3 (.in(MemWrite_Data), .\dist (5'b10000), .out(shifter_3_out));
  Shifter #(.width(32)) shifter_4 (.in(MemWrite_Data), .\dist (5'b11000), .out(shifter_4_out));
  Multiplexer #(.select(2), .width(32), .enable("false")) multiplexer_11 (
    .in0(MemWrite_Data), .in1(shifter_2_out), .in2(shifter_3_out), .in3(shifter_4_out),
    .out(multiplexer_11_out), .sel(MemAddr[1:0]));
  // MIPS_RAM mips_ram_1: pin names not known; wires that end beside it: comparator_4_gt, {{10{1'b0}}, MemAddr[11:2]}, out_4, MemWrite, multiplexer_10_out, CLK, RST, mips_ram_1_p8
  Multiplexer #(.width(32), .enable("false")) multiplexer_12 (
    .in0(MemWrite_Data), .in1(multiplexer_11_out), .out(out_4), .sel(SB));
  Demultiplexer #(.select(2), .enable("false")) demultiplexer_1 (
    .out1(demultiplexer_1_out1), .out2(demultiplexer_1_out2), .out3(demultiplexer_1_out3), .in(eret),
    .sel(nowint));  // open: out0
  Multiplexer #(.width(32), .enable("false")) multiplexer_13 (
    .in0(MemAddr), .in1(mips_ram_1_p8), .out(multiplexer_13_out), .sel(MemToReg));
  Multiplexer #(.width(32), .enable("false")) multiplexer_14 (
    .in0(multiplexer_13_out), .in1(pc0), .out(out_2), .sel(JAL));
  D_Flip_Flop d_ff_2 (.clk(\_3号中断 ), .D(1'b1), .Q(d_ff_2_q), .reset(IR2_q));  // open: Qn, preset, en
  or or_4 (\_3号中断等待指示 , IR2_q, d_ff_2_q);
  D_Flip_Flop d_ff_3 (.clk(\_2号中断 ), .D(1'b1), .Q(d_ff_3_q), .reset(IR2_2_q));  // open: Qn, preset, en
  or or_5 (\_2号中断等待指示 , IR2_2_q, d_ff_3_q);
  D_Flip_Flop d_ff_4 (.clk(\_1号中断 ), .D(1'b1), .Q(d_ff_4_q), .reset(IR1_q));  // open: Qn, preset, en
  or or_6 (\_1号中断等待指示 , IR1_q, d_ff_4_q);
  or or_7 (or_7_out, d_ff_2_q, IR2_q);
  or or_8 (or_8_out, d_ff_3_q, IR2_2_q);
  or or_9 (or_9_out, d_ff_4_q, IR1_q);
  and and_9 (and_9_out, or_7_out, ~demultiplexer_1_out3);  // AND_Gate
  and and_10 (and_10_out, or_8_out, ~demultiplexer_1_out2);  // AND_Gate
  and and_11 (and_11_out, or_9_out, ~demultiplexer_1_out1);  // AND_Gate
  D_Flip_Flop IR2 (.clk(CLK), .D(and_9_out), .Q(IR2_q));  // open: Qn, preset, en, reset
  D_Flip_Flop IR2_2 (.clk(CLK), .D(and_10_out), .Q(IR2_2_q));  // open: Qn, preset, en, reset
  D_Flip_Flop IR1 (.clk(CLK), .D(and_11_out), .Q(IR1_q));  // open: Qn, preset, en, reset
  Priority_Encoder #(.select(2)) priority_encoder_1 (
    .in0(1'b1), .in1(IR1_q), .in2(IR2_2_q), .in3(IR2_q), .out(priority_encoder_1_out));  // open: gs, en_out, en_in
  not not_2 (not_2_out, mfc0);
  Register #(.width(2)) register_3 (.D(priority_encoder_1_out), .en(mfc0), .Q(nowint), .clk(CLK));  // open: clr
  Register #(.width(2)) register_4 (.D(priority_encoder_1_out), .Q(register_4_q), .clk(CLK));  // open: en, clr
  and and_12 (and_12_out[1], CP0[0], not_2_out);
  // Probe on priority_encoder_1_out
  assign intnum = register_4_q & {2{and_12_out[1]}};  // AND_Gate and_13, 2 bits wide

  // Other names for the same wires on the sheet: index[25:0] = {out_6, out_7, imm};
  //   pc3[31:2] = {pc0[31:28], out_6, out_7, imm}; rt[4:0] = out_7; rs[4:0] = out_6; Aluop[3:0] = out_1;
  //   Din[31:0] = out_2; FinalMemData[31:0] = out_4; pc1[31:0] = out_5; PCSrc[0] = JMP

  // Notes on the sheet:
  //   数码管输出应该用寄存器锁存，否则显示数据只能一闪而过
  //   可以通过项目增加Logisim库的方式将前几次实验完成的电路作为子电路引入到本电路中使用
  //   指令存储器
  //   指令字
  //   contents of rom_1 (hex, n*v repeats v):
  //   20110001 8000c05 20110001 20120002 20130003 8000c09 20110001 20120002 20130003 8000c0d 20110001
  //   20120002 20130003 8000c11 20110001 20120002 20130003 c000cf8 20100001 20110001 118fc0 112020
  //   20020022 c 118882 12200001 8000c15 112020 20020022 c 20110001 118880 112020 20020022 c 12200001
  //   8000c1f 20110001 118fc0 112020 20020022 c 1188c3 112020 20020022 c 118903 112020 20020022 c 118903
  //   112020 20020022 c 118903 112020 20020022 c 118903 112020 20020022 c 118903 112020 20020022 c 118903
  //   112020 20020022 c 118903 112020 20020022 c 20100001 109fc0 139fc3 8021 2012000c 24160003 26100001
  //   3210000f 20080008 20090001 139900 2709825 132020 20020022 c 1094022 1500fff9 22100001 2018000f
  //   2188024 108700 20080008 20090001 139902 2709825 132021 20020022 c 1094022 1500fff9 108702 2c9b022
  //   12c00001 8000c50 4020 1084027 84400 3508ffff 82021 20020022 c 2010ffff 20110000 ae300000 22100001
  //   22310004 ae300000 22100001 22310004 ae300000 22100001 22310004 ae300000 22100001 22310004 ae300000
  //   22100001 22310004 ae300000 22100001 22310004 ae300000 22100001 22310004 ae300000 22100001 22310004
  //   ae300000 22100001 22310004 ae300000 22100001 22310004 ae300000 22100001 22310004 ae300000 22100001
  //   22310004 ae300000 22100001 22310004 ae300000 22100001 22310004 ae300000 22100001 22310004 ae300000
  //   22100001 22310004 22100001 8020 2011003c 8e130000 8e340000 274402a 11000002 ae330000 ae140000
  //   2231fffc 1611fff8 102020 20020022 c 22100004 2011003c 1611fff2 20020032 c 20080001 20090003 20110876
  //   118d00 112020 20020022 c 200b0008 1118807 1318807 112020 20020022 c 216bffff 1560fff9 20020032 c
  //   2008ffff 20117777 112020 20020022 c 200b0010 3a31ffff 112020 20020022 c 216bffff 1560fffa 20020032 c
  //   20090000 200b0020 20110000 20120001 a1310000 112020 20020022 c 2328820 21290001 216bffff 1560fff8
  //   200b0008 20090000 8d310000 112020 20020022 c 21290004 216bffff 1560fff9 20020032 c 2011fff1 112020
  //   20020022 c 22310001 1a20fffb 2002000a c 20020032 c 20100000 22100001 102020 20020022 c 22100002
  //   102020 20020022 c 22100003 102020 20020022 c 22100004 102020 20020022 c 22100005 102020 20020022 c
  //   22100006 102020 20020022 c 22100007 102020 20020022 c 22100008 102020 20020022 20020022 c 3e00008
  //   数码管输出
  //   OP
  //   Func
  //   rs
  //   rt
  //   rd
  //   JMP
  //   JR
  //   OP
  //   Func
  //   总复位信号应将除ROM以外所有存储组件全部清零
  //   Beq
  //   Bne
  //   MemToReg
  //   MemWrite
  //   AluOP
  //   AluSrcB
  //   RegWrite
  //   JAL
  //   RegDst
  //   Syscall
  //   Reset 
  //   Reset 
  //   Reset 
endmodule

// 单周期硬布线控制器
module \硬布线控制器  (
  input  [5:0] OP,
  input  [5:0] Func,
  output [3:0] ALU_OP,
  output MemToReg,
  output MemWrite,
  output ALU_SRC,
  output RegWrite,
  output SysCALL,
  output SignedExt,
  output RegDst,
  output Beq,
  output Bne,
  output JR,
  output JMP,
  output JAL,
  output SRAV,
  output BLEZ,
  output SB,
  output MFC0,
  output ERET
);

  \运算控制器  \u_运算控制器_1  (
    .OP0(OP[0]), .OP1(OP[1]), .OP2(OP[2]), .OP3(OP[3]), .OP4(OP[4]), .OP5(OP[5]), .F0(Func[0]), .F1(Func[1]),
    .F2(Func[2]), .F3(Func[3]), .F4(Func[4]), .F5(Func[5]), .S0(ALU_OP[0]), .S1(ALU_OP[1]), .S2(ALU_OP[2]),
    .S3(ALU_OP[3]));
  \控制信号生成  \u_控制信号生成_1  (
    .OP0(OP[0]), .OP1(OP[1]), .OP2(OP[2]), .OP3(OP[3]), .OP4(OP[4]), .OP5(OP[5]), .F0(Func[0]), .F1(Func[1]),
    .F2(Func[2]), .F3(Func[3]), .F4(Func[4]), .F5(Func[5]), .MemToReg(MemToReg), .MemWrite(MemWrite),
    .ALU_SRC(ALU_SRC), .RegWrite(RegWrite), .SysCALL(SysCALL), .SignedExt(SignedExt), .RegDst(RegDst),
    .BEQ(Beq), .BNE(Bne), .JR(JR), .JMP(JMP), .JAL(JAL));
  \额外控制信号  \u_额外控制信号_1  (
    .OP0(OP[0]), .OP1(OP[1]), .OP2(OP[2]), .OP3(OP[3]), .OP4(OP[4]), .OP5(OP[5]), .F0(Func[0]), .F1(Func[1]),
    .F2(Func[2]), .F3(Func[3]), .F4(Func[4]), .F5(Func[5]), .SRAV(SRAV), .BLEZ(BLEZ), .SB(SB), .MFC0(MFC0),
    .ERET(ERET));

  // Other names for the same wires on the sheet: OP_CODE[5:0] = OP

  // Notes on the sheet:
  //   运算器控制器，根据指令生成运算器功能选择信号
  //   控制信号生成，产生数据通路需要的其他控制信号
endmodule

// 运算器控制器
module \运算控制器  (
  input  OP0,
  input  OP1,
  input  OP2,
  input  OP3,
  input  OP4,
  input  OP5,
  input  F0,
  input  F1,
  input  F2,
  input  F3,
  input  F4,
  input  F5,
  output S0,
  output S1,
  output S2,
  output S3
);

  wire and_1_out, and_2_out, and_3_out, and_4_out, and_5_out, and_6_out, and_7_out, and_8_out, and_9_out,
       and_10_out, and_11_out, and_12_out, and_13_out, and_14_out, and_15_out, and_16_out, and_17_out,
       and_18_out, and_19_out, and_20_out, and_21_out, and_22_out, and_23_out, and_24_out, and_25_out,
       and_26_out, and_27_out, and_28_out, and_29_out, and_30_out, and_31_out, and_32_out, and_33_out,
       and_34_out, and_35_out, and_36_out, and_37_out, and_38_out, and_39_out, and_40_out, not_1_out,
       not_2_out, not_3_out, not_4_out, not_5_out, not_6_out, not_7_out, not_8_out, not_9_out, not_10_out,
       not_11_out, not_12_out, not_13_out, not_14_out, not_15_out, not_16_out, not_17_out, not_18_out,
       not_19_out, not_20_out, not_21_out, not_22_out, not_23_out, not_24_out, not_25_out, not_26_out,
       not_27_out, not_28_out, not_29_out, not_30_out, not_31_out, not_32_out, not_33_out, not_34_out,
       not_35_out, not_36_out, not_37_out, not_38_out, not_39_out, not_40_out, not_41_out, not_42_out,
       not_43_out, not_44_out, not_45_out, not_46_out, not_47_out, not_48_out, not_49_out, not_50_out,
       not_51_out, not_52_out, not_53_out, not_54_out, not_55_out, not_56_out, not_57_out, not_58_out,
       not_59_out, not_60_out, not_61_out, not_62_out, not_63_out, not_64_out, not_65_out, not_66_out,
       not_67_out, not_68_out, not_69_out, not_70_out, not_71_out, not_72_out, not_73_out, not_74_out,
       not_75_out, not_76_out, not_77_out, not_78_out, not_79_out, not_80_out, not_81_out, not_82_out,
       not_83_out, not_84_out, not_85_out, not_86_out, not_87_out, not_88_out, not_89_out, not_90_out,
       not_91_out, not_92_out, not_93_out, not_94_out, not_95_out, not_96_out, not_97_out, not_98_out,
       not_99_out, not_100_out, not_101_out, not_102_out, not_103_out, not_104_out, not_105_out, not_106_out,
       not_107_out, not_108_out, not_109_out, not_110_out, not_111_out, not_112_out, not_113_out,
       not_114_out, not_115_out, not_116_out, not_117_out, not_118_out, not_119_out, not_120_out,
       not_121_out, not_122_out, not_123_out, not_124_out, not_125_out, not_126_out, not_127_out,
       not_128_out, not_129_out, not_130_out, not_131_out, not_132_out, not_133_out, not_134_out,
       not_135_out, not_136_out, not_137_out, not_138_out, not_139_out, not_140_out, not_141_out,
       not_142_out, not_143_out, not_144_out, not_145_out, not_146_out, not_147_out, not_148_out,
       not_149_out, not_150_out, not_151_out, not_152_out, not_153_out, not_154_out, not_155_out,
       not_156_out, not_157_out, not_158_out, not_159_out, not_160_out, not_161_out, not_162_out,
       not_163_out, not_164_out, not_165_out, not_166_out, not_167_out, not_168_out, not_169_out,
       not_170_out, not_171_out, not_172_out, not_173_out, not_174_out, not_175_out, not_176_out,
       not_177_out, not_178_out, not_179_out, not_180_out, not_181_out, not_182_out, not_183_out,
       not_184_out, not_185_out, not_186_out, not_187_out, not_188_out, not_189_out, not_190_out,
       not_191_out, not_192_out, not_193_out, not_194_out, not_195_out, not_196_out, not_197_out,
       not_198_out, not_199_out, not_200_out, not_201_out, not_202_out, not_203_out, not_204_out,
       not_205_out, not_206_out, not_207_out, not_208_out, not_209_out, not_210_out, not_211_out,
       not_212_out, not_213_out, not_214_out, not_215_out, not_216_out, not_217_out, not_218_out,
       not_219_out, not_220_out, not_221_out, not_222_out, not_223_out, not_224_out, not_225_out,
       not_226_out, not_227_out, not_228_out, not_229_out, not_230_out, not_231_out, not_232_out,
       not_233_out, not_234_out, not_235_out, not_236_out, not_237_out, not_238_out, not_239_out,
       not_240_out, not_241_out, not_242_out, not_243_out, not_244_out, not_245_out, not_246_out,
       not_247_out, not_248_out, not_249_out, not_250_out, not_251_out, not_252_out, not_253_out,
       not_254_out, not_255_out, not_256_out, not_257_out, not_258_out, not_259_out, not_260_out,
       not_261_out, not_262_out, not_263_out, not_264_out, not_265_out, not_266_out, not_267_out, not_268_out;

  not not_1 (not_1_out, OP5);
  not not_2 (not_2_out, OP4);
  not not_3 (not_3_out, OP3);
  not not_4 (not_4_out, OP2);
  not not_5 (not_5_out, OP1);
  not not_6 (not_6_out, OP0);
  not not_7 (not_7_out, F5);
  not not_8 (not_8_out, F4);
  not not_9 (not_9_out, F3);
  not not_10 (not_10_out, F2);
  not not_11 (not_11_out, OP5);
  not not_12 (not_12_out, OP4);
  not not_13 (not_13_out, OP3);
  not not_14 (not_14_out, OP2);
  not not_15 (not_15_out, OP1);
  not not_16 (not_16_out, OP0);
  not not_17 (not_17_out, F4);
  not not_18 (not_18_out, F3);
  not not_19 (not_19_out, F2);
  not not_20 (not_20_out, F1);
  not not_21 (not_21_out, F0);
  not not_22 (not_22_out, OP5);
  not not_23 (not_23_out, OP4);
  not not_24 (not_24_out, OP3);
  not not_25 (not_25_out, OP2);
  not not_26 (not_26_out, OP1);
  not not_27 (not_27_out, OP0);
  not not_28 (not_28_out, F4);
  not not_29 (not_29_out, F3);
  not not_30 (not_30_out, F2);
  not not_31 (not_31_out, F1);
  not not_32 (not_32_out, OP5);
  not not_33 (not_33_out, OP4);
  not not_34 (not_34_out, OP3);
  not not_35 (not_35_out, OP2);
  not not_36 (not_36_out, OP1);
  not not_37 (not_37_out, OP0);
  not not_38 (not_38_out, F4);
  not not_39 (not_39_out, F3);
  not not_40 (not_40_out, F1);
  not not_41 (not_41_out, F0);
  not not_42 (not_42_out, OP5);
  not not_43 (not_43_out, OP4);
  not not_44 (not_44_out, OP3);
  not not_45 (not_45_out, OP2);
  not not_46 (not_46_out, OP1);
  not not_47 (not_47_out, OP0);
  not not_48 (not_48_out, F4);
  not not_49 (not_49_out, F2);
  not not_50 (not_50_out, F0);
  not not_51 (not_51_out, OP5);
  not not_52 (not_52_out, OP4);
  not not_53 (not_53_out, OP2);
  not not_54 (not_54_out, OP1);
  not not_55 (not_55_out, OP0);
  not not_56 (not_56_out, OP5);
  not not_57 (not_57_out, OP4);
  not not_58 (not_58_out, OP1);
  not not_59 (not_59_out, OP0);
  not not_60 (not_60_out, OP5);
  not not_61 (not_61_out, OP4);
  not not_62 (not_62_out, OP2);
  not not_63 (not_63_out, OP1);
  not not_64 (not_64_out, OP5);
  not not_65 (not_65_out, OP4);
  not not_66 (not_66_out, OP2);
  not not_67 (not_67_out, OP0);
  not not_68 (not_68_out, OP4);
  not not_69 (not_69_out, OP3);
  not not_70 (not_70_out, OP2);
  not not_71 (not_71_out, OP4);
  not not_72 (not_72_out, OP2);
  not not_73 (not_73_out, OP5);
  not not_74 (not_74_out, OP4);
  not not_75 (not_75_out, OP3);
  not not_76 (not_76_out, OP2);
  not not_77 (not_77_out, OP1);
  not not_78 (not_78_out, OP0);
  not not_79 (not_79_out, F5);
  not not_80 (not_80_out, F4);
  not not_81 (not_81_out, F3);
  not not_82 (not_82_out, OP4);
  not not_83 (not_83_out, OP2);
  not not_84 (not_84_out, OP1);
  not not_85 (not_85_out, OP0);
  not not_86 (not_86_out, OP5);
  not not_87 (not_87_out, OP4);
  not not_88 (not_88_out, OP3);
  not not_89 (not_89_out, OP2);
  not not_90 (not_90_out, OP1);
  not not_91 (not_91_out, OP0);
  not not_92 (not_92_out, F5);
  not not_93 (not_93_out, F4);
  not not_94 (not_94_out, F3);
  not not_95 (not_95_out, OP5);
  not not_96 (not_96_out, OP4);
  not not_97 (not_97_out, OP0);
  not not_98 (not_98_out, OP5);
  not not_99 (not_99_out, OP4);
  not not_100 (not_100_out, OP3);
  not not_101 (not_101_out, OP2);
  not not_102 (not_102_out, OP1);
  not not_103 (not_103_out, OP0);
  not not_104 (not_104_out, F5);
  not not_105 (not_105_out, F4);
  not not_106 (not_106_out, F3);
  not not_107 (not_107_out, F2);
  not not_108 (not_108_out, F0);
  not not_109 (not_109_out, OP5);
  not not_110 (not_110_out, OP4);
  not not_111 (not_111_out, OP3);
  not not_112 (not_112_out, OP2);
  not not_113 (not_113_out, OP1);
  not not_114 (not_114_out, OP0);
  not not_115 (not_115_out, F4);
  not not_116 (not_116_out, F3);
  not not_117 (not_117_out, F2);
  not not_118 (not_118_out, F0);
  not not_119 (not_119_out, OP5);
  not not_120 (not_120_out, OP4);
  not not_121 (not_121_out, OP3);
  not not_122 (not_122_out, OP2);
  not not_123 (not_123_out, OP1);
  not not_124 (not_124_out, OP0);
  not not_125 (not_125_out, F4);
  not not_126 (not_126_out, F3);
  not not_127 (not_127_out, F1);
  not not_128 (not_128_out, F0);
  not not_129 (not_129_out, OP5);
  not not_130 (not_130_out, OP4);
  not not_131 (not_131_out, OP3);
  not not_132 (not_132_out, OP2);
  not not_133 (not_133_out, OP1);
  not not_134 (not_134_out, OP0);
  not not_135 (not_135_out, F4);
  not not_136 (not_136_out, F3);
  not not_137 (not_137_out, OP5);
  not not_138 (not_138_out, OP4);
  not not_139 (not_139_out, OP3);
  not not_140 (not_140_out, OP2);
  not not_141 (not_141_out, OP1);
  not not_142 (not_142_out, OP0);
  not not_143 (not_143_out, F4);
  not not_144 (not_144_out, F2);
  not not_145 (not_145_out, F0);
  not not_146 (not_146_out, OP5);
  not not_147 (not_147_out, OP4);
  not not_148 (not_148_out, OP1);
  not not_149 (not_149_out, OP0);
  not not_150 (not_150_out, OP5);
  not not_151 (not_151_out, OP4);
  not not_152 (not_152_out, OP2);
  not not_153 (not_153_out, OP0);
  not not_154 (not_154_out, OP5);
  not not_155 (not_155_out, OP4);
  not not_156 (not_156_out, OP3);
  not not_157 (not_157_out, OP2);
  not not_158 (not_158_out, OP1);
  not not_159 (not_159_out, OP0);
  not not_160 (not_160_out, F4);
  not not_161 (not_161_out, F3);
  not not_162 (not_162_out, F2);
  not not_163 (not_163_out, F1);
  not not_164 (not_164_out, F0);
  not not_165 (not_165_out, OP5);
  not not_166 (not_166_out, OP4);
  not not_167 (not_167_out, OP3);
  not not_168 (not_168_out, OP2);
  not not_169 (not_169_out, OP1);
  not not_170 (not_170_out, OP0);
  not not_171 (not_171_out, F4);
  not not_172 (not_172_out, F3);
  not not_173 (not_173_out, F2);
  not not_174 (not_174_out, F1);
  not not_175 (not_175_out, OP5);
  not not_176 (not_176_out, OP4);
  not not_177 (not_177_out, OP3);
  not not_178 (not_178_out, OP2);
  not not_179 (not_179_out, OP1);
  not not_180 (not_180_out, OP0);
  not not_181 (not_181_out, F4);
  not not_182 (not_182_out, F3);
  not not_183 (not_183_out, F2);
  not not_184 (not_184_out, F0);
  not not_185 (not_185_out, OP5);
  not not_186 (not_186_out, OP4);
  not not_187 (not_187_out, OP3);
  not not_188 (not_188_out, OP2);
  not not_189 (not_189_out, OP1);
  not not_190 (not_190_out, OP0);
  not not_191 (not_191_out, F4);
  not not_192 (not_192_out, F3);
  not not_193 (not_193_out, F1);
  not not_194 (not_194_out, F0);
  not not_195 (not_195_out, OP5);
  not not_196 (not_196_out, OP4);
  not not_197 (not_197_out, OP3);
  not not_198 (not_198_out, OP2);
  not not_199 (not_199_out, OP1);
  not not_200 (not_200_out, OP0);
  not not_201 (not_201_out, F4);
  not not_202 (not_202_out, F2);
  not not_203 (not_203_out, OP5);
  not not_204 (not_204_out, OP4);
  not not_205 (not_205_out, OP2);
  not not_206 (not_206_out, OP1);
  not not_207 (not_207_out, OP0);
  not not_208 (not_208_out, OP5);
  not not_209 (not_209_out, OP4);
  not not_210 (not_210_out, OP1);
  not not_211 (not_211_out, OP0);
  not not_212 (not_212_out, OP5);
  not not_213 (not_213_out, OP4);
  not not_214 (not_214_out, OP2);
  not not_215 (not_215_out, OP1);
  not not_216 (not_216_out, OP4);
  not not_217 (not_217_out, OP3);
  not not_218 (not_218_out, OP2);
  not not_219 (not_219_out, OP4);
  not not_220 (not_220_out, OP2);
  not not_221 (not_221_out, OP4);
  not not_222 (not_222_out, OP2);
  not not_223 (not_223_out, OP1);
  not not_224 (not_224_out, OP0);
  not not_225 (not_225_out, OP5);
  not not_226 (not_226_out, OP4);
  not not_227 (not_227_out, OP3);
  not not_228 (not_228_out, OP2);
  not not_229 (not_229_out, OP1);
  not not_230 (not_230_out, OP0);
  not not_231 (not_231_out, F4);
  not not_232 (not_232_out, F3);
  not not_233 (not_233_out, F1);
  not not_234 (not_234_out, OP5);
  not not_235 (not_235_out, OP4);
  not not_236 (not_236_out, OP3);
  not not_237 (not_237_out, OP2);
  not not_238 (not_238_out, OP1);
  not not_239 (not_239_out, OP0);
  not not_240 (not_240_out, F4);
  not not_241 (not_241_out, F3);
  not not_242 (not_242_out, OP5);
  not not_243 (not_243_out, OP4);
  not not_244 (not_244_out, OP3);
  not not_245 (not_245_out, OP2);
  not not_246 (not_246_out, OP1);
  not not_247 (not_247_out, OP0);
  not not_248 (not_248_out, F4);
  not not_249 (not_249_out, F2);
  not not_250 (not_250_out, F0);
  not not_251 (not_251_out, OP5);
  not not_252 (not_252_out, OP4);
  not not_253 (not_253_out, OP3);
  not not_254 (not_254_out, OP2);
  not not_255 (not_255_out, OP1);
  not not_256 (not_256_out, OP0);
  not not_257 (not_257_out, F4);
  not not_258 (not_258_out, F2);
  not not_259 (not_259_out, OP5);
  not not_260 (not_260_out, OP4);
  not not_261 (not_261_out, OP2);
  not not_262 (not_262_out, OP0);
  not not_263 (not_263_out, OP5);
  not not_264 (not_264_out, OP4);
  not not_265 (not_265_out, OP1);
  not not_266 (not_266_out, OP5);
  not not_267 (not_267_out, OP4);
  not not_268 (not_268_out, OP0);
  and and_1 (and_1_out, not_1_out, not_2_out, not_3_out, not_4_out, not_5_out, not_6_out, not_7_out, not_8_out, not_9_out, not_10_out, F1, F0);
  and and_2 (and_2_out, not_11_out, not_12_out, not_13_out, not_14_out, not_15_out, not_16_out, F5, not_17_out, not_18_out, not_19_out, not_20_out, not_21_out);
  and and_3 (and_3_out, not_22_out, not_23_out, not_24_out, not_25_out, not_26_out, not_27_out, F5, not_28_out, not_29_out, not_30_out, not_31_out, F0);
  and and_4 (and_4_out, not_32_out, not_33_out, not_34_out, not_35_out, not_36_out, not_37_out, F5, not_38_out, not_39_out, F2, not_40_out, not_41_out);
  and and_5 (and_5_out, not_42_out, not_43_out, not_44_out, not_45_out, not_46_out, not_47_out, F5, not_48_out, F3, not_49_out, F1, not_50_out);
  and and_6 (and_6_out, not_51_out, not_52_out, OP3, not_53_out, not_54_out, not_55_out);
  and and_7 (and_7_out, not_56_out, not_57_out, OP3, OP2, not_58_out, not_59_out);
  and and_8 (and_8_out, not_60_out, not_61_out, OP3, not_62_out, not_63_out, OP0);
  and and_9 (and_9_out, not_64_out, not_65_out, OP3, not_66_out, OP1, not_67_out);
  and and_10 (and_10_out, OP5, not_68_out, not_69_out, not_70_out, OP1, OP0);
  and and_11 (and_11_out, OP5, not_71_out, OP3, not_72_out, OP1, OP0);
  and and_12 (and_12_out, not_73_out, not_74_out, not_75_out, not_76_out, not_77_out, not_78_out, not_79_out, not_80_out, not_81_out, F2, F1, F0);
  and and_13 (and_13_out, OP5, not_82_out, OP3, not_83_out, not_84_out, not_85_out);
  and and_14 (and_14_out, not_86_out, not_87_out, not_88_out, not_89_out, not_90_out, not_91_out, not_92_out, not_93_out, not_94_out, F2, F1, F0);
  and and_15 (and_15_out, not_95_out, not_96_out, OP3, OP2, OP1, not_97_out);
  and and_16 (and_16_out, not_98_out, not_99_out, not_100_out, not_101_out, not_102_out, not_103_out, not_104_out, not_105_out, not_106_out, not_107_out, F1, not_108_out);
  and and_17 (and_17_out, not_109_out, not_110_out, not_111_out, not_112_out, not_113_out, not_114_out, F5, not_115_out, not_116_out, not_117_out, F1, not_118_out);
  and and_18 (and_18_out, not_119_out, not_120_out, not_121_out, not_122_out, not_123_out, not_124_out, F5, not_125_out, not_126_out, F2, not_127_out, not_128_out);
  and and_19 (and_19_out, not_129_out, not_130_out, not_131_out, not_132_out, not_133_out, not_134_out, F5, not_135_out, not_136_out, F2, F1, F0);
  and and_20 (and_20_out, not_137_out, not_138_out, not_139_out, not_140_out, not_141_out, not_142_out, F5, not_143_out, F3, not_144_out, F1, not_145_out);
  and and_21 (and_21_out, not_146_out, not_147_out, OP3, OP2, not_148_out, not_149_out);
  and and_22 (and_22_out, not_150_out, not_151_out, OP3, not_152_out, OP1, not_153_out);
  and and_23 (and_23_out, not_154_out, not_155_out, not_156_out, not_157_out, not_158_out, not_159_out, F5, not_160_out, not_161_out, not_162_out, not_163_out, not_164_out);
  and and_24 (and_24_out, not_165_out, not_166_out, not_167_out, not_168_out, not_169_out, not_170_out, F5, not_171_out, not_172_out, not_173_out, not_174_out, F0);
  and and_25 (and_25_out, not_175_out, not_176_out, not_177_out, not_178_out, not_179_out, not_180_out, F5, not_181_out, not_182_out, not_183_out, F1, not_184_out);
  and and_26 (and_26_out, not_185_out, not_186_out, not_187_out, not_188_out, not_189_out, not_190_out, F5, not_191_out, not_192_out, F2, not_193_out, not_194_out);
  and and_27 (and_27_out, not_195_out, not_196_out, not_197_out, not_198_out, not_199_out, not_200_out, F5, not_201_out, F3, not_202_out, F1, F0);
  and and_28 (and_28_out, not_203_out, not_204_out, OP3, not_205_out, not_206_out, not_207_out);
  and and_29 (and_29_out, not_208_out, not_209_out, OP3, OP2, not_210_out, not_211_out);
  and and_30 (and_30_out, not_212_out, not_213_out, OP3, not_214_out, not_215_out, OP0);
  and and_31 (and_31_out, OP5, not_216_out, not_217_out, not_218_out, OP1, OP0);
  and and_32 (and_32_out, OP5, not_219_out, OP3, not_220_out, OP1, OP0);
  and and_33 (and_33_out, OP5, not_221_out, OP3, not_222_out, not_223_out, not_224_out);
  and and_34 (and_34_out, not_225_out, not_226_out, not_227_out, not_228_out, not_229_out, not_230_out, F5, not_231_out, not_232_out, F2, not_233_out, F0);
  and and_35 (and_35_out, not_234_out, not_235_out, not_236_out, not_237_out, not_238_out, not_239_out, F5, not_240_out, not_241_out, F2, F1, F0);
  and and_36 (and_36_out, not_242_out, not_243_out, not_244_out, not_245_out, not_246_out, not_247_out, F5, not_248_out, F3, not_249_out, F1, not_250_out);
  and and_37 (and_37_out, not_251_out, not_252_out, not_253_out, not_254_out, not_255_out, not_256_out, F5, not_257_out, F3, not_258_out, F1, F0);
  and and_38 (and_38_out, not_259_out, not_260_out, OP3, not_261_out, OP1, not_262_out);
  and and_39 (and_39_out, not_263_out, not_264_out, OP3, OP2, not_265_out, OP0);
  and and_40 (and_40_out, not_266_out, not_267_out, OP3, OP2, OP1, not_268_out);
  or or_1 (S1, and_16_out, and_17_out, and_18_out, and_19_out, and_20_out, and_21_out, and_22_out);
  or or_2 (S2, and_23_out, and_24_out, and_25_out, and_26_out, and_27_out, and_28_out, and_29_out, and_30_out, and_31_out, and_32_out, and_33_out);
  or or_3 (S3, and_34_out, and_35_out, and_36_out, and_37_out, and_38_out, and_39_out, and_40_out);
  or or_4 (S0, and_1_out, and_2_out, and_3_out, and_4_out, and_5_out, and_6_out, and_7_out, and_8_out, and_9_out, and_10_out, and_11_out, and_12_out, and_13_out, and_14_out, and_15_out);
endmodule

// 控制信号生成
module \控制信号生成  (
  input  OP0,
  input  OP1,
  input  OP2,
  input  OP3,
  input  OP4,
  input  OP5,
  input  F0,
  input  F1,
  input  F2,
  input  F3,
  input  F4,
  input  F5,
  output MemToReg,
  output MemWrite,
  output ALU_SRC,
  output RegWrite,
  output SysCALL,
  output SignedExt,
  output RegDst,
  output BEQ,
  output BNE,
  output JR,
  output JMP,
  output JAL
);

  wire and_2_out, and_3_out, and_4_out, and_5_out, and_6_out, and_7_out, and_8_out, and_9_out, and_10_out,
       and_11_out, and_12_out, and_13_out, and_14_out, and_15_out, and_16_out, and_17_out, and_18_out,
       and_19_out, and_20_out, and_21_out, and_22_out, and_23_out, and_24_out, and_25_out, and_26_out,
       and_27_out, and_28_out, and_29_out, and_30_out, and_31_out, and_32_out, and_34_out, and_35_out,
       and_36_out, and_37_out, and_38_out, and_39_out, and_40_out, and_41_out, and_42_out, and_43_out,
       and_44_out, and_45_out, and_46_out, and_47_out, and_48_out, and_49_out, and_50_out, and_51_out,
       and_52_out, and_56_out, and_57_out, and_58_out, not_1_out, not_2_out, not_3_out, not_4_out, not_5_out,
       not_6_out, not_7_out, not_8_out, not_9_out, not_10_out, not_11_out, not_12_out, not_13_out,
       not_14_out, not_15_out, not_16_out, not_17_out, not_18_out, not_19_out, not_20_out, not_21_out,
       not_22_out, not_23_out, not_24_out, not_25_out, not_26_out, not_27_out, not_28_out, not_29_out,
       not_30_out, not_31_out, not_32_out, not_33_out, not_34_out, not_35_out, not_36_out, not_37_out,
       not_38_out, not_39_out, not_40_out, not_41_out, not_42_out, not_43_out, not_44_out, not_45_out,
       not_46_out, not_47_out, not_48_out, not_49_out, not_50_out, not_51_out, not_52_out, not_53_out,
       not_54_out, not_55_out, not_56_out, not_57_out, not_58_out, not_59_out, not_60_out, not_61_out,
       not_62_out, not_63_out, not_64_out, not_65_out, not_66_out, not_67_out, not_68_out, not_69_out,
       not_70_out, not_71_out, not_72_out, not_73_out, not_74_out, not_75_out, not_76_out, not_77_out,
       not_78_out, not_79_out, not_80_out, not_81_out, not_82_out, not_83_out, not_84_out, not_85_out,
       not_86_out, not_87_out, not_88_out, not_89_out, not_90_out, not_91_out, not_92_out, not_93_out,
       not_94_out, not_95_out, not_96_out, not_97_out, not_98_out, not_99_out, not_100_out, not_101_out,
       not_102_out, not_103_out, not_104_out, not_105_out, not_106_out, not_107_out, not_108_out,
       not_109_out, not_110_out, not_111_out, not_112_out, not_113_out, not_114_out, not_115_out,
       not_116_out, not_117_out, not_118_out, not_119_out, not_120_out, not_121_out, not_122_out,
       not_123_out, not_124_out, not_125_out, not_126_out, not_127_out, not_128_out, not_129_out,
       not_130_out, not_131_out, not_132_out, not_133_out, not_134_out, not_135_out, not_136_out,
       not_137_out, not_138_out, not_139_out, not_140_out, not_141_out, not_142_out, not_143_out,
       not_144_out, not_145_out, not_146_out, not_147_out, not_148_out, not_149_out, not_150_out,
       not_151_out, not_152_out, not_153_out, not_154_out, not_155_out, not_156_out, not_157_out,
       not_158_out, not_159_out, not_160_out, not_161_out, not_162_out, not_163_out, not_164_out,
       not_165_out, not_166_out, not_167_out, not_168_out, not_169_out, not_170_out, not_171_out,
       not_172_out, not_173_out, not_174_out, not_175_out, not_176_out, not_177_out, not_178_out,
       not_179_out, not_180_out, not_181_out, not_182_out, not_183_out, not_184_out, not_185_out,
       not_186_out, not_187_out, not_188_out, not_189_out, not_190_out, not_191_out, not_192_out,
       not_193_out, not_194_out, not_195_out, not_196_out, not_197_out, not_198_out, not_199_out,
       not_200_out, not_201_out, not_202_out, not_203_out, not_204_out, not_205_out, not_206_out,
       not_207_out, not_208_out, not_209_out, not_210_out, not_211_out, not_212_out, not_213_out,
       not_214_out, not_215_out, not_216_out, not_217_out, not_218_out, not_219_out, not_220_out,
       not_221_out, not_222_out, not_223_out, not_224_out, not_225_out, not_226_out, not_227_out,
       not_228_out, not_229_out, not_230_out, not_231_out, not_232_out, not_233_out, not_234_out,
       not_235_out, not_236_out, not_237_out, not_238_out, not_239_out, not_240_out, not_241_out,
       not_242_out, not_243_out, not_244_out, not_245_out, not_246_out, not_247_out, not_248_out,
       not_249_out, not_250_out, not_251_out, not_252_out, not_253_out, not_254_out, not_255_out,
       not_256_out, not_257_out, not_258_out, not_259_out, not_260_out, not_261_out, not_262_out,
       not_263_out, not_264_out, not_265_out, not_266_out, not_267_out, not_268_out, not_269_out,
       not_270_out, not_271_out, not_272_out, not_273_out, not_274_out, not_275_out, not_276_out,
       not_277_out, not_278_out, not_279_out, not_280_out, not_281_out, not_282_out, not_283_out,
       not_284_out, not_285_out, not_286_out, not_287_out, not_288_out, not_289_out, not_290_out,
       not_291_out, not_292_out, not_293_out, not_294_out, not_295_out, not_296_out, not_297_out,
       not_298_out, not_299_out, not_300_out, not_301_out, not_302_out, not_303_out, not_304_out,
       not_305_out, not_306_out, not_307_out, not_308_out, not_309_out, not_310_out, not_311_out,
       not_312_out, not_313_out, not_314_out, not_315_out, not_316_out, not_317_out, not_318_out,
       not_319_out, not_320_out, not_321_out, not_322_out, not_323_out, not_324_out, not_325_out,
       not_326_out, not_327_out, not_328_out, not_329_out, not_330_out, not_331_out, not_332_out,
       not_333_out, not_334_out, not_335_out, not_336_out, not_337_out, not_338_out, not_339_out,
       not_340_out, not_341_out, not_342_out, not_343_out, not_344_out, not_345_out, not_346_out,
       not_347_out, not_348_out, not_349_out, not_350_out, not_351_out, not_352_out, not_353_out,
       not_354_out, not_355_out, not_356_out, not_357_out, not_358_out, not_359_out, not_360_out,
       not_361_out, not_362_out, not_363_out, not_364_out, not_365_out, not_366_out, not_367_out,
       not_368_out, not_369_out, not_370_out, not_371_out, not_372_out, not_373_out, not_374_out,
       not_375_out, not_376_out, not_377_out, not_378_out, not_379_out, not_380_out, not_381_out,
       not_382_out, not_383_out, not_384_out, not_385_out, not_386_out, not_387_out, not_388_out,
       not_389_out, not_390_out, not_391_out, not_392_out;

  not not_1 (not_1_out, OP4);
  not not_2 (not_2_out, OP3);
  not not_3 (not_3_out, OP2);
  not not_4 (not_4_out, OP4);
  not not_5 (not_5_out, OP2);
  not not_6 (not_6_out, OP4);
  not not_7 (not_7_out, OP2);
  not not_8 (not_8_out, OP1);
  not not_9 (not_9_out, OP0);
  not not_10 (not_10_out, OP5);
  not not_11 (not_11_out, OP4);
  not not_12 (not_12_out, OP2);
  not not_13 (not_13_out, OP1);
  not not_14 (not_14_out, OP0);
  not not_15 (not_15_out, OP5);
  not not_16 (not_16_out, OP4);
  not not_17 (not_17_out, OP1);
  not not_18 (not_18_out, OP0);
  not not_19 (not_19_out, OP5);
  not not_20 (not_20_out, OP4);
  not not_21 (not_21_out, OP2);
  not not_22 (not_22_out, OP1);
  not not_23 (not_23_out, OP5);
  not not_24 (not_24_out, OP4);
  not not_25 (not_25_out, OP2);
  not not_26 (not_26_out, OP0);
  not not_27 (not_27_out, OP5);
  not not_28 (not_28_out, OP4);
  not not_29 (not_29_out, OP1);
  not not_30 (not_30_out, OP4);
  not not_31 (not_31_out, OP3);
  not not_32 (not_32_out, OP2);
  not not_33 (not_33_out, OP4);
  not not_34 (not_34_out, OP2);
  not not_35 (not_35_out, OP5);
  not not_36 (not_36_out, OP4);
  not not_37 (not_37_out, OP0);
  not not_38 (not_38_out, OP4);
  not not_39 (not_39_out, OP2);
  not not_40 (not_40_out, OP1);
  not not_41 (not_41_out, OP0);
  not not_42 (not_42_out, OP5);
  not not_43 (not_43_out, OP4);
  not not_44 (not_44_out, OP3);
  not not_45 (not_45_out, OP2);
  not not_46 (not_46_out, OP1);
  not not_47 (not_47_out, OP0);
  not not_48 (not_48_out, F5);
  not not_49 (not_49_out, F4);
  not not_50 (not_50_out, F3);
  not not_51 (not_51_out, F2);
  not not_52 (not_52_out, F1);
  not not_53 (not_53_out, F0);
  not not_54 (not_54_out, OP5);
  not not_55 (not_55_out, OP4);
  not not_56 (not_56_out, OP3);
  not not_57 (not_57_out, OP2);
  not not_58 (not_58_out, OP1);
  not not_59 (not_59_out, OP0);
  not not_60 (not_60_out, F5);
  not not_61 (not_61_out, F4);
  not not_62 (not_62_out, F3);
  not not_63 (not_63_out, F2);
  not not_64 (not_64_out, OP5);
  not not_65 (not_65_out, OP4);
  not not_66 (not_66_out, OP3);
  not not_67 (not_67_out, OP2);
  not not_68 (not_68_out, OP1);
  not not_69 (not_69_out, OP0);
  not not_70 (not_70_out, F5);
  not not_71 (not_71_out, F4);
  not not_72 (not_72_out, F3);
  not not_73 (not_73_out, F2);
  not not_74 (not_74_out, F0);
  not not_75 (not_75_out, OP5);
  not not_76 (not_76_out, OP4);
  not not_77 (not_77_out, OP3);
  not not_78 (not_78_out, OP2);
  not not_79 (not_79_out, OP1);
  not not_80 (not_80_out, OP0);
  not not_81 (not_81_out, F4);
  not not_82 (not_82_out, F3);
  not not_83 (not_83_out, F2);
  not not_84 (not_84_out, F1);
  not not_85 (not_85_out, F0);
  not not_86 (not_86_out, OP5);
  not not_87 (not_87_out, OP4);
  not not_88 (not_88_out, OP3);
  not not_89 (not_89_out, OP2);
  not not_90 (not_90_out, OP1);
  not not_91 (not_91_out, OP0);
  not not_92 (not_92_out, F4);
  not not_93 (not_93_out, F3);
  not not_94 (not_94_out, F2);
  not not_95 (not_95_out, F1);
  not not_96 (not_96_out, OP5);
  not not_97 (not_97_out, OP4);
  not not_98 (not_98_out, OP3);
  not not_99 (not_99_out, OP2);
  not not_100 (not_100_out, OP1);
  not not_101 (not_101_out, OP0);
  not not_102 (not_102_out, F4);
  not not_103 (not_103_out, F3);
  not not_104 (not_104_out, F2);
  not not_105 (not_105_out, F0);
  not not_106 (not_106_out, OP5);
  not not_107 (not_107_out, OP4);
  not not_108 (not_108_out, OP3);
  not not_109 (not_109_out, OP2);
  not not_110 (not_110_out, OP1);
  not not_111 (not_111_out, OP0);
  not not_112 (not_112_out, F4);
  not not_113 (not_113_out, F3);
  not not_114 (not_114_out, F1);
  not not_115 (not_115_out, F0);
  not not_116 (not_116_out, OP5);
  not not_117 (not_117_out, OP4);
  not not_118 (not_118_out, OP3);
  not not_119 (not_119_out, OP2);
  not not_120 (not_120_out, OP1);
  not not_121 (not_121_out, OP0);
  not not_122 (not_122_out, F4);
  not not_123 (not_123_out, F3);
  not not_124 (not_124_out, F1);
  not not_125 (not_125_out, OP5);
  not not_126 (not_126_out, OP4);
  not not_127 (not_127_out, OP3);
  not not_128 (not_128_out, OP2);
  not not_129 (not_129_out, OP1);
  not not_130 (not_130_out, OP0);
  not not_131 (not_131_out, F4);
  not not_132 (not_132_out, F3);
  not not_133 (not_133_out, OP5);
  not not_134 (not_134_out, OP4);
  not not_135 (not_135_out, OP3);
  not not_136 (not_136_out, OP2);
  not not_137 (not_137_out, OP1);
  not not_138 (not_138_out, OP0);
  not not_139 (not_139_out, F4);
  not not_140 (not_140_out, F2);
  not not_141 (not_141_out, F0);
  not not_142 (not_142_out, OP5);
  not not_143 (not_143_out, OP4);
  not not_144 (not_144_out, OP3);
  not not_145 (not_145_out, OP2);
  not not_146 (not_146_out, OP1);
  not not_147 (not_147_out, OP0);
  not not_148 (not_148_out, F4);
  not not_149 (not_149_out, F2);
  not not_150 (not_150_out, OP5);
  not not_151 (not_151_out, OP4);
  not not_152 (not_152_out, OP3);
  not not_153 (not_153_out, OP2);
  not not_154 (not_154_out, OP5);
  not not_155 (not_155_out, OP4);
  not not_156 (not_156_out, OP2);
  not not_157 (not_157_out, OP1);
  not not_158 (not_158_out, OP0);
  not not_159 (not_159_out, OP5);
  not not_160 (not_160_out, OP4);
  not not_161 (not_161_out, OP1);
  not not_162 (not_162_out, OP0);
  not not_163 (not_163_out, OP5);
  not not_164 (not_164_out, OP4);
  not not_165 (not_165_out, OP2);
  not not_166 (not_166_out, OP1);
  not not_167 (not_167_out, OP5);
  not not_168 (not_168_out, OP4);
  not not_169 (not_169_out, OP2);
  not not_170 (not_170_out, OP0);
  not not_171 (not_171_out, OP5);
  not not_172 (not_172_out, OP4);
  not not_173 (not_173_out, OP1);
  not not_174 (not_174_out, OP4);
  not not_175 (not_175_out, OP3);
  not not_176 (not_176_out, OP2);
  not not_177 (not_177_out, OP5);
  not not_178 (not_178_out, OP4);
  not not_179 (not_179_out, OP0);
  not not_180 (not_180_out, OP5);
  not not_181 (not_181_out, OP4);
  not not_182 (not_182_out, OP3);
  not not_183 (not_183_out, OP2);
  not not_184 (not_184_out, OP1);
  not not_185 (not_185_out, OP0);
  not not_186 (not_186_out, F5);
  not not_187 (not_187_out, F4);
  not not_188 (not_188_out, F3);
  not not_189 (not_189_out, OP5);
  not not_190 (not_190_out, OP4);
  not not_191 (not_191_out, OP3);
  not not_192 (not_192_out, OP2);
  not not_193 (not_193_out, OP1);
  not not_194 (not_194_out, OP0);
  not not_195 (not_195_out, F5);
  not not_196 (not_196_out, F4);
  not not_197 (not_197_out, F1);
  not not_198 (not_198_out, F0);
  not not_199 (not_199_out, OP5);
  not not_200 (not_200_out, OP4);
  not not_201 (not_201_out, OP2);
  not not_202 (not_202_out, OP1);
  not not_203 (not_203_out, OP0);
  not not_204 (not_204_out, OP5);
  not not_205 (not_205_out, OP4);
  not not_206 (not_206_out, OP2);
  not not_207 (not_207_out, OP1);
  not not_208 (not_208_out, OP5);
  not not_209 (not_209_out, OP4);
  not not_210 (not_210_out, OP2);
  not not_211 (not_211_out, OP0);
  not not_212 (not_212_out, OP4);
  not not_213 (not_213_out, OP3);
  not not_214 (not_214_out, OP2);
  not not_215 (not_215_out, OP4);
  not not_216 (not_216_out, OP2);
  not not_217 (not_217_out, OP4);
  not not_218 (not_218_out, OP2);
  not not_219 (not_219_out, OP1);
  not not_220 (not_220_out, OP0);
  not not_221 (not_221_out, OP5);
  not not_222 (not_222_out, OP4);
  not not_223 (not_223_out, OP3);
  not not_224 (not_224_out, OP2);
  not not_225 (not_225_out, OP1);
  not not_226 (not_226_out, OP0);
  not not_227 (not_227_out, F5);
  not not_228 (not_228_out, F4);
  not not_229 (not_229_out, F3);
  not not_230 (not_230_out, F2);
  not not_231 (not_231_out, F1);
  not not_232 (not_232_out, F0);
  not not_233 (not_233_out, OP5);
  not not_234 (not_234_out, OP4);
  not not_235 (not_235_out, OP3);
  not not_236 (not_236_out, OP2);
  not not_237 (not_237_out, OP1);
  not not_238 (not_238_out, OP0);
  not not_239 (not_239_out, F5);
  not not_240 (not_240_out, F4);
  not not_241 (not_241_out, F3);
  not not_242 (not_242_out, F2);
  not not_243 (not_243_out, OP5);
  not not_244 (not_244_out, OP4);
  not not_245 (not_245_out, OP3);
  not not_246 (not_246_out, OP2);
  not not_247 (not_247_out, OP1);
  not not_248 (not_248_out, OP0);
  not not_249 (not_249_out, F5);
  not not_250 (not_250_out, F4);
  not not_251 (not_251_out, F3);
  not not_252 (not_252_out, F2);
  not not_253 (not_253_out, F0);
  not not_254 (not_254_out, OP5);
  not not_255 (not_255_out, OP4);
  not not_256 (not_256_out, OP3);
  not not_257 (not_257_out, OP2);
  not not_258 (not_258_out, OP1);
  not not_259 (not_259_out, OP0);
  not not_260 (not_260_out, F4);
  not not_261 (not_261_out, F3);
  not not_262 (not_262_out, F2);
  not not_263 (not_263_out, F1);
  not not_264 (not_264_out, F0);
  not not_265 (not_265_out, OP5);
  not not_266 (not_266_out, OP4);
  not not_267 (not_267_out, OP3);
  not not_268 (not_268_out, OP2);
  not not_269 (not_269_out, OP1);
  not not_270 (not_270_out, OP0);
  not not_271 (not_271_out, F4);
  not not_272 (not_272_out, F3);
  not not_273 (not_273_out, F2);
  not not_274 (not_274_out, F1);
  not not_275 (not_275_out, OP5);
  not not_276 (not_276_out, OP4);
  not not_277 (not_277_out, OP3);
  not not_278 (not_278_out, OP2);
  not not_279 (not_279_out, OP1);
  not not_280 (not_280_out, OP0);
  not not_281 (not_281_out, F4);
  not not_282 (not_282_out, F3);
  not not_283 (not_283_out, F2);
  not not_284 (not_284_out, F0);
  not not_285 (not_285_out, OP5);
  not not_286 (not_286_out, OP4);
  not not_287 (not_287_out, OP3);
  not not_288 (not_288_out, OP2);
  not not_289 (not_289_out, OP1);
  not not_290 (not_290_out, OP0);
  not not_291 (not_291_out, F4);
  not not_292 (not_292_out, F3);
  not not_293 (not_293_out, F1);
  not not_294 (not_294_out, F0);
  not not_295 (not_295_out, OP5);
  not not_296 (not_296_out, OP4);
  not not_297 (not_297_out, OP3);
  not not_298 (not_298_out, OP2);
  not not_299 (not_299_out, OP1);
  not not_300 (not_300_out, OP0);
  not not_301 (not_301_out, F4);
  not not_302 (not_302_out, F3);
  not not_303 (not_303_out, F1);
  not not_304 (not_304_out, OP5);
  not not_305 (not_305_out, OP4);
  not not_306 (not_306_out, OP3);
  not not_307 (not_307_out, OP2);
  not not_308 (not_308_out, OP1);
  not not_309 (not_309_out, OP0);
  not not_310 (not_310_out, F4);
  not not_311 (not_311_out, F3);
  not not_312 (not_312_out, OP5);
  not not_313 (not_313_out, OP4);
  not not_314 (not_314_out, OP3);
  not not_315 (not_315_out, OP2);
  not not_316 (not_316_out, OP1);
  not not_317 (not_317_out, OP0);
  not not_318 (not_318_out, F4);
  not not_319 (not_319_out, F2);
  not not_320 (not_320_out, F0);
  not not_321 (not_321_out, OP5);
  not not_322 (not_322_out, OP4);
  not not_323 (not_323_out, OP3);
  not not_324 (not_324_out, OP2);
  not not_325 (not_325_out, OP1);
  not not_326 (not_326_out, OP0);
  not not_327 (not_327_out, F4);
  not not_328 (not_328_out, F2);
  not not_329 (not_329_out, OP5);
  not not_330 (not_330_out, OP4);
  not not_331 (not_331_out, OP3);
  not not_332 (not_332_out, OP2);
  not not_333 (not_333_out, OP1);
  not not_334 (not_334_out, OP0);
  not not_335 (not_335_out, F5);
  not not_336 (not_336_out, F4);
  not not_337 (not_337_out, F2);
  not not_338 (not_338_out, F1);
  not not_339 (not_339_out, F0);
  not not_340 (not_340_out, OP5);
  not not_341 (not_341_out, OP4);
  not not_342 (not_342_out, OP3);
  not not_343 (not_343_out, OP2);
  not not_344 (not_344_out, OP1);
  not not_345 (not_345_out, OP0);
  not not_346 (not_346_out, F5);
  not not_347 (not_347_out, F4);
  not not_348 (not_348_out, F3);
  not not_349 (not_349_out, OP5);
  not not_350 (not_350_out, OP4);
  not not_351 (not_351_out, OP3);
  not not_352 (not_352_out, OP1);
  not not_353 (not_353_out, OP0);
  not not_354 (not_354_out, OP5);
  not not_355 (not_355_out, OP4);
  not not_356 (not_356_out, OP3);
  not not_357 (not_357_out, OP1);
  not not_358 (not_358_out, OP5);
  not not_359 (not_359_out, OP4);
  not not_360 (not_360_out, OP3);
  not not_361 (not_361_out, OP2);
  not not_362 (not_362_out, OP1);
  not not_363 (not_363_out, OP0);
  not not_364 (not_364_out, F5);
  not not_365 (not_365_out, F4);
  not not_366 (not_366_out, F2);
  not not_367 (not_367_out, F1);
  not not_368 (not_368_out, F0);
  not not_369 (not_369_out, OP5);
  not not_370 (not_370_out, OP4);
  not not_371 (not_371_out, OP3);
  not not_372 (not_372_out, OP2);
  not not_373 (not_373_out, OP1);
  not not_374 (not_374_out, OP0);
  not not_375 (not_375_out, F5);
  not not_376 (not_376_out, F4);
  not not_377 (not_377_out, F2);
  not not_378 (not_378_out, F1);
  not not_379 (not_379_out, F0);
  not not_380 (not_380_out, OP5);
  not not_381 (not_381_out, OP4);
  not not_382 (not_382_out, OP3);
  not not_383 (not_383_out, OP2);
  not not_384 (not_384_out, OP0);
  not not_385 (not_385_out, OP5);
  not not_386 (not_386_out, OP4);
  not not_387 (not_387_out, OP3);
  not not_388 (not_388_out, OP2);
  not not_389 (not_389_out, OP5);
  not not_390 (not_390_out, OP4);
  not not_391 (not_391_out, OP3);
  not not_392 (not_392_out, OP2);
  and and_1 (MemToReg, OP5, not_1_out, not_2_out, not_3_out, OP1, OP0);
  and and_2 (and_2_out, OP5, not_4_out, OP3, not_5_out, OP1, OP0);
  and and_3 (and_3_out, OP5, not_6_out, OP3, not_7_out, not_8_out, not_9_out);
  and and_4 (and_4_out, not_10_out, not_11_out, OP3, not_12_out, not_13_out, not_14_out);
  and and_5 (and_5_out, not_15_out, not_16_out, OP3, OP2, not_17_out, not_18_out);
  and and_6 (and_6_out, not_19_out, not_20_out, OP3, not_21_out, not_22_out, OP0);
  and and_7 (and_7_out, not_23_out, not_24_out, OP3, not_25_out, OP1, not_26_out);
  and and_8 (and_8_out, not_27_out, not_28_out, OP3, OP2, not_29_out, OP0);
  and and_9 (and_9_out, OP5, not_30_out, not_31_out, not_32_out, OP1, OP0);
  and and_10 (and_10_out, OP5, not_33_out, OP3, not_34_out, OP1, OP0);
  and and_11 (and_11_out, not_35_out, not_36_out, OP3, OP2, OP1, not_37_out);
  and and_12 (and_12_out, OP5, not_38_out, OP3, not_39_out, not_40_out, not_41_out);
  and and_13 (and_13_out, not_42_out, not_43_out, not_44_out, not_45_out, not_46_out, not_47_out, not_48_out, not_49_out, not_50_out, not_51_out, not_52_out, not_53_out);
  and and_14 (and_14_out, not_54_out, not_55_out, not_56_out, not_57_out, not_58_out, not_59_out, not_60_out, not_61_out, not_62_out, not_63_out, F1, F0);
  and and_15 (and_15_out, not_64_out, not_65_out, not_66_out, not_67_out, not_68_out, not_69_out, not_70_out, not_71_out, not_72_out, not_73_out, F1, not_74_out);
  and and_16 (and_16_out, not_75_out, not_76_out, not_77_out, not_78_out, not_79_out, not_80_out, F5, not_81_out, not_82_out, not_83_out, not_84_out, not_85_out);
  and and_17 (and_17_out, not_86_out, not_87_out, not_88_out, not_89_out, not_90_out, not_91_out, F5, not_92_out, not_93_out, not_94_out, not_95_out, F0);
  and and_18 (and_18_out, not_96_out, not_97_out, not_98_out, not_99_out, not_100_out, not_101_out, F5, not_102_out, not_103_out, not_104_out, F1, not_105_out);
  and and_19 (and_19_out, not_106_out, not_107_out, not_108_out, not_109_out, not_110_out, not_111_out, F5, not_112_out, not_113_out, F2, not_114_out, not_115_out);
  and and_20 (and_20_out, not_116_out, not_117_out, not_118_out, not_119_out, not_120_out, not_121_out, F5, not_122_out, not_123_out, F2, not_124_out, F0);
  and and_21 (and_21_out, not_125_out, not_126_out, not_127_out, not_128_out, not_129_out, not_130_out, F5, not_131_out, not_132_out, F2, F1, F0);
  and and_22 (and_22_out, not_133_out, not_134_out, not_135_out, not_136_out, not_137_out, not_138_out, F5, not_139_out, F3, not_140_out, F1, not_141_out);
  and and_23 (and_23_out, not_142_out, not_143_out, not_144_out, not_145_out, not_146_out, not_147_out, F5, not_148_out, F3, not_149_out, F1, F0);
  and and_24 (and_24_out, not_150_out, not_151_out, not_152_out, not_153_out, OP1, OP0);
  and and_25 (and_25_out, not_154_out, not_155_out, OP3, not_156_out, not_157_out, not_158_out);
  and and_26 (and_26_out, not_159_out, not_160_out, OP3, OP2, not_161_out, not_162_out);
  and and_27 (and_27_out, not_163_out, not_164_out, OP3, not_165_out, not_166_out, OP0);
  and and_28 (and_28_out, not_167_out, not_168_out, OP3, not_169_out, OP1, not_170_out);
  and and_29 (and_29_out, not_171_out, not_172_out, OP3, OP2, not_173_out, OP0);
  and and_30 (and_30_out, OP5, not_174_out, not_175_out, not_176_out, OP1, OP0);
  and and_31 (and_31_out, not_177_out, not_178_out, OP3, OP2, OP1, not_179_out);
  and and_32 (and_32_out, not_180_out, not_181_out, not_182_out, not_183_out, not_184_out, not_185_out, not_186_out, not_187_out, not_188_out, F2, F1, F0);
  and and_33 (SysCALL, not_189_out, not_190_out, not_191_out, not_192_out, not_193_out, not_194_out, not_195_out, not_196_out, F3, F2, not_197_out, not_198_out);
  and and_34 (and_34_out, not_199_out, not_200_out, OP3, not_201_out, not_202_out, not_203_out);
  and and_35 (and_35_out, not_204_out, not_205_out, OP3, not_206_out, not_207_out, OP0);
  and and_36 (and_36_out, not_208_out, not_209_out, OP3, not_210_out, OP1, not_211_out);
  and and_37 (and_37_out, OP5, not_212_out, not_213_out, not_214_out, OP1, OP0);
  and and_38 (and_38_out, OP5, not_215_out, OP3, not_216_out, OP1, OP0);
  and and_39 (and_39_out, OP5, not_217_out, OP3, not_218_out, not_219_out, not_220_out);
  and and_40 (and_40_out, not_221_out, not_222_out, not_223_out, not_224_out, not_225_out, not_226_out, not_227_out, not_228_out, not_229_out, not_230_out, not_231_out, not_232_out);
  and and_41 (and_41_out, not_233_out, not_234_out, not_235_out, not_236_out, not_237_out, not_238_out, not_239_out, not_240_out, not_241_out, not_242_out, F1, F0);
  and and_42 (and_42_out, not_243_out, not_244_out, not_245_out, not_246_out, not_247_out, not_248_out, not_249_out, not_250_out, not_251_out, not_252_out, F1, not_253_out);
  and and_43 (and_43_out, not_254_out, not_255_out, not_256_out, not_257_out, not_258_out, not_259_out, F5, not_260_out, not_261_out, not_262_out, not_263_out, not_264_out);
  and and_44 (and_44_out, not_265_out, not_266_out, not_267_out, not_268_out, not_269_out, not_270_out, F5, not_271_out, not_272_out, not_273_out, not_274_out, F0);
  and and_45 (and_45_out, not_275_out, not_276_out, not_277_out, not_278_out, not_279_out, not_280_out, F5, not_281_out, not_282_out, not_283_out, F1, not_284_out);
  and and_46 (and_46_out, not_285_out, not_286_out, not_287_out, not_288_out, not_289_out, not_290_out, F5, not_291_out, not_292_out, F2, not_293_out, not_294_out);
  and and_47 (and_47_out, not_295_out, not_296_out, not_297_out, not_298_out, not_299_out, not_300_out, F5, not_301_out, not_302_out, F2, not_303_out, F0);
  and and_48 (and_48_out, not_304_out, not_305_out, not_306_out, not_307_out, not_308_out, not_309_out, F5, not_310_out, not_311_out, F2, F1, F0);
  and and_49 (and_49_out, not_312_out, not_313_out, not_314_out, not_315_out, not_316_out, not_317_out, F5, not_318_out, F3, not_319_out, F1, not_320_out);
  and and_50 (and_50_out, not_321_out, not_322_out, not_323_out, not_324_out, not_325_out, not_326_out, F5, not_327_out, F3, not_328_out, F1, F0);
  and and_51 (and_51_out, not_329_out, not_330_out, not_331_out, not_332_out, not_333_out, not_334_out, not_335_out, not_336_out, F3, not_337_out, not_338_out, not_339_out);
  and and_52 (and_52_out, not_340_out, not_341_out, not_342_out, not_343_out, not_344_out, not_345_out, not_346_out, not_347_out, not_348_out, F2, F1, F0);
  and and_53 (BEQ, not_349_out, not_350_out, not_351_out, OP2, not_352_out, not_353_out);
  and and_54 (BNE, not_354_out, not_355_out, not_356_out, OP2, not_357_out, OP0);
  and and_55 (JR, not_358_out, not_359_out, not_360_out, not_361_out, not_362_out, not_363_out, not_364_out, not_365_out, F3, not_366_out, not_367_out, not_368_out);
  and and_56 (and_56_out, not_369_out, not_370_out, not_371_out, not_372_out, not_373_out, not_374_out, not_375_out, not_376_out, F3, not_377_out, not_378_out, not_379_out);
  and and_57 (and_57_out, not_380_out, not_381_out, not_382_out, not_383_out, OP1, not_384_out);
  and and_58 (and_58_out, not_385_out, not_386_out, not_387_out, not_388_out, OP1, OP0);
  and and_59 (JAL, not_389_out, not_390_out, not_391_out, not_392_out, OP1, OP0);
  or or_1 (MemWrite, and_2_out, and_3_out);
  or or_2 (ALU_SRC, and_4_out, and_5_out, and_6_out, and_7_out, and_8_out, and_9_out, and_10_out, and_11_out, and_12_out);
  or or_3 (SignedExt, and_34_out, and_35_out, and_36_out, and_37_out, and_38_out, and_39_out);
  or or_4 (JMP, and_56_out, and_57_out, and_58_out);
  or or_5 (RegWrite, and_13_out, and_14_out, and_15_out, and_16_out, and_17_out, and_18_out, and_19_out, and_20_out, and_21_out, and_22_out, and_23_out, and_24_out, and_25_out, and_26_out, and_27_out, and_28_out, and_29_out, and_30_out, and_31_out, and_32_out);
  or or_6 (RegDst, and_40_out, and_41_out, and_42_out, and_43_out, and_44_out, and_45_out, and_46_out, and_47_out, and_48_out, and_49_out, and_50_out, and_51_out, and_52_out);
endmodule

// ALU
module MIPS_ALU (
  input  [4:0] shamt,
  input  [31:0] X,
  input  [31:0] Y,
  input  [3:0] AluOP,
  output Equal,
  output [31:0] Result,
  output [31:0] Result_2
);

  wire [0:0] comparator_1_lt, comparator_2_lt;
  wire [31:0] adder_1_out, AND_out, divider_1_out, divider_1_rem, multiplier_1_cout, multiplier_1_out,
       NOR_out, OR_out, shifter_1_out, shifter_2_out, shifter_3_out, subtractor_1_out, XOR_out;

  assign AND_out = X & Y;  // AND_Gate AND, 32 bits wide
  assign OR_out = X | Y;  // OR_Gate OR, 32 bits wide
  Shifter #(.width(32)) shifter_1 (.in(Y), .\dist (shamt), .out(shifter_1_out));
  Shifter #(.width(32), .shift("ar")) shifter_2 (.in(Y), .\dist (shamt), .out(shifter_2_out));
  Shifter #(.width(32), .shift("lr")) shifter_3 (.in(Y), .\dist (shamt), .out(shifter_3_out));
  Multiplier #(.width(32)) multiplier_1 (.a(X), .b(Y), .out(multiplier_1_out), .cout(multiplier_1_cout));  // open: cin
  Divider #(.width(32)) divider_1 (.a(X), .b(Y), .out(divider_1_out), .rem(divider_1_rem));  // open: upper
  Adder #(.width(32)) adder_1 (.a(X), .b(Y), .out(adder_1_out));  // open: cin, cout
  Subtractor #(.width(32)) subtractor_1 (.a(X), .b(Y), .out(subtractor_1_out));  // open: bin, bout
  assign XOR_out = X ^ Y;  // XOR_Gate XOR, 32 bits wide
  assign NOR_out = ~(X | Y);  // NOR_Gate NOR, 32 bits wide
  Comparator #(.width(32)) comparator_1 (.a(X), .b(Y), .eq(Equal), .lt(comparator_1_lt[0]));  // open: gt
  Comparator #(.width(32), .mode("unsigned")) comparator_2 (.a(X), .b(Y), .lt(comparator_2_lt[0]));  // open: gt, eq
  Multiplexer #(.select(4), .width(32), .enable("false")) multiplexer_1 (
    .in0(shifter_1_out), .in1(shifter_2_out), .in2(shifter_3_out), .in3(multiplier_1_out),
    .in4(divider_1_out), .in5(adder_1_out), .in6(subtractor_1_out), .in7(AND_out), .in8(OR_out),
    .in9(XOR_out), .in10(NOR_out), .in11({{31{1'b0}}, comparator_1_lt[0]}),
    .in12({{31{1'b0}}, comparator_2_lt[0]}), .in13({32{1'b0}}), .in14({32{1'b0}}), .in15({32{1'b0}}),
    .out(Result), .sel(AluOP));
  Multiplexer #(.select(4), .width(32), .enable("false")) multiplexer_2 (
    .in0({32{1'b0}}), .in1({32{1'b0}}), .in2({32{1'b0}}), .in3(multiplier_1_cout), .in4(divider_1_rem),
    .in5({32{1'b0}}), .in6({32{1'b0}}), .in7({32{1'b0}}), .in8({32{1'b0}}), .in9({32{1'b0}}),
    .in10({32{1'b0}}), .in11({32{1'b0}}), .in12({32{1'b0}}), .in13({32{1'b0}}), .in14({32{1'b0}}),
    .in15({32{1'b0}}), .out(Result_2), .sel(AluOP));

  // Other names for the same wires on the sheet: Result2[31:0] = Result_2; S[3:0] = AluOP

  // Notes on the sheet:
  //   不要改变此引脚区域内容，也不要改变ALU封装形式
  //   输入引脚
  //   输出引脚
endmodule

module MIPS_Regifile (
  input  [31:0] Din,
  input  Clk,
  input  WE,
  input  [4:0] R1_num,
  input  [4:0] W_num,
  input  [4:0] R2_num,
  output [31:0] R1,
  output [31:0] R2
);

  // RegisterFile registerfile_1: pin names not known; wires that end beside it: Din, Clk, WE, W_num, R1_num, R2_num, R1, R2
endmodule

module \理想流水线  (
  output [31:0] out_1,
  output [31:0] out_2,
  output [31:0] out_3
);

  wire Alus, AlusEx, and_1_out, and_2_out, and_3_out, and_4_out, and_5_out, Beq, BeqEx, BLEZ, BLEZEx, BLEZM,
       BLEZWB, Bne, BneEx, CLK, comparator_1_gt, comparator_2_eq, comparator_3_eq, condi, d_ff_1_q, equ, Go,
       halt, IR1, IR2, IR3, JAL, JALEx, JALM, JALWB, JMP, JMPEx, JR, JREx, led, MemToReg, MemToRegEx,
       MemToRegM, MemToRegWB, MemWrite, MemWriteEx, MemWriteM, nor_1_out, not_1_out, not_2_out, or_1_out,
       pause, pcen, RegDst, RegDstEx, RegDstM, RegDstWB, RegWrite, RegWriteEx, RegWriteM, RegWriteWB, RST,
       SB, SBEx, SBM, SignedExt, SignedExtEx, SRAV, SRAVEx, SRAVM, SRAVWB, Sys, SysID, SysIDEx, SysM, SysWB,
       W1, W2, W3;
  wire [1:1] PCSrc;
  wire [3:0] Aluop, AluopEx, multiplexer_7_out, multiplexer_9_out;
  wire [4:0] multiplexer_5_out, R1_num, R2_num, W_num;
  wire [15:0] \LoadUse次数 , \总周期数 , \插入气泡数 , \无条件分支数 , \条件分支成功数 ;
  wire [31:0] adder_3_out, bit_extender_1_out, bit_extender_2_out, bit_extender_3_out, bit_extender_4_out,
       Din, EX_PC, Ext, ExtEX, FinalMemData, ID_PC, IF_PC, IREX, IRM, IRWB, LedData, MEM_PC, MemData,
       MemDataWB, multiplexer_4_out, multiplexer_8_out, multiplexer_12_out, pc1, pc2, PCWB, R1EX, R2EX, R2ID,
       R2M, result, resultM, resultWB, shifter_1_out, shifter_2_out, shifter_3_out, shifter_4_out;

  Button \u_总复位  (.out(RST));
  Button _1 (.out(IR1));
  Button _2 (.out(IR2));
  Button _3 (.out(IR3));
  Button \u_继续运行  (.out(Go));
  LED led_1 (.in(W1));
  LED led_2 (.in(W2));
  LED led_3 (.in(W3));
  and and_1 (and_1_out, ~SysWB, Go);  // AND_Gate
  Hex_Digit_Display hex_digit_display_1 (.value(LedData[31:28]));  // open: dp
  D_Flip_Flop d_ff_1 (.clk(CLK), .D(and_1_out), .Q(d_ff_1_q), .reset(RST));  // open: Qn, preset, en
  not not_1 (not_1_out, d_ff_1_q);
  or or_1 (or_1_out, SysWB, pause);
  Comparator #(.width(32)) comparator_1 (.a(pc1), .b({32{1'b0}}), .gt(comparator_1_gt));  // open: eq, lt
  Hex_Digit_Display hex_digit_display_2 (.value(LedData[23:20]));  // open: dp
  Hex_Digit_Display hex_digit_display_3 (.value(LedData[27:24]));  // open: dp
  xor xor_1 (pcen, not_1_out, or_1_out);
  Register #(.width(32)) PC (.D(out_3), .en(pcen), .Q(IF_PC), .clk(CLK), .clr(RST));
  assign bit_extender_1_out = {{16{1'b0}}, out_2[15:0]};  // Bit_Extender bit_extender_1
  assign bit_extender_2_out = {{16{out_2[15]}}, out_2[15:0]};  // Bit_Extender bit_extender_2
  and and_2 (and_2_out, Beq, equ);
  and and_3 (and_3_out, Bne, ~equ);  // AND_Gate
  and and_4 (and_4_out, BLEZ, ~comparator_1_gt);  // AND_Gate
  or or_2 (PCSrc[1], condi, and_5_out);
  and and_5 (and_5_out, JMP, ~JR);  // AND_Gate
  Adder #(.width(32)) adder_1 (.a(IF_PC), .b(32'h4), .out(out_3));  // open: cin, cout
  Shifter #(.width(32)) shifter_1 (.in(Ext), .\dist (5'b00010), .out(shifter_1_out));
  Hex_Digit_Display hex_digit_display_4 (.value(LedData[15:12]));  // open: dp
  Hex_Digit_Display hex_digit_display_5 (.value(LedData[19:16]));  // open: dp
  Comparator #(.width(32)) comparator_2 (.a(pc1), .b(32'h22), .eq(comparator_2_eq));  // open: gt, lt
  Comparator #(.width(32)) comparator_3 (.a(pc1), .b(32'ha), .eq(comparator_3_eq));  // open: gt, lt
  Multiplexer #(.width(32), .enable("false")) multiplexer_1 (
    .in0(bit_extender_1_out), .in1(bit_extender_2_out), .out(Ext), .sel(SignedExt));
  or or_3 (condi, and_2_out, and_3_out, and_4_out);
  Adder #(.width(32)) adder_2 (.a(out_3), .b(shifter_1_out), .out(pc2));  // open: cin, cout
  Hex_Digit_Display hex_digit_display_6 (.value(LedData[11:8]));  // open: dp
  Hex_Digit_Display hex_digit_display_7 (.value(LedData[7:4]));  // open: dp
  Clock clock_1 (.out(CLK));
  and and_6 (led, comparator_2_eq, Sys);
  and and_7 (halt, Sys, comparator_3_eq);
  nor nor_1 (nor_1_out, halt, led);
  Hex_Digit_Display hex_digit_display_8 (.value(LedData[3:0]));  // open: dp
  and and_8 (pause, nor_1_out, Sys);
  ROM #(.addrWidth(10), .dataWidth(32)) rom_1 (.addr(IF_PC[11:2]), .data(out_1));  // open: sel
  // Probe on \总周期数 
  // Probe on \无条件分支数 
  // Probe on \条件分支成功数 
  // Probe on \插入气泡数 
  // Probe on \LoadUse次数 
  and and_9 (SysID, Sys, halt);
  IF_ID if_id_1 (
    .IR(out_1), .PC(IF_PC), .CLK(CLK), .RST(RST), .EN(SysID), .IROUT(out_2), .PCOUT(ID_PC));  // open: forcast, forcast_out
  // Probe on IF_PC[11:0]
  // Probe on ID_PC[11:0]
  // Probe on MEM_PC[11:0]
  // Probe on EX_PC[11:0]
  \硬布线控制器  \u_硬布线控制器_1  (
    .Func(out_2[5:0]), .OP(out_2[31:26]), .ALU_OP(Aluop), .MemToReg(MemToReg), .MemWrite(MemWrite),
    .ALU_SRC(Alus), .RegWrite(RegWrite), .SysCALL(Sys), .SignedExt(SignedExt), .RegDst(RegDst), .JR(JR),
    .JMP(JMP), .Beq(Beq), .JAL(JAL), .Bne(Bne), .SRAV(SRAV), .BLEZ(BLEZ), .SB(SB));  // open: MFC0, ERET
  MIPS_Regifile mips_regifile_1 (
    .Din(Din), .Clk(CLK), .R1(pc1), .R2(R2ID), .WE(RegWriteWB), .W_num(W_num), .R1_num(R1_num),
    .R2_num(R2_num));
  Multiplexer #(.width(5), .enable("false")) multiplexer_2 (
    .in0(out_2[25:21]), .in1(5'b00010), .out(R1_num), .sel(Sys));
  Multiplexer #(.width(5), .enable("false")) multiplexer_3 (
    .in0(out_2[20:16]), .in1(5'b00100), .out(R2_num), .sel(Sys));
  // Probe on PCWB[11:0]
  Counter #(.width(16), .max('hffff)) counter_1 (
    .count(JMP), .Q(\无条件分支数 ), .clk(CLK), .clr(RST));  // open: load, D, carry
  Counter #(.width(16), .max('hffff)) counter_2 (
    .count(condi), .Q(\条件分支成功数 ), .clk(CLK), .clr(RST));  // open: load, D, carry
  not not_2 (not_2_out, SysWB);
  Counter #(.width(16), .max('hffff)) counter_3 (
    .count(not_2_out), .Q(\总周期数 ), .clk(CLK), .clr(RST));  // open: load, D, carry
  ID_EX id_ex_1 (
    .IR(out_2), .PC(ID_PC), .CLK(CLK), .RST(RST), .EN(SysIDEx), .R1(pc1), .R2(R2ID), .Beq(Beq), .JMP(JMP),
    .JR(JR), .Bne(Bne), .MemToReg(MemToReg), .SRAV(SRAV), .MemWrite(MemWrite), .BLEZ(BLEZ), .ALUop(Aluop),
    .SB(SB), .Alus(Alus), .RegWrite(RegWrite), .JAL(JAL), .RegDst(RegDst), .IRout(IREX), .PCout(EX_PC),
    .R1out(R1EX), .R2out(R2EX), .JMP_out(JMPEx), .Beq_out(BeqEx), .JR_out(JREx), .Bne_out(BneEx),
    .MemToReg_out(MemToRegEx), .SRAV_out(SRAVEx), .MemWrite_out(MemWriteEx), .BLEZ_out(BLEZEx),
    .Aluop_out(AluopEx), .SB_out(SBEx), .Alus_out(AlusEx), .RegWrite_out(RegWriteEx), .JAL_out(JALEx),
    .RegDst_out(RegDstEx), .SignedExt(SignedExt), .SignedExt_out(SignedExtEx), .SysDin(SysID),
    .SysDout(SysIDEx));  // open: forward1, f1out, forward2, f2out, forcast, forcast_out
  assign bit_extender_3_out = {{16{1'b0}}, IREX[15:0]};  // Bit_Extender bit_extender_3
  assign bit_extender_4_out = {{16{IREX[15]}}, IREX[15:0]};  // Bit_Extender bit_extender_4
  Multiplexer #(.width(32), .enable("false")) multiplexer_4 (
    .in0(R2EX), .in1(ExtEX), .out(multiplexer_4_out), .sel(AlusEx));
  Multiplexer #(.width(5), .enable("false")) multiplexer_5 (
    .in0(IREX[10:6]), .in1(R1EX[4:0]), .out(multiplexer_5_out), .sel(SRAVEx));
  Multiplexer #(.width(32), .enable("false")) multiplexer_6 (
    .in0(bit_extender_3_out), .in1(bit_extender_4_out), .out(ExtEX), .sel(SignedExtEx));
  MIPS_ALU mips_alu_1 (
    .X(R1EX), .Y(multiplexer_4_out), .AluOP(AluopEx), .Equal(equ), .Result(result), .shamt(multiplexer_5_out));  // open: Result_2
  EX_MEM ex_mem_1 (
    .CLK(CLK), .IR(IREX), .PC(EX_PC), .RST(RST), .EN(SysM), .result(result), .R2(R2EX),
    .MemToReg(MemToRegEx), .RegDst(RegDstEx), .JAL(JALEx), .BLEZ(BLEZEx), .SRAV(SRAVEx),
    .RegWrite(RegWriteEx), .MemWrite(MemWriteEx), .sys(SysIDEx), .IRout(IRM), .PCout(MEM_PC),
    .resultout(resultM), .R2out(R2M), .MemToRegout(MemToRegM), .RegDstout(RegDstM), .JALout(JALM),
    .BLEZ_2(BLEZM), .SRAVout(SRAVM), .RegWrite_2(RegWriteM), .MemWriteOut(MemWriteM), .sysout(SysM),
    .SB(SBEx), .SBout(SBM));
  Shifter #(.width(32)) shifter_2 (.in(R2M), .\dist (5'b01000), .out(shifter_2_out));
  Shifter #(.width(32)) shifter_3 (.in(R2M), .\dist (5'b10000), .out(shifter_3_out));
  Shifter #(.width(32)) shifter_4 (.in(R2M), .\dist (5'b11000), .out(shifter_4_out));
  Multiplexer #(.select(2), .width(4), .enable("false")) multiplexer_7 (
    .in0(4'b0001), .in1(4'b0010), .in2(4'b0100), .in3(4'b1000), .out(multiplexer_7_out), .sel(resultM[1:0]));
  Multiplexer #(.select(2), .width(32), .enable("false")) multiplexer_8 (
    .in0(R2M), .in1(shifter_2_out), .in2(shifter_3_out), .in3(shifter_4_out), .out(multiplexer_8_out),
    .sel(resultM[1:0]));
  Multiplexer #(.width(4), .enable("false")) multiplexer_9 (
    .in0(4'b1111), .in1(multiplexer_7_out), .out(multiplexer_9_out), .sel(SBM));
  // MIPS_RAM mips_ram_1: pin names not known; wires that end beside it: {{10{1'b0}}, resultM[11:2]}, FinalMemData, MemWriteM, multiplexer_9_out, CLK, RST, MemData
  Multiplexer #(.width(32), .enable("false")) multiplexer_10 (
    .in0(R2M), .in1(multiplexer_8_out), .out(FinalMemData), .sel(SB));
  MEM_WB mem_wb_1 (
    .CLK(CLK), .IR(IRM), .PC(MEM_PC), .RST(RST), .EN(SysWB), .result(resultM), .MemData(MemData),
    .MemToReg(MemToRegM), .RegDst(RegDstM), .JAL(JALM), .BLEZ(BLEZM), .SRAV(SRAVM), .RegWrite(RegWriteM),
    .sys(SysM), .IRout(IRWB), .PCout(PCWB), .MemDataout(MemDataWB), .resultout(resultWB),
    .MemToRegout(MemToRegWB), .RegDstout(RegDstWB), .JALout(JALWB), .BLEZ_2(BLEZWB), .SRAVout(SRAVWB),
    .RegWrite_2(RegWriteWB), .sysout(SysWB));
  Multiplexer #(.select(2), .width(5), .enable("false")) multiplexer_11 (
    .in0(IRWB[20:16]), .in1(IRWB[15:11]), .in2({5{1'b1}}), .in3({5{1'b1}}), .out(W_num),
    .sel({JALWB, RegDstWB}));
  Adder #(.width(32)) adder_3 (.a(IF_PC), .b(32'h4), .out(adder_3_out));  // open: cin, cout
  Multiplexer #(.width(32), .enable("false")) multiplexer_12 (
    .in0(resultWB), .in1(MemDataWB), .out(multiplexer_12_out), .sel(MemToRegWB));
  Multiplexer #(.width(32), .enable("false")) multiplexer_13 (
    .in0(multiplexer_12_out), .in1(adder_3_out), .out(Din), .sel(JALWB));
  MIPS_ALU mips_alu_2 ();  // open: X, Y, AluOP, Equal, Result, Result_2, shamt

  // Other names for the same wires on the sheet: IRID[31:0] = out_2; pc0[31:0] = out_3; R1ID[31:0] = pc1;
  //   pc3[31:2] = {out_3[31:28], out_2[25:0]}; PCEX[31:0] = EX_PC; PCID[31:0] = ID_PC; PCIF[31:0] = IF_PC;
  //   PCM[31:0] = MEM_PC; PCSrc[0] = JMP; WB_PC[31:0] = PCWB

  // Notes on the sheet:
  //   中断源
  //   中断等待指示
  //   pcout
  //   数码管输出
  //   irout
  //   contents of rom_1 (hex, n*v repeats v):
  //   20100000 20110001 20120002 20130003 36100000 36310001 36520002 36730003 ae100000 ae110004 ae120008
  //   ae13000c 2002000a 0 0 0 c
  //   JMP
  //   JR
  //   OP
  //   Func
  //   流水调试日志用
  //   Beq
  //   Bne
  //   MemToReg
  //   MemWrite
  //   AluOP
  //   AluSrcB
  //   RegWrite
  //   JAL
  //   RegDst
  //   Syscall
endmodule

// 源寄存器使用情况
module \源寄存器使用情况  (
  input  OP0,
  input  OP1,
  input  OP2,
  input  OP3,
  input  OP4,
  input  OP5,
  input  F0,
  input  F1,
  input  F2,
  input  F3,
  input  F4,
  input  F5,
  output R1_Used,
  output R2_Used
);

  wire and_1_out, and_2_out, and_3_out, and_4_out, and_5_out, and_6_out, and_7_out, and_8_out, and_9_out,
       and_10_out, and_11_out, and_12_out, and_13_out, and_14_out, and_15_out, and_16_out, and_17_out,
       and_18_out, and_19_out, and_20_out, and_21_out, and_22_out, and_23_out, and_24_out, and_25_out,
       and_26_out, and_27_out, and_28_out, and_29_out, and_30_out, and_31_out, and_32_out, and_33_out,
       and_34_out, and_35_out, and_36_out, and_37_out, and_38_out, and_39_out, and_40_out, and_41_out,
       and_42_out, not_1_out, not_2_out, not_3_out, not_4_out, not_5_out, not_6_out, not_7_out, not_8_out,
       not_9_out, not_10_out, not_11_out, not_12_out, not_13_out, not_14_out, not_15_out, not_16_out,
       not_17_out, not_18_out, not_19_out, not_20_out, not_21_out, not_22_out, not_23_out, not_24_out,
       not_25_out, not_26_out, not_27_out, not_28_out, not_29_out, not_30_out, not_31_out, not_32_out,
       not_33_out, not_34_out, not_35_out, not_36_out, not_37_out, not_38_out, not_39_out, not_40_out,
       not_41_out, not_42_out, not_43_out, not_44_out, not_45_out, not_46_out, not_47_out, not_48_out,
       not_49_out, not_50_out, not_51_out, not_52_out, not_53_out, not_54_out, not_55_out, not_56_out,
       not_57_out, not_58_out, not_59_out, not_60_out, not_61_out, not_62_out, not_63_out, not_64_out,
       not_65_out, not_66_out, not_67_out, not_68_out, not_69_out, not_70_out, not_71_out, not_72_out,
       not_73_out, not_74_out, not_75_out, not_76_out, not_77_out, not_78_out, not_79_out, not_80_out,
       not_81_out, not_82_out, not_83_out, not_84_out, not_85_out, not_86_out, not_87_out, not_88_out,
       not_89_out, not_90_out, not_91_out, not_92_out, not_93_out, not_94_out, not_95_out, not_96_out,
       not_97_out, not_98_out, not_99_out, not_100_out, not_101_out, not_102_out, not_103_out, not_104_out,
       not_105_out, not_106_out, not_107_out, not_108_out, not_109_out, not_110_out, not_111_out,
       not_112_out, not_113_out, not_114_out, not_115_out, not_116_out, not_117_out, not_118_out,
       not_119_out, not_120_out, not_121_out, not_122_out, not_123_out, not_124_out, not_125_out,
       not_126_out, not_127_out, not_128_out, not_129_out, not_130_out, not_131_out, not_132_out,
       not_133_out, not_134_out, not_135_out, not_136_out, not_137_out, not_138_out, not_139_out,
       not_140_out, not_141_out, not_142_out, not_143_out, not_144_out, not_145_out, not_146_out,
       not_147_out, not_148_out, not_149_out, not_150_out, not_151_out, not_152_out, not_153_out,
       not_154_out, not_155_out, not_156_out, not_157_out, not_158_out, not_159_out, not_160_out,
       not_161_out, not_162_out, not_163_out, not_164_out, not_165_out, not_166_out, not_167_out,
       not_168_out, not_169_out, not_170_out, not_171_out, not_172_out, not_173_out, not_174_out,
       not_175_out, not_176_out, not_177_out, not_178_out, not_179_out, not_180_out, not_181_out,
       not_182_out, not_183_out, not_184_out, not_185_out, not_186_out, not_187_out, not_188_out,
       not_189_out, not_190_out, not_191_out, not_192_out, not_193_out, not_194_out, not_195_out,
       not_196_out, not_197_out, not_198_out, not_199_out, not_200_out, not_201_out, not_202_out,
       not_203_out, not_204_out, not_205_out, not_206_out, not_207_out, not_208_out, not_209_out,
       not_210_out, not_211_out, not_212_out, not_213_out, not_214_out, not_215_out, not_216_out,
       not_217_out, not_218_out, not_219_out, not_220_out, not_221_out, not_222_out, not_223_out,
       not_224_out, not_225_out, not_226_out, not_227_out, not_228_out, not_229_out, not_230_out,
       not_231_out, not_232_out, not_233_out, not_234_out, not_235_out, not_236_out, not_237_out,
       not_238_out, not_239_out, not_240_out, not_241_out, not_242_out, not_243_out, not_244_out,
       not_245_out, not_246_out, not_247_out, not_248_out, not_249_out, not_250_out, not_251_out,
       not_252_out, not_253_out, not_254_out, not_255_out, not_256_out, not_257_out, not_258_out,
       not_259_out, not_260_out, not_261_out, not_262_out, not_263_out, not_264_out, not_265_out,
       not_266_out, not_267_out, not_268_out, not_269_out, not_270_out, not_271_out, not_272_out,
       not_273_out, not_274_out, not_275_out, not_276_out, not_277_out, not_278_out, not_279_out,
       not_280_out, not_281_out, not_282_out, not_283_out, not_284_out, not_285_out, not_286_out,
       not_287_out, not_288_out, not_289_out, not_290_out, not_291_out, not_292_out, not_293_out,
       not_294_out, not_295_out, not_296_out, not_297_out, not_298_out, not_299_out, not_300_out,
       not_301_out, not_302_out, not_303_out, not_304_out, not_305_out, not_306_out, not_307_out,
       not_308_out, not_309_out, not_310_out, not_311_out, not_312_out, not_313_out, not_314_out,
       not_315_out, not_316_out, not_317_out, not_318_out, not_319_out, not_320_out, not_321_out;

  not not_1 (not_1_out, OP5);
  not not_2 (not_2_out, OP4);
  not not_3 (not_3_out, OP3);
  not not_4 (not_4_out, OP2);
  not not_5 (not_5_out, OP1);
  not not_6 (not_6_out, OP0);
  not not_7 (not_7_out, F5);
  not not_8 (not_8_out, F4);
  not not_9 (not_9_out, F3);
  not not_10 (not_10_out, F2);
  not not_11 (not_11_out, F1);
  not not_12 (not_12_out, F0);
  not not_13 (not_13_out, OP5);
  not not_14 (not_14_out, OP4);
  not not_15 (not_15_out, OP3);
  not not_16 (not_16_out, OP2);
  not not_17 (not_17_out, OP1);
  not not_18 (not_18_out, OP0);
  not not_19 (not_19_out, F5);
  not not_20 (not_20_out, F4);
  not not_21 (not_21_out, F3);
  not not_22 (not_22_out, F2);
  not not_23 (not_23_out, OP5);
  not not_24 (not_24_out, OP4);
  not not_25 (not_25_out, OP3);
  not not_26 (not_26_out, OP2);
  not not_27 (not_27_out, OP1);
  not not_28 (not_28_out, OP0);
  not not_29 (not_29_out, F5);
  not not_30 (not_30_out, F4);
  not not_31 (not_31_out, F3);
  not not_32 (not_32_out, F2);
  not not_33 (not_33_out, F0);
  not not_34 (not_34_out, OP5);
  not not_35 (not_35_out, OP4);
  not not_36 (not_36_out, OP3);
  not not_37 (not_37_out, OP2);
  not not_38 (not_38_out, OP1);
  not not_39 (not_39_out, OP0);
  not not_40 (not_40_out, F4);
  not not_41 (not_41_out, F3);
  not not_42 (not_42_out, F2);
  not not_43 (not_43_out, F1);
  not not_44 (not_44_out, F0);
  not not_45 (not_45_out, OP5);
  not not_46 (not_46_out, OP4);
  not not_47 (not_47_out, OP3);
  not not_48 (not_48_out, OP2);
  not not_49 (not_49_out, OP1);
  not not_50 (not_50_out, OP0);
  not not_51 (not_51_out, F4);
  not not_52 (not_52_out, F3);
  not not_53 (not_53_out, F2);
  not not_54 (not_54_out, F1);
  not not_55 (not_55_out, OP5);
  not not_56 (not_56_out, OP4);
  not not_57 (not_57_out, OP3);
  not not_58 (not_58_out, OP2);
  not not_59 (not_59_out, OP1);
  not not_60 (not_60_out, OP0);
  not not_61 (not_61_out, F4);
  not not_62 (not_62_out, F3);
  not not_63 (not_63_out, F2);
  not not_64 (not_64_out, F0);
  not not_65 (not_65_out, OP5);
  not not_66 (not_66_out, OP4);
  not not_67 (not_67_out, OP3);
  not not_68 (not_68_out, OP2);
  not not_69 (not_69_out, OP1);
  not not_70 (not_70_out, OP0);
  not not_71 (not_71_out, F4);
  not not_72 (not_72_out, F3);
  not not_73 (not_73_out, F1);
  not not_74 (not_74_out, F0);
  not not_75 (not_75_out, OP5);
  not not_76 (not_76_out, OP4);
  not not_77 (not_77_out, OP3);
  not not_78 (not_78_out, OP2);
  not not_79 (not_79_out, OP1);
  not not_80 (not_80_out, OP0);
  not not_81 (not_81_out, F4);
  not not_82 (not_82_out, F3);
  not not_83 (not_83_out, F1);
  not not_84 (not_84_out, OP5);
  not not_85 (not_85_out, OP4);
  not not_86 (not_86_out, OP3);
  not not_87 (not_87_out, OP2);
  not not_88 (not_88_out, OP1);
  not not_89 (not_89_out, OP0);
  not not_90 (not_90_out, F4);
  not not_91 (not_91_out, F3);
  not not_92 (not_92_out, OP5);
  not not_93 (not_93_out, OP4);
  not not_94 (not_94_out, OP3);
  not not_95 (not_95_out, OP2);
  not not_96 (not_96_out, OP1);
  not not_97 (not_97_out, OP0);
  not not_98 (not_98_out, F4);
  not not_99 (not_99_out, F2);
  not not_100 (not_100_out, F0);
  not not_101 (not_101_out, OP5);
  not not_102 (not_102_out, OP4);
  not not_103 (not_103_out, OP3);
  not not_104 (not_104_out, OP2);
  not not_105 (not_105_out, OP1);
  not not_106 (not_106_out, OP0);
  not not_107 (not_107_out, F4);
  not not_108 (not_108_out, F2);
  not not_109 (not_109_out, OP5);
  not not_110 (not_110_out, OP4);
  not not_111 (not_111_out, OP3);
  not not_112 (not_112_out, OP2);
  not not_113 (not_113_out, OP1);
  not not_114 (not_114_out, OP0);
  not not_115 (not_115_out, F5);
  not not_116 (not_116_out, F4);
  not not_117 (not_117_out, F2);
  not not_118 (not_118_out, F1);
  not not_119 (not_119_out, F0);
  not not_120 (not_120_out, OP5);
  not not_121 (not_121_out, OP4);
  not not_122 (not_122_out, OP3);
  not not_123 (not_123_out, OP2);
  not not_124 (not_124_out, OP1);
  not not_125 (not_125_out, OP0);
  not not_126 (not_126_out, F5);
  not not_127 (not_127_out, F4);
  not not_128 (not_128_out, F1);
  not not_129 (not_129_out, F0);
  not not_130 (not_130_out, OP5);
  not not_131 (not_131_out, OP4);
  not not_132 (not_132_out, OP3);
  not not_133 (not_133_out, OP1);
  not not_134 (not_134_out, OP0);
  not not_135 (not_135_out, OP5);
  not not_136 (not_136_out, OP4);
  not not_137 (not_137_out, OP3);
  not not_138 (not_138_out, OP1);
  not not_139 (not_139_out, OP5);
  not not_140 (not_140_out, OP4);
  not not_141 (not_141_out, OP2);
  not not_142 (not_142_out, OP1);
  not not_143 (not_143_out, OP0);
  not not_144 (not_144_out, OP5);
  not not_145 (not_145_out, OP4);
  not not_146 (not_146_out, OP1);
  not not_147 (not_147_out, OP0);
  not not_148 (not_148_out, OP5);
  not not_149 (not_149_out, OP4);
  not not_150 (not_150_out, OP2);
  not not_151 (not_151_out, OP1);
  not not_152 (not_152_out, OP5);
  not not_153 (not_153_out, OP4);
  not not_154 (not_154_out, OP2);
  not not_155 (not_155_out, OP0);
  not not_156 (not_156_out, OP5);
  not not_157 (not_157_out, OP4);
  not not_158 (not_158_out, OP1);
  not not_159 (not_159_out, OP4);
  not not_160 (not_160_out, OP3);
  not not_161 (not_161_out, OP2);
  not not_162 (not_162_out, OP4);
  not not_163 (not_163_out, OP2);
  not not_164 (not_164_out, OP5);
  not not_165 (not_165_out, OP4);
  not not_166 (not_166_out, OP3);
  not not_167 (not_167_out, OP2);
  not not_168 (not_168_out, OP1);
  not not_169 (not_169_out, OP0);
  not not_170 (not_170_out, F5);
  not not_171 (not_171_out, F4);
  not not_172 (not_172_out, F3);
  not not_173 (not_173_out, OP5);
  not not_174 (not_174_out, OP4);
  not not_175 (not_175_out, OP0);
  not not_176 (not_176_out, OP5);
  not not_177 (not_177_out, OP4);
  not not_178 (not_178_out, OP3);
  not not_179 (not_179_out, OP0);
  not not_180 (not_180_out, OP5);
  not not_181 (not_181_out, OP4);
  not not_182 (not_182_out, OP3);
  not not_183 (not_183_out, OP2);
  not not_184 (not_184_out, OP1);
  not not_185 (not_185_out, OP0);
  not not_186 (not_186_out, F5);
  not not_187 (not_187_out, F4);
  not not_188 (not_188_out, F3);
  not not_189 (not_189_out, F2);
  not not_190 (not_190_out, F1);
  not not_191 (not_191_out, F0);
  not not_192 (not_192_out, OP5);
  not not_193 (not_193_out, OP4);
  not not_194 (not_194_out, OP3);
  not not_195 (not_195_out, OP2);
  not not_196 (not_196_out, OP1);
  not not_197 (not_197_out, OP0);
  not not_198 (not_198_out, F5);
  not not_199 (not_199_out, F4);
  not not_200 (not_200_out, F3);
  not not_201 (not_201_out, F2);
  not not_202 (not_202_out, OP5);
  not not_203 (not_203_out, OP4);
  not not_204 (not_204_out, OP3);
  not not_205 (not_205_out, OP2);
  not not_206 (not_206_out, OP1);
  not not_207 (not_207_out, OP0);
  not not_208 (not_208_out, F5);
  not not_209 (not_209_out, F4);
  not not_210 (not_210_out, F3);
  not not_211 (not_211_out, F2);
  not not_212 (not_212_out, F0);
  not not_213 (not_213_out, OP5);
  not not_214 (not_214_out, OP4);
  not not_215 (not_215_out, OP3);
  not not_216 (not_216_out, OP2);
  not not_217 (not_217_out, OP1);
  not not_218 (not_218_out, OP0);
  not not_219 (not_219_out, F4);
  not not_220 (not_220_out, F3);
  not not_221 (not_221_out, F2);
  not not_222 (not_222_out, F1);
  not not_223 (not_223_out, F0);
  not not_224 (not_224_out, OP5);
  not not_225 (not_225_out, OP4);
  not not_226 (not_226_out, OP3);
  not not_227 (not_227_out, OP2);
  not not_228 (not_228_out, OP1);
  not not_229 (not_229_out, OP0);
  not not_230 (not_230_out, F4);
  not not_231 (not_231_out, F3);
  not not_232 (not_232_out, F2);
  not not_233 (not_233_out, F1);
  not not_234 (not_234_out, OP5);
  not not_235 (not_235_out, OP4);
  not not_236 (not_236_out, OP3);
  not not_237 (not_237_out, OP2);
  not not_238 (not_238_out, OP1);
  not not_239 (not_239_out, OP0);
  not not_240 (not_240_out, F4);
  not not_241 (not_241_out, F3);
  not not_242 (not_242_out, F2);
  not not_243 (not_243_out, F0);
  not not_244 (not_244_out, OP5);
  not not_245 (not_245_out, OP4);
  not not_246 (not_246_out, OP3);
  not not_247 (not_247_out, OP2);
  not not_248 (not_248_out, OP1);
  not not_249 (not_249_out, OP0);
  not not_250 (not_250_out, F4);
  not not_251 (not_251_out, F3);
  not not_252 (not_252_out, F1);
  not not_253 (not_253_out, F0);
  not not_254 (not_254_out, OP5);
  not not_255 (not_255_out, OP4);
  not not_256 (not_256_out, OP3);
  not not_257 (not_257_out, OP2);
  not not_258 (not_258_out, OP1);
  not not_259 (not_259_out, OP0);
  not not_260 (not_260_out, F4);
  not not_261 (not_261_out, F3);
  not not_262 (not_262_out, F1);
  not not_263 (not_263_out, OP5);
  not not_264 (not_264_out, OP4);
  not not_265 (not_265_out, OP3);
  not not_266 (not_266_out, OP2);
  not not_267 (not_267_out, OP1);
  not not_268 (not_268_out, OP0);
  not not_269 (not_269_out, F4);
  not not_270 (not_270_out, F3);
  not not_271 (not_271_out, OP5);
  not not_272 (not_272_out, OP4);
  not not_273 (not_273_out, OP3);
  not not_274 (not_274_out, OP2);
  not not_275 (not_275_out, OP1);
  not not_276 (not_276_out, OP0);
  not not_277 (not_277_out, F4);
  not not_278 (not_278_out, F2);
  not not_279 (not_279_out, F0);
  not not_280 (not_280_out, OP5);
  not not_281 (not_281_out, OP4);
  not not_282 (not_282_out, OP3);
  not not_283 (not_283_out, OP2);
  not not_284 (not_284_out, OP1);
  not not_285 (not_285_out, OP0);
  not not_286 (not_286_out, F4);
  not not_287 (not_287_out, F2);
  not not_288 (not_288_out, OP5);
  not not_289 (not_289_out, OP4);
  not not_290 (not_290_out, OP3);
  not not_291 (not_291_out, OP2);
  not not_292 (not_292_out, OP1);
  not not_293 (not_293_out, OP0);
  not not_294 (not_294_out, F5);
  not not_295 (not_295_out, F4);
  not not_296 (not_296_out, F1);
  not not_297 (not_297_out, F0);
  not not_298 (not_298_out, OP5);
  not not_299 (not_299_out, OP4);
  not not_300 (not_300_out, OP3);
  not not_301 (not_301_out, OP1);
  not not_302 (not_302_out, OP0);
  not not_303 (not_303_out, OP5);
  not not_304 (not_304_out, OP4);
  not not_305 (not_305_out, OP3);
  not not_306 (not_306_out, OP1);
  not not_307 (not_307_out, OP4);
  not not_308 (not_308_out, OP2);
  not not_309 (not_309_out, OP5);
  not not_310 (not_310_out, OP4);
  not not_311 (not_311_out, OP3);
  not not_312 (not_312_out, OP2);
  not not_313 (not_313_out, OP1);
  not not_314 (not_314_out, OP0);
  not not_315 (not_315_out, F5);
  not not_316 (not_316_out, F4);
  not not_317 (not_317_out, F3);
  not not_318 (not_318_out, OP4);
  not not_319 (not_319_out, OP2);
  not not_320 (not_320_out, OP1);
  not not_321 (not_321_out, OP0);
  and and_1 (and_1_out, not_1_out, not_2_out, not_3_out, not_4_out, not_5_out, not_6_out, not_7_out, not_8_out, not_9_out, not_10_out, not_11_out, not_12_out);
  and and_2 (and_2_out, not_13_out, not_14_out, not_15_out, not_16_out, not_17_out, not_18_out, not_19_out, not_20_out, not_21_out, not_22_out, F1, F0);
  and and_3 (and_3_out, not_23_out, not_24_out, not_25_out, not_26_out, not_27_out, not_28_out, not_29_out, not_30_out, not_31_out, not_32_out, F1, not_33_out);
  and and_4 (and_4_out, not_34_out, not_35_out, not_36_out, not_37_out, not_38_out, not_39_out, F5, not_40_out, not_41_out, not_42_out, not_43_out, not_44_out);
  and and_5 (and_5_out, not_45_out, not_46_out, not_47_out, not_48_out, not_49_out, not_50_out, F5, not_51_out, not_52_out, not_53_out, not_54_out, F0);
  and and_6 (and_6_out, not_55_out, not_56_out, not_57_out, not_58_out, not_59_out, not_60_out, F5, not_61_out, not_62_out, not_63_out, F1, not_64_out);
  and and_7 (and_7_out, not_65_out, not_66_out, not_67_out, not_68_out, not_69_out, not_70_out, F5, not_71_out, not_72_out, F2, not_73_out, not_74_out);
  and and_8 (and_8_out, not_75_out, not_76_out, not_77_out, not_78_out, not_79_out, not_80_out, F5, not_81_out, not_82_out, F2, not_83_out, F0);
  and and_9 (and_9_out, not_84_out, not_85_out, not_86_out, not_87_out, not_88_out, not_89_out, F5, not_90_out, not_91_out, F2, F1, F0);
  and and_10 (and_10_out, not_92_out, not_93_out, not_94_out, not_95_out, not_96_out, not_97_out, F5, not_98_out, F3, not_99_out, F1, not_100_out);
  and and_11 (and_11_out, not_101_out, not_102_out, not_103_out, not_104_out, not_105_out, not_106_out, F5, not_107_out, F3, not_108_out, F1, F0);
  and and_12 (and_12_out, not_109_out, not_110_out, not_111_out, not_112_out, not_113_out, not_114_out, not_115_out, not_116_out, F3, not_117_out, not_118_out, not_119_out);
  and and_13 (and_13_out, not_120_out, not_121_out, not_122_out, not_123_out, not_124_out, not_125_out, not_126_out, not_127_out, F3, F2, not_128_out, not_129_out);
  and and_14 (and_14_out, not_130_out, not_131_out, not_132_out, OP2, not_133_out, not_134_out);
  and and_15 (and_15_out, not_135_out, not_136_out, not_137_out, OP2, not_138_out, OP0);
  and and_16 (and_16_out, not_139_out, not_140_out, OP3, not_141_out, not_142_out, not_143_out);
  and and_17 (and_17_out, not_144_out, not_145_out, OP3, OP2, not_146_out, not_147_out);
  and and_18 (and_18_out, not_148_out, not_149_out, OP3, not_150_out, not_151_out, OP0);
  and and_19 (and_19_out, not_152_out, not_153_out, OP3, not_154_out, OP1, not_155_out);
  and and_20 (and_20_out, not_156_out, not_157_out, OP3, OP2, not_158_out, OP0);
  and and_21 (and_21_out, OP5, not_159_out, not_160_out, not_161_out, OP1, OP0);
  and and_22 (and_22_out, OP5, not_162_out, OP3, not_163_out, OP1, OP0);
  and and_23 (and_23_out, not_164_out, not_165_out, not_166_out, not_167_out, not_168_out, not_169_out, not_170_out, not_171_out, not_172_out, F2, F1, F0);
  and and_24 (and_24_out, not_173_out, not_174_out, OP3, OP2, OP1, not_175_out);
  and and_25 (and_25_out, not_176_out, not_177_out, not_178_out, OP2, OP1, not_179_out);
  and and_26 (and_26_out, not_180_out, not_181_out, not_182_out, not_183_out, not_184_out, not_185_out, not_186_out, not_187_out, not_188_out, not_189_out, not_190_out, not_191_out);
  and and_27 (and_27_out, not_192_out, not_193_out, not_194_out, not_195_out, not_196_out, not_197_out, not_198_out, not_199_out, not_200_out, not_201_out, F1, F0);
  and and_28 (and_28_out, not_202_out, not_203_out, not_204_out, not_205_out, not_206_out, not_207_out, not_208_out, not_209_out, not_210_out, not_211_out, F1, not_212_out);
  and and_29 (and_29_out, not_213_out, not_214_out, not_215_out, not_216_out, not_217_out, not_218_out, F5, not_219_out, not_220_out, not_221_out, not_222_out, not_223_out);
  and and_30 (and_30_out, not_224_out, not_225_out, not_226_out, not_227_out, not_228_out, not_229_out, F5, not_230_out, not_231_out, not_232_out, not_233_out, F0);
  and and_31 (and_31_out, not_234_out, not_235_out, not_236_out, not_237_out, not_238_out, not_239_out, F5, not_240_out, not_241_out, not_242_out, F1, not_243_out);
  and and_32 (and_32_out, not_244_out, not_245_out, not_246_out, not_247_out, not_248_out, not_249_out, F5, not_250_out, not_251_out, F2, not_252_out, not_253_out);
  and and_33 (and_33_out, not_254_out, not_255_out, not_256_out, not_257_out, not_258_out, not_259_out, F5, not_260_out, not_261_out, F2, not_262_out, F0);
  and and_34 (and_34_out, not_263_out, not_264_out, not_265_out, not_266_out, not_267_out, not_268_out, F5, not_269_out, not_270_out, F2, F1, F0);
  and and_35 (and_35_out, not_271_out, not_272_out, not_273_out, not_274_out, not_275_out, not_276_out, F5, not_277_out, F3, not_278_out, F1, not_279_out);
  and and_36 (and_36_out, not_280_out, not_281_out, not_282_out, not_283_out, not_284_out, not_285_out, F5, not_286_out, F3, not_287_out, F1, F0);
  and and_37 (and_37_out, not_288_out, not_289_out, not_290_out, not_291_out, not_292_out, not_293_out, not_294_out, not_295_out, F3, F2, not_296_out, not_297_out);
  and and_38 (and_38_out, not_298_out, not_299_out, not_300_out, OP2, not_301_out, not_302_out);
  and and_39 (and_39_out, not_303_out, not_304_out, not_305_out, OP2, not_306_out, OP0);
  and and_40 (and_40_out, OP5, not_307_out, OP3, not_308_out, OP1, OP0);
  and and_41 (and_41_out, not_309_out, not_310_out, not_311_out, not_312_out, not_313_out, not_314_out, not_315_out, not_316_out, not_317_out, F2, F1, F0);
  and and_42 (and_42_out, OP5, not_318_out, OP3, not_319_out, not_320_out, not_321_out);
  or or_1 (R1_Used, and_1_out, and_2_out, and_3_out, and_4_out, and_5_out, and_6_out, and_7_out, and_8_out, and_9_out, and_10_out, and_11_out, and_12_out, and_13_out, and_14_out, and_15_out, and_16_out, and_17_out, and_18_out, and_19_out, and_20_out, and_21_out, and_22_out, and_23_out, and_24_out, and_25_out);
  or or_2 (R2_Used, and_26_out, and_27_out, and_28_out, and_29_out, and_30_out, and_31_out, and_32_out, and_33_out, and_34_out, and_35_out, and_36_out, and_37_out, and_38_out, and_39_out, and_40_out, and_41_out, and_42_out);
endmodule

module \数据相关检测  (
  input  [5:0] OP,
  input  [4:0] EX_WriteReg_num,
  input  EX_RegWrite,
  input  [4:0] MEM_WriteReg_num,
  input  MEM_RegWrite,
  input  [5:0] Func,
  input  [4:0] ID_R1_num,
  input  [4:0] ID_R2_num,
  output \数据相关 
);

  wire and_1_out, and_2_out, and_3_out, and_4_out, and_5_out, and_6_out, comparator_1_eq, comparator_2_eq,
       comparator_3_eq, comparator_4_eq, comparator_5_eq, comparator_6_eq, or_1_out, or_2_out, R1_Used,
       R2_Used;

  \源寄存器使用情况  \u_源寄存器使用情况_1  (
    .OP0(OP[0]), .OP1(OP[1]), .OP2(OP[2]), .OP3(OP[3]), .OP4(OP[4]), .OP5(OP[5]), .F0(Func[0]), .F1(Func[1]),
    .F2(Func[2]), .F3(Func[3]), .F4(Func[4]), .F5(Func[5]), .R1_Used(R1_Used), .R2_Used(R2_Used));
  Comparator #(.width(5)) comparator_1 (.a(ID_R1_num), .b({5{1'b0}}), .eq(comparator_1_eq));  // open: gt, lt
  and and_1 (and_1_out, EX_RegWrite, comparator_2_eq);
  Comparator #(.width(5)) comparator_2 (.a(EX_WriteReg_num), .b(ID_R1_num), .eq(comparator_2_eq));  // open: gt, lt
  Comparator #(.width(5)) comparator_3 (.a(MEM_WriteReg_num), .b(ID_R1_num), .eq(comparator_3_eq));  // open: gt, lt
  and and_2 (and_2_out, comparator_3_eq, MEM_RegWrite);
  and and_3 (and_3_out, EX_RegWrite, comparator_4_eq);
  Comparator #(.width(5)) comparator_4 (.a(EX_WriteReg_num), .b(ID_R2_num), .eq(comparator_4_eq));  // open: gt, lt
  Comparator #(.width(5)) comparator_5 (.a(MEM_WriteReg_num), .b(ID_R2_num), .eq(comparator_5_eq));  // open: gt, lt
  and and_4 (and_4_out, comparator_5_eq, MEM_RegWrite);
  Comparator #(.width(5)) comparator_6 (.a(ID_R2_num), .b({5{1'b0}}), .eq(comparator_6_eq));  // open: gt, lt
  or or_1 (or_1_out, and_1_out, and_2_out);
  or or_2 (or_2_out, and_3_out, and_4_out);
  and and_5 (and_5_out, ~comparator_1_eq, or_1_out, R1_Used);  // AND_Gate
  or or_3 (\数据相关 , and_5_out, and_6_out);
  and and_6 (and_6_out, R2_Used, or_2_out, ~comparator_6_eq);  // AND_Gate

  // Other names for the same wires on the sheet: OP_CODE[5:0] = OP
endmodule

module IF_ID (
  input  [31:0] IR,
  input  [31:0] PC,
  input  [1:0] forcast,
  input  CLK,
  input  RST,
  input  EN,
  output [31:0] IROUT,
  output [31:0] PCOUT,
  output [1:0] forcast_out
);

  wire EN_t;
  wire [1:0] multiplexer_3_out;
  wire [31:0] multiplexer_1_out, multiplexer_2_out;

  Multiplexer #(.width(32), .enable("false")) multiplexer_1 (
    .in0(IR), .in1({32{1'b0}}), .out(multiplexer_1_out), .sel(RST));
  Multiplexer #(.width(32), .enable("false")) multiplexer_2 (
    .in0(PC), .in1({32{1'b0}}), .out(multiplexer_2_out), .sel(RST));
  Multiplexer #(.width(2), .enable("false")) multiplexer_3 (
    .in0(forcast), .in1(2'b00), .out(multiplexer_3_out), .sel(RST));
  Register #(.width(32)) register_1 (.D(multiplexer_1_out), .en(EN_t), .Q(IROUT), .clk(CLK));  // open: clr
  Register #(.width(32)) register_2 (.D(multiplexer_2_out), .en(EN_t), .Q(PCOUT), .clk(CLK));  // open: clr
  Register #(.width(2)) register_3 (.D(multiplexer_3_out), .en(EN_t), .Q(forcast_out), .clk(CLK));  // open: clr
  not not_1 (EN_t, EN);
endmodule
module ID_EX (
  input  [31:0] IR,
  input  [31:0] PC,
  input  CLK,
  input  RST,
  input  EN,
  input  [31:0] R1,
  input  [31:0] R2,
  input  [1:0] forcast,
  input  Beq,
  input  JMP,
  input  JR,
  input  Bne,
  input  SignedExt,
  input  MemToReg,
  input  SRAV,
  input  MemWrite,
  input  BLEZ,
  input  [3:0] ALUop,
  input  SB,
  input  Alus,
  input  SysDin,
  input  RegWrite,
  input  JAL,
  input  RegDst,
  input  [1:0] forward1,
  input  [1:0] forward2,
  output [31:0] IRout,
  output [31:0] PCout,
  output [31:0] R1out,
  output [31:0] R2out,
  output JMP_out,
  output Beq_out,
  output JR_out,
  output Bne_out,
  output SignedExt_out,
  output MemToReg_out,
  output SRAV_out,
  output MemWrite_out,
  output BLEZ_out,
  output [3:0] Aluop_out,
  output SB_out,
  output Alus_out,
  output SysDout,
  output RegWrite_out,
  output JAL_out,
  output [1:0] forcast_out,
  output RegDst_out,
  output [1:0] f1out,
  output [1:0] f2out
);

  wire EN_t, multiplexer_5_out, multiplexer_6_out, multiplexer_7_out, multiplexer_8_out, multiplexer_9_out,
       multiplexer_10_out, multiplexer_11_out, multiplexer_12_out, multiplexer_13_out, multiplexer_14_out,
       multiplexer_16_out, multiplexer_17_out, multiplexer_18_out, multiplexer_19_out, multiplexer_20_out,
       undriven, undriven_2;
  wire [1:0] multiplexer_21_out, multiplexer_22_out, multiplexer_23_out;
  wire [3:0] multiplexer_15_out;
  wire [31:0] multiplexer_1_out, multiplexer_2_out, multiplexer_3_out, multiplexer_4_out;

  Multiplexer #(.width(32), .enable("false")) multiplexer_1 (
    .in0(IR), .in1({32{1'b0}}), .out(multiplexer_1_out), .sel(RST));
  Multiplexer #(.width(32), .enable("false")) multiplexer_2 (
    .in0(PC), .in1({32{1'b0}}), .out(multiplexer_2_out), .sel(RST));
  Multiplexer #(.width(32), .enable("false")) multiplexer_3 (
    .in0(R1), .in1({32{1'b0}}), .out(multiplexer_3_out), .sel(RST));
  Multiplexer #(.width(32), .enable("false")) multiplexer_4 (
    .in0(R2), .in1({32{1'b0}}), .out(multiplexer_4_out), .sel(RST));
  Multiplexer #(.enable("false")) multiplexer_5 (.in0(JMP), .in1(1'b0), .out(multiplexer_5_out), .sel(RST));
  Multiplexer #(.enable("false")) multiplexer_6 (.in0(JR), .in1(1'b0), .out(multiplexer_6_out), .sel(RST));
  Multiplexer #(.enable("false")) multiplexer_7 (.in0(SRAV), .in1(1'b0), .out(multiplexer_7_out), .sel(RST));
  Multiplexer #(.enable("false")) multiplexer_8 (.in0(BLEZ), .in1(1'b0), .out(multiplexer_8_out), .sel(RST));
  Multiplexer #(.enable("false")) multiplexer_9 (.in0(SignedExt), .in1(1'b0), .out(multiplexer_9_out), .sel(RST));
  Register #(.width(32)) register_1 (.D(multiplexer_1_out), .en(EN_t), .Q(IRout), .clk(CLK));  // open: clr
  Register #(.width(32)) register_2 (.D(multiplexer_2_out), .en(EN_t), .Q(PCout), .clk(CLK));  // open: clr
  Register #(.width(32)) register_3 (.D(multiplexer_3_out), .en(EN_t), .Q(R1out), .clk(CLK));  // open: clr
  Register #(.width(32)) register_4 (.D(multiplexer_4_out), .en(EN_t), .Q(R2out), .clk(CLK));  // open: clr
  Register #(.width(1)) register_5 (.D(multiplexer_5_out), .en(EN_t), .Q(JMP_out), .clk(CLK));  // open: clr
  Register #(.width(1)) register_6 (.D(multiplexer_6_out), .en(EN_t), .Q(JR_out), .clk(CLK));  // open: clr
  Register #(.width(1)) register_7 (.D(multiplexer_7_out), .en(EN_t), .Q(SRAV_out), .clk(CLK));  // open: clr
  Register #(.width(1)) register_8 (.D(multiplexer_8_out), .en(EN_t), .Q(BLEZ_out), .clk(CLK));  // open: clr
  Register #(.width(1)) register_9 (.D(multiplexer_9_out), .en(EN_t), .Q(SignedExt_out), .clk(CLK));  // open: clr
  not not_1 (EN_t, EN);
  Multiplexer #(.enable("false")) multiplexer_10 (.in0(SB), .in1(1'b0), .out(multiplexer_10_out), .sel(RST));
  Multiplexer #(.enable("false")) multiplexer_11 (.in0(Beq), .in1(1'b0), .out(multiplexer_11_out), .sel(RST));
  Multiplexer #(.enable("false")) multiplexer_12 (.in0(Bne), .in1(1'b0), .out(multiplexer_12_out), .sel(RST));
  Multiplexer #(.enable("false")) multiplexer_13 (.in0(MemToReg), .in1(1'b0), .out(multiplexer_13_out), .sel(RST));
  Multiplexer #(.enable("false")) multiplexer_14 (.in0(MemWrite), .in1(1'b0), .out(multiplexer_14_out), .sel(RST));
  Multiplexer #(.width(4), .enable("false")) multiplexer_15 (
    .in0(ALUop), .in1(4'b0000), .out(multiplexer_15_out), .sel(RST));
  Multiplexer #(.enable("false")) multiplexer_16 (.in0(Alus), .in1(1'b0), .out(multiplexer_16_out), .sel(RST));
  Multiplexer #(.enable("false")) multiplexer_17 (.in0(SysDin), .in1(1'b0), .out(multiplexer_17_out), .sel(RST));
  Register #(.width(1)) register_10 (.D(multiplexer_10_out), .en(EN_t), .Q(SB_out), .clk(CLK));  // open: clr
  Register #(.width(1)) register_11 (.D(multiplexer_11_out), .en(EN_t), .Q(Beq_out), .clk(CLK));  // open: clr
  Register #(.width(1)) register_12 (.D(multiplexer_12_out), .en(EN_t), .Q(Bne_out), .clk(CLK));  // open: clr
  Register #(.width(1)) register_13 (.D(multiplexer_13_out), .en(EN_t), .Q(MemToReg_out), .clk(CLK));  // open: clr
  Register #(.width(1)) register_14 (.D(multiplexer_14_out), .en(EN_t), .Q(MemWrite_out), .clk(CLK));  // open: clr
  Register #(.width(4)) register_15 (.D(multiplexer_15_out), .en(EN_t), .Q(Aluop_out), .clk(CLK));  // open: clr
  Register #(.width(1)) register_16 (.D(multiplexer_16_out), .en(EN_t), .Q(Alus_out), .clk(CLK), .clr(undriven));
  Register #(.width(1)) register_17 (.D(multiplexer_17_out), .en(EN_t), .Q(SysDout), .clk(CLK), .clr(undriven_2));
  Multiplexer #(.enable("false")) multiplexer_18 (.in0(RegWrite), .in1(1'b0), .out(multiplexer_18_out), .sel(RST));
  Multiplexer #(.enable("false")) multiplexer_19 (.in0(JAL), .in1(1'b0), .out(multiplexer_19_out), .sel(RST));
  Multiplexer #(.enable("false")) multiplexer_20 (.in0(RegDst), .in1(1'b0), .out(multiplexer_20_out), .sel(RST));
  Multiplexer #(.width(2), .enable("false")) multiplexer_21 (
    .in0(forward1), .in1(2'b00), .out(multiplexer_21_out), .sel(RST));
  Multiplexer #(.width(2), .enable("false")) multiplexer_22 (
    .in0(forward2), .in1(2'b00), .out(multiplexer_22_out), .sel(RST));
  Multiplexer #(.width(2), .enable("false")) multiplexer_23 (
    .in0(forcast), .in1(2'b00), .out(multiplexer_23_out), .sel(RST));
  Register #(.width(1)) register_18 (.D(multiplexer_18_out), .en(EN_t), .Q(RegWrite_out), .clk(CLK));  // open: clr
  Register #(.width(1)) register_19 (.D(multiplexer_19_out), .en(EN_t), .Q(JAL_out), .clk(CLK));  // open: clr
  Register #(.width(1)) register_20 (.D(multiplexer_20_out), .en(EN_t), .Q(RegDst_out), .clk(CLK));  // open: clr
  Register #(.width(2)) register_21 (.D(multiplexer_21_out), .en(EN_t), .Q(f1out), .clk(CLK));  // open: clr
  Register #(.width(2)) register_22 (.D(multiplexer_22_out), .en(EN_t), .Q(f2out), .clk(CLK));  // open: clr
  Register #(.width(2)) register_23 (.D(multiplexer_23_out), .en(EN_t), .Q(forcast_out), .clk(CLK));  // open: clr
endmodule

module EX_MEM (
  input  CLK,
  input  [31:0] IR,
  input  [31:0] PC,
  input  RST,
  input  EN,
  input  [31:0] result,
  input  [31:0] R2,
  input  MemToReg,
  input  RegDst,
  input  JAL,
  input  BLEZ,
  input  SRAV,
  input  RegWrite,
  input  MemWrite,
  input  sys,
  input  SB,
  output [31:0] IRout,
  output [31:0] PCout,
  output [31:0] resultout,
  output [31:0] R2out,
  output MemToRegout,
  output RegDstout,
  output JALout,
  output BLEZ_2,
  output SRAVout,
  output RegWrite_2,
  output MemWriteOut,
  output sysout,
  output SBout
);

  wire EN_t, multiplexer_3_out, multiplexer_4_out, multiplexer_5_out, multiplexer_6_out, multiplexer_8_out,
       multiplexer_9_out, multiplexer_11_out, multiplexer_12_out, multiplexer_13_out;
  wire [31:0] multiplexer_1_out, multiplexer_2_out, multiplexer_7_out, multiplexer_10_out;

  Multiplexer #(.width(32), .enable("false")) multiplexer_1 (
    .in0(IR), .in1({32{1'b0}}), .out(multiplexer_1_out), .sel(RST));
  Multiplexer #(.width(32), .enable("false")) multiplexer_2 (
    .in0(PC), .in1({32{1'b0}}), .out(multiplexer_2_out), .sel(RST));
  Multiplexer #(.enable("false")) multiplexer_3 (.in0(MemWrite), .in1(1'b0), .out(multiplexer_3_out), .sel(RST));
  Multiplexer #(.enable("false")) multiplexer_4 (.in0(SB), .in1(1'b0), .out(multiplexer_4_out), .sel(RST));
  Register #(.width(32)) register_1 (.D(multiplexer_1_out), .en(EN_t), .Q(IRout), .clk(CLK));  // open: clr
  Register #(.width(32)) register_2 (.D(multiplexer_2_out), .en(EN_t), .Q(PCout), .clk(CLK));  // open: clr
  Register #(.width(1)) register_3 (.D(multiplexer_3_out), .en(EN_t), .Q(MemWriteOut), .clk(CLK));  // open: clr
  Register #(.width(1)) register_4 (.D(multiplexer_4_out), .en(EN_t), .Q(SBout), .clk(CLK));  // open: clr
  not not_1 (EN_t, EN);
  Multiplexer #(.enable("false")) multiplexer_5 (.in0(MemToReg), .in1(1'b0), .out(multiplexer_5_out), .sel(RST));
  Multiplexer #(.enable("false")) multiplexer_6 (.in0(RegDst), .in1(1'b0), .out(multiplexer_6_out), .sel(RST));
  Multiplexer #(.width(32), .enable("false")) multiplexer_7 (
    .in0(result), .in1({32{1'b0}}), .out(multiplexer_7_out), .sel(RST));
  Register #(.width(1)) register_5 (.D(multiplexer_5_out), .en(EN_t), .Q(MemToRegout), .clk(CLK));  // open: clr
  Register #(.width(1)) register_6 (.D(multiplexer_6_out), .en(EN_t), .Q(RegDstout), .clk(CLK));  // open: clr
  Register #(.width(32)) register_7 (.D(multiplexer_7_out), .en(EN_t), .Q(resultout), .clk(CLK));  // open: clr
  Multiplexer #(.enable("false")) multiplexer_8 (.in0(JAL), .in1(1'b0), .out(multiplexer_8_out), .sel(RST));
  Multiplexer #(.enable("false")) multiplexer_9 (.in0(BLEZ), .in1(1'b0), .out(multiplexer_9_out), .sel(RST));
  Multiplexer #(.width(32), .enable("false")) multiplexer_10 (
    .in0(R2), .in1({32{1'b0}}), .out(multiplexer_10_out), .sel(RST));
  Register #(.width(1)) register_8 (.D(multiplexer_8_out), .en(EN_t), .Q(JALout), .clk(CLK));  // open: clr
  Register #(.width(1)) register_9 (.D(multiplexer_9_out), .en(EN_t), .Q(BLEZ_2), .clk(CLK));  // open: clr
  Register #(.width(32)) register_10 (.D(multiplexer_10_out), .en(EN_t), .Q(R2out), .clk(CLK));  // open: clr
  Multiplexer #(.enable("false")) multiplexer_11 (.in0(SRAV), .in1(1'b0), .out(multiplexer_11_out), .sel(RST));
  Multiplexer #(.enable("false")) multiplexer_12 (.in0(RegWrite), .in1(1'b0), .out(multiplexer_12_out), .sel(RST));
  Multiplexer #(.enable("false")) multiplexer_13 (.in0(sys), .in1(1'b0), .out(multiplexer_13_out), .sel(RST));
  Register #(.width(1)) register_11 (.D(multiplexer_11_out), .en(EN_t), .Q(SRAVout), .clk(CLK));  // open: clr
  Register #(.width(1)) register_12 (.D(multiplexer_12_out), .en(EN_t), .Q(RegWrite_2), .clk(CLK));  // open: clr
  Register #(.width(1)) register_13 (.D(multiplexer_13_out), .en(EN_t), .Q(sysout), .clk(CLK));  // open: clr

  // Other names for the same wires on the sheet: BLEZout = BLEZ_2; RegWriteout = RegWrite_2
endmodule

module MEM_WB (
  input  CLK,
  input  [31:0] IR,
  input  [31:0] PC,
  input  RST,
  input  EN,
  input  [31:0] result,
  input  [31:0] MemData,
  input  MemToReg,
  input  RegDst,
  input  JAL,
  input  BLEZ,
  input  SRAV,
  input  RegWrite,
  input  sys,
  output [31:0] IRout,
  output [31:0] PCout,
  output [31:0] MemDataout,
  output [31:0] resultout,
  output MemToRegout,
  output RegDstout,
  output JALout,
  output BLEZ_2,
  output SRAVout,
  output RegWrite_2,
  output sysout
);

  wire EN_t, multiplexer_3_out, multiplexer_4_out, multiplexer_6_out, multiplexer_7_out, multiplexer_9_out,
       multiplexer_10_out, multiplexer_11_out;
  wire [31:0] multiplexer_1_out, multiplexer_2_out, multiplexer_5_out, multiplexer_8_out;

  Multiplexer #(.width(32), .enable("false")) multiplexer_1 (
    .in0(IR), .in1({32{1'b0}}), .out(multiplexer_1_out), .sel(RST));
  Multiplexer #(.width(32), .enable("false")) multiplexer_2 (
    .in0(PC), .in1({32{1'b0}}), .out(multiplexer_2_out), .sel(RST));
  Register #(.width(32)) register_1 (.D(multiplexer_1_out), .en(EN_t), .Q(IRout), .clk(CLK));  // open: clr
  Register #(.width(32)) register_2 (.D(multiplexer_2_out), .en(EN_t), .Q(PCout), .clk(CLK));  // open: clr
  not not_1 (EN_t, EN);
  Multiplexer #(.enable("false")) multiplexer_3 (.in0(MemToReg), .in1(1'b0), .out(multiplexer_3_out), .sel(RST));
  Multiplexer #(.enable("false")) multiplexer_4 (.in0(RegDst), .in1(1'b0), .out(multiplexer_4_out), .sel(RST));
  Multiplexer #(.width(32), .enable("false")) multiplexer_5 (
    .in0(result), .in1({32{1'b0}}), .out(multiplexer_5_out), .sel(RST));
  Register #(.width(1)) register_3 (.D(multiplexer_3_out), .en(EN_t), .Q(MemToRegout), .clk(CLK));  // open: clr
  Register #(.width(1)) register_4 (.D(multiplexer_4_out), .en(EN_t), .Q(RegDstout), .clk(CLK));  // open: clr
  Register #(.width(32)) register_5 (.D(multiplexer_5_out), .en(EN_t), .Q(resultout), .clk(CLK));  // open: clr
  Multiplexer #(.enable("false")) multiplexer_6 (.in0(JAL), .in1(1'b0), .out(multiplexer_6_out), .sel(RST));
  Multiplexer #(.enable("false")) multiplexer_7 (.in0(BLEZ), .in1(1'b0), .out(multiplexer_7_out), .sel(RST));
  Multiplexer #(.width(32), .enable("false")) multiplexer_8 (
    .in0(MemData), .in1({32{1'b0}}), .out(multiplexer_8_out), .sel(RST));
  Register #(.width(1)) register_6 (.D(multiplexer_6_out), .en(EN_t), .Q(JALout), .clk(CLK));  // open: clr
  Register #(.width(1)) register_7 (.D(multiplexer_7_out), .en(EN_t), .Q(BLEZ_2), .clk(CLK));  // open: clr
  Register #(.width(32)) register_8 (.D(multiplexer_8_out), .en(EN_t), .Q(MemDataout), .clk(CLK));  // open: clr
  Multiplexer #(.enable("false")) multiplexer_9 (.in0(SRAV), .in1(1'b0), .out(multiplexer_9_out), .sel(RST));
  Multiplexer #(.enable("false")) multiplexer_10 (.in0(RegWrite), .in1(1'b0), .out(multiplexer_10_out), .sel(RST));
  Multiplexer #(.enable("false")) multiplexer_11 (.in0(sys), .in1(1'b0), .out(multiplexer_11_out), .sel(RST));
  Register #(.width(1)) register_9 (.D(multiplexer_9_out), .en(EN_t), .Q(SRAVout), .clk(CLK));  // open: clr
  Register #(.width(1)) register_10 (.D(multiplexer_10_out), .en(EN_t), .Q(RegWrite_2), .clk(CLK));  // open: clr
  Register #(.width(1)) register_11 (.D(multiplexer_11_out), .en(EN_t), .Q(sysout), .clk(CLK));  // open: clr

  // Other names for the same wires on the sheet: BLEZout = BLEZ_2; RegWriteout = RegWrite_2
endmodule

module \分支相关流水线  (
  output [31:0] out_1,
  output [31:0] out_2,
  output [31:0] out_3
);

  wire Alus, AlusEx, and_1_out, and_6_out, and_7_out, and_8_out, and_9_out, Beq, BeqEx, BLEZ, BLEZEx, BLEZM,
       BLEZWB, Bne, BneEx, branch, CLK, comparator_1_eq, comparator_2_eq, comparator_3_gt, comparator_4_eq,
       condi, d_ff_1_q, equ, Go, halt, IR1, IR2, IR3, JAL, JALEx, JALM, JALWB, JMP, JMPEx, JR, JREx, led,
       MemToReg, MemToRegEx, MemToRegM, MemToRegWB, MemWrite, MemWriteEx, MemWriteM, nor_1_out, not_1_out,
       not_2_out, or_1_out, or_2_out, or_3_out, pause, pcen, RegDst, RegDstEx, RegDstM, RegDstWB, RegWrite,
       RegWriteEx, RegWriteM, RegWriteWB, RST, SB, SBEx, SBM, SignedExt, SignedExtEx, SRAV, SRAVEx, SRAVM,
       SRAVWB, Sys, SysID, SysIDEx, SysM, SysWB, W1, W2, W3;
  wire [1:1] PCSrc;
  wire [3:0] Aluop, AluopEx, multiplexer_8_out, multiplexer_10_out;
  wire [4:0] multiplexer_6_out, R1_num, R2_num, W_num;
  wire [15:0] BranchNum, \LoadUse次数 , \总周期数 , \插入气泡数 , \无条件分支数 , \条件分支成功数 ;
  wire [31:0] adder_2_out, bit_extender_1_out, bit_extender_2_out, bit_extender_3_out, bit_extender_4_out,
       Din, EX_PC, Ext, ExtEX, FinalMemData, ID_PC, IF_PC, IREX, IRM, IRWB, JALWBD, LedData, MEM_PC, MemData,
       MemDataWB, multiplexer_5_out, multiplexer_9_out, multiplexer_13_out, pc0, pc1, pc2, PCWB, R1ID, R2EX,
       R2ID, R2M, result, resultM, resultWB, shifter_1_out, shifter_2_out, shifter_3_out, shifter_4_out;

  Button \u_总复位  (.out(RST));
  Button _1 (.out(IR1));
  Button _2 (.out(IR2));
  Button _3 (.out(IR3));
  Button \u_继续运行  (.out(Go));
  LED led_1 (.in(W1));
  LED led_2 (.in(W2));
  LED led_3 (.in(W3));
  and and_1 (and_1_out, ~SysWB, Go);  // AND_Gate
  Multiplexer #(.select(2), .width(32), .enable("false")) multiplexer_1 (
    .in0(pc0), .in1(pc1), .in2(pc2), .in3({pc0[31:28], IREX[25:0], 2'b00}), .out(out_2),
    .sel({PCSrc[1], JMPEx}));
  Hex_Digit_Display hex_digit_display_1 (.value(LedData[31:28]));  // open: dp
  not not_1 (not_1_out, d_ff_1_q);
  D_Flip_Flop d_ff_1 (.clk(CLK), .D(and_1_out), .Q(d_ff_1_q), .reset(RST));  // open: Qn, preset, en
  or or_1 (or_1_out, SysWB, pause);
  Hex_Digit_Display hex_digit_display_2 (.value(LedData[23:20]));  // open: dp
  Hex_Digit_Display hex_digit_display_3 (.value(LedData[27:24]));  // open: dp
  xor xor_1 (pcen, not_1_out, or_1_out);
  Register #(.width(32)) PC (.D(out_2), .en(pcen), .Q(IF_PC), .clk(CLK), .clr(RST));
  assign bit_extender_1_out = {{16{1'b0}}, out_3[15:0]};  // Bit_Extender bit_extender_1
  assign bit_extender_2_out = {{16{out_3[15]}}, out_3[15:0]};  // Bit_Extender bit_extender_2
  Adder #(.width(32)) adder_1 (.a(IF_PC), .b(32'h4), .out(pc0));  // open: cin, cout
  Hex_Digit_Display hex_digit_display_4 (.value(LedData[15:12]));  // open: dp
  Hex_Digit_Display hex_digit_display_5 (.value(LedData[19:16]));  // open: dp
  Multiplexer #(.width(32), .enable("false")) multiplexer_2 (
    .in0(bit_extender_1_out), .in1(bit_extender_2_out), .out(Ext), .sel(SignedExt));
  Hex_Digit_Display hex_digit_display_6 (.value(LedData[11:8]));  // open: dp
  Hex_Digit_Display hex_digit_display_7 (.value(LedData[7:4]));  // open: dp
  Clock clock_1 (.out(CLK));
  Hex_Digit_Display hex_digit_display_8 (.value(LedData[3:0]));  // open: dp
  and and_2 (SysID, Sys, halt);
  ROM #(.addrWidth(10), .dataWidth(32)) rom_1 (.addr(IF_PC[11:2]), .data(out_1));  // open: sel
  // Probe on \总周期数 
  // Probe on \无条件分支数 
  // Probe on \条件分支成功数 
  // Probe on \插入气泡数 
  // Probe on \LoadUse次数 
  or or_2 (or_2_out, RST, branch);
  IF_ID if_id_1 (
    .IR(out_1), .PC(IF_PC), .CLK(CLK), .RST(or_2_out), .EN(SysID), .IROUT(out_3), .PCOUT(ID_PC));  // open: forcast, forcast_out
  // Probe on IF_PC[11:0]
  // Probe on ID_PC[11:0]
  // Probe on MEM_PC[11:0]
  // Probe on EX_PC[11:0]
  \硬布线控制器  \u_硬布线控制器_1  (
    .Func(out_3[5:0]), .OP(out_3[31:26]), .ALU_OP(Aluop), .MemToReg(MemToReg), .MemWrite(MemWrite),
    .ALU_SRC(Alus), .RegWrite(RegWrite), .SysCALL(Sys), .SignedExt(SignedExt), .RegDst(RegDst), .JR(JR),
    .JMP(JMP), .Beq(Beq), .JAL(JAL), .Bne(Bne), .SRAV(SRAV), .BLEZ(BLEZ), .SB(SB));  // open: MFC0, ERET
  MIPS_Regifile mips_regifile_1 (
    .Din(Din), .Clk(CLK), .R1(R1ID), .R2(R2ID), .WE(RegWriteWB), .W_num(W_num), .R1_num(R1_num),
    .R2_num(R2_num));
  Multiplexer #(.width(5), .enable("false")) multiplexer_3 (
    .in0(out_3[25:21]), .in1(5'b00010), .out(R1_num), .sel(Sys));
  Multiplexer #(.width(5), .enable("false")) multiplexer_4 (
    .in0(out_3[20:16]), .in1(5'b00100), .out(R2_num), .sel(Sys));
  Comparator #(.width(32)) comparator_1 (.a(R1ID), .b(32'h22), .eq(comparator_1_eq));  // open: gt, lt
  Comparator #(.width(32)) comparator_2 (.a(R1ID), .b(32'ha), .eq(comparator_2_eq));  // open: gt, lt
  // Probe on PCWB[11:0]
  and and_3 (led, comparator_1_eq, Sys);
  and and_4 (halt, Sys, comparator_2_eq);
  nor nor_1 (nor_1_out, halt, led);
  and and_5 (pause, nor_1_out, Sys);
  Counter #(.width(16), .max('hffff)) counter_1 (
    .count(JMPEx), .Q(\无条件分支数 ), .clk(CLK), .clr(RST));  // open: load, D, carry
  Counter #(.width(16), .max('hffff)) counter_2 (
    .count(condi), .Q(\条件分支成功数 ), .clk(CLK), .clr(RST));  // open: load, D, carry
  not not_2 (not_2_out, SysWB);
  Counter #(.width(16), .max('hffff)) counter_3 (
    .count(not_2_out), .Q(\总周期数 ), .clk(CLK), .clr(RST));  // open: load, D, carry
  Counter #(.width(16), .max('hffff)) counter_4 (
    .count(branch), .Q(BranchNum), .clk(CLK), .clr(RST));  // open: load, D, carry
  or or_3 (or_3_out, RST, branch);
  ID_EX id_ex_1 (
    .IR(out_3), .PC(ID_PC), .CLK(CLK), .RST(or_3_out), .EN(SysIDEx), .R1(R1ID), .R2(R2ID), .Beq(Beq),
    .JMP(JMP), .JR(JR), .Bne(Bne), .MemToReg(MemToReg), .SRAV(SRAV), .MemWrite(MemWrite), .BLEZ(BLEZ),
    .ALUop(Aluop), .SB(SB), .Alus(Alus), .RegWrite(RegWrite), .JAL(JAL), .RegDst(RegDst), .IRout(IREX),
    .PCout(EX_PC), .R1out(pc1), .R2out(R2EX), .JMP_out(JMPEx), .Beq_out(BeqEx), .JR_out(JREx),
    .Bne_out(BneEx), .MemToReg_out(MemToRegEx), .SRAV_out(SRAVEx), .MemWrite_out(MemWriteEx),
    .BLEZ_out(BLEZEx), .Aluop_out(AluopEx), .SB_out(SBEx), .Alus_out(AlusEx), .RegWrite_out(RegWriteEx),
    .JAL_out(JALEx), .RegDst_out(RegDstEx), .SignedExt(SignedExt), .SignedExt_out(SignedExtEx),
    .SysDin(SysID), .SysDout(SysIDEx));  // open: forward1, f1out, forward2, f2out, forcast, forcast_out
  Multiplexer #(.width(32), .enable("false")) multiplexer_5 (
    .in0(R2EX), .in1(ExtEX), .out(multiplexer_5_out), .sel(AlusEx));
  Multiplexer #(.width(5), .enable("false")) multiplexer_6 (
    .in0(IREX[10:6]), .in1(pc1[4:0]), .out(multiplexer_6_out), .sel(SRAVEx));
  Comparator #(.width(32)) comparator_3 (.a(pc1), .b({32{1'b0}}), .gt(comparator_3_gt));  // open: eq, lt
  or or_4 (PCSrc[1], condi, and_6_out);
  and and_6 (and_6_out, JMPEx, ~JREx);  // AND_Gate
  Comparator #(.width(32)) comparator_4 (.a(pc1), .b(32'h22), .eq(comparator_4_eq));  // open: gt, lt
  or or_5 (branch, JMPEx, condi);
  MIPS_ALU mips_alu_1 (
    .X(pc1), .Y(multiplexer_5_out), .AluOP(AluopEx), .Equal(equ), .Result(result), .shamt(multiplexer_6_out));  // open: Result_2
  and and_7 (and_7_out, BeqEx, equ);
  and and_8 (and_8_out, BneEx, ~equ);  // AND_Gate
  and and_9 (and_9_out, BLEZEx, ~comparator_3_gt);  // AND_Gate
  Register #(.width(32)) register_1 (.D(R2EX), .en(comparator_4_eq), .Q(LedData), .clk(CLK), .clr(RST));
  or or_6 (condi, and_7_out, and_8_out, and_9_out);
  Adder #(.width(32)) adder_2 (.a(EX_PC), .b(32'h4), .out(adder_2_out));  // open: cin, cout
  Shifter #(.width(32)) shifter_1 (.in(ExtEX), .\dist (5'b00010), .out(shifter_1_out));
  assign bit_extender_3_out = {{16{1'b0}}, IREX[15:0]};  // Bit_Extender bit_extender_3
  Multiplexer #(.width(32), .enable("false")) multiplexer_7 (
    .in0(bit_extender_3_out), .in1(bit_extender_4_out), .out(ExtEX), .sel(SignedExtEx));
  assign bit_extender_4_out = {{16{IREX[15]}}, IREX[15:0]};  // Bit_Extender bit_extender_4
  EX_MEM ex_mem_1 (
    .CLK(CLK), .IR(IREX), .PC(EX_PC), .RST(RST), .EN(SysM), .result(result), .R2(R2EX),
    .MemToReg(MemToRegEx), .RegDst(RegDstEx), .JAL(JALEx), .BLEZ(BLEZEx), .SRAV(SRAVEx),
    .RegWrite(RegWriteEx), .MemWrite(MemWriteEx), .sys(SysIDEx), .IRout(IRM), .PCout(MEM_PC),
    .resultout(resultM), .R2out(R2M), .MemToRegout(MemToRegM), .RegDstout(RegDstM), .JALout(JALM),
    .BLEZ_2(BLEZM), .SRAVout(SRAVM), .RegWrite_2(RegWriteM), .MemWriteOut(MemWriteM), .sysout(SysM),
    .SB(SBEx), .SBout(SBM));
  Adder #(.width(32)) adder_3 (.a(adder_2_out), .b(shifter_1_out), .out(pc2));  // open: cin, cout
  Shifter #(.width(32)) shifter_2 (.in(R2M), .\dist (5'b01000), .out(shifter_2_out));
  Shifter #(.width(32)) shifter_3 (.in(R2M), .\dist (5'b10000), .out(shifter_3_out));
  Shifter #(.width(32)) shifter_4 (.in(R2M), .\dist (5'b11000), .out(shifter_4_out));
  Multiplexer #(.select(2), .width(4), .enable("false")) multiplexer_8 (
    .in0(4'b0001), .in1(4'b0010), .in2(4'b0100), .in3(4'b1000), .out(multiplexer_8_out), .sel(resultM[1:0]));
  Multiplexer #(.select(2), .width(32), .enable("false")) multiplexer_9 (
    .in0(R2M), .in1(shifter_2_out), .in2(shifter_3_out), .in3(shifter_4_out), .out(multiplexer_9_out),
    .sel(resultM[1:0]));
  Multiplexer #(.width(4), .enable("false")) multiplexer_10 (
    .in0(4'b1111), .in1(multiplexer_8_out), .out(multiplexer_10_out), .sel(SBM));
  // MIPS_RAM mips_ram_1: pin names not known; wires that end beside it: {{10{1'b0}}, resultM[11:2]}, FinalMemData, MemWriteM, multiplexer_10_out, CLK, RST, MemData
  Multiplexer #(.width(32), .enable("false")) multiplexer_11 (
    .in0(R2M), .in1(multiplexer_9_out), .out(FinalMemData), .sel(SB));
  MEM_WB mem_wb_1 (
    .CLK(CLK), .IR(IRM), .PC(MEM_PC), .RST(RST), .EN(SysWB), .result(resultM), .MemData(MemData),
    .MemToReg(MemToRegM), .RegDst(RegDstM), .JAL(JALM), .BLEZ(BLEZM), .SRAV(SRAVM), .RegWrite(RegWriteM),
    .sys(SysM), .IRout(IRWB), .PCout(PCWB), .MemDataout(MemDataWB), .resultout(resultWB),
    .MemToRegout(MemToRegWB), .RegDstout(RegDstWB), .JALout(JALWB), .BLEZ_2(BLEZWB), .SRAVout(SRAVWB),
    .RegWrite_2(RegWriteWB), .sysout(SysWB));
  Multiplexer #(.select(2), .width(5), .enable("false")) multiplexer_12 (
    .in0(IRWB[20:16]), .in1(IRWB[15:11]), .in2({5{1'b1}}), .in3({5{1'b1}}), .out(W_num),
    .sel({JALWB, RegDstWB}));
  Adder #(.width(32)) adder_4 (.a(PCWB), .b(32'h4), .out(JALWBD));  // open: cin, cout
  Multiplexer #(.width(32), .enable("false")) multiplexer_13 (
    .in0(resultWB), .in1(MemDataWB), .out(multiplexer_13_out), .sel(MemToRegWB));
  Multiplexer #(.width(32), .enable("false")) multiplexer_14 (
    .in0(multiplexer_13_out), .in1(JALWBD), .out(Din), .sel(JALWB));
  MIPS_ALU mips_alu_2 ();  // open: X, Y, AluOP, Equal, Result, Result_2, shamt

  // Other names for the same wires on the sheet: IRID[31:0] = out_3; pc3[31:2] = {pc0[31:28], IREX[25:0]};
  //   R1EX[31:0] = pc1; PCEX[31:0] = EX_PC; PCID[31:0] = ID_PC; PCIF[31:0] = IF_PC; PCM[31:0] = MEM_PC;
  //   PCSrc[0] = JMPEx; WB_PC[31:0] = PCWB

  // Notes on the sheet:
  //   中断源
  //   中断等待指示
  //   pcout
  //   数码管输出
  //   irout
  //   contents of rom_1 (hex, n*v repeats v):
  //   20110020 20020022 8000c06 20110000 20110000 2002000a 10000003 20110000 20110000 2002000a 14110003
  //   20110000 20110000 2002000a c000c14 2002000a 0 0 0 c 2231ffff 0 0 0 112020 0 0 0 c 1620fff6 3e00008
  //   JMP
  //   JR
  //   OP
  //   Func
  //   流水调试日志用
  //   Beq
  //   Bne
  //   MemToReg
  //   MemWrite
  //   AluOP
  //   AluSrcB
  //   RegWrite
  //   JAL
  //   RegDst
  //   Syscall
endmodule

module \气泡流水线  (
  output [31:0] out_1,
  output [31:0] out_2,
  output [31:0] out_3,
  output [1:0] out_4,
  output [31:0] out_5
);

  wire Alus, AlusEx, and_1_out, and_2_out, and_6_out, and_7_out, and_8_out, and_9_out, Beq, BeqEx, BLEZ,
       BLEZEx, BLEZM, BLEZWB, Bne, BneEx, branch, CLK, comparator_1_eq, comparator_2_eq, comparator_3_gt,
       comparator_4_eq, condi, dataConf, equ, Go, halt, IR1, IR2, IR3, JAL, JALEx, JALM, JALWB, JMP, JMPEx,
       JR, JREx, led, MemToReg, MemToRegEx, MemToRegM, MemToRegWB, MemWrite, MemWriteEx, MemWriteM,
       nor_1_out, not_2_out, or_2_out, or_3_out, or_4_out, pause, pcen, RegDst, RegDstEx, RegDstM, RegDstWB,
       RegWrite, RegWriteEx, RegWriteM, RegWriteWB, RST, SB, SBEx, SBM, SignedExt, SignedExtEx, SRAV, SRAVEx,
       SRAVM, SRAVWB, Sys, SysEx, SysFinal, SysI, SysM, SysWB, W1, W2, W3;
  wire [1:1] PCSrc;
  wire [3:0] Aluop, AluopEx, multiplexer_8_out, multiplexer_10_out;
  wire [4:0] multiplexer_6_out, R1_num, R2_num, W_EX, W_M, W_WB;
  wire [15:0] \LoadUse次数 , \总周期数 , \插入气泡数 , \无条件分支数 , \条件分支成功数 ;
  wire [31:0] adder_2_out, bit_extender_1_out, bit_extender_2_out, bit_extender_3_out, bit_extender_4_out,
       Din, EX_PC, Ext, ExtEX, ID_PC, IF_PC, IREX, IRM, IRWB, JALWBD, LedData, MEM_PC, MemData, MemDataWB,
       multiplexer_5_out, multiplexer_9_out, multiplexer_15_out, pc0, pc1, pc2, PCWB, R1ID, R2EX, R2ID, R2M,
       result, resultWB, shifter_1_out, shifter_2_out, shifter_3_out, shifter_4_out;
  wire [31:2] resultM;

  Button \u_总复位  (.out(RST));
  Button _1 (.out(IR1));
  Button _2 (.out(IR2));
  Button _3 (.out(IR3));
  Button \u_继续运行  (.out(Go));
  LED led_1 (.in(W1));
  LED led_2 (.in(W2));
  LED led_3 (.in(W3));
  and and_1 (and_1_out, Sys, halt);
  and and_2 (and_2_out, Sys, ~Go, pause);  // AND_Gate
  Multiplexer #(.select(2), .width(32), .enable("false")) multiplexer_1 (
    .in0(pc0), .in1(pc1), .in2(pc2), .in3({pc0[31:28], IREX[25:0], 2'b00}), .out(out_2),
    .sel({PCSrc[1], JMPEx}));
  Hex_Digit_Display hex_digit_display_1 (.value(LedData[31:28]));  // open: dp
  or or_1 (SysI, and_1_out, and_2_out);
  Hex_Digit_Display hex_digit_display_2 (.value(LedData[23:20]));  // open: dp
  Hex_Digit_Display hex_digit_display_3 (.value(LedData[27:24]));  // open: dp
  Register #(.width(32)) PC (.D(out_2), .en(pcen), .Q(IF_PC), .clk(CLK), .clr(RST));
  assign bit_extender_1_out = {{16{1'b0}}, out_3[15:0]};  // Bit_Extender bit_extender_1
  assign bit_extender_2_out = {{16{out_3[15]}}, out_3[15:0]};  // Bit_Extender bit_extender_2
  Adder #(.width(32)) adder_1 (.a(IF_PC), .b(32'h4), .out(pc0));  // open: cin, cout
  Hex_Digit_Display hex_digit_display_4 (.value(LedData[15:12]));  // open: dp
  Hex_Digit_Display hex_digit_display_5 (.value(LedData[19:16]));  // open: dp
  \数据相关检测  \u_数据相关检测_1  (
    .OP(out_3[31:26]), .EX_WriteReg_num(W_EX), .EX_RegWrite(RegWriteEx), .MEM_WriteReg_num(W_M),
    .MEM_RegWrite(RegWriteM), .\数据相关 (dataConf), .Func(out_3[5:0]), .ID_R1_num(R1_num), .ID_R2_num(R2_num));
  Multiplexer #(.width(32), .enable("false")) multiplexer_2 (
    .in0(bit_extender_1_out), .in1(bit_extender_2_out), .out(Ext), .sel(SignedExt));
  Hex_Digit_Display hex_digit_display_6 (.value(LedData[7:4]));  // open: dp
  Hex_Digit_Display hex_digit_display_7 (.value(LedData[11:8]));  // open: dp
  Clock clock_1 (.out(CLK));
  Hex_Digit_Display hex_digit_display_8 (.value(LedData[3:0]));  // open: dp
  or or_2 (or_2_out, SysI, dataConf);
  not not_1 (pcen, or_2_out);
  ROM #(.addrWidth(10), .dataWidth(32)) rom_1 (.addr(IF_PC[11:2]), .data(out_1));  // open: sel
  // Probe on \总周期数 
  // Probe on \无条件分支数 
  // Probe on \条件分支成功数 
  // Probe on \插入气泡数 
  // Probe on \LoadUse次数 
  or or_3 (or_3_out, RST, branch);
  IF_ID if_id_1 (
    .IR(out_1), .PC(IF_PC), .CLK(CLK), .RST(or_3_out), .EN(or_2_out), .IROUT(out_3), .PCOUT(ID_PC));  // open: forcast, forcast_out
  // Probe on IF_PC[11:0]
  // Probe on ID_PC[11:0]
  // Probe on EX_PC[11:0]
  // Probe on MEM_PC[11:0]
  \硬布线控制器  \u_硬布线控制器_1  (
    .Func(out_3[5:0]), .OP(out_3[31:26]), .ALU_OP(Aluop), .MemToReg(MemToReg), .MemWrite(MemWrite),
    .ALU_SRC(Alus), .RegWrite(RegWrite), .SysCALL(Sys), .SignedExt(SignedExt), .RegDst(RegDst), .JR(JR),
    .JMP(JMP), .Beq(Beq), .JAL(JAL), .Bne(Bne), .SRAV(SRAV), .BLEZ(BLEZ), .SB(SB));  // open: MFC0, ERET
  MIPS_Regifile mips_regifile_1 (
    .Din(Din), .Clk(CLK), .R1(R1ID), .R2(R2ID), .WE(RegWriteWB), .W_num(W_WB), .R1_num(R1_num),
    .R2_num(R2_num));
  Multiplexer #(.width(5), .enable("false")) multiplexer_3 (
    .in0(out_3[25:21]), .in1(5'b00010), .out(R1_num), .sel(Sys));
  Multiplexer #(.width(5), .enable("false")) multiplexer_4 (
    .in0(out_3[20:16]), .in1(5'b00100), .out(R2_num), .sel(Sys));
  Comparator #(.width(32)) comparator_1 (.a(R1ID), .b(32'h22), .eq(comparator_1_eq));  // open: gt, lt
  Comparator #(.width(32)) comparator_2 (.a(R1ID), .b(32'ha), .eq(comparator_2_eq));  // open: gt, lt
  // Probe on PCWB[11:0]
  and and_3 (led, comparator_1_eq, Sys);
  and and_4 (halt, Sys, comparator_2_eq);
  nor nor_1 (nor_1_out, halt, led);
  and and_5 (pause, nor_1_out, Sys);
  Counter #(.width(16), .max('hffff)) counter_1 (
    .count(JMPEx), .Q(\无条件分支数 ), .clk(CLK), .clr(RST));  // open: load, D, carry
  Counter #(.width(16), .max('hffff)) counter_2 (
    .count(condi), .Q(\条件分支成功数 ), .clk(CLK), .clr(RST));  // open: load, D, carry
  not not_2 (not_2_out, SysFinal);
  Counter #(.width(16), .max('hffff)) counter_3 (
    .count(not_2_out), .Q(\总周期数 ), .clk(CLK), .clr(RST));  // open: load, D, carry
  Counter #(.width(16), .max('hffff)) counter_4 (
    .count(dataConf), .Q(\插入气泡数 ), .clk(CLK), .clr(RST));  // open: load, D, carry
  or or_4 (or_4_out, RST, dataConf, branch);
  ID_EX id_ex_1 (
    .IR(out_3), .PC(ID_PC), .CLK(CLK), .RST(or_4_out), .EN(SysEx), .R1(R1ID), .R2(R2ID), .Beq(Beq),
    .JMP(JMP), .JR(JR), .Bne(Bne), .MemToReg(MemToReg), .SRAV(SRAV), .MemWrite(MemWrite), .BLEZ(BLEZ),
    .ALUop(Aluop), .SB(SB), .Alus(Alus), .RegWrite(RegWrite), .JAL(JAL), .RegDst(RegDst), .IRout(IREX),
    .PCout(EX_PC), .R1out(pc1), .R2out(R2EX), .JMP_out(JMPEx), .Beq_out(BeqEx), .JR_out(JREx),
    .Bne_out(BneEx), .MemToReg_out(MemToRegEx), .SRAV_out(SRAVEx), .MemWrite_out(MemWriteEx),
    .BLEZ_out(BLEZEx), .Aluop_out(AluopEx), .SB_out(SBEx), .Alus_out(AlusEx), .RegWrite_out(RegWriteEx),
    .JAL_out(JALEx), .RegDst_out(RegDstEx), .SignedExt(SignedExt), .SignedExt_out(SignedExtEx));  // open: SysDin, SysDout, forward1, f1out, forward2, f2out, forcast, forcast_out
  Register #(.width(1)) PC_2 (.D(SysI), .Q(SysEx), .clk(CLK));  // open: en, clr
  Register #(.width(1)) PC_3 (.D(SysEx), .Q(SysM), .clk(CLK));  // open: en, clr
  Register #(.width(1)) PC_4 (.D(SysM), .Q(SysWB), .clk(CLK));  // open: en, clr
  Register #(.width(1)) PC_5 (.D(SysWB), .Q(SysFinal), .clk(CLK));  // open: en, clr
  Multiplexer #(.width(32), .enable("false")) multiplexer_5 (
    .in0(R2EX), .in1(ExtEX), .out(multiplexer_5_out), .sel(AlusEx));
  Multiplexer #(.width(5), .enable("false")) multiplexer_6 (
    .in0(IREX[10:6]), .in1(pc1[4:0]), .out(multiplexer_6_out), .sel(SRAVEx));
  Comparator #(.width(32)) comparator_3 (.a(pc1), .b({32{1'b0}}), .gt(comparator_3_gt));  // open: eq, lt
  or or_5 (PCSrc[1], condi, and_6_out);
  and and_6 (and_6_out, JMPEx, ~JREx);  // AND_Gate
  Comparator #(.width(32)) comparator_4 (.a(pc1), .b(32'h22), .eq(comparator_4_eq));  // open: gt, lt
  or or_6 (branch, JMPEx, condi);
  MIPS_ALU mips_alu_1 (
    .X(pc1), .Y(multiplexer_5_out), .AluOP(AluopEx), .Equal(equ), .Result(result), .shamt(multiplexer_6_out));  // open: Result_2
  and and_7 (and_7_out, BeqEx, equ);
  and and_8 (and_8_out, BneEx, ~equ);  // AND_Gate
  and and_9 (and_9_out, BLEZEx, ~comparator_3_gt);  // AND_Gate
  Register #(.width(32)) register_1 (.D(R2EX), .en(comparator_4_eq), .Q(LedData), .clk(CLK), .clr(RST));
  or or_7 (condi, and_7_out, and_8_out, and_9_out);
  Adder #(.width(32)) adder_2 (.a(EX_PC), .b(32'h4), .out(adder_2_out));  // open: cin, cout
  Shifter #(.width(32)) shifter_1 (.in(ExtEX), .\dist (5'b00010), .out(shifter_1_out));
  assign bit_extender_3_out = {{16{1'b0}}, IREX[15:0]};  // Bit_Extender bit_extender_3
  Multiplexer #(.width(32), .enable("false")) multiplexer_7 (
    .in0(bit_extender_3_out), .in1(bit_extender_4_out), .out(ExtEX), .sel(SignedExtEx));
  assign bit_extender_4_out = {{16{IREX[15]}}, IREX[15:0]};  // Bit_Extender bit_extender_4
  EX_MEM ex_mem_1 (
    .CLK(CLK), .IR(IREX), .PC(EX_PC), .RST(RST), .EN(SysM), .result(result), .R2(R2EX),
    .MemToReg(MemToRegEx), .RegDst(RegDstEx), .JAL(JALEx), .BLEZ(BLEZEx), .SRAV(SRAVEx),
    .RegWrite(RegWriteEx), .MemWrite(MemWriteEx), .IRout(IRM), .PCout(MEM_PC), .resultout({resultM, out_4}),
    .R2out(R2M), .MemToRegout(MemToRegM), .RegDstout(RegDstM), .JALout(JALM), .BLEZ_2(BLEZM),
    .SRAVout(SRAVM), .RegWrite_2(RegWriteM), .MemWriteOut(MemWriteM), .SB(SBEx), .SBout(SBM));  // open: sys, sysout
  Adder #(.width(32)) adder_3 (.a(adder_2_out), .b(shifter_1_out), .out(pc2));  // open: cin, cout
  Shifter #(.width(32)) shifter_2 (.in(R2M), .\dist (5'b01000), .out(shifter_2_out));
  Shifter #(.width(32)) shifter_3 (.in(R2M), .\dist (5'b10000), .out(shifter_3_out));
  Shifter #(.width(32)) shifter_4 (.in(R2M), .\dist (5'b11000), .out(shifter_4_out));
  Multiplexer #(.select(2), .width(4), .enable("false")) multiplexer_8 (
    .in0(4'b0001), .in1(4'b0010), .in2(4'b0100), .in3(4'b1000), .out(multiplexer_8_out), .sel(out_4));
  Multiplexer #(.select(2), .width(32), .enable("false")) multiplexer_9 (
    .in0(R2M), .in1(shifter_2_out), .in2(shifter_3_out), .in3(shifter_4_out), .out(multiplexer_9_out),
    .sel(out_4));
  Multiplexer #(.width(4), .enable("false")) multiplexer_10 (
    .in0(4'b1111), .in1(multiplexer_8_out), .out(multiplexer_10_out), .sel(SBM));
  // MIPS_RAM mips_ram_1: pin names not known; wires that end beside it: {{10{1'b0}}, resultM[11:2]}, out_5, MemWriteM, multiplexer_10_out, CLK, RST, MemData
  Multiplexer #(.width(32), .enable("false")) multiplexer_11 (
    .in0(R2M), .in1(multiplexer_9_out), .out(out_5), .sel(SBM));
  MEM_WB mem_wb_1 (
    .CLK(CLK), .IR(IRM), .PC(MEM_PC), .RST(RST), .EN(SysWB), .result({resultM, out_4}), .MemData(MemData),
    .MemToReg(MemToRegM), .RegDst(RegDstM), .JAL(JALM), .BLEZ(BLEZM), .SRAV(SRAVM), .RegWrite(RegWriteM),
    .IRout(IRWB), .PCout(PCWB), .MemDataout(MemDataWB), .resultout(resultWB), .MemToRegout(MemToRegWB),
    .RegDstout(RegDstWB), .JALout(JALWB), .BLEZ_2(BLEZWB), .SRAVout(SRAVWB), .RegWrite_2(RegWriteWB));  // open: sys, sysout
  Multiplexer #(.select(2), .width(5), .enable("false")) multiplexer_12 (
    .in0(IREX[20:16]), .in1(IREX[15:11]), .in2({5{1'b1}}), .in3({5{1'b1}}), .out(W_EX),
    .sel({JALEx, RegDstEx}));
  Multiplexer #(.select(2), .width(5), .enable("false")) multiplexer_13 (
    .in0(IRWB[20:16]), .in1(IRWB[15:11]), .in2({5{1'b1}}), .in3({5{1'b1}}), .out(W_WB),
    .sel({JALWB, RegDstWB}));
  Adder #(.width(32)) adder_4 (.a(PCWB), .b(32'h4), .out(JALWBD));  // open: cin, cout
  Multiplexer #(.select(2), .width(5), .enable("false")) multiplexer_14 (
    .in0(IRM[20:16]), .in1(IRM[15:11]), .in2({5{1'b1}}), .in3({5{1'b1}}), .out(W_M), .sel({JALM, RegDstM}));
  Multiplexer #(.width(32), .enable("false")) multiplexer_15 (
    .in0(resultWB), .in1(MemDataWB), .out(multiplexer_15_out), .sel(MemToRegWB));
  Multiplexer #(.width(32), .enable("false")) multiplexer_16 (
    .in0(multiplexer_15_out), .in1(JALWBD), .out(Din), .sel(JALWB));

  // Other names for the same wires on the sheet: FinalMemData[31:0] = out_5; IRID[31:0] = out_3;
  //   pc3[31:2] = {pc0[31:28], IREX[25:0]}; R1EX[31:0] = pc1; PCEX[31:0] = EX_PC; PCID[31:0] = ID_PC;
  //   PCIF[31:0] = IF_PC; PCM[31:0] = MEM_PC; PCSrc[0] = JMPEx; resultM[1:0] = out_4; SysID = SysI;
  //   WB_PC[31:0] = PCWB

  // Notes on the sheet:
  //   中断源
  //   中断等待指示
  //   pcout
  //   数码管输出
  //   irout
  //   contents of rom_1 (hex, n*v repeats v):
  //   20110001 8000c05 20110001 20120002 20130003 8000c09 20110001 20120002 20130003 8000c0d 20110001
  //   20120002 20130003 8000c11 20110001 20120002 20130003 c000cf8 20100001 20110001 118fc0 112020
  //   20020022 c 118882 12200001 8000c15 112020 20020022 c 20110001 118880 112020 20020022 c 12200001
  //   8000c1f 20110001 118fc0 112020 20020022 c 1188c3 112020 20020022 c 118903 112020 20020022 c 118903
  //   112020 20020022 c 118903 112020 20020022 c 118903 112020 20020022 c 118903 112020 20020022 c 118903
  //   112020 20020022 c 118903 112020 20020022 c 20100001 109fc0 139fc3 8021 2012000c 24160003 26100001
  //   3210000f 20080008 20090001 139900 2709825 132020 20020022 c 1094022 1500fff9 22100001 2018000f
  //   2188024 108700 20080008 20090001 139902 2709825 132021 20020022 c 1094022 1500fff9 108702 2c9b022
  //   12c00001 8000c50 4020 1084027 84400 3508ffff 82021 20020022 c 2010ffff 20110000 ae300000 22100001
  //   22310004 ae300000 22100001 22310004 ae300000 22100001 22310004 ae300000 22100001 22310004 ae300000
  //   22100001 22310004 ae300000 22100001 22310004 ae300000 22100001 22310004 ae300000 22100001 22310004
  //   ae300000 22100001 22310004 ae300000 22100001 22310004 ae300000 22100001 22310004 ae300000 22100001
  //   22310004 ae300000 22100001 22310004 ae300000 22100001 22310004 ae300000 22100001 22310004 ae300000
  //   22100001 22310004 22100001 8020 2011003c 8e130000 8e340000 274402a 11000002 ae330000 ae140000
  //   2231fffc 1611fff8 102020 20020022 c 22100004 2011003c 1611fff2 20020032 c 20080001 20090003 20110876
  //   118d00 112020 20020022 c 200b0008 1118807 1318807 112020 20020022 c 216bffff 1560fff9 20020032 c
  //   2008ffff 20117777 112020 20020022 c 200b0010 3a31ffff 112020 20020022 c 216bffff 1560fffa 20020032 c
  //   20090000 200b0020 20110000 20120001 a1310000 112020 20020022 c 2328820 21290001 216bffff 1560fff8
  //   200b0008 20090000 8d310000 112020 20020022 c 21290004 216bffff 1560fff9 20020032 c 2011fff1 112020
  //   20020022 c 22310001 1a20fffb 2002000a c 20020032 c 20100000 22100001 102020 20020022 c 22100002
  //   102020 20020022 c 22100003 102020 20020022 c 22100004 102020 20020022 c 22100005 102020 20020022 c
  //   22100006 102020 20020022 c 22100007 102020 20020022 c 22100008 102020 20020022 20020022 c 3e00008
  //   JMP
  //   JR
  //   OP
  //   Func
  //   流水调试日志用
  //   Beq
  //   Bne
  //   MemToReg
  //   MemWrite
  //   AluOP
  //   AluSrcB
  //   RegWrite
  //   JAL
  //   RegDst
  //   Syscall
endmodule

module \重定向流水线  (
  output [31:0] out_1,
  output [4:0] out_2,
  output [4:0] out_3,
  output [31:0] out_4,
  output [4:0] out_5,
  output [31:0] out_6
);

  wire Alus, AlusEx, and_1_out, and_2_out, and_3_out, and_4_out, and_5_out, and_6_out, and_10_out,
       and_11_out, and_12_out, and_13_out, and_14_out, Beq, BeqEx, BLEZ, BLEZEx, BLEZM, BLEZWB, Bne, BneEx,
       branch, CLK, comparator_1_eq, comparator_2_eq, comparator_3_eq, comparator_4_eq, comparator_5_eq,
       comparator_6_eq, comparator_7_eq, comparator_8_eq, comparator_9_eq, comparator_10_eq,
       comparator_11_eq, comparator_12_gt, comparator_13_eq, condi, equ, Go, halt, IR1, IR2, IR3, JAL, JALEx,
       JALM, JALWB, JMP, JMPEx, JR, JREx, ldEX, ldM, led, loaduse, MemToReg, MemToRegEx, MemToRegM,
       MemToRegWB, MemWrite, MemWriteEx, MemWriteM, nor_1_out, or_2_out, or_3_out, or_4_out, or_5_out,
       or_6_out, or_8_out, or_9_out, or_12_out, pause, PC_7_q, pcen, RegDst, RegDstEx, RegDstM, RegDstWB,
       RegWrite, RegWriteEx, RegWriteM, RegWriteWB, RST, SB, SBEx, SBM, SignedExt, SignedExtEx, SRAV, SRAVEx,
       SRAVM, SRAVWB, Sys, SysEx, SysFinal, SysI, SysM, SysWB, W1, W2, W3;
  wire [1:0] f1EX, f2EX, forward1, forward2;
  wire [1:1] PCSrc;
  wire [3:0] Aluop, AluopEx, multiplexer_16_out, multiplexer_17_out;
  wire [4:0] multiplexer_10_out, R2_num, W_M;
  wire [15:0] \LoadUse次数 , \总周期数 , \插入气泡数 , \无条件分支数 , \条件分支成功数 ;
  wire [31:0] adder_2_out, ALUA, ALUB, bit_extender_1_out, bit_extender_2_out, bit_extender_3_out,
       bit_extender_4_out, EX_PC, Ext, ExtEX, FinalMemData, ID_PC, IF_PC, IREX, IRID, IRM, IRWB, JALWBD,
       LedData, MDWB, MEM_PC, MemData, MemDataWB, mips_regifile_1_r2, multiplexer_9_out, multiplexer_14_out,
       multiplexer_18_out, pc0, pc1, PCWB, R1ID, R2EX, R2ID, R2M, result, resultM, resultWB, rom_1_data,
       shifter_1_out, shifter_2_out, shifter_3_out, shifter_4_out;

  Button \u_总复位  (.out(RST));
  Button _1 (.out(IR1));
  Button _2 (.out(IR2));
  Button _3 (.out(IR3));
  Button \u_继续运行  (.out(Go));
  LED led_1 (.in(W1));
  LED led_2 (.in(W2));
  LED led_3 (.in(W3));
  and and_1 (and_1_out, Sys, halt);
  and and_2 (and_2_out, Sys, ~Go, pause);  // AND_Gate
  Multiplexer #(.select(2), .width(32), .enable("false")) multiplexer_1 (
    .in0(pc0), .in1(pc1), .in2(out_6), .in3({pc0[31:28], IREX[25:0], 2'b00}), .out(out_1),
    .sel({PCSrc[1], JMPEx}));
  Hex_Digit_Display hex_digit_display_1 (.value(LedData[31:28]));  // open: dp
  or or_1 (SysI, and_1_out, and_2_out);
  assign bit_extender_1_out = {{16{1'b0}}, IRID[15:0]};  // Bit_Extender bit_extender_1
  assign bit_extender_2_out = {{16{IRID[15]}}, IRID[15:0]};  // Bit_Extender bit_extender_2
  Comparator #(.width(2)) comparator_1 (.a(forward1), .b(2'b00), .eq(comparator_1_eq));  // open: gt, lt
  Comparator #(.width(32)) comparator_2 (.a(R1ID), .b(32'h22), .eq(comparator_2_eq));  // open: gt, lt
  Comparator #(.width(32)) comparator_3 (.a(resultM), .b(32'h22), .eq(comparator_3_eq));  // open: gt, lt
  Comparator #(.width(2)) comparator_4 (.a(forward1), .b(2'b11), .eq(comparator_4_eq));  // open: gt, lt
  Comparator #(.width(2)) comparator_5 (.a(forward1), .b(2'b00), .eq(comparator_5_eq));  // open: gt, lt
  Comparator #(.width(32)) comparator_6 (.a(R1ID), .b(32'ha), .eq(comparator_6_eq));  // open: gt, lt
  Comparator #(.width(32)) comparator_7 (.a(resultM), .b(32'ha), .eq(comparator_7_eq));  // open: gt, lt
  Comparator #(.width(2)) comparator_8 (.a(forward1), .b(2'b11), .eq(comparator_8_eq));  // open: gt, lt
  Hex_Digit_Display hex_digit_display_2 (.value(LedData[27:24]));  // open: dp
  Hex_Digit_Display hex_digit_display_3 (.value(LedData[23:20]));  // open: dp
  Register #(.width(32)) PC (.D(out_1), .en(pcen), .Q(IF_PC), .clk(CLK), .clr(RST));
  Multiplexer #(.width(32), .enable("false")) multiplexer_2 (
    .in0(bit_extender_1_out), .in1(bit_extender_2_out), .out(Ext), .sel(SignedExt));
  and and_3 (and_3_out, comparator_1_eq, comparator_2_eq);
  and and_4 (and_4_out, comparator_3_eq, comparator_4_eq);
  and and_5 (and_5_out, comparator_5_eq, comparator_6_eq);
  and and_6 (and_6_out, comparator_7_eq, comparator_8_eq);
  Hex_Digit_Display hex_digit_display_4 (.value(LedData[19:16]));  // open: dp
  Hex_Digit_Display hex_digit_display_5 (.value(LedData[15:12]));  // open: dp
  or or_2 (or_2_out, and_3_out, and_4_out);
  or or_3 (or_3_out, and_5_out, and_6_out);
  Hex_Digit_Display hex_digit_display_6 (.value(LedData[11:8]));  // open: dp
  Hex_Digit_Display hex_digit_display_7 (.value(LedData[7:4]));  // open: dp
  Clock clock_1 (.out(CLK));
  and and_7 (led, or_2_out, Sys);
  and and_8 (halt, Sys, or_3_out);
  nor nor_1 (nor_1_out, halt, led);
  and and_9 (pause, nor_1_out, Sys);
  Hex_Digit_Display hex_digit_display_8 (.value(LedData[3:0]));  // open: dp
  or or_4 (or_4_out, SysI, loaduse, ldEX, ldM);
  not not_1 (pcen, or_4_out);
  ROM #(.addrWidth(10), .dataWidth(32)) rom_1 (.addr(IF_PC[11:2]), .data(rom_1_data));  // open: sel
  // Probe on \总周期数 
  // Probe on \无条件分支数 
  // Probe on \条件分支成功数 
  // Probe on \插入气泡数 
  // Probe on \LoadUse次数 
  or or_5 (or_5_out, RST, branch);
  IF_ID if_id_1 (
    .IR(rom_1_data), .PC(IF_PC), .CLK(CLK), .RST(or_5_out), .EN(or_4_out), .IROUT(IRID), .PCOUT(ID_PC));  // open: forcast, forcast_out
  // Probe on IRID
  Multiplexer #(.width(5), .enable("false")) multiplexer_3 (.in0(IRID[25:21]), .in1(5'b00010), .out(out_5), .sel(Sys));
  Multiplexer #(.width(5), .enable("false")) multiplexer_4 (.in0(IRID[20:16]), .in1(5'b00100), .out(R2_num), .sel(Sys));
  // Probe on IF_PC[11:0]
  // Probe on out_2
  Multiplexer #(.select(2), .width(5), .enable("false")) multiplexer_5 (
    .in0(IREX[20:16]), .in1(IREX[15:11]), .in2({5{1'b1}}), .in3({5{1'b1}}), .out(out_3),
    .sel({JALEx, RegDstEx}));
  // Probe on ID_PC[11:0]
  \loaduse分析  \loaduse分析_1  (
    .OP0(IRID[31:26]), .OP1(IREX[31:26]), .EX_WriteReg_num(out_3), .Func0(IRID[5:0]), .Func1(IREX[5:0]),
    .ID_R1_num(out_5), .ID_R2_num(R2_num), .out_8(loaduse));
  // Probe on EX_PC[11:0]
  // Probe on MEM_PC[11:0]
  \硬布线控制器  \u_硬布线控制器_1  (
    .Func(IRID[5:0]), .OP(IRID[31:26]), .ALU_OP(Aluop), .MemToReg(MemToReg), .MemWrite(MemWrite),
    .ALU_SRC(Alus), .RegWrite(RegWrite), .SysCALL(Sys), .SignedExt(SignedExt), .RegDst(RegDst), .JR(JR),
    .JMP(JMP), .Beq(Beq), .JAL(JAL), .Bne(Bne), .SRAV(SRAV), .BLEZ(BLEZ), .SB(SB));  // open: MFC0, ERET
  MIPS_Regifile mips_regifile_1 (
    .Din(out_4), .Clk(CLK), .R1(R1ID), .R2(mips_regifile_1_r2), .WE(RegWriteWB), .W_num(out_2),
    .R1_num(out_5), .R2_num(R2_num));
  Comparator #(.width(5)) comparator_9 (.a(R2_num), .b(IRM[20:16]), .eq(comparator_9_eq));  // open: gt, lt
  Comparator #(.width(6)) comparator_10 (.a(IRID[31:26]), .b(6'b101000), .eq(comparator_10_eq));  // open: gt, lt
  Comparator #(.width(6)) comparator_11 (.a(IRM[31:26]), .b(6'b001000), .eq(comparator_11_eq));  // open: gt, lt
  Multiplexer #(.select(2), .width(5), .enable("false")) multiplexer_6 (
    .in0(IRM[20:16]), .in1(IRM[15:11]), .in2({5{1'b1}}), .in3({5{1'b1}}), .out(W_M), .sel({JALM, RegDstM}));
  Register #(.width(1)) PC_2 (.D(loaduse), .Q(ldEX), .clk(CLK));  // open: en, clr
  // Probe on PCWB[11:0]
  // Probe on mips_regifile_1_r2
  Multiplexer #(.width(32), .enable("false")) multiplexer_7 (
    .in0(mips_regifile_1_r2), .in1(resultM), .out(R2ID), .sel(and_10_out));
  and and_10 (and_10_out, comparator_9_eq, comparator_10_eq, comparator_11_eq);
  \重定向控制器  \u_重定向控制器_1  (
    .OP(IRID[31:26]), .EX_WriteReg_num(out_3), .EX_RegWrite(RegWriteEx), .MEM_mtr(MemToRegM),
    .MEM_WriteReg_num(W_M), .MEM_RegWrite(RegWriteM), .Func(IRID[5:0]), .ID_R1_num(out_5),
    .ID_R2_num(R2_num), .forward1(forward1), .forward2(forward2));
  // Probe on forward2
  Register #(.width(1)) PC_3 (.D(ldEX), .Q(ldM), .clk(CLK));  // open: en, clr
  Counter #(.width(16), .max('hffff)) counter_1 (
    .count(JMPEx), .Q(\无条件分支数 ), .clk(CLK), .clr(RST));  // open: load, D, carry
  Comparator #(.width(32)) comparator_12 (.a(pc1), .b({32{1'b0}}), .gt(comparator_12_gt));  // open: eq, lt
  and and_11 (and_11_out, JMPEx, ~JREx);  // AND_Gate
  Counter #(.width(16), .max('hffff)) counter_2 (
    .count(condi), .Q(\条件分支成功数 ), .clk(CLK), .clr(RST));  // open: load, D, carry
  or or_6 (or_6_out, loaduse, ldEX, ldM);
  and and_12 (and_12_out, BeqEx, equ);
  and and_13 (and_13_out, BneEx, ~equ);  // AND_Gate
  and and_14 (and_14_out, BLEZEx, ~comparator_12_gt);  // AND_Gate
  or or_7 (PCSrc[1], condi, and_11_out);
  Adder #(.width(32)) adder_1 (.a(IF_PC), .b(32'h4), .out(pc0));  // open: cin, cout
  Adder #(.width(32)) adder_2 (.a(EX_PC), .b(32'h4), .out(adder_2_out));  // open: cin, cout
  Shifter #(.width(32)) shifter_1 (.in(ExtEX), .\dist (5'b00010), .out(shifter_1_out));
  Counter #(.width(16), .max('hffff)) counter_3 (
    .count(SysFinal), .Q(\总周期数 ), .clk(CLK), .clr(RST));  // open: load, D, carry
  Counter #(.width(16), .max('hffff)) counter_4 (
    .count(or_8_out), .Q(\插入气泡数 ), .clk(CLK), .clr(RST));  // open: load, D, carry
  or or_8 (or_8_out, ldM, ldEX, loaduse, branch);
  or or_9 (or_9_out, RST, branch, or_6_out);
  ID_EX id_ex_1 (
    .IR(IRID), .PC(ID_PC), .CLK(CLK), .RST(or_9_out), .EN(SysEx), .R1(R1ID), .R2(R2ID), .Beq(Beq), .JMP(JMP),
    .JR(JR), .Bne(Bne), .MemToReg(MemToReg), .SRAV(SRAV), .MemWrite(MemWrite), .BLEZ(BLEZ), .ALUop(Aluop),
    .SB(SB), .Alus(Alus), .RegWrite(RegWrite), .JAL(JAL), .RegDst(RegDst), .IRout(IREX), .PCout(EX_PC),
    .R1out(pc1), .R2out(R2EX), .JMP_out(JMPEx), .Beq_out(BeqEx), .JR_out(JREx), .Bne_out(BneEx),
    .MemToReg_out(MemToRegEx), .SRAV_out(SRAVEx), .MemWrite_out(MemWriteEx), .BLEZ_out(BLEZEx),
    .Aluop_out(AluopEx), .SB_out(SBEx), .Alus_out(AlusEx), .RegWrite_out(RegWriteEx), .JAL_out(JALEx),
    .RegDst_out(RegDstEx), .SignedExt(SignedExt), .SignedExt_out(SignedExtEx), .forward1(forward1),
    .f1out(f1EX), .forward2(forward2), .f2out(f2EX));  // open: SysDin, SysDout, forcast, forcast_out
  or or_10 (condi, and_12_out, and_13_out, and_14_out);
  Adder #(.width(32)) adder_3 (.a(adder_2_out), .b(shifter_1_out), .out(out_6));  // open: cin, cout
  Counter #(.width(16), .max('hffff)) counter_5 (
    .D(\插入气泡数 ), .count(loaduse), .Q(\LoadUse次数 ), .clk(CLK), .clr(RST));  // open: load, carry
  or or_11 (branch, JMPEx, condi);
  Multiplexer #(.select(2), .width(32), .enable("false")) multiplexer_8 (
    .in0(pc1), .in1(MDWB), .in2(resultWB), .in3(resultM), .out(ALUA), .sel(f1EX));
  Multiplexer #(.width(32), .enable("false")) multiplexer_9 (
    .in0(ALUB), .in1(ExtEX), .out(multiplexer_9_out), .sel(AlusEx));
  Multiplexer #(.width(5), .enable("false")) multiplexer_10 (
    .in0(IREX[10:6]), .in1(pc1[4:0]), .out(multiplexer_10_out), .sel(SRAVEx));
  assign bit_extender_3_out = {{16{1'b0}}, IREX[15:0]};  // Bit_Extender bit_extender_3
  assign bit_extender_4_out = {{16{IREX[15]}}, IREX[15:0]};  // Bit_Extender bit_extender_4
  Register #(.width(1), .trigger("falling")) PC_4 (.D(SysEx), .Q(SysM), .clk(CLK), .clr(RST));  // open: en
  Register #(.width(1), .trigger("falling")) PC_5 (.D(SysI), .Q(SysEx), .clk(CLK), .clr(RST));  // open: en
  Comparator #(.width(32)) comparator_13 (.a(ALUA), .b(32'h22), .eq(comparator_13_eq));  // open: gt, lt
  MIPS_ALU mips_alu_1 (
    .X(ALUA), .Y(multiplexer_9_out), .AluOP(AluopEx), .Equal(equ), .Result(result), .shamt(multiplexer_10_out));  // open: Result_2
  Multiplexer #(.width(32), .enable("false")) multiplexer_11 (
    .in0(bit_extender_3_out), .in1(bit_extender_4_out), .out(ExtEX), .sel(SignedExtEx));
  Multiplexer #(.select(2), .width(32), .enable("false")) multiplexer_12 (
    .in0(R2EX), .in1(MDWB), .in2(resultWB), .in3(resultM), .out(ALUB), .sel(f2EX));
  Register #(.width(1), .trigger("falling")) PC_6 (.D(SysM), .Q(SysWB), .clk(CLK), .clr(RST));  // open: en
  Register #(.width(1), .trigger("falling")) PC_7 (.D(SysWB), .Q(PC_7_q), .clk(CLK), .clr(RST));  // open: en
  Register #(.width(32)) register_1 (.D(ALUB), .en(comparator_13_eq), .Q(LedData), .clk(CLK), .clr(RST));
  or or_12 (or_12_out, ldEX, ldM);
  and and_15 (SysFinal, ~or_12_out, ~PC_7_q);  // AND_Gate
  EX_MEM ex_mem_1 (
    .CLK(CLK), .IR(IREX), .PC(EX_PC), .RST(RST), .EN(SysM), .result(result), .R2(R2EX),
    .MemToReg(MemToRegEx), .RegDst(RegDstEx), .JAL(JALEx), .BLEZ(BLEZEx), .SRAV(SRAVEx),
    .RegWrite(RegWriteEx), .MemWrite(MemWriteEx), .IRout(IRM), .PCout(MEM_PC), .resultout(resultM),
    .R2out(R2M), .MemToRegout(MemToRegM), .RegDstout(RegDstM), .JALout(JALM), .BLEZ_2(BLEZM),
    .SRAVout(SRAVM), .RegWrite_2(RegWriteM), .MemWriteOut(MemWriteM), .SB(SBEx), .SBout(SBM));  // open: sys, sysout
  // Probe on IRM
  Multiplexer #(.select(2), .width(5), .enable("false")) multiplexer_13 (
    .in0(IRWB[20:16]), .in1(IRWB[15:11]), .in2({5{1'b1}}), .in3({5{1'b1}}), .out(out_2),
    .sel({JALWB, RegDstWB}));
  Multiplexer #(.width(32), .enable("false")) multiplexer_14 (
    .in0(resultWB), .in1(MemDataWB), .out(multiplexer_14_out), .sel(MemToRegWB));
  Adder #(.width(32)) adder_4 (.a(PCWB), .b(32'h4), .out(JALWBD));  // open: cin, cout
  Multiplexer #(.width(32), .enable("false")) multiplexer_15 (
    .in0(multiplexer_14_out), .in1(JALWBD), .out(out_4), .sel(JALWB));
  Multiplexer #(.select(2), .width(4), .enable("false")) multiplexer_16 (
    .in0(4'b0001), .in1(4'b0010), .in2(4'b0100), .in3(4'b1000), .out(multiplexer_16_out), .sel(resultM[1:0]));
  // Probe on resultM
  // Probe on multiplexer_17_out
  Multiplexer #(.width(4), .enable("false")) multiplexer_17 (
    .in0(4'b1111), .in1(multiplexer_16_out), .out(multiplexer_17_out), .sel(SBM));
  // MIPS_RAM mips_ram_1: pin names not known; wires that end beside it: {{10{1'b0}}, resultM[11:2]}, FinalMemData, MemWriteM, multiplexer_17_out, CLK, RST, MemData
  Shifter #(.width(32)) shifter_2 (.in(R2M), .\dist (5'b01000), .out(shifter_2_out));
  Shifter #(.width(32)) shifter_3 (.in(R2M), .\dist (5'b10000), .out(shifter_3_out));
  Shifter #(.width(32)) shifter_4 (.in(R2M), .\dist (5'b11000), .out(shifter_4_out));
  Multiplexer #(.select(2), .width(32), .enable("false")) multiplexer_18 (
    .in0(R2M), .in1(shifter_2_out), .in2(shifter_3_out), .in3(shifter_4_out), .out(multiplexer_18_out),
    .sel(resultM[1:0]));
  MEM_WB mem_wb_1 (
    .CLK(CLK), .IR(IRM), .PC(MEM_PC), .RST(RST), .EN(SysWB), .result(resultM), .MemData(MemData),
    .MemToReg(MemToRegM), .RegDst(RegDstM), .JAL(JALM), .BLEZ(BLEZM), .SRAV(SRAVM), .RegWrite(RegWriteM),
    .IRout(IRWB), .PCout(PCWB), .MemDataout(MemDataWB), .resultout(resultWB), .MemToRegout(MemToRegWB),
    .RegDstout(RegDstWB), .JALout(JALWB), .BLEZ_2(BLEZWB), .SRAVout(SRAVWB), .RegWrite_2(RegWriteWB));  // open: sys, sysout
  // Probe on R2M
  Multiplexer #(.width(32), .enable("false")) multiplexer_19 (
    .in0(R2M), .in1(multiplexer_18_out), .out(FinalMemData), .sel(SBM));
  // Probe on resultM[1:0]
  // Probe on IRWB
  // Probe on FinalMemData
  // Probe on resultWB

  // Other names for the same wires on the sheet: Din[31:0] = out_4; R1EX[31:0] = pc1; pc2[31:0] = out_6;
  //   pc3[31:2] = {pc0[31:28], IREX[25:0]}; PCEX[31:0] = EX_PC; PCID[31:0] = ID_PC; PCIF[31:0] = IF_PC;
  //   PCM[31:0] = MEM_PC; PCSrc[0] = JMPEx; R1_num[4:0] = out_5; SysID = SysI; W_EX[4:0] = out_3; W_WB[4:0] = out_2;
  //   WB_PC[31:0] = PCWB

  // Notes on the sheet:
  //   中断源
  //   中断等待指示
  //   pcout
  //   数码管输出
  //   irout
  //   contents of rom_1 (hex, n*v repeats v):
  //   20110001 8000c05 20110001 20120002 20130003 8000c09 20110001 20120002 20130003 8000c0d 20110001
  //   20120002 20130003 8000c11 20110001 20120002 20130003 c000cf8 20100001 20110001 118fc0 112020
  //   20020022 c 118882 12200001 8000c15 112020 20020022 c 20110001 118880 112020 20020022 c 12200001
  //   8000c1f 20110001 118fc0 112020 20020022 c 1188c3 112020 20020022 c 118903 112020 20020022 c 118903
  //   112020 20020022 c 118903 112020 20020022 c 118903 112020 20020022 c 118903 112020 20020022 c 118903
  //   112020 20020022 c 118903 112020 20020022 c 20100001 109fc0 139fc3 8021 2012000c 24160003 26100001
  //   3210000f 20080008 20090001 139900 2709825 132020 20020022 c 1094022 1500fff9 22100001 2018000f
  //   2188024 108700 20080008 20090001 139902 2709825 132021 20020022 c 1094022 1500fff9 108702 2c9b022
  //   12c00001 8000c50 4020 1084027 84400 3508ffff 82021 20020022 c 2010ffff 20110000 ae300000 22100001
  //   22310004 ae300000 22100001 22310004 ae300000 22100001 22310004 ae300000 22100001 22310004 ae300000
  //   22100001 22310004 ae300000 22100001 22310004 ae300000 22100001 22310004 ae300000 22100001 22310004
  //   ae300000 22100001 22310004 ae300000 22100001 22310004 ae300000 22100001 22310004 ae300000 22100001
  //   22310004 ae300000 22100001 22310004 ae300000 22100001 22310004 ae300000 22100001 22310004 ae300000
  //   22100001 22310004 22100001 8020 2011003c 8e130000 8e340000 274402a 11000002 ae330000 ae140000
  //   2231fffc 1611fff8 102020 20020022 c 22100004 2011003c 1611fff2 20020032 c 20080001 20090003 20110876
  //   118d00 112020 20020022 c 200b0008 1118807 1318807 112020 20020022 c 216bffff 1560fff9 20020032 c
  //   2008ffff 20117777 112020 20020022 c 200b0010 3a31ffff 112020 20020022 c 216bffff 1560fffa 20020032 c
  //   20090000 200b0020 20110000 20120001 a1310000 112020 20020022 c 2328820 21290001 216bffff 1560fff8
  //   200b0008 20090000 8d310000 112020 20020022 c 21290004 216bffff 1560fff9 20020032 c 2011fff1 112020
  //   20020022 c 22310001 1a20fffb 2002000a c 20020032 c 20100000 22100001 102020 20020022 c 22100002
  //   102020 20020022 c 22100003 102020 20020022 c 22100004 102020 20020022 c 22100005 102020 20020022 c
  //   22100006 102020 20020022 c 22100007 102020 20020022 c 22100008 102020 20020022 20020022 c 3e00008
  //   重定向分析
  //   JMP
  //   JR
  //   OP
  //   Func
  //   流水调试日志用
  //   Beq
  //   Bne
  //   MemToReg
  //   MemWrite
  //   AluOP
  //   AluSrcB
  //   RegWrite
  //   JAL
  //   RegDst
  //   Syscall
  //   地址转移逻辑
  //   重定向选择
  //   写回值与地址计算
endmodule

module \额外控制信号  (
  input  OP0,
  input  OP1,
  input  OP2,
  input  OP3,
  input  OP4,
  input  OP5,
  input  F0,
  input  F1,
  input  F2,
  input  F3,
  input  F4,
  input  F5,
  output SRAV,
  output BLEZ,
  output SB,
  output MFC0,
  output ERET
);

  wire not_1_out, not_2_out, not_3_out, not_4_out, not_5_out, not_6_out, not_7_out, not_8_out, not_9_out,
       not_10_out, not_11_out, not_12_out, not_13_out, not_14_out, not_15_out, not_16_out, not_17_out,
       not_18_out, not_19_out, not_20_out, not_21_out, not_22_out, not_23_out, not_24_out, not_25_out,
       not_26_out, not_27_out, not_28_out, not_29_out, not_30_out, not_31_out;

  not not_1 (not_1_out, OP5);
  not not_2 (not_2_out, OP4);
  not not_3 (not_3_out, OP3);
  not not_4 (not_4_out, OP2);
  not not_5 (not_5_out, OP1);
  not not_6 (not_6_out, OP0);
  not not_7 (not_7_out, F5);
  not not_8 (not_8_out, F4);
  not not_9 (not_9_out, F3);
  not not_10 (not_10_out, OP5);
  not not_11 (not_11_out, OP4);
  not not_12 (not_12_out, OP3);
  not not_13 (not_13_out, OP0);
  not not_14 (not_14_out, OP4);
  not not_15 (not_15_out, OP2);
  not not_16 (not_16_out, OP1);
  not not_17 (not_17_out, OP0);
  not not_18 (not_18_out, OP5);
  not not_19 (not_19_out, OP3);
  not not_20 (not_20_out, OP2);
  not not_21 (not_21_out, OP1);
  not not_22 (not_22_out, OP0);
  not not_23 (not_23_out, OP5);
  not not_24 (not_24_out, OP3);
  not not_25 (not_25_out, OP2);
  not not_26 (not_26_out, OP1);
  not not_27 (not_27_out, OP0);
  not not_28 (not_28_out, F0);
  not not_29 (not_29_out, F1);
  not not_30 (not_30_out, F2);
  not not_31 (not_31_out, F5);
  and and_1 (SRAV, not_1_out, not_2_out, not_3_out, not_4_out, not_5_out, not_6_out, not_7_out, not_8_out, not_9_out, F2, F1, F0);
  and and_2 (BLEZ, not_10_out, not_11_out, not_12_out, OP2, OP1, not_13_out);
  and and_3 (SB, OP5, not_14_out, OP3, not_15_out, not_16_out, not_17_out);
  and and_4 (MFC0, not_18_out, OP4, not_19_out, not_20_out, not_21_out, not_22_out);
  and and_5 (ERET, not_23_out, OP4, not_24_out, not_25_out, not_26_out, not_27_out, not_28_out, not_29_out, not_30_out, F3, F4, not_31_out);
endmodule

module \重定向控制器  (
  input  [5:0] OP,
  input  [4:0] EX_WriteReg_num,
  input  EX_RegWrite,
  input  MEM_mtr,
  input  [4:0] MEM_WriteReg_num,
  input  MEM_RegWrite,
  input  [5:0] Func,
  input  [4:0] ID_R1_num,
  input  [4:0] ID_R2_num,
  output [1:0] forward1,
  output [1:0] forward2
);

  wire and_1_out, and_2_out, and_3_out, and_4_out, and_5_out, and_6_out, and_7_out, and_8_out, and_9_out,
       and_10_out, and_11_out, and_12_out, comparator_1_eq, comparator_2_eq, comparator_3_eq,
       comparator_4_eq, comparator_5_eq, comparator_6_eq, comparator_7_eq, comparator_8_eq, comparator_9_eq,
       comparator_10_eq, comparator_11_eq, comparator_12_eq, comparator_13_eq, comparator_14_eq,
       comparator_15_eq, comparator_16_eq, R1_Used, R2_Used;

  \源寄存器使用情况  \u_源寄存器使用情况_1  (
    .OP0(OP[0]), .OP1(OP[1]), .OP2(OP[2]), .OP3(OP[3]), .OP4(OP[4]), .OP5(OP[5]), .F0(Func[0]), .F1(Func[1]),
    .F2(Func[2]), .F3(Func[3]), .F4(Func[4]), .F5(Func[5]), .R1_Used(R1_Used), .R2_Used(R2_Used));
  Comparator #(.width(5)) comparator_1 (.a(ID_R1_num), .b({5{1'b0}}), .eq(comparator_1_eq));  // open: gt, lt
  Comparator #(.width(5)) comparator_2 (.a(EX_WriteReg_num), .b(ID_R1_num), .eq(comparator_2_eq));  // open: gt, lt
  Comparator #(.width(5)) comparator_3 (.a(ID_R1_num), .b({5{1'b0}}), .eq(comparator_3_eq));  // open: gt, lt
  Comparator #(.width(5)) comparator_4 (.a(MEM_WriteReg_num), .b(ID_R1_num), .eq(comparator_4_eq));  // open: gt, lt
  Comparator #(.width(5)) comparator_5 (.a(ID_R1_num), .b({5{1'b0}}), .eq(comparator_5_eq));  // open: gt, lt
  Comparator #(.width(5)) comparator_6 (.a(EX_WriteReg_num), .b(ID_R1_num), .eq(comparator_6_eq));  // open: gt, lt
  Comparator #(.width(5)) comparator_7 (.a(ID_R1_num), .b({5{1'b0}}), .eq(comparator_7_eq));  // open: gt, lt
  Comparator #(.width(5)) comparator_8 (.a(MEM_WriteReg_num), .b(ID_R1_num), .eq(comparator_8_eq));  // open: gt, lt
  and and_1 (and_1_out, EX_RegWrite, R1_Used, ~comparator_1_eq, comparator_2_eq);  // AND_Gate
  and and_2 (and_2_out, ~and_1_out, ~MEM_mtr, and_3_out);  // AND_Gate
  and and_3 (and_3_out, MEM_RegWrite, R1_Used, ~comparator_3_eq, comparator_4_eq);  // AND_Gate
  and and_4 (and_4_out, EX_RegWrite, R1_Used, ~comparator_5_eq, comparator_6_eq);  // AND_Gate
  and and_5 (and_5_out, ~and_4_out, MEM_mtr, and_6_out);  // AND_Gate
  and and_6 (and_6_out, MEM_RegWrite, R1_Used, ~comparator_7_eq, comparator_8_eq);  // AND_Gate
  or or_1 (forward1[1], and_1_out, and_2_out);
  or or_2 (forward1[0], and_4_out, and_5_out);
  Comparator #(.width(5)) comparator_9 (.a(ID_R2_num), .b({5{1'b0}}), .eq(comparator_9_eq));  // open: gt, lt
  Comparator #(.width(5)) comparator_10 (.a(EX_WriteReg_num), .b(ID_R2_num), .eq(comparator_10_eq));  // open: gt, lt
  Comparator #(.width(5)) comparator_11 (.a(ID_R2_num), .b({5{1'b0}}), .eq(comparator_11_eq));  // open: gt, lt
  Comparator #(.width(5)) comparator_12 (.a(MEM_WriteReg_num), .b(ID_R2_num), .eq(comparator_12_eq));  // open: gt, lt
  Comparator #(.width(5)) comparator_13 (.a(ID_R2_num), .b({5{1'b0}}), .eq(comparator_13_eq));  // open: gt, lt
  Comparator #(.width(5)) comparator_14 (.a(EX_WriteReg_num), .b(ID_R2_num), .eq(comparator_14_eq));  // open: gt, lt
  Comparator #(.width(5)) comparator_15 (.a(ID_R2_num), .b({5{1'b0}}), .eq(comparator_15_eq));  // open: gt, lt
  Comparator #(.width(5)) comparator_16 (.a(MEM_WriteReg_num), .b(ID_R2_num), .eq(comparator_16_eq));  // open: gt, lt
  and and_7 (and_7_out, EX_RegWrite, R2_Used, ~comparator_9_eq, comparator_10_eq);  // AND_Gate
  and and_8 (and_8_out, MEM_RegWrite, R2_Used, ~comparator_11_eq, comparator_12_eq);  // AND_Gate
  and and_9 (and_9_out, EX_RegWrite, R2_Used, ~comparator_13_eq, comparator_14_eq);  // AND_Gate
  and and_10 (and_10_out, MEM_RegWrite, R2_Used, ~comparator_15_eq, comparator_16_eq);  // AND_Gate
  and and_11 (and_11_out, ~and_7_out, ~MEM_mtr, and_8_out);  // AND_Gate
  and and_12 (and_12_out, ~and_9_out, MEM_mtr, and_10_out);  // AND_Gate
  or or_3 (forward2[1], and_7_out, and_11_out);
  or or_4 (forward2[0], and_9_out, and_12_out);

  // Other names for the same wires on the sheet: OP_CODE[5:0] = OP
endmodule

module \loaduse分析  (
  input  [5:0] OP0,
  input  [5:0] OP1,
  input  [4:0] EX_WriteReg_num,
  input  [5:0] Func0,
  input  [5:0] Func1,
  input  [4:0] ID_R1_num,
  input  [4:0] ID_R2_num,
  output out_8
);

  wire and_1_out, and_2_out, comparator_1_eq, comparator_2_eq, comparator_3_eq, or_1_out, R1_Used, R2_Used;

  \源寄存器使用情况  \u_源寄存器使用情况_1  (
    .OP0(OP0[0]), .OP1(OP0[1]), .OP2(OP0[2]), .OP3(OP0[3]), .OP4(OP0[4]), .OP5(OP0[5]), .F0(Func0[0]),
    .F1(Func0[1]), .F2(Func0[2]), .F3(Func0[3]), .F4(Func0[4]), .F5(Func0[5]), .R1_Used(R1_Used),
    .R2_Used(R2_Used));
  Comparator #(.width(6)) comparator_1 (.a(OP1), .b(6'b100011), .eq(comparator_1_eq));  // open: gt, lt
  Comparator #(.width(5)) comparator_2 (.a(ID_R1_num), .b(EX_WriteReg_num), .eq(comparator_2_eq));  // open: gt, lt
  Comparator #(.width(5)) comparator_3 (.a(ID_R2_num), .b(EX_WriteReg_num), .eq(comparator_3_eq));  // open: gt, lt
  and and_1 (and_1_out, R1_Used, comparator_2_eq);
  and and_2 (and_2_out, R2_Used, comparator_3_eq);
  or or_1 (or_1_out, and_1_out, and_2_out);
  and and_3 (out_8, comparator_1_eq, or_1_out);

  // Other names for the same wires on the sheet: loaduse = out_8
endmodule

module BHT (
  input  [31:0] \写入PC ,
  input  \预测位写入 ,
  input  [31:0] \读入PC ,
  input  CLK,
  input  [1:0] \预测位 ,
  input  [31:0] \目标地址 ,
  input  \写入 ,
  output Hit2,
  output Hit,
  output [1:0] \历史预测位 ,
  output [31:0] DataOut
);

  wire and_1_out, and_2_out, and_3_out, and_4_out, and_5_out, and_6_out, and_7_out, and_8_out, and_9_out,
       and_10_out, and_11_out, and_12_out, and_13_out, and_14_out, and_15_out, and_16_out, and_36_out,
       and_37_out, and_38_out, and_39_out, and_40_out, and_41_out, and_42_out, and_43_out, and_44_out,
       and_45_out, and_46_out, and_47_out, and_48_out, and_49_out, and_50_out, and_51_out, and_52_out,
       and_53_out, and_54_out, and_55_out, and_56_out, and_57_out, and_58_out, and_59_out, change,
       comparator_1_eq, comparator_2_eq, comparator_3_eq, comparator_4_eq, comparator_5_eq, comparator_6_eq,
       comparator_7_eq, comparator_8_eq, comparator_9_eq, comparator_10_eq, comparator_11_eq,
       comparator_12_eq, comparator_13_eq, comparator_14_eq, comparator_15_eq, comparator_16_eq,
       comparator_17_eq, L0, L1, L2, L3, L4, L5, L6, L7, M0, M1, M2, M3, M4, M5, M6, M7, Miss, or_1_out,
       or_2_out, or_3_out, or_4_out, or_5_out, or_6_out, or_7_out, or_8_out, or_11_out, or_12_out, or_13_out,
       or_14_out, or_15_out, or_16_out, or_17_out, or_18_out, or_27_out, R0, R1, R2, R3, R4, R5, R6, R7, T0,
       T1, T2, T3, T4, T5, T6, T7, V0, V1, V2, V3, V4, V5, V6, V7, \不写入 , \无效写入 , \相等 ;
  wire [1:0] multiplexer_3_out, \历史预测位1 , \数据块副本_9_q , \数据块副本_10_q , \数据块副本_11_q , \数据块副本_12_q ,
       \数据块副本_13_q , \数据块副本_14_q , \数据块副本_15_q , \数据块副本_16_q ;
  wire [2:0] Max, max3_1_max_num, max3_2_max_num, max3_3_max_num, max3_4_max_num, max3_5_max_num,
       max3_6_max_num;
  wire [9:0] \数据块副本_2_q_2 , \数据块副本_3_q_2 , \数据块副本_q_2 ;
  wire [15:0] C0, C1, C2, C3, C4, C5, C6, C7, max3_1_max, max3_2_max, max3_3_max, max3_4_max, max3_5_max,
       max3_6_max, register_1_q, register_2_q, register_3_q, register_4_q, register_5_q, register_6_q,
       register_7_q, register_8_q;
  wire [31:0] DataOut1, multiplexer_1_out, Tag0, Tag1, Tag2, Tag3, Tag4, Tag5, Tag6, Tag7, \数据块副本_2_q ,
       \数据块副本_3_q , \数据块副本_4_q , \数据块副本_5_q , \数据块副本_6_q , \数据块副本_7_q , \数据块副本_8_q , \数据块副本_q ;

  Register #(.width(1)) valid (.D(1'b1), .en(R0), .Q(V0), .clk(CLK));  // open: clr
  Register #(.width(1)) valid_2 (.D(1'b1), .en(R1), .Q(V1), .clk(CLK));  // open: clr
  Register #(.width(1)) valid_3 (.D(1'b1), .en(R2), .Q(V2), .clk(CLK));  // open: clr
  Register #(.width(1)) valid_4 (.D(1'b1), .en(R3), .Q(V3), .clk(CLK));  // open: clr
  Register #(.width(1)) valid_5 (.D(1'b1), .en(R4), .Q(V4), .clk(CLK));  // open: clr
  Register #(.width(1)) valid_6 (.D(1'b1), .en(R5), .Q(V5), .clk(CLK));  // open: clr
  Register #(.width(1)) valid_7 (.D(1'b1), .en(R6), .Q(V6), .clk(CLK));  // open: clr
  Register #(.width(1)) valid_8 (.D(1'b1), .en(R7), .Q(V7), .clk(CLK));  // open: clr
  // Probe on \读入PC [11:2]
  // Probe on \目标地址 
  // Probe on Tag0[11:2]
  Register #(.width(32)) \u_标记位  (.D(\写入PC ), .en(R0), .Q(Tag0), .clk(CLK));  // open: clr
  // Probe on Tag1[11:2]
  Register #(.width(32)) \u_标记位_2  (.D(\写入PC ), .en(R1), .Q(Tag1), .clk(CLK));  // open: clr
  // Probe on Tag2[11:2]
  Register #(.width(32)) \u_标记位_3  (.D(\写入PC ), .en(R2), .Q(Tag2), .clk(CLK));  // open: clr
  Register #(.width(32)) \u_标记位_4  (.D(\写入PC ), .en(R3), .Q(Tag3), .clk(CLK));  // open: clr
  Register #(.width(32)) \u_标记位_5  (.D(\写入PC ), .en(R4), .Q(Tag4), .clk(CLK));  // open: clr
  Register #(.width(32)) \u_标记位_6  (.D(\写入PC ), .en(R5), .Q(Tag5), .clk(CLK));  // open: clr
  // Probe on Tag6[11:2]
  Register #(.width(32)) \u_标记位_7  (.D(\写入PC ), .en(R6), .Q(Tag6), .clk(CLK));  // open: clr
  // Probe on Tag7[11:2]
  Register #(.width(32)) \u_标记位_8  (.D(\写入PC ), .en(R7), .Q(Tag7), .clk(CLK));  // open: clr
  // Probe on C0
  Counter #(.width(16), .max('hffff), .ongoal("stay")) \u_淘汰标志位  (
    .count(1'b1), .Q(C0), .clk(CLK), .clr(and_1_out));  // open: load, D, carry
  and and_1 (and_1_out, V0, or_1_out);
  or or_1 (or_1_out, M0, R0);
  // Probe on C1
  Counter #(.width(16), .max('hffff), .ongoal("stay")) \u_淘汰标志位_2  (
    .count(1'b1), .Q(C1), .clk(CLK), .clr(and_2_out));  // open: load, D, carry
  and and_2 (and_2_out, V1, or_2_out);
  or or_2 (or_2_out, M1, R1);
  // Probe on C2
  Counter #(.width(16), .max('hffff), .ongoal("stay")) \u_淘汰标志位_3  (
    .count(1'b1), .Q(C2), .clk(CLK), .clr(and_3_out));  // open: load, D, carry
  and and_3 (and_3_out, V2, or_3_out);
  or or_3 (or_3_out, M2, R2);
  // Probe on C3
  Counter #(.width(16), .max('hffff), .ongoal("stay")) \u_淘汰标志位_4  (
    .count(1'b1), .Q(C3), .clk(CLK), .clr(and_4_out));  // open: load, D, carry
  and and_4 (and_4_out, V3, or_4_out);
  or or_4 (or_4_out, M3, R3);
  Counter #(.width(16), .max('hffff), .ongoal("stay")) \u_淘汰标志位_5  (
    .count(1'b1), .Q(C4), .clk(CLK), .clr(and_5_out));  // open: load, D, carry
  and and_5 (and_5_out, V4, or_5_out);
  or or_5 (or_5_out, M4, R4);
  Counter #(.width(16), .max('hffff), .ongoal("stay")) \u_淘汰标志位_6  (
    .count(1'b1), .Q(C5), .clk(CLK), .clr(and_6_out));  // open: load, D, carry
  and and_6 (and_6_out, V5, or_6_out);
  or or_6 (or_6_out, M5, R5);
  Counter #(.width(16), .max('hffff), .ongoal("stay")) \u_淘汰标志位_7  (
    .count(1'b1), .Q(C6), .clk(CLK), .clr(and_7_out));  // open: load, D, carry
  and and_7 (and_7_out, V6, or_7_out);
  or or_7 (or_7_out, M6, R6);
  Counter #(.width(16), .max('hffff)) \u_淘汰标志位_8  (
    .count(1'b1), .Q(C7), .clk(CLK), .clr(and_8_out));  // open: load, D, carry
  and and_8 (and_8_out, V7, or_8_out);
  or or_8 (or_8_out, M7, R7);
  and and_9 (and_9_out, R0, \写入 );
  and and_10 (and_10_out, R1, \写入 );
  and and_11 (and_11_out, R2, \写入 );
  and and_12 (and_12_out, R3, \写入 );
  and and_13 (and_13_out, R4, \写入 );
  and and_14 (and_14_out, R5, \写入 );
  and and_15 (and_15_out, R6, \写入 );
  and and_16 (and_16_out, R7, \写入 );
  // Probe on \数据块副本_q_2 
  Register #(.width(32)) \u_数据块副本  (
    .D(\目标地址 ), .en(and_9_out), .Q({\数据块副本_q [31:12], \数据块副本_q_2 , \数据块副本_q [1:0]}), .clk(CLK));  // open: clr
  assign DataOut1 = M0 ? {\数据块副本_q [31:12], \数据块副本_q_2 , \数据块副本_q [1:0]} : 32'bz;  // Controlled_Buffer controlled_buffer_1
  // Probe on \数据块副本_2_q_2 
  Register #(.width(32)) \u_数据块副本_2  (
    .D(\目标地址 ), .en(and_10_out), .Q({\数据块副本_2_q [31:12], \数据块副本_2_q_2 , \数据块副本_2_q [1:0]}), .clk(CLK));  // open: clr
  assign DataOut1 = M1 ? {\数据块副本_2_q [31:12], \数据块副本_2_q_2 , \数据块副本_2_q [1:0]} : 32'bz;  // Controlled_Buffer controlled_buffer_2
  // Probe on \数据块副本_3_q_2 
  assign DataOut1 = M2 ? {\数据块副本_3_q [31:12], \数据块副本_3_q_2 , \数据块副本_3_q [1:0]} : 32'bz;  // Controlled_Buffer controlled_buffer_3
  Register #(.width(32)) \u_数据块副本_3  (
    .D(\目标地址 ), .en(and_11_out), .Q({\数据块副本_3_q [31:12], \数据块副本_3_q_2 , \数据块副本_3_q [1:0]}), .clk(CLK));  // open: clr
  assign DataOut1 = M3 ? \数据块副本_4_q  : 32'bz;  // Controlled_Buffer controlled_buffer_4
  Register #(.width(32)) \u_数据块副本_4  (.D(\目标地址 ), .en(and_12_out), .Q(\数据块副本_4_q ), .clk(CLK));  // open: clr
  Register #(.width(32)) \u_数据块副本_5  (.D(\目标地址 ), .en(and_13_out), .Q(\数据块副本_5_q ), .clk(CLK));  // open: clr
  assign DataOut1 = M4 ? \数据块副本_5_q  : 32'bz;  // Controlled_Buffer controlled_buffer_5
  assign DataOut1 = M5 ? \数据块副本_6_q  : 32'bz;  // Controlled_Buffer controlled_buffer_6
  Register #(.width(32)) \u_数据块副本_6  (.D(\目标地址 ), .en(and_14_out), .Q(\数据块副本_6_q ), .clk(CLK));  // open: clr
  assign DataOut1 = M6 ? \数据块副本_7_q  : 32'bz;  // Controlled_Buffer controlled_buffer_7
  Register #(.width(32)) \u_数据块副本_7  (.D(\目标地址 ), .en(and_15_out), .Q(\数据块副本_7_q ), .clk(CLK));  // open: clr
  Register #(.width(32)) \u_数据块副本_8  (.D(\目标地址 ), .en(and_16_out), .Q(\数据块副本_8_q ), .clk(CLK));  // open: clr
  assign DataOut1 = M7 ? \数据块副本_8_q  : 32'bz;  // Controlled_Buffer controlled_buffer_8
  assign \历史预测位1  = M0 ? \数据块副本_9_q  : 2'bz;  // Controlled_Buffer controlled_buffer_9
  Register #(.width(2)) \u_数据块副本_9  (.D(\预测位 ), .en(R0), .Q(\数据块副本_9_q ), .clk(CLK));  // open: clr
  assign \历史预测位1  = M1 ? \数据块副本_10_q  : 2'bz;  // Controlled_Buffer controlled_buffer_10
  Register #(.width(2)) \u_数据块副本_10  (.D(\预测位 ), .en(R1), .Q(\数据块副本_10_q ), .clk(CLK));  // open: clr
  assign \历史预测位1  = M2 ? \数据块副本_11_q  : 2'bz;  // Controlled_Buffer controlled_buffer_11
  Register #(.width(2)) \u_数据块副本_11  (.D(\预测位 ), .en(R2), .Q(\数据块副本_11_q ), .clk(CLK));  // open: clr
  assign \历史预测位1  = M3 ? \数据块副本_12_q  : 2'bz;  // Controlled_Buffer controlled_buffer_12
  Register #(.width(2)) \u_数据块副本_12  (.D(\预测位 ), .en(R3), .Q(\数据块副本_12_q ), .clk(CLK));  // open: clr
  Register #(.width(2)) \u_数据块副本_13  (.D(\预测位 ), .en(R4), .Q(\数据块副本_13_q ), .clk(CLK));  // open: clr
  assign \历史预测位1  = M4 ? \数据块副本_13_q  : 2'bz;  // Controlled_Buffer controlled_buffer_13
  Register #(.width(2)) \u_数据块副本_14  (.D(\预测位 ), .en(R5), .Q(\数据块副本_14_q ), .clk(CLK));  // open: clr
  assign \历史预测位1  = M5 ? \数据块副本_14_q  : 2'bz;  // Controlled_Buffer controlled_buffer_14
  Register #(.width(2)) \u_数据块副本_15  (.D(\预测位 ), .en(R6), .Q(\数据块副本_15_q ), .clk(CLK));  // open: clr
  assign \历史预测位1  = M6 ? \数据块副本_15_q  : 2'bz;  // Controlled_Buffer controlled_buffer_15
  assign \历史预测位1  = M7 ? \数据块副本_16_q  : 2'bz;  // Controlled_Buffer controlled_buffer_16
  Register #(.width(2)) \u_数据块副本_16  (.D(\预测位 ), .en(R7), .Q(\数据块副本_16_q ), .clk(CLK));  // open: clr
  Multiplexer #(.width(32), .enable("false")) multiplexer_1 (
    .in0({32{1'b0}}), .in1(DataOut1), .out(multiplexer_1_out), .sel(Hit2));
  // Probe on DataOut
  Multiplexer #(.width(32), .enable("false")) multiplexer_2 (
    .in0(multiplexer_1_out), .in1(\目标地址 ), .out(DataOut), .sel(\相等 ));
  Decoder #(.select(3), .disabled(0)) decoder_1 (
    .out0(T0), .out1(T1), .out2(T2), .out3(T3), .out4(T4), .out5(T5), .out6(T6), .out7(T7), .sel(Max),
    .en(change));
  Comparator #(.width(10)) comparator_1 (.a(\写入PC [11:2]), .b(Tag0[11:2]), .eq(comparator_1_eq));  // open: gt, lt
  Comparator #(.width(10)) comparator_2 (.a(\写入PC [11:2]), .b(Tag1[11:2]), .eq(comparator_2_eq));  // open: gt, lt
  Comparator #(.width(10)) comparator_3 (.a(\写入PC [11:2]), .b(Tag2[11:2]), .eq(comparator_3_eq));  // open: gt, lt
  Comparator #(.width(10)) comparator_4 (.a(\写入PC [11:2]), .b(Tag3[11:2]), .eq(comparator_4_eq));  // open: gt, lt
  Comparator #(.width(10)) comparator_5 (.a(\写入PC [11:2]), .b(Tag4[11:2]), .eq(comparator_5_eq));  // open: gt, lt
  Comparator #(.width(10)) comparator_6 (.a(\写入PC [11:2]), .b(Tag5[11:2]), .eq(comparator_6_eq));  // open: gt, lt
  Comparator #(.width(10)) comparator_7 (.a(\写入PC [11:2]), .b(Tag6[11:2]), .eq(comparator_7_eq));  // open: gt, lt
  Comparator #(.width(10)) comparator_8 (.a(\写入PC [11:2]), .b(Tag7[11:2]), .eq(comparator_8_eq));  // open: gt, lt
  Comparator #(.width(10)) comparator_9 (.a(\读入PC [11:2]), .b(Tag0[11:2]), .eq(comparator_9_eq));  // open: gt, lt
  Comparator #(.width(10)) comparator_10 (.a(\读入PC [11:2]), .b(Tag1[11:2]), .eq(comparator_10_eq));  // open: gt, lt
  Comparator #(.width(10)) comparator_11 (.a(\读入PC [11:2]), .b(Tag2[11:2]), .eq(comparator_11_eq));  // open: gt, lt
  Comparator #(.width(10)) comparator_12 (.a(\读入PC [11:2]), .b(Tag3[11:2]), .eq(comparator_12_eq));  // open: gt, lt
  Comparator #(.width(10)) comparator_13 (.a(\读入PC [11:2]), .b(Tag4[11:2]), .eq(comparator_13_eq));  // open: gt, lt
  Comparator #(.width(10)) comparator_14 (.a(\读入PC [11:2]), .b(Tag5[11:2]), .eq(comparator_14_eq));  // open: gt, lt
  Comparator #(.width(10)) comparator_15 (.a(\读入PC [11:2]), .b(Tag6[11:2]), .eq(comparator_15_eq));  // open: gt, lt
  Comparator #(.width(10)) comparator_16 (.a(\读入PC [11:2]), .b(Tag7[11:2]), .eq(comparator_16_eq));  // open: gt, lt
  Multiplexer #(.width(2), .enable("false")) multiplexer_3 (
    .in0(2'b01), .in1(\历史预测位1 ), .out(multiplexer_3_out), .sel(Hit2));
  and and_17 (change, V0, V1, V2, V3, Miss, V4, V5, V6, V7);
  and and_18 (L0, comparator_1_eq, V0);
  and and_19 (L1, comparator_2_eq, V1);
  and and_20 (L2, comparator_3_eq, V2);
  and and_21 (L3, comparator_4_eq, V3);
  and and_22 (L4, comparator_5_eq, V4);
  and and_23 (L5, comparator_6_eq, V5);
  and and_24 (L6, comparator_7_eq, V6);
  and and_25 (L7, comparator_8_eq, V7);
  and and_26 (M0, comparator_9_eq, V0);
  and and_27 (M1, comparator_10_eq, V1);
  and and_28 (M2, comparator_11_eq, V2);
  and and_29 (M3, comparator_12_eq, V3);
  and and_30 (M4, comparator_13_eq, V4);
  and and_31 (M5, comparator_14_eq, V5);
  and and_32 (M6, comparator_15_eq, V6);
  and and_33 (M7, comparator_16_eq, V7);
  // Probe on \历史预测位 
  Multiplexer #(.width(2), .enable("false")) multiplexer_4 (
    .in0(multiplexer_3_out), .in1(\预测位 ), .out(\历史预测位 ), .sel(\相等 ));
  or or_9 (Hit, L0, L1, L2, L3, L4, L5, L6, L7);
  or or_10 (Hit2, M0, M1, M2, M3, M4, M5, M6, M7);
  and and_34 (\无效写入 , \预测位写入 , \不写入 );
  not not_1 (Miss, Hit);
  Comparator #(.width(32)) comparator_17 (.a(\读入PC ), .b(\写入PC ), .eq(comparator_17_eq));  // open: gt, lt
  and and_35 (\相等 , comparator_17_eq, Hit2);
  and and_36 (and_36_out, Miss, ~V0);  // AND_Gate
  and and_37 (and_37_out, V0, Miss, ~V1);  // AND_Gate
  and and_38 (and_38_out, V1, V0, Miss, ~V2);  // AND_Gate
  and and_39 (and_39_out, V2, V1, V0, Miss, ~V3);  // AND_Gate
  and and_40 (and_40_out, V3, V2, V1, V0, Miss, ~V4);  // AND_Gate
  and and_41 (and_41_out, V4, V3, V2, V1, V0, Miss, ~V5);  // AND_Gate
  and and_42 (and_42_out, V5, V4, V3, V2, V1, V0, Miss, ~V6);  // AND_Gate
  and and_43 (and_43_out, V6, V5, V4, V3, V2, V1, V0, Miss, ~V7);  // AND_Gate
  or or_11 (or_11_out, and_36_out, T0);
  or or_12 (or_12_out, and_37_out, T1);
  or or_13 (or_13_out, and_38_out, T2);
  or or_14 (or_14_out, and_39_out, T3);
  or or_15 (or_15_out, and_40_out, T4);
  or or_16 (or_16_out, and_41_out, T5);
  or or_17 (or_17_out, and_42_out, T6);
  or or_18 (or_18_out, and_43_out, T7);
  Register #(.width(16)) register_1 (.D(C0), .Q(register_1_q), .clk(CLK));  // open: en, clr
  Register #(.width(16)) register_2 (.D(C1), .Q(register_2_q), .clk(CLK));  // open: en, clr
  Register #(.width(16)) register_3 (.D(C2), .Q(register_3_q), .clk(CLK));  // open: en, clr
  Register #(.width(16)) register_4 (.D(C3), .Q(register_4_q), .clk(CLK));  // open: en, clr
  Register #(.width(16)) register_5 (.D(C4), .Q(register_5_q), .clk(CLK));  // open: en, clr
  Register #(.width(16)) register_6 (.D(C5), .Q(register_6_q), .clk(CLK));  // open: en, clr
  Register #(.width(16)) register_7 (.D(C6), .Q(register_7_q), .clk(CLK));  // open: en, clr
  Register #(.width(16)) register_8 (.D(C7), .Q(register_8_q), .clk(CLK));  // open: en, clr
  and and_44 (and_44_out, or_11_out, \写入 );
  and and_45 (and_45_out, or_12_out, \写入 );
  and and_46 (and_46_out, or_13_out, \写入 );
  and and_47 (and_47_out, or_14_out, \写入 );
  and and_48 (and_48_out, or_15_out, \写入 );
  and and_49 (and_49_out, or_16_out, \写入 );
  and and_50 (and_50_out, or_17_out, \写入 );
  and and_51 (and_51_out, or_18_out, \写入 );
  Max3 max3_1 (
    .Y(register_2_q), .X(register_1_q), .Y_num(3'b001), .X_num(3'b000), .MAX(max3_1_max),
    .Max_num(max3_1_max_num));
  Max3 max3_2 (
    .Y(register_4_q), .X(register_3_q), .Y_num(3'b011), .X_num(3'b010), .MAX(max3_2_max),
    .Max_num(max3_2_max_num));
  Max3 max3_3 (
    .Y(register_6_q), .X(register_5_q), .Y_num(3'b101), .X_num(3'b100), .MAX(max3_3_max),
    .Max_num(max3_3_max_num));
  Max3 max3_4 (
    .Y(register_8_q), .X(register_7_q), .Y_num(3'b111), .X_num(3'b110), .MAX(max3_4_max),
    .Max_num(max3_4_max_num));
  and and_52 (and_52_out, \预测位写入 , V0, L0);
  and and_53 (and_53_out, \预测位写入 , V1, L1);
  and and_54 (and_54_out, \预测位写入 , V2, L2);
  and and_55 (and_55_out, \预测位写入 , V3, L3);
  and and_56 (and_56_out, \预测位写入 , V4, L4);
  and and_57 (and_57_out, \预测位写入 , V5, L5);
  and and_58 (and_58_out, \预测位写入 , V6, L6);
  and and_59 (and_59_out, \预测位写入 , V7, L7);
  Max3 max3_5 (
    .Y(max3_2_max), .X(max3_1_max), .Y_num(max3_2_max_num), .X_num(max3_1_max_num), .MAX(max3_5_max),
    .Max_num(max3_5_max_num));
  Max3 max3_6 (
    .Y(max3_4_max), .X(max3_3_max), .Y_num(max3_4_max_num), .X_num(max3_3_max_num), .MAX(max3_6_max),
    .Max_num(max3_6_max_num));
  or or_19 (R0, and_52_out, and_44_out);
  or or_20 (R1, and_53_out, and_45_out);
  or or_21 (R2, and_54_out, and_46_out);
  or or_22 (R3, and_55_out, and_47_out);
  or or_23 (R4, and_56_out, and_48_out);
  or or_24 (R5, and_57_out, and_49_out);
  or or_25 (R6, and_58_out, and_50_out);
  or or_26 (R7, and_59_out, and_51_out);
  or or_27 (or_27_out, R0, R1, R2, R3, R4, R5, R6, R7);
  not not_2 (\不写入 , or_27_out);
  Max3 max3_7 (
    .Y(max3_6_max), .X(max3_5_max), .Y_num(max3_6_max_num), .X_num(max3_5_max_num), .Max_num(Max));  // open: MAX

  // Other names for the same wires on the sheet: Tag[31:0] = \写入PC 

  // Notes on the sheet:
  //   输入引脚区
  //   输出引脚区
  //   替换标志
  //   使用标志
endmodule

module Max3 (
  input  [15:0] Y,
  input  [15:0] X,
  input  [2:0] Y_num,
  input  [2:0] X_num,
  output [15:0] MAX,
  output [2:0] Max_num
);

  wire comparator_1_eq, comparator_1_gt, or_1_out;

  Multiplexer #(.width(16), .enable("false")) multiplexer_1 (.in0(Y), .in1(X), .out(MAX), .sel(or_1_out));
  Comparator #(.width(16), .mode("unsigned")) comparator_1 (
    .a(X), .b(Y), .gt(comparator_1_gt), .eq(comparator_1_eq));  // open: lt
  or or_1 (or_1_out, comparator_1_gt, comparator_1_eq);
  Multiplexer #(.width(3), .enable("false")) multiplexer_2 (.in0(Y_num), .in1(X_num), .out(Max_num), .sel(or_1_out));

  // Notes on the sheet:
  //   输出两个输入中的较大值，并输出较大值的3位编号
endmodule

module \分支预测状态机  (
  input  [1:0] fr,
  input  success,
  output [1:0] fr_2,
  output \预测位写入 ,
  output \写入 ,
  output \跳转错误 
);

  wire and_1_out, and_2_out, and_3_out, and_4_out, comparator_1_eq, not_1_out, not_2_out, not_3_out,
       not_4_out, not_5_out;

  Comparator #(.width(2), .mode("unsigned")) comparator_1 (.a(fr), .b(fr_2), .eq(comparator_1_eq));  // open: gt, lt
  and and_1 (and_1_out, fr[0], success);
  and and_2 (and_2_out, fr[1], not_1_out);
  not not_1 (not_1_out, fr[0]);
  not not_2 (not_2_out, fr[1]);
  and and_3 (and_3_out, not_2_out, not_3_out, success);
  not not_3 (not_3_out, fr[0]);
  and and_4 (and_4_out, fr[1], not_4_out, not_5_out);
  not not_4 (not_4_out, fr[0]);
  not not_5 (not_5_out, success);
  not not_6 (\预测位写入 , comparator_1_eq);
  xor xor_1 (\跳转错误 , success, fr[1]);
  or or_1 (fr_2[1], and_1_out, and_2_out);
  or or_2 (fr_2[0], and_3_out, and_4_out);
  and and_5 (\写入 , \预测位写入 , success);

  // Other names for the same wires on the sheet: fr_in[1:0] = fr; fr_t[1:0] = fr_2
endmodule
module \分支预测流水线  (
  output [31:0] out_1,
  output [4:0] out_2,
  output [4:0] out_3,
  output [31:0] out_4,
  output [4:0] out_5,
  output [31:0] out_6
);

  wire Alus, AlusEx, and_1_out, and_2_out, and_3_out, and_4_out, and_5_out, and_6_out, and_7_out, and_11_out,
       and_12_out, and_13_out, and_14_out, and_15_out, and_16_out, Beq, BeqEx, BLEZ, BLEZEx, BLEZM, BLEZWB,
       Bne, BneEx, branch, CLK, comparator_1_eq, comparator_2_eq, comparator_3_eq, comparator_4_eq,
       comparator_5_eq, comparator_6_eq, comparator_7_eq, comparator_8_eq, comparator_9_eq, comparator_10_eq,
       comparator_11_eq, comparator_12_gt, comparator_13_eq, condi, equ, Go, halt, Hit, Hit2, IR1, IR2, IR3,
       JAL, JALEx, JALM, JALWB, JMP, JMPEx, JR, JREx, ldEX, ldM, led, loaduse, MemToReg, MemToRegEx,
       MemToRegM, MemToRegWB, MemWrite, MemWriteEx, MemWriteM, nor_1_out, or_3_out, or_4_out, or_5_out,
       or_6_out, or_7_out, or_9_out, or_10_out, or_13_out, pause, PC_7_q, pcen, RegDst, RegDstEx, RegDstM,
       RegDstWB, RegWrite, RegWriteEx, RegWriteM, RegWriteWB, RST, SB, SBEx, SBM, SignedExt, SignedExtEx,
       SRAV, SRAVEx, SRAVM, SRAVWB, Sys, SysEx, SysFinal, SysI, SysM, SysWB, W1, W2, W3, \写入 , \跳转 , \跳转错误 ,
       \预测位写入 ;
  wire [1:0] EX_forcast, f1EX, f2EX, forward1, forward2, ID_forcast, IF_forcast, NEW_forcast;
  wire [1:1] PCSrc;
  wire [3:0] Aluop, AluopEx, multiplexer_18_out, multiplexer_19_out;
  wire [4:0] multiplexer_12_out, R2_num, W_M;
  wire [15:0] \LoadUse次数 , \总周期数 , \插入气泡数 , \无条件分支数 , \条件分支成功数 , \跳转错误次数 , \跳转错误次数2 ;
  wire [31:0] adder_1_out, adder_3_out, ALUA, ALUB, bit_extender_1_out, bit_extender_2_out,
       bit_extender_3_out, bit_extender_4_out, EX_PC, Ext, ExtEX, final_pc, FinalMemData, ForCast_PC, ID_PC,
       IF_PC, IREX, IRID, IRM, IRWB, JALWBD, LedData, MDWB, MEM_PC, MemData, MemDataWB, mips_regifile_1_r2,
       multiplexer_2_out, multiplexer_11_out, multiplexer_16_out, multiplexer_20_out, pc0, pc1, PCWB, R1ID,
       R2EX, R2ID, R2M, result, resultM, resultWB, rom_1_data, shifter_1_out, shifter_2_out, shifter_3_out,
       shifter_4_out;

  Button \u_总复位  (.out(RST));
  Button _1 (.out(IR1));
  Button _2 (.out(IR2));
  Button _3 (.out(IR3));
  Button \u_继续运行  (.out(Go));
  LED led_1 (.in(W1));
  LED led_2 (.in(W2));
  LED led_3 (.in(W3));
  and and_1 (and_1_out, Sys, halt);
  and and_2 (and_2_out, Sys, ~Go, pause);  // AND_Gate
  Multiplexer #(.select(2), .width(32), .enable("false")) multiplexer_1 (
    .in0(pc0), .in1(pc1), .in2(out_6), .in3({pc0[31:28], IREX[25:0], 2'b00}), .out(out_1),
    .sel({PCSrc[1], JMPEx}));
  or or_1 (\跳转 , JMPEx, JREx, condi);
  and and_3 (and_3_out, Hit2, IF_forcast[1]);
  Hex_Digit_Display hex_digit_display_1 (.value(LedData[31:28]));  // open: dp
  or or_2 (SysI, and_1_out, and_2_out);
  assign bit_extender_1_out = {{16{1'b0}}, IRID[15:0]};  // Bit_Extender bit_extender_1
  assign bit_extender_2_out = {{16{IRID[15]}}, IRID[15:0]};  // Bit_Extender bit_extender_2
  Comparator #(.width(2)) comparator_1 (.a(forward1), .b(2'b00), .eq(comparator_1_eq));  // open: gt, lt
  Comparator #(.width(32)) comparator_2 (.a(R1ID), .b(32'h22), .eq(comparator_2_eq));  // open: gt, lt
  Comparator #(.width(32)) comparator_3 (.a(resultM), .b(32'h22), .eq(comparator_3_eq));  // open: gt, lt
  Comparator #(.width(2)) comparator_4 (.a(forward1), .b(2'b11), .eq(comparator_4_eq));  // open: gt, lt
  Comparator #(.width(2)) comparator_5 (.a(forward1), .b(2'b00), .eq(comparator_5_eq));  // open: gt, lt
  Comparator #(.width(32)) comparator_6 (.a(R1ID), .b(32'ha), .eq(comparator_6_eq));  // open: gt, lt
  Comparator #(.width(32)) comparator_7 (.a(resultM), .b(32'ha), .eq(comparator_7_eq));  // open: gt, lt
  Comparator #(.width(2)) comparator_8 (.a(forward1), .b(2'b11), .eq(comparator_8_eq));  // open: gt, lt
  \分支预测状态机  \u_分支预测状态机_1  (
    .fr(EX_forcast), .fr_2(NEW_forcast), .success(\跳转 ), .\预测位写入 (\预测位写入 ), .\写入 (\写入 ), .\跳转错误 (\跳转错误 ));
  Multiplexer #(.width(32), .enable("false")) multiplexer_2 (
    .in0(pc0), .in1(ForCast_PC), .out(multiplexer_2_out), .sel(and_3_out));
  Adder #(.width(32)) adder_1 (.a(EX_PC), .b(32'h4), .out(adder_1_out));  // open: cin, cout
  Hex_Digit_Display hex_digit_display_2 (.value(LedData[27:24]));  // open: dp
  Hex_Digit_Display hex_digit_display_3 (.value(LedData[23:20]));  // open: dp
  Register #(.width(32)) PC (.D(final_pc), .en(pcen), .Q(IF_PC), .clk(CLK), .clr(RST));
  Multiplexer #(.width(32), .enable("false")) multiplexer_3 (
    .in0(bit_extender_1_out), .in1(bit_extender_2_out), .out(Ext), .sel(SignedExt));
  and and_4 (and_4_out, comparator_1_eq, comparator_2_eq);
  and and_5 (and_5_out, comparator_3_eq, comparator_4_eq);
  and and_6 (and_6_out, comparator_5_eq, comparator_6_eq);
  and and_7 (and_7_out, comparator_7_eq, comparator_8_eq);
  BHT bht_1 (
    .\写入PC (EX_PC), .\预测位写入 (\预测位写入 ), .\读入PC (IF_PC), .CLK(CLK), .\预测位 (NEW_forcast), .\目标地址 (out_1),
    .\写入 (\写入 ), .Hit2(Hit2), .Hit(Hit), .\历史预测位 (IF_forcast), .DataOut(ForCast_PC));
  Multiplexer #(.select(2), .width(32), .enable("false")) multiplexer_4 (
    .in0(multiplexer_2_out), .in1(multiplexer_2_out), .in2(adder_1_out), .in3(out_1), .out(final_pc),
    .sel({\跳转错误 , \跳转 }));
  Hex_Digit_Display hex_digit_display_4 (.value(LedData[15:12]));  // open: dp
  Hex_Digit_Display hex_digit_display_5 (.value(LedData[19:16]));  // open: dp
  or or_3 (or_3_out, and_4_out, and_5_out);
  or or_4 (or_4_out, and_6_out, and_7_out);
  Hex_Digit_Display hex_digit_display_6 (.value(LedData[11:8]));  // open: dp
  Hex_Digit_Display hex_digit_display_7 (.value(LedData[7:4]));  // open: dp
  Clock clock_1 (.out(CLK));
  and and_8 (led, or_3_out, Sys);
  and and_9 (halt, Sys, or_4_out);
  nor nor_1 (nor_1_out, halt, led);
  and and_10 (pause, nor_1_out, Sys);
  Hex_Digit_Display hex_digit_display_8 (.value(LedData[3:0]));  // open: dp
  or or_5 (or_5_out, SysI, loaduse, ldEX, ldM);
  not not_1 (pcen, or_5_out);
  ROM #(.addrWidth(10), .dataWidth(32)) rom_1 (.addr(IF_PC[11:2]), .data(rom_1_data));  // open: sel
  // Probe on \总周期数 
  // Probe on \无条件分支数 
  // Probe on \条件分支成功数 
  // Probe on \插入气泡数 
  // Probe on \LoadUse次数 
  or or_6 (or_6_out, RST, \跳转错误 );
  IF_ID if_id_1 (
    .IR(rom_1_data), .PC(IF_PC), .CLK(CLK), .RST(or_6_out), .EN(or_5_out), .IROUT(IRID), .PCOUT(ID_PC),
    .forcast(IF_forcast), .forcast_out(ID_forcast));
  // Probe on IRID
  Multiplexer #(.width(5), .enable("false")) multiplexer_5 (.in0(IRID[25:21]), .in1(5'b00010), .out(out_5), .sel(Sys));
  Multiplexer #(.width(5), .enable("false")) multiplexer_6 (.in0(IRID[20:16]), .in1(5'b00100), .out(R2_num), .sel(Sys));
  // Probe on IF_PC[11:0]
  // Probe on out_2
  Multiplexer #(.select(2), .width(5), .enable("false")) multiplexer_7 (
    .in0(IREX[20:16]), .in1(IREX[15:11]), .in2({5{1'b1}}), .in3({5{1'b1}}), .out(out_3),
    .sel({JALEx, RegDstEx}));
  // Probe on ID_PC[11:0]
  \loaduse分析  \loaduse分析_1  (
    .OP0(IRID[31:26]), .OP1(IREX[31:26]), .EX_WriteReg_num(out_3), .Func0(IRID[5:0]), .Func1(IREX[5:0]),
    .ID_R1_num(out_5), .ID_R2_num(R2_num), .out_8(loaduse));
  // Probe on MEM_PC[11:0]
  // Probe on EX_PC[11:0]
  \硬布线控制器  \u_硬布线控制器_1  (
    .Func(IRID[5:0]), .OP(IRID[31:26]), .ALU_OP(Aluop), .MemToReg(MemToReg), .MemWrite(MemWrite),
    .ALU_SRC(Alus), .RegWrite(RegWrite), .SysCALL(Sys), .SignedExt(SignedExt), .RegDst(RegDst), .JR(JR),
    .JMP(JMP), .Beq(Beq), .JAL(JAL), .Bne(Bne), .SRAV(SRAV), .BLEZ(BLEZ), .SB(SB));  // open: MFC0, ERET
  MIPS_Regifile mips_regifile_1 (
    .Din(out_4), .Clk(CLK), .R1(R1ID), .R2(mips_regifile_1_r2), .WE(RegWriteWB), .W_num(out_2),
    .R1_num(out_5), .R2_num(R2_num));
  Comparator #(.width(5)) comparator_9 (.a(R2_num), .b(IRM[20:16]), .eq(comparator_9_eq));  // open: gt, lt
  Comparator #(.width(6)) comparator_10 (.a(IRID[31:26]), .b(6'b101000), .eq(comparator_10_eq));  // open: gt, lt
  Comparator #(.width(6)) comparator_11 (.a(IRM[31:26]), .b(6'b001000), .eq(comparator_11_eq));  // open: gt, lt
  Multiplexer #(.select(2), .width(5), .enable("false")) multiplexer_8 (
    .in0(IRM[20:16]), .in1(IRM[15:11]), .in2({5{1'b1}}), .in3({5{1'b1}}), .out(W_M), .sel({JALM, RegDstM}));
  Register #(.width(1)) PC_2 (.D(loaduse), .Q(ldEX), .clk(CLK));  // open: en, clr
  // Probe on PCWB[11:0]
  // Probe on mips_regifile_1_r2
  Multiplexer #(.width(32), .enable("false")) multiplexer_9 (
    .in0(mips_regifile_1_r2), .in1(resultM), .out(R2ID), .sel(and_11_out));
  and and_11 (and_11_out, comparator_9_eq, comparator_10_eq, comparator_11_eq);
  \重定向控制器  \u_重定向控制器_1  (
    .OP(IRID[31:26]), .EX_WriteReg_num(out_3), .EX_RegWrite(RegWriteEx), .MEM_mtr(MemToRegM),
    .MEM_WriteReg_num(W_M), .MEM_RegWrite(RegWriteM), .Func(IRID[5:0]), .ID_R1_num(out_5),
    .ID_R2_num(R2_num), .forward1(forward1), .forward2(forward2));
  // Probe on forward2
  Register #(.width(1)) PC_3 (.D(ldEX), .Q(ldM), .clk(CLK));  // open: en, clr
  // Probe on \跳转错误次数 
  Counter #(.width(16), .max('hffff)) counter_1 (
    .count(JMPEx), .Q(\无条件分支数 ), .clk(CLK), .clr(RST));  // open: load, D, carry
  Comparator #(.width(32)) comparator_12 (.a(pc1), .b({32{1'b0}}), .gt(comparator_12_gt));  // open: eq, lt
  and and_12 (and_12_out, JMPEx, ~JREx);  // AND_Gate
  Counter #(.width(16), .max('hffff)) counter_2 (
    .count(condi), .Q(\条件分支成功数 ), .clk(CLK), .clr(RST));  // open: load, D, carry
  or or_7 (or_7_out, loaduse, ldEX, ldM);
  and and_13 (and_13_out, BeqEx, equ);
  and and_14 (and_14_out, BneEx, ~equ);  // AND_Gate
  and and_15 (and_15_out, BLEZEx, ~comparator_12_gt);  // AND_Gate
  or or_8 (PCSrc[1], condi, and_12_out);
  Adder #(.width(32)) adder_2 (.a(IF_PC), .b(32'h4), .out(pc0));  // open: cin, cout
  Adder #(.width(32)) adder_3 (.a(EX_PC), .b(32'h4), .out(adder_3_out));  // open: cin, cout
  Shifter #(.width(32)) shifter_1 (.in(ExtEX), .\dist (5'b00010), .out(shifter_1_out));
  Counter #(.width(16), .max('hffff)) counter_3 (
    .count(SysFinal), .Q(\总周期数 ), .clk(CLK), .clr(RST));  // open: load, D, carry
  Counter #(.width(16), .max('hffff)) counter_4 (
    .count(or_9_out), .Q(\插入气泡数 ), .clk(CLK), .clr(RST));  // open: load, D, carry
  or or_9 (or_9_out, ldM, ldEX, loaduse, branch);
  or or_10 (or_10_out, RST, \跳转错误 , or_7_out);
  ID_EX id_ex_1 (
    .IR(IRID), .PC(ID_PC), .CLK(CLK), .RST(or_10_out), .EN(SysEx), .R1(R1ID), .R2(R2ID), .Beq(Beq),
    .JMP(JMP), .JR(JR), .Bne(Bne), .MemToReg(MemToReg), .SRAV(SRAV), .MemWrite(MemWrite), .BLEZ(BLEZ),
    .ALUop(Aluop), .SB(SB), .Alus(Alus), .RegWrite(RegWrite), .JAL(JAL), .RegDst(RegDst), .IRout(IREX),
    .PCout(EX_PC), .R1out(pc1), .R2out(R2EX), .JMP_out(JMPEx), .Beq_out(BeqEx), .JR_out(JREx),
    .Bne_out(BneEx), .MemToReg_out(MemToRegEx), .SRAV_out(SRAVEx), .MemWrite_out(MemWriteEx),
    .BLEZ_out(BLEZEx), .Aluop_out(AluopEx), .SB_out(SBEx), .Alus_out(AlusEx), .RegWrite_out(RegWriteEx),
    .JAL_out(JALEx), .RegDst_out(RegDstEx), .SignedExt(SignedExt), .SignedExt_out(SignedExtEx),
    .forward1(forward1), .f1out(f1EX), .forward2(forward2), .f2out(f2EX), .forcast(ID_forcast),
    .forcast_out(EX_forcast));  // open: SysDin, SysDout
  or or_11 (condi, and_13_out, and_14_out, and_15_out);
  Adder #(.width(32)) adder_4 (.a(adder_3_out), .b(shifter_1_out), .out(out_6));  // open: cin, cout
  Counter #(.width(16), .max('hffff)) counter_5 (
    .D(\插入气泡数 ), .count(loaduse), .Q(\LoadUse次数 ), .clk(CLK), .clr(RST));  // open: load, carry
  or or_12 (branch, JMPEx, condi);
  Counter #(.width(16), .max('hffff)) counter_6 (
    .count(\跳转错误 ), .Q(\跳转错误次数 ), .clk(CLK), .clr(RST));  // open: load, D, carry
  Multiplexer #(.select(2), .width(32), .enable("false")) multiplexer_10 (
    .in0(pc1), .in1(MDWB), .in2(resultWB), .in3(resultM), .out(ALUA), .sel(f1EX));
  and and_16 (and_16_out, \跳转错误 , \跳转 );
  Multiplexer #(.width(32), .enable("false")) multiplexer_11 (
    .in0(ALUB), .in1(ExtEX), .out(multiplexer_11_out), .sel(AlusEx));
  Multiplexer #(.width(5), .enable("false")) multiplexer_12 (
    .in0(IREX[10:6]), .in1(pc1[4:0]), .out(multiplexer_12_out), .sel(SRAVEx));
  assign bit_extender_3_out = {{16{1'b0}}, IREX[15:0]};  // Bit_Extender bit_extender_3
  assign bit_extender_4_out = {{16{IREX[15]}}, IREX[15:0]};  // Bit_Extender bit_extender_4
  Counter #(.width(16), .max('hffff)) counter_7 (
    .count(and_16_out), .Q(\跳转错误次数2 ), .clk(CLK), .clr(RST));  // open: load, D, carry
  Comparator #(.width(32)) comparator_13 (.a(ALUA), .b(32'h22), .eq(comparator_13_eq));  // open: gt, lt
  MIPS_ALU mips_alu_1 (
    .X(ALUA), .Y(multiplexer_11_out), .AluOP(AluopEx), .Equal(equ), .Result(result),
    .shamt(multiplexer_12_out));  // open: Result_2
  Multiplexer #(.width(32), .enable("false")) multiplexer_13 (
    .in0(bit_extender_3_out), .in1(bit_extender_4_out), .out(ExtEX), .sel(SignedExtEx));
  Multiplexer #(.select(2), .width(32), .enable("false")) multiplexer_14 (
    .in0(R2EX), .in1(MDWB), .in2(resultWB), .in3(resultM), .out(ALUB), .sel(f2EX));
  Register #(.width(1), .trigger("falling")) PC_4 (.D(SysI), .Q(SysEx), .clk(CLK), .clr(RST));  // open: en
  Register #(.width(32)) register_1 (.D(ALUB), .en(comparator_13_eq), .Q(LedData), .clk(CLK), .clr(RST));
  Register #(.width(1), .trigger("falling")) PC_5 (.D(SysEx), .Q(SysM), .clk(CLK), .clr(RST));  // open: en
  Register #(.width(1), .trigger("falling")) PC_6 (.D(SysM), .Q(SysWB), .clk(CLK), .clr(RST));  // open: en
  EX_MEM ex_mem_1 (
    .CLK(CLK), .IR(IREX), .PC(EX_PC), .RST(RST), .EN(SysM), .result(result), .R2(R2EX),
    .MemToReg(MemToRegEx), .RegDst(RegDstEx), .JAL(JALEx), .BLEZ(BLEZEx), .SRAV(SRAVEx),
    .RegWrite(RegWriteEx), .MemWrite(MemWriteEx), .IRout(IRM), .PCout(MEM_PC), .resultout(resultM),
    .R2out(R2M), .MemToRegout(MemToRegM), .RegDstout(RegDstM), .JALout(JALM), .BLEZ_2(BLEZM),
    .SRAVout(SRAVM), .RegWrite_2(RegWriteM), .MemWriteOut(MemWriteM), .SB(SBEx), .SBout(SBM));  // open: sys, sysout
  or or_13 (or_13_out, ldEX, ldM);
  Register #(.width(1), .trigger("falling")) PC_7 (.D(SysWB), .Q(PC_7_q), .clk(CLK), .clr(RST));  // open: en
  // Probe on IRM
  Multiplexer #(.select(2), .width(5), .enable("false")) multiplexer_15 (
    .in0(IRWB[20:16]), .in1(IRWB[15:11]), .in2({5{1'b1}}), .in3({5{1'b1}}), .out(out_2),
    .sel({JALWB, RegDstWB}));
  Multiplexer #(.width(32), .enable("false")) multiplexer_16 (
    .in0(resultWB), .in1(MemDataWB), .out(multiplexer_16_out), .sel(MemToRegWB));
  Adder #(.width(32)) adder_5 (.a(PCWB), .b(32'h4), .out(JALWBD));  // open: cin, cout
  Multiplexer #(.width(32), .enable("false")) multiplexer_17 (
    .in0(multiplexer_16_out), .in1(JALWBD), .out(out_4), .sel(JALWB));
  and and_17 (SysFinal, ~or_13_out, ~PC_7_q);  // AND_Gate
  Multiplexer #(.select(2), .width(4), .enable("false")) multiplexer_18 (
    .in0(4'b0001), .in1(4'b0010), .in2(4'b0100), .in3(4'b1000), .out(multiplexer_18_out), .sel(resultM[1:0]));
  // Probe on resultM
  // Probe on multiplexer_19_out
  Multiplexer #(.width(4), .enable("false")) multiplexer_19 (
    .in0(4'b1111), .in1(multiplexer_18_out), .out(multiplexer_19_out), .sel(SBM));
  // MIPS_RAM mips_ram_1: pin names not known; wires that end beside it: {{10{1'b0}}, resultM[11:2]}, FinalMemData, MemWriteM, multiplexer_19_out, CLK, RST, MemData
  Shifter #(.width(32)) shifter_2 (.in(R2M), .\dist (5'b01000), .out(shifter_2_out));
  Shifter #(.width(32)) shifter_3 (.in(R2M), .\dist (5'b10000), .out(shifter_3_out));
  Shifter #(.width(32)) shifter_4 (.in(R2M), .\dist (5'b11000), .out(shifter_4_out));
  Multiplexer #(.select(2), .width(32), .enable("false")) multiplexer_20 (
    .in0(R2M), .in1(shifter_2_out), .in2(shifter_3_out), .in3(shifter_4_out), .out(multiplexer_20_out),
    .sel(resultM[1:0]));
  MEM_WB mem_wb_1 (
    .CLK(CLK), .IR(IRM), .PC(MEM_PC), .RST(RST), .EN(SysWB), .result(resultM), .MemData(MemData),
    .MemToReg(MemToRegM), .RegDst(RegDstM), .JAL(JALM), .BLEZ(BLEZM), .SRAV(SRAVM), .RegWrite(RegWriteM),
    .IRout(IRWB), .PCout(PCWB), .MemDataout(MemDataWB), .resultout(resultWB), .MemToRegout(MemToRegWB),
    .RegDstout(RegDstWB), .JALout(JALWB), .BLEZ_2(BLEZWB), .SRAVout(SRAVWB), .RegWrite_2(RegWriteWB));  // open: sys, sysout
  // Probe on R2M
  Multiplexer #(.width(32), .enable("false")) multiplexer_21 (
    .in0(R2M), .in1(multiplexer_20_out), .out(FinalMemData), .sel(SBM));
  // Probe on resultM[1:0]
  // Probe on IRWB
  // Probe on FinalMemData
  // Probe on resultWB

  // Other names for the same wires on the sheet: Din[31:0] = out_4; R1EX[31:0] = pc1; pc2[31:0] = out_6;
  //   pc3[31:2] = {pc0[31:28], IREX[25:0]}; PCEX[31:0] = EX_PC; PCID[31:0] = ID_PC; PCIF[31:0] = IF_PC;
  //   PCM[31:0] = MEM_PC; PCSrc[0] = JMPEx; R1_num[4:0] = out_5; SysID = SysI; W_EX[4:0] = out_3; W_WB[4:0] = out_2;
  //   WB_PC[31:0] = PCWB; 目标地址[31:0] = out_1

  // Notes on the sheet:
  //   中断源
  //   中断等待指示
  //   pcout
  //   数码管输出
  //   irout
  //   contents of rom_1 (hex, n*v repeats v):
  //   20110001 8000c05 20110001 20120002 20130003 8000c09 20110001 20120002 20130003 8000c0d 20110001
  //   20120002 20130003 8000c11 20110001 20120002 20130003 c000cf8 20100001 20110001 118fc0 112020
  //   20020022 c 118882 12200001 8000c15 112020 20020022 c 20110001 118880 112020 20020022 c 12200001
  //   8000c1f 20110001 118fc0 112020 20020022 c 1188c3 112020 20020022 c 118903 112020 20020022 c 118903
  //   112020 20020022 c 118903 112020 20020022 c 118903 112020 20020022 c 118903 112020 20020022 c 118903
  //   112020 20020022 c 118903 112020 20020022 c 20100001 109fc0 139fc3 8021 2012000c 24160003 26100001
  //   3210000f 20080008 20090001 139900 2709825 132020 20020022 c 1094022 1500fff9 22100001 2018000f
  //   2188024 108700 20080008 20090001 139902 2709825 132021 20020022 c 1094022 1500fff9 108702 2c9b022
  //   12c00001 8000c50 4020 1084027 84400 3508ffff 82021 20020022 c 2010ffff 20110000 ae300000 22100001
  //   22310004 ae300000 22100001 22310004 ae300000 22100001 22310004 ae300000 22100001 22310004 ae300000
  //   22100001 22310004 ae300000 22100001 22310004 ae300000 22100001 22310004 ae300000 22100001 22310004
  //   ae300000 22100001 22310004 ae300000 22100001 22310004 ae300000 22100001 22310004 ae300000 22100001
  //   22310004 ae300000 22100001 22310004 ae300000 22100001 22310004 ae300000 22100001 22310004 ae300000
  //   22100001 22310004 22100001 8020 2011003c 8e130000 8e340000 274402a 11000002 ae330000 ae140000
  //   2231fffc 1611fff8 102020 20020022 c 22100004 2011003c 1611fff2 20020032 c 20080001 20090003 20110876
  //   118d00 112020 20020022 c 200b0008 1118807 1318807 112020 20020022 c 216bffff 1560fff9 20020032 c
  //   2008ffff 20117777 112020 20020022 c 200b0010 3a31ffff 112020 20020022 c 216bffff 1560fffa 20020032 c
  //   20090000 200b0020 20110000 20120001 a1310000 112020 20020022 c 2328820 21290001 216bffff 1560fff8
  //   200b0008 20090000 8d310000 112020 20020022 c 21290004 216bffff 1560fff9 20020032 c 2011fff1 112020
  //   20020022 c 22310001 1a20fffb 2002000a c 20020032 c 20100000 22100001 102020 20020022 c 22100002
  //   102020 20020022 c 22100003 102020 20020022 c 22100004 102020 20020022 c 22100005 102020 20020022 c
  //   22100006 102020 20020022 c 22100007 102020 20020022 c 22100008 102020 20020022 20020022 c 3e00008
  //   重定向分析
  //   JMP
  //   JR
  //   OP
  //   Func
  //   流水调试日志用
  //   Beq
  //   Bne
  //   MemToReg
  //   MemWrite
  //   AluOP
  //   AluSrcB
  //   RegWrite
  //   JAL
  //   RegDst
  //   Syscall
  //   地址转移逻辑
  //   重定向选择
  //   写回值与地址计算
endmodule

module \单周期单级中断  (
  output [4:0] out_1,
  output [3:0] out_2,
  output [31:0] out_3,
  output [31:0] out_4,
  output [31:0] out_5,
  output [4:0] out_6,
  output [4:0] out_7
);

  wire \_1号中断 , \_1号中断等待指示 , \_2号中断 , \_2号中断等待指示 , \_3号中断 , \_3号中断等待指示 , Alus, and_4_out, and_5_out,
       and_6_out, and_7_out, and_8_out, and_9_out, and_10_out, and_11_out, Beq, BLEZ, Bne, CLK,
       comparator_1_eq, comparator_2_eq, comparator_4_gt, condi, d_ff_1_q, d_ff_2_q, d_ff_3_q, d_ff_4_q,
       demultiplexer_1_out1, demultiplexer_1_out2, demultiplexer_1_out3, equ, eret, Go, halt, IR1_q, IR2_2_q,
       IR2_q, JAL, JMP, JR, led, MemToReg, MemWrite, mfc0, nor_1_out, nor_2_out, not_1_out, not_2_out,
       or_1_out, or_3_out, or_8_out, or_9_out, or_10_out, pause, pcen, RegDst, register_2_q, RegWrite, RST,
       SB, SignedExt, SRAV, Sys;
  wire [1:0] intnum, nowint, priority_encoder_1_out, register_6_q;
  wire [1:1] and_12_out, PCSrc;
  wire [3:0] multiplexer_11_out, multiplexer_12_out;
  wire [4:0] CP0, multiplexer_4_out, multiplexer_5_out, multiplexer_6_out, multiplexer_7_out,
       multiplexer_10_out;
  wire [10:0] imm;
  wire [15:0] \总周期数 , \无条件分支数 , \条件分支成功数 ;
  wire [31:0] bit_extender_1_out, bit_extender_2_out, Ext, LedData, MemAddr, MemWrite_Data, mips_ram_1_p8,
       multiplexer_1_out, multiplexer_2_out, multiplexer_3_out, multiplexer_8_out, multiplexer_13_out,
       multiplexer_15_out, pc0, pc2, PC_q, register_1_q, shifter_1_out, shifter_2_out, shifter_3_out,
       shifter_4_out;
  wire [31:26] rom_1_data;

  Button _1 (.out(\_1号中断 ));
  Button _2 (.out(\_2号中断 ));
  Button _3 (.out(\_3号中断 ));
  or or_1 (or_1_out, intnum[0], intnum[1]);
  Register #(.width(32)) register_1 (.D(multiplexer_1_out), .en(or_1_out), .Q(register_1_q), .clk(CLK));  // open: clr
  Multiplexer #(.select(2), .width(32), .enable("false")) multiplexer_1 (
    .in0(pc0), .in1(out_5), .in2(pc2), .in3({pc0[31:28], out_6, out_7, out_1, imm, 2'b00}),
    .out(multiplexer_1_out), .sel({PCSrc[1], JMP}));
  LED _1_2 (.in(\_1号中断等待指示 ));
  LED _2_2 (.in(\_2号中断等待指示 ));
  LED _3_2 (.in(\_3号中断等待指示 ));
  // Probe on nowint
  Register #(.width(1)) register_2 (.D(eret), .Q(register_2_q), .clk(CLK));  // open: en, clr
  Comparator #(.width(32)) comparator_1 (.a(out_5), .b(32'h22), .eq(comparator_1_eq));  // open: gt, lt
  Comparator #(.width(32)) comparator_2 (.a(out_5), .b(32'ha), .eq(comparator_2_eq));  // open: gt, lt
  // Probe on intnum
  Multiplexer #(.width(32), .enable("false")) multiplexer_2 (
    .in0(multiplexer_1_out), .in1(register_1_q), .out(multiplexer_2_out), .sel(register_2_q));
  Button \u_总复位  (.out(RST));
  Button \u_继续运行  (.out(Go));
  Clock clock_1 (.out(CLK));
  and and_1 (led, comparator_1_eq, Sys);
  and and_2 (halt, Sys, comparator_2_eq);
  nor nor_1 (nor_1_out, halt, led);
  and and_3 (pause, nor_1_out, Sys);
  Multiplexer #(.select(2), .width(32), .enable("false")) multiplexer_3 (
    .in0(multiplexer_2_out), .in1(32'h128), .in2(32'h1c0), .in3(32'h258), .out(multiplexer_3_out),
    .sel(intnum));
  // Probe on PC_q[11:2]
  Register #(.width(32)) PC (.D(multiplexer_3_out), .en(pcen), .Q(PC_q), .clk(CLK), .clr(RST));
  Hex_Digit_Display hex_digit_display_1 (.value(LedData[27:24]));  // open: dp
  Hex_Digit_Display hex_digit_display_2 (.value(LedData[31:28]));  // open: dp
  Counter #(.width(16), .max('hffff)) counter_1 (
    .count(JMP), .Q(\无条件分支数 ), .clk(CLK), .clr(RST));  // open: load, D, carry
  and and_4 (and_4_out, ~halt, Go);  // AND_Gate
  Adder #(.width(32)) adder_1 (.a(PC_q), .b(32'h4), .out(pc0));  // open: cin, cout
  Shifter #(.width(32)) shifter_1 (.in(Ext), .\dist (5'b00010), .out(shifter_1_out));
  or or_2 (PCSrc[1], condi, and_5_out);
  and and_5 (and_5_out, JMP, ~JR);  // AND_Gate
  Hex_Digit_Display hex_digit_display_3 (.value(LedData[19:16]));  // open: dp
  Hex_Digit_Display hex_digit_display_4 (.value(LedData[23:20]));  // open: dp
  Counter #(.width(16), .max('hffff)) counter_2 (
    .count(condi), .Q(\条件分支成功数 ), .clk(CLK), .clr(RST));  // open: load, D, carry
  nor nor_2 (nor_2_out, halt, Go, pause);
  D_Flip_Flop d_ff_1 (.clk(CLK), .D(and_4_out), .Q(d_ff_1_q), .reset(RST));  // open: Qn, preset, en
  not not_1 (not_1_out, d_ff_1_q);
  or or_3 (or_3_out, halt, pause);
  // Probe on {rom_1_data, out_6, out_7, out_1, imm}
  Adder #(.width(32)) adder_2 (.a(pc0), .b(shifter_1_out), .out(pc2));  // open: cin, cout
  Hex_Digit_Display hex_digit_display_5 (.value(LedData[15:12]));  // open: dp
  Hex_Digit_Display hex_digit_display_6 (.value(LedData[11:8]));  // open: dp
  Counter #(.width(16), .max('hffff)) counter_3 (
    .count(nor_2_out), .Q(\总周期数 ), .clk(CLK), .clr(RST));  // open: load, D, carry
  xor xor_1 (pcen, not_1_out, or_3_out);
  ROM #(.addrWidth(10), .dataWidth(32)) rom_1 (
    .addr(PC_q[11:2]), .data({rom_1_data, out_6, out_7, out_1, imm}));  // open: sel
  Hex_Digit_Display hex_digit_display_7 (.value(LedData[7:4]));  // open: dp
  Hex_Digit_Display hex_digit_display_8 (.value(LedData[3:0]));  // open: dp
  Multiplexer #(.width(5), .enable("false")) multiplexer_4 (
    .in0(out_7), .in1(out_1), .out(multiplexer_4_out), .sel(RegDst));
  Multiplexer #(.width(5), .enable("false")) multiplexer_5 (
    .in0(out_6), .in1(5'b00010), .out(multiplexer_5_out), .sel(Sys));
  Multiplexer #(.width(5), .enable("false")) multiplexer_6 (
    .in0(out_7), .in1(5'b00100), .out(multiplexer_6_out), .sel(Sys));
  // Probe on multiplexer_7_out
  Multiplexer #(.width(5), .enable("false")) multiplexer_7 (
    .in0(multiplexer_4_out), .in1({5{1'b1}}), .out(multiplexer_7_out), .sel(JAL));
  \硬布线控制器  \u_硬布线控制器_1  (
    .Func(imm[5:0]), .OP(rom_1_data), .ALU_OP(out_2), .MemToReg(MemToReg), .MemWrite(MemWrite),
    .ALU_SRC(Alus), .RegWrite(RegWrite), .SysCALL(Sys), .SignedExt(SignedExt), .RegDst(RegDst), .JR(JR),
    .JMP(JMP), .Beq(Beq), .JAL(JAL), .Bne(Bne), .SRAV(SRAV), .BLEZ(BLEZ), .SB(SB), .MFC0(mfc0), .ERET(eret));
  assign bit_extender_1_out = {{16{1'b0}}, {out_1, imm}};  // Bit_Extender bit_extender_1
  assign bit_extender_2_out = {{16{out_1[4]}}, {out_1, imm}};  // Bit_Extender bit_extender_2
  // Probe on \总周期数 
  // Probe on \无条件分支数 
  // Probe on \条件分支成功数 
  MIPS_Regifile mips_regifile_1 (
    .Din(out_3), .Clk(CLK), .R1(out_5), .R2(MemWrite_Data), .WE(RegWrite), .W_num(multiplexer_7_out),
    .R1_num(multiplexer_5_out), .R2_num(multiplexer_6_out));
  Multiplexer #(.width(32), .enable("false")) multiplexer_8 (
    .in0(MemWrite_Data), .in1(Ext), .out(multiplexer_8_out), .sel(Alus));
  Multiplexer #(.width(32), .enable("false")) multiplexer_9 (
    .in0(bit_extender_1_out), .in1(bit_extender_2_out), .out(Ext), .sel(SignedExt));
  MIPS_ALU mips_alu_1 (
    .X(out_5), .Y(multiplexer_8_out), .AluOP(out_2), .Equal(equ), .Result(MemAddr), .shamt(multiplexer_10_out));  // open: Result_2
  Multiplexer #(.width(5), .enable("false")) multiplexer_10 (
    .in0(imm[10:6]), .in1(out_5[4:0]), .out(multiplexer_10_out), .sel(SRAV));
  Comparator #(.width(32)) comparator_3 (.a(out_5), .b(32'h22), .eq(led));  // open: gt, lt
  Comparator #(.width(32)) comparator_4 (.a(out_5), .b({32{1'b0}}), .gt(comparator_4_gt));  // open: eq, lt
  and and_6 (and_6_out, Beq, equ);
  and and_7 (and_7_out, Bne, ~equ);  // AND_Gate
  and and_8 (and_8_out, BLEZ, ~comparator_4_gt);  // AND_Gate
  Multiplexer #(.width(4), .enable("false")) multiplexer_11 (
    .in0(4'b1111), .in1(multiplexer_12_out), .out(multiplexer_11_out), .sel(SB));
  Multiplexer #(.select(2), .width(4), .enable("false")) multiplexer_12 (
    .in0(4'b0001), .in1(4'b0010), .in2(4'b0100), .in3(4'b1000), .out(multiplexer_12_out), .sel(MemAddr[1:0]));
  Register #(.width(32)) register_3 (.D(MemWrite_Data), .en(led), .Q(LedData), .clk(CLK), .clr(RST));
  or or_4 (condi, and_6_out, and_7_out, and_8_out);
  Shifter #(.width(32)) shifter_2 (.in(MemWrite_Data), .\dist (5'b01000), .out(shifter_2_out));
  Shifter #(.width(32)) shifter_3 (.in(MemWrite_Data), .\dist (5'b10000), .out(shifter_3_out));
  Shifter #(.width(32)) shifter_4 (.in(MemWrite_Data), .\dist (5'b11000), .out(shifter_4_out));
  // MIPS_RAM mips_ram_1: pin names not known; wires that end beside it: comparator_4_gt, {{10{1'b0}}, MemAddr[11:2]}, out_4, MemWrite, multiplexer_11_out, CLK, RST, mips_ram_1_p8
  Multiplexer #(.select(2), .width(32), .enable("false")) multiplexer_13 (
    .in0(MemWrite_Data), .in1(shifter_2_out), .in2(shifter_3_out), .in3(shifter_4_out),
    .out(multiplexer_13_out), .sel(MemAddr[1:0]));
  Multiplexer #(.width(32), .enable("false")) multiplexer_14 (
    .in0(MemWrite_Data), .in1(multiplexer_13_out), .out(out_4), .sel(SB));
  Demultiplexer #(.select(2), .enable("false")) demultiplexer_1 (
    .out1(demultiplexer_1_out1), .out2(demultiplexer_1_out2), .out3(demultiplexer_1_out3), .in(eret),
    .sel(nowint));  // open: out0
  Register #(.width(5)) register_4 (.D(out_1), .en(mfc0), .Q(CP0), .clk(CLK), .clr(RST));
  Multiplexer #(.width(32), .enable("false")) multiplexer_15 (
    .in0(MemAddr), .in1(mips_ram_1_p8), .out(multiplexer_15_out), .sel(MemToReg));
  Multiplexer #(.width(32), .enable("false")) multiplexer_16 (
    .in0(multiplexer_15_out), .in1(pc0), .out(out_3), .sel(JAL));
  or or_5 (\_3号中断等待指示 , IR2_q, d_ff_2_q);
  or or_6 (\_2号中断等待指示 , IR2_2_q, d_ff_3_q);
  or or_7 (\_1号中断等待指示 , IR1_q, d_ff_4_q);
  D_Flip_Flop d_ff_2 (.clk(\_3号中断 ), .D(1'b1), .Q(d_ff_2_q), .reset(IR2_q));  // open: Qn, preset, en
  D_Flip_Flop d_ff_3 (.clk(\_2号中断 ), .D(1'b1), .Q(d_ff_3_q), .reset(IR2_2_q));  // open: Qn, preset, en
  D_Flip_Flop d_ff_4 (.clk(\_1号中断 ), .D(1'b1), .Q(d_ff_4_q), .reset(IR1_q));  // open: Qn, preset, en
  or or_8 (or_8_out, d_ff_2_q, IR2_q);
  or or_9 (or_9_out, d_ff_3_q, IR2_2_q);
  or or_10 (or_10_out, d_ff_4_q, IR1_q);
  and and_9 (and_9_out, or_8_out, ~demultiplexer_1_out3);  // AND_Gate
  and and_10 (and_10_out, or_9_out, ~demultiplexer_1_out2);  // AND_Gate
  and and_11 (and_11_out, or_10_out, ~demultiplexer_1_out1);  // AND_Gate
  D_Flip_Flop IR2 (.clk(CLK), .D(and_9_out), .Q(IR2_q));  // open: Qn, preset, en, reset
  D_Flip_Flop IR2_2 (.clk(CLK), .D(and_10_out), .Q(IR2_2_q));  // open: Qn, preset, en, reset
  D_Flip_Flop IR1 (.clk(CLK), .D(and_11_out), .Q(IR1_q));  // open: Qn, preset, en, reset
  Priority_Encoder #(.select(2)) priority_encoder_1 (
    .in0(1'b1), .in1(IR1_q), .in2(IR2_2_q), .in3(IR2_q), .out(priority_encoder_1_out));  // open: gs, en_out, en_in
  not not_2 (not_2_out, mfc0);
  Register #(.width(2)) register_5 (.D(priority_encoder_1_out), .en(mfc0), .Q(nowint), .clk(CLK));  // open: clr
  // Probe on priority_encoder_1_out
  Register #(.width(2)) register_6 (.D(priority_encoder_1_out), .Q(register_6_q), .clk(CLK));  // open: en, clr
  and and_12 (and_12_out[1], CP0[0], not_2_out);
  assign intnum = register_6_q & {2{and_12_out[1]}};  // AND_Gate and_13, 2 bits wide

  // Other names for the same wires on the sheet: index[25:0] = {out_6, out_7, out_1, imm};
  //   pc3[31:2] = {pc0[31:28], out_6, out_7, out_1, imm}; imm[15:11] = out_1; rd[4:0] = out_1; rt[4:0] = out_7;
  //   rs[4:0] = out_6; Aluop[3:0] = out_2; Din[31:0] = out_3; FinalMemData[31:0] = out_4; pc1[31:0] = out_5;
  //   PCSrc[0] = JMP

  // Notes on the sheet:
  //   数码管输出应该用寄存器锁存，否则显示数据只能一闪而过
  //   可以通过项目增加Logisim库的方式将前几次实验完成的电路作为子电路引入到本电路中使用
  //   指令存储器
  //   OP
  //   rs
  //   指令字
  //   contents of rom_1 (hex, n*v repeats v):
  //   40110800 20110200 20020022 112020 c 2231ffff 1620fffc 20020032 c 2008ffff 20117777 112020 20020022 c
  //   200b0010 2288826 112020 20020022 c 216bffff 1560fffa 20020032 c 200b0008 3c11fedc 3631ffff 112020
  //   20020022 c 3c11ba98 112020 c 3c117654 112020 c 3c113210 112020 c 216bffff 1560fff0 20020032 c
  //   20090000 200b0010 34118483 20120404 118c00 129400 36318281 22520404 ad310000 2328820 21290004
  //   216bffff 1560fffb 200b0020 20090000 91310000 112020 20020022 c 21290001 216bffff 1560fff9 20020032 c
  //   2011000f 112020 20020022 c 2231ffff 1e20fffb 2002000a c 40110000 ac1d0230 201d0080 27bdfffc afa40000
  //   27bdfffc afa20000 27bdfffc afa80000 27bdfffc afa90000 27bdfffc afb00000 20160001 20140006 20150001
  //   168020 108100 2149825 132020 20020022 c 1600fffa 295a022 1680fff7 8fb00000 27bd0004 8fa90000
  //   27bd0004 8fa80000 27bd0004 8fa20000 27bd0004 8fa40000 27bd0004 8c1d0230 42000018 40110800 40110000
  //   ac1d0244 201d0080 27bdfffc afa40000 27bdfffc afa20000 27bdfffc afa80000 27bdfffc afa90000 27bdfffc
  //   afb00000 20160002 20140006 20150001 168020 108100 2149825 132020 20020022 c 1600fffa 295a022
  //   1680fff7 8fb00000 27bd0004 8fa90000 27bd0004 8fa80000 27bd0004 8fa20000 27bd0004 8fa40000 27bd0004
  //   8c1d0230 42000018 40110800 40110000 ac1d0258 201d0080 27bdfffc afa40000 27bdfffc afa20000 27bdfffc
  //   afa80000 27bdfffc afa90000 27bdfffc afb00000 20160003 20140006 20150001 168020 108100 2149825 132020
  //   20020022 c 1600fffa 295a022 1680fff7 8fb00000 27bd0004 8fa90000 27bd0004 8fa80000 27bd0004 8fa20000
  //   27bd0004 8fa40000 27bd0004 8c1d0230 42000018 40110800
  //   rt
  //   rd
  //   数码管输出
  //   Func
  //   JMP
  //   JR
  //   OP
  //   Func
  //   总复位信号应将除ROM以外所有存储组件全部清零
  //   Beq
  //   Bne
  //   MemToReg
  //   MemWrite
  //   AluOP
  //   AluSrcB
  //   RegWrite
  //   JAL
  //   RegDst
  //   Syscall
  //   中断信号源及指示电路规范（优先级3>2>1>CPU(0）)
  //   Reset 
  //   Reset 
  //   Reset 
endmodule
