// Logisim project cpu24_xxs.circ as structural Verilog: 25 circuits, main circuit ◇单周期MIPS
module \单周期MIPS  (
);

  wire and_1_out, and_2_out, and_6_out, and_7_out, and_8_out, BTLZ, CLK, comparator_1_eq, comparator_2_eq,
       Go, HB, JAL, JMP, JR, LUI, MemWrite, mips_alu_1_equal, MtoR, nor_1_out, nor_2_out, not_1_out,
       or_1_out, \PC使能 , RegDst, RST, SignedExt, SLLV, Syscall, \显示 , \暂停 , \有条件跳转 , \硬布线控制器_1_alu_src ,
       \硬布线控制器_1_beq , \硬布线控制器_1_bne , \硬布线控制器_1_regwrite , \结束 ;
  wire [1:0] PCsrc;
  wire [3:0] \硬布线控制器_1_alu_op ;
  wire [4:0] multiplexer_2_out, multiplexer_3_out, multiplexer_4_out, W_num;
  wire [15:0] \总周期数 , \无条件分支数 , \条件分支成功数 ;
  wire [25:0] instr_index;
  wire [31:0] bit_extender_1_out, bit_extender_2_out, Din, GPR2, LedData, MemData, multiplexer_1_out,
       multiplexer_7_out, PC, PC0, PC2, PC3, Result, shifter_1_out, \立即数扩展 ;
  wire [31:26] rom_1_data;

  Button \u_总复位  (.out(RST));
  Button \u_继续运行  (.out(Go));
  Clock clock_1 (.out(CLK));
  Hex_Digit_Display hex_digit_display_1 (.value(LedData[27:24]));  // open: dp
  Hex_Digit_Display hex_digit_display_2 (.value(LedData[31:28]));  // open: dp
  Register #(.width(32)) register_1 (.D(GPR2), .en(\显示 ), .Q(LedData), .clk(CLK), .clr(RST));
  and and_1 (and_1_out, Go, ~\结束 );  // AND_Gate
  or or_1 (or_1_out, \结束 , \暂停 );
  Register #(.width(32)) u_PC (.D(multiplexer_1_out), .en(\PC使能 ), .Q(PC), .clk(CLK), .clr(RST));
  Multiplexer #(.select(2), .width(32), .enable("false")) multiplexer_1 (
    .in0(PC0), .in1({PC0[31:28], instr_index, 2'b00}), .in2(PC2), .in3(PC3), .out(multiplexer_1_out),
    .sel(PCsrc));
  Adder #(.width(32)) adder_1 (.a(PC), .b(32'h4), .out(PC0));  // open: cin, cout
  Shifter #(.width(32)) shifter_1 (.in(\立即数扩展 ), .\dist (5'b00010), .out(shifter_1_out));
  or or_2 (PCsrc[1], JR, \有条件跳转 );
  Hex_Digit_Display hex_digit_display_3 (.value(LedData[19:16]));  // open: dp
  Hex_Digit_Display hex_digit_display_4 (.value(LedData[23:20]));  // open: dp
  not not_1 (not_1_out, and_1_out);
  Adder #(.width(32)) adder_2 (.a(shifter_1_out), .b(PC0), .out(PC3));  // open: cin, cout
  and and_2 (and_2_out, JMP, ~JR);  // AND_Gate
  or or_3 (PCsrc[0], and_2_out, \有条件跳转 );
  Hex_Digit_Display hex_digit_display_5 (.value(LedData[11:8]));  // open: dp
  Hex_Digit_Display hex_digit_display_6 (.value(LedData[15:12]));  // open: dp
  xor xor_1 (\PC使能 , not_1_out, or_1_out);
  Hex_Digit_Display hex_digit_display_7 (.value(LedData[3:0]));  // open: dp
  Hex_Digit_Display hex_digit_display_8 (.value(LedData[7:4]));  // open: dp
  ROM #(.addrWidth(10), .dataWidth(32)) rom_1 (.addr(PC[11:2]), .data({rom_1_data, instr_index}), .sel(1'b1));
  Multiplexer #(.width(5), .enable("false")) multiplexer_2 (
    .in0(instr_index[20:16]), .in1(instr_index[15:11]), .out(multiplexer_2_out), .sel(RegDst));
  Comparator #(.width(32)) comparator_1 (.a(PC2), .b(32'ha), .eq(comparator_1_eq));  // open: gt, lt
  // Probe on \总周期数 
  // Probe on \无条件分支数 
  // Probe on \条件分支成功数 
  \硬布线控制器  \u_硬布线控制器_1  (
    .Func(instr_index[5:0]), .OP(rom_1_data), .ALU_OP(\硬布线控制器_1_alu_op ), .MemToReg(MtoR),
    .MemWrite(MemWrite), .ALU_SRC(\硬布线控制器_1_alu_src ), .RegWrite(\硬布线控制器_1_regwrite ), .SysCALL(Syscall),
    .SignedExt(SignedExt), .RegDst(RegDst), .JR(JR), .JMP(JMP), .Beq(\硬布线控制器_1_beq ), .JAL(JAL),
    .Bne(\硬布线控制器_1_bne ), .LUI(LUI), .BTLZ(BTLZ), .HB(HB), .SLLV(SLLV));
  Multiplexer #(.width(5), .enable("false")) multiplexer_3 (
    .in0(instr_index[25:21]), .in1(5'b00010), .out(multiplexer_3_out), .sel(Syscall));
  Multiplexer #(.width(5), .enable("false")) multiplexer_4 (
    .in0(instr_index[20:16]), .in1(5'b00100), .out(multiplexer_4_out), .sel(Syscall));
  Multiplexer #(.width(5), .enable("false")) multiplexer_5 (
    .in0(multiplexer_2_out), .in1({5{1'b1}}), .out(W_num), .sel(JAL));
  and and_3 (\结束 , comparator_1_eq, Syscall);
  and and_4 (\显示 , Syscall, comparator_2_eq);
  Comparator #(.width(32)) comparator_2 (.a(PC2), .b(32'h22), .eq(comparator_2_eq));  // open: gt, lt
  assign bit_extender_1_out = {{16{1'b0}}, instr_index[15:0]};  // Bit_Extender bit_extender_1
  assign bit_extender_2_out = {{16{instr_index[15]}}, instr_index[15:0]};  // Bit_Extender bit_extender_2
  nor nor_1 (nor_1_out, \结束 , \显示 );
  MIPS_Regifile mips_regifile_1 (
    .Din(Din), .Clk(CLK), .R1(PC2), .R2(GPR2), .WE(\硬布线控制器_1_regwrite ), .W_num(W_num),
    .R1_num(multiplexer_3_out), .R2_num(multiplexer_4_out));
  Multiplexer #(.width(32), .enable("false")) multiplexer_6 (
    .in0(bit_extender_1_out), .in1(bit_extender_2_out), .out(\立即数扩展 ), .sel(SignedExt));
  and and_5 (\暂停 , nor_1_out, Syscall);
  Counter #(.width(16), .max('hffff)) counter_1 (
    .count(JMP), .Q(\无条件分支数 ), .clk(CLK), .clr(RST));  // open: load, D, carry
  Multiplexer #(.width(32), .enable("false")) multiplexer_7 (
    .in0(GPR2), .in1(\立即数扩展 ), .out(multiplexer_7_out), .sel(\硬布线控制器_1_alu_src ));
  and and_6 (and_6_out, mips_alu_1_equal, \硬布线控制器_1_beq );
  and and_7 (and_7_out, \硬布线控制器_1_bne , ~mips_alu_1_equal);  // AND_Gate
  MIPS_ALU mips_alu_1 (
    .X(PC2), .Y(multiplexer_7_out), .AluOP(\硬布线控制器_1_alu_op ), .Equal(mips_alu_1_equal), .Result(Result),
    .shamt(instr_index[10:6]));  // open: Result_2
  Counter #(.width(16), .max('hffff)) counter_2 (
    .count(\有条件跳转 ), .Q(\条件分支成功数 ), .clk(CLK), .clr(RST));  // open: load, D, carry
  or or_4 (\有条件跳转 , and_6_out, and_7_out, and_8_out);
  and and_8 (and_8_out, BTLZ, Result[0]);
  RAM #(.addrWidth(10), .dataWidth(32), .bus("separate")) ram_1 (
    .addr(Result[11:2]), .din(GPR2), .data(MemData), .str(MemWrite), .sel(1'b1), .clk(CLK), .clr(RST));  // open: ld
  nor nor_2 (nor_2_out, \结束 , Go, \暂停 );
  \Din计算  \din计算_1  (
    .MemData(MemData), .WB_R2(GPR2), .Result(Result), .WB_R1(PC2), .MemToReg(MtoR), .WB_Jal(JAL),
    .WB_LUI(LUI), .WB_Sllv(SLLV), .HB(HB), .Din(Din), .WB_PC(PC), .WB_imm(instr_index[15:0]));
  Counter #(.width(16), .max('hffff)) counter_3 (
    .count(nor_2_out), .Q(\总周期数 ), .clk(CLK), .clr(RST));  // open: load, D, carry

  // Other names for the same wires on the sheet: PC1[31:2] = {PC0[31:28], instr_index}; 立即数[15:0] = instr_index[15:0];
  //   rd[4:0] = instr_index[15:11]; rt[4:0] = instr_index[20:16]; PC高4位[3:0] = PC0[31:28]

  // Notes on the sheet:
  //   PC选择逻辑
  //   数码管输出应该用寄存器锁存，否则显示数据只能一闪而过
  //   可以通过项目增加Logisim库的方式将前几次实验完成的电路作为子电路引入到本电路中使用
  //   10:JR
  //   11:  条件跳转
  //   01:  无条件跳转
  //   数码管输出
  //   指令存储器
  //   contents of rom_1 (hex, n*v repeats v):
  //   20110001 8100005 20110001 20120002 20130003 8100009 20110001 20120002 20130003 810000d 20110001
  //   20120002 20130003 8100011 20110001 20120002 20130003 c1000fb 20100001 20110001 118fc0 112020
  //   20020022 c 118882 12200001 8100015 112020 20020022 c 20110001 118880 112020 20020022 c 12200001
  //   810001f 20110001 118fc0 112020 20020022 c 1188c3 112020 20020022 c 118903 112020 20020022 c 118903
  //   112020 20020022 c 118903 112020 20020022 c 118903 112020 20020022 c 118903 112020 20020022 c 118903
  //   112020 20020022 c 118903 112020 20020022 c 20100001 109fc0 139fc3 8021 2012000c 24160003 26100001
  //   3210000f 20080008 20090001 139900 2709825 132020 20020022 c 1094022 1500fff9 22100001 2018000f
  //   2188024 108700 20080008 20090001 139902 2709825 132021 20020022 c 1094022 1500fff9 108702 2c9b022
  //   12c00001 8100050 4020 1084027 84400 3508ffff 82021 20020022 c 2010ffff 20110000 ae300000 22100001
  //   22310004 ae300000 22100001 22310004 ae300000 22100001 22310004 ae300000 22100001 22310004 ae300000
  //   22100001 22310004 ae300000 22100001 22310004 ae300000 22100001 22310004 ae300000 22100001 22310004
  //   ae300000 22100001 22310004 ae300000 22100001 22310004 ae300000 22100001 22310004 ae300000 22100001
  //   22310004 ae300000 22100001 22310004 ae300000 22100001 22310004 ae300000 22100001 22310004 ae300000
  //   22100001 22310004 22100001 8020 2011003c 8e130000 8e340000 274402a 11000002 ae330000 ae140000
  //   2231fffc 1611fff8 102020 20020022 c 22100004 2011003c 1611fff2 20020032 c 20080001 20090003 20110876
  //   112020 20020022 c 200b0008 1118804 1318804 112020 20020022 c 216bffff 1560fff9 20020032 c 200b0008
  //   3c11fedc 3631ffff 112020 20020022 c 3c11ba98 112020 c 3c117654 112020 c 3c113210 112020 c 216bffff
  //   1560fff0 20020032 c 20090000 200b0010 34118483 20120404 118c00 129400 36318281 22520404 ad310000
  //   2328820 21290004 216bffff 1560fffb 200b0020 20090000 85310000 112020 20020022 c 21290002 216bffff
  //   1560fff9 20020032 c 2011fff1 112020 20020022 c 22310001 620fffb 2002000a c 20100000 22100001 102020
  //   20020022 c 22100002 102020 20020022 c 22100003 102020 20020022 c 22100004 102020 20020022 c 22100005
  //   102020 20020022 c 22100006 102020 20020022 c 22100007 102020 20020022 c 22100008 102020 20020022
  //   20020022 c 3e00008
  //   OP
  //   Func
  //   rs
  //   指令字
  //   rt
  //   rd
  //   shamt
  //   OP
  //   Func
  //   总复位信号应将除ROM以外所有存储组件全部清零
endmodule

// 单周期硬布线控制器
module \硬布线控制器  (
  input  [5:0] OP,
  input  [5:0] Func,
  output [3:0] ALU_OP,
  output MemToReg,
  output MemWrite,
  output ALU_SRC,
  output RegWrite,
  output SysCALL,
  output SignedExt,
  output RegDst,
  output Beq,
  output Bne,
  output JR,
  output JMP,
  output JAL,
  output LUI,
  output BTLZ,
  output HB,
  output SLLV
);

  \运算控制器  \u_运算控制器_1  (
    .OP0(OP[0]), .OP1(OP[1]), .OP2(OP[2]), .OP3(OP[3]), .OP4(OP[4]), .OP5(OP[5]), .F0(Func[0]), .F1(Func[1]),
    .F2(Func[2]), .F3(Func[3]), .F4(Func[4]), .F5(Func[5]), .S0(ALU_OP[0]), .S1(ALU_OP[1]), .S2(ALU_OP[2]),
    .S3(ALU_OP[3]));
  \控制信号生成  \u_控制信号生成_1  (
    .OP0(OP[0]), .OP1(OP[1]), .OP2(OP[2]), .OP3(OP[3]), .OP4(OP[4]), .OP5(OP[5]), .F0(Func[0]), .F1(Func[1]),
    .F2(Func[2]), .F3(Func[3]), .F4(Func[4]), .F5(Func[5]), .MemToReg(MemToReg), .MemWrite(MemWrite),
    .ALU_SRC(ALU_SRC), .RegWrite(RegWrite), .SysCALL(SysCALL), .SignedExt(SignedExt), .RegDst(RegDst),
    .BEQ(Beq), .BNE(Bne), .JR(JR), .JMP(JMP), .JAL(JAL), .LUI(LUI), .BTLZ(BTLZ), .HB(HB), .SLLV(SLLV));

  // Other names for the same wires on the sheet: OP_CODE[5:0] = OP

  // Notes on the sheet:
  //   运算器控制器，根据指令生成运算器功能选择信号
  //   控制信号生成，产生数据通路需要的其他控制信号
endmodule

// 运算器控制器
module \运算控制器  (
  input  OP0,
  input  OP1,
  input  OP2,
  input  OP3,
  input  OP4,
  input  OP5,
  input  F0,
  input  F1,
  input  F2,
  input  F3,
  input  F4,
  input  F5,
  output S0,
  output S1,
  output S2,
  output S3
);

  wire and_1_out, and_2_out, and_3_out, and_4_out, and_5_out, and_6_out, and_7_out, and_8_out, and_9_out,
       and_10_out, and_11_out, and_12_out, and_13_out, and_14_out, and_15_out, and_16_out, and_17_out,
       and_18_out, and_19_out, and_20_out, and_21_out, and_22_out, and_23_out, and_24_out, and_25_out,
       and_26_out, and_27_out, and_28_out, and_29_out, and_30_out, and_31_out, and_32_out, and_33_out,
       and_34_out, and_35_out, and_36_out, and_37_out, and_38_out, and_39_out, not_1_out, not_2_out,
       not_3_out, not_4_out, not_5_out, not_6_out, not_7_out, not_8_out, not_9_out, not_10_out, not_11_out,
       not_12_out, not_13_out, not_14_out, not_15_out, not_16_out, not_17_out, not_18_out, not_19_out,
       not_20_out, not_21_out, not_22_out, not_23_out, not_24_out, not_25_out, not_26_out, not_27_out,
       not_28_out, not_29_out, not_30_out, not_31_out, not_32_out, not_33_out, not_34_out, not_35_out,
       not_36_out, not_37_out, not_38_out, not_39_out, not_40_out, not_41_out, not_42_out, not_43_out,
       not_44_out, not_45_out, not_46_out, not_47_out, not_48_out, not_49_out, not_50_out, not_51_out,
       not_52_out, not_53_out, not_54_out, not_55_out, not_56_out, not_57_out, not_58_out, not_59_out,
       not_60_out, not_61_out, not_62_out, not_63_out, not_64_out, not_65_out, not_66_out, not_67_out,
       not_68_out, not_69_out, not_70_out, not_71_out, not_72_out, not_73_out, not_74_out, not_75_out,
       not_76_out, not_77_out, not_78_out, not_79_out, not_80_out, not_81_out, not_82_out, not_83_out,
       not_84_out, not_85_out, not_86_out, not_87_out, not_88_out, not_89_out, not_90_out, not_91_out,
       not_92_out, not_93_out, not_94_out, not_95_out, not_96_out, not_97_out, not_98_out, not_99_out,
       not_100_out, not_101_out, not_102_out, not_103_out, not_104_out, not_105_out, not_106_out,
       not_107_out, not_108_out, not_109_out, not_110_out, not_111_out, not_112_out, not_113_out,
       not_114_out, not_115_out, not_116_out, not_117_out, not_118_out, not_119_out, not_120_out,
       not_121_out, not_122_out, not_123_out, not_124_out, not_125_out, not_126_out, not_127_out,
       not_128_out, not_129_out, not_130_out, not_131_out, not_132_out, not_133_out, not_134_out,
       not_135_out, not_136_out, not_137_out, not_138_out, not_139_out, not_140_out, not_141_out,
       not_142_out, not_143_out, not_144_out, not_145_out, not_146_out, not_147_out, not_148_out,
       not_149_out, not_150_out, not_151_out, not_152_out, not_153_out, not_154_out, not_155_out,
       not_156_out, not_157_out, not_158_out, not_159_out, not_160_out, not_161_out, not_162_out,
       not_163_out, not_164_out, not_165_out, not_166_out, not_167_out, not_168_out, not_169_out,
       not_170_out, not_171_out, not_172_out, not_173_out, not_174_out, not_175_out, not_176_out,
       not_177_out, not_178_out, not_179_out, not_180_out, not_181_out, not_182_out, not_183_out,
       not_184_out, not_185_out, not_186_out, not_187_out, not_188_out, not_189_out, not_190_out,
       not_191_out, not_192_out, not_193_out, not_194_out, not_195_out, not_196_out, not_197_out,
       not_198_out, not_199_out, not_200_out, not_201_out, not_202_out, not_203_out, not_204_out,
       not_205_out, not_206_out, not_207_out, not_208_out, not_209_out, not_210_out, not_211_out,
       not_212_out, not_213_out, not_214_out, not_215_out, not_216_out, not_217_out, not_218_out,
       not_219_out, not_220_out, not_221_out, not_222_out, not_223_out, not_224_out, not_225_out,
       not_226_out, not_227_out, not_228_out, not_229_out, not_230_out, not_231_out, not_232_out,
       not_233_out, not_234_out, not_235_out, not_236_out, not_237_out, not_238_out, not_239_out,
       not_240_out, not_241_out, not_242_out, not_243_out, not_244_out, not_245_out, not_246_out,
       not_247_out, not_248_out, not_249_out, not_250_out, not_251_out, not_252_out, not_253_out,
       not_254_out, not_255_out, not_256_out, not_257_out, not_258_out, not_259_out;

  not not_1 (not_1_out, OP5);
  not not_2 (not_2_out, OP4);
  not not_3 (not_3_out, OP3);
  not not_4 (not_4_out, OP2);
  not not_5 (not_5_out, OP1);
  not not_6 (not_6_out, OP0);
  not not_7 (not_7_out, F5);
  not not_8 (not_8_out, F4);
  not not_9 (not_9_out, F3);
  not not_10 (not_10_out, F2);
  not not_11 (not_11_out, OP5);
  not not_12 (not_12_out, OP4);
  not not_13 (not_13_out, OP3);
  not not_14 (not_14_out, OP2);
  not not_15 (not_15_out, OP1);
  not not_16 (not_16_out, OP0);
  not not_17 (not_17_out, F4);
  not not_18 (not_18_out, F3);
  not not_19 (not_19_out, F2);
  not not_20 (not_20_out, F1);
  not not_21 (not_21_out, F0);
  not not_22 (not_22_out, OP5);
  not not_23 (not_23_out, OP4);
  not not_24 (not_24_out, OP3);
  not not_25 (not_25_out, OP2);
  not not_26 (not_26_out, OP1);
  not not_27 (not_27_out, OP0);
  not not_28 (not_28_out, F4);
  not not_29 (not_29_out, F3);
  not not_30 (not_30_out, F2);
  not not_31 (not_31_out, F1);
  not not_32 (not_32_out, OP5);
  not not_33 (not_33_out, OP4);
  not not_34 (not_34_out, OP3);
  not not_35 (not_35_out, OP2);
  not not_36 (not_36_out, OP1);
  not not_37 (not_37_out, OP0);
  not not_38 (not_38_out, F4);
  not not_39 (not_39_out, F3);
  not not_40 (not_40_out, F1);
  not not_41 (not_41_out, F0);
  not not_42 (not_42_out, OP5);
  not not_43 (not_43_out, OP4);
  not not_44 (not_44_out, OP3);
  not not_45 (not_45_out, OP2);
  not not_46 (not_46_out, OP1);
  not not_47 (not_47_out, OP0);
  not not_48 (not_48_out, F4);
  not not_49 (not_49_out, F2);
  not not_50 (not_50_out, F0);
  not not_51 (not_51_out, OP5);
  not not_52 (not_52_out, OP4);
  not not_53 (not_53_out, OP2);
  not not_54 (not_54_out, OP1);
  not not_55 (not_55_out, OP0);
  not not_56 (not_56_out, OP5);
  not not_57 (not_57_out, OP4);
  not not_58 (not_58_out, OP1);
  not not_59 (not_59_out, OP0);
  not not_60 (not_60_out, OP5);
  not not_61 (not_61_out, OP4);
  not not_62 (not_62_out, OP2);
  not not_63 (not_63_out, OP1);
  not not_64 (not_64_out, OP5);
  not not_65 (not_65_out, OP4);
  not not_66 (not_66_out, OP2);
  not not_67 (not_67_out, OP0);
  not not_68 (not_68_out, OP4);
  not not_69 (not_69_out, OP3);
  not not_70 (not_70_out, OP2);
  not not_71 (not_71_out, OP4);
  not not_72 (not_72_out, OP2);
  not not_73 (not_73_out, OP4);
  not not_74 (not_74_out, OP3);
  not not_75 (not_75_out, OP2);
  not not_76 (not_76_out, OP1);
  not not_77 (not_77_out, OP5);
  not not_78 (not_78_out, OP4);
  not not_79 (not_79_out, OP3);
  not not_80 (not_80_out, OP2);
  not not_81 (not_81_out, OP1);
  not not_82 (not_82_out, OP5);
  not not_83 (not_83_out, OP4);
  not not_84 (not_84_out, OP3);
  not not_85 (not_85_out, OP2);
  not not_86 (not_86_out, OP1);
  not not_87 (not_87_out, OP0);
  not not_88 (not_88_out, F5);
  not not_89 (not_89_out, F4);
  not not_90 (not_90_out, F3);
  not not_91 (not_91_out, F2);
  not not_92 (not_92_out, F0);
  not not_93 (not_93_out, OP5);
  not not_94 (not_94_out, OP4);
  not not_95 (not_95_out, OP3);
  not not_96 (not_96_out, OP2);
  not not_97 (not_97_out, OP1);
  not not_98 (not_98_out, OP0);
  not not_99 (not_99_out, F4);
  not not_100 (not_100_out, F3);
  not not_101 (not_101_out, F2);
  not not_102 (not_102_out, F0);
  not not_103 (not_103_out, OP5);
  not not_104 (not_104_out, OP4);
  not not_105 (not_105_out, OP3);
  not not_106 (not_106_out, OP2);
  not not_107 (not_107_out, OP1);
  not not_108 (not_108_out, OP0);
  not not_109 (not_109_out, F4);
  not not_110 (not_110_out, F3);
  not not_111 (not_111_out, F1);
  not not_112 (not_112_out, F0);
  not not_113 (not_113_out, OP5);
  not not_114 (not_114_out, OP4);
  not not_115 (not_115_out, OP3);
  not not_116 (not_116_out, OP2);
  not not_117 (not_117_out, OP1);
  not not_118 (not_118_out, OP0);
  not not_119 (not_119_out, F4);
  not not_120 (not_120_out, F3);
  not not_121 (not_121_out, OP5);
  not not_122 (not_122_out, OP4);
  not not_123 (not_123_out, OP3);
  not not_124 (not_124_out, OP2);
  not not_125 (not_125_out, OP1);
  not not_126 (not_126_out, OP0);
  not not_127 (not_127_out, F4);
  not not_128 (not_128_out, F2);
  not not_129 (not_129_out, F0);
  not not_130 (not_130_out, OP5);
  not not_131 (not_131_out, OP4);
  not not_132 (not_132_out, OP1);
  not not_133 (not_133_out, OP0);
  not not_134 (not_134_out, OP5);
  not not_135 (not_135_out, OP4);
  not not_136 (not_136_out, OP2);
  not not_137 (not_137_out, OP0);
  not not_138 (not_138_out, OP5);
  not not_139 (not_139_out, OP4);
  not not_140 (not_140_out, OP3);
  not not_141 (not_141_out, OP2);
  not not_142 (not_142_out, OP1);
  not not_143 (not_143_out, OP5);
  not not_144 (not_144_out, OP4);
  not not_145 (not_145_out, OP3);
  not not_146 (not_146_out, OP2);
  not not_147 (not_147_out, OP1);
  not not_148 (not_148_out, OP0);
  not not_149 (not_149_out, F4);
  not not_150 (not_150_out, F3);
  not not_151 (not_151_out, F2);
  not not_152 (not_152_out, F1);
  not not_153 (not_153_out, F0);
  not not_154 (not_154_out, OP5);
  not not_155 (not_155_out, OP4);
  not not_156 (not_156_out, OP3);
  not not_157 (not_157_out, OP2);
  not not_158 (not_158_out, OP1);
  not not_159 (not_159_out, OP0);
  not not_160 (not_160_out, F4);
  not not_161 (not_161_out, F3);
  not not_162 (not_162_out, F2);
  not not_163 (not_163_out, F1);
  not not_164 (not_164_out, OP5);
  not not_165 (not_165_out, OP4);
  not not_166 (not_166_out, OP3);
  not not_167 (not_167_out, OP2);
  not not_168 (not_168_out, OP1);
  not not_169 (not_169_out, OP0);
  not not_170 (not_170_out, F4);
  not not_171 (not_171_out, F3);
  not not_172 (not_172_out, F2);
  not not_173 (not_173_out, F0);
  not not_174 (not_174_out, OP5);
  not not_175 (not_175_out, OP4);
  not not_176 (not_176_out, OP3);
  not not_177 (not_177_out, OP2);
  not not_178 (not_178_out, OP1);
  not not_179 (not_179_out, OP0);
  not not_180 (not_180_out, F4);
  not not_181 (not_181_out, F3);
  not not_182 (not_182_out, F1);
  not not_183 (not_183_out, F0);
  not not_184 (not_184_out, OP5);
  not not_185 (not_185_out, OP4);
  not not_186 (not_186_out, OP3);
  not not_187 (not_187_out, OP2);
  not not_188 (not_188_out, OP1);
  not not_189 (not_189_out, OP0);
  not not_190 (not_190_out, F4);
  not not_191 (not_191_out, F2);
  not not_192 (not_192_out, OP5);
  not not_193 (not_193_out, OP4);
  not not_194 (not_194_out, OP2);
  not not_195 (not_195_out, OP1);
  not not_196 (not_196_out, OP0);
  not not_197 (not_197_out, OP5);
  not not_198 (not_198_out, OP4);
  not not_199 (not_199_out, OP1);
  not not_200 (not_200_out, OP0);
  not not_201 (not_201_out, OP5);
  not not_202 (not_202_out, OP4);
  not not_203 (not_203_out, OP2);
  not not_204 (not_204_out, OP1);
  not not_205 (not_205_out, OP4);
  not not_206 (not_206_out, OP3);
  not not_207 (not_207_out, OP2);
  not not_208 (not_208_out, OP4);
  not not_209 (not_209_out, OP2);
  not not_210 (not_210_out, OP4);
  not not_211 (not_211_out, OP3);
  not not_212 (not_212_out, OP2);
  not not_213 (not_213_out, OP1);
  not not_214 (not_214_out, OP5);
  not not_215 (not_215_out, OP4);
  not not_216 (not_216_out, OP3);
  not not_217 (not_217_out, OP2);
  not not_218 (not_218_out, OP1);
  not not_219 (not_219_out, OP0);
  not not_220 (not_220_out, F4);
  not not_221 (not_221_out, F3);
  not not_222 (not_222_out, F1);
  not not_223 (not_223_out, OP5);
  not not_224 (not_224_out, OP4);
  not not_225 (not_225_out, OP3);
  not not_226 (not_226_out, OP2);
  not not_227 (not_227_out, OP1);
  not not_228 (not_228_out, OP0);
  not not_229 (not_229_out, F4);
  not not_230 (not_230_out, F3);
  not not_231 (not_231_out, OP5);
  not not_232 (not_232_out, OP4);
  not not_233 (not_233_out, OP3);
  not not_234 (not_234_out, OP2);
  not not_235 (not_235_out, OP1);
  not not_236 (not_236_out, OP0);
  not not_237 (not_237_out, F4);
  not not_238 (not_238_out, F2);
  not not_239 (not_239_out, F0);
  not not_240 (not_240_out, OP5);
  not not_241 (not_241_out, OP4);
  not not_242 (not_242_out, OP3);
  not not_243 (not_243_out, OP2);
  not not_244 (not_244_out, OP1);
  not not_245 (not_245_out, OP0);
  not not_246 (not_246_out, F4);
  not not_247 (not_247_out, F2);
  not not_248 (not_248_out, OP5);
  not not_249 (not_249_out, OP4);
  not not_250 (not_250_out, OP2);
  not not_251 (not_251_out, OP0);
  not not_252 (not_252_out, OP5);
  not not_253 (not_253_out, OP4);
  not not_254 (not_254_out, OP1);
  not not_255 (not_255_out, OP5);
  not not_256 (not_256_out, OP4);
  not not_257 (not_257_out, OP3);
  not not_258 (not_258_out, OP2);
  not not_259 (not_259_out, OP1);
  and and_1 (and_1_out, not_1_out, not_2_out, not_3_out, not_4_out, not_5_out, not_6_out, not_7_out, not_8_out, not_9_out, not_10_out, F1, F0);
  and and_2 (and_2_out, not_11_out, not_12_out, not_13_out, not_14_out, not_15_out, not_16_out, F5, not_17_out, not_18_out, not_19_out, not_20_out, not_21_out);
  and and_3 (and_3_out, not_22_out, not_23_out, not_24_out, not_25_out, not_26_out, not_27_out, F5, not_28_out, not_29_out, not_30_out, not_31_out, F0);
  and and_4 (and_4_out, not_32_out, not_33_out, not_34_out, not_35_out, not_36_out, not_37_out, F5, not_38_out, not_39_out, F2, not_40_out, not_41_out);
  and and_5 (and_5_out, not_42_out, not_43_out, not_44_out, not_45_out, not_46_out, not_47_out, F5, not_48_out, F3, not_49_out, F1, not_50_out);
  and and_6 (and_6_out, not_51_out, not_52_out, OP3, not_53_out, not_54_out, not_55_out);
  and and_7 (and_7_out, not_56_out, not_57_out, OP3, OP2, not_58_out, not_59_out);
  and and_8 (and_8_out, not_60_out, not_61_out, OP3, not_62_out, not_63_out, OP0);
  and and_9 (and_9_out, not_64_out, not_65_out, OP3, not_66_out, OP1, not_67_out);
  and and_10 (and_10_out, OP5, not_68_out, not_69_out, not_70_out, OP1, OP0);
  and and_11 (and_11_out, OP5, not_71_out, OP3, not_72_out, OP1, OP0);
  and and_12 (and_12_out, OP5, not_73_out, not_74_out, not_75_out, not_76_out, OP0);
  and and_13 (and_13_out, not_77_out, not_78_out, not_79_out, not_80_out, not_81_out, OP0);
  and and_14 (and_14_out, not_82_out, not_83_out, not_84_out, not_85_out, not_86_out, not_87_out, not_88_out, not_89_out, not_90_out, not_91_out, F1, not_92_out);
  and and_15 (and_15_out, not_93_out, not_94_out, not_95_out, not_96_out, not_97_out, not_98_out, F5, not_99_out, not_100_out, not_101_out, F1, not_102_out);
  and and_16 (and_16_out, not_103_out, not_104_out, not_105_out, not_106_out, not_107_out, not_108_out, F5, not_109_out, not_110_out, F2, not_111_out, not_112_out);
  and and_17 (and_17_out, not_113_out, not_114_out, not_115_out, not_116_out, not_117_out, not_118_out, F5, not_119_out, not_120_out, F2, F1, F0);
  and and_18 (and_18_out, not_121_out, not_122_out, not_123_out, not_124_out, not_125_out, not_126_out, F5, not_127_out, F3, not_128_out, F1, not_129_out);
  and and_19 (and_19_out, not_130_out, not_131_out, OP3, OP2, not_132_out, not_133_out);
  and and_20 (and_20_out, not_134_out, not_135_out, OP3, not_136_out, OP1, not_137_out);
  and and_21 (and_21_out, not_138_out, not_139_out, not_140_out, not_141_out, not_142_out, OP0);
  and and_22 (and_22_out, not_143_out, not_144_out, not_145_out, not_146_out, not_147_out, not_148_out, F5, not_149_out, not_150_out, not_151_out, not_152_out, not_153_out);
  and and_23 (and_23_out, not_154_out, not_155_out, not_156_out, not_157_out, not_158_out, not_159_out, F5, not_160_out, not_161_out, not_162_out, not_163_out, F0);
  and and_24 (and_24_out, not_164_out, not_165_out, not_166_out, not_167_out, not_168_out, not_169_out, F5, not_170_out, not_171_out, not_172_out, F1, not_173_out);
  and and_25 (and_25_out, not_174_out, not_175_out, not_176_out, not_177_out, not_178_out, not_179_out, F5, not_180_out, not_181_out, F2, not_182_out, not_183_out);
  and and_26 (and_26_out, not_184_out, not_185_out, not_186_out, not_187_out, not_188_out, not_189_out, F5, not_190_out, F3, not_191_out, F1, F0);
  and and_27 (and_27_out, not_192_out, not_193_out, OP3, not_194_out, not_195_out, not_196_out);
  and and_28 (and_28_out, not_197_out, not_198_out, OP3, OP2, not_199_out, not_200_out);
  and and_29 (and_29_out, not_201_out, not_202_out, OP3, not_203_out, not_204_out, OP0);
  and and_30 (and_30_out, OP5, not_205_out, not_206_out, not_207_out, OP1, OP0);
  and and_31 (and_31_out, OP5, not_208_out, OP3, not_209_out, OP1, OP0);
  and and_32 (and_32_out, OP5, not_210_out, not_211_out, not_212_out, not_213_out, OP0);
  and and_33 (and_33_out, not_214_out, not_215_out, not_216_out, not_217_out, not_218_out, not_219_out, F5, not_220_out, not_221_out, F2, not_222_out, F0);
  and and_34 (and_34_out, not_223_out, not_224_out, not_225_out, not_226_out, not_227_out, not_228_out, F5, not_229_out, not_230_out, F2, F1, F0);
  and and_35 (and_35_out, not_231_out, not_232_out, not_233_out, not_234_out, not_235_out, not_236_out, F5, not_237_out, F3, not_238_out, F1, not_239_out);
  and and_36 (and_36_out, not_240_out, not_241_out, not_242_out, not_243_out, not_244_out, not_245_out, F5, not_246_out, F3, not_247_out, F1, F0);
  and and_37 (and_37_out, not_248_out, not_249_out, OP3, not_250_out, OP1, not_251_out);
  and and_38 (and_38_out, not_252_out, not_253_out, OP3, OP2, not_254_out, OP0);
  and and_39 (and_39_out, not_255_out, not_256_out, not_257_out, not_258_out, not_259_out, OP0);
  or or_1 (S1, and_14_out, and_15_out, and_16_out, and_17_out, and_18_out, and_19_out, and_20_out, and_21_out);
  or or_2 (S2, and_22_out, and_23_out, and_24_out, and_25_out, and_26_out, and_27_out, and_28_out, and_29_out, and_30_out, and_31_out, and_32_out);
  or or_3 (S3, and_33_out, and_34_out, and_35_out, and_36_out, and_37_out, and_38_out, and_39_out);
  or or_4 (S0, and_1_out, and_2_out, and_3_out, and_4_out, and_5_out, and_6_out, and_7_out, and_8_out, and_9_out, and_10_out, and_11_out, and_12_out, and_13_out);
endmodule

// 控制信号生成
module \控制信号生成  (
  input  OP0,
  input  OP1,
  input  OP2,
  input  OP3,
  input  OP4,
  input  OP5,
  input  F0,
  input  F1,
  input  F2,
  input  F3,
  input  F4,
  input  F5,
  output MemToReg,
  output MemWrite,
  output ALU_SRC,
  output RegWrite,
  output SysCALL,
  output SignedExt,
  output RegDst,
  output BEQ,
  output BNE,
  output JR,
  output JMP,
  output JAL,
  output LUI,
  output BTLZ,
  output HB,
  output SLLV
);

  \控制信号生成_1  \u_控制信号生成_1_1  (
    .OP0(OP0), .OP1(OP1), .OP2(OP2), .MemToReg(MemToReg), .OP3(OP3), .OP4(OP4), .OP5(OP5),
    .MemWrite(MemWrite), .F0(F0), .F1(F1), .F2(F2), .F3(F3), .F4(F4), .F5(F5), .ALU_SRC(ALU_SRC),
    .RegWrite(RegWrite), .SysCALL(SysCALL), .SignedExt(SignedExt), .RegDst(RegDst), .BEQ(BEQ), .BNE(BNE),
    .JR(JR), .JMP(JMP), .JAL(JAL));
  \控制信号生成_2  \u_控制信号生成_2_1  (
    .OP0(OP0), .OP1(OP1), .LUI(LUI), .OP2(OP2), .OP3(OP3), .BTLZ(BTLZ), .OP4(OP4), .OP5(OP5), .F0(F0),
    .HB(HB), .F1(F1), .F2(F2), .F3(F3), .F4(F4), .SLLV(SLLV), .F5(F5));
endmodule

// ALU
module MIPS_ALU (
  input  [4:0] shamt,
  input  [31:0] X,
  input  [31:0] Y,
  input  [3:0] AluOP,
  output Equal,
  output [31:0] Result,
  output [31:0] Result_2
);

  wire [0:0] comparator_1_lt, comparator_2_lt;
  wire [31:0] adder_1_out, AND_out, divider_1_out, divider_1_rem, multiplier_1_cout, multiplier_1_out,
       NOR_out, OR_out, shifter_1_out, shifter_2_out, shifter_3_out, subtractor_1_out, XOR_out;

  assign AND_out = X & Y;  // AND_Gate AND, 32 bits wide
  assign OR_out = X | Y;  // OR_Gate OR, 32 bits wide
  Shifter #(.width(32)) shifter_1 (.in(Y), .\dist (shamt), .out(shifter_1_out));
  Shifter #(.width(32), .shift("ar")) shifter_2 (.in(Y), .\dist (shamt), .out(shifter_2_out));
  Shifter #(.width(32), .shift("lr")) shifter_3 (.in(Y), .\dist (shamt), .out(shifter_3_out));
  Multiplier #(.width(32)) multiplier_1 (.a(X), .b(Y), .out(multiplier_1_out), .cout(multiplier_1_cout));  // open: cin
  Divider #(.width(32)) divider_1 (.a(X), .b(Y), .out(divider_1_out), .rem(divider_1_rem));  // open: upper
  Adder #(.width(32)) adder_1 (.a(X), .b(Y), .out(adder_1_out));  // open: cin, cout
  Subtractor #(.width(32)) subtractor_1 (.a(X), .b(Y), .out(subtractor_1_out));  // open: bin, bout
  assign XOR_out = X ^ Y;  // XOR_Gate XOR, 32 bits wide
  assign NOR_out = ~(X | Y);  // NOR_Gate NOR, 32 bits wide
  Comparator #(.width(32)) comparator_1 (.a(X), .b(Y), .eq(Equal), .lt(comparator_1_lt[0]));  // open: gt
  Comparator #(.width(32), .mode("unsigned")) comparator_2 (.a(X), .b(Y), .lt(comparator_2_lt[0]));  // open: gt, eq
  Multiplexer #(.select(4), .width(32), .enable("false")) multiplexer_1 (
    .in0(shifter_1_out), .in1(shifter_2_out), .in2(shifter_3_out), .in3(multiplier_1_out),
    .in4(divider_1_out), .in5(adder_1_out), .in6(subtractor_1_out), .in7(AND_out), .in8(OR_out),
    .in9(XOR_out), .in10(NOR_out), .in11({{31{1'b0}}, comparator_1_lt[0]}),
    .in12({{31{1'b0}}, comparator_2_lt[0]}), .in13({32{1'b0}}), .in14({32{1'b0}}), .in15({32{1'b0}}),
    .out(Result), .sel(AluOP));
  Multiplexer #(.select(4), .width(32), .enable("false")) multiplexer_2 (
    .in0({32{1'b0}}), .in1({32{1'b0}}), .in2({32{1'b0}}), .in3(multiplier_1_cout), .in4(divider_1_rem),
    .in5({32{1'b0}}), .in6({32{1'b0}}), .in7({32{1'b0}}), .in8({32{1'b0}}), .in9({32{1'b0}}),
    .in10({32{1'b0}}), .in11({32{1'b0}}), .in12({32{1'b0}}), .in13({32{1'b0}}), .in14({32{1'b0}}),
    .in15({32{1'b0}}), .out(Result_2), .sel(AluOP));

  // Other names for the same wires on the sheet: Result2[31:0] = Result_2; S[3:0] = AluOP

  // Notes on the sheet:
  //   不要改变此引脚区域内容，也不要改变ALU封装形式
  //   输入引脚
  //   输出引脚
endmodule

module MIPS_Regifile (
  input  [31:0] Din,
  input  Clk,
  input  WE,
  input  [4:0] R1_num,
  input  [4:0] W_num,
  input  [4:0] R2_num,
  output [31:0] R1,
  output [31:0] R2
);

  // RegisterFile registerfile_1: pin names not known; wires that end beside it: Din, Clk, WE, W_num, R1_num, R2_num, R1, R2
endmodule

module \理想流水线  (
);

  wire and_2_out, and_3_out, BLTZ_in, CLK, comparator_1_eq, ex_mem_1_memtoreg, ex_mem_1_regdst,
       ex_mem_1_regwrite, \ex_mem_1_传输状态out_表明当前传输数据有效 , Go, HB_in, id_ex_1_alusrcb, id_ex_1_memtoreg,
       id_ex_1_memwrite, id_ex_1_regdst, id_ex_1_regwrite, \id_ex_1_传输状态out_表明当前传输数据有效 ,
       \if_id_1_传输状态out_表明当前传输数据有效 , IR1, IR2, IR3, JMP_in, JR_in, LUI_in, mem_wb_1_memtoreg,
       mem_wb_1_regdst, MemWrite, nand_1_out, not_1_out, not_2_out, not_3_out, not_4_out, not_5_out, out,
       RegWrite, RST, SignedExt, SignedExt_in, SLLV_in, Syscall, W1, W2, W3, \硬布线控制器_1_alu_src ,
       \硬布线控制器_1_beq , \硬布线控制器_1_bne , \硬布线控制器_1_jal , \硬布线控制器_1_memtoreg , \硬布线控制器_1_memwrite ,
       \硬布线控制器_1_regdst , \硬布线控制器_1_regwrite , \结束 ;
  wire [3:0] id_ex_1_aluop, \硬布线控制器_1_alu_op ;
  wire [4:0] multiplexer_2_out, multiplexer_3_out, shamt, W_num;
  wire [15:0] \LoadUse次数 , \总周期数 , \插入气泡数 , \无条件分支数 , \条件分支成功数 , \立即数 ;
  wire [31:0] adder_1_out, bit_extender_1_out, bit_extender_2_out, Din, ex_mem_1_ir, ex_mem_1_r2,
       ex_mem_1_result, EX_PC, id_ex_1_r1, id_ex_1_r2, ID_PC, if_id_1_ir, IF_PC, LedData, MEM_PC,
       mem_wb_1_ir, mem_wb_1_memdata, mem_wb_1_result, mips_alu_1_result, mips_regifile_1_r2,
       multiplexer_4_out, R1, ram_1_data, rom_1_data, WB_PC, \立即数扩展 ;
  wire [31:16] id_ex_1_ir;

  Button \u_总复位  (.out(RST));
  Button _1 (.out(IR1));
  Button _2 (.out(IR2));
  Button _3 (.out(IR3));
  Button \u_继续运行  (.out(Go));
  LED led_1 (.in(W1));
  LED led_2 (.in(W2));
  LED led_3 (.in(W3));
  Hex_Digit_Display hex_digit_display_1 (.value(LedData[31:28]));  // open: dp
  nand nand_1 (nand_1_out, Syscall, ~out);  // NAND_Gate
  assign bit_extender_1_out = {{16{1'b0}}, {\立即数 [15:11], shamt, \立即数 [5:0]}};  // Bit_Extender bit_extender_1
  assign bit_extender_2_out = {{16{\立即数 [15]}}, {\立即数 [15:11], shamt, \立即数 [5:0]}};  // Bit_Extender bit_extender_2
  Hex_Digit_Display hex_digit_display_2 (.value(LedData[27:24]));  // open: dp
  Hex_Digit_Display hex_digit_display_3 (.value(LedData[23:20]));  // open: dp
  Counter #(.width(16), .max('hffff)) counter_1 (
    .count(nand_1_out), .Q(\总周期数 ), .clk(CLK), .clr(RST));  // open: load, D, carry
  Multiplexer #(.width(32), .enable("false")) multiplexer_1 (
    .in0(bit_extender_1_out), .in1(bit_extender_2_out), .out(\立即数扩展 ), .sel(SignedExt));
  Adder #(.width(32)) adder_1 (.a(IF_PC), .b(32'h4), .out(adder_1_out));  // open: cin, cout
  not not_1 (not_1_out, \结束 );
  Hex_Digit_Display hex_digit_display_4 (.value(LedData[19:16]));  // open: dp
  Hex_Digit_Display hex_digit_display_5 (.value(LedData[15:12]));  // open: dp
  Register #(.width(32)) PC (.D(adder_1_out), .en(not_1_out), .Q(IF_PC), .clk(CLK), .clr(RST));
  Hex_Digit_Display hex_digit_display_6 (.value(LedData[11:8]));  // open: dp
  Hex_Digit_Display hex_digit_display_7 (.value(LedData[7:4]));  // open: dp
  Clock clock_1 (.out(CLK));
  Hex_Digit_Display hex_digit_display_8 (.value(LedData[3:0]));  // open: dp
  Comparator #(.width(32)) comparator_1 (.a(R1), .b(32'ha), .eq(comparator_1_eq));  // open: gt, lt
  and and_1 (\结束 , comparator_1_eq, Syscall);
  ROM #(.addrWidth(10), .dataWidth(32)) rom_1 (.addr(IF_PC[11:2]), .data(rom_1_data), .sel(1'b1));
  and and_2 (and_2_out, \结束 , ~RST);  // AND_Gate
  // Probe on \总周期数 
  // Probe on \无条件分支数 
  // Probe on \条件分支成功数 
  // Probe on \插入气泡数 
  // Probe on \LoadUse次数 
  IF_ID if_id_1 (
    .CLK(CLK), .EN(and_2_out), .RST(RST), .PC_in(IF_PC), .PC(ID_PC), .IR_in(rom_1_data), .IR(if_id_1_ir),
    .\传输状态In_表明当前传输数据有效 (not_2_out), .\传输状态Out_表明当前传输数据有效 (\if_id_1_传输状态out_表明当前传输数据有效 ), .\数据有效 (1'b0));  // open: 预测位_in, 预测位
  not not_2 (not_2_out, and_2_out);
  // Probe on IF_PC[11:0]
  // Probe on ID_PC[11:0]
  // Probe on MEM_PC[11:0]
  // Probe on EX_PC[11:0]
  \硬布线控制器  \u_硬布线控制器_1  (
    .Func(if_id_1_ir[5:0]), .OP(if_id_1_ir[31:26]), .ALU_OP(\硬布线控制器_1_alu_op ),
    .MemToReg(\硬布线控制器_1_memtoreg ), .MemWrite(\硬布线控制器_1_memwrite ), .ALU_SRC(\硬布线控制器_1_alu_src ),
    .RegWrite(\硬布线控制器_1_regwrite ), .SysCALL(Syscall), .SignedExt(SignedExt_in), .RegDst(\硬布线控制器_1_regdst ),
    .JR(JR_in), .JMP(JMP_in), .Beq(\硬布线控制器_1_beq ), .JAL(\硬布线控制器_1_jal ), .Bne(\硬布线控制器_1_bne ), .LUI(LUI_in),
    .BTLZ(BLTZ_in), .HB(HB_in), .SLLV(SLLV_in));
  Multiplexer #(.width(5), .enable("false")) multiplexer_2 (
    .in0(if_id_1_ir[25:21]), .in1(5'b00010), .out(multiplexer_2_out), .sel(Syscall));
  Multiplexer #(.width(5), .enable("false")) multiplexer_3 (
    .in0(if_id_1_ir[20:16]), .in1(5'b00100), .out(multiplexer_3_out), .sel(Syscall));
  // Probe on WB_PC[11:0]
  and and_3 (and_3_out, \if_id_1_传输状态out_表明当前传输数据有效 , ~\结束 );  // AND_Gate
  MIPS_Regifile mips_regifile_1 (
    .Din(Din), .Clk(CLK), .R1(R1), .R2(mips_regifile_1_r2), .WE(RegWrite), .W_num(W_num),
    .R1_num(multiplexer_2_out), .R2_num(multiplexer_3_out));
  ID_EX id_ex_1 (
    .CLK(CLK), .PC_in(ID_PC), .EN(not_3_out), .IR_in(if_id_1_ir), .SignedExt(SignedExt),
    .MemToReg(id_ex_1_memtoreg), .MemWrite(id_ex_1_memwrite), .AluOP(id_ex_1_aluop),
    .AluSrcB(id_ex_1_alusrcb), .RegDst(id_ex_1_regdst), .RST(RST), .Beq_in(\硬布线控制器_1_beq ),
    .MemToReg_in(\硬布线控制器_1_memtoreg ), .Bne_in(\硬布线控制器_1_bne ), .MemWrite_in(\硬布线控制器_1_memwrite ),
    .AluOP_in(\硬布线控制器_1_alu_op ), .AluSrcB_in(\硬布线控制器_1_alu_src ), .JR_in(JR_in), .Jal_in(\硬布线控制器_1_jal ),
    .SignedExt_in(SignedExt_in), .LUI_in(LUI_in), .BLTZ_in(BLTZ_in), .HB_in(HB_in), .SLLV_in(SLLV_in),
    .JMP_in(JMP_in), .RegDst_in(\硬布线控制器_1_regdst ), .PC(EX_PC),
    .IR({id_ex_1_ir, \立即数 [15:11], shamt, \立即数 [5:0]}), .\传输状态In_表明当前传输数据有效 (and_3_out),
    .\传输状态Out_表明当前传输数据有效 (\id_ex_1_传输状态out_表明当前传输数据有效 ), .R1_in(R1), .R2_in(mips_regifile_1_r2),
    .R1(id_ex_1_r1), .R2(id_ex_1_r2), .RegWrite_in(\硬布线控制器_1_regwrite ), .Regwrite(id_ex_1_regwrite),
    .\跳转 (1'b0));  // open: JMP, JR, LUI, BLTZ, HB, Sllv, Beq, Bne, Jal, ForwardA_in, ForwardA, ForwardB_in, ForwardB, 预测位_in, 预测位
  not not_3 (not_3_out, and_3_out);
  Multiplexer #(.width(32), .enable("false")) multiplexer_4 (
    .in0(id_ex_1_r2), .in1(\立即数扩展 ), .out(multiplexer_4_out), .sel(id_ex_1_alusrcb));
  MIPS_ALU mips_alu_1 (
    .X(id_ex_1_r1), .Y(multiplexer_4_out), .AluOP(id_ex_1_aluop), .Result(mips_alu_1_result), .shamt(shamt));  // open: Equal, Result_2
  EX_MEM ex_mem_1 (
    .CLK(CLK), .EN(not_4_out), .RST(RST), .PC_in(EX_PC), .Result_in(mips_alu_1_result),
    .MemToReg_in(id_ex_1_memtoreg), .RegDst_in(id_ex_1_regdst), .MemWrite_in(id_ex_1_memwrite),
    .IR_in({id_ex_1_ir, \立即数 [15:11], shamt, \立即数 [5:0]}), .R2_in(id_ex_1_r2), .PC(MEM_PC),
    .Result(ex_mem_1_result), .IR(ex_mem_1_ir), .R2(ex_mem_1_r2),
    .\传输状态In_表明当前传输数据有效 (\id_ex_1_传输状态out_表明当前传输数据有效 ), .RegDst(ex_mem_1_regdst),
    .MemToReg(ex_mem_1_memtoreg), .MemWrite(MemWrite), .\传输状态Out_表明当前传输数据有效 (\ex_mem_1_传输状态out_表明当前传输数据有效 ),
    .RegWrite_in(id_ex_1_regwrite), .Regwrite(ex_mem_1_regwrite));  // open: Beq_in, JR_in, SLLV_in, Bne_in, Jal_in, JMP_in, LUI_in, BLTZ_in, HB_in, Beq, JR, JMP, Bne, Jal, Sllv, LUI, HB, BLTZ, R1_in, R1
  not not_4 (not_4_out, \id_ex_1_传输状态out_表明当前传输数据有效 );
  RAM #(.addrWidth(10), .dataWidth(32), .bus("separate")) ram_1 (
    .addr(ex_mem_1_result[11:2]), .din(ex_mem_1_r2), .data(ram_1_data), .str(MemWrite), .sel(1'b1),
    .clk(CLK), .ld(1'b1), .clr(RST));
  not not_5 (not_5_out, \ex_mem_1_传输状态out_表明当前传输数据有效 );
  MEM_WB mem_wb_1 (
    .CLK(CLK), .EN(not_5_out), .RST(RST), .PC_in(MEM_PC), .Result_in(ex_mem_1_result),
    .MemToReg_in(ex_mem_1_memtoreg), .RegDst_in(ex_mem_1_regdst), .RegWrite_in(ex_mem_1_regwrite),
    .IR_in(ex_mem_1_ir), .MemData_in(ram_1_data), .PC(WB_PC), .Result(mem_wb_1_result), .IR(mem_wb_1_ir),
    .MemData(mem_wb_1_memdata), .\传输状态In_表明当前传输数据有效 (\ex_mem_1_传输状态out_表明当前传输数据有效 ),
    .RegDst(mem_wb_1_regdst), .MemToReg(mem_wb_1_memtoreg), .Regwrite(RegWrite), .\传输状态Out_表明当前传输数据有效 (out));  // open: Beq_in, JR_in, SLLV_in, Bne_in, Jal_in, JMP_in, LUI_in, BLTZ_in, HB_in, Beq, JR, JMP, Bne, Jal, Sllv, LUI, HB, BLTZ, R1_in, R2_in, R1, R2
  Multiplexer #(.width(5), .enable("false")) multiplexer_5 (
    .in0(mem_wb_1_ir[20:16]), .in1(mem_wb_1_ir[15:11]), .out(W_num), .sel(mem_wb_1_regdst));
  Multiplexer #(.width(32), .enable("false")) multiplexer_6 (
    .in0(mem_wb_1_result), .in1(mem_wb_1_memdata), .out(Din), .sel(mem_wb_1_memtoreg));

  // Other names for the same wires on the sheet: 立即数[10:6] = shamt

  // Notes on the sheet:
  //   中断源
  //   中断等待指示
  //   数码管输出
  //   指令字
  //   contents of rom_1 (hex, n*v repeats v):
  //   20100000 20110001 20120002 20130003 36100000 36310001 36520002 36730003 ae100000 ae110004 ae120008
  //   ae13000c 2002000a 0 0 0 c
  //   Func
  //   rs
  //   rt
  //   OP
  //   Func
  //   流水调试日志用
  //   shamt
  //   rt
  //   rd
endmodule

// 源寄存器使用情况
module \源寄存器使用情况  (
  input  OP0,
  input  OP1,
  input  OP2,
  input  OP3,
  input  OP4,
  input  OP5,
  input  F0,
  input  F1,
  input  F2,
  input  F3,
  input  F4,
  input  F5,
  output R1_Used,
  output R2_Used
);

  wire and_1_out, and_2_out, and_3_out, and_4_out, and_5_out, and_6_out, and_7_out, and_8_out, and_9_out,
       and_10_out, and_11_out, and_12_out, and_13_out, and_14_out, and_15_out, and_16_out, and_17_out,
       and_18_out, and_19_out, and_20_out, and_21_out, and_22_out, and_23_out, and_24_out, and_25_out,
       and_26_out, and_27_out, and_28_out, and_29_out, and_30_out, and_31_out, and_32_out, and_33_out,
       and_34_out, and_35_out, and_36_out, and_37_out, and_38_out, and_39_out, and_40_out, and_41_out,
       and_42_out, not_1_out, not_2_out, not_3_out, not_4_out, not_5_out, not_6_out, not_7_out, not_8_out,
       not_9_out, not_10_out, not_11_out, not_12_out, not_13_out, not_14_out, not_15_out, not_16_out,
       not_17_out, not_18_out, not_19_out, not_20_out, not_21_out, not_22_out, not_23_out, not_24_out,
       not_25_out, not_26_out, not_27_out, not_28_out, not_29_out, not_30_out, not_31_out, not_32_out,
       not_33_out, not_34_out, not_35_out, not_36_out, not_37_out, not_38_out, not_39_out, not_40_out,
       not_41_out, not_42_out, not_43_out, not_44_out, not_45_out, not_46_out, not_47_out, not_48_out,
       not_49_out, not_50_out, not_51_out, not_52_out, not_53_out, not_54_out, not_55_out, not_56_out,
       not_57_out, not_58_out, not_59_out, not_60_out, not_61_out, not_62_out, not_63_out, not_64_out,
       not_65_out, not_66_out, not_67_out, not_68_out, not_69_out, not_70_out, not_71_out, not_72_out,
       not_73_out, not_74_out, not_75_out, not_76_out, not_77_out, not_78_out, not_79_out, not_80_out,
       not_81_out, not_82_out, not_83_out, not_84_out, not_85_out, not_86_out, not_87_out, not_88_out,
       not_89_out, not_90_out, not_91_out, not_92_out, not_93_out, not_94_out, not_95_out, not_96_out,
       not_97_out, not_98_out, not_99_out, not_100_out, not_101_out, not_102_out, not_103_out, not_104_out,
       not_105_out, not_106_out, not_107_out, not_108_out, not_109_out, not_110_out, not_111_out,
       not_112_out, not_113_out, not_114_out, not_115_out, not_116_out, not_117_out, not_118_out,
       not_119_out, not_120_out, not_121_out, not_122_out, not_123_out, not_124_out, not_125_out,
       not_126_out, not_127_out, not_128_out, not_129_out, not_130_out, not_131_out, not_132_out,
       not_133_out, not_134_out, not_135_out, not_136_out, not_137_out, not_138_out, not_139_out,
       not_140_out, not_141_out, not_142_out, not_143_out, not_144_out, not_145_out, not_146_out,
       not_147_out, not_148_out, not_149_out, not_150_out, not_151_out, not_152_out, not_153_out,
       not_154_out, not_155_out, not_156_out, not_157_out, not_158_out, not_159_out, not_160_out,
       not_161_out, not_162_out, not_163_out, not_164_out, not_165_out, not_166_out, not_167_out,
       not_168_out, not_169_out, not_170_out, not_171_out, not_172_out, not_173_out, not_174_out,
       not_175_out, not_176_out, not_177_out, not_178_out, not_179_out, not_180_out, not_181_out,
       not_182_out, not_183_out, not_184_out, not_185_out, not_186_out, not_187_out, not_188_out,
       not_189_out, not_190_out, not_191_out, not_192_out, not_193_out, not_194_out, not_195_out,
       not_196_out, not_197_out, not_198_out, not_199_out, not_200_out, not_201_out, not_202_out,
       not_203_out, not_204_out, not_205_out, not_206_out, not_207_out, not_208_out, not_209_out,
       not_210_out, not_211_out, not_212_out, not_213_out, not_214_out, not_215_out, not_216_out,
       not_217_out, not_218_out, not_219_out, not_220_out, not_221_out, not_222_out, not_223_out,
       not_224_out, not_225_out, not_226_out, not_227_out, not_228_out, not_229_out, not_230_out,
       not_231_out, not_232_out, not_233_out, not_234_out, not_235_out, not_236_out, not_237_out,
       not_238_out, not_239_out, not_240_out, not_241_out, not_242_out, not_243_out, not_244_out,
       not_245_out, not_246_out, not_247_out, not_248_out, not_249_out, not_250_out, not_251_out,
       not_252_out, not_253_out, not_254_out, not_255_out, not_256_out, not_257_out, not_258_out,
       not_259_out, not_260_out, not_261_out, not_262_out, not_263_out, not_264_out, not_265_out,
       not_266_out, not_267_out, not_268_out, not_269_out, not_270_out, not_271_out, not_272_out,
       not_273_out, not_274_out, not_275_out, not_276_out, not_277_out, not_278_out, not_279_out,
       not_280_out, not_281_out, not_282_out, not_283_out, not_284_out, not_285_out, not_286_out,
       not_287_out, not_288_out, not_289_out, not_290_out, not_291_out, not_292_out, not_293_out,
       not_294_out, not_295_out, not_296_out, not_297_out, not_298_out, not_299_out, not_300_out,
       not_301_out, not_302_out, not_303_out, not_304_out, not_305_out, not_306_out, not_307_out,
       not_308_out, not_309_out, not_310_out, not_311_out, not_312_out, not_313_out, not_314_out,
       not_315_out, not_316_out, not_317_out, not_318_out, not_319_out, not_320_out, not_321_out,
       not_322_out, not_323_out, not_324_out, not_325_out, not_326_out, not_327_out, not_328_out;

  not not_1 (not_1_out, OP5);
  not not_2 (not_2_out, OP4);
  not not_3 (not_3_out, OP3);
  not not_4 (not_4_out, OP2);
  not not_5 (not_5_out, OP1);
  not not_6 (not_6_out, OP0);
  not not_7 (not_7_out, F5);
  not not_8 (not_8_out, F4);
  not not_9 (not_9_out, F3);
  not not_10 (not_10_out, F2);
  not not_11 (not_11_out, F1);
  not not_12 (not_12_out, F0);
  not not_13 (not_13_out, OP5);
  not not_14 (not_14_out, OP4);
  not not_15 (not_15_out, OP3);
  not not_16 (not_16_out, OP2);
  not not_17 (not_17_out, OP1);
  not not_18 (not_18_out, OP0);
  not not_19 (not_19_out, F5);
  not not_20 (not_20_out, F4);
  not not_21 (not_21_out, F3);
  not not_22 (not_22_out, F2);
  not not_23 (not_23_out, OP5);
  not not_24 (not_24_out, OP4);
  not not_25 (not_25_out, OP3);
  not not_26 (not_26_out, OP2);
  not not_27 (not_27_out, OP1);
  not not_28 (not_28_out, OP0);
  not not_29 (not_29_out, F5);
  not not_30 (not_30_out, F4);
  not not_31 (not_31_out, F3);
  not not_32 (not_32_out, F2);
  not not_33 (not_33_out, F0);
  not not_34 (not_34_out, OP5);
  not not_35 (not_35_out, OP4);
  not not_36 (not_36_out, OP3);
  not not_37 (not_37_out, OP2);
  not not_38 (not_38_out, OP1);
  not not_39 (not_39_out, OP0);
  not not_40 (not_40_out, F4);
  not not_41 (not_41_out, F3);
  not not_42 (not_42_out, F2);
  not not_43 (not_43_out, F1);
  not not_44 (not_44_out, F0);
  not not_45 (not_45_out, OP5);
  not not_46 (not_46_out, OP4);
  not not_47 (not_47_out, OP3);
  not not_48 (not_48_out, OP2);
  not not_49 (not_49_out, OP1);
  not not_50 (not_50_out, OP0);
  not not_51 (not_51_out, F4);
  not not_52 (not_52_out, F3);
  not not_53 (not_53_out, F2);
  not not_54 (not_54_out, F1);
  not not_55 (not_55_out, OP5);
  not not_56 (not_56_out, OP4);
  not not_57 (not_57_out, OP3);
  not not_58 (not_58_out, OP2);
  not not_59 (not_59_out, OP1);
  not not_60 (not_60_out, OP0);
  not not_61 (not_61_out, F4);
  not not_62 (not_62_out, F3);
  not not_63 (not_63_out, F2);
  not not_64 (not_64_out, F0);
  not not_65 (not_65_out, OP5);
  not not_66 (not_66_out, OP4);
  not not_67 (not_67_out, OP3);
  not not_68 (not_68_out, OP2);
  not not_69 (not_69_out, OP1);
  not not_70 (not_70_out, OP0);
  not not_71 (not_71_out, F4);
  not not_72 (not_72_out, F3);
  not not_73 (not_73_out, F1);
  not not_74 (not_74_out, F0);
  not not_75 (not_75_out, OP5);
  not not_76 (not_76_out, OP4);
  not not_77 (not_77_out, OP3);
  not not_78 (not_78_out, OP2);
  not not_79 (not_79_out, OP1);
  not not_80 (not_80_out, OP0);
  not not_81 (not_81_out, F4);
  not not_82 (not_82_out, F3);
  not not_83 (not_83_out, F1);
  not not_84 (not_84_out, OP5);
  not not_85 (not_85_out, OP4);
  not not_86 (not_86_out, OP3);
  not not_87 (not_87_out, OP2);
  not not_88 (not_88_out, OP1);
  not not_89 (not_89_out, OP0);
  not not_90 (not_90_out, F4);
  not not_91 (not_91_out, F3);
  not not_92 (not_92_out, OP5);
  not not_93 (not_93_out, OP4);
  not not_94 (not_94_out, OP3);
  not not_95 (not_95_out, OP2);
  not not_96 (not_96_out, OP1);
  not not_97 (not_97_out, OP0);
  not not_98 (not_98_out, F4);
  not not_99 (not_99_out, F2);
  not not_100 (not_100_out, F0);
  not not_101 (not_101_out, OP5);
  not not_102 (not_102_out, OP4);
  not not_103 (not_103_out, OP3);
  not not_104 (not_104_out, OP2);
  not not_105 (not_105_out, OP1);
  not not_106 (not_106_out, OP0);
  not not_107 (not_107_out, F4);
  not not_108 (not_108_out, F2);
  not not_109 (not_109_out, OP5);
  not not_110 (not_110_out, OP4);
  not not_111 (not_111_out, OP3);
  not not_112 (not_112_out, OP2);
  not not_113 (not_113_out, OP1);
  not not_114 (not_114_out, OP0);
  not not_115 (not_115_out, F5);
  not not_116 (not_116_out, F4);
  not not_117 (not_117_out, F2);
  not not_118 (not_118_out, F1);
  not not_119 (not_119_out, F0);
  not not_120 (not_120_out, OP5);
  not not_121 (not_121_out, OP4);
  not not_122 (not_122_out, OP3);
  not not_123 (not_123_out, OP2);
  not not_124 (not_124_out, OP1);
  not not_125 (not_125_out, OP0);
  not not_126 (not_126_out, F5);
  not not_127 (not_127_out, F4);
  not not_128 (not_128_out, F1);
  not not_129 (not_129_out, F0);
  not not_130 (not_130_out, OP5);
  not not_131 (not_131_out, OP4);
  not not_132 (not_132_out, OP3);
  not not_133 (not_133_out, OP1);
  not not_134 (not_134_out, OP0);
  not not_135 (not_135_out, OP5);
  not not_136 (not_136_out, OP4);
  not not_137 (not_137_out, OP3);
  not not_138 (not_138_out, OP1);
  not not_139 (not_139_out, OP5);
  not not_140 (not_140_out, OP4);
  not not_141 (not_141_out, OP2);
  not not_142 (not_142_out, OP1);
  not not_143 (not_143_out, OP0);
  not not_144 (not_144_out, OP5);
  not not_145 (not_145_out, OP4);
  not not_146 (not_146_out, OP1);
  not not_147 (not_147_out, OP0);
  not not_148 (not_148_out, OP5);
  not not_149 (not_149_out, OP4);
  not not_150 (not_150_out, OP2);
  not not_151 (not_151_out, OP1);
  not not_152 (not_152_out, OP5);
  not not_153 (not_153_out, OP4);
  not not_154 (not_154_out, OP2);
  not not_155 (not_155_out, OP0);
  not not_156 (not_156_out, OP5);
  not not_157 (not_157_out, OP4);
  not not_158 (not_158_out, OP1);
  not not_159 (not_159_out, OP4);
  not not_160 (not_160_out, OP3);
  not not_161 (not_161_out, OP2);
  not not_162 (not_162_out, OP4);
  not not_163 (not_163_out, OP2);
  not not_164 (not_164_out, OP5);
  not not_165 (not_165_out, OP4);
  not not_166 (not_166_out, OP3);
  not not_167 (not_167_out, OP2);
  not not_168 (not_168_out, OP1);
  not not_169 (not_169_out, OP0);
  not not_170 (not_170_out, F5);
  not not_171 (not_171_out, F4);
  not not_172 (not_172_out, F3);
  not not_173 (not_173_out, F1);
  not not_174 (not_174_out, F0);
  not not_175 (not_175_out, OP4);
  not not_176 (not_176_out, OP3);
  not not_177 (not_177_out, OP2);
  not not_178 (not_178_out, OP1);
  not not_179 (not_179_out, OP5);
  not not_180 (not_180_out, OP4);
  not not_181 (not_181_out, OP3);
  not not_182 (not_182_out, OP2);
  not not_183 (not_183_out, OP1);
  not not_184 (not_184_out, OP5);
  not not_185 (not_185_out, OP4);
  not not_186 (not_186_out, OP3);
  not not_187 (not_187_out, OP2);
  not not_188 (not_188_out, OP1);
  not not_189 (not_189_out, OP0);
  not not_190 (not_190_out, F5);
  not not_191 (not_191_out, F4);
  not not_192 (not_192_out, F3);
  not not_193 (not_193_out, F2);
  not not_194 (not_194_out, F1);
  not not_195 (not_195_out, F0);
  not not_196 (not_196_out, OP5);
  not not_197 (not_197_out, OP4);
  not not_198 (not_198_out, OP3);
  not not_199 (not_199_out, OP2);
  not not_200 (not_200_out, OP1);
  not not_201 (not_201_out, OP0);
  not not_202 (not_202_out, F5);
  not not_203 (not_203_out, F4);
  not not_204 (not_204_out, F3);
  not not_205 (not_205_out, F2);
  not not_206 (not_206_out, OP5);
  not not_207 (not_207_out, OP4);
  not not_208 (not_208_out, OP3);
  not not_209 (not_209_out, OP2);
  not not_210 (not_210_out, OP1);
  not not_211 (not_211_out, OP0);
  not not_212 (not_212_out, F5);
  not not_213 (not_213_out, F4);
  not not_214 (not_214_out, F3);
  not not_215 (not_215_out, F2);
  not not_216 (not_216_out, F0);
  not not_217 (not_217_out, OP5);
  not not_218 (not_218_out, OP4);
  not not_219 (not_219_out, OP3);
  not not_220 (not_220_out, OP2);
  not not_221 (not_221_out, OP1);
  not not_222 (not_222_out, OP0);
  not not_223 (not_223_out, F4);
  not not_224 (not_224_out, F3);
  not not_225 (not_225_out, F2);
  not not_226 (not_226_out, F1);
  not not_227 (not_227_out, F0);
  not not_228 (not_228_out, OP5);
  not not_229 (not_229_out, OP4);
  not not_230 (not_230_out, OP3);
  not not_231 (not_231_out, OP2);
  not not_232 (not_232_out, OP1);
  not not_233 (not_233_out, OP0);
  not not_234 (not_234_out, F4);
  not not_235 (not_235_out, F3);
  not not_236 (not_236_out, F2);
  not not_237 (not_237_out, F1);
  not not_238 (not_238_out, OP5);
  not not_239 (not_239_out, OP4);
  not not_240 (not_240_out, OP3);
  not not_241 (not_241_out, OP2);
  not not_242 (not_242_out, OP1);
  not not_243 (not_243_out, OP0);
  not not_244 (not_244_out, F4);
  not not_245 (not_245_out, F3);
  not not_246 (not_246_out, F2);
  not not_247 (not_247_out, F0);
  not not_248 (not_248_out, OP5);
  not not_249 (not_249_out, OP4);
  not not_250 (not_250_out, OP3);
  not not_251 (not_251_out, OP2);
  not not_252 (not_252_out, OP1);
  not not_253 (not_253_out, OP0);
  not not_254 (not_254_out, F4);
  not not_255 (not_255_out, F3);
  not not_256 (not_256_out, F1);
  not not_257 (not_257_out, F0);
  not not_258 (not_258_out, OP5);
  not not_259 (not_259_out, OP4);
  not not_260 (not_260_out, OP3);
  not not_261 (not_261_out, OP2);
  not not_262 (not_262_out, OP1);
  not not_263 (not_263_out, OP0);
  not not_264 (not_264_out, F4);
  not not_265 (not_265_out, F3);
  not not_266 (not_266_out, F1);
  not not_267 (not_267_out, OP5);
  not not_268 (not_268_out, OP4);
  not not_269 (not_269_out, OP3);
  not not_270 (not_270_out, OP2);
  not not_271 (not_271_out, OP1);
  not not_272 (not_272_out, OP0);
  not not_273 (not_273_out, F4);
  not not_274 (not_274_out, F3);
  not not_275 (not_275_out, OP5);
  not not_276 (not_276_out, OP4);
  not not_277 (not_277_out, OP3);
  not not_278 (not_278_out, OP2);
  not not_279 (not_279_out, OP1);
  not not_280 (not_280_out, OP0);
  not not_281 (not_281_out, F4);
  not not_282 (not_282_out, F2);
  not not_283 (not_283_out, F0);
  not not_284 (not_284_out, OP5);
  not not_285 (not_285_out, OP4);
  not not_286 (not_286_out, OP3);
  not not_287 (not_287_out, OP2);
  not not_288 (not_288_out, OP1);
  not not_289 (not_289_out, OP0);
  not not_290 (not_290_out, F4);
  not not_291 (not_291_out, F2);
  not not_292 (not_292_out, OP5);
  not not_293 (not_293_out, OP4);
  not not_294 (not_294_out, OP3);
  not not_295 (not_295_out, OP2);
  not not_296 (not_296_out, OP1);
  not not_297 (not_297_out, OP0);
  not not_298 (not_298_out, F5);
  not not_299 (not_299_out, F4);
  not not_300 (not_300_out, F1);
  not not_301 (not_301_out, F0);
  not not_302 (not_302_out, OP5);
  not not_303 (not_303_out, OP4);
  not not_304 (not_304_out, OP3);
  not not_305 (not_305_out, OP1);
  not not_306 (not_306_out, OP0);
  not not_307 (not_307_out, OP5);
  not not_308 (not_308_out, OP4);
  not not_309 (not_309_out, OP3);
  not not_310 (not_310_out, OP1);
  not not_311 (not_311_out, OP4);
  not not_312 (not_312_out, OP2);
  not not_313 (not_313_out, OP5);
  not not_314 (not_314_out, OP4);
  not not_315 (not_315_out, OP3);
  not not_316 (not_316_out, OP2);
  not not_317 (not_317_out, OP1);
  not not_318 (not_318_out, OP0);
  not not_319 (not_319_out, F5);
  not not_320 (not_320_out, F4);
  not not_321 (not_321_out, F3);
  not not_322 (not_322_out, F1);
  not not_323 (not_323_out, F0);
  not not_324 (not_324_out, OP5);
  not not_325 (not_325_out, OP4);
  not not_326 (not_326_out, OP3);
  not not_327 (not_327_out, OP2);
  not not_328 (not_328_out, OP1);
  and and_1 (and_1_out, not_1_out, not_2_out, not_3_out, not_4_out, not_5_out, not_6_out, not_7_out, not_8_out, not_9_out, not_10_out, not_11_out, not_12_out);
  and and_2 (and_2_out, not_13_out, not_14_out, not_15_out, not_16_out, not_17_out, not_18_out, not_19_out, not_20_out, not_21_out, not_22_out, F1, F0);
  and and_3 (and_3_out, not_23_out, not_24_out, not_25_out, not_26_out, not_27_out, not_28_out, not_29_out, not_30_out, not_31_out, not_32_out, F1, not_33_out);
  and and_4 (and_4_out, not_34_out, not_35_out, not_36_out, not_37_out, not_38_out, not_39_out, F5, not_40_out, not_41_out, not_42_out, not_43_out, not_44_out);
  and and_5 (and_5_out, not_45_out, not_46_out, not_47_out, not_48_out, not_49_out, not_50_out, F5, not_51_out, not_52_out, not_53_out, not_54_out, F0);
  and and_6 (and_6_out, not_55_out, not_56_out, not_57_out, not_58_out, not_59_out, not_60_out, F5, not_61_out, not_62_out, not_63_out, F1, not_64_out);
  and and_7 (and_7_out, not_65_out, not_66_out, not_67_out, not_68_out, not_69_out, not_70_out, F5, not_71_out, not_72_out, F2, not_73_out, not_74_out);
  and and_8 (and_8_out, not_75_out, not_76_out, not_77_out, not_78_out, not_79_out, not_80_out, F5, not_81_out, not_82_out, F2, not_83_out, F0);
  and and_9 (and_9_out, not_84_out, not_85_out, not_86_out, not_87_out, not_88_out, not_89_out, F5, not_90_out, not_91_out, F2, F1, F0);
  and and_10 (and_10_out, not_92_out, not_93_out, not_94_out, not_95_out, not_96_out, not_97_out, F5, not_98_out, F3, not_99_out, F1, not_100_out);
  and and_11 (and_11_out, not_101_out, not_102_out, not_103_out, not_104_out, not_105_out, not_106_out, F5, not_107_out, F3, not_108_out, F1, F0);
  and and_12 (and_12_out, not_109_out, not_110_out, not_111_out, not_112_out, not_113_out, not_114_out, not_115_out, not_116_out, F3, not_117_out, not_118_out, not_119_out);
  and and_13 (and_13_out, not_120_out, not_121_out, not_122_out, not_123_out, not_124_out, not_125_out, not_126_out, not_127_out, F3, F2, not_128_out, not_129_out);
  and and_14 (and_14_out, not_130_out, not_131_out, not_132_out, OP2, not_133_out, not_134_out);
  and and_15 (and_15_out, not_135_out, not_136_out, not_137_out, OP2, not_138_out, OP0);
  and and_16 (and_16_out, not_139_out, not_140_out, OP3, not_141_out, not_142_out, not_143_out);
  and and_17 (and_17_out, not_144_out, not_145_out, OP3, OP2, not_146_out, not_147_out);
  and and_18 (and_18_out, not_148_out, not_149_out, OP3, not_150_out, not_151_out, OP0);
  and and_19 (and_19_out, not_152_out, not_153_out, OP3, not_154_out, OP1, not_155_out);
  and and_20 (and_20_out, not_156_out, not_157_out, OP3, OP2, not_158_out, OP0);
  and and_21 (and_21_out, OP5, not_159_out, not_160_out, not_161_out, OP1, OP0);
  and and_22 (and_22_out, OP5, not_162_out, OP3, not_163_out, OP1, OP0);
  and and_23 (and_23_out, not_164_out, not_165_out, not_166_out, not_167_out, not_168_out, not_169_out, not_170_out, not_171_out, not_172_out, F2, not_173_out, not_174_out);
  and and_24 (and_24_out, OP5, not_175_out, not_176_out, not_177_out, not_178_out, OP0);
  and and_25 (and_25_out, not_179_out, not_180_out, not_181_out, not_182_out, not_183_out, OP0);
  and and_26 (and_26_out, not_184_out, not_185_out, not_186_out, not_187_out, not_188_out, not_189_out, not_190_out, not_191_out, not_192_out, not_193_out, not_194_out, not_195_out);
  and and_27 (and_27_out, not_196_out, not_197_out, not_198_out, not_199_out, not_200_out, not_201_out, not_202_out, not_203_out, not_204_out, not_205_out, F1, F0);
  and and_28 (and_28_out, not_206_out, not_207_out, not_208_out, not_209_out, not_210_out, not_211_out, not_212_out, not_213_out, not_214_out, not_215_out, F1, not_216_out);
  and and_29 (and_29_out, not_217_out, not_218_out, not_219_out, not_220_out, not_221_out, not_222_out, F5, not_223_out, not_224_out, not_225_out, not_226_out, not_227_out);
  and and_30 (and_30_out, not_228_out, not_229_out, not_230_out, not_231_out, not_232_out, not_233_out, F5, not_234_out, not_235_out, not_236_out, not_237_out, F0);
  and and_31 (and_31_out, not_238_out, not_239_out, not_240_out, not_241_out, not_242_out, not_243_out, F5, not_244_out, not_245_out, not_246_out, F1, not_247_out);
  and and_32 (and_32_out, not_248_out, not_249_out, not_250_out, not_251_out, not_252_out, not_253_out, F5, not_254_out, not_255_out, F2, not_256_out, not_257_out);
  and and_33 (and_33_out, not_258_out, not_259_out, not_260_out, not_261_out, not_262_out, not_263_out, F5, not_264_out, not_265_out, F2, not_266_out, F0);
  and and_34 (and_34_out, not_267_out, not_268_out, not_269_out, not_270_out, not_271_out, not_272_out, F5, not_273_out, not_274_out, F2, F1, F0);
  and and_35 (and_35_out, not_275_out, not_276_out, not_277_out, not_278_out, not_279_out, not_280_out, F5, not_281_out, F3, not_282_out, F1, not_283_out);
  and and_36 (and_36_out, not_284_out, not_285_out, not_286_out, not_287_out, not_288_out, not_289_out, F5, not_290_out, F3, not_291_out, F1, F0);
  and and_37 (and_37_out, not_292_out, not_293_out, not_294_out, not_295_out, not_296_out, not_297_out, not_298_out, not_299_out, F3, F2, not_300_out, not_301_out);
  and and_38 (and_38_out, not_302_out, not_303_out, not_304_out, OP2, not_305_out, not_306_out);
  and and_39 (and_39_out, not_307_out, not_308_out, not_309_out, OP2, not_310_out, OP0);
  and and_40 (and_40_out, OP5, not_311_out, OP3, not_312_out, OP1, OP0);
  and and_41 (and_41_out, not_313_out, not_314_out, not_315_out, not_316_out, not_317_out, not_318_out, not_319_out, not_320_out, not_321_out, F2, not_322_out, not_323_out);
  and and_42 (and_42_out, not_324_out, not_325_out, not_326_out, not_327_out, not_328_out, OP0);
  or or_1 (R1_Used, and_1_out, and_2_out, and_3_out, and_4_out, and_5_out, and_6_out, and_7_out, and_8_out, and_9_out, and_10_out, and_11_out, and_12_out, and_13_out, and_14_out, and_15_out, and_16_out, and_17_out, and_18_out, and_19_out, and_20_out, and_21_out, and_22_out, and_23_out, and_24_out, and_25_out);
  or or_2 (R2_Used, and_26_out, and_27_out, and_28_out, and_29_out, and_30_out, and_31_out, and_32_out, and_33_out, and_34_out, and_35_out, and_36_out, and_37_out, and_38_out, and_39_out, and_40_out, and_41_out, and_42_out);
endmodule

module \数据相关检测  (
  input  [5:0] OP,
  input  [4:0] EX_WriteReg_num,
  input  EX_RegWrite,
  input  [4:0] MEM_WriteReg_num,
  input  MEM_RegWrite,
  input  [5:0] Func,
  input  [4:0] ID_R1_num,
  input  [4:0] ID_R2_num,
  output \数据相关 
);

  wire and_5_out, and_6_out, and_7_out, and_8_out, comparator_1_eq, comparator_2_eq, comparator_3_eq,
       comparator_4_eq, comparator_5_eq, comparator_6_eq, R1_EX, R1_MEM, R1_Used, R2_EX, R2_MEM, R2_Used;

  \源寄存器使用情况  \u_源寄存器使用情况_1  (
    .OP0(OP[0]), .OP1(OP[1]), .OP2(OP[2]), .OP3(OP[3]), .OP4(OP[4]), .OP5(OP[5]), .F0(Func[0]), .F1(Func[1]),
    .F2(Func[2]), .F3(Func[3]), .F4(Func[4]), .F5(Func[5]), .R1_Used(R1_Used), .R2_Used(R2_Used));
  Comparator #(.width(5)) comparator_1 (.a(ID_R1_num), .b(EX_WriteReg_num), .eq(comparator_1_eq));  // open: gt, lt
  Comparator #(.width(5)) comparator_2 (.a(ID_R1_num), .b(MEM_WriteReg_num), .eq(comparator_2_eq));  // open: gt, lt
  Comparator #(.width(5)) comparator_3 (.a(ID_R2_num), .b(EX_WriteReg_num), .eq(comparator_3_eq));  // open: gt, lt
  Comparator #(.width(5)) comparator_4 (.a(ID_R2_num), .b(MEM_WriteReg_num), .eq(comparator_4_eq));  // open: gt, lt
  Comparator #(.width(5)) comparator_5 (.a(EX_WriteReg_num), .b({5{1'b0}}), .eq(comparator_5_eq));  // open: gt, lt
  Comparator #(.width(5)) comparator_6 (.a(MEM_WriteReg_num), .b({5{1'b0}}), .eq(comparator_6_eq));  // open: gt, lt
  and and_1 (R1_EX, comparator_1_eq, ~comparator_5_eq);  // AND_Gate
  and and_2 (R1_MEM, comparator_2_eq, ~comparator_6_eq);  // AND_Gate
  and and_3 (R2_EX, comparator_3_eq, ~comparator_5_eq);  // AND_Gate
  and and_4 (R2_MEM, comparator_4_eq, ~comparator_6_eq);  // AND_Gate
  and and_5 (and_5_out, R1_Used, EX_RegWrite, R1_EX);
  and and_6 (and_6_out, R1_Used, MEM_RegWrite, R1_MEM);
  and and_7 (and_7_out, R2_Used, MEM_RegWrite, R2_MEM);
  and and_8 (and_8_out, R2_Used, EX_RegWrite, R2_EX);
  or or_1 (\数据相关 , and_5_out, and_6_out, and_7_out, and_8_out);

  // Other names for the same wires on the sheet: OP_CODE[5:0] = OP
endmodule

module IF_ID (
  input  CLK,
  input  EN,
  input  RST,
  input  \数据有效 ,
  input  [1:0] \预测位_in ,
  input  [31:0] PC_in,
  input  [31:0] IR_in,
  input  \传输状态In_表明当前传输数据有效 ,
  output [1:0] \预测位 ,
  output [31:0] PC,
  output [31:0] IR,
  output \传输状态Out_表明当前传输数据有效 
);

  wire and_1_out, multiplexer_3_out, not_1_out, not_2_out, not_3_out;
  wire [1:0] multiplexer_4_out;
  wire [31:0] multiplexer_1_out, multiplexer_2_out;

  Multiplexer #(.width(32), .enable("false")) multiplexer_1 (
    .in0(PC_in), .in1({32{1'b0}}), .out(multiplexer_1_out), .sel(RST));
  Multiplexer #(.width(32), .enable("false")) multiplexer_2 (
    .in0(IR_in), .in1({32{1'b0}}), .out(multiplexer_2_out), .sel(RST));
  Register #(.width(32)) register_1 (.D(multiplexer_1_out), .en(not_1_out), .Q(PC), .clk(CLK));  // open: clr
  not not_1 (not_1_out, EN);
  Register #(.width(32)) register_2 (.D(multiplexer_2_out), .en(not_2_out), .Q(IR), .clk(CLK));  // open: clr
  not not_2 (not_2_out, EN);
  Multiplexer #(.enable("false")) multiplexer_3 (
    .in0(\传输状态In_表明当前传输数据有效 ), .in1(1'b0), .out(multiplexer_3_out), .sel(and_1_out));
  and and_1 (and_1_out, RST, ~\数据有效 );  // AND_Gate
  Multiplexer #(.width(2), .enable("false")) multiplexer_4 (
    .in0(\预测位_in ), .in1(2'b00), .out(multiplexer_4_out), .sel(RST));
  not not_3 (not_3_out, EN);
  Register #(.width(1)) register_3 (
    .D(multiplexer_3_out), .Q(\传输状态Out_表明当前传输数据有效 ), .clk(CLK), .clr(1'b0));  // open: en
  Register #(.width(2)) register_4 (.D(multiplexer_4_out), .en(not_3_out), .Q(\预测位 ), .clk(CLK));  // open: clr
endmodule

module ID_EX (
  input  CLK,
  input  EN,
  input  RST,
  input  \跳转 ,
  input  Beq_in,
  input  SignedExt_in,
  input  SLLV_in,
  input  [31:0] PC_in,
  input  Bne_in,
  input  JR_in,
  input  JMP_in,
  input  [31:0] R1_in,
  input  MemToReg_in,
  input  Jal_in,
  input  RegDst_in,
  input  MemWrite_in,
  input  LUI_in,
  input  RegWrite_in,
  input  [31:0] IR_in,
  input  [3:0] AluOP_in,
  input  BLTZ_in,
  input  [1:0] \预测位_in ,
  input  [31:0] R2_in,
  input  AluSrcB_in,
  input  HB_in,
  input  [1:0] ForwardA_in,
  input  [1:0] ForwardB_in,
  input  \传输状态In_表明当前传输数据有效 ,
  output Beq,
  output JR,
  output JMP,
  output [31:0] PC,
  output Bne,
  output Jal,
  output RegDst,
  output [31:0] R1,
  output MemToReg,
  output SignedExt,
  output Regwrite,
  output MemWrite,
  output LUI,
  output Sllv,
  output [31:0] IR,
  output [3:0] AluOP,
  output BLTZ,
  output [1:0] \预测位 ,
  output [31:0] R2,
  output [1:0] ForwardB,
  output AluSrcB,
  output HB,
  output [1:0] ForwardA,
  output \传输状态Out_表明当前传输数据有效 
);

  wire and_1_out, multiplexer_6_out, multiplexer_7_out, multiplexer_8_out, multiplexer_9_out,
       multiplexer_10_out, multiplexer_12_out, multiplexer_13_out, multiplexer_14_out, multiplexer_15_out,
       multiplexer_16_out, multiplexer_17_out, multiplexer_19_out, multiplexer_20_out, multiplexer_21_out,
       multiplexer_22_out, multiplexer_23_out, not_1_out, not_2_out, not_3_out, not_4_out, not_5_out,
       not_6_out, not_7_out, not_8_out, not_9_out, not_10_out, not_11_out, not_12_out, not_13_out,
       not_14_out, not_15_out, not_16_out, not_17_out, not_18_out, not_19_out, not_20_out, not_21_out,
       not_22_out, not_23_out;
  wire [1:0] multiplexer_11_out, multiplexer_18_out, multiplexer_24_out;
  wire [3:0] multiplexer_5_out;
  wire [31:0] multiplexer_1_out, multiplexer_2_out, multiplexer_3_out, multiplexer_4_out;

  Multiplexer #(.width(32), .enable("false")) multiplexer_1 (
    .in0(PC_in), .in1({32{1'b0}}), .out(multiplexer_1_out), .sel(RST));
  Multiplexer #(.width(32), .enable("false")) multiplexer_2 (
    .in0(IR_in), .in1({32{1'b0}}), .out(multiplexer_2_out), .sel(RST));
  Multiplexer #(.width(32), .enable("false")) multiplexer_3 (
    .in0(R1_in), .in1({32{1'b0}}), .out(multiplexer_3_out), .sel(RST));
  Multiplexer #(.width(32), .enable("false")) multiplexer_4 (
    .in0(R2_in), .in1({32{1'b0}}), .out(multiplexer_4_out), .sel(RST));
  Multiplexer #(.width(4), .enable("false")) multiplexer_5 (
    .in0(AluOP_in), .in1(4'b0000), .out(multiplexer_5_out), .sel(RST));
  Register #(.width(32)) register_1 (.D(multiplexer_1_out), .en(not_1_out), .Q(PC), .clk(CLK));  // open: clr
  not not_1 (not_1_out, EN);
  Register #(.width(32)) register_2 (.D(multiplexer_2_out), .en(not_2_out), .Q(IR), .clk(CLK));  // open: clr
  not not_2 (not_2_out, EN);
  Register #(.width(32)) register_3 (.D(multiplexer_3_out), .en(not_3_out), .Q(R1), .clk(CLK));  // open: clr
  not not_3 (not_3_out, EN);
  Register #(.width(32)) register_4 (.D(multiplexer_4_out), .en(not_4_out), .Q(R2), .clk(CLK));  // open: clr
  not not_4 (not_4_out, EN);
  Register #(.width(4)) register_5 (.D(multiplexer_5_out), .en(not_5_out), .Q(AluOP), .clk(CLK));  // open: clr
  not not_5 (not_5_out, EN);
  Multiplexer #(.enable("false")) multiplexer_6 (.in0(Beq_in), .in1(1'b0), .out(multiplexer_6_out), .sel(RST));
  not not_6 (not_6_out, EN);
  Multiplexer #(.enable("false")) multiplexer_7 (.in0(MemWrite_in), .in1(1'b0), .out(multiplexer_7_out), .sel(RST));
  not not_7 (not_7_out, EN);
  Multiplexer #(.enable("false")) multiplexer_8 (.in0(LUI_in), .in1(1'b0), .out(multiplexer_8_out), .sel(RST));
  not not_8 (not_8_out, EN);
  Multiplexer #(.enable("false")) multiplexer_9 (.in0(JMP_in), .in1(1'b0), .out(multiplexer_9_out), .sel(RST));
  not not_9 (not_9_out, EN);
  Multiplexer #(.enable("false")) multiplexer_10 (.in0(SignedExt_in), .in1(1'b0), .out(multiplexer_10_out), .sel(RST));
  not not_10 (not_10_out, EN);
  Multiplexer #(.width(2), .enable("false")) multiplexer_11 (
    .in0(\预测位_in ), .in1(2'b00), .out(multiplexer_11_out), .sel(RST));
  not not_11 (not_11_out, EN);
  Multiplexer #(.enable("false")) multiplexer_12 (
    .in0(\传输状态In_表明当前传输数据有效 ), .in1(1'b0), .out(multiplexer_12_out), .sel(and_1_out));
  and and_1 (and_1_out, RST, ~\跳转 );  // AND_Gate
  Register #(.width(1)) register_6 (.D(multiplexer_6_out), .en(not_6_out), .Q(Beq), .clk(CLK));  // open: clr
  Register #(.width(1)) register_7 (.D(multiplexer_7_out), .en(not_7_out), .Q(MemWrite), .clk(CLK));  // open: clr
  Register #(.width(1)) register_8 (.D(multiplexer_8_out), .en(not_8_out), .Q(LUI), .clk(CLK));  // open: clr
  Register #(.width(1)) register_9 (.D(multiplexer_9_out), .en(not_9_out), .Q(JMP), .clk(CLK));  // open: clr
  Register #(.width(1)) register_10 (.D(multiplexer_10_out), .en(not_10_out), .Q(SignedExt), .clk(CLK));  // open: clr
  Register #(.width(2)) register_11 (.D(multiplexer_11_out), .en(not_11_out), .Q(\预测位 ), .clk(CLK));  // open: clr
  Register #(.width(1)) register_12 (
    .D(multiplexer_12_out), .Q(\传输状态Out_表明当前传输数据有效 ), .clk(CLK), .clr(1'b0));  // open: en
  Multiplexer #(.enable("false")) multiplexer_13 (.in0(Bne_in), .in1(1'b0), .out(multiplexer_13_out), .sel(RST));
  not not_12 (not_12_out, EN);
  Multiplexer #(.enable("false")) multiplexer_14 (.in0(AluSrcB_in), .in1(1'b0), .out(multiplexer_14_out), .sel(RST));
  not not_13 (not_13_out, EN);
  Multiplexer #(.enable("false")) multiplexer_15 (.in0(BLTZ_in), .in1(1'b0), .out(multiplexer_15_out), .sel(RST));
  not not_14 (not_14_out, EN);
  Multiplexer #(.enable("false")) multiplexer_16 (.in0(RegDst_in), .in1(1'b0), .out(multiplexer_16_out), .sel(RST));
  not not_15 (not_15_out, EN);
  Register #(.width(1)) register_13 (.D(multiplexer_13_out), .en(not_12_out), .Q(Bne), .clk(CLK));  // open: clr
  Register #(.width(1)) register_14 (.D(multiplexer_14_out), .en(not_13_out), .Q(AluSrcB), .clk(CLK));  // open: clr
  Register #(.width(1)) register_15 (.D(multiplexer_15_out), .en(not_14_out), .Q(BLTZ), .clk(CLK));  // open: clr
  Register #(.width(1)) register_16 (.D(multiplexer_16_out), .en(not_15_out), .Q(RegDst), .clk(CLK));  // open: clr
  Register #(.width(1)) register_17 (.D(multiplexer_17_out), .en(not_16_out), .Q(Jal), .clk(CLK));  // open: clr
  Multiplexer #(.enable("false")) multiplexer_17 (.in0(Jal_in), .in1(1'b0), .out(multiplexer_17_out), .sel(RST));
  not not_16 (not_16_out, EN);
  Register #(.width(2)) register_18 (.D(multiplexer_18_out), .en(not_17_out), .Q(ForwardA), .clk(CLK));  // open: clr
  Multiplexer #(.width(2), .enable("false")) multiplexer_18 (
    .in0(ForwardA_in), .in1(2'b00), .out(multiplexer_18_out), .sel(RST));
  not not_17 (not_17_out, EN);
  Multiplexer #(.enable("false")) multiplexer_19 (.in0(MemToReg_in), .in1(1'b0), .out(multiplexer_19_out), .sel(RST));
  not not_18 (not_18_out, EN);
  Multiplexer #(.enable("false")) multiplexer_20 (.in0(JR_in), .in1(1'b0), .out(multiplexer_20_out), .sel(RST));
  not not_19 (not_19_out, EN);
  Multiplexer #(.enable("false")) multiplexer_21 (.in0(HB_in), .in1(1'b0), .out(multiplexer_21_out), .sel(RST));
  not not_20 (not_20_out, EN);
  Multiplexer #(.enable("false")) multiplexer_22 (.in0(SLLV_in), .in1(1'b0), .out(multiplexer_22_out), .sel(RST));
  not not_21 (not_21_out, EN);
  Multiplexer #(.enable("false")) multiplexer_23 (.in0(RegWrite_in), .in1(1'b0), .out(multiplexer_23_out), .sel(RST));
  not not_22 (not_22_out, EN);
  Multiplexer #(.width(2), .enable("false")) multiplexer_24 (
    .in0(ForwardB_in), .in1(2'b00), .out(multiplexer_24_out), .sel(RST));
  not not_23 (not_23_out, EN);
  Register #(.width(1)) register_19 (.D(multiplexer_19_out), .en(not_18_out), .Q(MemToReg), .clk(CLK));  // open: clr
  Register #(.width(1)) register_20 (.D(multiplexer_20_out), .en(not_19_out), .Q(JR), .clk(CLK));  // open: clr
  Register #(.width(1)) register_21 (.D(multiplexer_21_out), .en(not_20_out), .Q(HB), .clk(CLK));  // open: clr
  Register #(.width(1)) register_22 (.D(multiplexer_22_out), .en(not_21_out), .Q(Sllv), .clk(CLK));  // open: clr
  Register #(.width(1)) register_23 (.D(multiplexer_23_out), .en(not_22_out), .Q(Regwrite), .clk(CLK));  // open: clr
  Register #(.width(2)) register_24 (.D(multiplexer_24_out), .en(not_23_out), .Q(ForwardB), .clk(CLK));  // open: clr

  // Other names for the same wires on the sheet: MenToReg = MemToReg; MenWrite = MemWrite
endmodule

module EX_MEM (
  input  CLK,
  input  EN,
  input  RST,
  input  Beq_in,
  input  JR_in,
  input  SLLV_in,
  input  [31:0] PC_in,
  input  Bne_in,
  input  Jal_in,
  input  JMP_in,
  input  [31:0] R1_in,
  input  [31:0] Result_in,
  input  MemToReg_in,
  input  LUI_in,
  input  RegDst_in,
  input  MemWrite_in,
  input  BLTZ_in,
  input  HB_in,
  input  [31:0] IR_in,
  input  RegWrite_in,
  input  [31:0] R2_in,
  input  \传输状态In_表明当前传输数据有效 ,
  output [31:0] Result,
  output Beq,
  output JR,
  output JMP,
  output [31:0] PC,
  output Bne,
  output Jal,
  output RegDst,
  output [31:0] R1,
  output Sllv,
  output MemToReg,
  output LUI,
  output HB,
  output MemWrite,
  output BLTZ,
  output [31:0] IR,
  output Regwrite,
  output [31:0] R2,
  output \传输状态Out_表明当前传输数据有效 
);

  wire multiplexer_6_out, multiplexer_7_out, multiplexer_8_out, multiplexer_9_out, multiplexer_10_out,
       multiplexer_11_out, multiplexer_12_out, multiplexer_13_out, multiplexer_14_out, multiplexer_15_out,
       multiplexer_16_out, multiplexer_17_out, multiplexer_18_out, multiplexer_19_out, not_1_out, not_2_out,
       not_3_out, not_4_out, not_5_out, not_6_out, not_7_out, not_8_out, not_9_out, not_10_out, not_11_out,
       not_12_out, not_13_out, not_14_out, not_15_out, not_16_out, not_17_out, not_18_out;
  wire [31:0] multiplexer_1_out, multiplexer_2_out, multiplexer_3_out, multiplexer_4_out, multiplexer_5_out,
       undriven;

  Multiplexer #(.width(32), .enable("false")) multiplexer_1 (
    .in0(PC_in), .in1({32{1'b0}}), .out(multiplexer_1_out), .sel(RST));
  Multiplexer #(.width(32), .enable("false")) multiplexer_2 (
    .in0(IR_in), .in1({32{1'b0}}), .out(multiplexer_2_out), .sel(RST));
  Multiplexer #(.width(32), .enable("false")) multiplexer_3 (
    .in0(R1_in), .in1(undriven), .out(multiplexer_3_out), .sel(RST));
  Multiplexer #(.width(32), .enable("false")) multiplexer_4 (
    .in0(R2_in), .in1({32{1'b0}}), .out(multiplexer_4_out), .sel(RST));
  Multiplexer #(.width(32), .enable("false")) multiplexer_5 (
    .in0(Result_in), .in1({32{1'b0}}), .out(multiplexer_5_out), .sel(RST));
  Register #(.width(32)) register_1 (.D(multiplexer_1_out), .en(not_1_out), .Q(PC), .clk(CLK));  // open: clr
  not not_1 (not_1_out, EN);
  Register #(.width(32)) register_2 (.D(multiplexer_2_out), .en(not_2_out), .Q(IR), .clk(CLK));  // open: clr
  not not_2 (not_2_out, EN);
  Register #(.width(32)) register_3 (.D(multiplexer_3_out), .en(not_3_out), .Q(R1), .clk(CLK));  // open: clr
  not not_3 (not_3_out, EN);
  Register #(.width(32)) register_4 (.D(multiplexer_4_out), .en(not_4_out), .Q(R2), .clk(CLK));  // open: clr
  not not_4 (not_4_out, EN);
  Register #(.width(32)) register_5 (.D(multiplexer_5_out), .en(not_5_out), .Q(Result), .clk(CLK));  // open: clr
  not not_5 (not_5_out, EN);
  Multiplexer #(.enable("false")) multiplexer_6 (.in0(Beq_in), .in1(1'b0), .out(multiplexer_6_out), .sel(RST));
  not not_6 (not_6_out, EN);
  Multiplexer #(.enable("false")) multiplexer_7 (.in0(MemWrite_in), .in1(1'b0), .out(multiplexer_7_out), .sel(RST));
  not not_7 (not_7_out, EN);
  Multiplexer #(.enable("false")) multiplexer_8 (.in0(LUI_in), .in1(1'b0), .out(multiplexer_8_out), .sel(RST));
  not not_8 (not_8_out, EN);
  Multiplexer #(.enable("false")) multiplexer_9 (.in0(JMP_in), .in1(1'b0), .out(multiplexer_9_out), .sel(RST));
  not not_9 (not_9_out, EN);
  Multiplexer #(.enable("false")) multiplexer_10 (.in0(RegWrite_in), .in1(1'b0), .out(multiplexer_10_out), .sel(RST));
  not not_10 (not_10_out, EN);
  Multiplexer #(.enable("false")) multiplexer_11 (
    .in0(\传输状态In_表明当前传输数据有效 ), .in1(1'b0), .out(multiplexer_11_out), .sel(RST));
  Register #(.width(1)) register_6 (.D(multiplexer_6_out), .en(not_6_out), .Q(Beq), .clk(CLK));  // open: clr
  Register #(.width(1)) register_7 (.D(multiplexer_7_out), .en(not_7_out), .Q(MemWrite), .clk(CLK));  // open: clr
  Register #(.width(1)) register_8 (.D(multiplexer_8_out), .en(not_8_out), .Q(LUI), .clk(CLK), .clr(RST));
  Register #(.width(1)) register_9 (.D(multiplexer_9_out), .en(not_9_out), .Q(JMP), .clk(CLK));  // open: clr
  Register #(.width(1)) register_10 (.D(multiplexer_10_out), .en(not_10_out), .Q(Regwrite), .clk(CLK));  // open: clr
  Register #(.width(1)) register_11 (
    .D(multiplexer_11_out), .Q(\传输状态Out_表明当前传输数据有效 ), .clk(CLK), .clr(1'b0));  // open: en
  Multiplexer #(.enable("false")) multiplexer_12 (.in0(Bne_in), .in1(1'b0), .out(multiplexer_12_out), .sel(RST));
  not not_11 (not_11_out, EN);
  Multiplexer #(.enable("false")) multiplexer_13 (.in0(Jal_in), .in1(1'b0), .out(multiplexer_13_out), .sel(RST));
  not not_12 (not_12_out, EN);
  Multiplexer #(.enable("false")) multiplexer_14 (.in0(BLTZ_in), .in1(1'b0), .out(multiplexer_14_out), .sel(RST));
  not not_13 (not_13_out, EN);
  Multiplexer #(.enable("false")) multiplexer_15 (.in0(RegDst_in), .in1(1'b0), .out(multiplexer_15_out), .sel(RST));
  not not_14 (not_14_out, EN);
  Register #(.width(1)) register_12 (.D(multiplexer_12_out), .en(not_11_out), .Q(Bne), .clk(CLK));  // open: clr
  Register #(.width(1)) register_13 (.D(multiplexer_13_out), .en(not_12_out), .Q(Jal), .clk(CLK));  // open: clr
  Register #(.width(1)) register_14 (.D(multiplexer_14_out), .en(not_13_out), .Q(BLTZ), .clk(CLK), .clr(RST));
  Register #(.width(1)) register_15 (.D(multiplexer_15_out), .en(not_14_out), .Q(RegDst), .clk(CLK));  // open: clr
  Multiplexer #(.enable("false")) multiplexer_16 (.in0(MemToReg_in), .in1(1'b0), .out(multiplexer_16_out), .sel(RST));
  not not_15 (not_15_out, EN);
  Multiplexer #(.enable("false")) multiplexer_17 (.in0(JR_in), .in1(1'b0), .out(multiplexer_17_out), .sel(RST));
  not not_16 (not_16_out, EN);
  Register #(.width(1)) register_16 (.D(multiplexer_18_out), .en(not_17_out), .Q(HB), .clk(CLK), .clr(RST));
  Multiplexer #(.enable("false")) multiplexer_18 (.in0(HB_in), .in1(1'b0), .out(multiplexer_18_out), .sel(RST));
  not not_17 (not_17_out, EN);
  Register #(.width(1)) register_17 (.D(multiplexer_19_out), .en(not_18_out), .Q(Sllv), .clk(CLK));  // open: clr
  Multiplexer #(.enable("false")) multiplexer_19 (.in0(SLLV_in), .in1(1'b0), .out(multiplexer_19_out), .sel(RST));
  not not_18 (not_18_out, EN);
  Register #(.width(1)) register_18 (.D(multiplexer_16_out), .en(not_15_out), .Q(MemToReg), .clk(CLK));  // open: clr
  Register #(.width(1)) register_19 (.D(multiplexer_17_out), .en(not_16_out), .Q(JR), .clk(CLK));  // open: clr

  // Other names for the same wires on the sheet: MenToReg = MemToReg; MenWrite = MemWrite
endmodule

module MEM_WB (
  input  CLK,
  input  EN,
  input  RST,
  input  Beq_in,
  input  JR_in,
  input  SLLV_in,
  input  [31:0] PC_in,
  input  Bne_in,
  input  Jal_in,
  input  JMP_in,
  input  [31:0] Result_in,
  input  [31:0] R1_in,
  input  MemToReg_in,
  input  LUI_in,
  input  RegDst_in,
  input  RegWrite_in,
  input  BLTZ_in,
  input  HB_in,
  input  [31:0] IR_in,
  input  [31:0] MemData_in,
  input  [31:0] R2_in,
  input  \传输状态In_表明当前传输数据有效 ,
  output Beq,
  output JR,
  output JMP,
  output [31:0] PC,
  output Bne,
  output Jal,
  output RegDst,
  output [31:0] Result,
  output [31:0] R1,
  output Sllv,
  output MemToReg,
  output LUI,
  output HB,
  output BLTZ,
  output Regwrite,
  output [31:0] IR,
  output [31:0] MemData,
  output [31:0] R2,
  output \传输状态Out_表明当前传输数据有效 
);

  wire multiplexer_5_out, multiplexer_6_out, multiplexer_7_out, multiplexer_8_out, multiplexer_9_out,
       multiplexer_10_out, multiplexer_11_out, multiplexer_12_out, multiplexer_13_out, multiplexer_14_out,
       multiplexer_15_out, multiplexer_16_out, multiplexer_17_out, not_1_out, not_2_out, not_3_out,
       not_4_out, not_5_out, not_6_out, not_7_out, not_8_out, not_9_out, not_10_out, not_11_out, not_12_out,
       not_13_out, not_14_out, not_15_out, not_16_out, not_17_out, not_18_out;
  wire [31:0] multiplexer_1_out, multiplexer_2_out, multiplexer_3_out, multiplexer_4_out, multiplexer_18_out,
       multiplexer_19_out;

  Multiplexer #(.width(32), .enable("false")) multiplexer_1 (
    .in0(PC_in), .in1({32{1'b0}}), .out(multiplexer_1_out), .sel(RST));
  Multiplexer #(.width(32), .enable("false")) multiplexer_2 (
    .in0(IR_in), .in1({32{1'b0}}), .out(multiplexer_2_out), .sel(RST));
  Multiplexer #(.width(32), .enable("false")) multiplexer_3 (
    .in0(Result_in), .in1({32{1'b0}}), .out(multiplexer_3_out), .sel(RST));
  Multiplexer #(.width(32), .enable("false")) multiplexer_4 (
    .in0(MemData_in), .in1({32{1'b0}}), .out(multiplexer_4_out), .sel(RST));
  Register #(.width(32)) register_1 (.D(multiplexer_1_out), .en(not_1_out), .Q(PC), .clk(CLK));  // open: clr
  not not_1 (not_1_out, EN);
  Register #(.width(32)) register_2 (.D(multiplexer_2_out), .en(not_2_out), .Q(IR), .clk(CLK));  // open: clr
  not not_2 (not_2_out, EN);
  Register #(.width(32)) register_3 (.D(multiplexer_3_out), .en(not_3_out), .Q(Result), .clk(CLK));  // open: clr
  not not_3 (not_3_out, EN);
  Register #(.width(32)) register_4 (.D(multiplexer_4_out), .en(not_4_out), .Q(MemData), .clk(CLK));  // open: clr
  not not_4 (not_4_out, EN);
  Multiplexer #(.enable("false")) multiplexer_5 (.in0(Beq_in), .in1(1'b0), .out(multiplexer_5_out), .sel(RST));
  not not_5 (not_5_out, EN);
  Multiplexer #(.enable("false")) multiplexer_6 (.in0(RegWrite_in), .in1(1'b0), .out(multiplexer_6_out), .sel(RST));
  not not_6 (not_6_out, EN);
  Multiplexer #(.enable("false")) multiplexer_7 (.in0(LUI_in), .in1(1'b0), .out(multiplexer_7_out), .sel(RST));
  not not_7 (not_7_out, EN);
  Multiplexer #(.enable("false")) multiplexer_8 (.in0(JMP_in), .in1(1'b0), .out(multiplexer_8_out), .sel(RST));
  not not_8 (not_8_out, EN);
  Multiplexer #(.enable("false")) multiplexer_9 (
    .in0(\传输状态In_表明当前传输数据有效 ), .in1(1'b0), .out(multiplexer_9_out), .sel(RST));
  Register #(.width(1)) register_5 (.D(multiplexer_5_out), .en(not_5_out), .Q(Beq), .clk(CLK));  // open: clr
  Register #(.width(1)) register_6 (.D(multiplexer_6_out), .en(not_6_out), .Q(Regwrite), .clk(CLK));  // open: clr
  Register #(.width(1)) register_7 (.D(multiplexer_7_out), .en(not_7_out), .Q(LUI), .clk(CLK));  // open: clr
  Register #(.width(1)) register_8 (.D(multiplexer_8_out), .en(not_8_out), .Q(JMP), .clk(CLK));  // open: clr
  Register #(.width(1)) register_9 (
    .D(multiplexer_9_out), .Q(\传输状态Out_表明当前传输数据有效 ), .clk(CLK), .clr(1'b0));  // open: en
  Multiplexer #(.enable("false")) multiplexer_10 (.in0(Bne_in), .in1(1'b0), .out(multiplexer_10_out), .sel(RST));
  not not_9 (not_9_out, EN);
  Multiplexer #(.enable("false")) multiplexer_11 (.in0(Jal_in), .in1(1'b0), .out(multiplexer_11_out), .sel(RST));
  not not_10 (not_10_out, EN);
  Multiplexer #(.enable("false")) multiplexer_12 (.in0(BLTZ_in), .in1(1'b0), .out(multiplexer_12_out), .sel(RST));
  not not_11 (not_11_out, EN);
  Multiplexer #(.enable("false")) multiplexer_13 (.in0(RegDst_in), .in1(1'b0), .out(multiplexer_13_out), .sel(RST));
  not not_12 (not_12_out, EN);
  Register #(.width(1)) register_10 (.D(multiplexer_10_out), .en(not_9_out), .Q(Bne), .clk(CLK));  // open: clr
  Register #(.width(1)) register_11 (.D(multiplexer_11_out), .en(not_10_out), .Q(Jal), .clk(CLK));  // open: clr
  Register #(.width(1)) register_12 (.D(multiplexer_12_out), .en(not_11_out), .Q(BLTZ), .clk(CLK));  // open: clr
  Register #(.width(1)) register_13 (.D(multiplexer_13_out), .en(not_12_out), .Q(RegDst), .clk(CLK));  // open: clr
  Multiplexer #(.enable("false")) multiplexer_14 (.in0(MemToReg_in), .in1(1'b0), .out(multiplexer_14_out), .sel(RST));
  not not_13 (not_13_out, EN);
  Multiplexer #(.enable("false")) multiplexer_15 (.in0(JR_in), .in1(1'b0), .out(multiplexer_15_out), .sel(RST));
  not not_14 (not_14_out, EN);
  Multiplexer #(.enable("false")) multiplexer_16 (.in0(HB_in), .in1(1'b0), .out(multiplexer_16_out), .sel(RST));
  not not_15 (not_15_out, EN);
  Multiplexer #(.enable("false")) multiplexer_17 (.in0(SLLV_in), .in1(1'b0), .out(multiplexer_17_out), .sel(RST));
  not not_16 (not_16_out, EN);
  Register #(.width(1)) register_14 (.D(multiplexer_14_out), .en(not_13_out), .Q(MemToReg), .clk(CLK));  // open: clr
  Register #(.width(1)) register_15 (.D(multiplexer_15_out), .en(not_14_out), .Q(JR), .clk(CLK));  // open: clr
  Register #(.width(1)) register_16 (.D(multiplexer_16_out), .en(not_15_out), .Q(HB), .clk(CLK));  // open: clr
  Register #(.width(1)) register_17 (.D(multiplexer_17_out), .en(not_16_out), .Q(Sllv), .clk(CLK));  // open: clr
  Multiplexer #(.width(32), .enable("false")) multiplexer_18 (
    .in0(R1_in), .in1({32{1'b0}}), .out(multiplexer_18_out), .sel(RST));
  Multiplexer #(.width(32), .enable("false")) multiplexer_19 (
    .in0(R2_in), .in1({32{1'b0}}), .out(multiplexer_19_out), .sel(RST));
  Register #(.width(32)) register_18 (.D(multiplexer_18_out), .en(not_17_out), .Q(R1), .clk(CLK));  // open: clr
  not not_17 (not_17_out, EN);
  Register #(.width(32)) register_19 (.D(multiplexer_19_out), .en(not_18_out), .Q(R2), .clk(CLK));  // open: clr
  not not_18 (not_18_out, EN);

  // Other names for the same wires on the sheet: MenToReg = MemToReg
endmodule

module \分支相关流水线  (
);

  wire and_1_out, and_2_out, and_3_out, and_4_out, and_5_out, Beq, BLTZ, BLTZ_in, Bne, CLK, comparator_1_eq,
       comparator_2_eq, equal, ex_mem_1_jal, ex_mem_1_memtoreg, ex_mem_1_regdst, ex_mem_1_regwrite,
       \ex_mem_1_传输状态out_表明当前传输数据有效 , Go, HB, HB_in, id_ex_1_alusrcb, id_ex_1_memtoreg, id_ex_1_memwrite,
       id_ex_1_regdst, id_ex_1_regwrite, \id_ex_1_传输状态out_表明当前传输数据有效 , \if_id_1_传输状态out_表明当前传输数据有效 , IR1,
       IR2, IR3, Jal, JMP, JMP_in, JR, JR_in, LUI, LUI_in, mem_wb_1_jal, mem_wb_1_memtoreg, mem_wb_1_regdst,
       MemWrite, nand_1_out, not_1_out, not_2_out, not_3_out, not_4_out, not_5_out, or_2_out, or_6_out,
       or_7_out, out, RegWrite, RST, SignedExt, SignedExt_in, SLLV, SLLV_in, Syscall, W1, W2, W3, \显示 ,
       \有条件跳转 , \硬布线控制器_1_alu_src , \硬布线控制器_1_beq , \硬布线控制器_1_bne , \硬布线控制器_1_jal , \硬布线控制器_1_memtoreg ,
       \硬布线控制器_1_memwrite , \硬布线控制器_1_regdst , \硬布线控制器_1_regwrite , \结束 , \跳转 ;
  wire [1:0] PCsrc;
  wire [3:0] id_ex_1_aluop, \硬布线控制器_1_alu_op ;
  wire [4:0] multiplexer_3_out, multiplexer_4_out, multiplexer_6_out, W_num;
  wire [15:0] \LoadUse次数 , \总周期数 , \插入气泡数 , \无条件分支数 , \条件分支成功数 ;
  wire [31:0] adder_4_out, bit_extender_1_out, bit_extender_2_out, Din, EX_IR, ex_mem_1_ir, ex_mem_1_r2,
       ex_mem_1_result, EX_PC, GPR2, id_ex_1_r2, ID_PC, if_id_1_ir, IF_PC, LedData, MEM_PC, mem_wb_1_ir,
       mem_wb_1_memdata, mem_wb_1_result, multiplexer_1_out, multiplexer_5_out, multiplexer_7_out, PC, PC0,
       PC2, PC3, R1, ram_1_data, Result, rom_1_data, shifter_1_out, WB_PC, \立即数扩展 ;

  Button \u_总复位  (.out(RST));
  Button _1 (.out(IR1));
  Button _2 (.out(IR2));
  Button _3 (.out(IR3));
  Button \u_继续运行  (.out(Go));
  LED led_1 (.in(W1));
  LED led_2 (.in(W2));
  LED led_3 (.in(W3));
  nand nand_1 (nand_1_out, Syscall, ~out);  // NAND_Gate
  Hex_Digit_Display hex_digit_display_1 (.value(LedData[31:28]));  // open: dp
  Counter #(.width(16), .max('hffff)) counter_1 (
    .count(nand_1_out), .Q(\总周期数 ), .clk(CLK), .clr(RST));  // open: load, D, carry
  Hex_Digit_Display hex_digit_display_2 (.value(LedData[23:20]));  // open: dp
  Hex_Digit_Display hex_digit_display_3 (.value(LedData[27:24]));  // open: dp
  Multiplexer #(.select(2), .width(32), .enable("false")) multiplexer_1 (
    .in0(PC0), .in1({PC[31:28], EX_IR[25:0], 2'b00}), .in2(PC2), .in3(PC3), .out(multiplexer_1_out),
    .sel(PCsrc));
  not not_1 (not_1_out, \结束 );
  Adder #(.width(32)) adder_1 (.a(IF_PC), .b(32'h4), .out(PC0));  // open: cin, cout
  Adder #(.width(32)) adder_2 (.a(EX_PC), .b(32'h4), .out(PC));  // open: cin, cout
  // Probe on {PC[31:28], EX_IR[25:0], 2'b00}
  Shifter #(.width(32)) shifter_1 (.in(\立即数扩展 ), .\dist (5'b00010), .out(shifter_1_out));
  and and_1 (and_1_out, equal, Beq);
  and and_2 (and_2_out, Bne, ~equal);  // AND_Gate
  and and_3 (and_3_out, BLTZ, Result[0]);
  Hex_Digit_Display hex_digit_display_4 (.value(LedData[15:12]));  // open: dp
  Hex_Digit_Display hex_digit_display_5 (.value(LedData[19:16]));  // open: dp
  Counter #(.width(16), .max('hffff)) counter_2 (
    .count(JMP), .Q(\无条件分支数 ), .clk(CLK), .clr(RST));  // open: load, D, carry
  assign bit_extender_1_out = {{16{1'b0}}, EX_IR[15:0]};  // Bit_Extender bit_extender_1
  assign bit_extender_2_out = {{16{EX_IR[15]}}, EX_IR[15:0]};  // Bit_Extender bit_extender_2
  Register #(.width(32)) u_PC (.D(multiplexer_1_out), .en(not_1_out), .Q(IF_PC), .clk(CLK), .clr(RST));
  Adder #(.width(32)) adder_3 (.a(shifter_1_out), .b(PC), .out(PC3));  // open: cin, cout
  or or_1 (\有条件跳转 , and_1_out, and_2_out, and_3_out);
  Hex_Digit_Display hex_digit_display_6 (.value(LedData[7:4]));  // open: dp
  Hex_Digit_Display hex_digit_display_7 (.value(LedData[11:8]));  // open: dp
  Clock clock_1 (.out(CLK));
  Multiplexer #(.width(32), .enable("false")) multiplexer_2 (
    .in0(bit_extender_1_out), .in1(bit_extender_2_out), .out(\立即数扩展 ), .sel(SignedExt));
  Hex_Digit_Display hex_digit_display_8 (.value(LedData[3:0]));  // open: dp
  Counter #(.width(16), .max('hffff)) counter_3 (
    .count(\有条件跳转 ), .Q(\条件分支成功数 ), .clk(CLK), .clr(RST));  // open: load, D, carry
  ROM #(.addrWidth(10), .dataWidth(32)) rom_1 (.addr(IF_PC[11:2]), .data(rom_1_data), .sel(1'b1));
  // Probe on rom_1_data
  and and_4 (and_4_out, \结束 , ~RST);  // AND_Gate
  // Probe on \总周期数 
  // Probe on \无条件分支数 
  // Probe on \条件分支成功数 
  // Probe on \插入气泡数 
  // Probe on \LoadUse次数 
  or or_2 (or_2_out, RST, \跳转 );
  IF_ID if_id_1 (
    .CLK(CLK), .EN(and_4_out), .RST(or_2_out), .PC_in(IF_PC), .PC(ID_PC), .IR_in(rom_1_data),
    .IR(if_id_1_ir), .\传输状态In_表明当前传输数据有效 (not_2_out), .\传输状态Out_表明当前传输数据有效 (\if_id_1_传输状态out_表明当前传输数据有效 ),
    .\数据有效 (\跳转 ));  // open: 预测位_in, 预测位
  not not_2 (not_2_out, and_4_out);
  not not_3 (not_3_out, JR);
  or or_3 (PCsrc[1], JR, \有条件跳转 );
  or or_4 (\跳转 , JR, JMP, \有条件跳转 );
  // Probe on IF_PC[11:2]
  and and_5 (and_5_out, JMP, not_3_out);
  // Probe on ID_PC[11:2]
  // Probe on PCsrc
  or or_5 (PCsrc[0], and_5_out, \有条件跳转 );
  // Probe on MEM_PC[11:2]
  // Probe on EX_PC[11:2]
  \硬布线控制器  \u_硬布线控制器_1  (
    .Func(if_id_1_ir[5:0]), .OP(if_id_1_ir[31:26]), .ALU_OP(\硬布线控制器_1_alu_op ),
    .MemToReg(\硬布线控制器_1_memtoreg ), .MemWrite(\硬布线控制器_1_memwrite ), .ALU_SRC(\硬布线控制器_1_alu_src ),
    .RegWrite(\硬布线控制器_1_regwrite ), .SysCALL(Syscall), .SignedExt(SignedExt_in), .RegDst(\硬布线控制器_1_regdst ),
    .JR(JR_in), .JMP(JMP_in), .Beq(\硬布线控制器_1_beq ), .JAL(\硬布线控制器_1_jal ), .Bne(\硬布线控制器_1_bne ), .LUI(LUI_in),
    .BTLZ(BLTZ_in), .HB(HB_in), .SLLV(SLLV_in));
  Multiplexer #(.width(5), .enable("false")) multiplexer_3 (
    .in0(if_id_1_ir[25:21]), .in1(5'b00010), .out(multiplexer_3_out), .sel(Syscall));
  Multiplexer #(.width(5), .enable("false")) multiplexer_4 (
    .in0(if_id_1_ir[20:16]), .in1(5'b00100), .out(multiplexer_4_out), .sel(Syscall));
  // Probe on WB_PC[11:2]
  MIPS_Regifile mips_regifile_1 (
    .Din(Din), .Clk(CLK), .R1(R1), .R2(GPR2), .WE(RegWrite), .W_num(W_num), .R1_num(multiplexer_3_out),
    .R2_num(multiplexer_4_out));
  Comparator #(.width(32)) comparator_1 (.a(R1), .b(32'ha), .eq(comparator_1_eq));  // open: gt, lt
  Register #(.width(32)) register_1 (.D(GPR2), .en(\显示 ), .Q(LedData), .clk(CLK), .clr(RST));
  or or_6 (or_6_out, RST, \跳转 );
  ID_EX id_ex_1 (
    .CLK(CLK), .PC_in(ID_PC), .EN(or_7_out), .IR_in(if_id_1_ir), .JMP(JMP), .JR(JR), .SignedExt(SignedExt),
    .LUI(LUI), .BLTZ(BLTZ), .HB(HB), .Sllv(SLLV), .Beq(Beq), .Bne(Bne), .MemToReg(id_ex_1_memtoreg),
    .MemWrite(id_ex_1_memwrite), .AluOP(id_ex_1_aluop), .AluSrcB(id_ex_1_alusrcb), .Jal(Jal),
    .RegDst(id_ex_1_regdst), .RST(or_6_out), .Beq_in(\硬布线控制器_1_beq ), .MemToReg_in(\硬布线控制器_1_memtoreg ),
    .Bne_in(\硬布线控制器_1_bne ), .MemWrite_in(\硬布线控制器_1_memwrite ), .AluOP_in(\硬布线控制器_1_alu_op ),
    .AluSrcB_in(\硬布线控制器_1_alu_src ), .JR_in(JR_in), .Jal_in(\硬布线控制器_1_jal ), .SignedExt_in(SignedExt_in),
    .LUI_in(LUI_in), .BLTZ_in(BLTZ_in), .HB_in(HB_in), .SLLV_in(SLLV_in), .JMP_in(JMP_in),
    .RegDst_in(\硬布线控制器_1_regdst ), .PC(EX_PC), .IR(EX_IR),
    .\传输状态In_表明当前传输数据有效 (\if_id_1_传输状态out_表明当前传输数据有效 ), .\传输状态Out_表明当前传输数据有效 (\id_ex_1_传输状态out_表明当前传输数据有效 ),
    .R1_in(R1), .R2_in(GPR2), .R1(PC2), .R2(id_ex_1_r2), .RegWrite_in(\硬布线控制器_1_regwrite ),
    .Regwrite(id_ex_1_regwrite), .\跳转 (\跳转 ));  // open: ForwardA_in, ForwardA, ForwardB_in, ForwardB, 预测位_in, 预测位
  or or_7 (or_7_out, ~\if_id_1_传输状态out_表明当前传输数据有效 , \结束 );  // OR_Gate
  and and_6 (\结束 , comparator_1_eq, Syscall);
  and and_7 (\显示 , Syscall, comparator_2_eq);
  Comparator #(.width(32)) comparator_2 (.a(R1), .b(32'h22), .eq(comparator_2_eq));  // open: gt, lt
  // Probe on EX_IR
  Multiplexer #(.width(32), .enable("false")) multiplexer_5 (
    .in0(id_ex_1_r2), .in1(\立即数扩展 ), .out(multiplexer_5_out), .sel(id_ex_1_alusrcb));
  MIPS_ALU mips_alu_1 (
    .X(PC2), .Y(multiplexer_5_out), .AluOP(id_ex_1_aluop), .Equal(equal), .Result(Result), .shamt(EX_IR[10:6]));  // open: Result_2
  not not_4 (not_4_out, \id_ex_1_传输状态out_表明当前传输数据有效 );
  EX_MEM ex_mem_1 (
    .CLK(CLK), .EN(not_4_out), .RST(RST), .PC_in(EX_PC), .Jal_in(Jal), .Result_in(Result),
    .MemToReg_in(id_ex_1_memtoreg), .RegDst_in(id_ex_1_regdst), .MemWrite_in(id_ex_1_memwrite),
    .IR_in(EX_IR), .R2_in(id_ex_1_r2), .PC(MEM_PC), .Result(ex_mem_1_result), .IR(ex_mem_1_ir),
    .R2(ex_mem_1_r2), .\传输状态In_表明当前传输数据有效 (\id_ex_1_传输状态out_表明当前传输数据有效 ), .Jal(ex_mem_1_jal),
    .RegDst(ex_mem_1_regdst), .MemToReg(ex_mem_1_memtoreg), .MemWrite(MemWrite),
    .\传输状态Out_表明当前传输数据有效 (\ex_mem_1_传输状态out_表明当前传输数据有效 ), .RegWrite_in(id_ex_1_regwrite),
    .Regwrite(ex_mem_1_regwrite));  // open: Beq_in, JR_in, SLLV_in, Bne_in, JMP_in, LUI_in, BLTZ_in, HB_in, Beq, JR, JMP, Bne, Sllv, LUI, HB, BLTZ, R1_in, R1
  MEM_WB mem_wb_1 (
    .CLK(CLK), .EN(not_5_out), .RST(RST), .PC_in(MEM_PC), .Jal_in(ex_mem_1_jal), .Result_in(ex_mem_1_result),
    .MemToReg_in(ex_mem_1_memtoreg), .RegDst_in(ex_mem_1_regdst), .RegWrite_in(ex_mem_1_regwrite),
    .IR_in(ex_mem_1_ir), .MemData_in(ram_1_data), .PC(WB_PC), .Result(mem_wb_1_result), .IR(mem_wb_1_ir),
    .MemData(mem_wb_1_memdata), .\传输状态In_表明当前传输数据有效 (\ex_mem_1_传输状态out_表明当前传输数据有效 ), .Jal(mem_wb_1_jal),
    .RegDst(mem_wb_1_regdst), .MemToReg(mem_wb_1_memtoreg), .Regwrite(RegWrite), .\传输状态Out_表明当前传输数据有效 (out));  // open: Beq_in, JR_in, SLLV_in, Bne_in, JMP_in, LUI_in, BLTZ_in, HB_in, Beq, JR, JMP, Bne, Sllv, LUI, HB, BLTZ, R1_in, R2_in, R1, R2
  RAM #(.addrWidth(10), .dataWidth(32), .bus("separate")) ram_1 (
    .addr(ex_mem_1_result[11:2]), .din(ex_mem_1_r2), .data(ram_1_data), .str(MemWrite), .sel(1'b1),
    .clk(CLK), .ld(1'b1), .clr(RST));
  not not_5 (not_5_out, \ex_mem_1_传输状态out_表明当前传输数据有效 );
  Multiplexer #(.width(5), .enable("false")) multiplexer_6 (
    .in0(mem_wb_1_ir[20:16]), .in1(mem_wb_1_ir[15:11]), .out(multiplexer_6_out), .sel(mem_wb_1_regdst));
  Multiplexer #(.width(32), .enable("false")) multiplexer_7 (
    .in0(mem_wb_1_result), .in1(mem_wb_1_memdata), .out(multiplexer_7_out), .sel(mem_wb_1_memtoreg));
  Adder #(.width(32)) adder_4 (.a(WB_PC), .b(32'h4), .out(adder_4_out));  // open: cin, cout
  Multiplexer #(.width(5), .enable("false")) multiplexer_8 (
    .in0(multiplexer_6_out), .in1({5{1'b1}}), .out(W_num), .sel(mem_wb_1_jal));
  Multiplexer #(.width(32), .enable("false")) multiplexer_9 (
    .in0(multiplexer_7_out), .in1(adder_4_out), .out(Din), .sel(mem_wb_1_jal));

  // Other names for the same wires on the sheet: instr_index[25:0] = EX_IR[25:0];
  //   PC1[31:2] = {PC[31:28], EX_IR[25:0]}; 立即数[15:0] = EX_IR[15:0]; shamt[4:0] = EX_IR[10:6]; PC高4位[3:0] = PC[31:28]

  // Notes on the sheet:
  //   中断源
  //   中断等待指示
  //   数码管输出
  //   指令字
  //   contents of rom_1 (hex, n*v repeats v):
  //   20110020 20020022 8000c06 20110000 20110000 2002000a 10000003 20110000 20110000 2002000a 14110003
  //   20110000 20110000 2002000a c000c14 2002000a 0 0 0 c 2231ffff 0 0 0 112020 0 0 0 c 1620fff6 3e00008
  //   Func
  //   rs
  //   rt
  //   OP
  //   Func
  //   流水调试日志用
  //   shamt
  //   rt
  //   rd
endmodule
module \气泡流水线  (
);

  wire and_1_out, and_2_out, and_3_out, and_4_out, and_5_out, and_6_out, and_7_out, and_8_out, and_9_out,
       and_10_out, and_15_out, and_16_out, Beq, BLTZ, BLTZ_in, Bne, CLK, comparator_1_eq, comparator_2_eq,
       d_ff_1_q, en, equal, EX_Jal, ex_mem_1_bltz, ex_mem_1_hb, ex_mem_1_lui, ex_mem_1_memtoreg,
       ex_mem_1_memwrite, ex_mem_1_sllv, \ex_mem_1_传输状态out_表明当前传输数据有效 , EX_RegDst, EX_RegWrite, Go, HB,
       HB_in, id_ex_1_alusrcb, id_ex_1_hb, id_ex_1_lui, id_ex_1_memtoreg, id_ex_1_memwrite, id_ex_1_sllv,
       \id_ex_1_传输状态out_表明当前传输数据有效 , \if_id_1_传输状态out_表明当前传输数据有效 , IR1, IR2, IR3, JMP, JMP_in, JR, JR_in,
       LUI, LUI_in, MEM_Jal, MEM_RegDst, MEM_RegWrite, MemToReg, nand_1_out, nor_1_out, not_1_out, not_2_out,
       or_2_out, or_4_out, or_5_out, or_10_out, out, pause, \PC使能 , RegWrite, RST, SignedExt, SignedExt_in,
       SLLV, SLLV_in, Syscall, W1, W2, W3, WB_Jal, WB_RegDst, \数据相关 , \显示 , \暂停 , \有条件跳转 , \气泡 ,
       \硬布线控制器_1_alu_src , \硬布线控制器_1_beq , \硬布线控制器_1_bne , \硬布线控制器_1_jal , \硬布线控制器_1_memtoreg ,
       \硬布线控制器_1_memwrite , \硬布线控制器_1_regdst , \硬布线控制器_1_regwrite , \结束 , \继续运行 , \跳转 ;
  wire [1:0] PCsrc;
  wire [3:0] id_ex_1_aluop, \硬布线控制器_1_alu_op ;
  wire [4:0] EX_W_num, ID_R1, ID_R2, MEM_W_num, WB_W_num;
  wire [5:0] Func, OP;
  wire [15:0] \LoadUse次数 , WB_imm, \总周期数 , \插入气泡数 , \无条件分支数 , \条件分支成功数 ;
  wire [25:6] if_id_1_ir;
  wire [31:0] bit_extender_1_out, bit_extender_2_out, Din, EX_IR, ex_mem_1_r1, ex_mem_1_r2, ex_mem_1_result,
       EX_PC, id_ex_1_r2, ID_PC, IF_PC, LedData, MEM_IR, MEM_PC, MemData, multiplexer_1_out,
       multiplexer_4_out, PC, PC0, PC2, PC3, R1, R2, ram_1_data, Result, rom_1_data, shifter_1_out, WB_PC,
       WB_R1, WB_R2, WB_Result, \立即数扩展 ;
  wire [31:16] WB_IR;

  Button \u_总复位  (.out(RST));
  Button _1 (.out(IR1));
  Button _2 (.out(IR2));
  Button _3 (.out(IR3));
  Button \u_继续运行  (.out(Go));
  LED led_1 (.in(W1));
  LED led_2 (.in(W2));
  LED led_3 (.in(W3));
  nand nand_1 (nand_1_out, Syscall, ~out);  // NAND_Gate
  Hex_Digit_Display hex_digit_display_1 (.value(LedData[31:28]));  // open: dp
  Counter #(.width(16), .max('hffff)) counter_1 (
    .count(nand_1_out), .Q(\总周期数 ), .clk(CLK), .clr(RST));  // open: load, D, carry
  and and_1 (and_1_out, Go, ~\结束 );  // AND_Gate
  Hex_Digit_Display hex_digit_display_2 (.value(LedData[23:20]));  // open: dp
  Hex_Digit_Display hex_digit_display_3 (.value(LedData[27:24]));  // open: dp
  // Probe on PCsrc
  Multiplexer #(.select(2), .width(32), .enable("false")) multiplexer_1 (
    .in0(PC0), .in1({PC[31:28], EX_IR[25:0], 2'b00}), .in2(PC2), .in3(PC3), .out(multiplexer_1_out),
    .sel(PCsrc));
  Adder #(.width(32)) adder_1 (.a(IF_PC), .b(32'h4), .out(PC0));  // open: cin, cout
  Adder #(.width(32)) adder_2 (.a(EX_PC), .b(32'h4), .out(PC));  // open: cin, cout
  Shifter #(.width(32)) shifter_1 (.in(\立即数扩展 ), .\dist (5'b00010), .out(shifter_1_out));
  and and_2 (and_2_out, equal, Beq);
  and and_3 (and_3_out, Bne, ~equal);  // AND_Gate
  and and_4 (and_4_out, BLTZ, Result[0]);
  D_Flip_Flop d_ff_1 (.clk(CLK), .D(and_1_out), .Q(d_ff_1_q), .en(1'b1), .reset(RST));  // open: Qn, preset
  Hex_Digit_Display hex_digit_display_4 (.value(LedData[15:12]));  // open: dp
  Hex_Digit_Display hex_digit_display_5 (.value(LedData[19:16]));  // open: dp
  Counter #(.width(16), .max('hffff)) counter_2 (
    .count(JMP), .Q(\无条件分支数 ), .clk(CLK), .clr(RST));  // open: load, D, carry
  Register #(.width(32)) u_PC (.D(multiplexer_1_out), .en(\PC使能 ), .Q(IF_PC), .clk(CLK), .clr(RST));
  Adder #(.width(32)) adder_3 (.a(shifter_1_out), .b(PC), .out(PC3));  // open: cin, cout
  or or_1 (\有条件跳转 , and_2_out, and_3_out, and_4_out);
  and and_5 (and_5_out, \暂停 , d_ff_1_q);
  or or_2 (or_2_out, and_6_out, nor_1_out);
  nor nor_1 (nor_1_out, pause, \数据相关 );
  and and_6 (and_6_out, ~pause, \跳转 );  // AND_Gate
  Hex_Digit_Display hex_digit_display_6 (.value(LedData[11:8]));  // open: dp
  Hex_Digit_Display hex_digit_display_7 (.value(LedData[7:4]));  // open: dp
  Clock clock_1 (.out(CLK));
  or or_3 (\PC使能 , and_5_out, or_2_out);
  Hex_Digit_Display hex_digit_display_8 (.value(LedData[3:0]));  // open: dp
  Counter #(.width(16), .max('hffff)) counter_3 (
    .count(\有条件跳转 ), .Q(\条件分支成功数 ), .clk(CLK), .clr(RST));  // open: load, D, carry
  Counter #(.width(16), .max('hffff)) counter_4 (
    .count(\数据相关 ), .Q(\插入气泡数 ), .clk(CLK), .clr(RST));  // open: load, D, carry
  and and_7 (and_7_out, en, ~RST);  // AND_Gate
  ROM #(.addrWidth(10), .dataWidth(32)) rom_1 (.addr(IF_PC[11:2]), .data(rom_1_data), .sel(1'b1));
  // Probe on rom_1_data
  or or_4 (or_4_out, and_7_out, \数据相关 );
  // Probe on \总周期数 
  // Probe on \无条件分支数 
  // Probe on \条件分支成功数 
  // Probe on \插入气泡数 
  // Probe on \LoadUse次数 
  or or_5 (or_5_out, RST, \跳转 );
  IF_ID if_id_1 (
    .CLK(CLK), .EN(and_8_out), .RST(or_5_out), .PC_in(IF_PC), .PC(ID_PC), .IR_in(rom_1_data),
    .IR({OP, if_id_1_ir, Func}), .\传输状态In_表明当前传输数据有效 (not_1_out),
    .\传输状态Out_表明当前传输数据有效 (\if_id_1_传输状态out_表明当前传输数据有效 ), .\数据有效 (\气泡 ));  // open: 预测位_in, 预测位
  not not_1 (not_1_out, and_7_out);
  and and_8 (and_8_out, or_4_out, ~\跳转 );  // AND_Gate
  not not_2 (not_2_out, JR);
  or or_6 (PCsrc[1], JR, \有条件跳转 );
  or or_7 (\跳转 , JR, JMP, \有条件跳转 );
  // Probe on IF_PC[11:0]
  and and_9 (and_9_out, JMP, not_2_out);
  // Probe on ID_PC[11:0]
  or or_8 (\气泡 , \跳转 , pause, \数据相关 );
  or or_9 (PCsrc[0], and_9_out, \有条件跳转 );
  // Probe on EX_PC[11:0]
  // Probe on MEM_PC[11:0]
  \硬布线控制器  \u_硬布线控制器_1  (
    .Func(Func), .OP(OP), .ALU_OP(\硬布线控制器_1_alu_op ), .MemToReg(\硬布线控制器_1_memtoreg ),
    .MemWrite(\硬布线控制器_1_memwrite ), .ALU_SRC(\硬布线控制器_1_alu_src ), .RegWrite(\硬布线控制器_1_regwrite ),
    .SysCALL(Syscall), .SignedExt(SignedExt_in), .RegDst(\硬布线控制器_1_regdst ), .JR(JR_in), .JMP(JMP_in),
    .Beq(\硬布线控制器_1_beq ), .JAL(\硬布线控制器_1_jal ), .Bne(\硬布线控制器_1_bne ), .LUI(LUI_in), .BTLZ(BLTZ_in),
    .HB(HB_in), .SLLV(SLLV_in));
  Multiplexer #(.width(5), .enable("false")) multiplexer_2 (
    .in0(if_id_1_ir[25:21]), .in1(5'b00010), .out(ID_R1), .sel(Syscall));
  Multiplexer #(.width(5), .enable("false")) multiplexer_3 (
    .in0(if_id_1_ir[20:16]), .in1(5'b00100), .out(ID_R2), .sel(Syscall));
  // Probe on WB_PC[11:0]
  MIPS_Regifile mips_regifile_1 (
    .Din(Din), .Clk(CLK), .R1(R1), .R2(R2), .WE(RegWrite), .W_num(WB_W_num), .R1_num(ID_R1), .R2_num(ID_R2));
  and and_10 (and_10_out, ~\if_id_1_传输状态out_表明当前传输数据有效 , ~en);  // AND_Gate
  Comparator #(.width(32)) comparator_1 (.a(R1), .b(32'ha), .eq(comparator_1_eq));  // open: gt, lt
  Register #(.width(32)) register_1 (.D(R2), .en(\显示 ), .Q(LedData), .clk(CLK), .clr(RST));
  or or_10 (or_10_out, \继续运行 , RST, \数据相关 , \跳转 , \结束 );
  ID_EX id_ex_1 (
    .CLK(CLK), .PC_in(ID_PC), .EN(and_10_out), .IR_in({OP, if_id_1_ir, Func}), .JMP(JMP), .JR(JR),
    .SignedExt(SignedExt), .LUI(id_ex_1_lui), .BLTZ(BLTZ), .HB(id_ex_1_hb), .Sllv(id_ex_1_sllv), .Beq(Beq),
    .Bne(Bne), .MemToReg(id_ex_1_memtoreg), .MemWrite(id_ex_1_memwrite), .AluOP(id_ex_1_aluop),
    .AluSrcB(id_ex_1_alusrcb), .Jal(EX_Jal), .RegDst(EX_RegDst), .RST(or_10_out), .Beq_in(\硬布线控制器_1_beq ),
    .MemToReg_in(\硬布线控制器_1_memtoreg ), .Bne_in(\硬布线控制器_1_bne ), .MemWrite_in(\硬布线控制器_1_memwrite ),
    .AluOP_in(\硬布线控制器_1_alu_op ), .AluSrcB_in(\硬布线控制器_1_alu_src ), .JR_in(JR_in), .Jal_in(\硬布线控制器_1_jal ),
    .SignedExt_in(SignedExt_in), .LUI_in(LUI_in), .BLTZ_in(BLTZ_in), .HB_in(HB_in), .SLLV_in(SLLV_in),
    .JMP_in(JMP_in), .RegDst_in(\硬布线控制器_1_regdst ), .PC(EX_PC), .IR(EX_IR),
    .\传输状态In_表明当前传输数据有效 (\if_id_1_传输状态out_表明当前传输数据有效 ), .\传输状态Out_表明当前传输数据有效 (\id_ex_1_传输状态out_表明当前传输数据有效 ),
    .R1_in(R1), .R2_in(R2), .R1(PC2), .R2(id_ex_1_r2), .RegWrite_in(\硬布线控制器_1_regwrite ),
    .Regwrite(EX_RegWrite), .\跳转 (\气泡 ));  // open: ForwardA_in, ForwardA, ForwardB_in, ForwardB, 预测位_in, 预测位
  and and_11 (\结束 , comparator_1_eq, Syscall);
  and and_12 (\显示 , Syscall, comparator_2_eq);
  Comparator #(.width(32)) comparator_2 (.a(R1), .b(32'h22), .eq(comparator_2_eq));  // open: gt, lt
  and and_13 (\暂停 , ~\显示 , ~\结束 , Syscall, ~\数据相关 );  // AND_Gate
  \数据相关检测  \u_数据相关检测_1  (
    .OP(OP), .EX_WriteReg_num(EX_W_num), .EX_RegWrite(EX_RegWrite), .MEM_WriteReg_num(MEM_W_num),
    .MEM_RegWrite(MEM_RegWrite), .\数据相关 (\数据相关 ), .Func(Func), .ID_R1_num(ID_R1), .ID_R2_num(ID_R2));
  Multiplexer #(.width(32), .enable("false")) multiplexer_4 (
    .in0(id_ex_1_r2), .in1(\立即数扩展 ), .out(multiplexer_4_out), .sel(id_ex_1_alusrcb));
  or or_11 (pause, \结束 , \暂停 );
  and and_14 (\继续运行 , \暂停 , ~Go);  // AND_Gate
  MIPS_ALU mips_alu_1 (
    .X(PC2), .Y(multiplexer_4_out), .AluOP(id_ex_1_aluop), .Equal(equal), .Result(Result), .shamt(EX_IR[10:6]));  // open: Result_2
  or or_12 (en, \结束 , \继续运行 );
  and and_15 (and_15_out, ~\id_ex_1_传输状态out_表明当前传输数据有效 , ~en);  // AND_Gate
  assign bit_extender_1_out = {{16{1'b0}}, EX_IR[15:0]};  // Bit_Extender bit_extender_1
  assign bit_extender_2_out = {{16{EX_IR[15]}}, EX_IR[15:0]};  // Bit_Extender bit_extender_2
  EX_MEM ex_mem_1 (
    .CLK(CLK), .EN(and_15_out), .RST(RST), .SLLV_in(id_ex_1_sllv), .PC_in(EX_PC), .Jal_in(EX_Jal),
    .Result_in(Result), .MemToReg_in(id_ex_1_memtoreg), .LUI_in(id_ex_1_lui), .RegDst_in(EX_RegDst),
    .MemWrite_in(id_ex_1_memwrite), .BLTZ_in(BLTZ), .HB_in(id_ex_1_hb), .IR_in(EX_IR), .R2_in(id_ex_1_r2),
    .PC(MEM_PC), .Result(ex_mem_1_result), .IR(MEM_IR), .R2(ex_mem_1_r2),
    .\传输状态In_表明当前传输数据有效 (\id_ex_1_传输状态out_表明当前传输数据有效 ), .Jal(MEM_Jal), .RegDst(MEM_RegDst),
    .Sllv(ex_mem_1_sllv), .MemToReg(ex_mem_1_memtoreg), .LUI(ex_mem_1_lui), .HB(ex_mem_1_hb),
    .MemWrite(ex_mem_1_memwrite), .BLTZ(ex_mem_1_bltz), .\传输状态Out_表明当前传输数据有效 (\ex_mem_1_传输状态out_表明当前传输数据有效 ),
    .RegWrite_in(EX_RegWrite), .Regwrite(MEM_RegWrite), .R1_in(PC2), .R1(ex_mem_1_r1));  // open: Beq_in, JR_in, Bne_in, JMP_in, Beq, JR, JMP, Bne
  Multiplexer #(.width(32), .enable("false")) multiplexer_5 (
    .in0(bit_extender_1_out), .in1(bit_extender_2_out), .out(\立即数扩展 ), .sel(SignedExt));
  \W_计算  \w_计算_1  (
    .EX_RegDst(EX_RegDst), .MEM_RegDst(MEM_RegDst), .EX_IR(EX_IR), .WB_RegDst(WB_RegDst), .EX_Jal(EX_Jal),
    .MEM_IR(MEM_IR), .MEM_Jal(MEM_Jal), .WB_Jal(WB_Jal), .EX_W_num(EX_W_num), .WB_IR({WB_IR, WB_imm}),
    .MEM_W_num(MEM_W_num), .WB_W_num(WB_W_num));
  MEM_WB mem_wb_1 (
    .CLK(CLK), .EN(and_16_out), .RST(RST), .SLLV_in(ex_mem_1_sllv), .PC_in(MEM_PC), .Jal_in(MEM_Jal),
    .Result_in(ex_mem_1_result), .MemToReg_in(ex_mem_1_memtoreg), .LUI_in(ex_mem_1_lui),
    .RegDst_in(MEM_RegDst), .RegWrite_in(MEM_RegWrite), .BLTZ_in(ex_mem_1_bltz), .HB_in(ex_mem_1_hb),
    .IR_in(MEM_IR), .MemData_in(ram_1_data), .PC(WB_PC), .Result(WB_Result), .IR({WB_IR, WB_imm}),
    .MemData(MemData), .\传输状态In_表明当前传输数据有效 (\ex_mem_1_传输状态out_表明当前传输数据有效 ), .Jal(WB_Jal), .RegDst(WB_RegDst),
    .Sllv(SLLV), .MemToReg(MemToReg), .LUI(LUI), .HB(HB), .Regwrite(RegWrite), .\传输状态Out_表明当前传输数据有效 (out),
    .R1_in(ex_mem_1_r1), .R2_in(ex_mem_1_r2), .R1(WB_R1), .R2(WB_R2));  // open: Beq_in, JR_in, Bne_in, JMP_in, Beq, JR, JMP, Bne, BLTZ
  RAM #(.addrWidth(10), .dataWidth(32), .bus("separate")) ram_1 (
    .addr(ex_mem_1_result[11:2]), .din(ex_mem_1_r2), .data(ram_1_data), .str(ex_mem_1_memwrite), .sel(1'b1),
    .clk(CLK), .ld(1'b1), .clr(RST));
  and and_16 (and_16_out, ~\ex_mem_1_传输状态out_表明当前传输数据有效 , ~en);  // AND_Gate
  \Din计算  \din计算_1  (
    .MemData(MemData), .WB_R2(WB_R2), .Result(WB_Result), .WB_R1(WB_R1), .MemToReg(MemToReg),
    .WB_Jal(WB_Jal), .WB_LUI(LUI), .WB_Sllv(SLLV), .HB(HB), .Din(Din), .WB_PC(WB_PC), .WB_imm(WB_imm));

  // Other names for the same wires on the sheet: instr_index[25:0] = EX_IR[25:0];
  //   PC1[31:2] = {PC[31:28], EX_IR[25:0]}; 立即数[15:0] = EX_IR[15:0]; shamt[4:0] = EX_IR[10:6]; PC高4位[3:0] = PC[31:28];
  //   WB_IR[15:0] = WB_imm

  // Notes on the sheet:
  //   中断源
  //   中断等待指示
  //   数码管输出
  //   指令字
  //   contents of rom_1 (hex, n*v repeats v):
  //   20110001 8100005 20110001 20120002 20130003 8100009 20110001 20120002 20130003 810000d 20110001
  //   20120002 20130003 8100011 20110001 20120002 20130003 c1000fb 20100001 20110001 118fc0 112020
  //   20020022 c 118882 12200001 8100015 112020 20020022 c 20110001 118880 112020 20020022 c 12200001
  //   810001f 20110001 118fc0 112020 20020022 c 1188c3 112020 20020022 c 118903 112020 20020022 c 118903
  //   112020 20020022 c 118903 112020 20020022 c 118903 112020 20020022 c 118903 112020 20020022 c 118903
  //   112020 20020022 c 118903 112020 20020022 c 20100001 109fc0 139fc3 8021 2012000c 24160003 26100001
  //   3210000f 20080008 20090001 139900 2709825 132020 20020022 c 1094022 1500fff9 22100001 2018000f
  //   2188024 108700 20080008 20090001 139902 2709825 132021 20020022 c 1094022 1500fff9 108702 2c9b022
  //   12c00001 8100050 4020 1084027 84400 3508ffff 82021 20020022 c 2010ffff 20110000 ae300000 22100001
  //   22310004 ae300000 22100001 22310004 ae300000 22100001 22310004 ae300000 22100001 22310004 ae300000
  //   22100001 22310004 ae300000 22100001 22310004 ae300000 22100001 22310004 ae300000 22100001 22310004
  //   ae300000 22100001 22310004 ae300000 22100001 22310004 ae300000 22100001 22310004 ae300000 22100001
  //   22310004 ae300000 22100001 22310004 ae300000 22100001 22310004 ae300000 22100001 22310004 ae300000
  //   22100001 22310004 22100001 8020 2011003c 8e130000 8e340000 274402a 11000002 ae330000 ae140000
  //   2231fffc 1611fff8 102020 20020022 c 22100004 2011003c 1611fff2 20020032 c 20080001 20090003 20110876
  //   112020 20020022 c 200b0008 1118804 1318804 112020 20020022 c 216bffff 1560fff9 20020032 c 200b0008
  //   3c11fedc 3631ffff 112020 20020022 c 3c11ba98 112020 c 3c117654 112020 c 3c113210 112020 c 216bffff
  //   1560fff0 20020032 c 20090000 200b0010 34118483 20120404 118c00 129400 36318281 22520404 ad310000
  //   2328820 21290004 216bffff 1560fffb 200b0020 20090000 85310000 112020 20020022 c 21290002 216bffff
  //   1560fff9 20020032 c 2011fff1 112020 20020022 c 22310001 620fffb 2002000a c 20100000 22100001 102020
  //   20020022 c 22100002 102020 20020022 c 22100003 102020 20020022 c 22100004 102020 20020022 c 22100005
  //   102020 20020022 c 22100006 102020 20020022 c 22100007 102020 20020022 c 22100008 102020 20020022
  //   20020022 c 3e00008
  //   Func
  //   rs
  //   rt
  //   OP
  //   Func
  //   流水调试日志用
  //   shamt
endmodule

module \重定向流水线  (
);

  wire and_1_out, and_2_out, and_3_out, and_4_out, and_5_out, and_6_out, and_7_out, and_8_out, and_9_out,
       and_14_out, and_15_out, Beq, BLTZ, BLTZ_in, Bne, CLK, comparator_1_eq, comparator_2_eq, en, equal,
       EX_Jal, ex_mem_1_bltz, ex_mem_1_hb, ex_mem_1_memwrite, \ex_mem_1_传输状态out_表明当前传输数据有效 , EX_MtoR,
       EX_RegDst, EX_RegWrite, Go, HB, HB_in, id_ex_1_alusrcb, id_ex_1_hb, id_ex_1_lui, id_ex_1_memwrite,
       id_ex_1_sllv, \id_ex_1_传输状态out_表明当前传输数据有效 , \if_id_1_传输状态out_表明当前传输数据有效 , IR1, IR2, IR3, JMP, JMP_in,
       JR, JR_in, Load_Use, LUI, LUI_in, MEM_Jal, Mem_LUI, MEM_MtoR, MEM_RegDst, MEM_RegWrite, Mem_SLLV,
       MemToReg, nand_1_out, nor_1_out, not_1_out, not_2_out, or_3_out, or_4_out, or_9_out, out, pause,
       \PC使能 , RegWrite, RST, SignedExt, SignedExt_in, SLLV, SLLV_in, Syscall, W1, W2, W3, WB_Jal, WB_RegDst,
       \显示 , \暂停 , \有条件跳转 , \气泡 , \硬布线控制器_1_alu_src , \硬布线控制器_1_beq , \硬布线控制器_1_bne , \硬布线控制器_1_jal ,
       \硬布线控制器_1_memtoreg , \硬布线控制器_1_memwrite , \硬布线控制器_1_regdst , \硬布线控制器_1_regwrite , \结束 , \继续运行 , \跳转 ;
  wire [1:0] FordA, FordB, id_ex_1_forwarda, id_ex_1_forwardb, PCsrc;
  wire [3:0] id_ex_1_aluop, \硬布线控制器_1_alu_op ;
  wire [4:0] EX_W_num, ID_R1, ID_R2, MEM_W_num, WB_W_num;
  wire [5:0] Func, OP;
  wire [15:0] \LoadUse次数 , Mem_imm, WB_imm, \总周期数 , \插入气泡数 , \无条件分支数 , \条件分支成功数 ;
  wire [25:6] if_id_1_ir;
  wire [31:0] bit_extender_1_out, bit_extender_2_out, Din, EX_IR, EX_PC, EX_Result, id_ex_1_r2, ID_PC, IF_PC,
       LedData, MEM_PC, Mem_R1, Mem_R2, Mem_Result, MemData, multiplexer_1_out, multiplexer_4_out,
       multiplexer_5_out, multiplexer_6_out, multiplexer_7_out, multiplexer_8_out, PC, PC0, PC2, PC3, R1, R2,
       ram_1_data, Result, Result1, rom_1_data, shifter_1_out, WB_MemData, WB_PC, WB_R1, WB_R2, WB_Result,
       \立即数扩展 ;
  wire [31:16] MEM_IR, WB_IR;

  Button \u_总复位  (.out(RST));
  Button _1 (.out(IR1));
  Button _2 (.out(IR2));
  Button _3 (.out(IR3));
  Button \u_继续运行  (.out(Go));
  LED led_1 (.in(W1));
  LED led_2 (.in(W2));
  LED led_3 (.in(W3));
  nand nand_1 (nand_1_out, Syscall, ~out);  // NAND_Gate
  Hex_Digit_Display hex_digit_display_1 (.value(LedData[31:28]));  // open: dp
  Counter #(.width(16), .max('hffff)) counter_1 (
    .count(nand_1_out), .Q(\总周期数 ), .clk(CLK), .clr(RST));  // open: load, D, carry
  Hex_Digit_Display hex_digit_display_2 (.value(LedData[27:24]));  // open: dp
  Hex_Digit_Display hex_digit_display_3 (.value(LedData[23:20]));  // open: dp
  Multiplexer #(.select(2), .width(32), .enable("false")) multiplexer_1 (
    .in0(PC0), .in1({PC[31:28], EX_IR[25:0], 2'b00}), .in2(PC2), .in3(PC3), .out(multiplexer_1_out),
    .sel(PCsrc));
  Adder #(.width(32)) adder_1 (.a(IF_PC), .b(32'h4), .out(PC0));  // open: cin, cout
  Adder #(.width(32)) adder_2 (.a(EX_PC), .b(32'h4), .out(PC));  // open: cin, cout
  Shifter #(.width(32)) shifter_1 (.in(\立即数扩展 ), .\dist (5'b00010), .out(shifter_1_out));
  and and_1 (and_1_out, equal, Beq);
  and and_2 (and_2_out, Bne, ~equal);  // AND_Gate
  and and_3 (and_3_out, BLTZ, EX_Result[0]);
  Hex_Digit_Display hex_digit_display_4 (.value(LedData[15:12]));  // open: dp
  Hex_Digit_Display hex_digit_display_5 (.value(LedData[19:16]));  // open: dp
  Counter #(.width(16), .max('hffff)) counter_2 (
    .count(JMP), .Q(\无条件分支数 ), .clk(CLK), .clr(RST));  // open: load, D, carry
  Register #(.width(32)) u_PC (.D(multiplexer_1_out), .en(\PC使能 ), .Q(IF_PC), .clk(CLK), .clr(RST));
  Adder #(.width(32)) adder_3 (.a(shifter_1_out), .b(PC), .out(PC3));  // open: cin, cout
  or or_1 (\有条件跳转 , and_1_out, and_2_out, and_3_out);
  and and_4 (and_4_out, \暂停 , Go, ~\结束 );  // AND_Gate
  nor nor_1 (nor_1_out, pause, Load_Use);
  and and_5 (and_5_out, ~pause, \跳转 );  // AND_Gate
  Hex_Digit_Display hex_digit_display_6 (.value(LedData[7:4]));  // open: dp
  Hex_Digit_Display hex_digit_display_7 (.value(LedData[11:8]));  // open: dp
  Clock clock_1 (.out(CLK));
  // Probe on IF_PC[11:2]
  or or_2 (\PC使能 , and_4_out, and_5_out, nor_1_out);
  Hex_Digit_Display hex_digit_display_8 (.value(LedData[3:0]));  // open: dp
  Counter #(.width(16), .max('hffff)) counter_3 (
    .count(\有条件跳转 ), .Q(\条件分支成功数 ), .clk(CLK), .clr(RST));  // open: load, D, carry
  Counter #(.width(16), .max('hffff)) counter_4 (
    .count(Load_Use), .Q(\LoadUse次数 ), .clk(CLK), .clr(RST));  // open: load, D, carry
  and and_6 (and_6_out, en, ~RST);  // AND_Gate
  ROM #(.addrWidth(10), .dataWidth(32)) rom_1 (.addr(IF_PC[11:2]), .data(rom_1_data), .sel(1'b1));
  // Probe on rom_1_data
  or or_3 (or_3_out, and_6_out, Load_Use);
  // Probe on \总周期数 
  // Probe on \无条件分支数 
  // Probe on \条件分支成功数 
  // Probe on \插入气泡数 
  // Probe on \LoadUse次数 
  or or_4 (or_4_out, RST, \跳转 );
  IF_ID if_id_1 (
    .CLK(CLK), .EN(and_7_out), .RST(or_4_out), .PC_in(IF_PC), .PC(ID_PC), .IR_in(rom_1_data),
    .IR({OP, if_id_1_ir, Func}), .\传输状态In_表明当前传输数据有效 (not_1_out),
    .\传输状态Out_表明当前传输数据有效 (\if_id_1_传输状态out_表明当前传输数据有效 ), .\数据有效 (\气泡 ));  // open: 预测位_in, 预测位
  not not_1 (not_1_out, and_6_out);
  and and_7 (and_7_out, or_3_out, ~\跳转 );  // AND_Gate
  not not_2 (not_2_out, JR);
  or or_5 (PCsrc[1], JR, \有条件跳转 );
  or or_6 (\跳转 , JR, JMP, \有条件跳转 );
  // Probe on IF_PC[11:0]
  and and_8 (and_8_out, JMP, not_2_out);
  // Probe on ID_PC[11:0]
  or or_7 (\气泡 , \跳转 , pause, Load_Use);
  or or_8 (PCsrc[0], and_8_out, \有条件跳转 );
  // Probe on MEM_PC[11:0]
  // Probe on EX_PC[11:0]
  \硬布线控制器  \u_硬布线控制器_1  (
    .Func(Func), .OP(OP), .ALU_OP(\硬布线控制器_1_alu_op ), .MemToReg(\硬布线控制器_1_memtoreg ),
    .MemWrite(\硬布线控制器_1_memwrite ), .ALU_SRC(\硬布线控制器_1_alu_src ), .RegWrite(\硬布线控制器_1_regwrite ),
    .SysCALL(Syscall), .SignedExt(SignedExt_in), .RegDst(\硬布线控制器_1_regdst ), .JR(JR_in), .JMP(JMP_in),
    .Beq(\硬布线控制器_1_beq ), .JAL(\硬布线控制器_1_jal ), .Bne(\硬布线控制器_1_bne ), .LUI(LUI_in), .BTLZ(BLTZ_in),
    .HB(HB_in), .SLLV(SLLV_in));
  Multiplexer #(.width(5), .enable("false")) multiplexer_2 (
    .in0(if_id_1_ir[25:21]), .in1(5'b00010), .out(ID_R1), .sel(Syscall));
  Multiplexer #(.width(5), .enable("false")) multiplexer_3 (
    .in0(if_id_1_ir[20:16]), .in1(5'b00100), .out(ID_R2), .sel(Syscall));
  // Probe on WB_PC[11:0]
  MIPS_Regifile mips_regifile_1 (
    .Din(Din), .Clk(CLK), .R1(R1), .R2(R2), .WE(RegWrite), .W_num(WB_W_num), .R1_num(ID_R1), .R2_num(ID_R2));
  or or_9 (or_9_out, \继续运行 , RST, Load_Use, \跳转 , \结束 );
  ID_EX id_ex_1 (
    .CLK(CLK), .PC_in(ID_PC), .EN(and_9_out), .IR_in({OP, if_id_1_ir, Func}), .JMP(JMP), .JR(JR),
    .SignedExt(SignedExt), .LUI(id_ex_1_lui), .BLTZ(BLTZ), .HB(id_ex_1_hb), .Sllv(id_ex_1_sllv), .Beq(Beq),
    .Bne(Bne), .MemToReg(EX_MtoR), .MemWrite(id_ex_1_memwrite), .AluOP(id_ex_1_aluop),
    .AluSrcB(id_ex_1_alusrcb), .Jal(EX_Jal), .RegDst(EX_RegDst), .RST(or_9_out), .Beq_in(\硬布线控制器_1_beq ),
    .MemToReg_in(\硬布线控制器_1_memtoreg ), .Bne_in(\硬布线控制器_1_bne ), .MemWrite_in(\硬布线控制器_1_memwrite ),
    .AluOP_in(\硬布线控制器_1_alu_op ), .AluSrcB_in(\硬布线控制器_1_alu_src ), .JR_in(JR_in), .Jal_in(\硬布线控制器_1_jal ),
    .SignedExt_in(SignedExt_in), .LUI_in(LUI_in), .BLTZ_in(BLTZ_in), .HB_in(HB_in), .SLLV_in(SLLV_in),
    .JMP_in(JMP_in), .RegDst_in(\硬布线控制器_1_regdst ), .PC(EX_PC), .IR(EX_IR),
    .\传输状态In_表明当前传输数据有效 (\if_id_1_传输状态out_表明当前传输数据有效 ), .\传输状态Out_表明当前传输数据有效 (\id_ex_1_传输状态out_表明当前传输数据有效 ),
    .R1_in(R1), .R2_in(R2), .R1(PC2), .R2(id_ex_1_r2), .RegWrite_in(\硬布线控制器_1_regwrite ),
    .Regwrite(EX_RegWrite), .\跳转 (\气泡 ), .ForwardA_in(FordA), .ForwardA(id_ex_1_forwarda),
    .ForwardB_in(FordB), .ForwardB(id_ex_1_forwardb));  // open: 预测位_in, 预测位
  and and_9 (and_9_out, ~\if_id_1_传输状态out_表明当前传输数据有效 , ~en);  // AND_Gate
  Multiplexer #(.select(2), .width(32), .enable("false")) multiplexer_4 (
    .in0(R1), .in1(R1), .in2(Result1), .in3(EX_Result), .out(multiplexer_4_out), .sel(FordA));
  Multiplexer #(.select(2), .width(32), .enable("false")) multiplexer_5 (
    .in0(R2), .in1(R2), .in2(Result1), .in3(EX_Result), .out(multiplexer_5_out), .sel(FordB));
  \W_计算  \w_计算_1  (
    .EX_RegDst(EX_RegDst), .MEM_RegDst(MEM_RegDst), .EX_IR(EX_IR), .WB_RegDst(WB_RegDst), .EX_Jal(EX_Jal),
    .MEM_IR({MEM_IR, Mem_imm}), .MEM_Jal(MEM_Jal), .WB_Jal(WB_Jal), .EX_W_num(EX_W_num),
    .WB_IR({WB_IR, WB_imm}), .MEM_W_num(MEM_W_num), .WB_W_num(WB_W_num));
  Comparator #(.width(32)) comparator_1 (.a(multiplexer_4_out), .b(32'ha), .eq(comparator_1_eq));  // open: gt, lt
  Register #(.width(32)) register_1 (.D(multiplexer_5_out), .en(\显示 ), .Q(LedData), .clk(CLK), .clr(RST));
  Multiplexer #(.select(2), .width(32), .enable("false")) multiplexer_6 (
    .in0(PC2), .in1(MemData), .in2(Result), .in3(Result1), .out(multiplexer_6_out), .sel(id_ex_1_forwarda));
  Multiplexer #(.select(2), .width(32), .enable("false")) multiplexer_7 (
    .in0(id_ex_1_r2), .in1(MemData), .in2(Result), .in3(Result1), .out(multiplexer_7_out),
    .sel(id_ex_1_forwardb));
  and and_10 (\结束 , comparator_1_eq, Syscall);
  and and_11 (\显示 , Syscall, comparator_2_eq);
  Comparator #(.width(32)) comparator_2 (.a(multiplexer_4_out), .b(32'h22), .eq(comparator_2_eq));  // open: gt, lt
  Multiplexer #(.width(32), .enable("false")) multiplexer_8 (
    .in0(multiplexer_7_out), .in1(\立即数扩展 ), .out(multiplexer_8_out), .sel(id_ex_1_alusrcb));
  and and_12 (\暂停 , ~\显示 , ~\结束 , Syscall, ~Load_Use);  // AND_Gate
  MIPS_ALU mips_alu_1 (
    .X(multiplexer_6_out), .Y(multiplexer_8_out), .AluOP(id_ex_1_aluop), .Equal(equal), .Result(EX_Result),
    .shamt(EX_IR[10:6]));  // open: Result_2
  or or_10 (pause, \结束 , \暂停 );
  and and_13 (\继续运行 , \暂停 , ~Go);  // AND_Gate
  EX_MEM ex_mem_1 (
    .CLK(CLK), .EN(and_14_out), .RST(RST), .SLLV_in(id_ex_1_sllv), .PC_in(EX_PC), .Jal_in(EX_Jal),
    .Result_in(EX_Result), .MemToReg_in(EX_MtoR), .LUI_in(id_ex_1_lui), .RegDst_in(EX_RegDst),
    .MemWrite_in(id_ex_1_memwrite), .BLTZ_in(BLTZ), .HB_in(id_ex_1_hb), .IR_in(EX_IR),
    .R2_in(multiplexer_7_out), .PC(MEM_PC), .Result(Mem_Result), .IR({MEM_IR, Mem_imm}), .R2(Mem_R2),
    .\传输状态In_表明当前传输数据有效 (\id_ex_1_传输状态out_表明当前传输数据有效 ), .Jal(MEM_Jal), .RegDst(MEM_RegDst), .Sllv(Mem_SLLV),
    .MemToReg(MEM_MtoR), .LUI(Mem_LUI), .HB(ex_mem_1_hb), .MemWrite(ex_mem_1_memwrite), .BLTZ(ex_mem_1_bltz),
    .\传输状态Out_表明当前传输数据有效 (\ex_mem_1_传输状态out_表明当前传输数据有效 ), .RegWrite_in(EX_RegWrite), .Regwrite(MEM_RegWrite),
    .R1_in(multiplexer_6_out), .R1(Mem_R1));  // open: Beq_in, JR_in, Bne_in, JMP_in, Beq, JR, JMP, Bne
  and and_14 (and_14_out, ~\id_ex_1_传输状态out_表明当前传输数据有效 , ~en);  // AND_Gate
  or or_11 (en, \结束 , \继续运行 );
  \Din计算  \din计算_1  (
    .MemData(MemData), .WB_R2(WB_R2), .Result(WB_Result), .WB_R1(WB_R1), .MemToReg(MemToReg),
    .WB_Jal(WB_Jal), .WB_LUI(LUI), .WB_Sllv(SLLV), .HB(HB), .Din(Din), .WB_PC(WB_PC), .WB_imm(WB_imm));
  assign bit_extender_1_out = {{16{1'b0}}, EX_IR[15:0]};  // Bit_Extender bit_extender_1
  assign bit_extender_2_out = {{16{EX_IR[15]}}, EX_IR[15:0]};  // Bit_Extender bit_extender_2
  MEM_WB mem_wb_1 (
    .CLK(CLK), .EN(and_15_out), .RST(RST), .SLLV_in(Mem_SLLV), .PC_in(MEM_PC), .Jal_in(MEM_Jal),
    .Result_in(Mem_Result), .MemToReg_in(MEM_MtoR), .LUI_in(Mem_LUI), .RegDst_in(MEM_RegDst),
    .RegWrite_in(MEM_RegWrite), .BLTZ_in(ex_mem_1_bltz), .HB_in(ex_mem_1_hb), .IR_in({MEM_IR, Mem_imm}),
    .MemData_in(ram_1_data), .PC(WB_PC), .Result(WB_Result), .IR({WB_IR, WB_imm}), .MemData(WB_MemData),
    .\传输状态In_表明当前传输数据有效 (\ex_mem_1_传输状态out_表明当前传输数据有效 ), .Jal(WB_Jal), .RegDst(WB_RegDst), .Sllv(SLLV),
    .MemToReg(MemToReg), .LUI(LUI), .HB(HB), .Regwrite(RegWrite), .\传输状态Out_表明当前传输数据有效 (out), .R1_in(Mem_R1),
    .R2_in(Mem_R2), .R1(WB_R1), .R2(WB_R2));  // open: Beq_in, JR_in, Bne_in, JMP_in, Beq, JR, JMP, Bne, BLTZ
  RAM #(.addrWidth(10), .dataWidth(32), .bus("separate")) ram_1 (
    .addr(Mem_Result[11:2]), .din(Mem_R2), .data(ram_1_data), .str(ex_mem_1_memwrite), .sel(1'b1), .clk(CLK),
    .ld(1'b1), .clr(RST));
  and and_15 (and_15_out, ~\ex_mem_1_传输状态out_表明当前传输数据有效 , ~en);  // AND_Gate
  Multiplexer #(.width(32), .enable("false")) multiplexer_9 (
    .in0(bit_extender_1_out), .in1(bit_extender_2_out), .out(\立即数扩展 ), .sel(SignedExt));
  \重定向控制器  \u_重定向控制器_1  (
    .OP(OP), .EX_WriteReg_num(EX_W_num), .EX_RegWrite(EX_RegWrite), .ForwardA(FordA),
    .MEM_WriteReg_num(MEM_W_num), .MEM_RegWrite(MEM_RegWrite), .ForwardB(FordB), .Func(Func),
    .ID_R1_num(ID_R1), .ID_R2_num(ID_R2), .Load_Use(Load_Use), .EX_MemToReg(EX_MtoR),
    .Mem_MemToReg(MEM_MtoR), .WB_MemData(WB_MemData), .Mem_R1(Mem_R1), .WB_R1(WB_R1), .WB_Result(WB_Result),
    .WB_imm(WB_imm), .Mem_R2(Mem_R2), .WB_R2(WB_R2), .Mem_imm(Mem_imm), .Mem_LUI(Mem_LUI), .WB_LUI(LUI),
    .Mem_Sllv(Mem_SLLV), .WB_Sllv(SLLV), .WB_MemToReg(MemToReg), .WB_HB(HB), .Result1(Result1),
    .Result2(Result), .MemData(MemData), .Mem_Result(Mem_Result));

  // Other names for the same wires on the sheet: instr_index[25:0] = EX_IR[25:0];
  //   PC1[31:2] = {PC[31:28], EX_IR[25:0]}; 立即数[15:0] = EX_IR[15:0]; shamt[4:0] = EX_IR[10:6]; MEM_IR[15:0] = Mem_imm;
  //   PC高4位[3:0] = PC[31:28]; WB_IR[15:0] = WB_imm

  // Notes on the sheet:
  //   中断源
  //   中断等待指示
  //   数码管输出
  //   指令字
  //   contents of rom_1 (hex, n*v repeats v):
  //   20110001 8100005 20110001 20120002 20130003 8100009 20110001 20120002 20130003 810000d 20110001
  //   20120002 20130003 8100011 20110001 20120002 20130003 c1000fb 20100001 20110001 118fc0 112020
  //   20020022 c 118882 12200001 8100015 112020 20020022 c 20110001 118880 112020 20020022 c 12200001
  //   810001f 20110001 118fc0 112020 20020022 c 1188c3 112020 20020022 c 118903 112020 20020022 c 118903
  //   112020 20020022 c 118903 112020 20020022 c 118903 112020 20020022 c 118903 112020 20020022 c 118903
  //   112020 20020022 c 118903 112020 20020022 c 20100001 109fc0 139fc3 8021 2012000c 24160003 26100001
  //   3210000f 20080008 20090001 139900 2709825 132020 20020022 c 1094022 1500fff9 22100001 2018000f
  //   2188024 108700 20080008 20090001 139902 2709825 132021 20020022 c 1094022 1500fff9 108702 2c9b022
  //   12c00001 8100050 4020 1084027 84400 3508ffff 82021 20020022 c 2010ffff 20110000 ae300000 22100001
  //   22310004 ae300000 22100001 22310004 ae300000 22100001 22310004 ae300000 22100001 22310004 ae300000
  //   22100001 22310004 ae300000 22100001 22310004 ae300000 22100001 22310004 ae300000 22100001 22310004
  //   ae300000 22100001 22310004 ae300000 22100001 22310004 ae300000 22100001 22310004 ae300000 22100001
  //   22310004 ae300000 22100001 22310004 ae300000 22100001 22310004 ae300000 22100001 22310004 ae300000
  //   22100001 22310004 22100001 8020 2011003c 8e130000 8e340000 274402a 11000002 ae330000 ae140000
  //   2231fffc 1611fff8 102020 20020022 c 22100004 2011003c 1611fff2 20020032 c 20080001 20090003 20110876
  //   112020 20020022 c 200b0008 1118804 1318804 112020 20020022 c 216bffff 1560fff9 20020032 c 200b0008
  //   3c11fedc 3631ffff 112020 20020022 c 3c11ba98 112020 c 3c117654 112020 c 3c113210 112020 c 216bffff
  //   1560fff0 20020032 c 20090000 200b0010 34118483 20120404 118c00 129400 36318281 22520404 ad310000
  //   2328820 21290004 216bffff 1560fffb 200b0020 20090000 85310000 112020 20020022 c 21290002 216bffff
  //   1560fff9 20020032 c 2011fff1 112020 20020022 c 22310001 620fffb 2002000a c 20100000 22100001 102020
  //   20020022 c 22100002 102020 20020022 c 22100003 102020 20020022 c 22100004 102020 20020022 c 22100005
  //   102020 20020022 c 22100006 102020 20020022 c 22100007 102020 20020022 c 22100008 102020 20020022
  //   20020022 c 3e00008
  //   Func
  //   rs
  //   rt
  //   OP
  //   Func
  //   流水调试日志用
  //   shamt
endmodule

module \控制信号生成_2  (
  input  OP0,
  input  OP1,
  input  OP2,
  input  OP3,
  input  OP4,
  input  OP5,
  input  F0,
  input  F1,
  input  F2,
  input  F3,
  input  F4,
  input  F5,
  output LUI,
  output BTLZ,
  output HB,
  output SLLV
);

  wire not_1_out, not_2_out, not_3_out, not_4_out, not_5_out, not_6_out, not_7_out, not_8_out, not_9_out,
       not_10_out, not_11_out, not_12_out, not_13_out, not_14_out, not_15_out, not_16_out, not_17_out,
       not_18_out, not_19_out, not_20_out, not_21_out, not_22_out;

  not not_1 (not_1_out, OP5);
  not not_2 (not_2_out, OP4);
  not not_3 (not_3_out, OP5);
  not not_4 (not_4_out, OP4);
  not not_5 (not_5_out, OP3);
  not not_6 (not_6_out, OP2);
  not not_7 (not_7_out, OP1);
  not not_8 (not_8_out, OP4);
  not not_9 (not_9_out, OP3);
  not not_10 (not_10_out, OP2);
  not not_11 (not_11_out, OP1);
  not not_12 (not_12_out, OP5);
  not not_13 (not_13_out, OP4);
  not not_14 (not_14_out, OP3);
  not not_15 (not_15_out, OP2);
  not not_16 (not_16_out, OP1);
  not not_17 (not_17_out, OP0);
  not not_18 (not_18_out, F5);
  not not_19 (not_19_out, F4);
  not not_20 (not_20_out, F3);
  not not_21 (not_21_out, F1);
  not not_22 (not_22_out, F0);
  and and_1 (LUI, not_1_out, not_2_out, OP3, OP2, OP1, OP0);
  and and_2 (BTLZ, not_3_out, not_4_out, not_5_out, not_6_out, not_7_out, OP0);
  and and_3 (HB, OP5, not_8_out, not_9_out, not_10_out, not_11_out, OP0);
  and and_4 (SLLV, not_12_out, not_13_out, not_14_out, not_15_out, not_16_out, not_17_out, not_18_out, not_19_out, not_20_out, F2, not_21_out, not_22_out);
endmodule

module \控制信号生成_1  (
  input  OP0,
  input  OP1,
  input  OP2,
  input  OP3,
  input  OP4,
  input  OP5,
  input  F0,
  input  F1,
  input  F2,
  input  F3,
  input  F4,
  input  F5,
  output MemToReg,
  output MemWrite,
  output ALU_SRC,
  output RegWrite,
  output SysCALL,
  output SignedExt,
  output RegDst,
  output BEQ,
  output BNE,
  output JR,
  output JMP,
  output JAL
);

  wire and_1_out, and_2_out, and_4_out, and_5_out, and_6_out, and_7_out, and_8_out, and_9_out, and_10_out,
       and_11_out, and_12_out, and_13_out, and_14_out, and_15_out, and_16_out, and_17_out, and_18_out,
       and_19_out, and_20_out, and_21_out, and_22_out, and_23_out, and_24_out, and_25_out, and_26_out,
       and_27_out, and_28_out, and_29_out, and_30_out, and_31_out, and_32_out, and_34_out, and_35_out,
       and_36_out, and_37_out, and_38_out, and_39_out, and_40_out, and_41_out, and_42_out, and_43_out,
       and_44_out, and_45_out, and_46_out, and_47_out, and_48_out, and_49_out, and_50_out, and_51_out,
       and_52_out, and_53_out, and_54_out, and_58_out, and_59_out, and_60_out, not_1_out, not_2_out,
       not_3_out, not_4_out, not_5_out, not_6_out, not_7_out, not_8_out, not_9_out, not_10_out, not_11_out,
       not_12_out, not_13_out, not_14_out, not_15_out, not_16_out, not_17_out, not_18_out, not_19_out,
       not_20_out, not_21_out, not_22_out, not_23_out, not_24_out, not_25_out, not_26_out, not_27_out,
       not_28_out, not_29_out, not_30_out, not_31_out, not_32_out, not_33_out, not_34_out, not_35_out,
       not_36_out, not_37_out, not_38_out, not_39_out, not_40_out, not_41_out, not_42_out, not_43_out,
       not_44_out, not_45_out, not_46_out, not_47_out, not_48_out, not_49_out, not_50_out, not_51_out,
       not_52_out, not_53_out, not_54_out, not_55_out, not_56_out, not_57_out, not_58_out, not_59_out,
       not_60_out, not_61_out, not_62_out, not_63_out, not_64_out, not_65_out, not_66_out, not_67_out,
       not_68_out, not_69_out, not_70_out, not_71_out, not_72_out, not_73_out, not_74_out, not_75_out,
       not_76_out, not_77_out, not_78_out, not_79_out, not_80_out, not_81_out, not_82_out, not_83_out,
       not_84_out, not_85_out, not_86_out, not_87_out, not_88_out, not_89_out, not_90_out, not_91_out,
       not_92_out, not_93_out, not_94_out, not_95_out, not_96_out, not_97_out, not_98_out, not_99_out,
       not_100_out, not_101_out, not_102_out, not_103_out, not_104_out, not_105_out, not_106_out,
       not_107_out, not_108_out, not_109_out, not_110_out, not_111_out, not_112_out, not_113_out,
       not_114_out, not_115_out, not_116_out, not_117_out, not_118_out, not_119_out, not_120_out,
       not_121_out, not_122_out, not_123_out, not_124_out, not_125_out, not_126_out, not_127_out,
       not_128_out, not_129_out, not_130_out, not_131_out, not_132_out, not_133_out, not_134_out,
       not_135_out, not_136_out, not_137_out, not_138_out, not_139_out, not_140_out, not_141_out,
       not_142_out, not_143_out, not_144_out, not_145_out, not_146_out, not_147_out, not_148_out,
       not_149_out, not_150_out, not_151_out, not_152_out, not_153_out, not_154_out, not_155_out,
       not_156_out, not_157_out, not_158_out, not_159_out, not_160_out, not_161_out, not_162_out,
       not_163_out, not_164_out, not_165_out, not_166_out, not_167_out, not_168_out, not_169_out,
       not_170_out, not_171_out, not_172_out, not_173_out, not_174_out, not_175_out, not_176_out,
       not_177_out, not_178_out, not_179_out, not_180_out, not_181_out, not_182_out, not_183_out,
       not_184_out, not_185_out, not_186_out, not_187_out, not_188_out, not_189_out, not_190_out,
       not_191_out, not_192_out, not_193_out, not_194_out, not_195_out, not_196_out, not_197_out,
       not_198_out, not_199_out, not_200_out, not_201_out, not_202_out, not_203_out, not_204_out,
       not_205_out, not_206_out, not_207_out, not_208_out, not_209_out, not_210_out, not_211_out,
       not_212_out, not_213_out, not_214_out, not_215_out, not_216_out, not_217_out, not_218_out,
       not_219_out, not_220_out, not_221_out, not_222_out, not_223_out, not_224_out, not_225_out,
       not_226_out, not_227_out, not_228_out, not_229_out, not_230_out, not_231_out, not_232_out,
       not_233_out, not_234_out, not_235_out, not_236_out, not_237_out, not_238_out, not_239_out,
       not_240_out, not_241_out, not_242_out, not_243_out, not_244_out, not_245_out, not_246_out,
       not_247_out, not_248_out, not_249_out, not_250_out, not_251_out, not_252_out, not_253_out,
       not_254_out, not_255_out, not_256_out, not_257_out, not_258_out, not_259_out, not_260_out,
       not_261_out, not_262_out, not_263_out, not_264_out, not_265_out, not_266_out, not_267_out,
       not_268_out, not_269_out, not_270_out, not_271_out, not_272_out, not_273_out, not_274_out,
       not_275_out, not_276_out, not_277_out, not_278_out, not_279_out, not_280_out, not_281_out,
       not_282_out, not_283_out, not_284_out, not_285_out, not_286_out, not_287_out, not_288_out,
       not_289_out, not_290_out, not_291_out, not_292_out, not_293_out, not_294_out, not_295_out,
       not_296_out, not_297_out, not_298_out, not_299_out, not_300_out, not_301_out, not_302_out,
       not_303_out, not_304_out, not_305_out, not_306_out, not_307_out, not_308_out, not_309_out,
       not_310_out, not_311_out, not_312_out, not_313_out, not_314_out, not_315_out, not_316_out,
       not_317_out, not_318_out, not_319_out, not_320_out, not_321_out, not_322_out, not_323_out,
       not_324_out, not_325_out, not_326_out, not_327_out, not_328_out, not_329_out, not_330_out,
       not_331_out, not_332_out, not_333_out, not_334_out, not_335_out, not_336_out, not_337_out,
       not_338_out, not_339_out, not_340_out, not_341_out, not_342_out, not_343_out, not_344_out,
       not_345_out, not_346_out, not_347_out, not_348_out, not_349_out, not_350_out, not_351_out,
       not_352_out, not_353_out, not_354_out, not_355_out, not_356_out, not_357_out, not_358_out,
       not_359_out, not_360_out, not_361_out, not_362_out, not_363_out, not_364_out, not_365_out,
       not_366_out, not_367_out, not_368_out, not_369_out, not_370_out, not_371_out, not_372_out,
       not_373_out, not_374_out, not_375_out, not_376_out, not_377_out, not_378_out, not_379_out,
       not_380_out, not_381_out, not_382_out, not_383_out, not_384_out, not_385_out, not_386_out,
       not_387_out, not_388_out, not_389_out, not_390_out, not_391_out, not_392_out, not_393_out,
       not_394_out, not_395_out, not_396_out, not_397_out, not_398_out, not_399_out;

  not not_1 (not_1_out, OP4);
  not not_2 (not_2_out, OP3);
  not not_3 (not_3_out, OP2);
  not not_4 (not_4_out, OP4);
  not not_5 (not_5_out, OP3);
  not not_6 (not_6_out, OP2);
  not not_7 (not_7_out, OP1);
  not not_8 (not_8_out, OP4);
  not not_9 (not_9_out, OP2);
  not not_10 (not_10_out, OP5);
  not not_11 (not_11_out, OP4);
  not not_12 (not_12_out, OP2);
  not not_13 (not_13_out, OP1);
  not not_14 (not_14_out, OP0);
  not not_15 (not_15_out, OP5);
  not not_16 (not_16_out, OP4);
  not not_17 (not_17_out, OP1);
  not not_18 (not_18_out, OP0);
  not not_19 (not_19_out, OP5);
  not not_20 (not_20_out, OP4);
  not not_21 (not_21_out, OP2);
  not not_22 (not_22_out, OP1);
  not not_23 (not_23_out, OP5);
  not not_24 (not_24_out, OP4);
  not not_25 (not_25_out, OP2);
  not not_26 (not_26_out, OP0);
  not not_27 (not_27_out, OP5);
  not not_28 (not_28_out, OP4);
  not not_29 (not_29_out, OP1);
  not not_30 (not_30_out, OP4);
  not not_31 (not_31_out, OP3);
  not not_32 (not_32_out, OP2);
  not not_33 (not_33_out, OP4);
  not not_34 (not_34_out, OP2);
  not not_35 (not_35_out, OP4);
  not not_36 (not_36_out, OP3);
  not not_37 (not_37_out, OP2);
  not not_38 (not_38_out, OP1);
  not not_39 (not_39_out, OP5);
  not not_40 (not_40_out, OP4);
  not not_41 (not_41_out, OP3);
  not not_42 (not_42_out, OP2);
  not not_43 (not_43_out, OP1);
  not not_44 (not_44_out, OP0);
  not not_45 (not_45_out, F5);
  not not_46 (not_46_out, F4);
  not not_47 (not_47_out, F3);
  not not_48 (not_48_out, F2);
  not not_49 (not_49_out, F1);
  not not_50 (not_50_out, F0);
  not not_51 (not_51_out, OP5);
  not not_52 (not_52_out, OP4);
  not not_53 (not_53_out, OP3);
  not not_54 (not_54_out, OP2);
  not not_55 (not_55_out, OP1);
  not not_56 (not_56_out, OP0);
  not not_57 (not_57_out, F5);
  not not_58 (not_58_out, F4);
  not not_59 (not_59_out, F3);
  not not_60 (not_60_out, F2);
  not not_61 (not_61_out, OP5);
  not not_62 (not_62_out, OP4);
  not not_63 (not_63_out, OP3);
  not not_64 (not_64_out, OP2);
  not not_65 (not_65_out, OP1);
  not not_66 (not_66_out, OP0);
  not not_67 (not_67_out, F5);
  not not_68 (not_68_out, F4);
  not not_69 (not_69_out, F3);
  not not_70 (not_70_out, F2);
  not not_71 (not_71_out, F0);
  not not_72 (not_72_out, OP5);
  not not_73 (not_73_out, OP4);
  not not_74 (not_74_out, OP3);
  not not_75 (not_75_out, OP2);
  not not_76 (not_76_out, OP1);
  not not_77 (not_77_out, OP0);
  not not_78 (not_78_out, F4);
  not not_79 (not_79_out, F3);
  not not_80 (not_80_out, F2);
  not not_81 (not_81_out, F1);
  not not_82 (not_82_out, F0);
  not not_83 (not_83_out, OP5);
  not not_84 (not_84_out, OP4);
  not not_85 (not_85_out, OP3);
  not not_86 (not_86_out, OP2);
  not not_87 (not_87_out, OP1);
  not not_88 (not_88_out, OP0);
  not not_89 (not_89_out, F4);
  not not_90 (not_90_out, F3);
  not not_91 (not_91_out, F2);
  not not_92 (not_92_out, F1);
  not not_93 (not_93_out, OP5);
  not not_94 (not_94_out, OP4);
  not not_95 (not_95_out, OP3);
  not not_96 (not_96_out, OP2);
  not not_97 (not_97_out, OP1);
  not not_98 (not_98_out, OP0);
  not not_99 (not_99_out, F4);
  not not_100 (not_100_out, F3);
  not not_101 (not_101_out, F2);
  not not_102 (not_102_out, F0);
  not not_103 (not_103_out, OP5);
  not not_104 (not_104_out, OP4);
  not not_105 (not_105_out, OP3);
  not not_106 (not_106_out, OP2);
  not not_107 (not_107_out, OP1);
  not not_108 (not_108_out, OP0);
  not not_109 (not_109_out, F4);
  not not_110 (not_110_out, F3);
  not not_111 (not_111_out, F1);
  not not_112 (not_112_out, F0);
  not not_113 (not_113_out, OP5);
  not not_114 (not_114_out, OP4);
  not not_115 (not_115_out, OP3);
  not not_116 (not_116_out, OP2);
  not not_117 (not_117_out, OP1);
  not not_118 (not_118_out, OP0);
  not not_119 (not_119_out, F4);
  not not_120 (not_120_out, F3);
  not not_121 (not_121_out, F1);
  not not_122 (not_122_out, OP5);
  not not_123 (not_123_out, OP4);
  not not_124 (not_124_out, OP3);
  not not_125 (not_125_out, OP2);
  not not_126 (not_126_out, OP1);
  not not_127 (not_127_out, OP0);
  not not_128 (not_128_out, F4);
  not not_129 (not_129_out, F3);
  not not_130 (not_130_out, OP5);
  not not_131 (not_131_out, OP4);
  not not_132 (not_132_out, OP3);
  not not_133 (not_133_out, OP2);
  not not_134 (not_134_out, OP1);
  not not_135 (not_135_out, OP0);
  not not_136 (not_136_out, F4);
  not not_137 (not_137_out, F2);
  not not_138 (not_138_out, F0);
  not not_139 (not_139_out, OP5);
  not not_140 (not_140_out, OP4);
  not not_141 (not_141_out, OP3);
  not not_142 (not_142_out, OP2);
  not not_143 (not_143_out, OP1);
  not not_144 (not_144_out, OP0);
  not not_145 (not_145_out, F4);
  not not_146 (not_146_out, F2);
  not not_147 (not_147_out, OP5);
  not not_148 (not_148_out, OP4);
  not not_149 (not_149_out, OP3);
  not not_150 (not_150_out, OP2);
  not not_151 (not_151_out, OP5);
  not not_152 (not_152_out, OP4);
  not not_153 (not_153_out, OP2);
  not not_154 (not_154_out, OP1);
  not not_155 (not_155_out, OP0);
  not not_156 (not_156_out, OP5);
  not not_157 (not_157_out, OP4);
  not not_158 (not_158_out, OP1);
  not not_159 (not_159_out, OP0);
  not not_160 (not_160_out, OP5);
  not not_161 (not_161_out, OP4);
  not not_162 (not_162_out, OP2);
  not not_163 (not_163_out, OP1);
  not not_164 (not_164_out, OP5);
  not not_165 (not_165_out, OP4);
  not not_166 (not_166_out, OP2);
  not not_167 (not_167_out, OP0);
  not not_168 (not_168_out, OP5);
  not not_169 (not_169_out, OP4);
  not not_170 (not_170_out, OP1);
  not not_171 (not_171_out, OP4);
  not not_172 (not_172_out, OP3);
  not not_173 (not_173_out, OP2);
  not not_174 (not_174_out, OP5);
  not not_175 (not_175_out, OP4);
  not not_176 (not_176_out, OP3);
  not not_177 (not_177_out, OP2);
  not not_178 (not_178_out, OP1);
  not not_179 (not_179_out, OP0);
  not not_180 (not_180_out, F5);
  not not_181 (not_181_out, F4);
  not not_182 (not_182_out, F3);
  not not_183 (not_183_out, F1);
  not not_184 (not_184_out, F0);
  not not_185 (not_185_out, OP5);
  not not_186 (not_186_out, OP4);
  not not_187 (not_187_out, OP4);
  not not_188 (not_188_out, OP3);
  not not_189 (not_189_out, OP2);
  not not_190 (not_190_out, OP1);
  not not_191 (not_191_out, OP5);
  not not_192 (not_192_out, OP4);
  not not_193 (not_193_out, OP3);
  not not_194 (not_194_out, OP2);
  not not_195 (not_195_out, OP1);
  not not_196 (not_196_out, OP0);
  not not_197 (not_197_out, F5);
  not not_198 (not_198_out, F4);
  not not_199 (not_199_out, F1);
  not not_200 (not_200_out, F0);
  not not_201 (not_201_out, OP5);
  not not_202 (not_202_out, OP4);
  not not_203 (not_203_out, OP3);
  not not_204 (not_204_out, OP1);
  not not_205 (not_205_out, OP0);
  not not_206 (not_206_out, OP5);
  not not_207 (not_207_out, OP4);
  not not_208 (not_208_out, OP3);
  not not_209 (not_209_out, OP1);
  not not_210 (not_210_out, OP5);
  not not_211 (not_211_out, OP4);
  not not_212 (not_212_out, OP2);
  not not_213 (not_213_out, OP1);
  not not_214 (not_214_out, OP0);
  not not_215 (not_215_out, OP5);
  not not_216 (not_216_out, OP4);
  not not_217 (not_217_out, OP2);
  not not_218 (not_218_out, OP1);
  not not_219 (not_219_out, OP5);
  not not_220 (not_220_out, OP4);
  not not_221 (not_221_out, OP2);
  not not_222 (not_222_out, OP0);
  not not_223 (not_223_out, OP4);
  not not_224 (not_224_out, OP3);
  not not_225 (not_225_out, OP2);
  not not_226 (not_226_out, OP4);
  not not_227 (not_227_out, OP2);
  not not_228 (not_228_out, OP4);
  not not_229 (not_229_out, OP3);
  not not_230 (not_230_out, OP2);
  not not_231 (not_231_out, OP1);
  not not_232 (not_232_out, OP5);
  not not_233 (not_233_out, OP4);
  not not_234 (not_234_out, OP3);
  not not_235 (not_235_out, OP2);
  not not_236 (not_236_out, OP1);
  not not_237 (not_237_out, OP5);
  not not_238 (not_238_out, OP4);
  not not_239 (not_239_out, OP3);
  not not_240 (not_240_out, OP2);
  not not_241 (not_241_out, OP1);
  not not_242 (not_242_out, OP0);
  not not_243 (not_243_out, F5);
  not not_244 (not_244_out, F4);
  not not_245 (not_245_out, F3);
  not not_246 (not_246_out, F2);
  not not_247 (not_247_out, F1);
  not not_248 (not_248_out, F0);
  not not_249 (not_249_out, OP5);
  not not_250 (not_250_out, OP4);
  not not_251 (not_251_out, OP3);
  not not_252 (not_252_out, OP2);
  not not_253 (not_253_out, OP1);
  not not_254 (not_254_out, OP0);
  not not_255 (not_255_out, F5);
  not not_256 (not_256_out, F4);
  not not_257 (not_257_out, F3);
  not not_258 (not_258_out, F2);
  not not_259 (not_259_out, OP5);
  not not_260 (not_260_out, OP4);
  not not_261 (not_261_out, OP3);
  not not_262 (not_262_out, OP2);
  not not_263 (not_263_out, OP1);
  not not_264 (not_264_out, OP0);
  not not_265 (not_265_out, F5);
  not not_266 (not_266_out, F4);
  not not_267 (not_267_out, F3);
  not not_268 (not_268_out, F2);
  not not_269 (not_269_out, F0);
  not not_270 (not_270_out, OP5);
  not not_271 (not_271_out, OP4);
  not not_272 (not_272_out, OP3);
  not not_273 (not_273_out, OP2);
  not not_274 (not_274_out, OP1);
  not not_275 (not_275_out, OP0);
  not not_276 (not_276_out, F4);
  not not_277 (not_277_out, F3);
  not not_278 (not_278_out, F2);
  not not_279 (not_279_out, F1);
  not not_280 (not_280_out, F0);
  not not_281 (not_281_out, OP5);
  not not_282 (not_282_out, OP4);
  not not_283 (not_283_out, OP3);
  not not_284 (not_284_out, OP2);
  not not_285 (not_285_out, OP1);
  not not_286 (not_286_out, OP0);
  not not_287 (not_287_out, F4);
  not not_288 (not_288_out, F3);
  not not_289 (not_289_out, F2);
  not not_290 (not_290_out, F1);
  not not_291 (not_291_out, OP5);
  not not_292 (not_292_out, OP4);
  not not_293 (not_293_out, OP3);
  not not_294 (not_294_out, OP2);
  not not_295 (not_295_out, OP1);
  not not_296 (not_296_out, OP0);
  not not_297 (not_297_out, F4);
  not not_298 (not_298_out, F3);
  not not_299 (not_299_out, F2);
  not not_300 (not_300_out, F0);
  not not_301 (not_301_out, OP5);
  not not_302 (not_302_out, OP4);
  not not_303 (not_303_out, OP3);
  not not_304 (not_304_out, OP2);
  not not_305 (not_305_out, OP1);
  not not_306 (not_306_out, OP0);
  not not_307 (not_307_out, F4);
  not not_308 (not_308_out, F3);
  not not_309 (not_309_out, F1);
  not not_310 (not_310_out, F0);
  not not_311 (not_311_out, OP5);
  not not_312 (not_312_out, OP4);
  not not_313 (not_313_out, OP3);
  not not_314 (not_314_out, OP2);
  not not_315 (not_315_out, OP1);
  not not_316 (not_316_out, OP0);
  not not_317 (not_317_out, F4);
  not not_318 (not_318_out, F3);
  not not_319 (not_319_out, F1);
  not not_320 (not_320_out, OP5);
  not not_321 (not_321_out, OP4);
  not not_322 (not_322_out, OP3);
  not not_323 (not_323_out, OP2);
  not not_324 (not_324_out, OP1);
  not not_325 (not_325_out, OP0);
  not not_326 (not_326_out, F4);
  not not_327 (not_327_out, F3);
  not not_328 (not_328_out, OP5);
  not not_329 (not_329_out, OP4);
  not not_330 (not_330_out, OP3);
  not not_331 (not_331_out, OP2);
  not not_332 (not_332_out, OP1);
  not not_333 (not_333_out, OP0);
  not not_334 (not_334_out, F4);
  not not_335 (not_335_out, F2);
  not not_336 (not_336_out, F0);
  not not_337 (not_337_out, OP5);
  not not_338 (not_338_out, OP4);
  not not_339 (not_339_out, OP3);
  not not_340 (not_340_out, OP2);
  not not_341 (not_341_out, OP1);
  not not_342 (not_342_out, OP0);
  not not_343 (not_343_out, F4);
  not not_344 (not_344_out, F2);
  not not_345 (not_345_out, OP5);
  not not_346 (not_346_out, OP4);
  not not_347 (not_347_out, OP3);
  not not_348 (not_348_out, OP2);
  not not_349 (not_349_out, OP1);
  not not_350 (not_350_out, OP0);
  not not_351 (not_351_out, F5);
  not not_352 (not_352_out, F4);
  not not_353 (not_353_out, F3);
  not not_354 (not_354_out, F1);
  not not_355 (not_355_out, F0);
  not not_356 (not_356_out, OP5);
  not not_357 (not_357_out, OP4);
  not not_358 (not_358_out, OP3);
  not not_359 (not_359_out, OP1);
  not not_360 (not_360_out, OP0);
  not not_361 (not_361_out, OP5);
  not not_362 (not_362_out, OP4);
  not not_363 (not_363_out, OP3);
  not not_364 (not_364_out, OP1);
  not not_365 (not_365_out, OP5);
  not not_366 (not_366_out, OP4);
  not not_367 (not_367_out, OP3);
  not not_368 (not_368_out, OP2);
  not not_369 (not_369_out, OP1);
  not not_370 (not_370_out, OP0);
  not not_371 (not_371_out, F5);
  not not_372 (not_372_out, F4);
  not not_373 (not_373_out, F2);
  not not_374 (not_374_out, F1);
  not not_375 (not_375_out, F0);
  not not_376 (not_376_out, OP5);
  not not_377 (not_377_out, OP4);
  not not_378 (not_378_out, OP3);
  not not_379 (not_379_out, OP2);
  not not_380 (not_380_out, OP1);
  not not_381 (not_381_out, OP0);
  not not_382 (not_382_out, F5);
  not not_383 (not_383_out, F4);
  not not_384 (not_384_out, F2);
  not not_385 (not_385_out, F1);
  not not_386 (not_386_out, F0);
  not not_387 (not_387_out, OP5);
  not not_388 (not_388_out, OP4);
  not not_389 (not_389_out, OP3);
  not not_390 (not_390_out, OP2);
  not not_391 (not_391_out, OP0);
  not not_392 (not_392_out, OP5);
  not not_393 (not_393_out, OP4);
  not not_394 (not_394_out, OP3);
  not not_395 (not_395_out, OP2);
  not not_396 (not_396_out, OP5);
  not not_397 (not_397_out, OP4);
  not not_398 (not_398_out, OP3);
  not not_399 (not_399_out, OP2);
  and and_1 (and_1_out, OP5, not_1_out, not_2_out, not_3_out, OP1, OP0);
  and and_2 (and_2_out, OP5, not_4_out, not_5_out, not_6_out, not_7_out, OP0);
  and and_3 (MemWrite, OP5, not_8_out, OP3, not_9_out, OP1, OP0);
  and and_4 (and_4_out, not_10_out, not_11_out, OP3, not_12_out, not_13_out, not_14_out);
  and and_5 (and_5_out, not_15_out, not_16_out, OP3, OP2, not_17_out, not_18_out);
  and and_6 (and_6_out, not_19_out, not_20_out, OP3, not_21_out, not_22_out, OP0);
  and and_7 (and_7_out, not_23_out, not_24_out, OP3, not_25_out, OP1, not_26_out);
  and and_8 (and_8_out, not_27_out, not_28_out, OP3, OP2, not_29_out, OP0);
  and and_9 (and_9_out, OP5, not_30_out, not_31_out, not_32_out, OP1, OP0);
  and and_10 (and_10_out, OP5, not_33_out, OP3, not_34_out, OP1, OP0);
  and and_11 (and_11_out, OP5, not_35_out, not_36_out, not_37_out, not_38_out, OP0);
  and and_12 (and_12_out, not_39_out, not_40_out, not_41_out, not_42_out, not_43_out, not_44_out, not_45_out, not_46_out, not_47_out, not_48_out, not_49_out, not_50_out);
  and and_13 (and_13_out, not_51_out, not_52_out, not_53_out, not_54_out, not_55_out, not_56_out, not_57_out, not_58_out, not_59_out, not_60_out, F1, F0);
  and and_14 (and_14_out, not_61_out, not_62_out, not_63_out, not_64_out, not_65_out, not_66_out, not_67_out, not_68_out, not_69_out, not_70_out, F1, not_71_out);
  and and_15 (and_15_out, not_72_out, not_73_out, not_74_out, not_75_out, not_76_out, not_77_out, F5, not_78_out, not_79_out, not_80_out, not_81_out, not_82_out);
  and and_16 (and_16_out, not_83_out, not_84_out, not_85_out, not_86_out, not_87_out, not_88_out, F5, not_89_out, not_90_out, not_91_out, not_92_out, F0);
  and and_17 (and_17_out, not_93_out, not_94_out, not_95_out, not_96_out, not_97_out, not_98_out, F5, not_99_out, not_100_out, not_101_out, F1, not_102_out);
  and and_18 (and_18_out, not_103_out, not_104_out, not_105_out, not_106_out, not_107_out, not_108_out, F5, not_109_out, not_110_out, F2, not_111_out, not_112_out);
  and and_19 (and_19_out, not_113_out, not_114_out, not_115_out, not_116_out, not_117_out, not_118_out, F5, not_119_out, not_120_out, F2, not_121_out, F0);
  and and_20 (and_20_out, not_122_out, not_123_out, not_124_out, not_125_out, not_126_out, not_127_out, F5, not_128_out, not_129_out, F2, F1, F0);
  and and_21 (and_21_out, not_130_out, not_131_out, not_132_out, not_133_out, not_134_out, not_135_out, F5, not_136_out, F3, not_137_out, F1, not_138_out);
  and and_22 (and_22_out, not_139_out, not_140_out, not_141_out, not_142_out, not_143_out, not_144_out, F5, not_145_out, F3, not_146_out, F1, F0);
  and and_23 (and_23_out, not_147_out, not_148_out, not_149_out, not_150_out, OP1, OP0);
  and and_24 (and_24_out, not_151_out, not_152_out, OP3, not_153_out, not_154_out, not_155_out);
  and and_25 (and_25_out, not_156_out, not_157_out, OP3, OP2, not_158_out, not_159_out);
  and and_26 (and_26_out, not_160_out, not_161_out, OP3, not_162_out, not_163_out, OP0);
  and and_27 (and_27_out, not_164_out, not_165_out, OP3, not_166_out, OP1, not_167_out);
  and and_28 (and_28_out, not_168_out, not_169_out, OP3, OP2, not_170_out, OP0);
  and and_29 (and_29_out, OP5, not_171_out, not_172_out, not_173_out, OP1, OP0);
  and and_30 (and_30_out, not_174_out, not_175_out, not_176_out, not_177_out, not_178_out, not_179_out, not_180_out, not_181_out, not_182_out, F2, not_183_out, not_184_out);
  and and_31 (and_31_out, not_185_out, not_186_out, OP3, OP2, OP1, OP0);
  and and_32 (and_32_out, OP5, not_187_out, not_188_out, not_189_out, not_190_out, OP0);
  and and_33 (SysCALL, not_191_out, not_192_out, not_193_out, not_194_out, not_195_out, not_196_out, not_197_out, not_198_out, F3, F2, not_199_out, not_200_out);
  and and_34 (and_34_out, not_201_out, not_202_out, not_203_out, OP2, not_204_out, not_205_out);
  and and_35 (and_35_out, not_206_out, not_207_out, not_208_out, OP2, not_209_out, OP0);
  and and_36 (and_36_out, not_210_out, not_211_out, OP3, not_212_out, not_213_out, not_214_out);
  and and_37 (and_37_out, not_215_out, not_216_out, OP3, not_217_out, not_218_out, OP0);
  and and_38 (and_38_out, not_219_out, not_220_out, OP3, not_221_out, OP1, not_222_out);
  and and_39 (and_39_out, OP5, not_223_out, not_224_out, not_225_out, OP1, OP0);
  and and_40 (and_40_out, OP5, not_226_out, OP3, not_227_out, OP1, OP0);
  and and_41 (and_41_out, OP5, not_228_out, not_229_out, not_230_out, not_231_out, OP0);
  and and_42 (and_42_out, not_232_out, not_233_out, not_234_out, not_235_out, not_236_out, OP0);
  and and_43 (and_43_out, not_237_out, not_238_out, not_239_out, not_240_out, not_241_out, not_242_out, not_243_out, not_244_out, not_245_out, not_246_out, not_247_out, not_248_out);
  and and_44 (and_44_out, not_249_out, not_250_out, not_251_out, not_252_out, not_253_out, not_254_out, not_255_out, not_256_out, not_257_out, not_258_out, F1, F0);
  and and_45 (and_45_out, not_259_out, not_260_out, not_261_out, not_262_out, not_263_out, not_264_out, not_265_out, not_266_out, not_267_out, not_268_out, F1, not_269_out);
  and and_46 (and_46_out, not_270_out, not_271_out, not_272_out, not_273_out, not_274_out, not_275_out, F5, not_276_out, not_277_out, not_278_out, not_279_out, not_280_out);
  and and_47 (and_47_out, not_281_out, not_282_out, not_283_out, not_284_out, not_285_out, not_286_out, F5, not_287_out, not_288_out, not_289_out, not_290_out, F0);
  and and_48 (and_48_out, not_291_out, not_292_out, not_293_out, not_294_out, not_295_out, not_296_out, F5, not_297_out, not_298_out, not_299_out, F1, not_300_out);
  and and_49 (and_49_out, not_301_out, not_302_out, not_303_out, not_304_out, not_305_out, not_306_out, F5, not_307_out, not_308_out, F2, not_309_out, not_310_out);
  and and_50 (and_50_out, not_311_out, not_312_out, not_313_out, not_314_out, not_315_out, not_316_out, F5, not_317_out, not_318_out, F2, not_319_out, F0);
  and and_51 (and_51_out, not_320_out, not_321_out, not_322_out, not_323_out, not_324_out, not_325_out, F5, not_326_out, not_327_out, F2, F1, F0);
  and and_52 (and_52_out, not_328_out, not_329_out, not_330_out, not_331_out, not_332_out, not_333_out, F5, not_334_out, F3, not_335_out, F1, not_336_out);
  and and_53 (and_53_out, not_337_out, not_338_out, not_339_out, not_340_out, not_341_out, not_342_out, F5, not_343_out, F3, not_344_out, F1, F0);
  and and_54 (and_54_out, not_345_out, not_346_out, not_347_out, not_348_out, not_349_out, not_350_out, not_351_out, not_352_out, not_353_out, F2, not_354_out, not_355_out);
  and and_55 (BEQ, not_356_out, not_357_out, not_358_out, OP2, not_359_out, not_360_out);
  and and_56 (BNE, not_361_out, not_362_out, not_363_out, OP2, not_364_out, OP0);
  and and_57 (JR, not_365_out, not_366_out, not_367_out, not_368_out, not_369_out, not_370_out, not_371_out, not_372_out, F3, not_373_out, not_374_out, not_375_out);
  and and_58 (and_58_out, not_376_out, not_377_out, not_378_out, not_379_out, not_380_out, not_381_out, not_382_out, not_383_out, F3, not_384_out, not_385_out, not_386_out);
  and and_59 (and_59_out, not_387_out, not_388_out, not_389_out, not_390_out, OP1, not_391_out);
  and and_60 (and_60_out, not_392_out, not_393_out, not_394_out, not_395_out, OP1, OP0);
  and and_61 (JAL, not_396_out, not_397_out, not_398_out, not_399_out, OP1, OP0);
  or or_1 (MemToReg, and_1_out, and_2_out);
  or or_2 (ALU_SRC, and_4_out, and_5_out, and_6_out, and_7_out, and_8_out, and_9_out, and_10_out, and_11_out);
  or or_3 (SignedExt, and_34_out, and_35_out, and_36_out, and_37_out, and_38_out, and_39_out, and_40_out, and_41_out, and_42_out);
  or or_4 (JMP, and_58_out, and_59_out, and_60_out);
  or or_5 (RegWrite, and_12_out, and_13_out, and_14_out, and_15_out, and_16_out, and_17_out, and_18_out, and_19_out, and_20_out, and_21_out, and_22_out, and_23_out, and_24_out, and_25_out, and_26_out, and_27_out, and_28_out, and_29_out, and_30_out, and_31_out, and_32_out);
  or or_6 (RegDst, and_43_out, and_44_out, and_45_out, and_46_out, and_47_out, and_48_out, and_49_out, and_50_out, and_51_out, and_52_out, and_53_out, and_54_out);
endmodule

module \W_计算  (
  input  EX_RegDst,
  input  MEM_RegDst,
  input  [31:0] EX_IR,
  input  WB_RegDst,
  input  EX_Jal,
  input  [31:0] MEM_IR,
  input  MEM_Jal,
  input  WB_Jal,
  input  [31:0] WB_IR,
  output [4:0] EX_W_num,
  output [4:0] MEM_W_num,
  output [4:0] WB_W_num
);

  wire [4:0] multiplexer_1_out, multiplexer_2_out, multiplexer_3_out;

  Multiplexer #(.width(5), .enable("false")) multiplexer_1 (
    .in0(EX_IR[20:16]), .in1(EX_IR[15:11]), .out(multiplexer_1_out), .sel(EX_RegDst));
  Multiplexer #(.width(5), .enable("false")) multiplexer_2 (
    .in0(MEM_IR[20:16]), .in1(MEM_IR[15:11]), .out(multiplexer_2_out), .sel(MEM_RegDst));
  Multiplexer #(.width(5), .enable("false")) multiplexer_3 (
    .in0(WB_IR[20:16]), .in1(WB_IR[15:11]), .out(multiplexer_3_out), .sel(WB_RegDst));
  Multiplexer #(.width(5), .enable("false")) multiplexer_4 (
    .in0(multiplexer_1_out), .in1({5{1'b1}}), .out(EX_W_num), .sel(EX_Jal));
  Multiplexer #(.width(5), .enable("false")) multiplexer_5 (
    .in0(multiplexer_2_out), .in1({5{1'b1}}), .out(MEM_W_num), .sel(MEM_Jal));
  Multiplexer #(.width(5), .enable("false")) multiplexer_6 (
    .in0(multiplexer_3_out), .in1({5{1'b1}}), .out(WB_W_num), .sel(WB_Jal));

  // Notes on the sheet:
  //   rt
  //   rd
  //   rt
  //   rd
  //   rt
  //   rd
endmodule

module \Din计算  (
  input  [31:0] MemData,
  input  [31:0] WB_R2,
  input  [31:0] Result,
  input  [31:0] WB_R1,
  input  [31:0] WB_PC,
  input  [15:0] WB_imm,
  input  MemToReg,
  input  WB_Jal,
  input  WB_LUI,
  input  WB_Sllv,
  input  HB,
  output [31:0] Din
);

  wire [15:0] multiplexer_4_out;
  wire [31:0] multiplexer_1_out, multiplexer_2_out, multiplexer_3_out, multiplexer_5_out, PC, \半字 , \可变左移 ;

  Multiplexer #(.width(32), .enable("false")) multiplexer_1 (
    .in0(MemData), .in1(\半字 ), .out(multiplexer_1_out), .sel(HB));
  Shifter #(.width(32)) shifter_1 (.in(WB_R2), .\dist (WB_R1[4:0]), .out(\可变左移 ));
  Multiplexer #(.width(32), .enable("false")) multiplexer_2 (
    .in0(Result), .in1(multiplexer_1_out), .out(multiplexer_2_out), .sel(MemToReg));
  Multiplexer #(.width(32), .enable("false")) multiplexer_3 (
    .in0(multiplexer_2_out), .in1(PC), .out(multiplexer_3_out), .sel(WB_Jal));
  Multiplexer #(.width(16), .enable("false")) multiplexer_4 (
    .in0(MemData[15:0]), .in1(MemData[31:16]), .out(multiplexer_4_out), .sel(Result[1]));
  assign \半字  = {{16{multiplexer_4_out[15]}}, multiplexer_4_out};  // Bit_Extender bit_extender_1
  Multiplexer #(.width(32), .enable("false")) multiplexer_5 (
    .in0(multiplexer_3_out), .in1({WB_imm, {16{1'b0}}}), .out(multiplexer_5_out), .sel(WB_LUI));
  Multiplexer #(.width(32), .enable("false")) multiplexer_6 (
    .in0(multiplexer_5_out), .in1(\可变左移 ), .out(Din), .sel(WB_Sllv));
  Adder #(.width(32)) adder_1 (.a(WB_PC), .b(32'h4), .out(PC));  // open: cin, cout
endmodule

module \重定向控制器  (
  input  [5:0] OP,
  input  [4:0] EX_WriteReg_num,
  input  EX_RegWrite,
  input  [15:0] WB_imm,
  input  [4:0] MEM_WriteReg_num,
  input  MEM_RegWrite,
  input  [5:0] Func,
  input  [15:0] Mem_imm,
  input  [4:0] ID_R1_num,
  input  [4:0] ID_R2_num,
  input  EX_MemToReg,
  input  Mem_MemToReg,
  input  [31:0] WB_MemData,
  input  [31:0] Mem_R1,
  input  [31:0] WB_R1,
  input  [31:0] WB_Result,
  input  [31:0] Mem_Result,
  input  [31:0] Mem_R2,
  input  [31:0] WB_R2,
  input  Mem_LUI,
  input  Mem_Sllv,
  input  WB_LUI,
  input  WB_Sllv,
  input  WB_MemToReg,
  input  WB_HB,
  output [1:0] ForwardA,
  output [1:0] ForwardB,
  output Load_Use,
  output [31:0] Result1,
  output [31:0] Result2,
  output [31:0] MemData
);

  wire and_8_out, and_9_out, comparator_1_eq, comparator_2_eq, comparator_3_eq, comparator_4_eq,
       comparator_5_eq, comparator_6_eq, \EX_数据相关1 , \EX_数据相关2 , Mem_ResultA, Mem_ResultB, \Mem_数据相关1 ,
       \Mem_数据相关2 , R1_EX, R1_MEM, R1_Used, R2_EX, R2_MEM, R2_Used, WB_MemdataA, WB_MemdataB, WB_ResultA,
       WB_ResultB;
  wire [15:0] multiplexer_5_out;
  wire [31:0] \Mem_左移 , multiplexer_1_out, multiplexer_3_out, multiplexer_7_out, \WB_左移 , \半字 ;

  \源寄存器使用情况  \u_源寄存器使用情况_1  (
    .OP0(OP[0]), .OP1(OP[1]), .OP2(OP[2]), .OP3(OP[3]), .OP4(OP[4]), .OP5(OP[5]), .F0(Func[0]), .F1(Func[1]),
    .F2(Func[2]), .F3(Func[3]), .F4(Func[4]), .F5(Func[5]), .R1_Used(R1_Used), .R2_Used(R2_Used));
  Comparator #(.width(5)) comparator_1 (.a(ID_R1_num), .b(EX_WriteReg_num), .eq(comparator_1_eq));  // open: gt, lt
  Comparator #(.width(5)) comparator_2 (.a(ID_R1_num), .b(MEM_WriteReg_num), .eq(comparator_2_eq));  // open: gt, lt
  Comparator #(.width(5)) comparator_3 (.a(ID_R2_num), .b(EX_WriteReg_num), .eq(comparator_3_eq));  // open: gt, lt
  Comparator #(.width(5)) comparator_4 (.a(ID_R2_num), .b(MEM_WriteReg_num), .eq(comparator_4_eq));  // open: gt, lt
  Comparator #(.width(5)) comparator_5 (.a(EX_WriteReg_num), .b({5{1'b0}}), .eq(comparator_5_eq));  // open: gt, lt
  Comparator #(.width(5)) comparator_6 (.a(MEM_WriteReg_num), .b({5{1'b0}}), .eq(comparator_6_eq));  // open: gt, lt
  or or_1 (ForwardA[0], Mem_ResultA, WB_MemdataA);
  or or_2 (ForwardA[1], WB_ResultA, Mem_ResultA);
  or or_3 (ForwardB[0], Mem_ResultB, WB_MemdataB);
  or or_4 (ForwardB[1], WB_ResultB, Mem_ResultB);
  and and_1 (R1_EX, comparator_1_eq, ~comparator_5_eq);  // AND_Gate
  and and_2 (R1_MEM, comparator_2_eq, ~comparator_6_eq);  // AND_Gate
  and and_3 (R2_EX, comparator_3_eq, ~comparator_5_eq);  // AND_Gate
  and and_4 (R2_MEM, comparator_4_eq, ~comparator_6_eq);  // AND_Gate
  and and_5 (Mem_ResultA, \EX_数据相关1 , ~Load_Use);  // AND_Gate
  and and_6 (WB_ResultA, ~Mem_ResultA, \Mem_数据相关1 , ~Mem_MemToReg);  // AND_Gate
  and and_7 (WB_MemdataA, ~Mem_ResultA, \Mem_数据相关1 , Mem_MemToReg);  // AND_Gate
  and and_8 (and_8_out, R1_Used, EX_MemToReg, R1_EX);
  and and_9 (and_9_out, R2_Used, EX_MemToReg, R2_EX);
  or or_5 (Load_Use, and_8_out, and_9_out);
  and and_10 (\EX_数据相关1 , R1_Used, EX_RegWrite, R1_EX);
  and and_11 (\Mem_数据相关1 , R1_Used, MEM_RegWrite, R1_MEM);
  and and_12 (\Mem_数据相关2 , R2_Used, MEM_RegWrite, R2_MEM);
  and and_13 (\EX_数据相关2 , R2_Used, EX_RegWrite, R2_EX);
  and and_14 (Mem_ResultB, \EX_数据相关2 , ~Load_Use);  // AND_Gate
  and and_15 (WB_ResultB, ~Mem_ResultB, \Mem_数据相关2 , ~Mem_MemToReg);  // AND_Gate
  and and_16 (WB_MemdataB, ~Mem_ResultB, \Mem_数据相关2 , Mem_MemToReg);  // AND_Gate
  Shifter #(.width(32)) shifter_1 (.in(Mem_R2), .\dist (Mem_R1[4:0]), .out(\Mem_左移 ));
  Shifter #(.width(32)) shifter_2 (.in(WB_R2), .\dist (WB_R1[4:0]), .out(\WB_左移 ));
  Multiplexer #(.width(32), .enable("false")) multiplexer_1 (
    .in0(Mem_Result), .in1({Mem_imm, {16{1'b0}}}), .out(multiplexer_1_out), .sel(Mem_LUI));
  Multiplexer #(.width(32), .enable("false")) multiplexer_2 (
    .in0(multiplexer_1_out), .in1(\Mem_左移 ), .out(Result1), .sel(Mem_Sllv));
  Multiplexer #(.width(32), .enable("false")) multiplexer_3 (
    .in0(WB_Result), .in1({WB_imm, {16{1'b0}}}), .out(multiplexer_3_out), .sel(WB_LUI));
  Multiplexer #(.width(32), .enable("false")) multiplexer_4 (
    .in0(multiplexer_3_out), .in1(\WB_左移 ), .out(Result2), .sel(WB_Sllv));
  Multiplexer #(.width(16), .enable("false")) multiplexer_5 (
    .in0(WB_MemData[15:0]), .in1(WB_MemData[31:16]), .out(multiplexer_5_out), .sel(WB_Result[1]));
  Multiplexer #(.width(32), .enable("false")) multiplexer_6 (
    .in0(WB_Result), .in1(multiplexer_7_out), .out(MemData), .sel(WB_MemToReg));
  Multiplexer #(.width(32), .enable("false")) multiplexer_7 (
    .in0(WB_MemData), .in1(\半字 ), .out(multiplexer_7_out), .sel(WB_HB));
  assign \半字  = {{16{multiplexer_5_out[15]}}, multiplexer_5_out};  // Bit_Extender bit_extender_1

  // Other names for the same wires on the sheet: OP_CODE[5:0] = OP
endmodule

module \分支预测流水线  (
);

  wire and_1_out, and_2_out, and_3_out, and_4_out, and_5_out, and_6_out, and_7_out, and_8_out, and_9_out,
       and_10_out, and_11_out, and_12_out, and_17_out, and_18_out, Beq, BLTZ, BLTZ_in, Bne, CLK,
       comparator_1_eq, comparator_2_eq, d_ff_1_q, en, equal, EX_Jal, ex_mem_1_bltz, ex_mem_1_hb,
       ex_mem_1_memwrite, \ex_mem_1_传输状态out_表明当前传输数据有效 , EX_MtoR, EX_RegDst, EX_RegWrite, Go, HB, HB_in, Hit,
       Hit2, id_ex_1_alusrcb, id_ex_1_hb, id_ex_1_lui, id_ex_1_memwrite, id_ex_1_sllv,
       \id_ex_1_传输状态out_表明当前传输数据有效 , \if_id_1_传输状态out_表明当前传输数据有效 , IR1, IR2, IR3, JMP, JMP_in, JR, JR_in,
       Load_Use, LUI, LUI_in, MEM_Jal, Mem_LUI, MEM_MtoR, MEM_RegDst, MEM_RegWrite, Mem_SLLV, MemToReg,
       nand_1_out, nor_1_out, not_1_out, not_2_out, or_2_out, or_4_out, or_5_out, or_10_out, out, pause,
       \PC使能 , RegWrite, RST, SignedExt, SignedExt_in, SLLV, SLLV_in, Syscall, W1, W2, W3, WB_Jal, WB_RegDst,
       \写入 , \显示 , \暂停 , \有条件跳转 , \气泡 , \硬布线控制器_1_alu_src , \硬布线控制器_1_beq , \硬布线控制器_1_bne , \硬布线控制器_1_jal ,
       \硬布线控制器_1_memtoreg , \硬布线控制器_1_memwrite , \硬布线控制器_1_regdst , \硬布线控制器_1_regwrite , \结束 , \继续运行 , \跳转 ,
       \错误 , \预测位写入 ;
  wire [1:0] EX_fr, FordA, FordB, id_ex_1_forwarda, id_ex_1_forwardb, \if_id_1_预测位 , PCsrc, \历史预测位 , \预测位 ;
  wire [3:0] id_ex_1_aluop, \硬布线控制器_1_alu_op ;
  wire [4:0] EX_W_num, ID_R1, ID_R2, MEM_W_num, WB_W_num;
  wire [5:0] Func, OP;
  wire [15:0] \LoadUse次数 , Mem_imm, WB_imm, \总周期数 , \插入气泡数 , \无条件分支数 , \条件分支成功数 , \跳转错误数 , \跳转错误数2 ;
  wire [25:6] if_id_1_ir;
  wire [31:0] bit_extender_1_out, bit_extender_2_out, Din, EX_IR, EX_PC, EX_Result, id_ex_1_r2, ID_PC, IF_PC,
       LedData, MEM_PC, Mem_R1, Mem_R2, Mem_Result, MemData, multiplexer_2_out, multiplexer_6_out,
       multiplexer_7_out, multiplexer_8_out, multiplexer_9_out, multiplexer_10_out, PC, PC0, PC2, PC3, R1,
       R2, ram_1_data, Result, Result1, rom_1_data, shifter_1_out, WB_MemData, WB_PC, WB_R1, WB_R2,
       WB_Result, \最终PC , \目标地址 , \立即数扩展 , \预测PC ;
  wire [31:16] MEM_IR, WB_IR;

  Button \u_总复位  (.out(RST));
  Button _1 (.out(IR1));
  Button _2 (.out(IR2));
  Button _3 (.out(IR3));
  Button \u_继续运行  (.out(Go));
  LED led_1 (.in(W1));
  LED led_2 (.in(W2));
  LED led_3 (.in(W3));
  nand nand_1 (nand_1_out, Syscall, ~out);  // NAND_Gate
  and and_1 (and_1_out, \跳转 , \错误 );
  // Probe on EX_PC
  Hex_Digit_Display hex_digit_display_1 (.value(LedData[31:28]));  // open: dp
  Counter #(.width(16), .max('hffff)) counter_1 (
    .count(nand_1_out), .Q(\总周期数 ), .clk(CLK), .clr(RST));  // open: load, D, carry
  Counter #(.width(16), .max('hffff)) counter_2 (
    .count(and_1_out), .Q(\跳转错误数2 ), .clk(CLK), .clr(RST));  // open: load, D, carry
  Multiplexer #(.select(2), .width(32), .enable("false")) multiplexer_1 (
    .in0(PC0), .in1({PC[31:28], EX_IR[25:0], 2'b00}), .in2(PC2), .in3(PC3), .out(\目标地址 ), .sel(PCsrc));
  // Probe on \目标地址 [11:2]
  // Probe on \预测位 
  \分支预测状态机  \u_分支预测状态机_1  (.fr(EX_fr), .fr_2(\预测位 ), .success(\跳转 ), .\跳转错误 (\错误 ), .\预测位写入 (\预测位写入 ), .\写入 (\写入 ));
  // Probe on EX_fr
  and and_2 (and_2_out, Go, ~\结束 );  // AND_Gate
  Hex_Digit_Display hex_digit_display_2 (.value(LedData[27:24]));  // open: dp
  Hex_Digit_Display hex_digit_display_3 (.value(LedData[23:20]));  // open: dp
  Cache cache_1 (
    .\读入PC (IF_PC), .\预测位写入 (\预测位写入 ), .CLK(CLK), .\预测位 (\预测位 ), .Hit(Hit), .\历史预测位 (\历史预测位 ),
    .DataOut(\预测PC ), .\目标地址 (\目标地址 ), .\写入PC (EX_PC), .\写入 (\写入 ), .Hit2(Hit2));
  Adder #(.width(32)) adder_1 (.a(IF_PC), .b(32'h4), .out(PC0));  // open: cin, cout
  Adder #(.width(32)) adder_2 (.a(EX_PC), .b(32'h4), .out(PC));  // open: cin, cout
  Shifter #(.width(32)) shifter_1 (.in(\立即数扩展 ), .\dist (5'b00010), .out(shifter_1_out));
  and and_3 (and_3_out, equal, Beq);
  and and_4 (and_4_out, Bne, ~equal);  // AND_Gate
  D_Flip_Flop d_ff_1 (.clk(CLK), .D(and_2_out), .Q(d_ff_1_q), .en(1'b1), .reset(RST));  // open: Qn, preset
  Hex_Digit_Display hex_digit_display_4 (.value(LedData[19:16]));  // open: dp
  Hex_Digit_Display hex_digit_display_5 (.value(LedData[15:12]));  // open: dp
  Counter #(.width(16), .max('hffff)) counter_3 (
    .count(JMP), .Q(\无条件分支数 ), .clk(CLK), .clr(RST));  // open: load, D, carry
  Counter #(.width(16), .max('hffff)) counter_4 (
    .count(\错误 ), .Q(\跳转错误数 ), .clk(CLK), .clr(RST));  // open: load, D, carry
  Register #(.width(32)) u_PC (.D(\最终PC ), .en(\PC使能 ), .Q(IF_PC), .clk(CLK), .clr(RST));
  // Probe on EX_IR[25:0]
  Adder #(.width(32)) adder_3 (.a(shifter_1_out), .b(PC), .out(PC3));  // open: cin, cout
  or or_1 (\有条件跳转 , and_3_out, and_4_out, and_5_out);
  and and_5 (and_5_out, BLTZ, EX_Result[0]);
  and and_6 (and_6_out, \暂停 , d_ff_1_q);
  or or_2 (or_2_out, and_7_out, nor_1_out);
  nor nor_1 (nor_1_out, pause, Load_Use);
  and and_7 (and_7_out, ~pause, \错误 );  // AND_Gate
  Hex_Digit_Display hex_digit_display_6 (.value(LedData[7:4]));  // open: dp
  Hex_Digit_Display hex_digit_display_7 (.value(LedData[11:8]));  // open: dp
  Clock clock_1 (.out(CLK));
  // Probe on IF_PC[11:2]
  or or_3 (\PC使能 , and_6_out, or_2_out);
  Hex_Digit_Display hex_digit_display_8 (.value(LedData[3:0]));  // open: dp
  Counter #(.width(16), .max('hffff)) counter_5 (
    .count(\有条件跳转 ), .Q(\条件分支成功数 ), .clk(CLK), .clr(RST));  // open: load, D, carry
  Counter #(.width(16), .max('hffff)) counter_6 (
    .count(Load_Use), .Q(\LoadUse次数 ), .clk(CLK), .clr(RST));  // open: load, D, carry
  and and_8 (and_8_out, en, ~RST);  // AND_Gate
  // Probe on \跳转错误数 
  ROM #(.addrWidth(10), .dataWidth(32)) rom_1 (.addr(IF_PC[11:2]), .data(rom_1_data), .sel(1'b1));
  or or_4 (or_4_out, and_8_out, Load_Use);
  and and_9 (and_9_out, Hit2, \历史预测位 [1]);
  Multiplexer #(.width(32), .enable("false")) multiplexer_2 (
    .in0(PC0), .in1(\预测PC ), .out(multiplexer_2_out), .sel(and_9_out));
  // Probe on \总周期数 
  // Probe on \无条件分支数 
  // Probe on \条件分支成功数 
  // Probe on \插入气泡数 
  // Probe on \LoadUse次数 
  or or_5 (or_5_out, RST, \错误 );
  IF_ID if_id_1 (
    .CLK(CLK), .EN(and_10_out), .RST(or_5_out), .PC_in(IF_PC), .PC(ID_PC), .IR_in(rom_1_data),
    .IR({OP, if_id_1_ir, Func}), .\传输状态In_表明当前传输数据有效 (not_1_out),
    .\传输状态Out_表明当前传输数据有效 (\if_id_1_传输状态out_表明当前传输数据有效 ), .\数据有效 (\气泡 ), .\预测位_in (\历史预测位 ),
    .\预测位 (\if_id_1_预测位 ));
  not not_1 (not_1_out, and_8_out);
  and and_10 (and_10_out, or_4_out, ~\错误 );  // AND_Gate
  not not_2 (not_2_out, JR);
  or or_6 (PCsrc[1], JR, \有条件跳转 );
  or or_7 (\跳转 , JR, JMP, \有条件跳转 );
  // Probe on IF_PC[11:2]
  // Probe on \跳转错误数2 
  // Probe on \最终PC [11:2]
  Multiplexer #(.select(2), .width(32), .enable("false")) multiplexer_3 (
    .in0(multiplexer_2_out), .in1(multiplexer_2_out), .in2(PC), .in3(\目标地址 ), .out(\最终PC ), .sel({\错误 , \跳转 }));
  and and_11 (and_11_out, JMP, not_2_out);
  // Probe on ID_PC[11:2]
  // Probe on EX_PC[11:2]
  or or_8 (\气泡 , \错误 , pause, Load_Use);
  or or_9 (PCsrc[0], and_11_out, \有条件跳转 );
  // Probe on MEM_PC[11:2]
  // Probe on EX_PC[11:2]
  // Probe on R1
  \硬布线控制器  \u_硬布线控制器_1  (
    .Func(Func), .OP(OP), .ALU_OP(\硬布线控制器_1_alu_op ), .MemToReg(\硬布线控制器_1_memtoreg ),
    .MemWrite(\硬布线控制器_1_memwrite ), .ALU_SRC(\硬布线控制器_1_alu_src ), .RegWrite(\硬布线控制器_1_regwrite ),
    .SysCALL(Syscall), .SignedExt(SignedExt_in), .RegDst(\硬布线控制器_1_regdst ), .JR(JR_in), .JMP(JMP_in),
    .Beq(\硬布线控制器_1_beq ), .JAL(\硬布线控制器_1_jal ), .Bne(\硬布线控制器_1_bne ), .LUI(LUI_in), .BTLZ(BLTZ_in),
    .HB(HB_in), .SLLV(SLLV_in));
  Multiplexer #(.width(5), .enable("false")) multiplexer_4 (
    .in0(if_id_1_ir[25:21]), .in1(5'b00010), .out(ID_R1), .sel(Syscall));
  Multiplexer #(.width(5), .enable("false")) multiplexer_5 (
    .in0(if_id_1_ir[20:16]), .in1(5'b00100), .out(ID_R2), .sel(Syscall));
  // Probe on WB_PC[11:2]
  MIPS_Regifile mips_regifile_1 (
    .Din(Din), .Clk(CLK), .R1(R1), .R2(R2), .WE(RegWrite), .W_num(WB_W_num), .R1_num(ID_R1), .R2_num(ID_R2));
  // Probe on R2
  or or_10 (or_10_out, \继续运行 , RST, Load_Use, \错误 , \结束 );
  ID_EX id_ex_1 (
    .CLK(CLK), .PC_in(ID_PC), .EN(and_12_out), .IR_in({OP, if_id_1_ir, Func}), .JMP(JMP), .JR(JR),
    .SignedExt(SignedExt), .LUI(id_ex_1_lui), .BLTZ(BLTZ), .HB(id_ex_1_hb), .Sllv(id_ex_1_sllv), .Beq(Beq),
    .Bne(Bne), .MemToReg(EX_MtoR), .MemWrite(id_ex_1_memwrite), .AluOP(id_ex_1_aluop),
    .AluSrcB(id_ex_1_alusrcb), .Jal(EX_Jal), .RegDst(EX_RegDst), .RST(or_10_out), .Beq_in(\硬布线控制器_1_beq ),
    .MemToReg_in(\硬布线控制器_1_memtoreg ), .Bne_in(\硬布线控制器_1_bne ), .MemWrite_in(\硬布线控制器_1_memwrite ),
    .AluOP_in(\硬布线控制器_1_alu_op ), .AluSrcB_in(\硬布线控制器_1_alu_src ), .JR_in(JR_in), .Jal_in(\硬布线控制器_1_jal ),
    .SignedExt_in(SignedExt_in), .LUI_in(LUI_in), .BLTZ_in(BLTZ_in), .HB_in(HB_in), .SLLV_in(SLLV_in),
    .JMP_in(JMP_in), .RegDst_in(\硬布线控制器_1_regdst ), .PC(EX_PC), .IR(EX_IR),
    .\传输状态In_表明当前传输数据有效 (\if_id_1_传输状态out_表明当前传输数据有效 ), .\传输状态Out_表明当前传输数据有效 (\id_ex_1_传输状态out_表明当前传输数据有效 ),
    .R1_in(R1), .R2_in(R2), .R1(PC2), .R2(id_ex_1_r2), .RegWrite_in(\硬布线控制器_1_regwrite ),
    .Regwrite(EX_RegWrite), .\跳转 (\气泡 ), .ForwardA_in(FordA), .ForwardA(id_ex_1_forwarda),
    .ForwardB_in(FordB), .ForwardB(id_ex_1_forwardb), .\预测位_in (\if_id_1_预测位 ), .\预测位 (EX_fr));
  and and_12 (and_12_out, ~\if_id_1_传输状态out_表明当前传输数据有效 , ~en);  // AND_Gate
  Multiplexer #(.select(2), .width(32), .enable("false")) multiplexer_6 (
    .in0(R1), .in1(R1), .in2(Result1), .in3(EX_Result), .out(multiplexer_6_out), .sel(FordA));
  Multiplexer #(.select(2), .width(32), .enable("false")) multiplexer_7 (
    .in0(R2), .in1(R2), .in2(Result1), .in3(EX_Result), .out(multiplexer_7_out), .sel(FordB));
  \W_计算  \w_计算_1  (
    .EX_RegDst(EX_RegDst), .MEM_RegDst(MEM_RegDst), .EX_IR(EX_IR), .WB_RegDst(WB_RegDst), .EX_Jal(EX_Jal),
    .MEM_IR({MEM_IR, Mem_imm}), .MEM_Jal(MEM_Jal), .WB_Jal(WB_Jal), .EX_W_num(EX_W_num),
    .WB_IR({WB_IR, WB_imm}), .MEM_W_num(MEM_W_num), .WB_W_num(WB_W_num));
  // Probe on Result1
  // Probe on Result
  // Probe on MemData
  Comparator #(.width(32)) comparator_1 (.a(multiplexer_6_out), .b(32'ha), .eq(comparator_1_eq));  // open: gt, lt
  Register #(.width(32)) register_1 (.D(multiplexer_7_out), .en(\显示 ), .Q(LedData), .clk(CLK), .clr(RST));
  // Probe on id_ex_1_forwarda
  Multiplexer #(.select(2), .width(32), .enable("false")) multiplexer_8 (
    .in0(PC2), .in1(MemData), .in2(Result), .in3(Result1), .out(multiplexer_8_out), .sel(id_ex_1_forwarda));
  Multiplexer #(.select(2), .width(32), .enable("false")) multiplexer_9 (
    .in0(id_ex_1_r2), .in1(MemData), .in2(Result), .in3(Result1), .out(multiplexer_9_out),
    .sel(id_ex_1_forwardb));
  and and_13 (\结束 , comparator_1_eq, Syscall);
  and and_14 (\显示 , Syscall, comparator_2_eq);
  Comparator #(.width(32)) comparator_2 (.a(multiplexer_6_out), .b(32'h22), .eq(comparator_2_eq));  // open: gt, lt
  Multiplexer #(.width(32), .enable("false")) multiplexer_10 (
    .in0(multiplexer_9_out), .in1(\立即数扩展 ), .out(multiplexer_10_out), .sel(id_ex_1_alusrcb));
  and and_15 (\暂停 , ~\显示 , ~\结束 , Syscall, ~Load_Use);  // AND_Gate
  MIPS_ALU mips_alu_1 (
    .X(multiplexer_8_out), .Y(multiplexer_10_out), .AluOP(id_ex_1_aluop), .Equal(equal), .Result(EX_Result),
    .shamt(EX_IR[10:6]));  // open: Result_2
  or or_11 (pause, \结束 , \暂停 );
  and and_16 (\继续运行 , \暂停 , ~Go);  // AND_Gate
  EX_MEM ex_mem_1 (
    .CLK(CLK), .EN(and_17_out), .RST(RST), .SLLV_in(id_ex_1_sllv), .PC_in(EX_PC), .Jal_in(EX_Jal),
    .Result_in(EX_Result), .MemToReg_in(EX_MtoR), .LUI_in(id_ex_1_lui), .RegDst_in(EX_RegDst),
    .MemWrite_in(id_ex_1_memwrite), .BLTZ_in(BLTZ), .HB_in(id_ex_1_hb), .IR_in(EX_IR),
    .R2_in(multiplexer_9_out), .PC(MEM_PC), .Result(Mem_Result), .IR({MEM_IR, Mem_imm}), .R2(Mem_R2),
    .\传输状态In_表明当前传输数据有效 (\id_ex_1_传输状态out_表明当前传输数据有效 ), .Jal(MEM_Jal), .RegDst(MEM_RegDst), .Sllv(Mem_SLLV),
    .MemToReg(MEM_MtoR), .LUI(Mem_LUI), .HB(ex_mem_1_hb), .MemWrite(ex_mem_1_memwrite), .BLTZ(ex_mem_1_bltz),
    .\传输状态Out_表明当前传输数据有效 (\ex_mem_1_传输状态out_表明当前传输数据有效 ), .RegWrite_in(EX_RegWrite), .Regwrite(MEM_RegWrite),
    .R1_in(multiplexer_8_out), .R1(Mem_R1));  // open: Beq_in, JR_in, Bne_in, JMP_in, Beq, JR, JMP, Bne
  and and_17 (and_17_out, ~\id_ex_1_传输状态out_表明当前传输数据有效 , ~en);  // AND_Gate
  or or_12 (en, \结束 , \继续运行 );
  \Din计算  \din计算_1  (
    .MemData(MemData), .WB_R2(WB_R2), .Result(WB_Result), .WB_R1(WB_R1), .MemToReg(MemToReg),
    .WB_Jal(WB_Jal), .WB_LUI(LUI), .WB_Sllv(SLLV), .HB(HB), .Din(Din), .WB_PC(WB_PC), .WB_imm(WB_imm));
  assign bit_extender_1_out = {{16{1'b0}}, EX_IR[15:0]};  // Bit_Extender bit_extender_1
  assign bit_extender_2_out = {{16{EX_IR[15]}}, EX_IR[15:0]};  // Bit_Extender bit_extender_2
  MEM_WB mem_wb_1 (
    .CLK(CLK), .EN(and_18_out), .RST(RST), .SLLV_in(Mem_SLLV), .PC_in(MEM_PC), .Jal_in(MEM_Jal),
    .Result_in(Mem_Result), .MemToReg_in(MEM_MtoR), .LUI_in(Mem_LUI), .RegDst_in(MEM_RegDst),
    .RegWrite_in(MEM_RegWrite), .BLTZ_in(ex_mem_1_bltz), .HB_in(ex_mem_1_hb), .IR_in({MEM_IR, Mem_imm}),
    .MemData_in(ram_1_data), .PC(WB_PC), .Result(WB_Result), .IR({WB_IR, WB_imm}), .MemData(WB_MemData),
    .\传输状态In_表明当前传输数据有效 (\ex_mem_1_传输状态out_表明当前传输数据有效 ), .Jal(WB_Jal), .RegDst(WB_RegDst), .Sllv(SLLV),
    .MemToReg(MemToReg), .LUI(LUI), .HB(HB), .Regwrite(RegWrite), .\传输状态Out_表明当前传输数据有效 (out), .R1_in(Mem_R1),
    .R2_in(Mem_R2), .R1(WB_R1), .R2(WB_R2));  // open: Beq_in, JR_in, Bne_in, JMP_in, Beq, JR, JMP, Bne, BLTZ
  RAM #(.addrWidth(10), .dataWidth(32), .bus("separate")) ram_1 (
    .addr(Mem_Result[11:2]), .din(Mem_R2), .data(ram_1_data), .str(ex_mem_1_memwrite), .sel(1'b1), .clk(CLK),
    .ld(1'b1), .clr(RST));
  and and_18 (and_18_out, ~\ex_mem_1_传输状态out_表明当前传输数据有效 , ~en);  // AND_Gate
  Multiplexer #(.width(32), .enable("false")) multiplexer_11 (
    .in0(bit_extender_1_out), .in1(bit_extender_2_out), .out(\立即数扩展 ), .sel(SignedExt));
  \重定向控制器  \u_重定向控制器_1  (
    .OP(OP), .EX_WriteReg_num(EX_W_num), .EX_RegWrite(EX_RegWrite), .ForwardA(FordA),
    .MEM_WriteReg_num(MEM_W_num), .MEM_RegWrite(MEM_RegWrite), .ForwardB(FordB), .Func(Func),
    .ID_R1_num(ID_R1), .ID_R2_num(ID_R2), .Load_Use(Load_Use), .EX_MemToReg(EX_MtoR),
    .Mem_MemToReg(MEM_MtoR), .WB_MemData(WB_MemData), .Mem_R1(Mem_R1), .WB_R1(WB_R1), .WB_Result(WB_Result),
    .WB_imm(WB_imm), .Mem_R2(Mem_R2), .WB_R2(WB_R2), .Mem_imm(Mem_imm), .Mem_LUI(Mem_LUI), .WB_LUI(LUI),
    .Mem_Sllv(Mem_SLLV), .WB_Sllv(SLLV), .WB_MemToReg(MemToReg), .WB_HB(HB), .Result1(Result1),
    .Result2(Result), .MemData(MemData), .Mem_Result(Mem_Result));

  // Other names for the same wires on the sheet: instr_index[25:0] = EX_IR[25:0];
  //   PC1[31:2] = {PC[31:28], EX_IR[25:0]}; 立即数[15:0] = EX_IR[15:0]; shamt[4:0] = EX_IR[10:6]; MEM_IR[15:0] = Mem_imm;
  //   PC高4位[3:0] = PC[31:28]; WB_IR[15:0] = WB_imm

  // Notes on the sheet:
  //   中断源
  //   中断等待指示
  //   数码管输出
  //   contents of rom_1 (hex, n*v repeats v):
  //   20110001 8100005 20110001 20120002 20130003 8100009 20110001 20120002 20130003 810000d 20110001
  //   20120002 20130003 8100011 20110001 20120002 20130003 c1000fb 20100001 20110001 118fc0 112020
  //   20020022 c 118882 12200001 8100015 112020 20020022 c 20110001 118880 112020 20020022 c 12200001
  //   810001f 20110001 118fc0 112020 20020022 c 1188c3 112020 20020022 c 118903 112020 20020022 c 118903
  //   112020 20020022 c 118903 112020 20020022 c 118903 112020 20020022 c 118903 112020 20020022 c 118903
  //   112020 20020022 c 118903 112020 20020022 c 20100001 109fc0 139fc3 8021 2012000c 24160003 26100001
  //   3210000f 20080008 20090001 139900 2709825 132020 20020022 c 1094022 1500fff9 22100001 2018000f
  //   2188024 108700 20080008 20090001 139902 2709825 132021 20020022 c 1094022 1500fff9 108702 2c9b022
  //   12c00001 8100050 4020 1084027 84400 3508ffff 82021 20020022 c 2010ffff 20110000 ae300000 22100001
  //   22310004 ae300000 22100001 22310004 ae300000 22100001 22310004 ae300000 22100001 22310004 ae300000
  //   22100001 22310004 ae300000 22100001 22310004 ae300000 22100001 22310004 ae300000 22100001 22310004
  //   ae300000 22100001 22310004 ae300000 22100001 22310004 ae300000 22100001 22310004 ae300000 22100001
  //   22310004 ae300000 22100001 22310004 ae300000 22100001 22310004 ae300000 22100001 22310004 ae300000
  //   22100001 22310004 22100001 8020 2011003c 8e130000 8e340000 274402a 11000002 ae330000 ae140000
  //   2231fffc 1611fff8 102020 20020022 c 22100004 2011003c 1611fff2 20020032 c 20080001 20090003 20110876
  //   112020 20020022 c 200b0008 1118804 1318804 112020 20020022 c 216bffff 1560fff9 20020032 c 200b0008
  //   3c11fedc 3631ffff 112020 20020022 c 3c11ba98 112020 c 3c117654 112020 c 3c113210 112020 c 216bffff
  //   1560fff0 20020032 c 20090000 200b0010 34118483 20120404 118c00 129400 36318281 22520404 ad310000
  //   2328820 21290004 216bffff 1560fffb 200b0020 20090000 85310000 112020 20020022 c 21290002 216bffff
  //   1560fff9 20020032 c 2011fff1 112020 20020022 c 22310001 620fffb 2002000a c 20100000 22100001 102020
  //   20020022 c 22100002 102020 20020022 c 22100003 102020 20020022 c 22100004 102020 20020022 c 22100005
  //   102020 20020022 c 22100006 102020 20020022 c 22100007 102020 20020022 c 22100008 102020 20020022
  //   20020022 c 3e00008
  //   指令字
  //   Func
  //   rs
  //   rt
  //   OP
  //   Func
  //   流水调试日志用
  //   shamt
endmodule
module Cache (
  input  [31:0] \写入PC ,
  input  \预测位写入 ,
  input  [31:0] \读入PC ,
  input  CLK,
  input  [1:0] \预测位 ,
  input  [31:0] \目标地址 ,
  input  \写入 ,
  output Hit2,
  output Hit,
  output [1:0] \历史预测位 ,
  output [31:0] DataOut
);

  wire and_1_out, and_2_out, and_3_out, and_4_out, and_5_out, and_6_out, and_7_out, and_8_out, and_9_out,
       and_10_out, and_11_out, and_12_out, and_13_out, and_14_out, and_15_out, and_16_out, and_36_out,
       and_37_out, and_38_out, and_39_out, and_40_out, and_41_out, and_42_out, and_43_out, and_44_out,
       and_45_out, and_46_out, and_47_out, and_48_out, and_49_out, and_50_out, and_51_out, and_52_out,
       and_53_out, and_54_out, and_55_out, and_56_out, and_57_out, and_58_out, and_59_out, change,
       comparator_1_eq, comparator_2_eq, comparator_3_eq, comparator_4_eq, comparator_5_eq, comparator_6_eq,
       comparator_7_eq, comparator_8_eq, comparator_9_eq, comparator_10_eq, comparator_11_eq,
       comparator_12_eq, comparator_13_eq, comparator_14_eq, comparator_15_eq, comparator_16_eq,
       comparator_17_eq, L0, L1, L2, L3, L4, L5, L6, L7, M0, M1, M2, M3, M4, M5, M6, M7, Miss, or_1_out,
       or_2_out, or_3_out, or_4_out, or_5_out, or_6_out, or_7_out, or_8_out, or_11_out, or_12_out, or_13_out,
       or_14_out, or_15_out, or_16_out, or_17_out, or_18_out, or_27_out, R0, R1, R2, R3, R4, R5, R6, R7, T0,
       T1, T2, T3, T4, T5, T6, T7, V0, V1, V2, V3, V4, V5, V6, V7, \不写入 , \无效写入 , \相等 ;
  wire [1:0] multiplexer_3_out, \历史预测位1 , \数据块副本_9_q , \数据块副本_10_q , \数据块副本_11_q , \数据块副本_12_q ,
       \数据块副本_13_q , \数据块副本_14_q , \数据块副本_15_q , \数据块副本_16_q ;
  wire [2:0] Max, max3_1_max_num, max3_2_max_num, max3_3_max_num, max3_4_max_num, max3_5_max_num,
       max3_6_max_num;
  wire [9:0] \数据块副本_2_q_2 , \数据块副本_3_q_2 , \数据块副本_q_2 ;
  wire [15:0] C0, C1, C2, C3, C4, C5, C6, C7, max3_1_max, max3_2_max, max3_3_max, max3_4_max, max3_5_max,
       max3_6_max, register_1_q, register_2_q, register_3_q, register_4_q, register_5_q, register_6_q,
       register_7_q, register_8_q;
  wire [31:0] DataOut1, multiplexer_1_out, Tag0, Tag1, Tag2, Tag3, Tag4, Tag5, Tag6, Tag7, \数据块副本_2_q ,
       \数据块副本_3_q , \数据块副本_4_q , \数据块副本_5_q , \数据块副本_6_q , \数据块副本_7_q , \数据块副本_8_q , \数据块副本_q ;

  Register #(.width(1)) valid (.D(1'b1), .en(R0), .Q(V0), .clk(CLK));  // open: clr
  Register #(.width(1)) valid_2 (.D(1'b1), .en(R1), .Q(V1), .clk(CLK));  // open: clr
  Register #(.width(1)) valid_3 (.D(1'b1), .en(R2), .Q(V2), .clk(CLK));  // open: clr
  Register #(.width(1)) valid_4 (.D(1'b1), .en(R3), .Q(V3), .clk(CLK));  // open: clr
  Register #(.width(1)) valid_5 (.D(1'b1), .en(R4), .Q(V4), .clk(CLK));  // open: clr
  Register #(.width(1)) valid_6 (.D(1'b1), .en(R5), .Q(V5), .clk(CLK));  // open: clr
  Register #(.width(1)) valid_7 (.D(1'b1), .en(R6), .Q(V6), .clk(CLK));  // open: clr
  Register #(.width(1)) valid_8 (.D(1'b1), .en(R7), .Q(V7), .clk(CLK));  // open: clr
  // Probe on \读入PC [11:2]
  // Probe on \目标地址 
  // Probe on Tag0[11:2]
  Register #(.width(32)) \u_标记位  (.D(\写入PC ), .en(R0), .Q(Tag0), .clk(CLK));  // open: clr
  // Probe on Tag1[11:2]
  Register #(.width(32)) \u_标记位_2  (.D(\写入PC ), .en(R1), .Q(Tag1), .clk(CLK));  // open: clr
  // Probe on Tag2[11:2]
  Register #(.width(32)) \u_标记位_3  (.D(\写入PC ), .en(R2), .Q(Tag2), .clk(CLK));  // open: clr
  Register #(.width(32)) \u_标记位_4  (.D(\写入PC ), .en(R3), .Q(Tag3), .clk(CLK));  // open: clr
  Register #(.width(32)) \u_标记位_5  (.D(\写入PC ), .en(R4), .Q(Tag4), .clk(CLK));  // open: clr
  Register #(.width(32)) \u_标记位_6  (.D(\写入PC ), .en(R5), .Q(Tag5), .clk(CLK));  // open: clr
  // Probe on Tag6[11:2]
  Register #(.width(32)) \u_标记位_7  (.D(\写入PC ), .en(R6), .Q(Tag6), .clk(CLK));  // open: clr
  // Probe on Tag7[11:2]
  Register #(.width(32)) \u_标记位_8  (.D(\写入PC ), .en(R7), .Q(Tag7), .clk(CLK));  // open: clr
  // Probe on C0
  Counter #(.width(16), .max('hffff), .ongoal("stay")) \u_淘汰标志位  (
    .count(1'b1), .Q(C0), .clk(CLK), .clr(and_1_out));  // open: load, D, carry
  and and_1 (and_1_out, V0, or_1_out);
  or or_1 (or_1_out, M0, R0);
  // Probe on C1
  Counter #(.width(16), .max('hffff), .ongoal("stay")) \u_淘汰标志位_2  (
    .count(1'b1), .Q(C1), .clk(CLK), .clr(and_2_out));  // open: load, D, carry
  and and_2 (and_2_out, V1, or_2_out);
  or or_2 (or_2_out, M1, R1);
  // Probe on C2
  Counter #(.width(16), .max('hffff), .ongoal("stay")) \u_淘汰标志位_3  (
    .count(1'b1), .Q(C2), .clk(CLK), .clr(and_3_out));  // open: load, D, carry
  and and_3 (and_3_out, V2, or_3_out);
  or or_3 (or_3_out, M2, R2);
  // Probe on C3
  Counter #(.width(16), .max('hffff), .ongoal("stay")) \u_淘汰标志位_4  (
    .count(1'b1), .Q(C3), .clk(CLK), .clr(and_4_out));  // open: load, D, carry
  and and_4 (and_4_out, V3, or_4_out);
  or or_4 (or_4_out, M3, R3);
  Counter #(.width(16), .max('hffff), .ongoal("stay")) \u_淘汰标志位_5  (
    .count(1'b1), .Q(C4), .clk(CLK), .clr(and_5_out));  // open: load, D, carry
  and and_5 (and_5_out, V4, or_5_out);
  or or_5 (or_5_out, M4, R4);
  Counter #(.width(16), .max('hffff), .ongoal("stay")) \u_淘汰标志位_6  (
    .count(1'b1), .Q(C5), .clk(CLK), .clr(and_6_out));  // open: load, D, carry
  and and_6 (and_6_out, V5, or_6_out);
  or or_6 (or_6_out, M5, R5);
  Counter #(.width(16), .max('hffff), .ongoal("stay")) \u_淘汰标志位_7  (
    .count(1'b1), .Q(C6), .clk(CLK), .clr(and_7_out));  // open: load, D, carry
  and and_7 (and_7_out, V6, or_7_out);
  or or_7 (or_7_out, M6, R6);
  Counter #(.width(16), .max('hffff)) \u_淘汰标志位_8  (
    .count(1'b1), .Q(C7), .clk(CLK), .clr(and_8_out));  // open: load, D, carry
  and and_8 (and_8_out, V7, or_8_out);
  or or_8 (or_8_out, M7, R7);
  and and_9 (and_9_out, R0, \写入 );
  and and_10 (and_10_out, R1, \写入 );
  and and_11 (and_11_out, R2, \写入 );
  and and_12 (and_12_out, R3, \写入 );
  and and_13 (and_13_out, R4, \写入 );
  and and_14 (and_14_out, R5, \写入 );
  and and_15 (and_15_out, R6, \写入 );
  and and_16 (and_16_out, R7, \写入 );
  // Probe on \数据块副本_q_2 
  assign DataOut1 = M0 ? {\数据块副本_q [31:12], \数据块副本_q_2 , \数据块副本_q [1:0]} : 32'bz;  // Controlled_Buffer controlled_buffer_1
  Register #(.width(32)) \u_数据块副本  (
    .D(\目标地址 ), .en(and_9_out), .Q({\数据块副本_q [31:12], \数据块副本_q_2 , \数据块副本_q [1:0]}), .clk(CLK));  // open: clr
  // Probe on \数据块副本_2_q_2 
  Register #(.width(32)) \u_数据块副本_2  (
    .D(\目标地址 ), .en(and_10_out), .Q({\数据块副本_2_q [31:12], \数据块副本_2_q_2 , \数据块副本_2_q [1:0]}), .clk(CLK));  // open: clr
  assign DataOut1 = M1 ? {\数据块副本_2_q [31:12], \数据块副本_2_q_2 , \数据块副本_2_q [1:0]} : 32'bz;  // Controlled_Buffer controlled_buffer_2
  // Probe on \数据块副本_3_q_2 
  Register #(.width(32)) \u_数据块副本_3  (
    .D(\目标地址 ), .en(and_11_out), .Q({\数据块副本_3_q [31:12], \数据块副本_3_q_2 , \数据块副本_3_q [1:0]}), .clk(CLK));  // open: clr
  assign DataOut1 = M2 ? {\数据块副本_3_q [31:12], \数据块副本_3_q_2 , \数据块副本_3_q [1:0]} : 32'bz;  // Controlled_Buffer controlled_buffer_3
  Register #(.width(32)) \u_数据块副本_4  (.D(\目标地址 ), .en(and_12_out), .Q(\数据块副本_4_q ), .clk(CLK));  // open: clr
  assign DataOut1 = M3 ? \数据块副本_4_q  : 32'bz;  // Controlled_Buffer controlled_buffer_4
  Register #(.width(32)) \u_数据块副本_5  (.D(\目标地址 ), .en(and_13_out), .Q(\数据块副本_5_q ), .clk(CLK));  // open: clr
  assign DataOut1 = M4 ? \数据块副本_5_q  : 32'bz;  // Controlled_Buffer controlled_buffer_5
  assign DataOut1 = M5 ? \数据块副本_6_q  : 32'bz;  // Controlled_Buffer controlled_buffer_6
  Register #(.width(32)) \u_数据块副本_6  (.D(\目标地址 ), .en(and_14_out), .Q(\数据块副本_6_q ), .clk(CLK));  // open: clr
  assign DataOut1 = M6 ? \数据块副本_7_q  : 32'bz;  // Controlled_Buffer controlled_buffer_7
  Register #(.width(32)) \u_数据块副本_7  (.D(\目标地址 ), .en(and_15_out), .Q(\数据块副本_7_q ), .clk(CLK));  // open: clr
  Register #(.width(32)) \u_数据块副本_8  (.D(\目标地址 ), .en(and_16_out), .Q(\数据块副本_8_q ), .clk(CLK));  // open: clr
  assign DataOut1 = M7 ? \数据块副本_8_q  : 32'bz;  // Controlled_Buffer controlled_buffer_8
  assign \历史预测位1  = M0 ? \数据块副本_9_q  : 2'bz;  // Controlled_Buffer controlled_buffer_9
  Register #(.width(2)) \u_数据块副本_9  (.D(\预测位 ), .en(R0), .Q(\数据块副本_9_q ), .clk(CLK));  // open: clr
  Register #(.width(2)) \u_数据块副本_10  (.D(\预测位 ), .en(R1), .Q(\数据块副本_10_q ), .clk(CLK));  // open: clr
  assign \历史预测位1  = M1 ? \数据块副本_10_q  : 2'bz;  // Controlled_Buffer controlled_buffer_10
  Register #(.width(2)) \u_数据块副本_11  (.D(\预测位 ), .en(R2), .Q(\数据块副本_11_q ), .clk(CLK));  // open: clr
  assign \历史预测位1  = M2 ? \数据块副本_11_q  : 2'bz;  // Controlled_Buffer controlled_buffer_11
  assign \历史预测位1  = M3 ? \数据块副本_12_q  : 2'bz;  // Controlled_Buffer controlled_buffer_12
  Register #(.width(2)) \u_数据块副本_12  (.D(\预测位 ), .en(R3), .Q(\数据块副本_12_q ), .clk(CLK));  // open: clr
  Register #(.width(2)) \u_数据块副本_13  (.D(\预测位 ), .en(R4), .Q(\数据块副本_13_q ), .clk(CLK));  // open: clr
  assign \历史预测位1  = M4 ? \数据块副本_13_q  : 2'bz;  // Controlled_Buffer controlled_buffer_13
  Register #(.width(2)) \u_数据块副本_14  (.D(\预测位 ), .en(R5), .Q(\数据块副本_14_q ), .clk(CLK));  // open: clr
  assign \历史预测位1  = M5 ? \数据块副本_14_q  : 2'bz;  // Controlled_Buffer controlled_buffer_14
  assign \历史预测位1  = M6 ? \数据块副本_15_q  : 2'bz;  // Controlled_Buffer controlled_buffer_15
  Register #(.width(2)) \u_数据块副本_15  (.D(\预测位 ), .en(R6), .Q(\数据块副本_15_q ), .clk(CLK));  // open: clr
  Register #(.width(2)) \u_数据块副本_16  (.D(\预测位 ), .en(R7), .Q(\数据块副本_16_q ), .clk(CLK));  // open: clr
  assign \历史预测位1  = M7 ? \数据块副本_16_q  : 2'bz;  // Controlled_Buffer controlled_buffer_16
  Multiplexer #(.width(32), .enable("false")) multiplexer_1 (
    .in0({32{1'b0}}), .in1(DataOut1), .out(multiplexer_1_out), .sel(Hit2));
  // Probe on DataOut
  Multiplexer #(.width(32), .enable("false")) multiplexer_2 (
    .in0(multiplexer_1_out), .in1(\目标地址 ), .out(DataOut), .sel(\相等 ));
  Decoder #(.select(3), .disabled(0)) decoder_1 (
    .out0(T0), .out1(T1), .out2(T2), .out3(T3), .out4(T4), .out5(T5), .out6(T6), .out7(T7), .sel(Max),
    .en(change));
  Comparator #(.width(10)) comparator_1 (.a(\写入PC [11:2]), .b(Tag0[11:2]), .eq(comparator_1_eq));  // open: gt, lt
  Comparator #(.width(10)) comparator_2 (.a(\写入PC [11:2]), .b(Tag1[11:2]), .eq(comparator_2_eq));  // open: gt, lt
  Comparator #(.width(10)) comparator_3 (.a(\写入PC [11:2]), .b(Tag2[11:2]), .eq(comparator_3_eq));  // open: gt, lt
  Comparator #(.width(10)) comparator_4 (.a(\写入PC [11:2]), .b(Tag3[11:2]), .eq(comparator_4_eq));  // open: gt, lt
  Comparator #(.width(10)) comparator_5 (.a(\写入PC [11:2]), .b(Tag4[11:2]), .eq(comparator_5_eq));  // open: gt, lt
  Comparator #(.width(10)) comparator_6 (.a(\写入PC [11:2]), .b(Tag5[11:2]), .eq(comparator_6_eq));  // open: gt, lt
  Comparator #(.width(10)) comparator_7 (.a(\写入PC [11:2]), .b(Tag6[11:2]), .eq(comparator_7_eq));  // open: gt, lt
  Comparator #(.width(10)) comparator_8 (.a(\写入PC [11:2]), .b(Tag7[11:2]), .eq(comparator_8_eq));  // open: gt, lt
  Comparator #(.width(10)) comparator_9 (.a(\读入PC [11:2]), .b(Tag0[11:2]), .eq(comparator_9_eq));  // open: gt, lt
  Comparator #(.width(10)) comparator_10 (.a(\读入PC [11:2]), .b(Tag1[11:2]), .eq(comparator_10_eq));  // open: gt, lt
  Comparator #(.width(10)) comparator_11 (.a(\读入PC [11:2]), .b(Tag2[11:2]), .eq(comparator_11_eq));  // open: gt, lt
  Comparator #(.width(10)) comparator_12 (.a(\读入PC [11:2]), .b(Tag3[11:2]), .eq(comparator_12_eq));  // open: gt, lt
  Comparator #(.width(10)) comparator_13 (.a(\读入PC [11:2]), .b(Tag4[11:2]), .eq(comparator_13_eq));  // open: gt, lt
  Comparator #(.width(10)) comparator_14 (.a(\读入PC [11:2]), .b(Tag5[11:2]), .eq(comparator_14_eq));  // open: gt, lt
  Comparator #(.width(10)) comparator_15 (.a(\读入PC [11:2]), .b(Tag6[11:2]), .eq(comparator_15_eq));  // open: gt, lt
  Comparator #(.width(10)) comparator_16 (.a(\读入PC [11:2]), .b(Tag7[11:2]), .eq(comparator_16_eq));  // open: gt, lt
  Multiplexer #(.width(2), .enable("false")) multiplexer_3 (
    .in0(2'b01), .in1(\历史预测位1 ), .out(multiplexer_3_out), .sel(Hit2));
  and and_17 (change, V0, V1, V2, V3, Miss, V4, V5, V6, V7);
  and and_18 (L0, comparator_1_eq, V0);
  and and_19 (L1, comparator_2_eq, V1);
  and and_20 (L2, comparator_3_eq, V2);
  and and_21 (L3, comparator_4_eq, V3);
  and and_22 (L4, comparator_5_eq, V4);
  and and_23 (L5, comparator_6_eq, V5);
  and and_24 (L6, comparator_7_eq, V6);
  and and_25 (L7, comparator_8_eq, V7);
  and and_26 (M0, comparator_9_eq, V0);
  and and_27 (M1, comparator_10_eq, V1);
  and and_28 (M2, comparator_11_eq, V2);
  and and_29 (M3, comparator_12_eq, V3);
  and and_30 (M4, comparator_13_eq, V4);
  and and_31 (M5, comparator_14_eq, V5);
  and and_32 (M6, comparator_15_eq, V6);
  and and_33 (M7, comparator_16_eq, V7);
  // Probe on \历史预测位 
  Multiplexer #(.width(2), .enable("false")) multiplexer_4 (
    .in0(multiplexer_3_out), .in1(\预测位 ), .out(\历史预测位 ), .sel(\相等 ));
  or or_9 (Hit, L0, L1, L2, L3, L4, L5, L6, L7);
  or or_10 (Hit2, M0, M1, M2, M3, M4, M5, M6, M7);
  and and_34 (\无效写入 , \预测位写入 , \不写入 );
  not not_1 (Miss, Hit);
  Comparator #(.width(32)) comparator_17 (.a(\读入PC ), .b(\写入PC ), .eq(comparator_17_eq));  // open: gt, lt
  and and_35 (\相等 , comparator_17_eq, Hit2);
  and and_36 (and_36_out, Miss, ~V0);  // AND_Gate
  and and_37 (and_37_out, V0, Miss, ~V1);  // AND_Gate
  and and_38 (and_38_out, V1, V0, Miss, ~V2);  // AND_Gate
  and and_39 (and_39_out, V2, V1, V0, Miss, ~V3);  // AND_Gate
  and and_40 (and_40_out, V3, V2, V1, V0, Miss, ~V4);  // AND_Gate
  and and_41 (and_41_out, V4, V3, V2, V1, V0, Miss, ~V5);  // AND_Gate
  and and_42 (and_42_out, V5, V4, V3, V2, V1, V0, Miss, ~V6);  // AND_Gate
  and and_43 (and_43_out, V6, V5, V4, V3, V2, V1, V0, Miss, ~V7);  // AND_Gate
  or or_11 (or_11_out, and_36_out, T0);
  or or_12 (or_12_out, and_37_out, T1);
  or or_13 (or_13_out, and_38_out, T2);
  or or_14 (or_14_out, and_39_out, T3);
  or or_15 (or_15_out, and_40_out, T4);
  or or_16 (or_16_out, and_41_out, T5);
  or or_17 (or_17_out, and_42_out, T6);
  or or_18 (or_18_out, and_43_out, T7);
  and and_44 (and_44_out, or_11_out, \写入 );
  and and_45 (and_45_out, or_12_out, \写入 );
  and and_46 (and_46_out, or_13_out, \写入 );
  and and_47 (and_47_out, or_14_out, \写入 );
  and and_48 (and_48_out, or_15_out, \写入 );
  and and_49 (and_49_out, or_16_out, \写入 );
  and and_50 (and_50_out, or_17_out, \写入 );
  and and_51 (and_51_out, or_18_out, \写入 );
  Register #(.width(16)) register_1 (.D(C0), .Q(register_1_q), .clk(CLK));  // open: en, clr
  Register #(.width(16)) register_2 (.D(C1), .Q(register_2_q), .clk(CLK));  // open: en, clr
  Register #(.width(16)) register_3 (.D(C2), .Q(register_3_q), .clk(CLK));  // open: en, clr
  Register #(.width(16)) register_4 (.D(C3), .Q(register_4_q), .clk(CLK));  // open: en, clr
  Register #(.width(16)) register_5 (.D(C4), .Q(register_5_q), .clk(CLK));  // open: en, clr
  Register #(.width(16)) register_6 (.D(C5), .Q(register_6_q), .clk(CLK));  // open: en, clr
  Register #(.width(16)) register_7 (.D(C6), .Q(register_7_q), .clk(CLK));  // open: en, clr
  Register #(.width(16)) register_8 (.D(C7), .Q(register_8_q), .clk(CLK));  // open: en, clr
  and and_52 (and_52_out, \预测位写入 , V0, L0);
  and and_53 (and_53_out, \预测位写入 , V1, L1);
  and and_54 (and_54_out, \预测位写入 , V2, L2);
  and and_55 (and_55_out, \预测位写入 , V3, L3);
  and and_56 (and_56_out, \预测位写入 , V4, L4);
  and and_57 (and_57_out, \预测位写入 , V5, L5);
  and and_58 (and_58_out, \预测位写入 , V6, L6);
  and and_59 (and_59_out, \预测位写入 , V7, L7);
  Max3 max3_1 (
    .Y(register_2_q), .X(register_1_q), .Y_num(3'b001), .X_num(3'b000), .MAX(max3_1_max),
    .Max_num(max3_1_max_num));
  Max3 max3_2 (
    .Y(register_4_q), .X(register_3_q), .Y_num(3'b011), .X_num(3'b010), .MAX(max3_2_max),
    .Max_num(max3_2_max_num));
  Max3 max3_3 (
    .Y(register_6_q), .X(register_5_q), .Y_num(3'b101), .X_num(3'b100), .MAX(max3_3_max),
    .Max_num(max3_3_max_num));
  Max3 max3_4 (
    .Y(register_8_q), .X(register_7_q), .Y_num(3'b111), .X_num(3'b110), .MAX(max3_4_max),
    .Max_num(max3_4_max_num));
  or or_19 (R0, and_52_out, and_44_out);
  or or_20 (R1, and_53_out, and_45_out);
  or or_21 (R2, and_54_out, and_46_out);
  or or_22 (R3, and_55_out, and_47_out);
  or or_23 (R4, and_56_out, and_48_out);
  or or_24 (R5, and_57_out, and_49_out);
  or or_25 (R6, and_58_out, and_50_out);
  or or_26 (R7, and_59_out, and_51_out);
  Max3 max3_5 (
    .Y(max3_2_max), .X(max3_1_max), .Y_num(max3_2_max_num), .X_num(max3_1_max_num), .MAX(max3_5_max),
    .Max_num(max3_5_max_num));
  Max3 max3_6 (
    .Y(max3_4_max), .X(max3_3_max), .Y_num(max3_4_max_num), .X_num(max3_3_max_num), .MAX(max3_6_max),
    .Max_num(max3_6_max_num));
  or or_27 (or_27_out, R0, R1, R2, R3, R4, R5, R6, R7);
  not not_2 (\不写入 , or_27_out);
  Max3 max3_7 (
    .Y(max3_6_max), .X(max3_5_max), .Y_num(max3_6_max_num), .X_num(max3_5_max_num), .Max_num(Max));  // open: MAX

  // Other names for the same wires on the sheet: Tag[31:0] = \写入PC 

  // Notes on the sheet:
  //   输入引脚区
  //   输出引脚区
  //   替换标志
  //   使用标志
endmodule

module Max3 (
  input  [15:0] Y,
  input  [15:0] X,
  input  [2:0] Y_num,
  input  [2:0] X_num,
  output [15:0] MAX,
  output [2:0] Max_num
);

  wire comparator_1_eq, comparator_1_gt, or_1_out;

  Multiplexer #(.width(16), .enable("false")) multiplexer_1 (.in0(Y), .in1(X), .out(MAX), .sel(or_1_out));
  Comparator #(.width(16), .mode("unsigned")) comparator_1 (
    .a(X), .b(Y), .gt(comparator_1_gt), .eq(comparator_1_eq));  // open: lt
  or or_1 (or_1_out, comparator_1_gt, comparator_1_eq);
  Multiplexer #(.width(3), .enable("false")) multiplexer_2 (.in0(Y_num), .in1(X_num), .out(Max_num), .sel(or_1_out));

  // Notes on the sheet:
  //   输出两个输入中的较大值，并输出较大值的3位编号
endmodule

module \分支预测状态机  (
  input  [1:0] fr,
  input  success,
  output [1:0] fr_2,
  output \预测位写入 ,
  output \写入 ,
  output \跳转错误 
);

  wire and_1_out, and_2_out, and_3_out, and_4_out, comparator_1_eq, not_1_out, not_2_out, not_3_out,
       not_4_out, not_5_out;

  Comparator #(.width(2), .mode("unsigned")) comparator_1 (.a(fr), .b(fr_2), .eq(comparator_1_eq));  // open: gt, lt
  and and_1 (and_1_out, fr[0], success);
  and and_2 (and_2_out, fr[1], not_1_out);
  not not_1 (not_1_out, fr[0]);
  not not_2 (not_2_out, fr[1]);
  not not_3 (not_3_out, fr[0]);
  and and_3 (and_3_out, not_2_out, not_3_out, success);
  not not_4 (not_4_out, fr[0]);
  and and_4 (and_4_out, fr[1], not_4_out, not_5_out);
  not not_5 (not_5_out, success);
  not not_6 (\预测位写入 , comparator_1_eq);
  xor xor_1 (\跳转错误 , success, fr[1]);
  or or_1 (fr_2[1], and_1_out, and_2_out);
  or or_2 (fr_2[0], and_3_out, and_4_out);
  and and_5 (\写入 , \预测位写入 , success);

  // Other names for the same wires on the sheet: fr_in[1:0] = fr; fr_t[1:0] = fr_2
endmodule
