// Logisim project cpu单级中断.circ as structural Verilog: 15 circuits, main circuit ◆单周期单级中断
module \单周期单级中断  (
);

  wire \_1号中断 , \_1号中断等待指示 , \_2号中断 , \_2号中断等待指示 , \_3号中断 , \_3号中断等待指示 , alus, and_1_out, and_2_out,
       and_3_out, and_4_out, and_5_out, and_9_out, and_10_out, and_11_out, beq, bgtz, bne, CLK,
       comparator_1_gt, comparator_2_eq, comparator_3_eq, condi, d_ff_1_q, d_ff_2_q, d_ff_3_q, d_ff_4_q,
       demultiplexer_1_out1, demultiplexer_1_out2, demultiplexer_1_out3, equ, eret, Go, halt, IR1_2_q, IR1_q,
       IR2_q, jal, jmp, jr, lbu, led, lui, mfc0, mtr, mw, nor_1_out, nor_2_out, not_1_out, not_2_out,
       or_1_out, or_2_out, or_8_out, or_9_out, or_10_out, pause, pcen, Rd, register_2_q, RST, rw, SignedExt,
       Sys;
  wire [1:0] intnum, nowint, priority_encoder_1_out, register_6_q;
  wire [1:1] and_12_out, PCSrc;
  wire [3:0] aluop;
  wire [4:0] CP0, R1_num, R2_num, W_num;
  wire [7:0] mips_ram_1_p6, multiplexer_9_out;
  wire [15:0] imm, \总周期数 , \无条件分支数 , \条件分支成功数 ;
  wire [25:16] index;
  wire [31:0] bit_extender_1_out, bit_extender_2_out, bit_extender_3_out, Din, Ext, LedData,
       multiplexer_1_out, multiplexer_2_out, multiplexer_3_out, multiplexer_5_out, multiplexer_10_out,
       multiplexer_11_out, multiplexer_12_out, mwaddr, mwdata, pc0, pc1, pc2, PC_q, register_1_q,
       shifter_1_out;
  wire [31:8] mips_ram_1_p6_2;
  wire [31:26] rom_1_data;

  Button \u_总复位  (.out(RST));
  Button \u_继续运行  (.out(Go));
  Clock clock_1 (.out(CLK));
  Button _1 (.out(\_1号中断 ));
  Button _2 (.out(\_2号中断 ));
  Button _3 (.out(\_3号中断 ));
  or or_1 (or_1_out, intnum[0], intnum[1]);
  Multiplexer #(.select(2), .width(32), .enable("false")) multiplexer_1 (
    .in0(pc0), .in1(pc1), .in2(pc2), .in3({pc0[31:28], index, imm, 2'b00}), .out(multiplexer_1_out),
    .sel({PCSrc[1], jmp}));
  Hex_Digit_Display hex_digit_display_1 (.value(LedData[27:24]));  // open: dp
  Hex_Digit_Display hex_digit_display_2 (.value(LedData[31:28]));  // open: dp
  LED _1_2 (.in(\_1号中断等待指示 ));
  LED _2_2 (.in(\_2号中断等待指示 ));
  LED _3_2 (.in(\_3号中断等待指示 ));
  Register #(.width(32)) register_1 (.D(multiplexer_1_out), .en(or_1_out), .Q(register_1_q), .clk(CLK));  // open: clr
  // Probe on nothing
  Hex_Digit_Display hex_digit_display_3 (.value(LedData[23:20]));  // open: dp
  Hex_Digit_Display hex_digit_display_4 (.value(LedData[19:16]));  // open: dp
  Register #(.width(1)) register_2 (.D(eret), .Q(register_2_q), .clk(CLK));  // open: en, clr
  Multiplexer #(.width(32), .enable("false")) multiplexer_2 (
    .in0(multiplexer_1_out), .in1(register_1_q), .out(multiplexer_2_out), .sel(register_2_q));
  Hex_Digit_Display hex_digit_display_5 (.value(LedData[11:8]));  // open: dp
  Hex_Digit_Display hex_digit_display_6 (.value(LedData[15:12]));  // open: dp
  // Probe on nowint
  Hex_Digit_Display hex_digit_display_7 (.value(LedData[3:0]));  // open: dp
  Hex_Digit_Display hex_digit_display_8 (.value(LedData[7:4]));  // open: dp
  and and_1 (and_1_out, ~halt, Go);  // AND_Gate
  Register #(.width(32)) PC (.D(multiplexer_3_out), .en(pcen), .Q(PC_q), .clk(CLK), .clr(RST));
  Multiplexer #(.select(2), .width(32), .enable("false")) multiplexer_3 (
    .in0(multiplexer_2_out), .in1(32'h128), .in2(32'h1c0), .in3(32'h258), .out(multiplexer_3_out),
    .sel(intnum));
  D_Flip_Flop d_ff_1 (.clk(CLK), .D(and_1_out), .Q(d_ff_1_q), .reset(RST));  // open: Qn, preset, en
  not not_1 (not_1_out, d_ff_1_q);
  or or_2 (or_2_out, halt, pause);
  Shifter #(.width(32)) shifter_1 (.in(Ext), .\dist (5'b00010), .out(shifter_1_out));
  and and_2 (and_2_out, jmp, ~jr);  // AND_Gate
  assign bit_extender_1_out = {{16{1'b0}}, imm};  // Bit_Extender bit_extender_1
  assign bit_extender_2_out = {{16{imm[15]}}, imm};  // Bit_Extender bit_extender_2
  and and_3 (and_3_out, beq, equ);
  and and_4 (and_4_out, bne, ~equ);  // AND_Gate
  and and_5 (and_5_out, bgtz, comparator_1_gt);
  Comparator #(.width(32)) comparator_1 (.a(pc1), .b({32{1'b0}}), .gt(comparator_1_gt));  // open: eq, lt
  xor xor_1 (pcen, not_1_out, or_2_out);
  Adder #(.width(32)) adder_1 (.a(PC_q), .b(32'h4), .out(pc0));  // open: cin, cout
  Adder #(.width(32)) adder_2 (.a(pc0), .b(shifter_1_out), .out(pc2));  // open: cin, cout
  or or_3 (PCSrc[1], condi, and_2_out);
  Multiplexer #(.width(32), .enable("false")) multiplexer_4 (
    .in0(bit_extender_1_out), .in1(bit_extender_2_out), .out(Ext), .sel(SignedExt));
  or or_4 (condi, and_3_out, and_4_out, and_5_out);
  // Probe on \总周期数 
  // Probe on \无条件分支数 
  // Probe on \条件分支成功数 
  ROM #(.addrWidth(10), .dataWidth(32)) rom_1 (.addr(PC_q[11:2]), .data({rom_1_data, index, imm}));  // open: sel
  // Probe on rom_1_data
  // Probe on imm[5:0]
  \硬布线控制器  \u_硬布线控制器_1  (
    .OP(rom_1_data), .Func(imm[5:0]), .ALU_OP(aluop), .MemToReg(mtr), .MemWrite(mw), .ALU_SRC(alus),
    .RegWrite(rw), .SysCALL(Sys), .SignedExt(SignedExt), .RegDst(Rd), .Beq(beq), .Bne(bne), .JR(jr),
    .JMP(jmp), .JAL(jal), .LUI(lui), .BGTZ(bgtz), .LBU(lbu), .MFC0(mfc0), .ERET(eret));
  Comparator #(.width(32)) comparator_2 (.a(pc1), .b(32'h22), .eq(comparator_2_eq));  // open: gt, lt
  and and_6 (led, comparator_2_eq, Sys);
  and and_7 (halt, Sys, comparator_3_eq);
  Comparator #(.width(32)) comparator_3 (.a(pc1), .b(32'ha), .eq(comparator_3_eq));  // open: gt, lt
  nor nor_1 (nor_1_out, halt, led);
  and and_8 (pause, nor_1_out, Sys);
  MIPS_Regifile mips_regifile_1 (
    .Din(Din), .Clk(CLK), .R1(pc1), .R2(mwdata), .WE(rw), .W_num(W_num), .R1_num(R1_num), .R2_num(R2_num));
  Multiplexer #(.width(32), .enable("false")) multiplexer_5 (
    .in0(mwdata), .in1(Ext), .out(multiplexer_5_out), .sel(alus));
  Counter #(.width(16), .max('hffff)) counter_1 (
    .count(jmp), .Q(\无条件分支数 ), .clk(CLK), .clr(RST));  // open: load, D, carry
  Comparator #(.width(32)) comparator_4 (.a(pc1), .b(32'h22), .eq(led));  // open: gt, lt
  MIPS_ALU mips_alu_1 (
    .shamt(imm[10:6]), .X(pc1), .Y(multiplexer_5_out), .AluOP(aluop), .Equal(equ), .Result(mwaddr));  // open: Result_2
  Counter #(.width(16), .max('hffff)) counter_2 (
    .count(condi), .Q(\条件分支成功数 ), .clk(CLK), .clr(RST));  // open: load, D, carry
  nor nor_2 (nor_2_out, halt, Go, pause);
  Register #(.width(32)) register_3 (.D(mwdata), .en(led), .Q(LedData), .clk(CLK), .clr(RST));
  Multiplexer #(.width(5), .enable("false")) multiplexer_6 (
    .in0(index[25:21]), .in1(5'b00010), .out(R1_num), .sel(Sys));
  Multiplexer #(.width(5), .enable("false")) multiplexer_7 (
    .in0(index[20:16]), .in1(5'b00100), .out(R2_num), .sel(Sys));
  Multiplexer #(.select(2), .width(5), .enable("false")) multiplexer_8 (
    .in0(index[20:16]), .in1(imm[15:11]), .in2({5{1'b1}}), .in3({5{1'b1}}), .out(W_num), .sel({jal, Rd}));
  Counter #(.width(16), .max('hffff)) counter_3 (
    .count(nor_2_out), .Q(\总周期数 ), .clk(CLK), .clr(RST));  // open: load, D, carry
  // Probe on {{10{1'b0}}, mwaddr[11:2]}
  Demultiplexer #(.select(2), .enable("false")) demultiplexer_1 (
    .out1(demultiplexer_1_out1), .out2(demultiplexer_1_out2), .out3(demultiplexer_1_out3), .in(eret),
    .sel(nowint));  // open: out0
  Register #(.width(5)) register_4 (.D(imm[15:11]), .en(mfc0), .Q(CP0), .clk(CLK), .clr(RST));
  // MIPS_RAM mips_ram_1: pin names not known; wires that end beside it: {{10{1'b0}}, mwaddr[11:2]}, mwdata, mw, CLK, RST, {mips_ram_1_p6_2, mips_ram_1_p6}
  Multiplexer #(.select(2), .width(8), .enable("false")) multiplexer_9 (
    .in0(mips_ram_1_p6), .in1(mips_ram_1_p6_2[15:8]), .in2(mips_ram_1_p6_2[23:16]),
    .in3(mips_ram_1_p6_2[31:24]), .out(multiplexer_9_out), .sel(mwaddr[1:0]));
  Multiplexer #(.width(32), .enable("false")) multiplexer_10 (
    .in0(mwaddr), .in1(multiplexer_11_out), .out(multiplexer_10_out), .sel(mtr));
  Multiplexer #(.width(32), .enable("false")) multiplexer_11 (
    .in0({mips_ram_1_p6_2, mips_ram_1_p6}), .in1(bit_extender_3_out), .out(multiplexer_11_out), .sel(lbu));
  assign bit_extender_3_out = {{24{1'b0}}, multiplexer_9_out};  // Bit_Extender bit_extender_3
  Multiplexer #(.width(32), .enable("false")) multiplexer_12 (
    .in0(multiplexer_10_out), .in1(pc0), .out(multiplexer_12_out), .sel(jal));
  D_Flip_Flop d_ff_2 (.clk(\_3号中断 ), .D(1'b1), .Q(d_ff_2_q), .reset(IR1_q));  // open: Qn, preset, en
  or or_5 (\_3号中断等待指示 , IR1_q, d_ff_2_q);
  D_Flip_Flop d_ff_3 (.clk(\_2号中断 ), .D(1'b1), .Q(d_ff_3_q), .reset(IR2_q));  // open: Qn, preset, en
  or or_6 (\_2号中断等待指示 , IR2_q, d_ff_3_q);
  D_Flip_Flop d_ff_4 (.clk(\_1号中断 ), .D(1'b1), .Q(d_ff_4_q), .reset(IR1_2_q));  // open: Qn, preset, en
  or or_7 (\_1号中断等待指示 , IR1_2_q, d_ff_4_q);
  Multiplexer #(.width(32), .enable("false")) multiplexer_13 (
    .in0(multiplexer_12_out), .in1({imm, {16{1'b0}}}), .out(Din), .sel(lui));
  or or_8 (or_8_out, d_ff_2_q, IR1_q);
  or or_9 (or_9_out, d_ff_3_q, IR2_q);
  or or_10 (or_10_out, d_ff_4_q, IR1_2_q);
  and and_9 (and_9_out, or_8_out, ~demultiplexer_1_out3);  // AND_Gate
  and and_10 (and_10_out, or_9_out, ~demultiplexer_1_out2);  // AND_Gate
  and and_11 (and_11_out, or_10_out, ~demultiplexer_1_out1);  // AND_Gate
  D_Flip_Flop IR1 (.clk(CLK), .D(and_9_out), .Q(IR1_q));  // open: Qn, preset, en, reset
  D_Flip_Flop IR2 (.clk(CLK), .D(and_10_out), .Q(IR2_q));  // open: Qn, preset, en, reset
  D_Flip_Flop IR1_2 (.clk(CLK), .D(and_11_out), .Q(IR1_2_q));  // open: Qn, preset, en, reset
  Priority_Encoder #(.select(2)) priority_encoder_1 (
    .in0(1'b1), .in1(IR1_2_q), .in2(IR2_q), .in3(IR1_q), .out(priority_encoder_1_out));  // open: gs, en_out, en_in
  not not_2 (not_2_out, mfc0);
  Register #(.width(2)) register_5 (.D(priority_encoder_1_out), .en(mfc0), .Q(nowint), .clk(CLK));  // open: clr
  Register #(.width(2)) register_6 (.D(priority_encoder_1_out), .Q(register_6_q), .clk(CLK));  // open: en, clr
  and and_12 (and_12_out[1], CP0[0], not_2_out);
  assign intnum = register_6_q & {2{and_12_out[1]}};  // AND_Gate and_13, 2 bits wide

  // Other names for the same wires on the sheet: pc3[31:2] = {pc0[31:28], index, imm}; rt[4:0] = index[20:16];
  //   rs[4:0] = index[25:21]; index[15:0] = imm; rd_t[4:0] = imm[15:11]; PCSrc[0] = jmp

  // Notes on the sheet:
  //   中断信号源及指示电路规范（优先级3>2>1>CPU(0）)
  //   PC使能逻辑
  //   地址转移逻辑
  //   数码管输出
  //   pcin
  //   pcout
  //   pre_pc2
  //   指令存储器
  //   指令字
  //   contents of rom_1 (hex, n*v repeats v):
  //   40110800 20110200 20020022 112020 c 2231ffff 1620fffc 20020032 c 2008ffff 20117777 112020 20020022 c
  //   200b0010 2288826 112020 20020022 c 216bffff 1560fffa 20020032 c 200b0008 3c11fedc 3631ffff 112020
  //   20020022 c 3c11ba98 112020 c 3c117654 112020 c 3c113210 112020 c 216bffff 1560fff0 20020032 c
  //   20090000 200b0010 34118483 20120404 118c00 129400 36318281 22520404 ad310000 2328820 21290004
  //   216bffff 1560fffb 200b0020 20090000 91310000 112020 20020022 c 21290001 216bffff 1560fff9 20020032 c
  //   2011000f 112020 20020022 c 2231ffff 1e20fffb 2002000a c 40110000 ac1d0230 201d0080 27bdfffc afa40000
  //   27bdfffc afa20000 27bdfffc afa80000 27bdfffc afa90000 27bdfffc afb00000 20160001 20140006 20150001
  //   168020 108100 2149825 132020 20020022 c 1600fffa 295a022 1680fff7 8fb00000 27bd0004 8fa90000
  //   27bd0004 8fa80000 27bd0004 8fa20000 27bd0004 8fa40000 27bd0004 8c1d0230 42000018 40110800 40110000
  //   ac1d0244 201d0080 27bdfffc afa40000 27bdfffc afa20000 27bdfffc afa80000 27bdfffc afa90000 27bdfffc
  //   afb00000 20160002 20140006 20150001 168020 108100 2149825 132020 20020022 c 1600fffa 295a022
  //   1680fff7 8fb00000 27bd0004 8fa90000 27bd0004 8fa80000 27bd0004 8fa20000 27bd0004 8fa40000 27bd0004
  //   8c1d0230 42000018 40110800 40110000 ac1d0258 201d0080 27bdfffc afa40000 27bdfffc afa20000 27bdfffc
  //   afa80000 27bdfffc afa90000 27bdfffc afb00000 20160003 20140006 20150001 168020 108100 2149825 132020
  //   20020022 c 1600fffa 295a022 1680fff7 8fb00000 27bd0004 8fa90000 27bd0004 8fa80000 27bd0004 8fa20000
  //   27bd0004 8fa40000 27bd0004 8c1d0230 42000018 40110800
  //   irout
  //   OP
  //   Func
  //   rs
  //   rt
  //   rd
  //   JMP
  //   JR
  //   OP
  //   Func
  //   r1addr
  //   waddr
  //   Beq
  //   Bne
  //   MemToReg
  //   MemWrite
  //   AluOP
  //   AluSrcB
  //   RegWrite
  //   JAL
  //   RegDst
  //   Syscall
  //   Reset 
  //   Reset 
  //   Reset 
endmodule

module \硬布线控制器  (
  input  [5:0] OP,
  input  [5:0] Func,
  output [3:0] ALU_OP,
  output MemToReg,
  output MemWrite,
  output ALU_SRC,
  output RegWrite,
  output SysCALL,
  output SignedExt,
  output RegDst,
  output Beq,
  output Bne,
  output JR,
  output JMP,
  output JAL,
  output LUI,
  output BGTZ,
  output LBU,
  output MFC0,
  output ERET
);

  \运算控制器  \u_运算控制器_1  (
    .OP0(OP[0]), .OP1(OP[1]), .OP2(OP[2]), .OP3(OP[3]), .OP4(OP[4]), .OP5(OP[5]), .F0(Func[0]), .F1(Func[1]),
    .F2(Func[2]), .F3(Func[3]), .F4(Func[4]), .F5(Func[5]), .S0(ALU_OP[0]), .S1(ALU_OP[1]), .S2(ALU_OP[2]),
    .S3(ALU_OP[3]));
  \控制信号生成  \u_控制信号生成_1  (
    .OP0(OP[0]), .OP1(OP[1]), .OP2(OP[2]), .OP3(OP[3]), .OP4(OP[4]), .OP5(OP[5]), .F0(Func[0]), .F1(Func[1]),
    .F2(Func[2]), .F3(Func[3]), .F4(Func[4]), .F5(Func[5]), .MemToReg(MemToReg), .MemWrite(MemWrite),
    .ALU_SRC(ALU_SRC), .RegWrite(RegWrite), .SysCALL(SysCALL), .SignedExt(SignedExt), .RegDst(RegDst),
    .BEQ(Beq), .BNE(Bne), .JR(JR), .JMP(JMP), .JAL(JAL));
  \额外控制信号生成  \u_额外控制信号生成_1  (
    .OP0(OP[0]), .OP1(OP[1]), .OP2(OP[2]), .OP3(OP[3]), .OP4(OP[4]), .OP5(OP[5]), .F0(Func[0]), .F1(Func[1]),
    .F2(Func[2]), .F3(Func[3]), .F4(Func[4]), .F5(Func[5]), .LUI(LUI), .BGTZ(BGTZ), .LBU(LBU), .MFC0(MFC0),
    .ERET(ERET));

  // Other names for the same wires on the sheet: OP_CODE[5:0] = OP

  // Notes on the sheet:
  //   运算器控制器，根据指令生成运算器功能选择信号
  //   控制信号生成，产生数据通路需要的其他控制信号
endmodule

module \运算控制器  (
  input  OP0,
  input  OP1,
  input  OP2,
  input  OP3,
  input  OP4,
  input  OP5,
  input  F0,
  input  F1,
  input  F2,
  input  F3,
  input  F4,
  input  F5,
  output S0,
  output S1,
  output S2,
  output S3
);

  wire and_1_out, and_2_out, and_3_out, and_4_out, and_5_out, and_6_out, and_7_out, and_8_out, and_9_out,
       and_10_out, and_11_out, and_12_out, and_13_out, and_14_out, and_15_out, and_16_out, and_17_out,
       and_18_out, and_19_out, and_20_out, and_21_out, and_22_out, and_23_out, and_24_out, and_25_out,
       and_26_out, and_27_out, and_28_out, and_29_out, and_30_out, and_31_out, and_32_out, and_33_out,
       and_34_out, and_35_out, and_36_out, and_37_out, and_38_out, not_1_out, not_2_out, not_3_out,
       not_4_out, not_5_out, not_6_out, not_7_out, not_8_out, not_9_out, not_10_out, not_11_out, not_12_out,
       not_13_out, not_14_out, not_15_out, not_16_out, not_17_out, not_18_out, not_19_out, not_20_out,
       not_21_out, not_22_out, not_23_out, not_24_out, not_25_out, not_26_out, not_27_out, not_28_out,
       not_29_out, not_30_out, not_31_out, not_32_out, not_33_out, not_34_out, not_35_out, not_36_out,
       not_37_out, not_38_out, not_39_out, not_40_out, not_41_out, not_42_out, not_43_out, not_44_out,
       not_45_out, not_46_out, not_47_out, not_48_out, not_49_out, not_50_out, not_51_out, not_52_out,
       not_53_out, not_54_out, not_55_out, not_56_out, not_57_out, not_58_out, not_59_out, not_60_out,
       not_61_out, not_62_out, not_63_out, not_64_out, not_65_out, not_66_out, not_67_out, not_68_out,
       not_69_out, not_70_out, not_71_out, not_72_out, not_73_out, not_74_out, not_75_out, not_76_out,
       not_77_out, not_78_out, not_79_out, not_80_out, not_81_out, not_82_out, not_83_out, not_84_out,
       not_85_out, not_86_out, not_87_out, not_88_out, not_89_out, not_90_out, not_91_out, not_92_out,
       not_93_out, not_94_out, not_95_out, not_96_out, not_97_out, not_98_out, not_99_out, not_100_out,
       not_101_out, not_102_out, not_103_out, not_104_out, not_105_out, not_106_out, not_107_out,
       not_108_out, not_109_out, not_110_out, not_111_out, not_112_out, not_113_out, not_114_out,
       not_115_out, not_116_out, not_117_out, not_118_out, not_119_out, not_120_out, not_121_out,
       not_122_out, not_123_out, not_124_out, not_125_out, not_126_out, not_127_out, not_128_out,
       not_129_out, not_130_out, not_131_out, not_132_out, not_133_out, not_134_out, not_135_out,
       not_136_out, not_137_out, not_138_out, not_139_out, not_140_out, not_141_out, not_142_out,
       not_143_out, not_144_out, not_145_out, not_146_out, not_147_out, not_148_out, not_149_out,
       not_150_out, not_151_out, not_152_out, not_153_out, not_154_out, not_155_out, not_156_out,
       not_157_out, not_158_out, not_159_out, not_160_out, not_161_out, not_162_out, not_163_out,
       not_164_out, not_165_out, not_166_out, not_167_out, not_168_out, not_169_out, not_170_out,
       not_171_out, not_172_out, not_173_out, not_174_out, not_175_out, not_176_out, not_177_out,
       not_178_out, not_179_out, not_180_out, not_181_out, not_182_out, not_183_out, not_184_out,
       not_185_out, not_186_out, not_187_out, not_188_out, not_189_out, not_190_out, not_191_out,
       not_192_out, not_193_out, not_194_out, not_195_out, not_196_out, not_197_out, not_198_out,
       not_199_out, not_200_out, not_201_out, not_202_out, not_203_out, not_204_out, not_205_out,
       not_206_out, not_207_out, not_208_out, not_209_out, not_210_out, not_211_out, not_212_out,
       not_213_out, not_214_out, not_215_out, not_216_out, not_217_out, not_218_out, not_219_out,
       not_220_out, not_221_out, not_222_out, not_223_out, not_224_out, not_225_out, not_226_out,
       not_227_out, not_228_out, not_229_out, not_230_out, not_231_out, not_232_out, not_233_out,
       not_234_out, not_235_out, not_236_out, not_237_out, not_238_out, not_239_out, not_240_out,
       not_241_out, not_242_out, not_243_out, not_244_out, not_245_out, not_246_out, not_247_out,
       not_248_out, not_249_out, not_250_out, not_251_out, not_252_out, not_253_out, not_254_out,
       not_255_out, not_256_out, not_257_out, not_258_out, not_259_out, not_260_out, not_261_out, not_262_out;

  not not_1 (not_1_out, OP5);
  not not_2 (not_2_out, OP4);
  not not_3 (not_3_out, OP3);
  not not_4 (not_4_out, OP2);
  not not_5 (not_5_out, OP1);
  not not_6 (not_6_out, OP0);
  not not_7 (not_7_out, F5);
  not not_8 (not_8_out, F4);
  not not_9 (not_9_out, F3);
  not not_10 (not_10_out, F2);
  not not_11 (not_11_out, OP5);
  not not_12 (not_12_out, OP4);
  not not_13 (not_13_out, OP3);
  not not_14 (not_14_out, OP2);
  not not_15 (not_15_out, OP1);
  not not_16 (not_16_out, OP0);
  not not_17 (not_17_out, F4);
  not not_18 (not_18_out, F3);
  not not_19 (not_19_out, F2);
  not not_20 (not_20_out, F1);
  not not_21 (not_21_out, F0);
  not not_22 (not_22_out, OP5);
  not not_23 (not_23_out, OP4);
  not not_24 (not_24_out, OP3);
  not not_25 (not_25_out, OP2);
  not not_26 (not_26_out, OP1);
  not not_27 (not_27_out, OP0);
  not not_28 (not_28_out, F4);
  not not_29 (not_29_out, F3);
  not not_30 (not_30_out, F2);
  not not_31 (not_31_out, F1);
  not not_32 (not_32_out, OP5);
  not not_33 (not_33_out, OP4);
  not not_34 (not_34_out, OP3);
  not not_35 (not_35_out, OP2);
  not not_36 (not_36_out, OP1);
  not not_37 (not_37_out, OP0);
  not not_38 (not_38_out, F4);
  not not_39 (not_39_out, F3);
  not not_40 (not_40_out, F1);
  not not_41 (not_41_out, F0);
  not not_42 (not_42_out, OP5);
  not not_43 (not_43_out, OP4);
  not not_44 (not_44_out, OP3);
  not not_45 (not_45_out, OP2);
  not not_46 (not_46_out, OP1);
  not not_47 (not_47_out, OP0);
  not not_48 (not_48_out, F4);
  not not_49 (not_49_out, F2);
  not not_50 (not_50_out, F0);
  not not_51 (not_51_out, OP5);
  not not_52 (not_52_out, OP4);
  not not_53 (not_53_out, OP2);
  not not_54 (not_54_out, OP1);
  not not_55 (not_55_out, OP0);
  not not_56 (not_56_out, OP5);
  not not_57 (not_57_out, OP4);
  not not_58 (not_58_out, OP1);
  not not_59 (not_59_out, OP0);
  not not_60 (not_60_out, OP5);
  not not_61 (not_61_out, OP4);
  not not_62 (not_62_out, OP2);
  not not_63 (not_63_out, OP1);
  not not_64 (not_64_out, OP5);
  not not_65 (not_65_out, OP4);
  not not_66 (not_66_out, OP2);
  not not_67 (not_67_out, OP0);
  not not_68 (not_68_out, OP4);
  not not_69 (not_69_out, OP3);
  not not_70 (not_70_out, OP2);
  not not_71 (not_71_out, OP4);
  not not_72 (not_72_out, OP2);
  not not_73 (not_73_out, OP5);
  not not_74 (not_74_out, OP4);
  not not_75 (not_75_out, OP3);
  not not_76 (not_76_out, OP2);
  not not_77 (not_77_out, OP1);
  not not_78 (not_78_out, OP0);
  not not_79 (not_79_out, F4);
  not not_80 (not_80_out, F3);
  not not_81 (not_81_out, F0);
  not not_82 (not_82_out, OP4);
  not not_83 (not_83_out, OP3);
  not not_84 (not_84_out, OP1);
  not not_85 (not_85_out, OP0);
  not not_86 (not_86_out, OP5);
  not not_87 (not_87_out, OP4);
  not not_88 (not_88_out, OP3);
  not not_89 (not_89_out, OP2);
  not not_90 (not_90_out, OP1);
  not not_91 (not_91_out, OP0);
  not not_92 (not_92_out, F5);
  not not_93 (not_93_out, F4);
  not not_94 (not_94_out, F3);
  not not_95 (not_95_out, F2);
  not not_96 (not_96_out, F0);
  not not_97 (not_97_out, OP5);
  not not_98 (not_98_out, OP4);
  not not_99 (not_99_out, OP3);
  not not_100 (not_100_out, OP2);
  not not_101 (not_101_out, OP1);
  not not_102 (not_102_out, OP0);
  not not_103 (not_103_out, F4);
  not not_104 (not_104_out, F3);
  not not_105 (not_105_out, F2);
  not not_106 (not_106_out, F0);
  not not_107 (not_107_out, OP5);
  not not_108 (not_108_out, OP4);
  not not_109 (not_109_out, OP3);
  not not_110 (not_110_out, OP2);
  not not_111 (not_111_out, OP1);
  not not_112 (not_112_out, OP0);
  not not_113 (not_113_out, F4);
  not not_114 (not_114_out, F3);
  not not_115 (not_115_out, F1);
  not not_116 (not_116_out, F0);
  not not_117 (not_117_out, OP5);
  not not_118 (not_118_out, OP4);
  not not_119 (not_119_out, OP3);
  not not_120 (not_120_out, OP2);
  not not_121 (not_121_out, OP1);
  not not_122 (not_122_out, OP0);
  not not_123 (not_123_out, F4);
  not not_124 (not_124_out, F3);
  not not_125 (not_125_out, OP5);
  not not_126 (not_126_out, OP4);
  not not_127 (not_127_out, OP3);
  not not_128 (not_128_out, OP2);
  not not_129 (not_129_out, OP1);
  not not_130 (not_130_out, OP0);
  not not_131 (not_131_out, F4);
  not not_132 (not_132_out, F2);
  not not_133 (not_133_out, F0);
  not not_134 (not_134_out, OP5);
  not not_135 (not_135_out, OP4);
  not not_136 (not_136_out, OP1);
  not not_137 (not_137_out, OP0);
  not not_138 (not_138_out, OP5);
  not not_139 (not_139_out, OP4);
  not not_140 (not_140_out, OP2);
  not not_141 (not_141_out, OP0);
  not not_142 (not_142_out, OP5);
  not not_143 (not_143_out, OP4);
  not not_144 (not_144_out, OP3);
  not not_145 (not_145_out, OP2);
  not not_146 (not_146_out, OP1);
  not not_147 (not_147_out, OP0);
  not not_148 (not_148_out, F4);
  not not_149 (not_149_out, F3);
  not not_150 (not_150_out, F2);
  not not_151 (not_151_out, F1);
  not not_152 (not_152_out, F0);
  not not_153 (not_153_out, OP5);
  not not_154 (not_154_out, OP4);
  not not_155 (not_155_out, OP3);
  not not_156 (not_156_out, OP2);
  not not_157 (not_157_out, OP1);
  not not_158 (not_158_out, OP0);
  not not_159 (not_159_out, F4);
  not not_160 (not_160_out, F3);
  not not_161 (not_161_out, F2);
  not not_162 (not_162_out, F1);
  not not_163 (not_163_out, OP5);
  not not_164 (not_164_out, OP4);
  not not_165 (not_165_out, OP3);
  not not_166 (not_166_out, OP2);
  not not_167 (not_167_out, OP1);
  not not_168 (not_168_out, OP0);
  not not_169 (not_169_out, F4);
  not not_170 (not_170_out, F3);
  not not_171 (not_171_out, F2);
  not not_172 (not_172_out, F0);
  not not_173 (not_173_out, OP5);
  not not_174 (not_174_out, OP4);
  not not_175 (not_175_out, OP3);
  not not_176 (not_176_out, OP2);
  not not_177 (not_177_out, OP1);
  not not_178 (not_178_out, OP0);
  not not_179 (not_179_out, F4);
  not not_180 (not_180_out, F3);
  not not_181 (not_181_out, F1);
  not not_182 (not_182_out, F0);
  not not_183 (not_183_out, OP5);
  not not_184 (not_184_out, OP4);
  not not_185 (not_185_out, OP3);
  not not_186 (not_186_out, OP2);
  not not_187 (not_187_out, OP1);
  not not_188 (not_188_out, OP0);
  not not_189 (not_189_out, F4);
  not not_190 (not_190_out, F2);
  not not_191 (not_191_out, OP5);
  not not_192 (not_192_out, OP4);
  not not_193 (not_193_out, OP2);
  not not_194 (not_194_out, OP1);
  not not_195 (not_195_out, OP0);
  not not_196 (not_196_out, OP5);
  not not_197 (not_197_out, OP4);
  not not_198 (not_198_out, OP1);
  not not_199 (not_199_out, OP0);
  not not_200 (not_200_out, OP5);
  not not_201 (not_201_out, OP4);
  not not_202 (not_202_out, OP2);
  not not_203 (not_203_out, OP1);
  not not_204 (not_204_out, OP4);
  not not_205 (not_205_out, OP3);
  not not_206 (not_206_out, OP2);
  not not_207 (not_207_out, OP4);
  not not_208 (not_208_out, OP2);
  not not_209 (not_209_out, OP4);
  not not_210 (not_210_out, OP3);
  not not_211 (not_211_out, OP1);
  not not_212 (not_212_out, OP0);
  not not_213 (not_213_out, OP5);
  not not_214 (not_214_out, OP4);
  not not_215 (not_215_out, OP3);
  not not_216 (not_216_out, OP2);
  not not_217 (not_217_out, OP1);
  not not_218 (not_218_out, OP0);
  not not_219 (not_219_out, F4);
  not not_220 (not_220_out, F3);
  not not_221 (not_221_out, F1);
  not not_222 (not_222_out, OP5);
  not not_223 (not_223_out, OP4);
  not not_224 (not_224_out, OP3);
  not not_225 (not_225_out, OP2);
  not not_226 (not_226_out, OP1);
  not not_227 (not_227_out, OP0);
  not not_228 (not_228_out, F4);
  not not_229 (not_229_out, F3);
  not not_230 (not_230_out, OP5);
  not not_231 (not_231_out, OP4);
  not not_232 (not_232_out, OP3);
  not not_233 (not_233_out, OP2);
  not not_234 (not_234_out, OP1);
  not not_235 (not_235_out, OP0);
  not not_236 (not_236_out, F4);
  not not_237 (not_237_out, F2);
  not not_238 (not_238_out, F0);
  not not_239 (not_239_out, OP5);
  not not_240 (not_240_out, OP4);
  not not_241 (not_241_out, OP3);
  not not_242 (not_242_out, OP2);
  not not_243 (not_243_out, OP1);
  not not_244 (not_244_out, OP0);
  not not_245 (not_245_out, F4);
  not not_246 (not_246_out, F2);
  not not_247 (not_247_out, OP5);
  not not_248 (not_248_out, OP4);
  not not_249 (not_249_out, OP2);
  not not_250 (not_250_out, OP0);
  not not_251 (not_251_out, OP5);
  not not_252 (not_252_out, OP4);
  not not_253 (not_253_out, OP1);
  not not_254 (not_254_out, OP5);
  not not_255 (not_255_out, OP4);
  not not_256 (not_256_out, OP3);
  not not_257 (not_257_out, OP2);
  not not_258 (not_258_out, OP1);
  not not_259 (not_259_out, OP0);
  not not_260 (not_260_out, F4);
  not not_261 (not_261_out, F3);
  not not_262 (not_262_out, F0);
  and and_1 (and_1_out, not_1_out, not_2_out, not_3_out, not_4_out, not_5_out, not_6_out, not_7_out, not_8_out, not_9_out, not_10_out, F1, F0);
  and and_2 (and_2_out, not_11_out, not_12_out, not_13_out, not_14_out, not_15_out, not_16_out, F5, not_17_out, not_18_out, not_19_out, not_20_out, not_21_out);
  and and_3 (and_3_out, not_22_out, not_23_out, not_24_out, not_25_out, not_26_out, not_27_out, F5, not_28_out, not_29_out, not_30_out, not_31_out, F0);
  and and_4 (and_4_out, not_32_out, not_33_out, not_34_out, not_35_out, not_36_out, not_37_out, F5, not_38_out, not_39_out, F2, not_40_out, not_41_out);
  and and_5 (and_5_out, not_42_out, not_43_out, not_44_out, not_45_out, not_46_out, not_47_out, F5, not_48_out, F3, not_49_out, F1, not_50_out);
  and and_6 (and_6_out, not_51_out, not_52_out, OP3, not_53_out, not_54_out, not_55_out);
  and and_7 (and_7_out, not_56_out, not_57_out, OP3, OP2, not_58_out, not_59_out);
  and and_8 (and_8_out, not_60_out, not_61_out, OP3, not_62_out, not_63_out, OP0);
  and and_9 (and_9_out, not_64_out, not_65_out, OP3, not_66_out, OP1, not_67_out);
  and and_10 (and_10_out, OP5, not_68_out, not_69_out, not_70_out, OP1, OP0);
  and and_11 (and_11_out, OP5, not_71_out, OP3, not_72_out, OP1, OP0);
  and and_12 (and_12_out, not_73_out, not_74_out, not_75_out, not_76_out, not_77_out, not_78_out, F5, not_79_out, not_80_out, F2, F1, not_81_out);
  and and_13 (and_13_out, OP5, not_82_out, not_83_out, OP2, not_84_out, not_85_out);
  and and_14 (and_14_out, not_86_out, not_87_out, not_88_out, not_89_out, not_90_out, not_91_out, not_92_out, not_93_out, not_94_out, not_95_out, F1, not_96_out);
  and and_15 (and_15_out, not_97_out, not_98_out, not_99_out, not_100_out, not_101_out, not_102_out, F5, not_103_out, not_104_out, not_105_out, F1, not_106_out);
  and and_16 (and_16_out, not_107_out, not_108_out, not_109_out, not_110_out, not_111_out, not_112_out, F5, not_113_out, not_114_out, F2, not_115_out, not_116_out);
  and and_17 (and_17_out, not_117_out, not_118_out, not_119_out, not_120_out, not_121_out, not_122_out, F5, not_123_out, not_124_out, F2, F1, F0);
  and and_18 (and_18_out, not_125_out, not_126_out, not_127_out, not_128_out, not_129_out, not_130_out, F5, not_131_out, F3, not_132_out, F1, not_133_out);
  and and_19 (and_19_out, not_134_out, not_135_out, OP3, OP2, not_136_out, not_137_out);
  and and_20 (and_20_out, not_138_out, not_139_out, OP3, not_140_out, OP1, not_141_out);
  and and_21 (and_21_out, not_142_out, not_143_out, not_144_out, not_145_out, not_146_out, not_147_out, F5, not_148_out, not_149_out, not_150_out, not_151_out, not_152_out);
  and and_22 (and_22_out, not_153_out, not_154_out, not_155_out, not_156_out, not_157_out, not_158_out, F5, not_159_out, not_160_out, not_161_out, not_162_out, F0);
  and and_23 (and_23_out, not_163_out, not_164_out, not_165_out, not_166_out, not_167_out, not_168_out, F5, not_169_out, not_170_out, not_171_out, F1, not_172_out);
  and and_24 (and_24_out, not_173_out, not_174_out, not_175_out, not_176_out, not_177_out, not_178_out, F5, not_179_out, not_180_out, F2, not_181_out, not_182_out);
  and and_25 (and_25_out, not_183_out, not_184_out, not_185_out, not_186_out, not_187_out, not_188_out, F5, not_189_out, F3, not_190_out, F1, F0);
  and and_26 (and_26_out, not_191_out, not_192_out, OP3, not_193_out, not_194_out, not_195_out);
  and and_27 (and_27_out, not_196_out, not_197_out, OP3, OP2, not_198_out, not_199_out);
  and and_28 (and_28_out, not_200_out, not_201_out, OP3, not_202_out, not_203_out, OP0);
  and and_29 (and_29_out, OP5, not_204_out, not_205_out, not_206_out, OP1, OP0);
  and and_30 (and_30_out, OP5, not_207_out, OP3, not_208_out, OP1, OP0);
  and and_31 (and_31_out, OP5, not_209_out, not_210_out, OP2, not_211_out, not_212_out);
  and and_32 (and_32_out, not_213_out, not_214_out, not_215_out, not_216_out, not_217_out, not_218_out, F5, not_219_out, not_220_out, F2, not_221_out, F0);
  and and_33 (and_33_out, not_222_out, not_223_out, not_224_out, not_225_out, not_226_out, not_227_out, F5, not_228_out, not_229_out, F2, F1, F0);
  and and_34 (and_34_out, not_230_out, not_231_out, not_232_out, not_233_out, not_234_out, not_235_out, F5, not_236_out, F3, not_237_out, F1, not_238_out);
  and and_35 (and_35_out, not_239_out, not_240_out, not_241_out, not_242_out, not_243_out, not_244_out, F5, not_245_out, F3, not_246_out, F1, F0);
  and and_36 (and_36_out, not_247_out, not_248_out, OP3, not_249_out, OP1, not_250_out);
  and and_37 (and_37_out, not_251_out, not_252_out, OP3, OP2, not_253_out, OP0);
  and and_38 (and_38_out, not_254_out, not_255_out, not_256_out, not_257_out, not_258_out, not_259_out, F5, not_260_out, not_261_out, F2, F1, not_262_out);
  or or_1 (S1, and_14_out, and_15_out, and_16_out, and_17_out, and_18_out, and_19_out, and_20_out);
  or or_2 (S2, and_21_out, and_22_out, and_23_out, and_24_out, and_25_out, and_26_out, and_27_out, and_28_out, and_29_out, and_30_out, and_31_out);
  or or_3 (S3, and_32_out, and_33_out, and_34_out, and_35_out, and_36_out, and_37_out, and_38_out);
  or or_4 (S0, and_1_out, and_2_out, and_3_out, and_4_out, and_5_out, and_6_out, and_7_out, and_8_out, and_9_out, and_10_out, and_11_out, and_12_out, and_13_out);
endmodule

module \控制信号生成  (
  input  OP0,
  input  OP1,
  input  OP2,
  input  OP3,
  input  OP4,
  input  OP5,
  input  F0,
  input  F1,
  input  F2,
  input  F3,
  input  F4,
  input  F5,
  output MemToReg,
  output MemWrite,
  output ALU_SRC,
  output RegWrite,
  output SysCALL,
  output SignedExt,
  output RegDst,
  output BEQ,
  output BNE,
  output JR,
  output JMP,
  output JAL
);

  wire and_1_out, and_2_out, and_4_out, and_5_out, and_6_out, and_7_out, and_8_out, and_9_out, and_10_out,
       and_11_out, and_12_out, and_13_out, and_14_out, and_15_out, and_16_out, and_17_out, and_18_out,
       and_19_out, and_20_out, and_21_out, and_22_out, and_23_out, and_24_out, and_25_out, and_26_out,
       and_27_out, and_28_out, and_29_out, and_30_out, and_31_out, and_32_out, and_34_out, and_35_out,
       and_36_out, and_37_out, and_38_out, and_39_out, and_40_out, and_41_out, and_42_out, and_43_out,
       and_44_out, and_45_out, and_46_out, and_47_out, and_48_out, and_49_out, and_50_out, and_51_out,
       and_52_out, and_56_out, and_57_out, and_58_out, not_1_out, not_2_out, not_3_out, not_4_out, not_5_out,
       not_6_out, not_7_out, not_8_out, not_9_out, not_10_out, not_11_out, not_12_out, not_13_out,
       not_14_out, not_15_out, not_16_out, not_17_out, not_18_out, not_19_out, not_20_out, not_21_out,
       not_22_out, not_23_out, not_24_out, not_25_out, not_26_out, not_27_out, not_28_out, not_29_out,
       not_30_out, not_31_out, not_32_out, not_33_out, not_34_out, not_35_out, not_36_out, not_37_out,
       not_38_out, not_39_out, not_40_out, not_41_out, not_42_out, not_43_out, not_44_out, not_45_out,
       not_46_out, not_47_out, not_48_out, not_49_out, not_50_out, not_51_out, not_52_out, not_53_out,
       not_54_out, not_55_out, not_56_out, not_57_out, not_58_out, not_59_out, not_60_out, not_61_out,
       not_62_out, not_63_out, not_64_out, not_65_out, not_66_out, not_67_out, not_68_out, not_69_out,
       not_70_out, not_71_out, not_72_out, not_73_out, not_74_out, not_75_out, not_76_out, not_77_out,
       not_78_out, not_79_out, not_80_out, not_81_out, not_82_out, not_83_out, not_84_out, not_85_out,
       not_86_out, not_87_out, not_88_out, not_89_out, not_90_out, not_91_out, not_92_out, not_93_out,
       not_94_out, not_95_out, not_96_out, not_97_out, not_98_out, not_99_out, not_100_out, not_101_out,
       not_102_out, not_103_out, not_104_out, not_105_out, not_106_out, not_107_out, not_108_out,
       not_109_out, not_110_out, not_111_out, not_112_out, not_113_out, not_114_out, not_115_out,
       not_116_out, not_117_out, not_118_out, not_119_out, not_120_out, not_121_out, not_122_out,
       not_123_out, not_124_out, not_125_out, not_126_out, not_127_out, not_128_out, not_129_out,
       not_130_out, not_131_out, not_132_out, not_133_out, not_134_out, not_135_out, not_136_out,
       not_137_out, not_138_out, not_139_out, not_140_out, not_141_out, not_142_out, not_143_out,
       not_144_out, not_145_out, not_146_out, not_147_out, not_148_out, not_149_out, not_150_out,
       not_151_out, not_152_out, not_153_out, not_154_out, not_155_out, not_156_out, not_157_out,
       not_158_out, not_159_out, not_160_out, not_161_out, not_162_out, not_163_out, not_164_out,
       not_165_out, not_166_out, not_167_out, not_168_out, not_169_out, not_170_out, not_171_out,
       not_172_out, not_173_out, not_174_out, not_175_out, not_176_out, not_177_out, not_178_out,
       not_179_out, not_180_out, not_181_out, not_182_out, not_183_out, not_184_out, not_185_out,
       not_186_out, not_187_out, not_188_out, not_189_out, not_190_out, not_191_out, not_192_out,
       not_193_out, not_194_out, not_195_out, not_196_out, not_197_out, not_198_out, not_199_out,
       not_200_out, not_201_out, not_202_out, not_203_out, not_204_out, not_205_out, not_206_out,
       not_207_out, not_208_out, not_209_out, not_210_out, not_211_out, not_212_out, not_213_out,
       not_214_out, not_215_out, not_216_out, not_217_out, not_218_out, not_219_out, not_220_out,
       not_221_out, not_222_out, not_223_out, not_224_out, not_225_out, not_226_out, not_227_out,
       not_228_out, not_229_out, not_230_out, not_231_out, not_232_out, not_233_out, not_234_out,
       not_235_out, not_236_out, not_237_out, not_238_out, not_239_out, not_240_out, not_241_out,
       not_242_out, not_243_out, not_244_out, not_245_out, not_246_out, not_247_out, not_248_out,
       not_249_out, not_250_out, not_251_out, not_252_out, not_253_out, not_254_out, not_255_out,
       not_256_out, not_257_out, not_258_out, not_259_out, not_260_out, not_261_out, not_262_out,
       not_263_out, not_264_out, not_265_out, not_266_out, not_267_out, not_268_out, not_269_out,
       not_270_out, not_271_out, not_272_out, not_273_out, not_274_out, not_275_out, not_276_out,
       not_277_out, not_278_out, not_279_out, not_280_out, not_281_out, not_282_out, not_283_out,
       not_284_out, not_285_out, not_286_out, not_287_out, not_288_out, not_289_out, not_290_out,
       not_291_out, not_292_out, not_293_out, not_294_out, not_295_out, not_296_out, not_297_out,
       not_298_out, not_299_out, not_300_out, not_301_out, not_302_out, not_303_out, not_304_out,
       not_305_out, not_306_out, not_307_out, not_308_out, not_309_out, not_310_out, not_311_out,
       not_312_out, not_313_out, not_314_out, not_315_out, not_316_out, not_317_out, not_318_out,
       not_319_out, not_320_out, not_321_out, not_322_out, not_323_out, not_324_out, not_325_out,
       not_326_out, not_327_out, not_328_out, not_329_out, not_330_out, not_331_out, not_332_out,
       not_333_out, not_334_out, not_335_out, not_336_out, not_337_out, not_338_out, not_339_out,
       not_340_out, not_341_out, not_342_out, not_343_out, not_344_out, not_345_out, not_346_out,
       not_347_out, not_348_out, not_349_out, not_350_out, not_351_out, not_352_out, not_353_out,
       not_354_out, not_355_out, not_356_out, not_357_out, not_358_out, not_359_out, not_360_out,
       not_361_out, not_362_out, not_363_out, not_364_out, not_365_out, not_366_out, not_367_out,
       not_368_out, not_369_out, not_370_out, not_371_out, not_372_out, not_373_out, not_374_out,
       not_375_out, not_376_out, not_377_out, not_378_out, not_379_out, not_380_out, not_381_out,
       not_382_out, not_383_out, not_384_out, not_385_out, not_386_out, not_387_out, not_388_out,
       not_389_out, not_390_out, not_391_out, not_392_out;

  not not_1 (not_1_out, OP4);
  not not_2 (not_2_out, OP3);
  not not_3 (not_3_out, OP2);
  not not_4 (not_4_out, OP4);
  not not_5 (not_5_out, OP3);
  not not_6 (not_6_out, OP1);
  not not_7 (not_7_out, OP0);
  not not_8 (not_8_out, OP4);
  not not_9 (not_9_out, OP2);
  not not_10 (not_10_out, OP5);
  not not_11 (not_11_out, OP4);
  not not_12 (not_12_out, OP2);
  not not_13 (not_13_out, OP1);
  not not_14 (not_14_out, OP0);
  not not_15 (not_15_out, OP5);
  not not_16 (not_16_out, OP4);
  not not_17 (not_17_out, OP1);
  not not_18 (not_18_out, OP0);
  not not_19 (not_19_out, OP5);
  not not_20 (not_20_out, OP4);
  not not_21 (not_21_out, OP2);
  not not_22 (not_22_out, OP1);
  not not_23 (not_23_out, OP5);
  not not_24 (not_24_out, OP4);
  not not_25 (not_25_out, OP2);
  not not_26 (not_26_out, OP0);
  not not_27 (not_27_out, OP5);
  not not_28 (not_28_out, OP4);
  not not_29 (not_29_out, OP1);
  not not_30 (not_30_out, OP4);
  not not_31 (not_31_out, OP3);
  not not_32 (not_32_out, OP2);
  not not_33 (not_33_out, OP4);
  not not_34 (not_34_out, OP2);
  not not_35 (not_35_out, OP4);
  not not_36 (not_36_out, OP3);
  not not_37 (not_37_out, OP1);
  not not_38 (not_38_out, OP0);
  not not_39 (not_39_out, OP5);
  not not_40 (not_40_out, OP4);
  not not_41 (not_41_out, OP3);
  not not_42 (not_42_out, OP2);
  not not_43 (not_43_out, OP1);
  not not_44 (not_44_out, OP0);
  not not_45 (not_45_out, F5);
  not not_46 (not_46_out, F4);
  not not_47 (not_47_out, F3);
  not not_48 (not_48_out, F2);
  not not_49 (not_49_out, F1);
  not not_50 (not_50_out, F0);
  not not_51 (not_51_out, OP5);
  not not_52 (not_52_out, OP4);
  not not_53 (not_53_out, OP3);
  not not_54 (not_54_out, OP2);
  not not_55 (not_55_out, OP1);
  not not_56 (not_56_out, OP0);
  not not_57 (not_57_out, F5);
  not not_58 (not_58_out, F4);
  not not_59 (not_59_out, F3);
  not not_60 (not_60_out, F2);
  not not_61 (not_61_out, OP5);
  not not_62 (not_62_out, OP4);
  not not_63 (not_63_out, OP3);
  not not_64 (not_64_out, OP2);
  not not_65 (not_65_out, OP1);
  not not_66 (not_66_out, OP0);
  not not_67 (not_67_out, F5);
  not not_68 (not_68_out, F4);
  not not_69 (not_69_out, F3);
  not not_70 (not_70_out, F2);
  not not_71 (not_71_out, F0);
  not not_72 (not_72_out, OP5);
  not not_73 (not_73_out, OP4);
  not not_74 (not_74_out, OP3);
  not not_75 (not_75_out, OP2);
  not not_76 (not_76_out, OP1);
  not not_77 (not_77_out, OP0);
  not not_78 (not_78_out, F4);
  not not_79 (not_79_out, F3);
  not not_80 (not_80_out, F2);
  not not_81 (not_81_out, F1);
  not not_82 (not_82_out, F0);
  not not_83 (not_83_out, OP5);
  not not_84 (not_84_out, OP4);
  not not_85 (not_85_out, OP3);
  not not_86 (not_86_out, OP2);
  not not_87 (not_87_out, OP1);
  not not_88 (not_88_out, OP0);
  not not_89 (not_89_out, F4);
  not not_90 (not_90_out, F3);
  not not_91 (not_91_out, F2);
  not not_92 (not_92_out, F1);
  not not_93 (not_93_out, OP5);
  not not_94 (not_94_out, OP4);
  not not_95 (not_95_out, OP3);
  not not_96 (not_96_out, OP2);
  not not_97 (not_97_out, OP1);
  not not_98 (not_98_out, OP0);
  not not_99 (not_99_out, F4);
  not not_100 (not_100_out, F3);
  not not_101 (not_101_out, F2);
  not not_102 (not_102_out, F0);
  not not_103 (not_103_out, OP5);
  not not_104 (not_104_out, OP4);
  not not_105 (not_105_out, OP3);
  not not_106 (not_106_out, OP2);
  not not_107 (not_107_out, OP1);
  not not_108 (not_108_out, OP0);
  not not_109 (not_109_out, F4);
  not not_110 (not_110_out, F3);
  not not_111 (not_111_out, F1);
  not not_112 (not_112_out, F0);
  not not_113 (not_113_out, OP5);
  not not_114 (not_114_out, OP4);
  not not_115 (not_115_out, OP3);
  not not_116 (not_116_out, OP2);
  not not_117 (not_117_out, OP1);
  not not_118 (not_118_out, OP0);
  not not_119 (not_119_out, F4);
  not not_120 (not_120_out, F3);
  not not_121 (not_121_out, F1);
  not not_122 (not_122_out, OP5);
  not not_123 (not_123_out, OP4);
  not not_124 (not_124_out, OP3);
  not not_125 (not_125_out, OP2);
  not not_126 (not_126_out, OP1);
  not not_127 (not_127_out, OP0);
  not not_128 (not_128_out, F4);
  not not_129 (not_129_out, F3);
  not not_130 (not_130_out, OP5);
  not not_131 (not_131_out, OP4);
  not not_132 (not_132_out, OP3);
  not not_133 (not_133_out, OP2);
  not not_134 (not_134_out, OP1);
  not not_135 (not_135_out, OP0);
  not not_136 (not_136_out, F4);
  not not_137 (not_137_out, F2);
  not not_138 (not_138_out, F0);
  not not_139 (not_139_out, OP5);
  not not_140 (not_140_out, OP4);
  not not_141 (not_141_out, OP3);
  not not_142 (not_142_out, OP2);
  not not_143 (not_143_out, OP1);
  not not_144 (not_144_out, OP0);
  not not_145 (not_145_out, F4);
  not not_146 (not_146_out, F2);
  not not_147 (not_147_out, OP5);
  not not_148 (not_148_out, OP4);
  not not_149 (not_149_out, OP3);
  not not_150 (not_150_out, OP2);
  not not_151 (not_151_out, OP5);
  not not_152 (not_152_out, OP4);
  not not_153 (not_153_out, OP2);
  not not_154 (not_154_out, OP1);
  not not_155 (not_155_out, OP0);
  not not_156 (not_156_out, OP5);
  not not_157 (not_157_out, OP4);
  not not_158 (not_158_out, OP1);
  not not_159 (not_159_out, OP0);
  not not_160 (not_160_out, OP5);
  not not_161 (not_161_out, OP4);
  not not_162 (not_162_out, OP2);
  not not_163 (not_163_out, OP1);
  not not_164 (not_164_out, OP5);
  not not_165 (not_165_out, OP4);
  not not_166 (not_166_out, OP2);
  not not_167 (not_167_out, OP0);
  not not_168 (not_168_out, OP5);
  not not_169 (not_169_out, OP4);
  not not_170 (not_170_out, OP1);
  not not_171 (not_171_out, OP4);
  not not_172 (not_172_out, OP3);
  not not_173 (not_173_out, OP2);
  not not_174 (not_174_out, OP5);
  not not_175 (not_175_out, OP4);
  not not_176 (not_176_out, OP3);
  not not_177 (not_177_out, OP2);
  not not_178 (not_178_out, OP1);
  not not_179 (not_179_out, OP0);
  not not_180 (not_180_out, F4);
  not not_181 (not_181_out, F3);
  not not_182 (not_182_out, F0);
  not not_183 (not_183_out, OP5);
  not not_184 (not_184_out, OP4);
  not not_185 (not_185_out, OP4);
  not not_186 (not_186_out, OP3);
  not not_187 (not_187_out, OP1);
  not not_188 (not_188_out, OP0);
  not not_189 (not_189_out, OP5);
  not not_190 (not_190_out, OP4);
  not not_191 (not_191_out, OP3);
  not not_192 (not_192_out, OP2);
  not not_193 (not_193_out, OP1);
  not not_194 (not_194_out, OP0);
  not not_195 (not_195_out, F5);
  not not_196 (not_196_out, F4);
  not not_197 (not_197_out, F1);
  not not_198 (not_198_out, F0);
  not not_199 (not_199_out, OP5);
  not not_200 (not_200_out, OP4);
  not not_201 (not_201_out, OP2);
  not not_202 (not_202_out, OP1);
  not not_203 (not_203_out, OP0);
  not not_204 (not_204_out, OP5);
  not not_205 (not_205_out, OP4);
  not not_206 (not_206_out, OP2);
  not not_207 (not_207_out, OP1);
  not not_208 (not_208_out, OP5);
  not not_209 (not_209_out, OP4);
  not not_210 (not_210_out, OP2);
  not not_211 (not_211_out, OP0);
  not not_212 (not_212_out, OP4);
  not not_213 (not_213_out, OP3);
  not not_214 (not_214_out, OP2);
  not not_215 (not_215_out, OP4);
  not not_216 (not_216_out, OP2);
  not not_217 (not_217_out, OP4);
  not not_218 (not_218_out, OP3);
  not not_219 (not_219_out, OP1);
  not not_220 (not_220_out, OP0);
  not not_221 (not_221_out, OP5);
  not not_222 (not_222_out, OP4);
  not not_223 (not_223_out, OP3);
  not not_224 (not_224_out, OP2);
  not not_225 (not_225_out, OP1);
  not not_226 (not_226_out, OP0);
  not not_227 (not_227_out, F5);
  not not_228 (not_228_out, F4);
  not not_229 (not_229_out, F3);
  not not_230 (not_230_out, F2);
  not not_231 (not_231_out, F1);
  not not_232 (not_232_out, F0);
  not not_233 (not_233_out, OP5);
  not not_234 (not_234_out, OP4);
  not not_235 (not_235_out, OP3);
  not not_236 (not_236_out, OP2);
  not not_237 (not_237_out, OP1);
  not not_238 (not_238_out, OP0);
  not not_239 (not_239_out, F5);
  not not_240 (not_240_out, F4);
  not not_241 (not_241_out, F3);
  not not_242 (not_242_out, F2);
  not not_243 (not_243_out, OP5);
  not not_244 (not_244_out, OP4);
  not not_245 (not_245_out, OP3);
  not not_246 (not_246_out, OP2);
  not not_247 (not_247_out, OP1);
  not not_248 (not_248_out, OP0);
  not not_249 (not_249_out, F5);
  not not_250 (not_250_out, F4);
  not not_251 (not_251_out, F3);
  not not_252 (not_252_out, F2);
  not not_253 (not_253_out, F0);
  not not_254 (not_254_out, OP5);
  not not_255 (not_255_out, OP4);
  not not_256 (not_256_out, OP3);
  not not_257 (not_257_out, OP2);
  not not_258 (not_258_out, OP1);
  not not_259 (not_259_out, OP0);
  not not_260 (not_260_out, F4);
  not not_261 (not_261_out, F3);
  not not_262 (not_262_out, F2);
  not not_263 (not_263_out, F1);
  not not_264 (not_264_out, F0);
  not not_265 (not_265_out, OP5);
  not not_266 (not_266_out, OP4);
  not not_267 (not_267_out, OP3);
  not not_268 (not_268_out, OP2);
  not not_269 (not_269_out, OP1);
  not not_270 (not_270_out, OP0);
  not not_271 (not_271_out, F4);
  not not_272 (not_272_out, F3);
  not not_273 (not_273_out, F2);
  not not_274 (not_274_out, F1);
  not not_275 (not_275_out, OP5);
  not not_276 (not_276_out, OP4);
  not not_277 (not_277_out, OP3);
  not not_278 (not_278_out, OP2);
  not not_279 (not_279_out, OP1);
  not not_280 (not_280_out, OP0);
  not not_281 (not_281_out, F4);
  not not_282 (not_282_out, F3);
  not not_283 (not_283_out, F2);
  not not_284 (not_284_out, F0);
  not not_285 (not_285_out, OP5);
  not not_286 (not_286_out, OP4);
  not not_287 (not_287_out, OP3);
  not not_288 (not_288_out, OP2);
  not not_289 (not_289_out, OP1);
  not not_290 (not_290_out, OP0);
  not not_291 (not_291_out, F4);
  not not_292 (not_292_out, F3);
  not not_293 (not_293_out, F1);
  not not_294 (not_294_out, F0);
  not not_295 (not_295_out, OP5);
  not not_296 (not_296_out, OP4);
  not not_297 (not_297_out, OP3);
  not not_298 (not_298_out, OP2);
  not not_299 (not_299_out, OP1);
  not not_300 (not_300_out, OP0);
  not not_301 (not_301_out, F4);
  not not_302 (not_302_out, F3);
  not not_303 (not_303_out, F1);
  not not_304 (not_304_out, OP5);
  not not_305 (not_305_out, OP4);
  not not_306 (not_306_out, OP3);
  not not_307 (not_307_out, OP2);
  not not_308 (not_308_out, OP1);
  not not_309 (not_309_out, OP0);
  not not_310 (not_310_out, F4);
  not not_311 (not_311_out, F3);
  not not_312 (not_312_out, OP5);
  not not_313 (not_313_out, OP4);
  not not_314 (not_314_out, OP3);
  not not_315 (not_315_out, OP2);
  not not_316 (not_316_out, OP1);
  not not_317 (not_317_out, OP0);
  not not_318 (not_318_out, F4);
  not not_319 (not_319_out, F2);
  not not_320 (not_320_out, F0);
  not not_321 (not_321_out, OP5);
  not not_322 (not_322_out, OP4);
  not not_323 (not_323_out, OP3);
  not not_324 (not_324_out, OP2);
  not not_325 (not_325_out, OP1);
  not not_326 (not_326_out, OP0);
  not not_327 (not_327_out, F4);
  not not_328 (not_328_out, F2);
  not not_329 (not_329_out, OP5);
  not not_330 (not_330_out, OP4);
  not not_331 (not_331_out, OP3);
  not not_332 (not_332_out, OP2);
  not not_333 (not_333_out, OP1);
  not not_334 (not_334_out, OP0);
  not not_335 (not_335_out, F5);
  not not_336 (not_336_out, F4);
  not not_337 (not_337_out, F2);
  not not_338 (not_338_out, F1);
  not not_339 (not_339_out, F0);
  not not_340 (not_340_out, OP5);
  not not_341 (not_341_out, OP4);
  not not_342 (not_342_out, OP3);
  not not_343 (not_343_out, OP2);
  not not_344 (not_344_out, OP1);
  not not_345 (not_345_out, OP0);
  not not_346 (not_346_out, F4);
  not not_347 (not_347_out, F3);
  not not_348 (not_348_out, F0);
  not not_349 (not_349_out, OP5);
  not not_350 (not_350_out, OP4);
  not not_351 (not_351_out, OP3);
  not not_352 (not_352_out, OP1);
  not not_353 (not_353_out, OP0);
  not not_354 (not_354_out, OP5);
  not not_355 (not_355_out, OP4);
  not not_356 (not_356_out, OP3);
  not not_357 (not_357_out, OP1);
  not not_358 (not_358_out, OP5);
  not not_359 (not_359_out, OP4);
  not not_360 (not_360_out, OP3);
  not not_361 (not_361_out, OP2);
  not not_362 (not_362_out, OP1);
  not not_363 (not_363_out, OP0);
  not not_364 (not_364_out, F5);
  not not_365 (not_365_out, F4);
  not not_366 (not_366_out, F2);
  not not_367 (not_367_out, F1);
  not not_368 (not_368_out, F0);
  not not_369 (not_369_out, OP5);
  not not_370 (not_370_out, OP4);
  not not_371 (not_371_out, OP3);
  not not_372 (not_372_out, OP2);
  not not_373 (not_373_out, OP1);
  not not_374 (not_374_out, OP0);
  not not_375 (not_375_out, F5);
  not not_376 (not_376_out, F4);
  not not_377 (not_377_out, F2);
  not not_378 (not_378_out, F1);
  not not_379 (not_379_out, F0);
  not not_380 (not_380_out, OP5);
  not not_381 (not_381_out, OP4);
  not not_382 (not_382_out, OP3);
  not not_383 (not_383_out, OP2);
  not not_384 (not_384_out, OP0);
  not not_385 (not_385_out, OP5);
  not not_386 (not_386_out, OP4);
  not not_387 (not_387_out, OP3);
  not not_388 (not_388_out, OP2);
  not not_389 (not_389_out, OP5);
  not not_390 (not_390_out, OP4);
  not not_391 (not_391_out, OP3);
  not not_392 (not_392_out, OP2);
  and and_1 (and_1_out, OP5, not_1_out, not_2_out, not_3_out, OP1, OP0);
  and and_2 (and_2_out, OP5, not_4_out, not_5_out, OP2, not_6_out, not_7_out);
  and and_3 (MemWrite, OP5, not_8_out, OP3, not_9_out, OP1, OP0);
  and and_4 (and_4_out, not_10_out, not_11_out, OP3, not_12_out, not_13_out, not_14_out);
  and and_5 (and_5_out, not_15_out, not_16_out, OP3, OP2, not_17_out, not_18_out);
  and and_6 (and_6_out, not_19_out, not_20_out, OP3, not_21_out, not_22_out, OP0);
  and and_7 (and_7_out, not_23_out, not_24_out, OP3, not_25_out, OP1, not_26_out);
  and and_8 (and_8_out, not_27_out, not_28_out, OP3, OP2, not_29_out, OP0);
  and and_9 (and_9_out, OP5, not_30_out, not_31_out, not_32_out, OP1, OP0);
  and and_10 (and_10_out, OP5, not_33_out, OP3, not_34_out, OP1, OP0);
  and and_11 (and_11_out, OP5, not_35_out, not_36_out, OP2, not_37_out, not_38_out);
  and and_12 (and_12_out, not_39_out, not_40_out, not_41_out, not_42_out, not_43_out, not_44_out, not_45_out, not_46_out, not_47_out, not_48_out, not_49_out, not_50_out);
  and and_13 (and_13_out, not_51_out, not_52_out, not_53_out, not_54_out, not_55_out, not_56_out, not_57_out, not_58_out, not_59_out, not_60_out, F1, F0);
  and and_14 (and_14_out, not_61_out, not_62_out, not_63_out, not_64_out, not_65_out, not_66_out, not_67_out, not_68_out, not_69_out, not_70_out, F1, not_71_out);
  and and_15 (and_15_out, not_72_out, not_73_out, not_74_out, not_75_out, not_76_out, not_77_out, F5, not_78_out, not_79_out, not_80_out, not_81_out, not_82_out);
  and and_16 (and_16_out, not_83_out, not_84_out, not_85_out, not_86_out, not_87_out, not_88_out, F5, not_89_out, not_90_out, not_91_out, not_92_out, F0);
  and and_17 (and_17_out, not_93_out, not_94_out, not_95_out, not_96_out, not_97_out, not_98_out, F5, not_99_out, not_100_out, not_101_out, F1, not_102_out);
  and and_18 (and_18_out, not_103_out, not_104_out, not_105_out, not_106_out, not_107_out, not_108_out, F5, not_109_out, not_110_out, F2, not_111_out, not_112_out);
  and and_19 (and_19_out, not_113_out, not_114_out, not_115_out, not_116_out, not_117_out, not_118_out, F5, not_119_out, not_120_out, F2, not_121_out, F0);
  and and_20 (and_20_out, not_122_out, not_123_out, not_124_out, not_125_out, not_126_out, not_127_out, F5, not_128_out, not_129_out, F2, F1, F0);
  and and_21 (and_21_out, not_130_out, not_131_out, not_132_out, not_133_out, not_134_out, not_135_out, F5, not_136_out, F3, not_137_out, F1, not_138_out);
  and and_22 (and_22_out, not_139_out, not_140_out, not_141_out, not_142_out, not_143_out, not_144_out, F5, not_145_out, F3, not_146_out, F1, F0);
  and and_23 (and_23_out, not_147_out, not_148_out, not_149_out, not_150_out, OP1, OP0);
  and and_24 (and_24_out, not_151_out, not_152_out, OP3, not_153_out, not_154_out, not_155_out);
  and and_25 (and_25_out, not_156_out, not_157_out, OP3, OP2, not_158_out, not_159_out);
  and and_26 (and_26_out, not_160_out, not_161_out, OP3, not_162_out, not_163_out, OP0);
  and and_27 (and_27_out, not_164_out, not_165_out, OP3, not_166_out, OP1, not_167_out);
  and and_28 (and_28_out, not_168_out, not_169_out, OP3, OP2, not_170_out, OP0);
  and and_29 (and_29_out, OP5, not_171_out, not_172_out, not_173_out, OP1, OP0);
  and and_30 (and_30_out, not_174_out, not_175_out, not_176_out, not_177_out, not_178_out, not_179_out, F5, not_180_out, not_181_out, F2, F1, not_182_out);
  and and_31 (and_31_out, not_183_out, not_184_out, OP3, OP2, OP1, OP0);
  and and_32 (and_32_out, OP5, not_185_out, not_186_out, OP2, not_187_out, not_188_out);
  and and_33 (SysCALL, not_189_out, not_190_out, not_191_out, not_192_out, not_193_out, not_194_out, not_195_out, not_196_out, F3, F2, not_197_out, not_198_out);
  and and_34 (and_34_out, not_199_out, not_200_out, OP3, not_201_out, not_202_out, not_203_out);
  and and_35 (and_35_out, not_204_out, not_205_out, OP3, not_206_out, not_207_out, OP0);
  and and_36 (and_36_out, not_208_out, not_209_out, OP3, not_210_out, OP1, not_211_out);
  and and_37 (and_37_out, OP5, not_212_out, not_213_out, not_214_out, OP1, OP0);
  and and_38 (and_38_out, OP5, not_215_out, OP3, not_216_out, OP1, OP0);
  and and_39 (and_39_out, OP5, not_217_out, not_218_out, OP2, not_219_out, not_220_out);
  and and_40 (and_40_out, not_221_out, not_222_out, not_223_out, not_224_out, not_225_out, not_226_out, not_227_out, not_228_out, not_229_out, not_230_out, not_231_out, not_232_out);
  and and_41 (and_41_out, not_233_out, not_234_out, not_235_out, not_236_out, not_237_out, not_238_out, not_239_out, not_240_out, not_241_out, not_242_out, F1, F0);
  and and_42 (and_42_out, not_243_out, not_244_out, not_245_out, not_246_out, not_247_out, not_248_out, not_249_out, not_250_out, not_251_out, not_252_out, F1, not_253_out);
  and and_43 (and_43_out, not_254_out, not_255_out, not_256_out, not_257_out, not_258_out, not_259_out, F5, not_260_out, not_261_out, not_262_out, not_263_out, not_264_out);
  and and_44 (and_44_out, not_265_out, not_266_out, not_267_out, not_268_out, not_269_out, not_270_out, F5, not_271_out, not_272_out, not_273_out, not_274_out, F0);
  and and_45 (and_45_out, not_275_out, not_276_out, not_277_out, not_278_out, not_279_out, not_280_out, F5, not_281_out, not_282_out, not_283_out, F1, not_284_out);
  and and_46 (and_46_out, not_285_out, not_286_out, not_287_out, not_288_out, not_289_out, not_290_out, F5, not_291_out, not_292_out, F2, not_293_out, not_294_out);
  and and_47 (and_47_out, not_295_out, not_296_out, not_297_out, not_298_out, not_299_out, not_300_out, F5, not_301_out, not_302_out, F2, not_303_out, F0);
  and and_48 (and_48_out, not_304_out, not_305_out, not_306_out, not_307_out, not_308_out, not_309_out, F5, not_310_out, not_311_out, F2, F1, F0);
  and and_49 (and_49_out, not_312_out, not_313_out, not_314_out, not_315_out, not_316_out, not_317_out, F5, not_318_out, F3, not_319_out, F1, not_320_out);
  and and_50 (and_50_out, not_321_out, not_322_out, not_323_out, not_324_out, not_325_out, not_326_out, F5, not_327_out, F3, not_328_out, F1, F0);
  and and_51 (and_51_out, not_329_out, not_330_out, not_331_out, not_332_out, not_333_out, not_334_out, not_335_out, not_336_out, F3, not_337_out, not_338_out, not_339_out);
  and and_52 (and_52_out, not_340_out, not_341_out, not_342_out, not_343_out, not_344_out, not_345_out, F5, not_346_out, not_347_out, F2, F1, not_348_out);
  and and_53 (BEQ, not_349_out, not_350_out, not_351_out, OP2, not_352_out, not_353_out);
  and and_54 (BNE, not_354_out, not_355_out, not_356_out, OP2, not_357_out, OP0);
  and and_55 (JR, not_358_out, not_359_out, not_360_out, not_361_out, not_362_out, not_363_out, not_364_out, not_365_out, F3, not_366_out, not_367_out, not_368_out);
  and and_56 (and_56_out, not_369_out, not_370_out, not_371_out, not_372_out, not_373_out, not_374_out, not_375_out, not_376_out, F3, not_377_out, not_378_out, not_379_out);
  and and_57 (and_57_out, not_380_out, not_381_out, not_382_out, not_383_out, OP1, not_384_out);
  and and_58 (and_58_out, not_385_out, not_386_out, not_387_out, not_388_out, OP1, OP0);
  and and_59 (JAL, not_389_out, not_390_out, not_391_out, not_392_out, OP1, OP0);
  or or_1 (MemToReg, and_1_out, and_2_out);
  or or_2 (ALU_SRC, and_4_out, and_5_out, and_6_out, and_7_out, and_8_out, and_9_out, and_10_out, and_11_out);
  or or_3 (SignedExt, and_34_out, and_35_out, and_36_out, and_37_out, and_38_out, and_39_out);
  or or_4 (JMP, and_56_out, and_57_out, and_58_out);
  or or_5 (RegWrite, and_12_out, and_13_out, and_14_out, and_15_out, and_16_out, and_17_out, and_18_out, and_19_out, and_20_out, and_21_out, and_22_out, and_23_out, and_24_out, and_25_out, and_26_out, and_27_out, and_28_out, and_29_out, and_30_out, and_31_out, and_32_out);
  or or_6 (RegDst, and_40_out, and_41_out, and_42_out, and_43_out, and_44_out, and_45_out, and_46_out, and_47_out, and_48_out, and_49_out, and_50_out, and_51_out, and_52_out);
endmodule

module MIPS_ALU (
  input  [4:0] shamt,
  input  [31:0] X,
  input  [31:0] Y,
  input  [3:0] AluOP,
  output Equal,
  output [31:0] Result,
  output [31:0] Result_2
);

  wire [0:0] comparator_1_lt, comparator_2_lt;
  wire [31:0] adder_1_out, AND_out, divider_1_out, divider_1_rem, multiplier_1_cout, multiplier_1_out,
       NOR_out, OR_out, shifter_1_out, shifter_2_out, shifter_3_out, subtractor_1_out, XOR_out;

  assign AND_out = X & Y;  // AND_Gate AND, 32 bits wide
  assign OR_out = X | Y;  // OR_Gate OR, 32 bits wide
  Shifter #(.width(32)) shifter_1 (.in(Y), .\dist (shamt), .out(shifter_1_out));
  Shifter #(.width(32), .shift("ar")) shifter_2 (.in(Y), .\dist (shamt), .out(shifter_2_out));
  Shifter #(.width(32), .shift("lr")) shifter_3 (.in(Y), .\dist (shamt), .out(shifter_3_out));
  Multiplier #(.width(32)) multiplier_1 (.a(X), .b(Y), .out(multiplier_1_out), .cout(multiplier_1_cout));  // open: cin
  Divider #(.width(32)) divider_1 (.a(X), .b(Y), .out(divider_1_out), .rem(divider_1_rem));  // open: upper
  Adder #(.width(32)) adder_1 (.a(X), .b(Y), .out(adder_1_out));  // open: cin, cout
  Subtractor #(.width(32)) subtractor_1 (.a(X), .b(Y), .out(subtractor_1_out));  // open: bin, bout
  assign XOR_out = X ^ Y;  // XOR_Gate XOR, 32 bits wide
  assign NOR_out = ~(X | Y);  // NOR_Gate NOR, 32 bits wide
  Comparator #(.width(32)) comparator_1 (.a(X), .b(Y), .eq(Equal), .lt(comparator_1_lt[0]));  // open: gt
  Comparator #(.width(32), .mode("unsigned")) comparator_2 (.a(X), .b(Y), .lt(comparator_2_lt[0]));  // open: gt, eq
  Multiplexer #(.select(4), .width(32), .enable("false")) multiplexer_1 (
    .in0(shifter_1_out), .in1(shifter_2_out), .in2(shifter_3_out), .in3(multiplier_1_out),
    .in4(divider_1_out), .in5(adder_1_out), .in6(subtractor_1_out), .in7(AND_out), .in8(OR_out),
    .in9(XOR_out), .in10(NOR_out), .in11({{31{1'b0}}, comparator_1_lt[0]}),
    .in12({{31{1'b0}}, comparator_2_lt[0]}), .in13({32{1'b0}}), .in14({32{1'b0}}), .in15({32{1'b0}}),
    .out(Result), .sel(AluOP));
  Multiplexer #(.select(4), .width(32), .enable("false")) multiplexer_2 (
    .in0({32{1'b0}}), .in1({32{1'b0}}), .in2({32{1'b0}}), .in3(multiplier_1_cout), .in4(divider_1_rem),
    .in5({32{1'b0}}), .in6({32{1'b0}}), .in7({32{1'b0}}), .in8({32{1'b0}}), .in9({32{1'b0}}),
    .in10({32{1'b0}}), .in11({32{1'b0}}), .in12({32{1'b0}}), .in13({32{1'b0}}), .in14({32{1'b0}}),
    .in15({32{1'b0}}), .out(Result_2), .sel(AluOP));

  // Other names for the same wires on the sheet: Result2[31:0] = Result_2; S[3:0] = AluOP

  // Notes on the sheet:
  //   不要改变此引脚区域内容，也不要改变ALU封装形式
  //   输入引脚
  //   输出引脚
endmodule

module MIPS_Regifile (
  input  [31:0] Din,
  input  Clk,
  input  WE,
  input  [4:0] R1_num,
  input  [4:0] W_num,
  input  [4:0] R2_num,
  output [31:0] R1,
  output [31:0] R2
);

  // RegisterFile registerfile_1: pin names not known; wires that end beside it: Din, Clk, WE, W_num, R1_num, R2_num, R1, R2
endmodule

module \额外控制信号生成  (
  input  OP0,
  input  OP1,
  input  OP2,
  input  OP3,
  input  OP4,
  input  OP5,
  input  F0,
  input  F1,
  input  F2,
  input  F3,
  input  F4,
  input  F5,
  output LUI,
  output BGTZ,
  output LBU,
  output MFC0,
  output ERET
);

  wire not_1_out, not_2_out, not_3_out, not_4_out, not_5_out, not_6_out, not_7_out, not_8_out, not_9_out,
       not_10_out, not_11_out, not_12_out, not_13_out, not_14_out, not_15_out, not_16_out, not_17_out,
       not_18_out;

  not not_1 (not_1_out, OP5);
  not not_2 (not_2_out, OP4);
  not not_3 (not_3_out, OP5);
  not not_4 (not_4_out, OP4);
  not not_5 (not_5_out, OP3);
  not not_6 (not_6_out, OP4);
  not not_7 (not_7_out, OP3);
  not not_8 (not_8_out, OP1);
  not not_9 (not_9_out, OP0);
  not not_10 (not_10_out, OP5);
  not not_11 (not_11_out, OP3);
  not not_12 (not_12_out, OP2);
  not not_13 (not_13_out, OP1);
  not not_14 (not_14_out, OP0);
  not not_15 (not_15_out, F0);
  not not_16 (not_16_out, F1);
  not not_17 (not_17_out, F2);
  not not_18 (not_18_out, F5);
  and and_1 (LUI, not_1_out, not_2_out, OP3, OP2, OP1, OP0);
  and and_2 (BGTZ, not_3_out, not_4_out, not_5_out, OP2, OP1, OP0);
  and and_3 (LBU, OP5, not_6_out, not_7_out, OP2, not_8_out, not_9_out);
  and and_4 (MFC0, not_10_out, OP4, not_11_out, not_12_out, not_13_out, not_14_out);
  and and_5 (ERET, MFC0, not_15_out, not_16_out, not_17_out, F3, F4, not_18_out);
endmodule

module ID_EX (
  input  [1:0] forward1,
  input  CLK,
  input  [31:0] IR,
  input  [31:0] PC,
  input  RST,
  input  [1:0] forward2,
  input  EN,
  input  mtr,
  input  rd,
  input  jal,
  input  lui,
  input  lbu,
  input  rw,
  input  mw,
  input  [1:0] sys,
  input  [3:0] ALUop,
  input  alusrc,
  input  SignedExt,
  input  jmp,
  input  jr,
  input  beq,
  input  bne,
  input  bgtz,
  input  [31:0] R1,
  input  [31:0] R2,
  output [1:0] f1out,
  output [31:0] IRout,
  output [31:0] PCout,
  output [1:0] f2out,
  output mtr_2,
  output rd_2,
  output jal_2,
  output lui_2,
  output lbu_2,
  output rw_2,
  output mw_2,
  output [1:0] sysout,
  output [3:0] ALUop_2,
  output alusrc_2,
  output SignedExt_2,
  output jmp_2,
  output jr_2,
  output beq_2,
  output bne_2,
  output bgtz_2,
  output [31:0] R1_2,
  output [31:0] R2out
);

  wire EN_t, multiplexer_3_out, multiplexer_5_out, multiplexer_7_out, multiplexer_8_out, multiplexer_9_out,
       multiplexer_10_out, multiplexer_11_out, multiplexer_13_out, multiplexer_14_out, multiplexer_15_out,
       multiplexer_16_out, multiplexer_17_out, multiplexer_18_out, multiplexer_19_out;
  wire [1:0] multiplexer_20_out, multiplexer_21_out, multiplexer_22_out;
  wire [3:0] multiplexer_4_out;
  wire [31:0] multiplexer_1_out, multiplexer_2_out, multiplexer_6_out, multiplexer_12_out;

  not not_1 (EN_t, EN);
  Multiplexer #(.width(32), .enable("false")) multiplexer_1 (
    .in0(IR), .in1({32{1'b0}}), .out(multiplexer_1_out), .sel(RST));
  Multiplexer #(.width(32), .enable("false")) multiplexer_2 (
    .in0(PC), .in1({32{1'b0}}), .out(multiplexer_2_out), .sel(RST));
  Multiplexer #(.enable("false")) multiplexer_3 (.in0(mw), .in1(1'b0), .out(multiplexer_3_out), .sel(RST));
  Multiplexer #(.width(4), .enable("false")) multiplexer_4 (
    .in0(ALUop), .in1(4'b0000), .out(multiplexer_4_out), .sel(RST));
  Multiplexer #(.enable("false")) multiplexer_5 (.in0(beq), .in1(1'b0), .out(multiplexer_5_out), .sel(RST));
  Multiplexer #(.width(32), .enable("false")) multiplexer_6 (
    .in0(R1), .in1({32{1'b0}}), .out(multiplexer_6_out), .sel(RST));
  Register #(.width(32)) register_1 (.D(multiplexer_1_out), .en(EN_t), .Q(IRout), .clk(CLK));  // open: clr
  Register #(.width(32)) register_2 (.D(multiplexer_2_out), .en(EN_t), .Q(PCout), .clk(CLK));  // open: clr
  Register #(.width(1)) register_3 (.D(multiplexer_3_out), .en(EN_t), .Q(mw_2), .clk(CLK));  // open: clr
  Register #(.width(4)) register_4 (.D(multiplexer_4_out), .en(EN_t), .Q(ALUop_2), .clk(CLK));  // open: clr
  Register #(.width(1)) register_5 (.D(multiplexer_5_out), .en(EN_t), .Q(beq_2), .clk(CLK));  // open: clr
  Register #(.width(32)) register_6 (.D(multiplexer_6_out), .en(EN_t), .Q(R1_2), .clk(CLK));  // open: clr
  Multiplexer #(.enable("false")) multiplexer_7 (.in0(mtr), .in1(1'b0), .out(multiplexer_7_out), .sel(RST));
  Multiplexer #(.enable("false")) multiplexer_8 (.in0(rd), .in1(1'b0), .out(multiplexer_8_out), .sel(RST));
  Multiplexer #(.enable("false")) multiplexer_9 (.in0(alusrc), .in1(1'b0), .out(multiplexer_9_out), .sel(RST));
  Multiplexer #(.enable("false")) multiplexer_10 (.in0(SignedExt), .in1(1'b0), .out(multiplexer_10_out), .sel(RST));
  Multiplexer #(.enable("false")) multiplexer_11 (.in0(bne), .in1(1'b0), .out(multiplexer_11_out), .sel(RST));
  Multiplexer #(.width(32), .enable("false")) multiplexer_12 (
    .in0(R2), .in1({32{1'b0}}), .out(multiplexer_12_out), .sel(RST));
  Register #(.width(1)) register_7 (.D(multiplexer_7_out), .en(EN_t), .Q(mtr_2), .clk(CLK));  // open: clr
  Register #(.width(1)) register_8 (.D(multiplexer_8_out), .en(EN_t), .Q(rd_2), .clk(CLK));  // open: clr
  Register #(.width(1)) register_9 (.D(multiplexer_9_out), .en(EN_t), .Q(alusrc_2), .clk(CLK));  // open: clr
  Register #(.width(1)) register_10 (.D(multiplexer_10_out), .en(EN_t), .Q(SignedExt_2), .clk(CLK));  // open: clr
  Register #(.width(1)) register_11 (.D(multiplexer_11_out), .en(EN_t), .Q(bne_2), .clk(CLK));  // open: clr
  Register #(.width(32)) register_12 (.D(multiplexer_12_out), .en(EN_t), .Q(R2out), .clk(CLK));  // open: clr
  Multiplexer #(.enable("false")) multiplexer_13 (.in0(jal), .in1(1'b0), .out(multiplexer_13_out), .sel(RST));
  Multiplexer #(.enable("false")) multiplexer_14 (.in0(lui), .in1(1'b0), .out(multiplexer_14_out), .sel(RST));
  Multiplexer #(.enable("false")) multiplexer_15 (.in0(jmp), .in1(1'b0), .out(multiplexer_15_out), .sel(RST));
  Multiplexer #(.enable("false")) multiplexer_16 (.in0(jr), .in1(1'b0), .out(multiplexer_16_out), .sel(RST));
  Multiplexer #(.enable("false")) multiplexer_17 (.in0(bgtz), .in1(1'b0), .out(multiplexer_17_out), .sel(RST));
  Register #(.width(1)) register_13 (.D(multiplexer_13_out), .en(EN_t), .Q(jal_2), .clk(CLK));  // open: clr
  Register #(.width(1)) register_14 (.D(multiplexer_14_out), .en(EN_t), .Q(lui_2), .clk(CLK));  // open: clr
  Register #(.width(1)) register_15 (.D(multiplexer_15_out), .en(EN_t), .Q(jmp_2), .clk(CLK));  // open: clr
  Register #(.width(1)) register_16 (.D(multiplexer_16_out), .en(EN_t), .Q(jr_2), .clk(CLK));  // open: clr
  Register #(.width(1)) register_17 (.D(multiplexer_17_out), .en(EN_t), .Q(bgtz_2), .clk(CLK));  // open: clr
  Multiplexer #(.enable("false")) multiplexer_18 (.in0(lbu), .in1(1'b0), .out(multiplexer_18_out), .sel(RST));
  Multiplexer #(.enable("false")) multiplexer_19 (.in0(rw), .in1(1'b0), .out(multiplexer_19_out), .sel(RST));
  Multiplexer #(.width(2), .enable("false")) multiplexer_20 (
    .in0(sys), .in1(2'b00), .out(multiplexer_20_out), .sel(RST));
  Multiplexer #(.width(2), .enable("false")) multiplexer_21 (
    .in0(forward1), .in1(2'b00), .out(multiplexer_21_out), .sel(RST));
  Multiplexer #(.width(2), .enable("false")) multiplexer_22 (
    .in0(forward2), .in1(2'b00), .out(multiplexer_22_out), .sel(RST));
  Register #(.width(1)) register_18 (.D(multiplexer_18_out), .en(EN_t), .Q(lbu_2), .clk(CLK));  // open: clr
  Register #(.width(1)) register_19 (.D(multiplexer_19_out), .en(EN_t), .Q(rw_2), .clk(CLK));  // open: clr
  Register #(.width(2)) register_20 (.D(multiplexer_20_out), .en(EN_t), .Q(sysout), .clk(CLK));  // open: clr
  Register #(.width(2)) register_21 (.D(multiplexer_21_out), .en(EN_t), .Q(f1out), .clk(CLK));  // open: clr
  Register #(.width(2)) register_22 (.D(multiplexer_22_out), .en(EN_t), .Q(f2out), .clk(CLK));  // open: clr

  // Other names for the same wires on the sheet: ALUopout[3:0] = ALUop_2; alusrcout = alusrc_2; beqout = beq_2;
  //   bgtzout = bgtz_2; bneout = bne_2; jalout = jal_2; jmpout = jmp_2; jrout = jr_2; lbuout = lbu_2; luiout = lui_2;
  //   mtrout = mtr_2; mwout = mw_2; R1out[31:0] = R1_2; rdout = rd_2; rwout = rw_2; SExt = SignedExt;
  //   SExtout = SignedExt_2
endmodule

module IF_ID (
  input  [31:0] IR,
  input  [31:0] PC,
  input  [1:0] intnum,
  input  CLK,
  input  RST,
  input  EN,
  output [31:0] IRout,
  output [31:0] PCout,
  output [1:0] intnumout
);

  wire EN_t;
  wire [1:0] multiplexer_3_out;
  wire [31:0] multiplexer_1_out, multiplexer_2_out;

  Multiplexer #(.width(32), .enable("false")) multiplexer_1 (
    .in0(IR), .in1({32{1'b0}}), .out(multiplexer_1_out), .sel(RST));
  Multiplexer #(.width(32), .enable("false")) multiplexer_2 (
    .in0(PC), .in1({32{1'b0}}), .out(multiplexer_2_out), .sel(RST));
  Register #(.width(32)) register_1 (.D(multiplexer_1_out), .en(EN_t), .Q(IRout), .clk(CLK));  // open: clr
  Register #(.width(32)) register_2 (.D(multiplexer_2_out), .en(EN_t), .Q(PCout), .clk(CLK));  // open: clr
  not not_1 (EN_t, EN);
  Multiplexer #(.width(2), .enable("false")) multiplexer_3 (
    .in0(intnum), .in1(2'b00), .out(multiplexer_3_out), .sel(RST));
  Register #(.width(2)) register_3 (.D(multiplexer_3_out), .en(EN_t), .Q(intnumout), .clk(CLK));  // open: clr
endmodule

module EX_MEM (
  input  CLK,
  input  [31:0] IR,
  input  [31:0] PC,
  input  RST,
  input  EN,
  input  mtr,
  input  rd,
  input  jal,
  input  lui,
  input  lbu,
  input  rw,
  input  mw,
  input  sys,
  input  [31:0] result,
  input  [31:0] R2,
  output [31:0] IRout,
  output [31:0] PCout,
  output mtr_2,
  output rd_2,
  output jal_2,
  output lui_2,
  output lbu_2,
  output rw_2,
  output mw_2,
  output sysout,
  output [31:0] resultout,
  output [31:0] R2out
);

  wire EN_t, multiplexer_3_out, multiplexer_4_out, multiplexer_5_out, multiplexer_7_out, multiplexer_8_out,
       multiplexer_10_out, multiplexer_11_out, multiplexer_12_out;
  wire [31:0] multiplexer_1_out, multiplexer_2_out, multiplexer_6_out, multiplexer_9_out;

  not not_1 (EN_t, EN);
  Multiplexer #(.width(32), .enable("false")) multiplexer_1 (
    .in0(IR), .in1({32{1'b0}}), .out(multiplexer_1_out), .sel(RST));
  Multiplexer #(.width(32), .enable("false")) multiplexer_2 (
    .in0(PC), .in1({32{1'b0}}), .out(multiplexer_2_out), .sel(RST));
  Multiplexer #(.enable("false")) multiplexer_3 (.in0(mw), .in1(1'b0), .out(multiplexer_3_out), .sel(RST));
  Register #(.width(32)) register_1 (.D(multiplexer_1_out), .en(EN_t), .Q(IRout), .clk(CLK));  // open: clr
  Register #(.width(32)) register_2 (.D(multiplexer_2_out), .en(EN_t), .Q(PCout), .clk(CLK));  // open: clr
  Register #(.width(1)) register_3 (.D(multiplexer_3_out), .en(EN_t), .Q(mw_2), .clk(CLK));  // open: clr
  Multiplexer #(.enable("false")) multiplexer_4 (.in0(mtr), .in1(1'b0), .out(multiplexer_4_out), .sel(RST));
  Multiplexer #(.enable("false")) multiplexer_5 (.in0(rd), .in1(1'b0), .out(multiplexer_5_out), .sel(RST));
  Multiplexer #(.width(32), .enable("false")) multiplexer_6 (
    .in0(result), .in1({32{1'b0}}), .out(multiplexer_6_out), .sel(RST));
  Register #(.width(1)) register_4 (.D(multiplexer_4_out), .en(EN_t), .Q(mtr_2), .clk(CLK));  // open: clr
  Register #(.width(1)) register_5 (.D(multiplexer_5_out), .en(EN_t), .Q(rd_2), .clk(CLK));  // open: clr
  Register #(.width(32)) register_6 (.D(multiplexer_6_out), .en(EN_t), .Q(resultout), .clk(CLK));  // open: clr
  Multiplexer #(.enable("false")) multiplexer_7 (.in0(jal), .in1(1'b0), .out(multiplexer_7_out), .sel(RST));
  Multiplexer #(.enable("false")) multiplexer_8 (.in0(lui), .in1(1'b0), .out(multiplexer_8_out), .sel(RST));
  Multiplexer #(.width(32), .enable("false")) multiplexer_9 (
    .in0(R2), .in1({32{1'b0}}), .out(multiplexer_9_out), .sel(RST));
  Register #(.width(1)) register_7 (.D(multiplexer_7_out), .en(EN_t), .Q(jal_2), .clk(CLK));  // open: clr
  Register #(.width(1)) register_8 (.D(multiplexer_8_out), .en(EN_t), .Q(lui_2), .clk(CLK));  // open: clr
  Register #(.width(32)) register_9 (.D(multiplexer_9_out), .en(EN_t), .Q(R2out), .clk(CLK));  // open: clr
  Multiplexer #(.enable("false")) multiplexer_10 (.in0(lbu), .in1(1'b0), .out(multiplexer_10_out), .sel(RST));
  Multiplexer #(.enable("false")) multiplexer_11 (.in0(rw), .in1(1'b0), .out(multiplexer_11_out), .sel(RST));
  Multiplexer #(.enable("false")) multiplexer_12 (.in0(sys), .in1(1'b0), .out(multiplexer_12_out), .sel(RST));
  Register #(.width(1)) register_10 (.D(multiplexer_10_out), .en(EN_t), .Q(lbu_2), .clk(CLK));  // open: clr
  Register #(.width(1)) register_11 (.D(multiplexer_11_out), .en(EN_t), .Q(rw_2), .clk(CLK));  // open: clr
  Register #(.width(1)) register_12 (.D(multiplexer_12_out), .en(EN_t), .Q(sysout), .clk(CLK));  // open: clr

  // Other names for the same wires on the sheet: jalout = jal_2; lbuout = lbu_2; luiout = lui_2; mtrout = mtr_2;
  //   mwout = mw_2; rdout = rd_2; rwout = rw_2
endmodule

module MEM_WB (
  input  CLK,
  input  [31:0] IR,
  input  [31:0] PC,
  input  RST,
  input  EN,
  input  mtr,
  input  rd,
  input  jal,
  input  lui,
  input  lbu,
  input  rw,
  input  sys,
  input  [31:0] result,
  input  [31:0] MemD,
  output [31:0] IRout,
  output [31:0] PCout,
  output mtr_2,
  output rd_2,
  output jal_2,
  output lui_2,
  output lbu_2,
  output rw_2,
  output sysout,
  output [31:0] resultout,
  output [31:0] MemDout
);

  wire EN_t, multiplexer_4_out, multiplexer_5_out, multiplexer_7_out, multiplexer_8_out, multiplexer_9_out,
       multiplexer_10_out, multiplexer_11_out;
  wire [31:0] multiplexer_1_out, multiplexer_2_out, multiplexer_3_out, multiplexer_6_out;

  not not_1 (EN_t, EN);
  Multiplexer #(.width(32), .enable("false")) multiplexer_1 (
    .in0(IR), .in1({32{1'b0}}), .out(multiplexer_1_out), .sel(RST));
  Multiplexer #(.width(32), .enable("false")) multiplexer_2 (
    .in0(PC), .in1({32{1'b0}}), .out(multiplexer_2_out), .sel(RST));
  Multiplexer #(.width(32), .enable("false")) multiplexer_3 (
    .in0(result), .in1({32{1'b0}}), .out(multiplexer_3_out), .sel(RST));
  Register #(.width(32)) register_1 (.D(multiplexer_1_out), .en(EN_t), .Q(IRout), .clk(CLK));  // open: clr
  Register #(.width(32)) register_2 (.D(multiplexer_2_out), .en(EN_t), .Q(PCout), .clk(CLK));  // open: clr
  Register #(.width(32)) register_3 (.D(multiplexer_3_out), .en(EN_t), .Q(resultout), .clk(CLK));  // open: clr
  Multiplexer #(.enable("false")) multiplexer_4 (.in0(mtr), .in1(1'b0), .out(multiplexer_4_out), .sel(RST));
  Multiplexer #(.enable("false")) multiplexer_5 (.in0(rd), .in1(1'b0), .out(multiplexer_5_out), .sel(RST));
  Multiplexer #(.width(32), .enable("false")) multiplexer_6 (
    .in0(MemD), .in1({32{1'b0}}), .out(multiplexer_6_out), .sel(RST));
  Register #(.width(1)) register_4 (.D(multiplexer_4_out), .en(EN_t), .Q(mtr_2), .clk(CLK));  // open: clr
  Register #(.width(1)) register_5 (.D(multiplexer_5_out), .en(EN_t), .Q(rd_2), .clk(CLK));  // open: clr
  Register #(.width(32)) register_6 (.D(multiplexer_6_out), .en(EN_t), .Q(MemDout), .clk(CLK));  // open: clr
  Multiplexer #(.enable("false")) multiplexer_7 (.in0(jal), .in1(1'b0), .out(multiplexer_7_out), .sel(RST));
  Multiplexer #(.enable("false")) multiplexer_8 (.in0(lui), .in1(1'b0), .out(multiplexer_8_out), .sel(RST));
  Multiplexer #(.enable("false")) multiplexer_9 (.in0(sys), .in1(1'b0), .out(multiplexer_9_out), .sel(RST));
  Register #(.width(1)) register_7 (.D(multiplexer_7_out), .en(EN_t), .Q(jal_2), .clk(CLK));  // open: clr
  Register #(.width(1)) register_8 (.D(multiplexer_8_out), .en(EN_t), .Q(lui_2), .clk(CLK));  // open: clr
  Register #(.width(1)) register_9 (.D(multiplexer_9_out), .en(EN_t), .Q(sysout), .clk(CLK));  // open: clr
  Multiplexer #(.enable("false")) multiplexer_10 (.in0(lbu), .in1(1'b0), .out(multiplexer_10_out), .sel(RST));
  Multiplexer #(.enable("false")) multiplexer_11 (.in0(rw), .in1(1'b0), .out(multiplexer_11_out), .sel(RST));
  Register #(.width(1)) register_10 (.D(multiplexer_10_out), .en(EN_t), .Q(lbu_2), .clk(CLK));  // open: clr
  Register #(.width(1)) register_11 (.D(multiplexer_11_out), .en(EN_t), .Q(rw_2), .clk(CLK));  // open: clr

  // Other names for the same wires on the sheet: jalout = jal_2; lbuout = lbu_2; luiout = lui_2; mtrout = mtr_2;
  //   rdout = rd_2; rwout = rw_2
endmodule

module \重定向  (
);

  wire alus, alusEX, and_1_out, and_2_out, and_3_out, and_4_out, and_5_out, and_6_out, and_11_out,
       and_12_out, and_13_out, and_14_out, and_15_out, and_16_out, and_17_out, and_18_out, beq, beqEX, bgtz,
       bgtzEX, bne, bneEX, branch, CLK, comparator_1_eq, comparator_2_eq, comparator_3_eq, comparator_4_eq,
       comparator_5_eq, comparator_6_eq, comparator_7_eq, comparator_8_eq, comparator_9_gt, comparator_10_eq,
       condi, d_ff_1_q, d_ff_2_q, d_ff_3_q, demultiplexer_1_out1, demultiplexer_1_out2, demultiplexer_1_out3,
       equ, eret, eretex, Go, halt, IR1, IR1_q, IR2, IR2_2_q, IR2_q, IR3, jal, jalEX, jalM, jalWB, jmp,
       jmpEX, jr, jrEX, lbu, lbuEX, lbuM, lbuWB, ldEX, ldM, led, loaduse, lui, luiEX, luiM, luiWB, mfc0,
       mfcex, mtr, mtrEX, mtrM, mtrWB, mw, mwEX, mwM, nor_1_out, not_1_out, not_2_out, or_1_out, or_2_out,
       or_3_out, or_4_out, or_5_out, or_6_out, or_7_out, or_9_out, or_12_out, or_13_out, or_17_out,
       or_18_out, or_19_out, pause, PC_8_q, Rd, RdEX, RdM, RdWB, register_2_q, RST, rw, rwEX, rwM, rwWB,
       SExt, SExtEX, Sys, SysEx, SysI, SysM, SysWB, W1, W2, W3;
  wire [1:0] f1EX, f2EX, forward1, forward2, intnum, nowint, nowintex, nowintid, priority_encoder_1_out,
       register_6_q;
  wire [1:1] and_19_out, PCSrc;
  wire [3:0] aluop, id_ex_1_aluop_2;
  wire [4:0] CP0, R1_num, R2_num, W_EX, W_M, W_WB;
  wire [7:0] multiplexer_13_out;
  wire [15:0] \LoadUse次数 , \总周期数 , \插入气泡数 , \无条件分支数 , \条件分支成功数 ;
  wire [31:0] adder_1_out, ALUA, ALUB, bit_extender_1_out, bit_extender_2_out, bit_extender_3_out,
       bit_extender_4_out, bit_extender_5_out, Din, Ext, ExtEX, IREX, IRID, IRIF, IRM, IRWB, jalWBD, LedData,
       MDEX, MDWB, multiplexer_1_out, multiplexer_2_out, multiplexer_3_out, multiplexer_9_out,
       multiplexer_10_out, multiplexer_14_out, multiplexer_17_out, multiplexer_18_out, pc0, pc1, pc2, PCEX,
       PCID, PCIF, PCM, PCWB, R1ID, R2EX, R2ID, R2M, register_1_q, result, resultM, resultWB, shifter_1_out;

  Button \u_总复位  (.out(RST));
  Button _1 (.out(IR1));
  Button _2 (.out(IR2));
  Button _3 (.out(IR3));
  Button \u_继续运行  (.out(Go));
  LED led_1 (.in(W1));
  LED led_2 (.in(W2));
  LED led_3 (.in(W3));
  Hex_Digit_Display hex_digit_display_1 (.value(LedData[31:28]));  // open: dp
  Hex_Digit_Display hex_digit_display_2 (.value(LedData[23:20]));  // open: dp
  Hex_Digit_Display hex_digit_display_3 (.value(LedData[27:24]));  // open: dp
  or or_1 (or_1_out, nowintex[0], nowintex[1]);
  Multiplexer #(.select(2), .width(32), .enable("false")) multiplexer_1 (
    .in0(pc0), .in1(pc1), .in2(pc2), .in3({pc0[31:28], IREX[25:0], 2'b00}), .out(multiplexer_1_out),
    .sel({PCSrc[1], jmpEX}));
  Hex_Digit_Display hex_digit_display_4 (.value(LedData[15:12]));  // open: dp
  Hex_Digit_Display hex_digit_display_5 (.value(LedData[19:16]));  // open: dp
  Register #(.width(32)) register_1 (.D(PCEX), .en(or_1_out), .Q(register_1_q), .clk(CLK));  // open: clr
  Hex_Digit_Display hex_digit_display_6 (.value(LedData[11:8]));  // open: dp
  Hex_Digit_Display hex_digit_display_7 (.value(LedData[7:4]));  // open: dp
  Clock clock_1 (.out(CLK));
  Register #(.width(1)) register_2 (.D(eretex), .Q(register_2_q), .clk(CLK));  // open: en, clr
  Multiplexer #(.width(32), .enable("false")) multiplexer_2 (
    .in0(multiplexer_1_out), .in1(register_1_q), .out(multiplexer_2_out), .sel(register_2_q));
  Hex_Digit_Display hex_digit_display_8 (.value(LedData[3:0]));  // open: dp
  Register #(.width(32)) PC (.D(multiplexer_3_out), .en(not_1_out), .Q(PCIF), .clk(CLK), .clr(RST));
  Multiplexer #(.select(2), .width(32), .enable("false")) multiplexer_3 (
    .in0(multiplexer_2_out), .in1(32'h128), .in2(32'h1c0), .in3(32'h258), .out(multiplexer_3_out),
    .sel(intnum));
  Comparator #(.width(2)) comparator_1 (.a(forward1), .b(2'b00), .eq(comparator_1_eq));  // open: gt, lt
  Comparator #(.width(32)) comparator_2 (.a(R1ID), .b(32'h22), .eq(comparator_2_eq));  // open: gt, lt
  Comparator #(.width(32)) comparator_3 (.a(resultM), .b(32'h22), .eq(comparator_3_eq));  // open: gt, lt
  Comparator #(.width(2)) comparator_4 (.a(forward1), .b(2'b11), .eq(comparator_4_eq));  // open: gt, lt
  Comparator #(.width(2)) comparator_5 (.a(forward1), .b(2'b00), .eq(comparator_5_eq));  // open: gt, lt
  Comparator #(.width(32)) comparator_6 (.a(R1ID), .b(32'ha), .eq(comparator_6_eq));  // open: gt, lt
  Comparator #(.width(32)) comparator_7 (.a(resultM), .b(32'ha), .eq(comparator_7_eq));  // open: gt, lt
  Comparator #(.width(2)) comparator_8 (.a(forward1), .b(2'b11), .eq(comparator_8_eq));  // open: gt, lt
  // Probe on \总周期数 
  // Probe on \无条件分支数 
  // Probe on \条件分支成功数 
  // Probe on \插入气泡数 
  // Probe on \LoadUse次数 
  and and_1 (and_1_out, Sys, halt);
  and and_2 (and_2_out, Sys, ~Go, pause);  // AND_Gate
  not not_1 (not_1_out, or_3_out);
  assign bit_extender_1_out = {{16{1'b0}}, IRID[15:0]};  // Bit_Extender bit_extender_1
  assign bit_extender_2_out = {{16{IRID[15]}}, IRID[15:0]};  // Bit_Extender bit_extender_2
  and and_3 (and_3_out, comparator_1_eq, comparator_2_eq);
  and and_4 (and_4_out, comparator_3_eq, comparator_4_eq);
  and and_5 (and_5_out, comparator_5_eq, comparator_6_eq);
  and and_6 (and_6_out, comparator_7_eq, comparator_8_eq);
  // Probe on PCIF[11:0]
  or or_2 (or_2_out, and_1_out, and_2_out);
  or or_3 (or_3_out, SysI, loaduse, ldEX, ldM);
  Multiplexer #(.width(32), .enable("false")) multiplexer_4 (
    .in0(bit_extender_1_out), .in1(bit_extender_2_out), .out(Ext), .sel(SExt));
  or or_4 (or_4_out, and_3_out, and_4_out);
  or or_5 (or_5_out, and_5_out, and_6_out);
  // Probe on PCID[11:0]
  and and_7 (SysI, ~RST, or_2_out);  // AND_Gate
  ROM #(.addrWidth(10), .dataWidth(32)) rom_1 (.addr(PCIF[11:2]), .data(IRIF));  // open: sel
  and and_8 (led, or_4_out, Sys);
  and and_9 (halt, Sys, or_5_out);
  nor nor_1 (nor_1_out, halt, led);
  and and_10 (pause, nor_1_out, Sys);
  // Probe on PCEX[11:0]
  // Probe on PCM[11:0]
  or or_6 (or_6_out, RST, mfc0, branch);
  IF_ID if_id_1 (
    .IR(IRIF), .PC(PCIF), .CLK(CLK), .RST(or_6_out), .EN(or_3_out), .IRout(IRID), .PCout(PCID),
    .intnum(nowint), .intnumout(nowintid));
  // Probe on PCWB[11:0]
  Multiplexer #(.select(2), .width(5), .enable("false")) multiplexer_5 (
    .in0(IREX[20:16]), .in1(IREX[15:11]), .in2({5{1'b1}}), .in3({5{1'b1}}), .out(W_EX), .sel({jalEX, RdEX}));
  Multiplexer #(.width(5), .enable("false")) multiplexer_6 (.in0(IRID[25:21]), .in1(5'b00010), .out(R1_num), .sel(Sys));
  Multiplexer #(.width(5), .enable("false")) multiplexer_7 (.in0(IRID[20:16]), .in1(5'b00100), .out(R2_num), .sel(Sys));
  \loaduse分析  \loaduse分析_1  (
    .OP0(IRID[31:26]), .OP1(IREX[31:26]), .EX_WriteReg_num(W_EX), .Func0(IRID[5:0]), .Func1(IREX[5:0]),
    .ID_R1_num(R1_num), .ID_R2_num(R2_num), .out_8(loaduse));
  \硬布线控制器  \u_硬布线控制器_1  (
    .OP(IRID[31:26]), .Func(IRID[5:0]), .ALU_OP(aluop), .MemToReg(mtr), .MemWrite(mw), .ALU_SRC(alus),
    .RegWrite(rw), .SysCALL(Sys), .SignedExt(SExt), .RegDst(Rd), .Beq(beq), .Bne(bne), .JR(jr), .JMP(jmp),
    .JAL(jal), .LUI(lui), .BGTZ(bgtz), .LBU(lbu), .MFC0(mfc0), .ERET(eret));
  MIPS_Regifile mips_regifile_1 (
    .Din(Din), .Clk(CLK), .R1(R1ID), .R2(R2ID), .WE(rwWB), .W_num(W_WB), .R1_num(R1_num), .R2_num(R2_num));
  Multiplexer #(.select(2), .width(5), .enable("false")) multiplexer_8 (
    .in0(IRM[20:16]), .in1(IRM[15:11]), .in2({5{1'b1}}), .in3({5{1'b1}}), .out(W_M), .sel({jalM, RdM}));
  \重定向控制器  \u_重定向控制器_1  (
    .OP(IRID[31:26]), .EX_WriteReg_num(W_EX), .EX_RegWrite(rwEX), .MEM_mtr(mtrM), .MEM_WriteReg_num(W_M),
    .MEM_RegWrite(rwM), .Func(IRID[5:0]), .ID_R1_num(R1_num), .ID_R2_num(R2_num), .forward1(forward1),
    .forward2(forward2));
  Register #(.width(1)) PC_2 (.D(loaduse), .Q(ldEX), .clk(CLK));  // open: en, clr
  or or_7 (or_7_out, or_9_out, RST, mfcex, branch);
  ID_EX id_ex_1 (
    .forward1(forward1), .CLK(CLK), .IR(IRID), .PC(PCID), .RST(or_7_out), .forward2(forward2), .EN(SysEx),
    .mtr(mtr), .rd(Rd), .jal(jal), .lui(lui), .lbu(lbu), .rw(rw), .mw(mw), .sys(nowintid), .ALUop(aluop),
    .alusrc(alus), .SignedExt(SExt), .jmp(jmp), .jr(jr), .beq(beq), .bne(bne), .bgtz(bgtz), .R1(R1ID),
    .R2(R2ID), .f1out(f1EX), .IRout(IREX), .PCout(PCEX), .f2out(f2EX), .mtr_2(mtrEX), .rd_2(RdEX),
    .jal_2(jalEX), .lui_2(luiEX), .lbu_2(lbuEX), .rw_2(rwEX), .mw_2(mwEX), .sysout(nowintex),
    .ALUop_2(id_ex_1_aluop_2), .alusrc_2(alusEX), .SignedExt_2(SExtEX), .jmp_2(jmpEX), .jr_2(jrEX),
    .beq_2(beqEX), .bne_2(bneEX), .bgtz_2(bgtzEX), .R1_2(pc1), .R2out(R2EX));
  Register #(.width(1)) PC_3 (.D(ldEX), .Q(ldM), .clk(CLK));  // open: en, clr
  or or_8 (branch, jmpEX, condi);
  or or_9 (or_9_out, loaduse, ldEX, ldM);
  Register #(.width(1), .trigger("falling")) PC_4 (.D(SysI), .Q(SysEx), .clk(CLK), .clr(RST));  // open: en
  Register #(.width(2), .trigger("falling")) PC_5 (.D({eret, mfc0}), .Q({eretex, mfcex}), .clk(CLK));  // open: en, clr
  Comparator #(.width(32)) comparator_9 (.a(pc1), .b({32{1'b0}}), .gt(comparator_9_gt));  // open: eq, lt
  and and_11 (and_11_out, jmpEX, ~jrEX);  // AND_Gate
  Adder #(.width(32)) adder_1 (.a(PCEX), .b(32'h4), .out(adder_1_out));  // open: cin, cout
  Shifter #(.width(32)) shifter_1 (.in(ExtEX), .\dist (5'b00010), .out(shifter_1_out));
  Counter #(.width(16), .max('hffff)) counter_1 (
    .count(jmpEX), .Q(\无条件分支数 ), .clk(CLK), .clr(RST));  // open: load, D, carry
  Register #(.width(1), .trigger("falling")) PC_6 (.D(SysEx), .Q(SysM), .clk(CLK), .clr(RST));  // open: en
  Multiplexer #(.width(32), .enable("false")) multiplexer_9 (
    .in0(ALUB), .in1(ExtEX), .out(multiplexer_9_out), .sel(alusEX));
  and and_12 (and_12_out, beqEX, equ);
  or or_10 (condi, and_12_out, and_13_out, and_14_out);
  and and_13 (and_13_out, bneEX, ~equ);  // AND_Gate
  and and_14 (and_14_out, bgtzEX, comparator_9_gt);
  or or_11 (PCSrc[1], condi, and_11_out);
  Adder #(.width(32)) adder_2 (.a(PCIF), .b(32'h4), .out(pc0));  // open: cin, cout
  Adder #(.width(32)) adder_3 (.a(adder_1_out), .b(shifter_1_out), .out(pc2));  // open: cin, cout
  Counter #(.width(16), .max('hffff)) counter_2 (
    .count(condi), .Q(\条件分支成功数 ), .clk(CLK), .clr(RST));  // open: load, D, carry
  and and_15 (and_15_out, ~or_12_out, ~PC_8_q);  // AND_Gate
  or or_12 (or_12_out, ldEX, ldM);
  Register #(.width(1), .trigger("falling")) PC_7 (.D(SysM), .Q(SysWB), .clk(CLK), .clr(RST));  // open: en
  Register #(.width(1), .trigger("falling")) PC_8 (.D(SysWB), .Q(PC_8_q), .clk(CLK), .clr(RST));  // open: en
  MIPS_ALU mips_alu_1 (
    .shamt(IREX[10:6]), .X(ALUA), .Y(multiplexer_9_out), .AluOP(id_ex_1_aluop_2), .Equal(equ), .Result(result));  // open: Result_2
  Counter #(.width(16), .max('hffff)) counter_3 (
    .count(and_15_out), .Q(\总周期数 ), .clk(CLK), .clr(RST));  // open: load, D, carry
  or or_13 (or_13_out, ldM, ldEX, loaduse, branch);
  Counter #(.width(16), .max('hffff)) counter_4 (
    .count(or_13_out), .Q(\插入气泡数 ), .clk(CLK), .clr(RST));  // open: load, D, carry
  EX_MEM ex_mem_1 (
    .CLK(CLK), .IR(IREX), .PC(PCEX), .RST(RST), .EN(SysM), .mtr(mtrEX), .rd(RdEX), .jal(jalEX), .lui(luiEX),
    .lbu(lbuEX), .rw(rwEX), .mw(mwEX), .result(result), .R2(ALUB), .IRout(IRM), .PCout(PCM), .mtr_2(mtrM),
    .rd_2(RdM), .jal_2(jalM), .lui_2(luiM), .lbu_2(lbuM), .rw_2(rwM), .mw_2(mwM), .resultout(resultM),
    .R2out(R2M));  // open: sys, sysout
  Multiplexer #(.width(32), .enable("false")) multiplexer_10 (
    .in0(resultM), .in1({IRM[15:0], {16{1'b0}}}), .out(multiplexer_10_out), .sel(luiM));
  Counter #(.width(16), .max('hffff)) counter_5 (
    .count(loaduse), .Q(\LoadUse次数 ), .clk(CLK), .clr(RST));  // open: load, D, carry
  Multiplexer #(.select(2), .width(32), .enable("false")) multiplexer_11 (
    .in0(pc1), .in1(MDWB), .in2(resultWB), .in3(multiplexer_10_out), .out(ALUA), .sel(f1EX));
  Demultiplexer #(.select(2), .enable("false")) demultiplexer_1 (
    .out1(demultiplexer_1_out1), .out2(demultiplexer_1_out2), .out3(demultiplexer_1_out3), .in(eretex),
    .sel(nowint));  // open: out0
  Register #(.width(5)) register_3 (.D(IREX[15:11]), .en(mfcex), .Q(CP0), .clk(CLK), .clr(RST));
  // MIPS_RAM mips_ram_1: pin names not known; wires that end beside it: {{10{1'b0}}, resultM[11:2]}, R2M, mwM, CLK, RST, MDEX
  Multiplexer #(.select(2), .width(32), .enable("false")) multiplexer_12 (
    .in0(R2EX), .in1(MDWB), .in2(resultWB), .in3(multiplexer_10_out), .out(ALUB), .sel(f2EX));
  MEM_WB mem_wb_1 (
    .CLK(CLK), .IR(IRM), .PC(PCM), .RST(RST), .EN(SysWB), .mtr(mtrM), .rd(RdM), .jal(jalM), .lui(luiM),
    .lbu(lbuM), .rw(rwM), .result(resultM), .MemD(MDEX), .IRout(IRWB), .PCout(PCWB), .mtr_2(mtrWB),
    .rd_2(RdWB), .jal_2(jalWB), .lui_2(luiWB), .lbu_2(lbuWB), .rw_2(rwWB), .resultout(resultWB),
    .MemDout(MDWB));  // open: sys, sysout
  D_Flip_Flop d_ff_1 (.clk(IR3), .D(1'b1), .Q(d_ff_1_q), .reset(IR2_q));  // open: Qn, preset, en
  or or_14 (W3, IR2_q, d_ff_1_q);
  D_Flip_Flop d_ff_2 (.clk(IR2), .D(1'b1), .Q(d_ff_2_q), .reset(IR2_2_q));  // open: Qn, preset, en
  or or_15 (W2, IR2_2_q, d_ff_2_q);
  D_Flip_Flop d_ff_3 (.clk(IR1), .D(1'b1), .Q(d_ff_3_q), .reset(IR1_q));  // open: Qn, preset, en
  or or_16 (W1, IR1_q, d_ff_3_q);
  Multiplexer #(.select(2), .width(8), .enable("false")) multiplexer_13 (
    .in0(MDWB[7:0]), .in1(MDWB[15:8]), .in2(MDWB[23:16]), .in3(MDWB[31:24]), .out(multiplexer_13_out),
    .sel(resultWB[1:0]));
  or or_17 (or_17_out, d_ff_1_q, IR2_q);
  or or_18 (or_18_out, d_ff_2_q, IR2_2_q);
  or or_19 (or_19_out, d_ff_3_q, IR1_q);
  assign bit_extender_3_out = {{16{1'b0}}, IREX[15:0]};  // Bit_Extender bit_extender_3
  assign bit_extender_4_out = {{16{IREX[15]}}, IREX[15:0]};  // Bit_Extender bit_extender_4
  Multiplexer #(.width(32), .enable("false")) multiplexer_14 (
    .in0(MDWB), .in1(bit_extender_5_out), .out(multiplexer_14_out), .sel(lbuWB));
  assign bit_extender_5_out = {{24{1'b0}}, multiplexer_13_out};  // Bit_Extender bit_extender_5
  and and_16 (and_16_out, or_17_out, ~demultiplexer_1_out3);  // AND_Gate
  and and_17 (and_17_out, or_18_out, ~demultiplexer_1_out2);  // AND_Gate
  and and_18 (and_18_out, or_19_out, ~demultiplexer_1_out1);  // AND_Gate
  Multiplexer #(.width(32), .enable("false")) multiplexer_15 (
    .in0(bit_extender_3_out), .in1(bit_extender_4_out), .out(ExtEX), .sel(SExtEX));
  Comparator #(.width(32)) comparator_10 (.a(ALUA), .b(32'h22), .eq(comparator_10_eq));  // open: gt, lt
  Multiplexer #(.select(2), .width(5), .enable("false")) multiplexer_16 (
    .in0(IRWB[20:16]), .in1(IRWB[15:11]), .in2({5{1'b1}}), .in3({5{1'b1}}), .out(W_WB), .sel({jalWB, RdWB}));
  Adder #(.width(32)) adder_4 (.a(PCWB), .b(32'h4), .out(jalWBD));  // open: cin, cout
  Multiplexer #(.width(32), .enable("false")) multiplexer_17 (
    .in0(resultWB), .in1(multiplexer_14_out), .out(multiplexer_17_out), .sel(mtrWB));
  D_Flip_Flop u_IR2 (.clk(CLK), .D(and_16_out), .Q(IR2_q));  // open: Qn, preset, en, reset
  D_Flip_Flop IR2_2 (.clk(CLK), .D(and_17_out), .Q(IR2_2_q));  // open: Qn, preset, en, reset
  D_Flip_Flop u_IR1 (.clk(CLK), .D(and_18_out), .Q(IR1_q));  // open: Qn, preset, en, reset
  Register #(.width(32)) register_4 (.D(ALUB), .en(comparator_10_eq), .Q(LedData), .clk(CLK), .clr(RST));
  Multiplexer #(.width(32), .enable("false")) multiplexer_18 (
    .in0(multiplexer_17_out), .in1(jalWBD), .out(multiplexer_18_out), .sel(jalWB));
  Multiplexer #(.width(32), .enable("false")) multiplexer_19 (
    .in0(multiplexer_18_out), .in1({IRWB[15:0], {16{1'b0}}}), .out(Din), .sel(luiWB));
  Priority_Encoder #(.select(2)) priority_encoder_1 (
    .in0(1'b1), .in1(IR1_q), .in2(IR2_2_q), .in3(IR2_q), .out(priority_encoder_1_out));  // open: gs, en_out, en_in
  not not_2 (not_2_out, mfc0);
  Register #(.width(2)) register_5 (.D(priority_encoder_1_out), .en(mfc0), .Q(nowint), .clk(CLK));  // open: clr
  Register #(.width(2)) register_6 (.D(priority_encoder_1_out), .Q(register_6_q), .clk(CLK));  // open: en, clr
  and and_19 (and_19_out[1], CP0[0], not_2_out);
  assign intnum = register_6_q & {2{and_19_out[1]}};  // AND_Gate and_20, 2 bits wide

  // Other names for the same wires on the sheet: mwdata[31:0] = ALUB; R1EX[31:0] = pc1;
  //   pc3[31:2] = {pc0[31:28], IREX[25:0]}; PCSrc[0] = jmpEX; SysID = SysI

  // Notes on the sheet:
  //   中断源
  //   中断等待指示
  //   数码管输出
  //   pcout
  //   指令存储器
  //   irout
  //   contents of rom_1 (hex, n*v repeats v):
  //   40110800 20110200 20020022 112020 c 2231ffff 1620fffc 20020032 c 2008ffff 20117777 112020 20020022 c
  //   200b0010 2288826 112020 20020022 c 216bffff 1560fffa 20020032 c 200b0008 3c11fedc 3631ffff 112020
  //   20020022 c 3c11ba98 112020 c 3c117654 112020 c 3c113210 112020 c 216bffff 1560fff0 20020032 c
  //   20090000 200b0010 34118483 20120404 118c00 129400 36318281 22520404 ad310000 2328820 21290004
  //   216bffff 1560fffb 200b0020 20090000 91310000 112020 20020022 c 21290001 216bffff 1560fff9 20020032 c
  //   2011000f 112020 20020022 c 2231ffff 1e20fffb 2002000a c 40110000 ac1d0230 201d0080 27bdfffc afa40000
  //   27bdfffc afa20000 27bdfffc afa80000 27bdfffc afa90000 27bdfffc afb00000 20160003 20140006 20150001
  //   168020 108100 2149825 132020 20020022 c 1600fffa 295a022 1680fff7 8fb00000 27bd0004 8fa90000
  //   27bd0004 8fa80000 27bd0004 8fa20000 27bd0004 8fa40000 27bd0004 8c1d0230 42000018 40110800 40110000
  //   ac1d0244 201d0080 27bdfffc afa40000 27bdfffc afa20000 27bdfffc afa80000 27bdfffc afa90000 27bdfffc
  //   afb00000 20160002 20140006 20150001 168020 108100 2149825 132020 20020022 c 1600fffa 295a022
  //   1680fff7 8fb00000 27bd0004 8fa90000 27bd0004 8fa80000 27bd0004 8fa20000 27bd0004 8fa40000 27bd0004
  //   8c1d0230 42000018 40110800 40110000 ac1d0258 201d0080 27bdfffc afa40000 27bdfffc afa20000 27bdfffc
  //   afa80000 27bdfffc afa90000 27bdfffc afb00000 20160003 20140006 20150001 168020 108100 2149825 132020
  //   20020022 c 1600fffa 295a022 1680fff7 8fb00000 27bd0004 8fa90000 27bd0004 8fa80000 27bd0004 8fa20000
  //   27bd0004 8fa40000 27bd0004 8c1d0230 42000018 40110800
  //   流水调试日志用
  //   重定向分析
  //   JR
  //   JMP
  //   OP
  //   Func
  //   Beq
  //   Bne
  //   MemToReg
  //   MemWrite
  //   AluOP
  //   AluSrcB
  //   RegWrite
  //   JAL
  //   RegDst
  //   Syscall
  //   地址转移逻辑
  //   重定向选择
  //   写回值与地址计算
  //   Reset 
  //   Reset 
  //   Reset 
endmodule
module \重定向控制器  (
  input  [5:0] OP,
  input  [4:0] EX_WriteReg_num,
  input  EX_RegWrite,
  input  MEM_mtr,
  input  [4:0] MEM_WriteReg_num,
  input  MEM_RegWrite,
  input  [5:0] Func,
  input  [4:0] ID_R1_num,
  input  [4:0] ID_R2_num,
  output [1:0] forward1,
  output [1:0] forward2
);

  wire and_1_out, and_2_out, and_3_out, and_4_out, and_5_out, and_6_out, and_7_out, and_8_out, and_9_out,
       and_10_out, and_11_out, and_12_out, comparator_1_eq, comparator_2_eq, comparator_3_eq,
       comparator_4_eq, comparator_5_eq, comparator_6_eq, comparator_7_eq, comparator_8_eq, comparator_9_eq,
       comparator_10_eq, comparator_11_eq, comparator_12_eq, comparator_13_eq, comparator_14_eq,
       comparator_15_eq, comparator_16_eq, R1_Used, R2_Used;

  \源寄存器使用情况  \u_源寄存器使用情况_1  (
    .OP0(OP[0]), .OP1(OP[1]), .OP2(OP[2]), .OP3(OP[3]), .OP4(OP[4]), .OP5(OP[5]), .F0(Func[0]), .F1(Func[1]),
    .F2(Func[2]), .F3(Func[3]), .F4(Func[4]), .F5(Func[5]), .R1_Used(R1_Used), .R2_Used(R2_Used));
  Comparator #(.width(5)) comparator_1 (.a(ID_R1_num), .b({5{1'b0}}), .eq(comparator_1_eq));  // open: gt, lt
  Comparator #(.width(5)) comparator_2 (.a(EX_WriteReg_num), .b(ID_R1_num), .eq(comparator_2_eq));  // open: gt, lt
  Comparator #(.width(5)) comparator_3 (.a(ID_R1_num), .b({5{1'b0}}), .eq(comparator_3_eq));  // open: gt, lt
  Comparator #(.width(5)) comparator_4 (.a(MEM_WriteReg_num), .b(ID_R1_num), .eq(comparator_4_eq));  // open: gt, lt
  Comparator #(.width(5)) comparator_5 (.a(ID_R1_num), .b({5{1'b0}}), .eq(comparator_5_eq));  // open: gt, lt
  Comparator #(.width(5)) comparator_6 (.a(EX_WriteReg_num), .b(ID_R1_num), .eq(comparator_6_eq));  // open: gt, lt
  Comparator #(.width(5)) comparator_7 (.a(ID_R1_num), .b({5{1'b0}}), .eq(comparator_7_eq));  // open: gt, lt
  Comparator #(.width(5)) comparator_8 (.a(MEM_WriteReg_num), .b(ID_R1_num), .eq(comparator_8_eq));  // open: gt, lt
  and and_1 (and_1_out, EX_RegWrite, R1_Used, ~comparator_1_eq, comparator_2_eq);  // AND_Gate
  and and_2 (and_2_out, ~and_1_out, ~MEM_mtr, and_3_out);  // AND_Gate
  and and_3 (and_3_out, MEM_RegWrite, R1_Used, ~comparator_3_eq, comparator_4_eq);  // AND_Gate
  and and_4 (and_4_out, EX_RegWrite, R1_Used, ~comparator_5_eq, comparator_6_eq);  // AND_Gate
  and and_5 (and_5_out, ~and_4_out, MEM_mtr, and_6_out);  // AND_Gate
  and and_6 (and_6_out, MEM_RegWrite, R1_Used, ~comparator_7_eq, comparator_8_eq);  // AND_Gate
  or or_1 (forward1[1], and_1_out, and_2_out);
  or or_2 (forward1[0], and_4_out, and_5_out);
  Comparator #(.width(5)) comparator_9 (.a(ID_R2_num), .b({5{1'b0}}), .eq(comparator_9_eq));  // open: gt, lt
  Comparator #(.width(5)) comparator_10 (.a(EX_WriteReg_num), .b(ID_R2_num), .eq(comparator_10_eq));  // open: gt, lt
  Comparator #(.width(5)) comparator_11 (.a(ID_R2_num), .b({5{1'b0}}), .eq(comparator_11_eq));  // open: gt, lt
  Comparator #(.width(5)) comparator_12 (.a(MEM_WriteReg_num), .b(ID_R2_num), .eq(comparator_12_eq));  // open: gt, lt
  Comparator #(.width(5)) comparator_13 (.a(ID_R2_num), .b({5{1'b0}}), .eq(comparator_13_eq));  // open: gt, lt
  Comparator #(.width(5)) comparator_14 (.a(EX_WriteReg_num), .b(ID_R2_num), .eq(comparator_14_eq));  // open: gt, lt
  Comparator #(.width(5)) comparator_15 (.a(ID_R2_num), .b({5{1'b0}}), .eq(comparator_15_eq));  // open: gt, lt
  Comparator #(.width(5)) comparator_16 (.a(MEM_WriteReg_num), .b(ID_R2_num), .eq(comparator_16_eq));  // open: gt, lt
  and and_7 (and_7_out, EX_RegWrite, R2_Used, ~comparator_9_eq, comparator_10_eq);  // AND_Gate
  and and_8 (and_8_out, MEM_RegWrite, R2_Used, ~comparator_11_eq, comparator_12_eq);  // AND_Gate
  and and_9 (and_9_out, EX_RegWrite, R2_Used, ~comparator_13_eq, comparator_14_eq);  // AND_Gate
  and and_10 (and_10_out, MEM_RegWrite, R2_Used, ~comparator_15_eq, comparator_16_eq);  // AND_Gate
  and and_11 (and_11_out, ~and_7_out, ~MEM_mtr, and_8_out);  // AND_Gate
  and and_12 (and_12_out, ~and_9_out, MEM_mtr, and_10_out);  // AND_Gate
  or or_3 (forward2[1], and_7_out, and_11_out);
  or or_4 (forward2[0], and_9_out, and_12_out);

  // Other names for the same wires on the sheet: OP_CODE[5:0] = OP
endmodule

module \源寄存器使用情况  (
  input  OP0,
  input  OP1,
  input  OP2,
  input  OP3,
  input  OP4,
  input  OP5,
  input  F0,
  input  F1,
  input  F2,
  input  F3,
  input  F4,
  input  F5,
  output R1_Used,
  output R2_Used
);

  wire and_1_out, and_2_out, and_3_out, and_4_out, and_5_out, and_6_out, and_7_out, and_8_out, and_9_out,
       and_10_out, and_11_out, and_12_out, and_13_out, and_14_out, and_15_out, and_16_out, and_17_out,
       and_18_out, and_19_out, and_20_out, and_21_out, and_22_out, and_23_out, and_24_out, and_25_out,
       and_26_out, and_27_out, and_28_out, and_29_out, and_30_out, and_31_out, and_32_out, and_33_out,
       and_34_out, and_35_out, and_36_out, and_37_out, and_38_out, and_39_out, and_40_out, and_41_out,
       and_42_out, not_1_out, not_2_out, not_3_out, not_4_out, not_5_out, not_6_out, not_7_out, not_8_out,
       not_9_out, not_10_out, not_11_out, not_12_out, not_13_out, not_14_out, not_15_out, not_16_out,
       not_17_out, not_18_out, not_19_out, not_20_out, not_21_out, not_22_out, not_23_out, not_24_out,
       not_25_out, not_26_out, not_27_out, not_28_out, not_29_out, not_30_out, not_31_out, not_32_out,
       not_33_out, not_34_out, not_35_out, not_36_out, not_37_out, not_38_out, not_39_out, not_40_out,
       not_41_out, not_42_out, not_43_out, not_44_out, not_45_out, not_46_out, not_47_out, not_48_out,
       not_49_out, not_50_out, not_51_out, not_52_out, not_53_out, not_54_out, not_55_out, not_56_out,
       not_57_out, not_58_out, not_59_out, not_60_out, not_61_out, not_62_out, not_63_out, not_64_out,
       not_65_out, not_66_out, not_67_out, not_68_out, not_69_out, not_70_out, not_71_out, not_72_out,
       not_73_out, not_74_out, not_75_out, not_76_out, not_77_out, not_78_out, not_79_out, not_80_out,
       not_81_out, not_82_out, not_83_out, not_84_out, not_85_out, not_86_out, not_87_out, not_88_out,
       not_89_out, not_90_out, not_91_out, not_92_out, not_93_out, not_94_out, not_95_out, not_96_out,
       not_97_out, not_98_out, not_99_out, not_100_out, not_101_out, not_102_out, not_103_out, not_104_out,
       not_105_out, not_106_out, not_107_out, not_108_out, not_109_out, not_110_out, not_111_out,
       not_112_out, not_113_out, not_114_out, not_115_out, not_116_out, not_117_out, not_118_out,
       not_119_out, not_120_out, not_121_out, not_122_out, not_123_out, not_124_out, not_125_out,
       not_126_out, not_127_out, not_128_out, not_129_out, not_130_out, not_131_out, not_132_out,
       not_133_out, not_134_out, not_135_out, not_136_out, not_137_out, not_138_out, not_139_out,
       not_140_out, not_141_out, not_142_out, not_143_out, not_144_out, not_145_out, not_146_out,
       not_147_out, not_148_out, not_149_out, not_150_out, not_151_out, not_152_out, not_153_out,
       not_154_out, not_155_out, not_156_out, not_157_out, not_158_out, not_159_out, not_160_out,
       not_161_out, not_162_out, not_163_out, not_164_out, not_165_out, not_166_out, not_167_out,
       not_168_out, not_169_out, not_170_out, not_171_out, not_172_out, not_173_out, not_174_out,
       not_175_out, not_176_out, not_177_out, not_178_out, not_179_out, not_180_out, not_181_out,
       not_182_out, not_183_out, not_184_out, not_185_out, not_186_out, not_187_out, not_188_out,
       not_189_out, not_190_out, not_191_out, not_192_out, not_193_out, not_194_out, not_195_out,
       not_196_out, not_197_out, not_198_out, not_199_out, not_200_out, not_201_out, not_202_out,
       not_203_out, not_204_out, not_205_out, not_206_out, not_207_out, not_208_out, not_209_out,
       not_210_out, not_211_out, not_212_out, not_213_out, not_214_out, not_215_out, not_216_out,
       not_217_out, not_218_out, not_219_out, not_220_out, not_221_out, not_222_out, not_223_out,
       not_224_out, not_225_out, not_226_out, not_227_out, not_228_out, not_229_out, not_230_out,
       not_231_out, not_232_out, not_233_out, not_234_out, not_235_out, not_236_out, not_237_out,
       not_238_out, not_239_out, not_240_out, not_241_out, not_242_out, not_243_out, not_244_out,
       not_245_out, not_246_out, not_247_out, not_248_out, not_249_out, not_250_out, not_251_out,
       not_252_out, not_253_out, not_254_out, not_255_out, not_256_out, not_257_out, not_258_out,
       not_259_out, not_260_out, not_261_out, not_262_out, not_263_out, not_264_out, not_265_out,
       not_266_out, not_267_out, not_268_out, not_269_out, not_270_out, not_271_out, not_272_out,
       not_273_out, not_274_out, not_275_out, not_276_out, not_277_out, not_278_out, not_279_out,
       not_280_out, not_281_out, not_282_out, not_283_out, not_284_out, not_285_out, not_286_out,
       not_287_out, not_288_out, not_289_out, not_290_out, not_291_out, not_292_out, not_293_out,
       not_294_out, not_295_out, not_296_out, not_297_out, not_298_out, not_299_out, not_300_out,
       not_301_out, not_302_out, not_303_out, not_304_out, not_305_out, not_306_out, not_307_out,
       not_308_out, not_309_out, not_310_out, not_311_out, not_312_out, not_313_out, not_314_out,
       not_315_out, not_316_out, not_317_out, not_318_out, not_319_out, not_320_out;

  not not_1 (not_1_out, OP5);
  not not_2 (not_2_out, OP4);
  not not_3 (not_3_out, OP3);
  not not_4 (not_4_out, OP2);
  not not_5 (not_5_out, OP1);
  not not_6 (not_6_out, OP0);
  not not_7 (not_7_out, F5);
  not not_8 (not_8_out, F4);
  not not_9 (not_9_out, F3);
  not not_10 (not_10_out, F2);
  not not_11 (not_11_out, F1);
  not not_12 (not_12_out, F0);
  not not_13 (not_13_out, OP5);
  not not_14 (not_14_out, OP4);
  not not_15 (not_15_out, OP3);
  not not_16 (not_16_out, OP2);
  not not_17 (not_17_out, OP1);
  not not_18 (not_18_out, OP0);
  not not_19 (not_19_out, F5);
  not not_20 (not_20_out, F4);
  not not_21 (not_21_out, F3);
  not not_22 (not_22_out, F2);
  not not_23 (not_23_out, OP5);
  not not_24 (not_24_out, OP4);
  not not_25 (not_25_out, OP3);
  not not_26 (not_26_out, OP2);
  not not_27 (not_27_out, OP1);
  not not_28 (not_28_out, OP0);
  not not_29 (not_29_out, F5);
  not not_30 (not_30_out, F4);
  not not_31 (not_31_out, F3);
  not not_32 (not_32_out, F2);
  not not_33 (not_33_out, F0);
  not not_34 (not_34_out, OP5);
  not not_35 (not_35_out, OP4);
  not not_36 (not_36_out, OP3);
  not not_37 (not_37_out, OP2);
  not not_38 (not_38_out, OP1);
  not not_39 (not_39_out, OP0);
  not not_40 (not_40_out, F4);
  not not_41 (not_41_out, F3);
  not not_42 (not_42_out, F2);
  not not_43 (not_43_out, F1);
  not not_44 (not_44_out, F0);
  not not_45 (not_45_out, OP5);
  not not_46 (not_46_out, OP4);
  not not_47 (not_47_out, OP3);
  not not_48 (not_48_out, OP2);
  not not_49 (not_49_out, OP1);
  not not_50 (not_50_out, OP0);
  not not_51 (not_51_out, F4);
  not not_52 (not_52_out, F3);
  not not_53 (not_53_out, F2);
  not not_54 (not_54_out, F1);
  not not_55 (not_55_out, OP5);
  not not_56 (not_56_out, OP4);
  not not_57 (not_57_out, OP3);
  not not_58 (not_58_out, OP2);
  not not_59 (not_59_out, OP1);
  not not_60 (not_60_out, OP0);
  not not_61 (not_61_out, F4);
  not not_62 (not_62_out, F3);
  not not_63 (not_63_out, F2);
  not not_64 (not_64_out, F0);
  not not_65 (not_65_out, OP5);
  not not_66 (not_66_out, OP4);
  not not_67 (not_67_out, OP3);
  not not_68 (not_68_out, OP2);
  not not_69 (not_69_out, OP1);
  not not_70 (not_70_out, OP0);
  not not_71 (not_71_out, F4);
  not not_72 (not_72_out, F3);
  not not_73 (not_73_out, F1);
  not not_74 (not_74_out, F0);
  not not_75 (not_75_out, OP5);
  not not_76 (not_76_out, OP4);
  not not_77 (not_77_out, OP3);
  not not_78 (not_78_out, OP2);
  not not_79 (not_79_out, OP1);
  not not_80 (not_80_out, OP0);
  not not_81 (not_81_out, F4);
  not not_82 (not_82_out, F3);
  not not_83 (not_83_out, F1);
  not not_84 (not_84_out, OP5);
  not not_85 (not_85_out, OP4);
  not not_86 (not_86_out, OP3);
  not not_87 (not_87_out, OP2);
  not not_88 (not_88_out, OP1);
  not not_89 (not_89_out, OP0);
  not not_90 (not_90_out, F4);
  not not_91 (not_91_out, F3);
  not not_92 (not_92_out, OP5);
  not not_93 (not_93_out, OP4);
  not not_94 (not_94_out, OP3);
  not not_95 (not_95_out, OP2);
  not not_96 (not_96_out, OP1);
  not not_97 (not_97_out, OP0);
  not not_98 (not_98_out, F4);
  not not_99 (not_99_out, F2);
  not not_100 (not_100_out, F0);
  not not_101 (not_101_out, OP5);
  not not_102 (not_102_out, OP4);
  not not_103 (not_103_out, OP3);
  not not_104 (not_104_out, OP2);
  not not_105 (not_105_out, OP1);
  not not_106 (not_106_out, OP0);
  not not_107 (not_107_out, F4);
  not not_108 (not_108_out, F2);
  not not_109 (not_109_out, OP5);
  not not_110 (not_110_out, OP4);
  not not_111 (not_111_out, OP3);
  not not_112 (not_112_out, OP2);
  not not_113 (not_113_out, OP1);
  not not_114 (not_114_out, OP0);
  not not_115 (not_115_out, F5);
  not not_116 (not_116_out, F4);
  not not_117 (not_117_out, F2);
  not not_118 (not_118_out, F1);
  not not_119 (not_119_out, F0);
  not not_120 (not_120_out, OP5);
  not not_121 (not_121_out, OP4);
  not not_122 (not_122_out, OP3);
  not not_123 (not_123_out, OP2);
  not not_124 (not_124_out, OP1);
  not not_125 (not_125_out, OP0);
  not not_126 (not_126_out, F5);
  not not_127 (not_127_out, F4);
  not not_128 (not_128_out, F1);
  not not_129 (not_129_out, F0);
  not not_130 (not_130_out, OP5);
  not not_131 (not_131_out, OP4);
  not not_132 (not_132_out, OP3);
  not not_133 (not_133_out, OP1);
  not not_134 (not_134_out, OP0);
  not not_135 (not_135_out, OP5);
  not not_136 (not_136_out, OP4);
  not not_137 (not_137_out, OP3);
  not not_138 (not_138_out, OP1);
  not not_139 (not_139_out, OP5);
  not not_140 (not_140_out, OP4);
  not not_141 (not_141_out, OP2);
  not not_142 (not_142_out, OP1);
  not not_143 (not_143_out, OP0);
  not not_144 (not_144_out, OP5);
  not not_145 (not_145_out, OP4);
  not not_146 (not_146_out, OP1);
  not not_147 (not_147_out, OP0);
  not not_148 (not_148_out, OP5);
  not not_149 (not_149_out, OP4);
  not not_150 (not_150_out, OP2);
  not not_151 (not_151_out, OP1);
  not not_152 (not_152_out, OP5);
  not not_153 (not_153_out, OP4);
  not not_154 (not_154_out, OP2);
  not not_155 (not_155_out, OP0);
  not not_156 (not_156_out, OP5);
  not not_157 (not_157_out, OP4);
  not not_158 (not_158_out, OP1);
  not not_159 (not_159_out, OP4);
  not not_160 (not_160_out, OP3);
  not not_161 (not_161_out, OP2);
  not not_162 (not_162_out, OP4);
  not not_163 (not_163_out, OP2);
  not not_164 (not_164_out, OP5);
  not not_165 (not_165_out, OP4);
  not not_166 (not_166_out, OP3);
  not not_167 (not_167_out, OP2);
  not not_168 (not_168_out, OP1);
  not not_169 (not_169_out, OP0);
  not not_170 (not_170_out, F4);
  not not_171 (not_171_out, F3);
  not not_172 (not_172_out, F0);
  not not_173 (not_173_out, OP4);
  not not_174 (not_174_out, OP3);
  not not_175 (not_175_out, OP1);
  not not_176 (not_176_out, OP0);
  not not_177 (not_177_out, OP5);
  not not_178 (not_178_out, OP4);
  not not_179 (not_179_out, OP3);
  not not_180 (not_180_out, OP5);
  not not_181 (not_181_out, OP4);
  not not_182 (not_182_out, OP3);
  not not_183 (not_183_out, OP2);
  not not_184 (not_184_out, OP1);
  not not_185 (not_185_out, OP0);
  not not_186 (not_186_out, F5);
  not not_187 (not_187_out, F4);
  not not_188 (not_188_out, F3);
  not not_189 (not_189_out, F2);
  not not_190 (not_190_out, F1);
  not not_191 (not_191_out, F0);
  not not_192 (not_192_out, OP5);
  not not_193 (not_193_out, OP4);
  not not_194 (not_194_out, OP3);
  not not_195 (not_195_out, OP2);
  not not_196 (not_196_out, OP1);
  not not_197 (not_197_out, OP0);
  not not_198 (not_198_out, F5);
  not not_199 (not_199_out, F4);
  not not_200 (not_200_out, F3);
  not not_201 (not_201_out, F2);
  not not_202 (not_202_out, OP5);
  not not_203 (not_203_out, OP4);
  not not_204 (not_204_out, OP3);
  not not_205 (not_205_out, OP2);
  not not_206 (not_206_out, OP1);
  not not_207 (not_207_out, OP0);
  not not_208 (not_208_out, F5);
  not not_209 (not_209_out, F4);
  not not_210 (not_210_out, F3);
  not not_211 (not_211_out, F2);
  not not_212 (not_212_out, F0);
  not not_213 (not_213_out, OP5);
  not not_214 (not_214_out, OP4);
  not not_215 (not_215_out, OP3);
  not not_216 (not_216_out, OP2);
  not not_217 (not_217_out, OP1);
  not not_218 (not_218_out, OP0);
  not not_219 (not_219_out, F4);
  not not_220 (not_220_out, F3);
  not not_221 (not_221_out, F2);
  not not_222 (not_222_out, F1);
  not not_223 (not_223_out, F0);
  not not_224 (not_224_out, OP5);
  not not_225 (not_225_out, OP4);
  not not_226 (not_226_out, OP3);
  not not_227 (not_227_out, OP2);
  not not_228 (not_228_out, OP1);
  not not_229 (not_229_out, OP0);
  not not_230 (not_230_out, F4);
  not not_231 (not_231_out, F3);
  not not_232 (not_232_out, F2);
  not not_233 (not_233_out, F1);
  not not_234 (not_234_out, OP5);
  not not_235 (not_235_out, OP4);
  not not_236 (not_236_out, OP3);
  not not_237 (not_237_out, OP2);
  not not_238 (not_238_out, OP1);
  not not_239 (not_239_out, OP0);
  not not_240 (not_240_out, F4);
  not not_241 (not_241_out, F3);
  not not_242 (not_242_out, F2);
  not not_243 (not_243_out, F0);
  not not_244 (not_244_out, OP5);
  not not_245 (not_245_out, OP4);
  not not_246 (not_246_out, OP3);
  not not_247 (not_247_out, OP2);
  not not_248 (not_248_out, OP1);
  not not_249 (not_249_out, OP0);
  not not_250 (not_250_out, F4);
  not not_251 (not_251_out, F3);
  not not_252 (not_252_out, F1);
  not not_253 (not_253_out, F0);
  not not_254 (not_254_out, OP5);
  not not_255 (not_255_out, OP4);
  not not_256 (not_256_out, OP3);
  not not_257 (not_257_out, OP2);
  not not_258 (not_258_out, OP1);
  not not_259 (not_259_out, OP0);
  not not_260 (not_260_out, F4);
  not not_261 (not_261_out, F3);
  not not_262 (not_262_out, F1);
  not not_263 (not_263_out, OP5);
  not not_264 (not_264_out, OP4);
  not not_265 (not_265_out, OP3);
  not not_266 (not_266_out, OP2);
  not not_267 (not_267_out, OP1);
  not not_268 (not_268_out, OP0);
  not not_269 (not_269_out, F4);
  not not_270 (not_270_out, F3);
  not not_271 (not_271_out, OP5);
  not not_272 (not_272_out, OP4);
  not not_273 (not_273_out, OP3);
  not not_274 (not_274_out, OP2);
  not not_275 (not_275_out, OP1);
  not not_276 (not_276_out, OP0);
  not not_277 (not_277_out, F4);
  not not_278 (not_278_out, F2);
  not not_279 (not_279_out, F0);
  not not_280 (not_280_out, OP5);
  not not_281 (not_281_out, OP4);
  not not_282 (not_282_out, OP3);
  not not_283 (not_283_out, OP2);
  not not_284 (not_284_out, OP1);
  not not_285 (not_285_out, OP0);
  not not_286 (not_286_out, F4);
  not not_287 (not_287_out, F2);
  not not_288 (not_288_out, OP5);
  not not_289 (not_289_out, OP4);
  not not_290 (not_290_out, OP3);
  not not_291 (not_291_out, OP2);
  not not_292 (not_292_out, OP1);
  not not_293 (not_293_out, OP0);
  not not_294 (not_294_out, F5);
  not not_295 (not_295_out, F4);
  not not_296 (not_296_out, F1);
  not not_297 (not_297_out, F0);
  not not_298 (not_298_out, OP5);
  not not_299 (not_299_out, OP4);
  not not_300 (not_300_out, OP3);
  not not_301 (not_301_out, OP1);
  not not_302 (not_302_out, OP0);
  not not_303 (not_303_out, OP5);
  not not_304 (not_304_out, OP4);
  not not_305 (not_305_out, OP3);
  not not_306 (not_306_out, OP1);
  not not_307 (not_307_out, OP4);
  not not_308 (not_308_out, OP2);
  not not_309 (not_309_out, OP5);
  not not_310 (not_310_out, OP4);
  not not_311 (not_311_out, OP3);
  not not_312 (not_312_out, OP2);
  not not_313 (not_313_out, OP1);
  not not_314 (not_314_out, OP0);
  not not_315 (not_315_out, F4);
  not not_316 (not_316_out, F3);
  not not_317 (not_317_out, F0);
  not not_318 (not_318_out, OP5);
  not not_319 (not_319_out, OP4);
  not not_320 (not_320_out, OP3);
  and and_1 (and_1_out, not_1_out, not_2_out, not_3_out, not_4_out, not_5_out, not_6_out, not_7_out, not_8_out, not_9_out, not_10_out, not_11_out, not_12_out);
  and and_2 (and_2_out, not_13_out, not_14_out, not_15_out, not_16_out, not_17_out, not_18_out, not_19_out, not_20_out, not_21_out, not_22_out, F1, F0);
  and and_3 (and_3_out, not_23_out, not_24_out, not_25_out, not_26_out, not_27_out, not_28_out, not_29_out, not_30_out, not_31_out, not_32_out, F1, not_33_out);
  and and_4 (and_4_out, not_34_out, not_35_out, not_36_out, not_37_out, not_38_out, not_39_out, F5, not_40_out, not_41_out, not_42_out, not_43_out, not_44_out);
  and and_5 (and_5_out, not_45_out, not_46_out, not_47_out, not_48_out, not_49_out, not_50_out, F5, not_51_out, not_52_out, not_53_out, not_54_out, F0);
  and and_6 (and_6_out, not_55_out, not_56_out, not_57_out, not_58_out, not_59_out, not_60_out, F5, not_61_out, not_62_out, not_63_out, F1, not_64_out);
  and and_7 (and_7_out, not_65_out, not_66_out, not_67_out, not_68_out, not_69_out, not_70_out, F5, not_71_out, not_72_out, F2, not_73_out, not_74_out);
  and and_8 (and_8_out, not_75_out, not_76_out, not_77_out, not_78_out, not_79_out, not_80_out, F5, not_81_out, not_82_out, F2, not_83_out, F0);
  and and_9 (and_9_out, not_84_out, not_85_out, not_86_out, not_87_out, not_88_out, not_89_out, F5, not_90_out, not_91_out, F2, F1, F0);
  and and_10 (and_10_out, not_92_out, not_93_out, not_94_out, not_95_out, not_96_out, not_97_out, F5, not_98_out, F3, not_99_out, F1, not_100_out);
  and and_11 (and_11_out, not_101_out, not_102_out, not_103_out, not_104_out, not_105_out, not_106_out, F5, not_107_out, F3, not_108_out, F1, F0);
  and and_12 (and_12_out, not_109_out, not_110_out, not_111_out, not_112_out, not_113_out, not_114_out, not_115_out, not_116_out, F3, not_117_out, not_118_out, not_119_out);
  and and_13 (and_13_out, not_120_out, not_121_out, not_122_out, not_123_out, not_124_out, not_125_out, not_126_out, not_127_out, F3, F2, not_128_out, not_129_out);
  and and_14 (and_14_out, not_130_out, not_131_out, not_132_out, OP2, not_133_out, not_134_out);
  and and_15 (and_15_out, not_135_out, not_136_out, not_137_out, OP2, not_138_out, OP0);
  and and_16 (and_16_out, not_139_out, not_140_out, OP3, not_141_out, not_142_out, not_143_out);
  and and_17 (and_17_out, not_144_out, not_145_out, OP3, OP2, not_146_out, not_147_out);
  and and_18 (and_18_out, not_148_out, not_149_out, OP3, not_150_out, not_151_out, OP0);
  and and_19 (and_19_out, not_152_out, not_153_out, OP3, not_154_out, OP1, not_155_out);
  and and_20 (and_20_out, not_156_out, not_157_out, OP3, OP2, not_158_out, OP0);
  and and_21 (and_21_out, OP5, not_159_out, not_160_out, not_161_out, OP1, OP0);
  and and_22 (and_22_out, OP5, not_162_out, OP3, not_163_out, OP1, OP0);
  and and_23 (and_23_out, not_164_out, not_165_out, not_166_out, not_167_out, not_168_out, not_169_out, F5, not_170_out, not_171_out, F2, F1, not_172_out);
  and and_24 (and_24_out, OP5, not_173_out, not_174_out, OP2, not_175_out, not_176_out);
  and and_25 (and_25_out, not_177_out, not_178_out, not_179_out, OP2, OP1, OP0);
  and and_26 (and_26_out, not_180_out, not_181_out, not_182_out, not_183_out, not_184_out, not_185_out, not_186_out, not_187_out, not_188_out, not_189_out, not_190_out, not_191_out);
  and and_27 (and_27_out, not_192_out, not_193_out, not_194_out, not_195_out, not_196_out, not_197_out, not_198_out, not_199_out, not_200_out, not_201_out, F1, F0);
  and and_28 (and_28_out, not_202_out, not_203_out, not_204_out, not_205_out, not_206_out, not_207_out, not_208_out, not_209_out, not_210_out, not_211_out, F1, not_212_out);
  and and_29 (and_29_out, not_213_out, not_214_out, not_215_out, not_216_out, not_217_out, not_218_out, F5, not_219_out, not_220_out, not_221_out, not_222_out, not_223_out);
  and and_30 (and_30_out, not_224_out, not_225_out, not_226_out, not_227_out, not_228_out, not_229_out, F5, not_230_out, not_231_out, not_232_out, not_233_out, F0);
  and and_31 (and_31_out, not_234_out, not_235_out, not_236_out, not_237_out, not_238_out, not_239_out, F5, not_240_out, not_241_out, not_242_out, F1, not_243_out);
  and and_32 (and_32_out, not_244_out, not_245_out, not_246_out, not_247_out, not_248_out, not_249_out, F5, not_250_out, not_251_out, F2, not_252_out, not_253_out);
  and and_33 (and_33_out, not_254_out, not_255_out, not_256_out, not_257_out, not_258_out, not_259_out, F5, not_260_out, not_261_out, F2, not_262_out, F0);
  and and_34 (and_34_out, not_263_out, not_264_out, not_265_out, not_266_out, not_267_out, not_268_out, F5, not_269_out, not_270_out, F2, F1, F0);
  and and_35 (and_35_out, not_271_out, not_272_out, not_273_out, not_274_out, not_275_out, not_276_out, F5, not_277_out, F3, not_278_out, F1, not_279_out);
  and and_36 (and_36_out, not_280_out, not_281_out, not_282_out, not_283_out, not_284_out, not_285_out, F5, not_286_out, F3, not_287_out, F1, F0);
  and and_37 (and_37_out, not_288_out, not_289_out, not_290_out, not_291_out, not_292_out, not_293_out, not_294_out, not_295_out, F3, F2, not_296_out, not_297_out);
  and and_38 (and_38_out, not_298_out, not_299_out, not_300_out, OP2, not_301_out, not_302_out);
  and and_39 (and_39_out, not_303_out, not_304_out, not_305_out, OP2, not_306_out, OP0);
  and and_40 (and_40_out, OP5, not_307_out, OP3, not_308_out, OP1, OP0);
  and and_41 (and_41_out, not_309_out, not_310_out, not_311_out, not_312_out, not_313_out, not_314_out, F5, not_315_out, not_316_out, F2, F1, not_317_out);
  and and_42 (and_42_out, not_318_out, not_319_out, not_320_out, OP2, OP1, OP0);
  or or_1 (R1_Used, and_1_out, and_2_out, and_3_out, and_4_out, and_5_out, and_6_out, and_7_out, and_8_out, and_9_out, and_10_out, and_11_out, and_12_out, and_13_out, and_14_out, and_15_out, and_16_out, and_17_out, and_18_out, and_19_out, and_20_out, and_21_out, and_22_out, and_23_out, and_24_out, and_25_out);
  or or_2 (R2_Used, and_26_out, and_27_out, and_28_out, and_29_out, and_30_out, and_31_out, and_32_out, and_33_out, and_34_out, and_35_out, and_36_out, and_37_out, and_38_out, and_39_out, and_40_out, and_41_out, and_42_out);
endmodule

module \loaduse分析  (
  input  [5:0] OP0,
  input  [5:0] OP1,
  input  [4:0] EX_WriteReg_num,
  input  [5:0] Func0,
  input  [5:0] Func1,
  input  [4:0] ID_R1_num,
  input  [4:0] ID_R2_num,
  output out_8
);

  wire and_1_out, and_2_out, and_3_out, and_4_out, comparator_1_eq, comparator_2_eq, comparator_3_eq,
       comparator_4_eq, comparator_5_eq, comparator_6_eq, or_1_out, or_2_out, R1_Used, R2_Used;

  \源寄存器使用情况  \u_源寄存器使用情况_1  (
    .OP0(OP0[0]), .OP1(OP0[1]), .OP2(OP0[2]), .OP3(OP0[3]), .OP4(OP0[4]), .OP5(OP0[5]), .F0(Func0[0]),
    .F1(Func0[1]), .F2(Func0[2]), .F3(Func0[3]), .F4(Func0[4]), .F5(Func0[5]), .R1_Used(R1_Used),
    .R2_Used(R2_Used));
  Comparator #(.width(6)) comparator_1 (.a(OP1), .b(6'b100011), .eq(comparator_1_eq));  // open: gt, lt
  Comparator #(.width(6)) comparator_2 (.a(OP1), .b(6'b100100), .eq(comparator_2_eq));  // open: gt, lt
  Comparator #(.width(5)) comparator_3 (.a(ID_R1_num), .b(EX_WriteReg_num), .eq(comparator_3_eq));  // open: gt, lt
  Comparator #(.width(6)) comparator_4 (.a(OP1), .b(6'b100011), .eq(comparator_4_eq));  // open: gt, lt
  Comparator #(.width(6)) comparator_5 (.a(OP1), .b(6'b100100), .eq(comparator_5_eq));  // open: gt, lt
  Comparator #(.width(5)) comparator_6 (.a(ID_R2_num), .b(EX_WriteReg_num), .eq(comparator_6_eq));  // open: gt, lt
  or or_1 (or_1_out, comparator_1_eq, comparator_2_eq);
  and and_1 (and_1_out, R1_Used, comparator_3_eq);
  or or_2 (or_2_out, comparator_4_eq, comparator_5_eq);
  and and_2 (and_2_out, R2_Used, comparator_6_eq);
  and and_3 (and_3_out, or_1_out, and_1_out);
  and and_4 (and_4_out, or_2_out, and_2_out);
  or or_3 (out_8, and_3_out, and_4_out);

  // Other names for the same wires on the sheet: loaduse = out_8
endmodule
