// Logisim project cpu.circ as structural Verilog: 12 circuits, main circuit cpu
module cpu (
);

  wire alu_1_equal, bubble, clear_IDEX, \continue , en_IFID, enable, jumped, RST, sysEn, T;
  wire [1:0] pipeexmem_1_out_14_2, pipeidex_1_out_11_2, pipeidex_1_out_11_3, pipememwb_1_controlout_2,
       redirect_1_redirect, redirect_1_redirect_2;
  wire [4:0] mips_ram_1_p9_2, multiplexer_2_out, multiplexer_3_out, multiplexer_5_out, multiplexer_9_out,
       multiplexer_10_out, multiplexer_11_out, multiplexer_14_out, pipeexmem_1_out_12_2, registerfile_1_p6;
  wire [7:0] multiplexer_13_out;
  wire [23:0] adder_1_out_2, \总周期数 , \无条件分支指令数 , \有条件分支成功跳转 , \有条件分支指令数 ;
  wire [31:0] adder_1_out, alu_1_result, alui_1_x, alui_1_y, bit_extender_1_out, bit_extender_2_out,
       mips_ram_1_p8, mips_ram_1_p9, multiplexer_1_out, multiplexer_6_out, multiplexer_7_out,
       multiplexer_8_out, multiplexer_12_out, pc_1_out_13, pipeexmem_1_out_11, pipeexmem_1_out_11_2,
       pipeexmem_1_out_11_3, pipeexmem_1_out_11_4, pipeexmem_1_out_11_5, pipeexmem_1_out_12,
       pipeexmem_1_out_14, pipeexmem_1_out_15, pipeexmem_1_out_16, pipeexmem_1_pcout, pipeidex_1_out_10,
       pipeidex_1_out_11, pipeidex_1_out_12, pipeidex_1_out_13, pipeifid_1_out_6, pipeifid_1_out_7,
       pipememwb_1_alurout, pipememwb_1_controlout, pipememwb_1_pcout, pipememwb_1_rsout, registerfile_1_p7,
       registerfile_1_p8, registerfile_1_p9, rom_1_data, SyscallOut;
  wire [31:10] controller_1_rbread;
  wire [31:0] pipeexmem_1_out_11_open;  // unused outputs

  Clock clock_1 (.out(T));
  Button \u_总复位  (.out(RST));
  Button button_1 (.out(\continue ));
  PC pc_1 (
    .in_2(multiplexer_6_out), .in_3(registerfile_1_p9[25:0]), .in_4(registerfile_1_p9[15:0]),
    .in_5(pipeidex_1_out_11_2), .in_6(alu_1_equal), .in_7(RST), .in_8(enable), .in_9(T),
    .in_10(pipeidex_1_out_11[15]), .out_13(pc_1_out_13), .out_14(\总周期数 ), .out_15(\无条件分支指令数 ),
    .out_16(\有条件分支指令数 ), .out_17(\有条件分支成功跳转 ), .in_11(pipeidex_1_out_11[12]), .jumped(jumped),
    .in_12(bubble), .in_1(pipeidex_1_out_10));
  and and_1 (en_IFID, enable, ~bubble);  // AND_Gate
  or or_1 (clear_IDEX, jumped, bubble);
  or or_2 (enable, \continue , sysEn);
  Hex_Digit_Display hex_digit_display_1 (.value(SyscallOut[27:24]));  // open: dp
  Hex_Digit_Display hex_digit_display_2 (.value(SyscallOut[31:28]));  // open: dp
  Hex_Digit_Display hex_digit_display_3 (.value(SyscallOut[23:20]));  // open: dp
  Hex_Digit_Display hex_digit_display_4 (.value(SyscallOut[19:16]));  // open: dp
  ROM #(.addrWidth(24), .dataWidth(32)) rom_1 (.addr(pc_1_out_13[25:2]), .data(rom_1_data));  // open: sel
  // Probe on pc_1_out_13
  Hex_Digit_Display hex_digit_display_5 (.value(SyscallOut[11:8]));  // open: dp
  Hex_Digit_Display hex_digit_display_6 (.value(SyscallOut[15:12]));  // open: dp
  Controller controller_1 (
    .instruction(pipeifid_1_out_6), .MemW(controller_1_rbread[18]), .rW(controller_1_rbread[21:20]),
    .aluop(controller_1_rbread[31:28]), .rWE(controller_1_rbread[22]), .alux(controller_1_rbread[27:26]),
    .aluy(controller_1_rbread[25:23]), .rW_2(controller_1_rbread[19]), .PCW(controller_1_rbread[17:16]),
    .J(controller_1_rbread[15]), .nLBU(controller_1_rbread[13]), .Sys1(controller_1_rbread[14]),
    .BLTZ(controller_1_rbread[12]), .rARead(controller_1_rbread[11]), .rBRead(controller_1_rbread[10]));
  PipeIFID pipeifid_1 (
    .in_1(T), .in_2(en_IFID), .in_3(jumped), .in_4(rom_1_data), .in_5(pc_1_out_13), .out_6(pipeifid_1_out_6),
    .out_7(pipeifid_1_out_7));
  Hex_Digit_Display hex_digit_display_7 (.value(SyscallOut[3:0]));  // open: dp
  Hex_Digit_Display hex_digit_display_8 (.value(SyscallOut[7:4]));  // open: dp
  Multiplexer #(.width(32), .enable("false")) multiplexer_1 (
    .in0(pipememwb_1_rsout), .in1(pipememwb_1_alurout), .out(multiplexer_1_out),
    .sel(pipememwb_1_controlout[19]));
  Bubble bubble_1 (
    .rARead(controller_1_rbread[11]), .rBRead(controller_1_rbread[10]), .rA(multiplexer_2_out),
    .rB(registerfile_1_p6), .rWE_EX(pipeidex_1_out_11[22]), .rW_EX(multiplexer_5_out), .bubble(bubble),
    .instr_EX(registerfile_1_p9));
  Multiplexer #(.width(5), .enable("false")) multiplexer_2 (
    .in0(pipeifid_1_out_6[25:21]), .in1(5'b00010), .out(multiplexer_2_out), .sel(controller_1_rbread[14]));
  Multiplexer #(.select(2), .width(5), .enable("false")) multiplexer_3 (
    .in0(mips_ram_1_p9_2), .in2(mips_ram_1_p9[20:16]), .in3({5{1'b1}}), .out(multiplexer_3_out),
    .sel(pipememwb_1_controlout_2));  // open: in1
  // Probe on {controller_1_rbread, {10{1'b0}}}
  // Probe on pipeifid_1_out_6
  // Probe on pipeifid_1_out_7
  // RegisterFile registerfile_1: pin names not known; wires that end beside it: multiplexer_1_out, T, pipememwb_1_controlout[22], multiplexer_3_out, multiplexer_2_out, registerfile_1_p6, registerfile_1_p7, registerfile_1_p8, registerfile_1_p9
  Multiplexer #(.width(5), .enable("false")) multiplexer_4 (
    .in0(pipeifid_1_out_6[20:16]), .in1(5'b00100), .out(registerfile_1_p6), .sel(controller_1_rbread[14]));
  // Probe on \总周期数 
  // Probe on \无条件分支指令数 
  // Probe on \有条件分支指令数 
  // Probe on \有条件分支成功跳转 
  PipeIDEX pipeidex_1 (
    .in_1(T), .in_3(clear_IDEX), .in_4(pipeifid_1_out_6), .in_5(pipeifid_1_out_7),
    .in_6({controller_1_rbread, {10{1'b0}}}), .out_10(pipeidex_1_out_10), .out_9(registerfile_1_p9),
    .out_11({pipeidex_1_out_11[31:22], pipeidex_1_out_11_3, pipeidex_1_out_11[19:18], pipeidex_1_out_11_2, pipeidex_1_out_11[15:0]}),
    .in_2(enable), .in_7(registerfile_1_p7), .in_8(registerfile_1_p8), .out_12(pipeidex_1_out_12),
    .out_13(pipeidex_1_out_13));
  Multiplexer #(.select(2), .width(5), .enable("false")) multiplexer_5 (
    .in0(registerfile_1_p9[15:11]), .in2(registerfile_1_p9[20:16]), .in3({5{1'b1}}), .out(multiplexer_5_out),
    .sel(pipeidex_1_out_11_3));  // open: in1
  Multiplexer #(.select(2), .width(32), .enable("false")) multiplexer_6 (
    .in0(pipeidex_1_out_12), .in1(multiplexer_8_out), .in2(pipeexmem_1_out_11), .in3(pipeexmem_1_out_11),
    .out(multiplexer_6_out), .sel(redirect_1_redirect_2));
  Multiplexer #(.select(2), .width(32), .enable("false")) multiplexer_7 (
    .in0(pipeidex_1_out_13), .in1(multiplexer_8_out), .in2(pipeexmem_1_out_11), .in3(pipeexmem_1_out_11),
    .out(multiplexer_7_out), .sel(redirect_1_redirect));
  Syscall syscall_1 (
    .in_1(multiplexer_6_out), .in_2(multiplexer_7_out), .in_3(pipeidex_1_out_11[14]), .in_4(T), .in_5(RST),
    .out_7(sysEn), .out_8(SyscallOut), .in_6(\continue ));
  Multiplexer #(.width(32), .enable("false")) multiplexer_8 (
    .in0(pipememwb_1_rsout), .in1(pipememwb_1_alurout), .out(multiplexer_8_out),
    .sel(pipememwb_1_controlout[19]));
  Redirect redirect_1 (
    .rARead(pipeidex_1_out_11[11]), .rBRead(pipeidex_1_out_11[10]), .rA(multiplexer_9_out),
    .rB(multiplexer_10_out), .rWE_EX(pipeexmem_1_out_14[22]), .rW_ME(multiplexer_11_out),
    .rWE_EX_2(pipememwb_1_controlout[22]), .rW_WB(multiplexer_14_out),
    .redirect({redirect_1_redirect_2[1], redirect_1_redirect[1], redirect_1_redirect_2[0], redirect_1_redirect[0]}));
  Multiplexer #(.width(5), .enable("false")) multiplexer_9 (
    .in0(registerfile_1_p9[25:21]), .in1(5'b00010), .out(multiplexer_9_out), .sel(pipeidex_1_out_11[14]));
  AluI alui_1 (
    .instruction(registerfile_1_p9), .AluX(pipeidex_1_out_11[27:26]), .AluY(pipeidex_1_out_11[25:23]),
    .rS(multiplexer_6_out), .rT(multiplexer_7_out), .PC(pipeidex_1_out_10), .X(alui_1_x), .Y(alui_1_y));
  Multiplexer #(.width(5), .enable("false")) multiplexer_10 (
    .in0(registerfile_1_p9[20:16]), .in1(5'b00100), .out(multiplexer_10_out), .sel(pipeidex_1_out_11[14]));
  // Probe on {pipeidex_1_out_11[31:22], pipeidex_1_out_11_3, pipeidex_1_out_11[19:18], pipeidex_1_out_11_2, pipeidex_1_out_11[15:0]}
  // Probe on registerfile_1_p9
  // Probe on pipeidex_1_out_10
  Alu alu_1 (
    .X(alui_1_x), .Y(alui_1_y), .AluOP(pipeidex_1_out_11[31:28]), .Equal(alu_1_equal), .Result(alu_1_result));  // open: Signed_Overflow, UnSigned_Overflow, Result_2
  PipeEXMEM pipeexmem_1 (
    .in_1(T), .in_2(enable), .in_3(1'b0), .in_4(registerfile_1_p9),
    .in_6({pipeidex_1_out_11[31:22], pipeidex_1_out_11_3, pipeidex_1_out_11[19:18], pipeidex_1_out_11_2, pipeidex_1_out_11[15:0]}),
    .in_7(multiplexer_6_out),
    .out_12({pipeexmem_1_out_12[31:16], pipeexmem_1_out_12_2, pipeexmem_1_out_12[10:0]}),
    .out_14({pipeexmem_1_out_14[31:22], pipeexmem_1_out_14_2, pipeexmem_1_out_14[19:0]}),
    .out_15(pipeexmem_1_out_15), .in_9(alu_1_result),
    .out_11({pipeexmem_1_out_11_5[31], pipeexmem_1_out_11[31], pipeexmem_1_out_11_4[31], pipeexmem_1_out_11_2[31], pipeexmem_1_out_11_3[31], pipeexmem_1_out_11_2[31], pipeexmem_1_out_11_3[31], pipeexmem_1_out_11_2[31], pipeexmem_1_out_11_4[31], pipeexmem_1_out_11_open[31], pipeexmem_1_out_11_2[31], pipeexmem_1_out_11_3[31], pipeexmem_1_out_11_2[31], pipeexmem_1_out_11_3[31], pipeexmem_1_out_11_2[31], pipeexmem_1_out_11_4[31], pipeexmem_1_out_11_5[30], pipeexmem_1_out_11[30], pipeexmem_1_out_11_4[30], pipeexmem_1_out_11_2[30], pipeexmem_1_out_11_3[30], pipeexmem_1_out_11_2[30], pipeexmem_1_out_11_3[30], pipeexmem_1_out_11_2[30], pipeexmem_1_out_11_4[30], pipeexmem_1_out_11_open[30], pipeexmem_1_out_11_2[30], pipeexmem_1_out_11_3[30], pipeexmem_1_out_11_2[30], pipeexmem_1_out_11_3[30], pipeexmem_1_out_11_2[30], pipeexmem_1_out_11_4[30], pipeexmem_1_out_11_5[29], pipeexmem_1_out_11[29], pipeexmem_1_out_11_4[29], pipeexmem_1_out_11_2[29], pipeexmem_1_out_11_3[29], pipeexmem_1_out_11_2[29], pipeexmem_1_out_11_3[29], pipeexmem_1_out_11_2[29], pipeexmem_1_out_11_4[29], pipeexmem_1_out_11_open[29], pipeexmem_1_out_11_2[29], pipeexmem_1_out_11_3[29], pipeexmem_1_out_11_2[29], pipeexmem_1_out_11_3[29], pipeexmem_1_out_11_2[29], pipeexmem_1_out_11_4[29], pipeexmem_1_out_11_5[28], pipeexmem_1_out_11[28], pipeexmem_1_out_11_4[28], pipeexmem_1_out_11_2[28], pipeexmem_1_out_11_3[28], pipeexmem_1_out_11_2[28], pipeexmem_1_out_11_3[28], pipeexmem_1_out_11_2[28], pipeexmem_1_out_11_4[28], pipeexmem_1_out_11_open[28], pipeexmem_1_out_11_2[28], pipeexmem_1_out_11_3[28], pipeexmem_1_out_11_2[28], pipeexmem_1_out_11_3[28], pipeexmem_1_out_11_2[28], pipeexmem_1_out_11_4[28], pipeexmem_1_out_11_5[27], pipeexmem_1_out_11[27], pipeexmem_1_out_11_4[27], pipeexmem_1_out_11_2[27], pipeexmem_1_out_11_3[27], pipeexmem_1_out_11_2[27], pipeexmem_1_out_11_3[27], pipeexmem_1_out_11_2[27], pipeexmem_1_out_11_4[27], pipeexmem_1_out_11_open[27], pipeexmem_1_out_11_2[27], pipeexmem_1_out_11_3[27], pipeexmem_1_out_11_2[27], pipeexmem_1_out_11_3[27], pipeexmem_1_out_11_2[27], pipeexmem_1_out_11_4[27], pipeexmem_1_out_11_5[26], pipeexmem_1_out_11[26], pipeexmem_1_out_11_4[26], pipeexmem_1_out_11_2[26], pipeexmem_1_out_11_3[26], pipeexmem_1_out_11_2[26], pipeexmem_1_out_11_3[26], pipeexmem_1_out_11_2[26], pipeexmem_1_out_11_4[26], pipeexmem_1_out_11_open[26], pipeexmem_1_out_11_2[26], pipeexmem_1_out_11_3[26], pipeexmem_1_out_11_2[26], pipeexmem_1_out_11_3[26], pipeexmem_1_out_11_2[26], pipeexmem_1_out_11_4[26], pipeexmem_1_out_11_5[25], pipeexmem_1_out_11[25], pipeexmem_1_out_11_4[25], pipeexmem_1_out_11_2[25], pipeexmem_1_out_11_3[25], pipeexmem_1_out_11_2[25], pipeexmem_1_out_11_3[25], pipeexmem_1_out_11_2[25], pipeexmem_1_out_11_4[25], pipeexmem_1_out_11_open[25], pipeexmem_1_out_11_2[25], pipeexmem_1_out_11_3[25], pipeexmem_1_out_11_2[25], pipeexmem_1_out_11_3[25], pipeexmem_1_out_11_2[25], pipeexmem_1_out_11_4[25], pipeexmem_1_out_11_5[24], pipeexmem_1_out_11[24], pipeexmem_1_out_11_4[24], pipeexmem_1_out_11_2[24], pipeexmem_1_out_11_3[24], pipeexmem_1_out_11_2[24], pipeexmem_1_out_11_3[24], pipeexmem_1_out_11_2[24], pipeexmem_1_out_11_4[24], pipeexmem_1_out_11_open[24], pipeexmem_1_out_11_2[24], pipeexmem_1_out_11_3[24], pipeexmem_1_out_11_2[24], pipeexmem_1_out_11_3[24], pipeexmem_1_out_11_2[24], pipeexmem_1_out_11_4[24], pipeexmem_1_out_11_5[23], pipeexmem_1_out_11[23], pipeexmem_1_out_11_4[23], pipeexmem_1_out_11_2[23], pipeexmem_1_out_11_3[23], pipeexmem_1_out_11_2[23], pipeexmem_1_out_11_3[23], pipeexmem_1_out_11_2[23], pipeexmem_1_out_11_4[23], pipeexmem_1_out_11_open[23], pipeexmem_1_out_11_2[23], pipeexmem_1_out_11_3[23], pipeexmem_1_out_11_2[23], pipeexmem_1_out_11_3[23], pipeexmem_1_out_11_2[23], pipeexmem_1_out_11_4[23], pipeexmem_1_out_11_5[22], pipeexmem_1_out_11[22], pipeexmem_1_out_11_4[22], pipeexmem_1_out_11_2[22], pipeexmem_1_out_11_3[22], pipeexmem_1_out_11_2[22], pipeexmem_1_out_11_3[22], pipeexmem_1_out_11_2[22], pipeexmem_1_out_11_4[22], pipeexmem_1_out_11_open[22], pipeexmem_1_out_11_2[22], pipeexmem_1_out_11_3[22], pipeexmem_1_out_11_2[22], pipeexmem_1_out_11_3[22], pipeexmem_1_out_11_2[22], pipeexmem_1_out_11_4[22], pipeexmem_1_out_11_5[21], pipeexmem_1_out_11[21], pipeexmem_1_out_11_4[21], pipeexmem_1_out_11_2[21], pipeexmem_1_out_11_3[21], pipeexmem_1_out_11_2[21], pipeexmem_1_out_11_3[21], pipeexmem_1_out_11_2[21], pipeexmem_1_out_11_4[21], pipeexmem_1_out_11_open[21], pipeexmem_1_out_11_2[21], pipeexmem_1_out_11_3[21], pipeexmem_1_out_11_2[21], pipeexmem_1_out_11_3[21], pipeexmem_1_out_11_2[21], pipeexmem_1_out_11_4[21], pipeexmem_1_out_11_5[20], pipeexmem_1_out_11[20], pipeexmem_1_out_11_4[20], pipeexmem_1_out_11_2[20], pipeexmem_1_out_11_3[20], pipeexmem_1_out_11_2[20], pipeexmem_1_out_11_3[20], pipeexmem_1_out_11_2[20], pipeexmem_1_out_11_4[20], pipeexmem_1_out_11_open[20], pipeexmem_1_out_11_2[20], pipeexmem_1_out_11_3[20], pipeexmem_1_out_11_2[20], pipeexmem_1_out_11_3[20], pipeexmem_1_out_11_2[20], pipeexmem_1_out_11_4[20], pipeexmem_1_out_11_5[19], pipeexmem_1_out_11[19], pipeexmem_1_out_11_4[19], pipeexmem_1_out_11_2[19], pipeexmem_1_out_11_3[19], pipeexmem_1_out_11_2[19], pipeexmem_1_out_11_3[19], pipeexmem_1_out_11_2[19], pipeexmem_1_out_11_4[19], pipeexmem_1_out_11_open[19], pipeexmem_1_out_11_2[19], pipeexmem_1_out_11_3[19], pipeexmem_1_out_11_2[19], pipeexmem_1_out_11_3[19], pipeexmem_1_out_11_2[19], pipeexmem_1_out_11_4[19], pipeexmem_1_out_11_5[18], pipeexmem_1_out_11[18], pipeexmem_1_out_11_4[18], pipeexmem_1_out_11_2[18], pipeexmem_1_out_11_3[18], pipeexmem_1_out_11_2[18], pipeexmem_1_out_11_3[18], pipeexmem_1_out_11_2[18], pipeexmem_1_out_11_4[18], pipeexmem_1_out_11_open[18], pipeexmem_1_out_11_2[18], pipeexmem_1_out_11_3[18], pipeexmem_1_out_11_2[18], pipeexmem_1_out_11_3[18], pipeexmem_1_out_11_2[18], pipeexmem_1_out_11_4[18], pipeexmem_1_out_11_5[17], pipeexmem_1_out_11[17], pipeexmem_1_out_11_4[17], pipeexmem_1_out_11_2[17], pipeexmem_1_out_11_3[17], pipeexmem_1_out_11_2[17], pipeexmem_1_out_11_3[17], pipeexmem_1_out_11_2[17], pipeexmem_1_out_11_4[17], pipeexmem_1_out_11_open[17], pipeexmem_1_out_11_2[17], pipeexmem_1_out_11_3[17], pipeexmem_1_out_11_2[17], pipeexmem_1_out_11_3[17], pipeexmem_1_out_11_2[17], pipeexmem_1_out_11_4[17], pipeexmem_1_out_11_5[16], pipeexmem_1_out_11[16], pipeexmem_1_out_11_4[16], pipeexmem_1_out_11_2[16], pipeexmem_1_out_11_3[16], pipeexmem_1_out_11_2[16], pipeexmem_1_out_11_3[16], pipeexmem_1_out_11_2[16], pipeexmem_1_out_11_4[16], pipeexmem_1_out_11_open[16], pipeexmem_1_out_11_2[16], pipeexmem_1_out_11_3[16], pipeexmem_1_out_11_2[16], pipeexmem_1_out_11_3[16], pipeexmem_1_out_11_2[16], pipeexmem_1_out_11_4[16], pipeexmem_1_out_11_5[15], pipeexmem_1_out_11[15], pipeexmem_1_out_11_4[15], pipeexmem_1_out_11_2[15], pipeexmem_1_out_11_3[15], pipeexmem_1_out_11_2[15], pipeexmem_1_out_11_3[15], pipeexmem_1_out_11_2[15], pipeexmem_1_out_11_4[15], pipeexmem_1_out_11_open[15], pipeexmem_1_out_11_2[15], pipeexmem_1_out_11_3[15], pipeexmem_1_out_11_2[15], pipeexmem_1_out_11_3[15], pipeexmem_1_out_11_2[15], pipeexmem_1_out_11_4[15], pipeexmem_1_out_11_5[14], pipeexmem_1_out_11[14], pipeexmem_1_out_11_4[14], pipeexmem_1_out_11_2[14], pipeexmem_1_out_11_3[14], pipeexmem_1_out_11_2[14], pipeexmem_1_out_11_3[14], pipeexmem_1_out_11_2[14], pipeexmem_1_out_11_4[14], pipeexmem_1_out_11_open[14], pipeexmem_1_out_11_2[14], pipeexmem_1_out_11_3[14], pipeexmem_1_out_11_2[14], pipeexmem_1_out_11_3[14], pipeexmem_1_out_11_2[14], pipeexmem_1_out_11_4[14], pipeexmem_1_out_11_5[13], pipeexmem_1_out_11[13], pipeexmem_1_out_11_4[13], pipeexmem_1_out_11_2[13], pipeexmem_1_out_11_3[13], pipeexmem_1_out_11_2[13], pipeexmem_1_out_11_3[13], pipeexmem_1_out_11_2[13], pipeexmem_1_out_11_4[13], pipeexmem_1_out_11_open[13], pipeexmem_1_out_11_2[13], pipeexmem_1_out_11_3[13], pipeexmem_1_out_11_2[13], pipeexmem_1_out_11_3[13], pipeexmem_1_out_11_2[13], pipeexmem_1_out_11_4[13], pipeexmem_1_out_11_5[12], pipeexmem_1_out_11[12], pipeexmem_1_out_11_4[12], pipeexmem_1_out_11_2[12], pipeexmem_1_out_11_3[12], pipeexmem_1_out_11_2[12], pipeexmem_1_out_11_3[12], pipeexmem_1_out_11_2[12], pipeexmem_1_out_11_4[12], pipeexmem_1_out_11_open[12], pipeexmem_1_out_11_2[12], pipeexmem_1_out_11_3[12], pipeexmem_1_out_11_2[12], pipeexmem_1_out_11_3[12], pipeexmem_1_out_11_2[12], pipeexmem_1_out_11_4[12], pipeexmem_1_out_11_5[11], pipeexmem_1_out_11[11], pipeexmem_1_out_11_4[11], pipeexmem_1_out_11_2[11], pipeexmem_1_out_11_3[11], pipeexmem_1_out_11_2[11], pipeexmem_1_out_11_3[11], pipeexmem_1_out_11_2[11], pipeexmem_1_out_11_4[11], pipeexmem_1_out_11_open[11], pipeexmem_1_out_11_2[11], pipeexmem_1_out_11_3[11], pipeexmem_1_out_11_2[11], pipeexmem_1_out_11_3[11], pipeexmem_1_out_11_2[11], pipeexmem_1_out_11_4[11], pipeexmem_1_out_11_5[10], pipeexmem_1_out_11[10], pipeexmem_1_out_11_4[10], pipeexmem_1_out_11_2[10], pipeexmem_1_out_11_3[10], pipeexmem_1_out_11_2[10], pipeexmem_1_out_11_3[10], pipeexmem_1_out_11_2[10], pipeexmem_1_out_11_4[10], pipeexmem_1_out_11_open[10], pipeexmem_1_out_11_2[10], pipeexmem_1_out_11_3[10], pipeexmem_1_out_11_2[10], pipeexmem_1_out_11_3[10], pipeexmem_1_out_11_2[10], pipeexmem_1_out_11_4[10], pipeexmem_1_out_11_5[9], pipeexmem_1_out_11[9], pipeexmem_1_out_11_4[9], pipeexmem_1_out_11_2[9], pipeexmem_1_out_11_3[9], pipeexmem_1_out_11_2[9], pipeexmem_1_out_11_3[9], pipeexmem_1_out_11_2[9], pipeexmem_1_out_11_4[9], pipeexmem_1_out_11_open[9], pipeexmem_1_out_11_2[9], pipeexmem_1_out_11_3[9], pipeexmem_1_out_11_2[9], pipeexmem_1_out_11_3[9], pipeexmem_1_out_11_2[9], pipeexmem_1_out_11_4[9], pipeexmem_1_out_11_5[8], pipeexmem_1_out_11[8], pipeexmem_1_out_11_4[8], pipeexmem_1_out_11_2[8], pipeexmem_1_out_11_3[8], pipeexmem_1_out_11_2[8], pipeexmem_1_out_11_3[8], pipeexmem_1_out_11_2[8], pipeexmem_1_out_11_4[8], pipeexmem_1_out_11_open[8], pipeexmem_1_out_11_2[8], pipeexmem_1_out_11_3[8], pipeexmem_1_out_11_2[8], pipeexmem_1_out_11_3[8], pipeexmem_1_out_11_2[8], pipeexmem_1_out_11_4[8], pipeexmem_1_out_11_5[7], pipeexmem_1_out_11[7], pipeexmem_1_out_11_4[7], pipeexmem_1_out_11_2[7], pipeexmem_1_out_11_3[7], pipeexmem_1_out_11_2[7], pipeexmem_1_out_11_3[7], pipeexmem_1_out_11_2[7], pipeexmem_1_out_11_4[7], pipeexmem_1_out_11_open[7], pipeexmem_1_out_11_2[7], pipeexmem_1_out_11_3[7], pipeexmem_1_out_11_2[7], pipeexmem_1_out_11_3[7], pipeexmem_1_out_11_2[7], pipeexmem_1_out_11_4[7], pipeexmem_1_out_11_5[6], pipeexmem_1_out_11[6], pipeexmem_1_out_11_4[6], pipeexmem_1_out_11_2[6], pipeexmem_1_out_11_3[6], pipeexmem_1_out_11_2[6], pipeexmem_1_out_11_3[6], pipeexmem_1_out_11_2[6], pipeexmem_1_out_11_4[6], pipeexmem_1_out_11_open[6], pipeexmem_1_out_11_2[6], pipeexmem_1_out_11_3[6], pipeexmem_1_out_11_2[6], pipeexmem_1_out_11_3[6], pipeexmem_1_out_11_2[6], pipeexmem_1_out_11_4[6], pipeexmem_1_out_11_5[5], pipeexmem_1_out_11[5], pipeexmem_1_out_11_4[5], pipeexmem_1_out_11_2[5], pipeexmem_1_out_11_3[5], pipeexmem_1_out_11_2[5], pipeexmem_1_out_11_3[5], pipeexmem_1_out_11_2[5], pipeexmem_1_out_11_4[5], pipeexmem_1_out_11_open[5], pipeexmem_1_out_11_2[5], pipeexmem_1_out_11_3[5], pipeexmem_1_out_11_2[5], pipeexmem_1_out_11_3[5], pipeexmem_1_out_11_2[5], pipeexmem_1_out_11_4[5], pipeexmem_1_out_11_5[4], pipeexmem_1_out_11[4], pipeexmem_1_out_11_4[4], pipeexmem_1_out_11_2[4], pipeexmem_1_out_11_3[4], pipeexmem_1_out_11_2[4], pipeexmem_1_out_11_3[4], pipeexmem_1_out_11_2[4], pipeexmem_1_out_11_4[4], pipeexmem_1_out_11_open[4], pipeexmem_1_out_11_2[4], pipeexmem_1_out_11_3[4], pipeexmem_1_out_11_2[4], pipeexmem_1_out_11_3[4], pipeexmem_1_out_11_2[4], pipeexmem_1_out_11_4[4], pipeexmem_1_out_11_5[3], pipeexmem_1_out_11[3], pipeexmem_1_out_11_4[3], pipeexmem_1_out_11_2[3], pipeexmem_1_out_11_3[3], pipeexmem_1_out_11_2[3], pipeexmem_1_out_11_3[3], pipeexmem_1_out_11_2[3], pipeexmem_1_out_11_4[3], pipeexmem_1_out_11_open[3], pipeexmem_1_out_11_2[3], pipeexmem_1_out_11_3[3], pipeexmem_1_out_11_2[3], pipeexmem_1_out_11_3[3], pipeexmem_1_out_11_2[3], pipeexmem_1_out_11_4[3], pipeexmem_1_out_11_5[2], pipeexmem_1_out_11[2], pipeexmem_1_out_11_4[2], pipeexmem_1_out_11_2[2], pipeexmem_1_out_11_3[2], pipeexmem_1_out_11_2[2], pipeexmem_1_out_11_3[2], pipeexmem_1_out_11_2[2], pipeexmem_1_out_11_4[2], pipeexmem_1_out_11_open[2], pipeexmem_1_out_11_2[2], pipeexmem_1_out_11_3[2], pipeexmem_1_out_11_2[2], pipeexmem_1_out_11_3[2], pipeexmem_1_out_11_2[2], pipeexmem_1_out_11_4[2], pipeexmem_1_out_11_5[1], pipeexmem_1_out_11[1], pipeexmem_1_out_11_4[1], pipeexmem_1_out_11_2[1], pipeexmem_1_out_11_3[1], pipeexmem_1_out_11_2[1], pipeexmem_1_out_11_3[1], pipeexmem_1_out_11_2[1], pipeexmem_1_out_11_4[1], pipeexmem_1_out_11_open[1], pipeexmem_1_out_11_2[1], pipeexmem_1_out_11_3[1], pipeexmem_1_out_11_2[1], pipeexmem_1_out_11_3[1], pipeexmem_1_out_11_2[1], pipeexmem_1_out_11_4[1], pipeexmem_1_out_11_5[0], pipeexmem_1_out_11[0], pipeexmem_1_out_11_4[0], pipeexmem_1_out_11_2[0], pipeexmem_1_out_11_3[0], pipeexmem_1_out_11_2[0], pipeexmem_1_out_11_3[0], pipeexmem_1_out_11_2[0], pipeexmem_1_out_11_4[0], pipeexmem_1_out_11_open[0], pipeexmem_1_out_11_2[0], pipeexmem_1_out_11_3[0], pipeexmem_1_out_11_2[0], pipeexmem_1_out_11_3[0], pipeexmem_1_out_11_2[0], pipeexmem_1_out_11_4[0]}),
    .in_8(multiplexer_7_out), .out_16(pipeexmem_1_out_16), .PC(pipeidex_1_out_10), .PCOut(pipeexmem_1_pcout));
  Multiplexer #(.select(2), .width(5), .enable("false")) multiplexer_11 (
    .in0(pipeexmem_1_out_12_2), .in2(pipeexmem_1_out_12[20:16]), .in3({5{1'b1}}), .out(multiplexer_11_out),
    .sel(pipeexmem_1_out_14_2));  // open: in1
  assign bit_extender_1_out = {{16{pipeexmem_1_out_12_2[4]}}, {pipeexmem_1_out_12_2, pipeexmem_1_out_12[10:0]}};  // Bit_Extender bit_extender_1
  Adder #(.width(32)) adder_1 (
    .a(bit_extender_1_out), .b(pipeexmem_1_out_15),
    .out({adder_1_out[31:26], adder_1_out_2, adder_1_out[1:0]}));  // open: cin, cout
  // Probe on {pipeexmem_1_out_14[31:22], pipeexmem_1_out_14_2, pipeexmem_1_out_14[19:0]}
  // Probe on {pipeexmem_1_out_12[31:16], pipeexmem_1_out_12_2, pipeexmem_1_out_12[10:0]}
  // Probe on pipeexmem_1_pcout
  // MIPS_RAM mips_ram_1: pin names not known; wires that end beside it: {pipeexmem_1_out_12[31:16], pipeexmem_1_out_12_2, pipeexmem_1_out_12[10:0]}, adder_1_out_2, pipeexmem_1_out_16, pipeexmem_1_out_14[18], T, 1'b1, RST, mips_ram_1_p8, {mips_ram_1_p9[31:16], mips_ram_1_p9_2, mips_ram_1_p9[10:0]}
  PipeMEMWB pipememwb_1 (
    .T(T), .enable(enable), .clear(1'b0),
    .instruction({pipeexmem_1_out_12[31:16], pipeexmem_1_out_12_2, pipeexmem_1_out_12[10:0]}),
    .control({pipeexmem_1_out_14[31:22], pipeexmem_1_out_14_2, pipeexmem_1_out_14[19:0]}),
    .AluR(pipeexmem_1_out_11_5),
    .instructionOut({mips_ram_1_p9[31:16], mips_ram_1_p9_2, mips_ram_1_p9[10:0]}),
    .ControlOut({pipememwb_1_controlout[31:22], pipememwb_1_controlout_2, pipememwb_1_controlout[19:0]}),
    .AluROut(pipememwb_1_alurout), .rSOut(pipememwb_1_rsout), .rS(multiplexer_12_out),
    .PC(pipeexmem_1_pcout), .PCOut(pipememwb_1_pcout));
  Multiplexer #(.width(32), .enable("false")) multiplexer_12 (
    .in0(mips_ram_1_p8), .in1(bit_extender_2_out), .out(multiplexer_12_out), .sel(pipeexmem_1_out_14[13]));
  assign bit_extender_2_out = {{24{1'b0}}, multiplexer_13_out};  // Bit_Extender bit_extender_2
  Multiplexer #(.select(2), .width(8), .enable("false")) multiplexer_13 (
    .in0(mips_ram_1_p8[7:0]), .in1(mips_ram_1_p8[15:8]), .in2(mips_ram_1_p8[23:16]),
    .in3(mips_ram_1_p8[31:24]), .out(multiplexer_13_out), .sel(adder_1_out[1:0]));
  Multiplexer #(.select(2), .width(5), .enable("false")) multiplexer_14 (
    .in0(mips_ram_1_p9_2), .in2(mips_ram_1_p9[20:16]), .in3({5{1'b1}}), .out(multiplexer_14_out),
    .sel(pipememwb_1_controlout_2));  // open: in1
  // Probe on {pipememwb_1_controlout[31:22], pipememwb_1_controlout_2, pipememwb_1_controlout[19:0]}
  // Probe on {mips_ram_1_p9[31:16], mips_ram_1_p9_2, mips_ram_1_p9[10:0]}
  // Probe on pipememwb_1_pcout

  // Notes on the sheet:
  //   指令存储器
  //   contents of rom_1 (hex, n*v repeats v):
  //   20110001 8000c05 20110001 20120002 20130003 8000c09 20110001 20120002 20130003 8000c0d 20110001
  //   20120002 20130003 8000c11 20110001 20120002 20130003 c000cf6 20100001 20110001 118fc0 112020
  //   20020022 c 118882 12200001 8000c15 112020 20020022 c 20110001 118880 112020 20020022 c 12200001
  //   8000c1f 20110001 118fc0 112020 20020022 c 1188c3 112020 20020022 c 118903 112020 20020022 c 118903
  //   112020 20020022 c 118903 112020 20020022 c 118903 112020 20020022 c 118903 112020 20020022 c 118903
  //   112020 20020022 c 118903 112020 20020022 c 20100001 109fc0 139fc3 8021 2012000c 24160003 26100001
  //   3210000f 20080008 20090001 139900 2709825 132020 20020022 c 1094022 1500fff9 22100001 2018000f
  //   2188024 108700 20080008 20090001 139902 2709825 132021 20020022 c 1094022 1500fff9 108702 2c9b022
  //   12c00001 8000c50 4020 1084027 84400 3508ffff 82021 20020022 c 2010ffff 20110000 ae300000 22100001
  //   22310004 ae300000 22100001 22310004 ae300000 22100001 22310004 ae300000 22100001 22310004 ae300000
  //   22100001 22310004 ae300000 22100001 22310004 ae300000 22100001 22310004 ae300000 22100001 22310004
  //   ae300000 22100001 22310004 ae300000 22100001 22310004 ae300000 22100001 22310004 ae300000 22100001
  //   22310004 ae300000 22100001 22310004 ae300000 22100001 22310004 ae300000 22100001 22310004 ae300000
  //   22100001 22310004 22100001 8020 2011003c 8e130000 8e340000 274402a 11000002 ae330000 ae140000
  //   2231fffc 1611fff8 102020 20020022 c 22100004 2011003c 1611fff2 20020032 c 20080001 20110010 112020
  //   20020022 c 200b0020 2288823 112020 20020022 c 216bffff 1560fffa 2002000a c 2008ffff 20117777 112020
  //   20020022 c 200b0010 2288826 112020 20020022 c 216bffff 1560fffa 2002000a c 20090000 200b0010
  //   34118483 20120404 118c00 129400 36318281 22520404 ad310000 2328820 21290004 216bffff 1560fffb
  //   200b0020 20090000 85310000 112020 20020022 c 21290002 216bffff 1560fff9 2002000a c 2011fff1 112020
  //   20020022 c 22310001 1a20fffb 2002000a c 2002000a c 20100000 22100001 102020 20020022 c 22100002
  //   102020 20020022 c 22100003 102020 20020022 c 22100004 102020 20020022 c 22100005 102020 20020022 c
  //   22100006 102020 20020022 c 22100007 102020 20020022 c 22100008 102020 20020022 20020022 c 3e00008
  //   数码管输出
  //   rS
  //   $rS
  //   $rT
  //   rT
  //   rT
  //   rD
  //   rS
  //   rT
  //   this part belongs to wb segment
  //   rT
  //   rD
  //   Immi
  //   运行内存
  //   rT
  //   rD
endmodule

module Controller (
  input  [31:0] instruction,
  output [3:0] aluop,
  output [1:0] alux,
  output [2:0] aluy,
  output rWE,
  output [1:0] rW,
  output rW_2,
  output MemW,
  output [1:0] PCW,
  output J,
  output Sys1,
  output nLBU,
  output BLTZ,
  output rARead,
  output rBRead
);

  wire add, addi, addiu, addu, \and , and_1_out, and_2_out, and_3_out, and_4_out, and_5_out, and_6_out,
       and_7_out, and_8_out, and_13_out, andi, beq, bltz_t, bne, j_t, jal, jr, lbu_t, lw, \nor , Op__0, \or ,
       or_1_out, or_2_out, or_3_out, or_4_out, or_5_out, or_8_out, or_9_out, or_11_out, or_12_out, or_13_out,
       or_14_out, or_15_out, or_16_out, or_17_out, ori, priority_encoder_2_p2, priority_encoder_2_p4,
       priority_encoder_2_p5, priority_encoder_2_p12, sll, slt, slti, sltiu, sltu, sra, srl, srlv, sub, subu,
       syscall, \xor ;
  wire [3:0] priority_encoder_1_out, priority_encoder_2_p1;

  Comparator #(.width(6)) comparator_1 (.a(instruction[31:26]), .b({6{1'b0}}), .eq(Op__0));  // open: gt, lt
  Comparator #(.width(6)) comparator_2 (.a(instruction[31:26]), .b(6'b000100), .eq(beq));  // open: gt, lt
  Comparator #(.width(6)) comparator_3 (.a(instruction[31:26]), .b(6'b000101), .eq(bne));  // open: gt, lt
  Comparator #(.width(6)) comparator_4 (.a(instruction[31:26]), .b(6'b001010), .eq(slti));  // open: gt, lt
  Comparator #(.width(6)) comparator_5 (.a(instruction[31:26]), .b(6'b001101), .eq(ori));  // open: gt, lt
  Comparator #(.width(6)) comparator_6 (.a(instruction[31:26]), .b(6'b001100), .eq(andi));  // open: gt, lt
  Comparator #(.width(6)) comparator_7 (.a(instruction[31:26]), .b(6'b001001), .eq(addiu));  // open: gt, lt
  Comparator #(.width(6)) comparator_8 (.a(instruction[31:26]), .b(6'b001000), .eq(addi));  // open: gt, lt
  Comparator #(.width(6)) comparator_9 (.a(instruction[31:26]), .b(6'b000010), .eq(j_t));  // open: gt, lt
  or or_1 (or_1_out, bltz_t, slti);
  or or_2 (or_2_out, bne, beq);
  Comparator #(.width(6)) comparator_10 (.a(instruction[31:26]), .b(6'b101011), .eq(MemW));  // open: gt, lt
  Comparator #(.width(6)) comparator_11 (.a(instruction[31:26]), .b(6'b100011), .eq(lw));  // open: gt, lt
  Comparator #(.width(6)) comparator_12 (.a(instruction[31:26]), .b(6'b000011), .eq(jal));  // open: gt, lt
  Comparator #(.width(6)) comparator_13 (.a(instruction[5:0]), .b(6'b101011), .eq(sltu));  // open: gt, lt
  Comparator #(.width(6)) comparator_14 (.a(instruction[5:0]), .b(6'b101010), .eq(slt));  // open: gt, lt
  Comparator #(.width(6)) comparator_15 (.a(instruction[5:0]), .b(6'b100111), .eq(\nor ));  // open: gt, lt
  Comparator #(.width(6)) comparator_16 (.a(instruction[5:0]), .b(6'b100101), .eq(\or ));  // open: gt, lt
  Comparator #(.width(6)) comparator_17 (.a(instruction[5:0]), .b(6'b100100), .eq(\and ));  // open: gt, lt
  or or_3 (or_3_out, jal, addi, lw, MemW, addiu, lbu_t);
  Priority_Encoder #(.select(4)) priority_encoder_1 (
    .in0(j_t), .in5(or_3_out), .in7(andi), .in8(ori), .in11(or_1_out), .in12(sltiu), .in14(or_2_out),
    .out(priority_encoder_1_out));  // open: in1, in2, in3, in4, in6, in9, in10, in13, in15, gs, en_out, en_in
  or or_4 (or_4_out, bltz_t, beq, slti, bne, ori, andi, addi, MemW, sltiu, lbu_t, addiu, lw);
  Multiplexer multiplexer_1 (.in0(or_4_out), .in1(or_5_out), .out(rARead), .sel(Op__0));  // open: en
  or or_5 (or_5_out, subu, sub, srlv, sltu, addu, slt, \xor , \or , \and , jr, syscall, \nor , add);
  Multiplexer #(.width(4)) multiplexer_2 (
    .in0(priority_encoder_1_out), .in1(priority_encoder_2_p1), .out(aluop), .sel(Op__0));  // open: en
  // Priority_Encoder #(.select(4)) priority_encoder_2: pin names not known; wires that end beside it: priority_encoder_2_p1, priority_encoder_2_p2, sra, priority_encoder_2_p4, priority_encoder_2_p5, sub, \and , \or , \nor , slt, sltu, priority_encoder_2_p12
  Comparator #(.width(6)) comparator_18 (.a(instruction[5:0]), .b(6'b100010), .eq(sub));  // open: gt, lt
  Comparator #(.width(6)) comparator_19 (.a(instruction[5:0]), .b(6'b100001), .eq(addu));  // open: gt, lt
  Comparator #(.width(6)) comparator_20 (.a(instruction[5:0]), .b(6'b100000), .eq(add));  // open: gt, lt
  Comparator #(.width(6)) comparator_21 (.a(instruction[5:0]), .b(6'b001100), .eq(syscall));  // open: gt, lt
  Comparator #(.width(6)) comparator_22 (.a(instruction[5:0]), .b(6'b001000), .eq(jr));  // open: gt, lt
  Comparator #(.width(6)) comparator_23 (.a(instruction[5:0]), .b(6'b000011), .eq(sra));  // open: gt, lt
  Comparator #(.width(6)) comparator_24 (.a(instruction[5:0]), .b(6'b000010), .eq(srl));  // open: gt, lt
  Comparator #(.width(6)) comparator_25 (.a(instruction[5:0]), .b({6{1'b0}}), .eq(sll));  // open: gt, lt
  or or_6 (priority_encoder_2_p2, jr, syscall, sll);
  or or_7 (priority_encoder_2_p5, add, addu);
  or or_8 (or_8_out, beq, bne, MemW);
  or or_9 (or_9_out, subu, sub, sra, sltu, srl, add, sll, srlv, \or , \and , slt, addu, \nor , syscall, \xor );
  Multiplexer #(.select(2), .width(2)) multiplexer_3 (
    .in0(2'b10), .in1(2'b11), .in2(2'b00), .in3(2'b00), .out(rW), .sel({Op__0, jal}));  // open: en
  or or_10 (priority_encoder_2_p4, srl, srlv);
  Multiplexer multiplexer_4 (.in0(or_8_out), .in1(or_9_out), .out(rBRead), .sel(Op__0));  // open: en
  and and_1 (and_1_out, Op__0, jr);
  and and_2 (and_2_out, ~Op__0, beq);  // AND_Gate
  and and_3 (and_3_out, ~Op__0, bne);  // AND_Gate
  or or_11 (or_11_out, sra, srl, sll, srlv);
  or or_12 (or_12_out, sltiu, slti, lw, addi, MemW, lbu_t, addiu);
  Comparator #(.width(6)) comparator_26 (.a(instruction[31:26]), .b(6'b000001), .eq(bltz_t));  // open: gt, lt
  Comparator #(.width(6)) comparator_27 (.a(instruction[31:26]), .b(6'b001011), .eq(sltiu));  // open: gt, lt
  or or_13 (or_13_out, jal, j_t);
  Priority_Encoder #(.select(2)) priority_encoder_3 (
    .in0(1'b1), .in1(and_1_out), .in2(and_2_out), .in3(and_3_out), .out(PCW));  // open: gs, en_out, en_in
  and and_4 (and_4_out, Op__0, or_11_out);
  and and_5 (and_5_out, jal, ~Op__0);  // AND_Gate
  and and_6 (and_6_out, ~Op__0, or_12_out);  // AND_Gate
  and and_7 (and_7_out, srlv, Op__0);
  and and_8 (and_8_out, ~Op__0, or_14_out);  // AND_Gate
  or or_14 (or_14_out, ori, andi);
  and and_9 (J, or_13_out, ~Op__0);  // AND_Gate
  or or_15 (or_15_out, lbu_t, lw);
  Priority_Encoder #(.select(2)) priority_encoder_4 (
    .in0(1'b1), .in1(and_4_out), .in2(and_5_out), .out(alux));  // open: in3, gs, en_out, en_in
  Priority_Encoder priority_encoder_5 (
    .in0(1'b1), .in1(and_4_out), .in2(and_6_out), .in3(and_5_out), .in4(and_7_out), .in5(and_8_out),
    .out(aluy));  // open: in6, in7, en_in, gs, en_out
  Comparator #(.width(6)) comparator_28 (.a(instruction[31:26]), .b(6'b100100), .eq(lbu_t));  // open: gt, lt
  Comparator #(.width(6)) comparator_29 (.a(instruction[5:0]), .b(6'b000110), .eq(srlv));  // open: gt, lt
  and and_10 (BLTZ, bltz_t, ~Op__0);  // AND_Gate
  and and_11 (Sys1, syscall, Op__0);
  and and_12 (nLBU, lbu_t, ~Op__0);  // AND_Gate
  not not_1 (rW_2, and_13_out);
  and and_13 (and_13_out, or_15_out, ~Op__0);  // AND_Gate
  Comparator #(.width(6)) comparator_30 (.a(instruction[5:0]), .b(6'b100011), .eq(subu));  // open: gt, lt
  Comparator #(.width(6)) comparator_31 (.a(instruction[5:0]), .b(6'b100110), .eq(\xor ));  // open: gt, lt
  or or_16 (or_16_out, addiu, lw, addi, jal, slti, ori, andi, lbu_t, sltiu);
  or or_17 (or_17_out, \xor , \nor , sub, \or , \and , slt, add, sra, addu, srl, sltu, sll, srlv, subu);
  Multiplexer multiplexer_5 (.in0(or_16_out), .in1(or_17_out), .out(rWE), .sel(Op__0));  // open: en

  // Other names for the same wires on the sheet: Sp[5:0] = instruction[5:0]; Op[5:0] = instruction[31:26]; LBU = nLBU;
  //   rW_t = rW_2; sw = MemW; Sys = Sys1

  // Notes on the sheet:
  //   Instructions
  //   is this instruction using rA or rB
  //   O->rD
  //   2->rT
  //   3->$31
  //   Alu Operator
  //   RAM Write
  //   Branching
  //   0->PC++
  //   1->$rS
  //   2->beq
  //   3->bne
  //   J/JAL
  //   CCMB
  //   lbtz(CCMB)
  //   Syscall
  //   lbu(CCMB)
  //   Reg Write Src
  //   0->MemO
  //   1->AluR
  //   Alu Input
  //   0->rS(default)
  //   1->rT
  //   2->PC
  //   0->rT(default)
  //   1->sA
  //   2->SignExtImmi
  //   3->4
  //   4->rS(CCMB)
  //   5->ZeroExtImmi
  //   reg Write Enable
endmodule

module Alu (
  input  [31:0] X,
  input  [31:0] Y,
  input  [3:0] AluOP,
  output Signed_Overflow,
  output UnSigned_Overflow,
  output Equal,
  output [31:0] Result,
  output [31:0] Result_2
);

  wire OF1, OF2, UOF1, UOF2, xnor_1_out, xor_1_out, xor_2_out, xor_3_out;
  wire [0:0] R12, R13;
  wire [31:0] R1, R2, R3, R4, R5, R6, R7, R8, R9, R10, R11, R21, R22;

  // Probe on X
  // Probe on X
  // Probe on Y
  // Probe on Y
  Shifter #(.width(32)) shifter_1 (.in(X), .\dist (Y[4:0]), .out(R1));
  Shifter #(.width(32), .shift("ar")) shifter_2 (.in(X), .\dist (Y[4:0]), .out(R2));
  Shifter #(.width(32), .shift("lr")) shifter_3 (.in(X), .\dist (Y[4:0]), .out(R3));
  Multiplier #(.width(32)) multiplier_1 (.a(X), .b(Y), .out(R4), .cout(R21));  // open: cin
  Divider #(.width(32)) divider_1 (.a(X), .b(Y), .out(R5), .rem(R22));  // open: upper
  xnor xnor_1 (xnor_1_out, X[31], Y[31]);
  xor xor_1 (xor_1_out, Y[31], X[31]);
  // Probe on AluOP
  Adder #(.width(32)) adder_1 (.a(X), .b(Y), .out(R6), .cin(1'b0), .cout(UOF1));
  xor xor_2 (xor_2_out, Y[31], R6[31]);
  and and_1 (OF1, xnor_1_out, xor_2_out);
  Subtractor #(.width(32)) subtractor_1 (.a(X), .b(Y), .out(R7), .bin(1'b0), .bout(UOF2));
  xor xor_3 (xor_3_out, X[31], R7[31]);
  and and_2 (OF2, xor_1_out, xor_3_out);
  // Probe on Result
  // Probe on Result
  assign R8 = X & Y;  // AND_Gate and_3, 32 bits wide
  assign R9 = X | Y;  // OR_Gate or_1, 32 bits wide
  assign R10 = X ^ Y;  // XOR_Gate xor_4, 32 bits wide
  assign R11 = ~(X | Y);  // NOR_Gate nor_1, 32 bits wide
  Comparator #(.width(32)) comparator_1 (.a(X), .b(Y), .eq(Equal), .lt(R12[0]));  // open: gt
  Comparator #(.width(32), .mode("unsigned")) comparator_2 (.a(X), .b(Y), .lt(R13[0]));  // open: gt, eq
  // Probe on Result_2
  Multiplexer #(.select(4), .width(32)) multiplexer_1 (
    .in0(R1), .in1(R2), .in2(R3), .in3(R4), .in4(R5), .in5(R6), .in6(R7), .in7(R8), .in8(R9), .in9(R10),
    .in10(R11), .in11({{31{1'b0}}, R12[0]}), .in12({{31{1'b0}}, R13[0]}), .in13({32{1'b0}}),
    .in14({32{1'b0}}), .in15({32{1'b0}}), .out(Result), .sel(AluOP));  // open: en
  Multiplexer #(.select(4)) multiplexer_2 (
    .in0(1'b0), .in1(1'b0), .in2(1'b0), .in3(1'b0), .in4(1'b0), .in5(UOF1), .in6(UOF2), .in7(1'b0),
    .in8(1'b0), .in9(1'b0), .in10(1'b0), .in11(1'b0), .in12(1'b0), .in13(1'b0), .in14(1'b0), .in15(1'b0),
    .out(UnSigned_Overflow), .sel(AluOP));  // open: en
  Multiplexer #(.select(4), .width(32)) multiplexer_3 (
    .in0({32{1'b0}}), .in1({32{1'b0}}), .in2({32{1'b0}}), .in3(R21), .in4(R22), .in5({32{1'b0}}),
    .in6({32{1'b0}}), .in7({32{1'b0}}), .in8({32{1'b0}}), .in9({32{1'b0}}), .in10({32{1'b0}}),
    .in11({32{1'b0}}), .in12({32{1'b0}}), .in13({32{1'b0}}), .in14({32{1'b0}}), .in15({32{1'b0}}),
    .out(Result_2), .sel(AluOP));  // open: en
  Multiplexer #(.select(4)) multiplexer_4 (
    .in0(1'b0), .in1(1'b0), .in2(1'b0), .in3(1'b0), .in4(1'b0), .in5(OF1), .in6(OF2), .in7(1'b0), .in8(1'b0),
    .in9(1'b0), .in10(1'b0), .in11(1'b0), .in12(1'b0), .in13(1'b0), .in14(1'b0), .in15(1'b0),
    .out(Signed_Overflow), .sel(AluOP));  // open: en

  // Other names for the same wires on the sheet: OF = Signed_Overflow; Result2[31:0] = Result_2; S[3:0] = AluOP;
  //   UOF = UnSigned_Overflow

  // Notes on the sheet:
  //   不要改变此引脚区域内容，也不要改变ALU封装形式
  //   输入引脚
  //   请在下方利用上方输入输出引脚的隧道信号构建ALU电路，ctrl+d复制选择部件
  //   华中科技大学计算机学院 计算机组成原理，鸣谢加州大学伯克利CS61C课程
  //   输出引脚
  //   探测区域
endmodule

module PC (
  input  [31:0] in_1,
  input  [31:0] in_2,
  input  [25:0] in_3,
  input  [15:0] in_4,
  input  [1:0] in_5,
  input  in_6,
  input  in_7,
  input  in_8,
  input  in_9,
  input  in_10,
  input  in_11,
  input  in_12,
  output [31:0] out_13,
  output [23:0] out_14,
  output [23:0] out_15,
  output [23:0] out_16,
  output [23:0] out_17,
  output jumped
);

  wire and_4_out, and_5_out, and_6_out, and_7_out, and_8_out, JE, JN, JR, multiplexer_1_out,
       multiplexer_2_out, multiplexer_3_out, or_1_out, or_2_out, or_3_out, pcEn;
  wire [1:1] and_1_out, and_2_out;
  wire [31:0] adder_1_out, adder_2_out, multiplexer_5_out, multiplexer_6_out, multiplexer_7_out, PC_4, PCDst,
       shifter_1_out, subtractor_1_out;

  Shifter #(.width(32), .shift("ar")) shifter_1 (.in({in_4, {16{1'b0}}}), .\dist (5'b01110), .out(shifter_1_out));
  Multiplexer #(.enable("false")) multiplexer_1 (.in0(1'b0), .in1(1'b1), .out(multiplexer_1_out), .sel(in_6));
  Multiplexer #(.select(2), .enable("false")) multiplexer_2 (
    .in0(1'b0), .in1(1'b1), .in2(multiplexer_1_out), .in3(multiplexer_3_out), .out(multiplexer_2_out),
    .sel(in_5));
  Multiplexer #(.enable("false")) multiplexer_3 (.in0(1'b1), .in1(1'b0), .out(multiplexer_3_out), .sel(in_6));
  Adder #(.width(32)) adder_1 (.a(in_1), .b(shifter_1_out), .out(adder_1_out));  // open: cin, cout
  Adder #(.width(32)) adder_2 (.a(adder_1_out), .b(32'h4), .out(adder_2_out));  // open: cin, cout
  Multiplexer #(.select(2), .enable("false")) multiplexer_4 (
    .in0(multiplexer_2_out), .in1(1'b1), .in2(1'b1), .out(jumped), .sel({and_1_out[1], in_10}));  // open: in3
  and and_1 (and_1_out[1], in_2[31], in_11);
  Multiplexer #(.width(32), .enable("false")) multiplexer_5 (
    .in0(PC_4), .in1(adder_2_out), .out(multiplexer_5_out), .sel(in_6));
  Multiplexer #(.width(32), .enable("false")) multiplexer_6 (
    .in0(adder_2_out), .in1(PC_4), .out(multiplexer_6_out), .sel(in_6));
  Multiplexer #(.select(2), .width(32), .enable("false")) multiplexer_7 (
    .in0(PC_4), .in1(in_2), .in2(multiplexer_5_out), .in3(multiplexer_6_out), .out(multiplexer_7_out),
    .sel(in_5));
  Subtractor #(.width(32)) subtractor_1 (
    .a({4'b0000, in_3, 2'b00}), .b(32'h3000), .out(subtractor_1_out));  // open: bin, bout
  Multiplexer #(.select(2), .width(32), .enable("false")) multiplexer_8 (
    .in0(multiplexer_7_out), .in1(subtractor_1_out), .in2(adder_2_out), .out(PCDst),
    .sel({and_2_out[1], in_10}));  // open: in3
  and and_2 (and_2_out[1], in_2[31], in_11);
  Register #(.width(32)) PC (.D(PCDst), .en(pcEn), .Q(out_13), .clk(in_9), .clr(in_7));
  Adder #(.width(32)) adder_3 (.a(out_13), .b(32'h4), .out(PC_4));  // open: cin, cout
  Decoder #(.select(2)) decoder_1 (.out1(JR), .out2(JE), .out3(JN), .sel(in_5));  // open: out0, en
  and and_3 (pcEn, in_8, ~in_12);  // AND_Gate
  Counter #(.width(24), .max('hffffff)) counter_1 (
    .count(in_8), .Q(out_14), .clk(in_9), .clr(in_7));  // open: load, D, carry
  or or_1 (or_1_out, JN, JE);
  and and_4 (and_4_out, or_1_out, in_8);
  and and_5 (and_5_out, JN, ~in_6);  // AND_Gate
  and and_6 (and_6_out, in_6, JE);
  Counter #(.width(24), .max('hffffff)) counter_2 (
    .count(and_4_out), .Q(out_16), .clk(in_9), .clr(in_7));  // open: load, D, carry
  Counter #(.width(24), .max('hffffff)) counter_3 (
    .count(and_7_out), .Q(out_17), .clk(in_9), .clr(in_7));  // open: load, D, carry
  or or_2 (or_2_out, and_5_out, and_6_out);
  and and_7 (and_7_out, or_2_out, in_8);
  Counter #(.width(24), .max('hffffff)) counter_4 (
    .count(and_8_out), .Q(out_15), .clk(in_9), .clr(in_7));  // open: load, D, carry
  or or_3 (or_3_out, JR, in_10);
  and and_8 (and_8_out, or_3_out, in_8);

  // Other names for the same wires on the sheet: immi[15:0] = in_4; inst[25:0] = in_3; J = in_10; AluEq = in_6;
  //   BLTZ = in_11; bubble = in_12; EN = in_8; originalPC[31:0] = in_1; PC[31:0] = out_13; PCW[1:0] = in_5;
  //   rS[31:0] = in_2; RST = in_7; T = in_9; 总周期数[23:0] = out_14; 无条件分支指令数[23:0] = out_15; 有条件分支成功跳转[23:0] = out_17;
  //   有条件分支指令数[23:0] = out_16

  // Notes on the sheet:
  //   this pc should not be current pc
  //   but the pc when the instruction
  //   is executed
  //   TODO:修改周期统计
endmodule

module Syscall (
  input  [31:0] in_1,
  input  [31:0] in_2,
  input  in_3,
  input  in_4,
  input  in_5,
  input  in_6,
  output out_7,
  output [31:0] out_8
);

  wire and_1_out, and_2_out, comparator_1_eq, or_1_out, or_2_out, register_1_q, register_3_q, register_4_q;
  wire [31:0] multiplexer_1_out;

  Comparator #(.width(32)) comparator_1 (.a(in_1), .b(32'ha), .eq(comparator_1_eq));  // open: gt, lt
  and and_1 (and_1_out, in_3, comparator_1_eq);
  Register #(.width(1)) register_1 (.D(and_1_out), .Q(register_1_q), .clk(in_4));  // open: en, clr
  and and_2 (and_2_out, ~comparator_1_eq, in_3);  // AND_Gate
  Register #(.width(32)) register_2 (.D(multiplexer_1_out), .Q(out_8), .clk(in_4), .clr(in_5));  // open: en
  Multiplexer #(.width(32)) multiplexer_1 (
    .in0(out_8), .in1(in_2), .out(multiplexer_1_out), .sel(and_2_out));  // open: en
  or or_1 (or_1_out, register_4_q, register_3_q);
  Register #(.width(1)) register_3 (.D(register_1_q), .Q(register_3_q), .clk(in_4));  // open: en, clr
  or or_2 (or_2_out, in_6, in_5);
  Register #(.width(1)) register_4 (.D(or_1_out), .Q(register_4_q), .clk(in_4), .clr(or_2_out));  // open: en
  not not_1 (out_7, register_4_q);

  // Other names for the same wires on the sheet: continue = in_6; EN = out_7; rS[31:0] = in_1; RST = in_5;
  //   rT[31:0] = in_2; Sys = in_3; SyscallOut[31:0] = out_8; T = in_4
endmodule

module AluI (
  input  [1:0] AluX,
  input  [2:0] AluY,
  input  [31:0] instruction,
  input  [31:0] rS,
  input  [31:0] rT,
  input  [31:0] PC,
  output [31:0] X,
  output [31:0] Y
);

  wire [31:0] shifter_1_out, shifter_2_out;

  Shifter #(.width(32), .shift("ar")) shifter_1 (
    .in({instruction[15:0], {16{1'b0}}}), .\dist (5'b10000), .out(shifter_1_out));
  Shifter #(.width(32), .shift("lr")) shifter_2 (
    .in({instruction[15:0], {16{1'b0}}}), .\dist (5'b10000), .out(shifter_2_out));
  Multiplexer #(.select(2), .width(32)) multiplexer_1 (
    .in0(rS), .in1(rT), .in2(PC), .out(X), .sel(AluX));  // open: in3, en
  Multiplexer #(.select(3), .width(32)) multiplexer_2 (
    .in0(rT), .in1({{27{1'b0}}, instruction[10:6]}), .in2(shifter_1_out), .in3(32'h4), .in4(rS),
    .in5(shifter_2_out), .out(Y), .sel(AluY));  // open: in6, in7, en

  // Other names for the same wires on the sheet: oPC[31:0] = PC

  // Notes on the sheet:
  //   Immi
  //   sa
endmodule

module PipeIDEX (
  input  in_1,
  input  in_2,
  input  in_3,
  input  [31:0] in_4,
  input  [31:0] in_5,
  input  [31:0] in_6,
  input  [31:0] in_7,
  input  [31:0] in_8,
  output [31:0] out_9,
  output [31:0] out_10,
  output [31:0] out_11,
  output [31:0] out_12,
  output [31:0] out_13
);

  wire [31:0] multiplexer_1_out, multiplexer_2_out, multiplexer_3_out, multiplexer_4_out, multiplexer_5_out;

  Multiplexer #(.width(32)) multiplexer_1 (
    .in0(in_4), .in1({32{1'b0}}), .out(multiplexer_1_out), .sel(in_3));  // open: en
  Multiplexer #(.width(32)) multiplexer_2 (
    .in0(in_7), .in1({32{1'b0}}), .out(multiplexer_2_out), .sel(in_3));  // open: en
  Register #(.width(32)) register_1 (.D(multiplexer_1_out), .en(in_2), .Q(out_9), .clk(in_1));  // open: clr
  Register #(.width(32)) register_2 (.D(multiplexer_2_out), .en(in_2), .Q(out_12), .clk(in_1));  // open: clr
  Multiplexer #(.width(32)) multiplexer_3 (
    .in0(in_6), .in1({32{1'b0}}), .out(multiplexer_3_out), .sel(in_3));  // open: en
  Multiplexer #(.width(32)) multiplexer_4 (
    .in0(in_8), .in1({32{1'b0}}), .out(multiplexer_4_out), .sel(in_3));  // open: en
  Register #(.width(32)) register_3 (.D(multiplexer_3_out), .en(in_2), .Q(out_11), .clk(in_1));  // open: clr
  Register #(.width(32)) register_4 (.D(multiplexer_4_out), .en(in_2), .Q(out_13), .clk(in_1));  // open: clr
  Multiplexer #(.width(32)) multiplexer_5 (
    .in0(in_5), .in1({32{1'b0}}), .out(multiplexer_5_out), .sel(in_3));  // open: en
  Register #(.width(32)) register_5 (.D(multiplexer_5_out), .en(in_2), .Q(out_10), .clk(in_1));  // open: clr

  // Other names for the same wires on the sheet: clear = in_3; Control[31:0] = in_6; ControlOut[31:0] = out_11;
  //   enable = in_2; instruction[31:0] = in_4; instructionOut[31:0] = out_9; PC[31:0] = in_5; PCOut[31:0] = out_10;
  //   rS[31:0] = in_7; rSOut[31:0] = out_12; rT[31:0] = in_8; rTOut[31:0] = out_13; T = in_1
endmodule

module PipeIFID (
  input  in_1,
  input  in_2,
  input  in_3,
  input  [31:0] in_4,
  input  [31:0] in_5,
  output [31:0] out_6,
  output [31:0] out_7
);

  wire [31:0] Control, ControlOut, multiplexer_1_out, multiplexer_2_out, multiplexer_3_out;

  Multiplexer #(.width(32)) multiplexer_1 (
    .in0(in_4), .in1({32{1'b0}}), .out(multiplexer_1_out), .sel(in_3));  // open: en
  Multiplexer #(.width(32)) multiplexer_2 (
    .in0(in_5), .in1({32{1'b0}}), .out(multiplexer_2_out), .sel(in_3));  // open: en
  Register #(.width(32)) register_1 (.D(multiplexer_1_out), .en(in_2), .Q(out_6), .clk(in_1));  // open: clr
  Register #(.width(32)) register_2 (.D(multiplexer_2_out), .en(in_2), .Q(out_7), .clk(in_1));  // open: clr
  Multiplexer #(.width(32)) multiplexer_3 (
    .in0(Control), .in1({32{1'b0}}), .out(multiplexer_3_out), .sel(in_3));  // open: en
  Register #(.width(32)) register_3 (.D(multiplexer_3_out), .en(in_2), .Q(ControlOut), .clk(in_1));  // open: clr

  // Other names for the same wires on the sheet: clear = in_3; enable = in_2; instruction[31:0] = in_4;
  //   instructionOut[31:0] = out_6; PC[31:0] = in_5; PCOut[31:0] = out_7; T = in_1
endmodule

module PipeEXMEM (
  input  in_1,
  input  in_2,
  input  in_3,
  input  [31:0] in_4,
  input  [31:0] PC,
  input  [31:0] in_6,
  input  [31:0] in_7,
  input  [31:0] in_8,
  input  [31:0] in_9,
  output [31:0] out_10,
  output [31:0] out_11,
  output [31:0] out_12,
  output [31:0] PCOut,
  output [31:0] out_14,
  output [31:0] out_15,
  output [31:0] out_16
);

  wire [31:0] multiplexer_1_out, multiplexer_2_out, multiplexer_3_out, multiplexer_4_out, multiplexer_5_out,
       multiplexer_6_out;

  Multiplexer #(.width(32)) multiplexer_1 (
    .in0(in_4), .in1({32{1'b0}}), .out(multiplexer_1_out), .sel(in_3));  // open: en
  Multiplexer #(.width(32)) multiplexer_2 (
    .in0(in_7), .in1({32{1'b0}}), .out(multiplexer_2_out), .sel(in_3));  // open: en
  Register #(.width(32)) register_1 (.D(multiplexer_1_out), .en(in_2), .Q(out_12), .clk(in_1));  // open: clr
  Register #(.width(32)) register_2 (.D(multiplexer_2_out), .en(in_2), .Q(out_15), .clk(in_1));  // open: clr
  Multiplexer #(.width(32)) multiplexer_3 (
    .in0(in_6), .in1({32{1'b0}}), .out(multiplexer_3_out), .sel(in_3));  // open: en
  Multiplexer #(.width(32), .enable("false")) multiplexer_4 (
    .in0(in_8), .in1({32{1'b0}}), .out(multiplexer_4_out), .sel(in_3));
  Register #(.width(32)) register_3 (.D(multiplexer_3_out), .en(in_2), .Q(out_14), .clk(in_1));  // open: clr
  Register #(.width(32)) register_4 (.D(multiplexer_4_out), .en(in_2), .Q(out_16), .clk(in_1));  // open: clr
  Multiplexer #(.width(32)) multiplexer_5 (
    .in0(PC), .in1({32{1'b0}}), .out(multiplexer_5_out), .sel(in_3));  // open: en
  Multiplexer #(.width(32)) multiplexer_6 (
    .in0(in_9), .in1({32{1'b0}}), .out(multiplexer_6_out), .sel(in_3));  // open: en
  Register #(.width(32)) register_5 (.D(multiplexer_5_out), .en(in_2), .Q(PCOut), .clk(in_1));  // open: clr
  Register #(.width(32)) register_6 (.D(multiplexer_6_out), .en(in_2), .Q(out_10), .clk(in_1));  // open: clr

  assign out_11 = out_10;

  // Other names for the same wires on the sheet: aluR[31:0] = in_9; aluROut[31:0] = out_10; clear = in_3;
  //   Control[31:0] = in_6; ControlOut[31:0] = out_14; enable = in_2; instruction[31:0] = in_4;
  //   instructionOut[31:0] = out_12; rS[31:0] = in_7; rSOut[31:0] = out_15; rT[31:0] = in_8; rTOut[31:0] = out_16;
  //   T = in_1
endmodule

module PipeMEMWB (
  input  T,
  input  enable,
  input  clear,
  input  [31:0] instruction,
  input  [31:0] PC,
  input  [31:0] control,
  input  [31:0] rS,
  input  [31:0] AluR,
  output [31:0] instructionOut,
  output [31:0] PCOut,
  output [31:0] ControlOut,
  output [31:0] rSOut,
  output [31:0] AluROut
);

  wire [31:0] multiplexer_1_out, multiplexer_2_out, multiplexer_3_out, multiplexer_4_out, multiplexer_5_out,
       multiplexer_6_out;

  Multiplexer #(.width(32)) multiplexer_1 (
    .in0(instruction), .in1({32{1'b0}}), .out(multiplexer_1_out), .sel(clear));  // open: en
  Multiplexer #(.width(32)) multiplexer_2 (
    .in0(rS), .in1({32{1'b0}}), .out(multiplexer_2_out), .sel(clear));  // open: en
  Register #(.width(32)) register_1 (.D(multiplexer_1_out), .en(enable), .Q(instructionOut), .clk(T));  // open: clr
  Register #(.width(32)) register_2 (.D(multiplexer_2_out), .en(enable), .Q(rSOut), .clk(T));  // open: clr
  Multiplexer #(.width(32)) multiplexer_3 (
    .in0(control), .in1({32{1'b0}}), .out(multiplexer_3_out), .sel(clear));  // open: en
  Multiplexer #(.width(32)) multiplexer_4 (
    .in0(PC), .in1({32{1'b0}}), .out(multiplexer_4_out), .sel(clear));  // open: en
  Register #(.width(32)) register_3 (.D(multiplexer_3_out), .en(enable), .Q(ControlOut), .clk(T));  // open: clr
  Register #(.width(32)) register_4 (.D(multiplexer_4_out), .en(enable), .Q(PCOut), .clk(T));  // open: clr
  Multiplexer #(.width(32)) multiplexer_5 (
    .in0(PC), .in1({32{1'b0}}), .out(multiplexer_5_out), .sel(clear));  // open: en
  Multiplexer #(.width(32)) multiplexer_6 (
    .in0(AluR), .in1({32{1'b0}}), .out(multiplexer_6_out), .sel(clear));  // open: en
  Register #(.width(32)) register_5 (.D(multiplexer_5_out), .en(enable), .Q(PCOut), .clk(T));  // open: clr
  Register #(.width(32)) register_6 (.D(multiplexer_6_out), .en(enable), .Q(AluROut), .clk(T));  // open: clr

  // Other names for the same wires on the sheet: ramResult[31:0] = rS; ramResultOut[31:0] = rSOut
endmodule

module Bubble (
  input  rARead,
  input  rBRead,
  input  [4:0] rA,
  input  [4:0] rB,
  input  rWE_EX,
  input  [4:0] rW_EX,
  input  [31:0] instr_EX,
  output bubble
);

  wire and_1_out, and_2_out, comparator_1_eq, comparator_2_eq, comparator_3_eq, comparator_4_eq,
       comparator_5_eq, comparator_6_eq, comparator_7_eq, or_1_out, or_2_out;

  Comparator #(.width(5)) comparator_1 (.a(rW_EX), .b({5{1'b0}}), .eq(comparator_1_eq));  // open: gt, lt
  Comparator #(.width(5)) comparator_2 (.a(rA), .b({5{1'b0}}), .eq(comparator_2_eq));  // open: gt, lt
  Comparator #(.width(5)) comparator_3 (.a(rB), .b({5{1'b0}}), .eq(comparator_3_eq));  // open: gt, lt
  Comparator #(.width(5)) comparator_4 (.a(rW_EX), .b(rA), .eq(comparator_4_eq));  // open: gt, lt
  Comparator #(.width(5)) comparator_5 (.a(rW_EX), .b(rB), .eq(comparator_5_eq));  // open: gt, lt
  Comparator #(.width(6)) comparator_6 (.a(instr_EX[31:26]), .b(6'b100011), .eq(comparator_6_eq));  // open: gt, lt
  Comparator #(.width(6)) comparator_7 (.a(instr_EX[31:26]), .b(6'b100100), .eq(comparator_7_eq));  // open: gt, lt
  and and_1 (and_1_out, rARead, ~comparator_1_eq, comparator_4_eq, ~comparator_2_eq, rWE_EX);  // AND_Gate
  and and_2 (and_2_out, rWE_EX, ~comparator_1_eq, comparator_5_eq, ~comparator_3_eq, rBRead);  // AND_Gate
  or or_1 (or_1_out, and_1_out, and_2_out);
  or or_2 (or_2_out, comparator_6_eq, comparator_7_eq);
  and and_3 (bubble, or_1_out, or_2_out);
endmodule

module Redirect (
  input  rARead,
  input  rBRead,
  input  [4:0] rA,
  input  [4:0] rB,
  input  rWE_EX,
  input  [4:0] rW_ME,
  input  rWE_EX_2,
  input  [4:0] rW_WB,
  output [3:0] redirect
);

  wire comparator_1_eq, comparator_2_eq, comparator_3_eq, comparator_4_eq, comparator_5_eq, comparator_6_eq,
       comparator_7_eq, comparator_8_eq;

  Comparator #(.width(5)) comparator_1 (.a(rW_ME), .b({5{1'b0}}), .eq(comparator_1_eq));  // open: gt, lt
  Comparator #(.width(5)) comparator_2 (.a(rW_WB), .b({5{1'b0}}), .eq(comparator_2_eq));  // open: gt, lt
  Comparator #(.width(5)) comparator_3 (.a(rA), .b({5{1'b0}}), .eq(comparator_3_eq));  // open: gt, lt
  Comparator #(.width(5)) comparator_4 (.a(rB), .b({5{1'b0}}), .eq(comparator_4_eq));  // open: gt, lt
  Comparator #(.width(5)) comparator_5 (.a(rW_ME), .b(rA), .eq(comparator_5_eq));  // open: gt, lt
  Comparator #(.width(5)) comparator_6 (.a(rW_ME), .b(rB), .eq(comparator_6_eq));  // open: gt, lt
  Comparator #(.width(5)) comparator_7 (.a(rW_WB), .b(rA), .eq(comparator_7_eq));  // open: gt, lt
  Comparator #(.width(5)) comparator_8 (.a(rW_WB), .b(rB), .eq(comparator_8_eq));  // open: gt, lt
  and and_1 (redirect[3], rARead, ~comparator_1_eq, comparator_5_eq, ~comparator_3_eq, rWE_EX);  // AND_Gate
  and and_2 (redirect[2], rWE_EX, ~comparator_1_eq, comparator_6_eq, ~comparator_4_eq, rBRead);  // AND_Gate
  and and_3 (redirect[1], rARead, ~comparator_2_eq, comparator_7_eq, ~comparator_3_eq, rWE_EX_2);  // AND_Gate
  and and_4 (redirect[0], rWE_EX_2, ~comparator_2_eq, comparator_8_eq, ~comparator_4_eq, rBRead);  // AND_Gate

  // Other names for the same wires on the sheet: rWE_ME = rWE_EX; rWE_WB = rWE_EX_2

  // Notes on the sheet:
  //   0001 -> redirect rB_WB
  //   0010 -> redirect rA_WB
  //   0100 -> redirect rB_ME
  //   1000 -> redirect rA_ME
  //   can be stacked with 'or'
endmodule
