// Logisim project cpu28_lsz.circ as structural Verilog: 21 circuits, main circuit ◇单周期MIPS
module \单周期MIPS  (
);

  wire bgzt, buffer_1_out, buffer_2_out, buffer_3_out, buffer_4_out, buffer_5_out, buffer_6_out,
       buffer_8_out, CLK, display, Go, halt, jal, jmp, jr, LBU, Load, Load_CLK, LUISrc, mips_alu_1_equal,
       nor_1_out, not_1_out, not_2_out, or_1_out, RST, run, show, SignedExt, syscall, \条件分支 ,
       \硬布线控制器_1_alu_src , \硬布线控制器_1_beq , \硬布线控制器_1_bne , \硬布线控制器_1_memtoreg , \硬布线控制器_1_memwrite ,
       \硬布线控制器_1_regdst , \硬布线控制器_1_regwrite ;
  wire [3:0] AluOP;
  wire [4:0] multiplexer_5_out, multiplexer_6_out, multiplexer_7_out, multiplexer_8_out, multiplexer_11_out;
  wire [7:0] multiplexer_14_out;
  wire [15:0] \总周期数 , \无条件分支数 , \条件分支成功数 ;
  wire [27:0] \原PC ;
  wire [31:0] adder_2_out, ALUres, Din, LedData, multiplexer_1_out, multiplexer_2_out, multiplexer_3_out,
       multiplexer_4_out, multiplexer_9_out, multiplexer_10_out, multiplexer_12_out, multiplexer_13_out, R1,
       R2, ram_1_data, \加1的PC , \左移2位有符号拓展Imm , \无符号拓展Imm , \有符号拓展Imm ;
  wire [31:2] J_addr;
  wire [31:26] rom_1_data;

  Button \u_总复位  (.out(RST));
  Button \u_继续运行  (.out(Go));
  Clock clock_1 (.out(CLK));
  Button \u_装载断点  (.out(Load));
  Multiplexer #(.width(32)) multiplexer_1 (
    .in0(\加1的PC ), .in1(adder_2_out), .out(multiplexer_1_out), .sel(\条件分支 ));  // open: en
  Hex_Digit_Display hex_digit_display_1 (.value(LedData[27:24]));  // open: dp
  Hex_Digit_Display hex_digit_display_2 (.value(LedData[31:28]));  // open: dp
  buf buffer_1 (buffer_1_out, Load);
  buf buffer_2 (buffer_2_out, buffer_1_out);
  Multiplexer #(.width(32)) multiplexer_2 (
    .in0(multiplexer_1_out), .in1(multiplexer_3_out), .out(multiplexer_2_out), .sel(jmp));  // open: en
  Multiplexer #(.width(32)) multiplexer_3 (
    .in0({J_addr, 2'b00}), .in1(R1), .out(multiplexer_3_out), .sel(jr));  // open: en
  Hex_Digit_Display hex_digit_display_3 (.value(LedData[23:20]));  // open: dp
  Hex_Digit_Display hex_digit_display_4 (.value(LedData[19:16]));  // open: dp
  and and_1 (show, syscall, display);
  Pull_Resistor pull_resistor_1 (.node(display));
  Comparator #(.width(32)) comparator_1 (.a(R2), .b(32'h22), .eq(display));  // open: gt, lt
  buf buffer_3 (buffer_3_out, buffer_2_out);
  buf buffer_4 (buffer_4_out, buffer_6_out);
  buf buffer_5 (buffer_5_out, buffer_3_out);
  buf buffer_6 (buffer_6_out, buffer_5_out);
  Multiplexer #(.width(32)) multiplexer_4 (
    .in0(multiplexer_2_out), .in1(32'h32dc), .out(multiplexer_4_out), .sel(Load));  // open: en
  Hex_Digit_Display hex_digit_display_5 (.value(LedData[15:12]));  // open: dp
  Hex_Digit_Display hex_digit_display_6 (.value(LedData[11:8]));  // open: dp
  buf buffer_7 (Load_CLK, buffer_8_out);
  buf buffer_8 (buffer_8_out, buffer_4_out);
  Register #(.width(32)) PC (.D(multiplexer_4_out), .en(run), .Q({J_addr[31:28], \原PC }), .clk(or_1_out), .clr(RST));
  or or_1 (or_1_out, Load_CLK, CLK);
  Hex_Digit_Display hex_digit_display_7 (.value(LedData[3:0]));  // open: dp
  Hex_Digit_Display hex_digit_display_8 (.value(LedData[7:4]));  // open: dp
  or or_2 (run, Go, not_1_out);
  not not_1 (not_1_out, halt);
  Adder #(.width(32)) adder_1 (.a({J_addr[31:28], \原PC }), .b(32'h4), .out(\加1的PC ));  // open: cin, cout
  Adder #(.width(32)) adder_2 (.a(\加1的PC ), .b(\左移2位有符号拓展Imm ), .out(adder_2_out));  // open: cin, cout
  // Probe on adder_2_out
  and and_2 (halt, syscall, not_2_out);
  not not_2 (not_2_out, display);
  Register #(.width(32)) register_1 (.D(R1), .en(show), .Q(LedData), .clk(CLK), .clr(RST));
  ROM #(.addrWidth(10), .dataWidth(32)) rom_1 (.addr(\原PC [11:2]), .data({rom_1_data, J_addr[27:2]}));  // open: sel
  // Probe on \总周期数 
  // Probe on \无条件分支数 
  // Probe on \条件分支成功数 
  Multiplexer #(.width(5)) multiplexer_5 (
    .in0(J_addr[27:23]), .in1(5'b00100), .out(multiplexer_5_out), .sel(syscall));  // open: en
  assign \无符号拓展Imm  = {{16{1'b0}}, J_addr[17:2]};  // Bit_Extender bit_extender_1
  assign \有符号拓展Imm  = {{16{J_addr[17]}}, J_addr[17:2]};  // Bit_Extender bit_extender_2
  Multiplexer #(.width(5)) multiplexer_6 (
    .in0(J_addr[22:18]), .in1(5'b00010), .out(multiplexer_6_out), .sel(syscall));  // open: en
  Multiplexer #(.width(5)) multiplexer_7 (
    .in0(J_addr[22:18]), .in1(J_addr[17:13]), .out(multiplexer_7_out), .sel(\硬布线控制器_1_regdst ));  // open: en
  Multiplexer #(.width(5)) multiplexer_8 (
    .in0(multiplexer_7_out), .in1({5{1'b1}}), .out(multiplexer_8_out), .sel(jal));  // open: en
  assign \左移2位有符号拓展Imm  = {{14{J_addr[17]}}, {J_addr[17:2], 2'b00}};  // Bit_Extender bit_extender_3
  Pull_Resistor pull_resistor_2 (.node(\条件分支 ));
  \硬布线控制器  \u_硬布线控制器_1  (
    .Func(J_addr[7:2]), .OP(rom_1_data), .ALU_OP(AluOP), .MemToReg(\硬布线控制器_1_memtoreg ),
    .MemWrite(\硬布线控制器_1_memwrite ), .ALU_SRC(\硬布线控制器_1_alu_src ), .RegWrite(\硬布线控制器_1_regwrite ),
    .SysCALL(syscall), .SignedExt(SignedExt), .RegDst(\硬布线控制器_1_regdst ), .JR(jr), .JMP(jmp),
    .Beq(\硬布线控制器_1_beq ), .JAL(jal), .Bne(\硬布线控制器_1_bne ), .LUISrc(LUISrc), .bgtz(bgzt), .LBU(LBU));
  MIPS_Regifile mips_regifile_1 (
    .Din(Din), .Clk(CLK), .R1(R1), .R2(R2), .WE(\硬布线控制器_1_regwrite ), .W_num(multiplexer_8_out),
    .R1_num(multiplexer_5_out), .R2_num(multiplexer_6_out));
  Multiplexer #(.width(32)) multiplexer_9 (
    .in0(\无符号拓展Imm ), .in1(\有符号拓展Imm ), .out(multiplexer_9_out), .sel(SignedExt));  // open: en
  assign \条件分支  = bgzt ? nor_1_out : 1'bz;  // Controlled_Buffer controlled_buffer_1
  assign \条件分支  = \硬布线控制器_1_beq  ? mips_alu_1_equal : 1'bz;  // Controlled_Buffer controlled_buffer_2
  assign \条件分支  = \硬布线控制器_1_bne  ? ~mips_alu_1_equal : 1'bz;  // Controlled_Inverter controlled_inverter_1
  nor nor_1 (nor_1_out, ALUres[0], mips_alu_1_equal);
  Multiplexer #(.width(32)) multiplexer_10 (
    .in0(R2), .in1(multiplexer_9_out), .out(multiplexer_10_out), .sel(\硬布线控制器_1_alu_src ));  // open: en
  // Probe on multiplexer_9_out
  // Probe on AluOP
  // Probe on Din
  // Probe on \有符号拓展Imm 
  // Probe on LedData
  // Probe on ALUres
  // Probe on R1
  // Probe on R2
  MIPS_ALU mips_alu_1 (
    .X(R1), .Y(multiplexer_10_out), .AluOP(AluOP), .Equal(mips_alu_1_equal), .Result(ALUres),
    .shamt(multiplexer_11_out));  // open: Result_2
  Multiplexer #(.width(5)) multiplexer_11 (
    .in0(J_addr[12:8]), .in1(5'b10000), .out(multiplexer_11_out), .sel(LUISrc));  // open: en
  // Probe on R2
  RAM #(.addrWidth(10), .dataWidth(32), .bus("separate")) ram_1 (
    .addr(ALUres[11:2]), .din(R2), .data(ram_1_data), .str(\硬布线控制器_1_memwrite ), .clk(CLK), .clr(RST));  // open: sel, ld
  Multiplexer #(.width(32)) multiplexer_12 (
    .in0(ALUres), .in1(ram_1_data), .out(multiplexer_12_out), .sel(\硬布线控制器_1_memtoreg ));  // open: en
  Multiplexer #(.width(32)) multiplexer_13 (
    .in0(multiplexer_12_out), .in1(\加1的PC ), .out(multiplexer_13_out), .sel(jal));  // open: en
  Multiplexer #(.select(2), .width(8)) multiplexer_14 (
    .in0(multiplexer_13_out[7:0]), .in1(multiplexer_13_out[15:8]), .in2(multiplexer_13_out[23:16]),
    .in3(multiplexer_13_out[31:24]), .out(multiplexer_14_out), .sel(ALUres[1:0]));  // open: en
  Multiplexer #(.width(32)) multiplexer_15 (
    .in0(multiplexer_13_out), .in1({{24{1'b0}}, multiplexer_14_out}), .out(Din), .sel(LBU));  // open: en
  Counter #(.width(16), .max('hffff)) counter_1 (
    .count(run), .Q(\总周期数 ), .clk(CLK), .clr(RST));  // open: load, D, carry
  Counter #(.width(16), .max('hffff)) counter_2 (
    .count(\条件分支 ), .Q(\条件分支成功数 ), .clk(CLK), .clr(RST));  // open: load, D, carry
  // Probe on nothing
  Counter #(.width(16), .max('hffff)) counter_3 (
    .count(jmp), .Q(\无条件分支数 ), .clk(CLK), .clr(RST));  // open: load, D, carry

  // Other names for the same wires on the sheet: Shamt[4:0] = J_addr[12:8]; 原PC[31:28] = J_addr[31:28]

  // Notes on the sheet:
  //   数码管输出应该用寄存器锁存，否则显示数据只能一闪而过
  //   可以通过项目增加Logisim库的方式将前几次实验完成的电路作为子电路引入到本电路中使用
  //   数码管输出
  //   指令存储器
  //   指令字
  //   contents of rom_1 (hex, n*v repeats v):
  //   20110001 8000c05 20110001 20120002 20130003 8000c09 20110001 20120002 20130003 8000c0d 20110001
  //   20120002 20130003 8000c11 20110001 20120002 20130003 c000cf6 20100001 20110001 118fc0 112020
  //   20020022 c 118882 12200001 8000c15 112020 20020022 c 20110001 118880 112020 20020022 c 12200001
  //   8000c1f 20110001 118fc0 112020 20020022 c 1188c3 112020 20020022 c 118903 112020 20020022 c 118903
  //   112020 20020022 c 118903 112020 20020022 c 118903 112020 20020022 c 118903 112020 20020022 c 118903
  //   112020 20020022 c 118903 112020 20020022 c 20100001 109fc0 139fc3 8021 2012000c 24160003 26100001
  //   3210000f 20080008 20090001 139900 2709825 132020 20020022 c 1094022 1500fff9 22100001 2018000f
  //   2188024 108700 20080008 20090001 139902 2709825 132021 20020022 c 1094022 1500fff9 108702 2c9b022
  //   12c00001 8000c50 4020 1084027 84400 3508ffff 82021 20020022 c 2010ffff 20110000 ae300000 22100001
  //   22310004 ae300000 22100001 22310004 ae300000 22100001 22310004 ae300000 22100001 22310004 ae300000
  //   22100001 22310004 ae300000 22100001 22310004 ae300000 22100001 22310004 ae300000 22100001 22310004
  //   ae300000 22100001 22310004 ae300000 22100001 22310004 ae300000 22100001 22310004 ae300000 22100001
  //   22310004 ae300000 22100001 22310004 ae300000 22100001 22310004 ae300000 22100001 22310004 ae300000
  //   22100001 22310004 22100001 8020 2011003c 8e130000 8e340000 274402a 11000002 ae330000 ae140000
  //   2231fffc 1611fff8 102020 20020022 c 22100004 2011003c 1611fff2 20020032 c 200b0008 3c11fedc 3631ffff
  //   112020 20020022 c 3c11ba98 112020 c 3c117654 112020 c 3c113210 112020 c 216bffff 1560fff0 2002000a c
  //   2008ffff 20090000 20111997 112020 20020022 c 2288820 2e291949 1120fffa 2002000a c 20090000 200b0010
  //   34118483 20120404 118c00 129400 36318281 22520404 ad310000 2328820 21290004 216bffff 1560fffb
  //   200b0020 20090000 91310000 112020 20020022 c 21290001 216bffff 1560fff9 2002000a c 2011000f 112020
  //   20020022 c 2231ffff 1e20fffb 2002000a c 20100000 22100001 102020 20020022 c 22100002 102020 20020022
  //   c 22100003 102020 20020022 c 22100004 102020 20020022 c 22100005 102020 20020022 c 22100006 102020
  //   20020022 c 22100007 102020 20020022 c 22100008 102020 20020022 20020022 c 3e00008
  //   总复位信号应将除ROM以外所有存储组件全部清零
  //   OP
  //   Func
  //   rs
  //   rt
  //   rd
  //   Imm
  //   Shamt
  //   addr
  //   JMP
  //   JR
  //   LUISrc
  //   bgtz
  //   OP
  //   Func
  //   Beq
  //   Bne
  //   MemToReg
  //   MemWrite
  //   AluOP
  //   AluSrcB
  //   RegWrite
  //   JAL
  //   RegDst
  //   Syscall
endmodule

// 单周期硬布线控制器
module \硬布线控制器  (
  input  [5:0] OP,
  input  [5:0] Func,
  output [3:0] ALU_OP,
  output MemToReg,
  output MemWrite,
  output ALU_SRC,
  output RegWrite,
  output SysCALL,
  output SignedExt,
  output RegDst,
  output Beq,
  output Bne,
  output JR,
  output JMP,
  output JAL,
  output LUISrc,
  output bgtz,
  output LBU
);

  \运算控制器  \u_运算控制器_1  (
    .OP0(OP[0]), .OP1(OP[1]), .OP2(OP[2]), .OP3(OP[3]), .OP4(OP[4]), .OP5(OP[5]), .F0(Func[0]), .F1(Func[1]),
    .F2(Func[2]), .F3(Func[3]), .F4(Func[4]), .F5(Func[5]), .S0(ALU_OP[0]), .S1(ALU_OP[1]), .S2(ALU_OP[2]),
    .S3(ALU_OP[3]));
  \控制信号生成  \u_控制信号生成_1  (
    .OP0(OP[0]), .OP1(OP[1]), .OP2(OP[2]), .OP3(OP[3]), .OP4(OP[4]), .OP5(OP[5]), .F0(Func[0]), .F1(Func[1]),
    .F2(Func[2]), .F3(Func[3]), .F4(Func[4]), .F5(Func[5]), .MemToReg(MemToReg), .MemWrite(MemWrite),
    .ALU_SRC(ALU_SRC), .RegWrite(RegWrite), .SysCALL(SysCALL), .SignedExt(SignedExt), .RegDst(RegDst),
    .BEQ(Beq), .BNE(Bne), .JR(JR), .JMP(JMP), .JAL(JAL));
  \扩展信号生成  \u_扩展信号生成_1  (
    .OP0(OP[0]), .OP1(OP[1]), .OP2(OP[2]), .OP3(OP[3]), .OP4(OP[4]), .OP5(OP[5]), .F0(Func[0]), .F1(Func[1]),
    .F2(Func[2]), .F3(Func[3]), .F4(Func[4]), .F5(Func[5]), .LUISrc(LUISrc), .bgtz(bgtz), .LBU(LBU));

  // Other names for the same wires on the sheet: OP_CODE[5:0] = OP

  // Notes on the sheet:
  //   运算器控制器，根据指令生成运算器功能选择信号
  //   控制信号生成，产生数据通路需要的其他控制信号
endmodule

// 运算器控制器
module \运算控制器  (
  input  OP0,
  input  OP1,
  input  OP2,
  input  OP3,
  input  OP4,
  input  OP5,
  input  F0,
  input  F1,
  input  F2,
  input  F3,
  input  F4,
  input  F5,
  output S0,
  output S1,
  output S2,
  output S3
);

  wire and_1_out, and_2_out, and_3_out, and_4_out, and_5_out, and_6_out, and_7_out, and_8_out, and_9_out,
       and_10_out, and_11_out, and_12_out, and_13_out, and_14_out, and_15_out, and_16_out, and_17_out,
       and_18_out, and_19_out, and_20_out, and_21_out, and_22_out, and_23_out, and_24_out, and_25_out,
       and_26_out, and_27_out, and_28_out, and_29_out, and_30_out, and_31_out, and_32_out, and_33_out,
       and_34_out, and_35_out, and_36_out, and_37_out, and_38_out, and_39_out, and_40_out, and_41_out,
       not_1_out, not_2_out, not_3_out, not_4_out, not_5_out, not_6_out, not_7_out, not_8_out, not_9_out,
       not_10_out, not_11_out, not_12_out, not_13_out, not_14_out, not_15_out, not_16_out, not_17_out,
       not_18_out, not_19_out, not_20_out, not_21_out, not_22_out, not_23_out, not_24_out, not_25_out,
       not_26_out, not_27_out, not_28_out, not_29_out, not_30_out, not_31_out, not_32_out, not_33_out,
       not_34_out, not_35_out, not_36_out, not_37_out, not_38_out, not_39_out, not_40_out, not_41_out,
       not_42_out, not_43_out, not_44_out, not_45_out, not_46_out, not_47_out, not_48_out, not_49_out,
       not_50_out, not_51_out, not_52_out, not_53_out, not_54_out, not_55_out, not_56_out, not_57_out,
       not_58_out, not_59_out, not_60_out, not_61_out, not_62_out, not_63_out, not_64_out, not_65_out,
       not_66_out, not_67_out, not_68_out, not_69_out, not_70_out, not_71_out, not_72_out, not_73_out,
       not_74_out, not_75_out, not_76_out, not_77_out, not_78_out, not_79_out, not_80_out, not_81_out,
       not_82_out, not_83_out, not_84_out, not_85_out, not_86_out, not_87_out, not_88_out, not_89_out,
       not_90_out, not_91_out, not_92_out, not_93_out, not_94_out, not_95_out, not_96_out, not_97_out,
       not_98_out, not_99_out, not_100_out, not_101_out, not_102_out, not_103_out, not_104_out, not_105_out,
       not_106_out, not_107_out, not_108_out, not_109_out, not_110_out, not_111_out, not_112_out,
       not_113_out, not_114_out, not_115_out, not_116_out, not_117_out, not_118_out, not_119_out,
       not_120_out, not_121_out, not_122_out, not_123_out, not_124_out, not_125_out, not_126_out,
       not_127_out, not_128_out, not_129_out, not_130_out, not_131_out, not_132_out, not_133_out,
       not_134_out, not_135_out, not_136_out, not_137_out, not_138_out, not_139_out, not_140_out,
       not_141_out, not_142_out, not_143_out, not_144_out, not_145_out, not_146_out, not_147_out,
       not_148_out, not_149_out, not_150_out, not_151_out, not_152_out, not_153_out, not_154_out,
       not_155_out, not_156_out, not_157_out, not_158_out, not_159_out, not_160_out, not_161_out,
       not_162_out, not_163_out, not_164_out, not_165_out, not_166_out, not_167_out, not_168_out,
       not_169_out, not_170_out, not_171_out, not_172_out, not_173_out, not_174_out, not_175_out,
       not_176_out, not_177_out, not_178_out, not_179_out, not_180_out, not_181_out, not_182_out,
       not_183_out, not_184_out, not_185_out, not_186_out, not_187_out, not_188_out, not_189_out,
       not_190_out, not_191_out, not_192_out, not_193_out, not_194_out, not_195_out, not_196_out,
       not_197_out, not_198_out, not_199_out, not_200_out, not_201_out, not_202_out, not_203_out,
       not_204_out, not_205_out, not_206_out, not_207_out, not_208_out, not_209_out, not_210_out,
       not_211_out, not_212_out, not_213_out, not_214_out, not_215_out, not_216_out, not_217_out,
       not_218_out, not_219_out, not_220_out, not_221_out, not_222_out, not_223_out, not_224_out,
       not_225_out, not_226_out, not_227_out, not_228_out, not_229_out, not_230_out, not_231_out,
       not_232_out, not_233_out, not_234_out, not_235_out, not_236_out, not_237_out, not_238_out,
       not_239_out, not_240_out, not_241_out, not_242_out, not_243_out, not_244_out, not_245_out,
       not_246_out, not_247_out, not_248_out, not_249_out, not_250_out, not_251_out, not_252_out,
       not_253_out, not_254_out, not_255_out, not_256_out, not_257_out, not_258_out, not_259_out;

  not not_1 (not_1_out, OP5);
  not not_2 (not_2_out, OP4);
  not not_3 (not_3_out, OP3);
  not not_4 (not_4_out, OP2);
  not not_5 (not_5_out, OP1);
  not not_6 (not_6_out, OP0);
  not not_7 (not_7_out, F5);
  not not_8 (not_8_out, F4);
  not not_9 (not_9_out, F3);
  not not_10 (not_10_out, F2);
  not not_11 (not_11_out, OP5);
  not not_12 (not_12_out, OP4);
  not not_13 (not_13_out, OP3);
  not not_14 (not_14_out, OP2);
  not not_15 (not_15_out, OP1);
  not not_16 (not_16_out, OP0);
  not not_17 (not_17_out, F4);
  not not_18 (not_18_out, F3);
  not not_19 (not_19_out, F2);
  not not_20 (not_20_out, F1);
  not not_21 (not_21_out, F0);
  not not_22 (not_22_out, OP5);
  not not_23 (not_23_out, OP4);
  not not_24 (not_24_out, OP3);
  not not_25 (not_25_out, OP2);
  not not_26 (not_26_out, OP1);
  not not_27 (not_27_out, OP0);
  not not_28 (not_28_out, F4);
  not not_29 (not_29_out, F3);
  not not_30 (not_30_out, F2);
  not not_31 (not_31_out, F1);
  not not_32 (not_32_out, OP5);
  not not_33 (not_33_out, OP4);
  not not_34 (not_34_out, OP3);
  not not_35 (not_35_out, OP2);
  not not_36 (not_36_out, OP1);
  not not_37 (not_37_out, OP0);
  not not_38 (not_38_out, F4);
  not not_39 (not_39_out, F3);
  not not_40 (not_40_out, F1);
  not not_41 (not_41_out, F0);
  not not_42 (not_42_out, OP5);
  not not_43 (not_43_out, OP4);
  not not_44 (not_44_out, OP3);
  not not_45 (not_45_out, OP2);
  not not_46 (not_46_out, OP1);
  not not_47 (not_47_out, OP0);
  not not_48 (not_48_out, F4);
  not not_49 (not_49_out, F2);
  not not_50 (not_50_out, F0);
  not not_51 (not_51_out, OP5);
  not not_52 (not_52_out, OP4);
  not not_53 (not_53_out, OP2);
  not not_54 (not_54_out, OP1);
  not not_55 (not_55_out, OP0);
  not not_56 (not_56_out, OP5);
  not not_57 (not_57_out, OP4);
  not not_58 (not_58_out, OP1);
  not not_59 (not_59_out, OP0);
  not not_60 (not_60_out, OP5);
  not not_61 (not_61_out, OP4);
  not not_62 (not_62_out, OP2);
  not not_63 (not_63_out, OP1);
  not not_64 (not_64_out, OP5);
  not not_65 (not_65_out, OP4);
  not not_66 (not_66_out, OP2);
  not not_67 (not_67_out, OP0);
  not not_68 (not_68_out, OP4);
  not not_69 (not_69_out, OP3);
  not not_70 (not_70_out, OP2);
  not not_71 (not_71_out, OP4);
  not not_72 (not_72_out, OP2);
  not not_73 (not_73_out, OP4);
  not not_74 (not_74_out, OP3);
  not not_75 (not_75_out, OP1);
  not not_76 (not_76_out, OP0);
  not not_77 (not_77_out, OP5);
  not not_78 (not_78_out, OP4);
  not not_79 (not_79_out, OP3);
  not not_80 (not_80_out, OP5);
  not not_81 (not_81_out, OP4);
  not not_82 (not_82_out, OP3);
  not not_83 (not_83_out, OP2);
  not not_84 (not_84_out, OP1);
  not not_85 (not_85_out, OP0);
  not not_86 (not_86_out, F5);
  not not_87 (not_87_out, F4);
  not not_88 (not_88_out, F3);
  not not_89 (not_89_out, F2);
  not not_90 (not_90_out, F0);
  not not_91 (not_91_out, OP5);
  not not_92 (not_92_out, OP4);
  not not_93 (not_93_out, OP3);
  not not_94 (not_94_out, OP2);
  not not_95 (not_95_out, OP1);
  not not_96 (not_96_out, OP0);
  not not_97 (not_97_out, F4);
  not not_98 (not_98_out, F3);
  not not_99 (not_99_out, F2);
  not not_100 (not_100_out, F0);
  not not_101 (not_101_out, OP5);
  not not_102 (not_102_out, OP4);
  not not_103 (not_103_out, OP3);
  not not_104 (not_104_out, OP2);
  not not_105 (not_105_out, OP1);
  not not_106 (not_106_out, OP0);
  not not_107 (not_107_out, F4);
  not not_108 (not_108_out, F3);
  not not_109 (not_109_out, F1);
  not not_110 (not_110_out, F0);
  not not_111 (not_111_out, OP5);
  not not_112 (not_112_out, OP4);
  not not_113 (not_113_out, OP3);
  not not_114 (not_114_out, OP2);
  not not_115 (not_115_out, OP1);
  not not_116 (not_116_out, OP0);
  not not_117 (not_117_out, F4);
  not not_118 (not_118_out, F3);
  not not_119 (not_119_out, OP5);
  not not_120 (not_120_out, OP4);
  not not_121 (not_121_out, OP3);
  not not_122 (not_122_out, OP2);
  not not_123 (not_123_out, OP1);
  not not_124 (not_124_out, OP0);
  not not_125 (not_125_out, F4);
  not not_126 (not_126_out, F2);
  not not_127 (not_127_out, F0);
  not not_128 (not_128_out, OP5);
  not not_129 (not_129_out, OP4);
  not not_130 (not_130_out, OP1);
  not not_131 (not_131_out, OP0);
  not not_132 (not_132_out, OP5);
  not not_133 (not_133_out, OP4);
  not not_134 (not_134_out, OP2);
  not not_135 (not_135_out, OP0);
  not not_136 (not_136_out, OP5);
  not not_137 (not_137_out, OP4);
  not not_138 (not_138_out, OP3);
  not not_139 (not_139_out, OP5);
  not not_140 (not_140_out, OP4);
  not not_141 (not_141_out, OP3);
  not not_142 (not_142_out, OP2);
  not not_143 (not_143_out, OP1);
  not not_144 (not_144_out, OP0);
  not not_145 (not_145_out, F4);
  not not_146 (not_146_out, F3);
  not not_147 (not_147_out, F2);
  not not_148 (not_148_out, F1);
  not not_149 (not_149_out, F0);
  not not_150 (not_150_out, OP5);
  not not_151 (not_151_out, OP4);
  not not_152 (not_152_out, OP3);
  not not_153 (not_153_out, OP2);
  not not_154 (not_154_out, OP1);
  not not_155 (not_155_out, OP0);
  not not_156 (not_156_out, F4);
  not not_157 (not_157_out, F3);
  not not_158 (not_158_out, F2);
  not not_159 (not_159_out, F1);
  not not_160 (not_160_out, OP5);
  not not_161 (not_161_out, OP4);
  not not_162 (not_162_out, OP3);
  not not_163 (not_163_out, OP2);
  not not_164 (not_164_out, OP1);
  not not_165 (not_165_out, OP0);
  not not_166 (not_166_out, F4);
  not not_167 (not_167_out, F3);
  not not_168 (not_168_out, F2);
  not not_169 (not_169_out, F0);
  not not_170 (not_170_out, OP5);
  not not_171 (not_171_out, OP4);
  not not_172 (not_172_out, OP3);
  not not_173 (not_173_out, OP2);
  not not_174 (not_174_out, OP1);
  not not_175 (not_175_out, OP0);
  not not_176 (not_176_out, F4);
  not not_177 (not_177_out, F3);
  not not_178 (not_178_out, F1);
  not not_179 (not_179_out, F0);
  not not_180 (not_180_out, OP5);
  not not_181 (not_181_out, OP4);
  not not_182 (not_182_out, OP3);
  not not_183 (not_183_out, OP2);
  not not_184 (not_184_out, OP1);
  not not_185 (not_185_out, OP0);
  not not_186 (not_186_out, F4);
  not not_187 (not_187_out, F2);
  not not_188 (not_188_out, OP5);
  not not_189 (not_189_out, OP4);
  not not_190 (not_190_out, OP2);
  not not_191 (not_191_out, OP1);
  not not_192 (not_192_out, OP0);
  not not_193 (not_193_out, OP5);
  not not_194 (not_194_out, OP4);
  not not_195 (not_195_out, OP1);
  not not_196 (not_196_out, OP0);
  not not_197 (not_197_out, OP5);
  not not_198 (not_198_out, OP4);
  not not_199 (not_199_out, OP2);
  not not_200 (not_200_out, OP1);
  not not_201 (not_201_out, OP4);
  not not_202 (not_202_out, OP3);
  not not_203 (not_203_out, OP2);
  not not_204 (not_204_out, OP4);
  not not_205 (not_205_out, OP2);
  not not_206 (not_206_out, OP5);
  not not_207 (not_207_out, OP4);
  not not_208 (not_208_out, OP2);
  not not_209 (not_209_out, OP4);
  not not_210 (not_210_out, OP3);
  not not_211 (not_211_out, OP1);
  not not_212 (not_212_out, OP0);
  not not_213 (not_213_out, OP5);
  not not_214 (not_214_out, OP4);
  not not_215 (not_215_out, OP3);
  not not_216 (not_216_out, OP2);
  not not_217 (not_217_out, OP1);
  not not_218 (not_218_out, OP0);
  not not_219 (not_219_out, F4);
  not not_220 (not_220_out, F3);
  not not_221 (not_221_out, F1);
  not not_222 (not_222_out, OP5);
  not not_223 (not_223_out, OP4);
  not not_224 (not_224_out, OP3);
  not not_225 (not_225_out, OP2);
  not not_226 (not_226_out, OP1);
  not not_227 (not_227_out, OP0);
  not not_228 (not_228_out, F4);
  not not_229 (not_229_out, F3);
  not not_230 (not_230_out, OP5);
  not not_231 (not_231_out, OP4);
  not not_232 (not_232_out, OP3);
  not not_233 (not_233_out, OP2);
  not not_234 (not_234_out, OP1);
  not not_235 (not_235_out, OP0);
  not not_236 (not_236_out, F4);
  not not_237 (not_237_out, F2);
  not not_238 (not_238_out, F0);
  not not_239 (not_239_out, OP5);
  not not_240 (not_240_out, OP4);
  not not_241 (not_241_out, OP3);
  not not_242 (not_242_out, OP2);
  not not_243 (not_243_out, OP1);
  not not_244 (not_244_out, OP0);
  not not_245 (not_245_out, F4);
  not not_246 (not_246_out, F2);
  not not_247 (not_247_out, OP5);
  not not_248 (not_248_out, OP4);
  not not_249 (not_249_out, OP2);
  not not_250 (not_250_out, OP0);
  not not_251 (not_251_out, OP5);
  not not_252 (not_252_out, OP4);
  not not_253 (not_253_out, OP1);
  not not_254 (not_254_out, OP5);
  not not_255 (not_255_out, OP4);
  not not_256 (not_256_out, OP2);
  not not_257 (not_257_out, OP5);
  not not_258 (not_258_out, OP4);
  not not_259 (not_259_out, OP3);
  and and_1 (and_1_out, not_1_out, not_2_out, not_3_out, not_4_out, not_5_out, not_6_out, not_7_out, not_8_out, not_9_out, not_10_out, F1, F0);
  and and_2 (and_2_out, not_11_out, not_12_out, not_13_out, not_14_out, not_15_out, not_16_out, F5, not_17_out, not_18_out, not_19_out, not_20_out, not_21_out);
  and and_3 (and_3_out, not_22_out, not_23_out, not_24_out, not_25_out, not_26_out, not_27_out, F5, not_28_out, not_29_out, not_30_out, not_31_out, F0);
  and and_4 (and_4_out, not_32_out, not_33_out, not_34_out, not_35_out, not_36_out, not_37_out, F5, not_38_out, not_39_out, F2, not_40_out, not_41_out);
  and and_5 (and_5_out, not_42_out, not_43_out, not_44_out, not_45_out, not_46_out, not_47_out, F5, not_48_out, F3, not_49_out, F1, not_50_out);
  and and_6 (and_6_out, not_51_out, not_52_out, OP3, not_53_out, not_54_out, not_55_out);
  and and_7 (and_7_out, not_56_out, not_57_out, OP3, OP2, not_58_out, not_59_out);
  and and_8 (and_8_out, not_60_out, not_61_out, OP3, not_62_out, not_63_out, OP0);
  and and_9 (and_9_out, not_64_out, not_65_out, OP3, not_66_out, OP1, not_67_out);
  and and_10 (and_10_out, OP5, not_68_out, not_69_out, not_70_out, OP1, OP0);
  and and_11 (and_11_out, OP5, not_71_out, OP3, not_72_out, OP1, OP0);
  and and_12 (and_12_out, OP5, not_73_out, not_74_out, OP2, not_75_out, not_76_out);
  and and_13 (and_13_out, not_77_out, not_78_out, not_79_out, OP2, OP1, OP0);
  and and_14 (and_14_out, not_80_out, not_81_out, not_82_out, not_83_out, not_84_out, not_85_out, not_86_out, not_87_out, not_88_out, not_89_out, F1, not_90_out);
  and and_15 (and_15_out, not_91_out, not_92_out, not_93_out, not_94_out, not_95_out, not_96_out, F5, not_97_out, not_98_out, not_99_out, F1, not_100_out);
  and and_16 (and_16_out, not_101_out, not_102_out, not_103_out, not_104_out, not_105_out, not_106_out, F5, not_107_out, not_108_out, F2, not_109_out, not_110_out);
  and and_17 (and_17_out, not_111_out, not_112_out, not_113_out, not_114_out, not_115_out, not_116_out, F5, not_117_out, not_118_out, F2, F1, F0);
  and and_18 (and_18_out, not_119_out, not_120_out, not_121_out, not_122_out, not_123_out, not_124_out, F5, not_125_out, F3, not_126_out, F1, not_127_out);
  and and_19 (and_19_out, not_128_out, not_129_out, OP3, OP2, not_130_out, not_131_out);
  and and_20 (and_20_out, not_132_out, not_133_out, OP3, not_134_out, OP1, not_135_out);
  and and_21 (and_21_out, not_136_out, not_137_out, not_138_out, OP2, OP1, OP0);
  and and_22 (and_22_out, not_139_out, not_140_out, not_141_out, not_142_out, not_143_out, not_144_out, F5, not_145_out, not_146_out, not_147_out, not_148_out, not_149_out);
  and and_23 (and_23_out, not_150_out, not_151_out, not_152_out, not_153_out, not_154_out, not_155_out, F5, not_156_out, not_157_out, not_158_out, not_159_out, F0);
  and and_24 (and_24_out, not_160_out, not_161_out, not_162_out, not_163_out, not_164_out, not_165_out, F5, not_166_out, not_167_out, not_168_out, F1, not_169_out);
  and and_25 (and_25_out, not_170_out, not_171_out, not_172_out, not_173_out, not_174_out, not_175_out, F5, not_176_out, not_177_out, F2, not_178_out, not_179_out);
  and and_26 (and_26_out, not_180_out, not_181_out, not_182_out, not_183_out, not_184_out, not_185_out, F5, not_186_out, F3, not_187_out, F1, F0);
  and and_27 (and_27_out, not_188_out, not_189_out, OP3, not_190_out, not_191_out, not_192_out);
  and and_28 (and_28_out, not_193_out, not_194_out, OP3, OP2, not_195_out, not_196_out);
  and and_29 (and_29_out, not_197_out, not_198_out, OP3, not_199_out, not_200_out, OP0);
  and and_30 (and_30_out, OP5, not_201_out, not_202_out, not_203_out, OP1, OP0);
  and and_31 (and_31_out, OP5, not_204_out, OP3, not_205_out, OP1, OP0);
  and and_32 (and_32_out, not_206_out, not_207_out, OP3, not_208_out, OP1, OP0);
  and and_33 (and_33_out, OP5, not_209_out, not_210_out, OP2, not_211_out, not_212_out);
  and and_34 (and_34_out, not_213_out, not_214_out, not_215_out, not_216_out, not_217_out, not_218_out, F5, not_219_out, not_220_out, F2, not_221_out, F0);
  and and_35 (and_35_out, not_222_out, not_223_out, not_224_out, not_225_out, not_226_out, not_227_out, F5, not_228_out, not_229_out, F2, F1, F0);
  and and_36 (and_36_out, not_230_out, not_231_out, not_232_out, not_233_out, not_234_out, not_235_out, F5, not_236_out, F3, not_237_out, F1, not_238_out);
  and and_37 (and_37_out, not_239_out, not_240_out, not_241_out, not_242_out, not_243_out, not_244_out, F5, not_245_out, F3, not_246_out, F1, F0);
  and and_38 (and_38_out, not_247_out, not_248_out, OP3, not_249_out, OP1, not_250_out);
  and and_39 (and_39_out, not_251_out, not_252_out, OP3, OP2, not_253_out, OP0);
  and and_40 (and_40_out, not_254_out, not_255_out, OP3, not_256_out, OP1, OP0);
  and and_41 (and_41_out, not_257_out, not_258_out, not_259_out, OP2, OP1, OP0);
  or or_1 (S1, and_14_out, and_15_out, and_16_out, and_17_out, and_18_out, and_19_out, and_20_out, and_21_out);
  or or_2 (S3, and_34_out, and_35_out, and_36_out, and_37_out, and_38_out, and_39_out, and_40_out, and_41_out);
  or or_3 (S0, and_1_out, and_2_out, and_3_out, and_4_out, and_5_out, and_6_out, and_7_out, and_8_out, and_9_out, and_10_out, and_11_out, and_12_out, and_13_out);
  or or_4 (S2, and_22_out, and_23_out, and_24_out, and_25_out, and_26_out, and_27_out, and_28_out, and_29_out, and_30_out, and_31_out, and_32_out, and_33_out);
endmodule

// 控制信号生成
module \控制信号生成  (
  input  OP0,
  input  OP1,
  input  OP2,
  input  OP3,
  input  OP4,
  input  OP5,
  input  F0,
  input  F1,
  input  F2,
  input  F3,
  input  F4,
  input  F5,
  output MemToReg,
  output MemWrite,
  output ALU_SRC,
  output RegWrite,
  output SysCALL,
  output SignedExt,
  output RegDst,
  output BEQ,
  output BNE,
  output JR,
  output JMP,
  output JAL
);

  wire and_1_out, and_2_out, and_4_out, and_5_out, and_6_out, and_7_out, and_8_out, and_9_out, and_10_out,
       and_11_out, and_12_out, and_13_out, and_14_out, and_15_out, and_16_out, and_17_out, and_18_out,
       and_19_out, and_20_out, and_21_out, and_22_out, and_23_out, and_24_out, and_25_out, and_26_out,
       and_27_out, and_28_out, and_29_out, and_30_out, and_31_out, and_32_out, and_33_out, and_34_out,
       and_36_out, and_37_out, and_38_out, and_39_out, and_40_out, and_41_out, and_42_out, and_43_out,
       and_44_out, and_45_out, and_46_out, and_47_out, and_48_out, and_49_out, and_50_out, and_51_out,
       and_52_out, and_53_out, and_54_out, and_55_out, and_59_out, and_60_out, and_61_out, not_1_out,
       not_2_out, not_3_out, not_4_out, not_5_out, not_6_out, not_7_out, not_8_out, not_9_out, not_10_out,
       not_11_out, not_12_out, not_13_out, not_14_out, not_15_out, not_16_out, not_17_out, not_18_out,
       not_19_out, not_20_out, not_21_out, not_22_out, not_23_out, not_24_out, not_25_out, not_26_out,
       not_27_out, not_28_out, not_29_out, not_30_out, not_31_out, not_32_out, not_33_out, not_34_out,
       not_35_out, not_36_out, not_37_out, not_38_out, not_39_out, not_40_out, not_41_out, not_42_out,
       not_43_out, not_44_out, not_45_out, not_46_out, not_47_out, not_48_out, not_49_out, not_50_out,
       not_51_out, not_52_out, not_53_out, not_54_out, not_55_out, not_56_out, not_57_out, not_58_out,
       not_59_out, not_60_out, not_61_out, not_62_out, not_63_out, not_64_out, not_65_out, not_66_out,
       not_67_out, not_68_out, not_69_out, not_70_out, not_71_out, not_72_out, not_73_out, not_74_out,
       not_75_out, not_76_out, not_77_out, not_78_out, not_79_out, not_80_out, not_81_out, not_82_out,
       not_83_out, not_84_out, not_85_out, not_86_out, not_87_out, not_88_out, not_89_out, not_90_out,
       not_91_out, not_92_out, not_93_out, not_94_out, not_95_out, not_96_out, not_97_out, not_98_out,
       not_99_out, not_100_out, not_101_out, not_102_out, not_103_out, not_104_out, not_105_out, not_106_out,
       not_107_out, not_108_out, not_109_out, not_110_out, not_111_out, not_112_out, not_113_out,
       not_114_out, not_115_out, not_116_out, not_117_out, not_118_out, not_119_out, not_120_out,
       not_121_out, not_122_out, not_123_out, not_124_out, not_125_out, not_126_out, not_127_out,
       not_128_out, not_129_out, not_130_out, not_131_out, not_132_out, not_133_out, not_134_out,
       not_135_out, not_136_out, not_137_out, not_138_out, not_139_out, not_140_out, not_141_out,
       not_142_out, not_143_out, not_144_out, not_145_out, not_146_out, not_147_out, not_148_out,
       not_149_out, not_150_out, not_151_out, not_152_out, not_153_out, not_154_out, not_155_out,
       not_156_out, not_157_out, not_158_out, not_159_out, not_160_out, not_161_out, not_162_out,
       not_163_out, not_164_out, not_165_out, not_166_out, not_167_out, not_168_out, not_169_out,
       not_170_out, not_171_out, not_172_out, not_173_out, not_174_out, not_175_out, not_176_out,
       not_177_out, not_178_out, not_179_out, not_180_out, not_181_out, not_182_out, not_183_out,
       not_184_out, not_185_out, not_186_out, not_187_out, not_188_out, not_189_out, not_190_out,
       not_191_out, not_192_out, not_193_out, not_194_out, not_195_out, not_196_out, not_197_out,
       not_198_out, not_199_out, not_200_out, not_201_out, not_202_out, not_203_out, not_204_out,
       not_205_out, not_206_out, not_207_out, not_208_out, not_209_out, not_210_out, not_211_out,
       not_212_out, not_213_out, not_214_out, not_215_out, not_216_out, not_217_out, not_218_out,
       not_219_out, not_220_out, not_221_out, not_222_out, not_223_out, not_224_out, not_225_out,
       not_226_out, not_227_out, not_228_out, not_229_out, not_230_out, not_231_out, not_232_out,
       not_233_out, not_234_out, not_235_out, not_236_out, not_237_out, not_238_out, not_239_out,
       not_240_out, not_241_out, not_242_out, not_243_out, not_244_out, not_245_out, not_246_out,
       not_247_out, not_248_out, not_249_out, not_250_out, not_251_out, not_252_out, not_253_out,
       not_254_out, not_255_out, not_256_out, not_257_out, not_258_out, not_259_out, not_260_out,
       not_261_out, not_262_out, not_263_out, not_264_out, not_265_out, not_266_out, not_267_out,
       not_268_out, not_269_out, not_270_out, not_271_out, not_272_out, not_273_out, not_274_out,
       not_275_out, not_276_out, not_277_out, not_278_out, not_279_out, not_280_out, not_281_out,
       not_282_out, not_283_out, not_284_out, not_285_out, not_286_out, not_287_out, not_288_out,
       not_289_out, not_290_out, not_291_out, not_292_out, not_293_out, not_294_out, not_295_out,
       not_296_out, not_297_out, not_298_out, not_299_out, not_300_out, not_301_out, not_302_out,
       not_303_out, not_304_out, not_305_out, not_306_out, not_307_out, not_308_out, not_309_out,
       not_310_out, not_311_out, not_312_out, not_313_out, not_314_out, not_315_out, not_316_out,
       not_317_out, not_318_out, not_319_out, not_320_out, not_321_out, not_322_out, not_323_out,
       not_324_out, not_325_out, not_326_out, not_327_out, not_328_out, not_329_out, not_330_out,
       not_331_out, not_332_out, not_333_out, not_334_out, not_335_out, not_336_out, not_337_out,
       not_338_out, not_339_out, not_340_out, not_341_out, not_342_out, not_343_out, not_344_out,
       not_345_out, not_346_out, not_347_out, not_348_out, not_349_out, not_350_out, not_351_out,
       not_352_out, not_353_out, not_354_out, not_355_out, not_356_out, not_357_out, not_358_out,
       not_359_out, not_360_out, not_361_out, not_362_out, not_363_out, not_364_out, not_365_out,
       not_366_out, not_367_out, not_368_out, not_369_out, not_370_out, not_371_out, not_372_out,
       not_373_out, not_374_out, not_375_out, not_376_out, not_377_out, not_378_out, not_379_out,
       not_380_out, not_381_out, not_382_out, not_383_out;

  not not_1 (not_1_out, OP4);
  not not_2 (not_2_out, OP3);
  not not_3 (not_3_out, OP2);
  not not_4 (not_4_out, OP4);
  not not_5 (not_5_out, OP3);
  not not_6 (not_6_out, OP1);
  not not_7 (not_7_out, OP0);
  not not_8 (not_8_out, OP4);
  not not_9 (not_9_out, OP2);
  not not_10 (not_10_out, OP5);
  not not_11 (not_11_out, OP4);
  not not_12 (not_12_out, OP2);
  not not_13 (not_13_out, OP1);
  not not_14 (not_14_out, OP0);
  not not_15 (not_15_out, OP5);
  not not_16 (not_16_out, OP4);
  not not_17 (not_17_out, OP1);
  not not_18 (not_18_out, OP0);
  not not_19 (not_19_out, OP5);
  not not_20 (not_20_out, OP4);
  not not_21 (not_21_out, OP2);
  not not_22 (not_22_out, OP1);
  not not_23 (not_23_out, OP5);
  not not_24 (not_24_out, OP4);
  not not_25 (not_25_out, OP2);
  not not_26 (not_26_out, OP0);
  not not_27 (not_27_out, OP5);
  not not_28 (not_28_out, OP4);
  not not_29 (not_29_out, OP1);
  not not_30 (not_30_out, OP4);
  not not_31 (not_31_out, OP3);
  not not_32 (not_32_out, OP2);
  not not_33 (not_33_out, OP4);
  not not_34 (not_34_out, OP2);
  not not_35 (not_35_out, OP5);
  not not_36 (not_36_out, OP4);
  not not_37 (not_37_out, OP5);
  not not_38 (not_38_out, OP4);
  not not_39 (not_39_out, OP2);
  not not_40 (not_40_out, OP4);
  not not_41 (not_41_out, OP3);
  not not_42 (not_42_out, OP1);
  not not_43 (not_43_out, OP0);
  not not_44 (not_44_out, OP5);
  not not_45 (not_45_out, OP4);
  not not_46 (not_46_out, OP3);
  not not_47 (not_47_out, OP2);
  not not_48 (not_48_out, OP1);
  not not_49 (not_49_out, OP0);
  not not_50 (not_50_out, F5);
  not not_51 (not_51_out, F4);
  not not_52 (not_52_out, F3);
  not not_53 (not_53_out, F2);
  not not_54 (not_54_out, F1);
  not not_55 (not_55_out, F0);
  not not_56 (not_56_out, OP5);
  not not_57 (not_57_out, OP4);
  not not_58 (not_58_out, OP3);
  not not_59 (not_59_out, OP2);
  not not_60 (not_60_out, OP1);
  not not_61 (not_61_out, OP0);
  not not_62 (not_62_out, F5);
  not not_63 (not_63_out, F4);
  not not_64 (not_64_out, F3);
  not not_65 (not_65_out, F2);
  not not_66 (not_66_out, OP5);
  not not_67 (not_67_out, OP4);
  not not_68 (not_68_out, OP3);
  not not_69 (not_69_out, OP2);
  not not_70 (not_70_out, OP1);
  not not_71 (not_71_out, OP0);
  not not_72 (not_72_out, F5);
  not not_73 (not_73_out, F4);
  not not_74 (not_74_out, F3);
  not not_75 (not_75_out, F2);
  not not_76 (not_76_out, F0);
  not not_77 (not_77_out, OP5);
  not not_78 (not_78_out, OP4);
  not not_79 (not_79_out, OP3);
  not not_80 (not_80_out, OP2);
  not not_81 (not_81_out, OP1);
  not not_82 (not_82_out, OP0);
  not not_83 (not_83_out, F4);
  not not_84 (not_84_out, F3);
  not not_85 (not_85_out, F2);
  not not_86 (not_86_out, F1);
  not not_87 (not_87_out, F0);
  not not_88 (not_88_out, OP5);
  not not_89 (not_89_out, OP4);
  not not_90 (not_90_out, OP3);
  not not_91 (not_91_out, OP2);
  not not_92 (not_92_out, OP1);
  not not_93 (not_93_out, OP0);
  not not_94 (not_94_out, F4);
  not not_95 (not_95_out, F3);
  not not_96 (not_96_out, F2);
  not not_97 (not_97_out, F1);
  not not_98 (not_98_out, OP5);
  not not_99 (not_99_out, OP4);
  not not_100 (not_100_out, OP3);
  not not_101 (not_101_out, OP2);
  not not_102 (not_102_out, OP1);
  not not_103 (not_103_out, OP0);
  not not_104 (not_104_out, F4);
  not not_105 (not_105_out, F3);
  not not_106 (not_106_out, F2);
  not not_107 (not_107_out, F0);
  not not_108 (not_108_out, OP5);
  not not_109 (not_109_out, OP4);
  not not_110 (not_110_out, OP3);
  not not_111 (not_111_out, OP2);
  not not_112 (not_112_out, OP1);
  not not_113 (not_113_out, OP0);
  not not_114 (not_114_out, F4);
  not not_115 (not_115_out, F3);
  not not_116 (not_116_out, F1);
  not not_117 (not_117_out, F0);
  not not_118 (not_118_out, OP5);
  not not_119 (not_119_out, OP4);
  not not_120 (not_120_out, OP3);
  not not_121 (not_121_out, OP2);
  not not_122 (not_122_out, OP1);
  not not_123 (not_123_out, OP0);
  not not_124 (not_124_out, F4);
  not not_125 (not_125_out, F3);
  not not_126 (not_126_out, F1);
  not not_127 (not_127_out, OP5);
  not not_128 (not_128_out, OP4);
  not not_129 (not_129_out, OP3);
  not not_130 (not_130_out, OP2);
  not not_131 (not_131_out, OP1);
  not not_132 (not_132_out, OP0);
  not not_133 (not_133_out, F4);
  not not_134 (not_134_out, F3);
  not not_135 (not_135_out, OP5);
  not not_136 (not_136_out, OP4);
  not not_137 (not_137_out, OP3);
  not not_138 (not_138_out, OP2);
  not not_139 (not_139_out, OP1);
  not not_140 (not_140_out, OP0);
  not not_141 (not_141_out, F4);
  not not_142 (not_142_out, F2);
  not not_143 (not_143_out, F0);
  not not_144 (not_144_out, OP5);
  not not_145 (not_145_out, OP4);
  not not_146 (not_146_out, OP3);
  not not_147 (not_147_out, OP2);
  not not_148 (not_148_out, OP1);
  not not_149 (not_149_out, OP0);
  not not_150 (not_150_out, F4);
  not not_151 (not_151_out, F2);
  not not_152 (not_152_out, OP5);
  not not_153 (not_153_out, OP4);
  not not_154 (not_154_out, OP3);
  not not_155 (not_155_out, OP2);
  not not_156 (not_156_out, OP5);
  not not_157 (not_157_out, OP4);
  not not_158 (not_158_out, OP2);
  not not_159 (not_159_out, OP1);
  not not_160 (not_160_out, OP0);
  not not_161 (not_161_out, OP5);
  not not_162 (not_162_out, OP4);
  not not_163 (not_163_out, OP1);
  not not_164 (not_164_out, OP0);
  not not_165 (not_165_out, OP5);
  not not_166 (not_166_out, OP4);
  not not_167 (not_167_out, OP2);
  not not_168 (not_168_out, OP1);
  not not_169 (not_169_out, OP5);
  not not_170 (not_170_out, OP4);
  not not_171 (not_171_out, OP2);
  not not_172 (not_172_out, OP0);
  not not_173 (not_173_out, OP5);
  not not_174 (not_174_out, OP4);
  not not_175 (not_175_out, OP1);
  not not_176 (not_176_out, OP4);
  not not_177 (not_177_out, OP3);
  not not_178 (not_178_out, OP2);
  not not_179 (not_179_out, OP5);
  not not_180 (not_180_out, OP4);
  not not_181 (not_181_out, OP5);
  not not_182 (not_182_out, OP4);
  not not_183 (not_183_out, OP2);
  not not_184 (not_184_out, OP4);
  not not_185 (not_185_out, OP3);
  not not_186 (not_186_out, OP1);
  not not_187 (not_187_out, OP0);
  not not_188 (not_188_out, OP5);
  not not_189 (not_189_out, OP4);
  not not_190 (not_190_out, OP3);
  not not_191 (not_191_out, OP2);
  not not_192 (not_192_out, OP1);
  not not_193 (not_193_out, OP0);
  not not_194 (not_194_out, F5);
  not not_195 (not_195_out, F4);
  not not_196 (not_196_out, F1);
  not not_197 (not_197_out, F0);
  not not_198 (not_198_out, OP5);
  not not_199 (not_199_out, OP4);
  not not_200 (not_200_out, OP3);
  not not_201 (not_201_out, OP1);
  not not_202 (not_202_out, OP0);
  not not_203 (not_203_out, OP5);
  not not_204 (not_204_out, OP4);
  not not_205 (not_205_out, OP3);
  not not_206 (not_206_out, OP1);
  not not_207 (not_207_out, OP5);
  not not_208 (not_208_out, OP4);
  not not_209 (not_209_out, OP2);
  not not_210 (not_210_out, OP1);
  not not_211 (not_211_out, OP0);
  not not_212 (not_212_out, OP5);
  not not_213 (not_213_out, OP4);
  not not_214 (not_214_out, OP2);
  not not_215 (not_215_out, OP1);
  not not_216 (not_216_out, OP5);
  not not_217 (not_217_out, OP4);
  not not_218 (not_218_out, OP2);
  not not_219 (not_219_out, OP0);
  not not_220 (not_220_out, OP4);
  not not_221 (not_221_out, OP3);
  not not_222 (not_222_out, OP2);
  not not_223 (not_223_out, OP4);
  not not_224 (not_224_out, OP2);
  not not_225 (not_225_out, OP5);
  not not_226 (not_226_out, OP4);
  not not_227 (not_227_out, OP2);
  not not_228 (not_228_out, OP4);
  not not_229 (not_229_out, OP3);
  not not_230 (not_230_out, OP1);
  not not_231 (not_231_out, OP0);
  not not_232 (not_232_out, OP5);
  not not_233 (not_233_out, OP4);
  not not_234 (not_234_out, OP3);
  not not_235 (not_235_out, OP2);
  not not_236 (not_236_out, OP1);
  not not_237 (not_237_out, OP0);
  not not_238 (not_238_out, F5);
  not not_239 (not_239_out, F4);
  not not_240 (not_240_out, F3);
  not not_241 (not_241_out, F2);
  not not_242 (not_242_out, F1);
  not not_243 (not_243_out, F0);
  not not_244 (not_244_out, OP5);
  not not_245 (not_245_out, OP4);
  not not_246 (not_246_out, OP3);
  not not_247 (not_247_out, OP2);
  not not_248 (not_248_out, OP1);
  not not_249 (not_249_out, OP0);
  not not_250 (not_250_out, F5);
  not not_251 (not_251_out, F4);
  not not_252 (not_252_out, F3);
  not not_253 (not_253_out, F2);
  not not_254 (not_254_out, OP5);
  not not_255 (not_255_out, OP4);
  not not_256 (not_256_out, OP3);
  not not_257 (not_257_out, OP2);
  not not_258 (not_258_out, OP1);
  not not_259 (not_259_out, OP0);
  not not_260 (not_260_out, F5);
  not not_261 (not_261_out, F4);
  not not_262 (not_262_out, F3);
  not not_263 (not_263_out, F2);
  not not_264 (not_264_out, F0);
  not not_265 (not_265_out, OP5);
  not not_266 (not_266_out, OP4);
  not not_267 (not_267_out, OP3);
  not not_268 (not_268_out, OP2);
  not not_269 (not_269_out, OP1);
  not not_270 (not_270_out, OP0);
  not not_271 (not_271_out, F4);
  not not_272 (not_272_out, F3);
  not not_273 (not_273_out, F2);
  not not_274 (not_274_out, F1);
  not not_275 (not_275_out, F0);
  not not_276 (not_276_out, OP5);
  not not_277 (not_277_out, OP4);
  not not_278 (not_278_out, OP3);
  not not_279 (not_279_out, OP2);
  not not_280 (not_280_out, OP1);
  not not_281 (not_281_out, OP0);
  not not_282 (not_282_out, F4);
  not not_283 (not_283_out, F3);
  not not_284 (not_284_out, F2);
  not not_285 (not_285_out, F1);
  not not_286 (not_286_out, OP5);
  not not_287 (not_287_out, OP4);
  not not_288 (not_288_out, OP3);
  not not_289 (not_289_out, OP2);
  not not_290 (not_290_out, OP1);
  not not_291 (not_291_out, OP0);
  not not_292 (not_292_out, F4);
  not not_293 (not_293_out, F3);
  not not_294 (not_294_out, F2);
  not not_295 (not_295_out, F0);
  not not_296 (not_296_out, OP5);
  not not_297 (not_297_out, OP4);
  not not_298 (not_298_out, OP3);
  not not_299 (not_299_out, OP2);
  not not_300 (not_300_out, OP1);
  not not_301 (not_301_out, OP0);
  not not_302 (not_302_out, F4);
  not not_303 (not_303_out, F3);
  not not_304 (not_304_out, F1);
  not not_305 (not_305_out, F0);
  not not_306 (not_306_out, OP5);
  not not_307 (not_307_out, OP4);
  not not_308 (not_308_out, OP3);
  not not_309 (not_309_out, OP2);
  not not_310 (not_310_out, OP1);
  not not_311 (not_311_out, OP0);
  not not_312 (not_312_out, F4);
  not not_313 (not_313_out, F3);
  not not_314 (not_314_out, F1);
  not not_315 (not_315_out, OP5);
  not not_316 (not_316_out, OP4);
  not not_317 (not_317_out, OP3);
  not not_318 (not_318_out, OP2);
  not not_319 (not_319_out, OP1);
  not not_320 (not_320_out, OP0);
  not not_321 (not_321_out, F4);
  not not_322 (not_322_out, F3);
  not not_323 (not_323_out, OP5);
  not not_324 (not_324_out, OP4);
  not not_325 (not_325_out, OP3);
  not not_326 (not_326_out, OP2);
  not not_327 (not_327_out, OP1);
  not not_328 (not_328_out, OP0);
  not not_329 (not_329_out, F4);
  not not_330 (not_330_out, F2);
  not not_331 (not_331_out, F0);
  not not_332 (not_332_out, OP5);
  not not_333 (not_333_out, OP4);
  not not_334 (not_334_out, OP3);
  not not_335 (not_335_out, OP2);
  not not_336 (not_336_out, OP1);
  not not_337 (not_337_out, OP0);
  not not_338 (not_338_out, F4);
  not not_339 (not_339_out, F2);
  not not_340 (not_340_out, OP5);
  not not_341 (not_341_out, OP4);
  not not_342 (not_342_out, OP3);
  not not_343 (not_343_out, OP1);
  not not_344 (not_344_out, OP0);
  not not_345 (not_345_out, OP5);
  not not_346 (not_346_out, OP4);
  not not_347 (not_347_out, OP3);
  not not_348 (not_348_out, OP1);
  not not_349 (not_349_out, OP5);
  not not_350 (not_350_out, OP4);
  not not_351 (not_351_out, OP3);
  not not_352 (not_352_out, OP2);
  not not_353 (not_353_out, OP1);
  not not_354 (not_354_out, OP0);
  not not_355 (not_355_out, F5);
  not not_356 (not_356_out, F4);
  not not_357 (not_357_out, F2);
  not not_358 (not_358_out, F1);
  not not_359 (not_359_out, F0);
  not not_360 (not_360_out, OP5);
  not not_361 (not_361_out, OP4);
  not not_362 (not_362_out, OP3);
  not not_363 (not_363_out, OP2);
  not not_364 (not_364_out, OP1);
  not not_365 (not_365_out, OP0);
  not not_366 (not_366_out, F5);
  not not_367 (not_367_out, F4);
  not not_368 (not_368_out, F2);
  not not_369 (not_369_out, F1);
  not not_370 (not_370_out, F0);
  not not_371 (not_371_out, OP5);
  not not_372 (not_372_out, OP4);
  not not_373 (not_373_out, OP3);
  not not_374 (not_374_out, OP2);
  not not_375 (not_375_out, OP0);
  not not_376 (not_376_out, OP5);
  not not_377 (not_377_out, OP4);
  not not_378 (not_378_out, OP3);
  not not_379 (not_379_out, OP2);
  not not_380 (not_380_out, OP5);
  not not_381 (not_381_out, OP4);
  not not_382 (not_382_out, OP3);
  not not_383 (not_383_out, OP2);
  and and_1 (and_1_out, OP5, not_1_out, not_2_out, not_3_out, OP1, OP0);
  and and_2 (and_2_out, OP5, not_4_out, not_5_out, OP2, not_6_out, not_7_out);
  and and_3 (MemWrite, OP5, not_8_out, OP3, not_9_out, OP1, OP0);
  and and_4 (and_4_out, not_10_out, not_11_out, OP3, not_12_out, not_13_out, not_14_out);
  and and_5 (and_5_out, not_15_out, not_16_out, OP3, OP2, not_17_out, not_18_out);
  and and_6 (and_6_out, not_19_out, not_20_out, OP3, not_21_out, not_22_out, OP0);
  and and_7 (and_7_out, not_23_out, not_24_out, OP3, not_25_out, OP1, not_26_out);
  and and_8 (and_8_out, not_27_out, not_28_out, OP3, OP2, not_29_out, OP0);
  and and_9 (and_9_out, OP5, not_30_out, not_31_out, not_32_out, OP1, OP0);
  and and_10 (and_10_out, OP5, not_33_out, OP3, not_34_out, OP1, OP0);
  and and_11 (and_11_out, not_35_out, not_36_out, OP3, OP2, OP1, OP0);
  and and_12 (and_12_out, not_37_out, not_38_out, OP3, not_39_out, OP1, OP0);
  and and_13 (and_13_out, OP5, not_40_out, not_41_out, OP2, not_42_out, not_43_out);
  and and_14 (and_14_out, not_44_out, not_45_out, not_46_out, not_47_out, not_48_out, not_49_out, not_50_out, not_51_out, not_52_out, not_53_out, not_54_out, not_55_out);
  and and_15 (and_15_out, not_56_out, not_57_out, not_58_out, not_59_out, not_60_out, not_61_out, not_62_out, not_63_out, not_64_out, not_65_out, F1, F0);
  and and_16 (and_16_out, not_66_out, not_67_out, not_68_out, not_69_out, not_70_out, not_71_out, not_72_out, not_73_out, not_74_out, not_75_out, F1, not_76_out);
  and and_17 (and_17_out, not_77_out, not_78_out, not_79_out, not_80_out, not_81_out, not_82_out, F5, not_83_out, not_84_out, not_85_out, not_86_out, not_87_out);
  and and_18 (and_18_out, not_88_out, not_89_out, not_90_out, not_91_out, not_92_out, not_93_out, F5, not_94_out, not_95_out, not_96_out, not_97_out, F0);
  and and_19 (and_19_out, not_98_out, not_99_out, not_100_out, not_101_out, not_102_out, not_103_out, F5, not_104_out, not_105_out, not_106_out, F1, not_107_out);
  and and_20 (and_20_out, not_108_out, not_109_out, not_110_out, not_111_out, not_112_out, not_113_out, F5, not_114_out, not_115_out, F2, not_116_out, not_117_out);
  and and_21 (and_21_out, not_118_out, not_119_out, not_120_out, not_121_out, not_122_out, not_123_out, F5, not_124_out, not_125_out, F2, not_126_out, F0);
  and and_22 (and_22_out, not_127_out, not_128_out, not_129_out, not_130_out, not_131_out, not_132_out, F5, not_133_out, not_134_out, F2, F1, F0);
  and and_23 (and_23_out, not_135_out, not_136_out, not_137_out, not_138_out, not_139_out, not_140_out, F5, not_141_out, F3, not_142_out, F1, not_143_out);
  and and_24 (and_24_out, not_144_out, not_145_out, not_146_out, not_147_out, not_148_out, not_149_out, F5, not_150_out, F3, not_151_out, F1, F0);
  and and_25 (and_25_out, not_152_out, not_153_out, not_154_out, not_155_out, OP1, OP0);
  and and_26 (and_26_out, not_156_out, not_157_out, OP3, not_158_out, not_159_out, not_160_out);
  and and_27 (and_27_out, not_161_out, not_162_out, OP3, OP2, not_163_out, not_164_out);
  and and_28 (and_28_out, not_165_out, not_166_out, OP3, not_167_out, not_168_out, OP0);
  and and_29 (and_29_out, not_169_out, not_170_out, OP3, not_171_out, OP1, not_172_out);
  and and_30 (and_30_out, not_173_out, not_174_out, OP3, OP2, not_175_out, OP0);
  and and_31 (and_31_out, OP5, not_176_out, not_177_out, not_178_out, OP1, OP0);
  and and_32 (and_32_out, not_179_out, not_180_out, OP3, OP2, OP1, OP0);
  and and_33 (and_33_out, not_181_out, not_182_out, OP3, not_183_out, OP1, OP0);
  and and_34 (and_34_out, OP5, not_184_out, not_185_out, OP2, not_186_out, not_187_out);
  and and_35 (SysCALL, not_188_out, not_189_out, not_190_out, not_191_out, not_192_out, not_193_out, not_194_out, not_195_out, F3, F2, not_196_out, not_197_out);
  and and_36 (and_36_out, not_198_out, not_199_out, not_200_out, OP2, not_201_out, not_202_out);
  and and_37 (and_37_out, not_203_out, not_204_out, not_205_out, OP2, not_206_out, OP0);
  and and_38 (and_38_out, not_207_out, not_208_out, OP3, not_209_out, not_210_out, not_211_out);
  and and_39 (and_39_out, not_212_out, not_213_out, OP3, not_214_out, not_215_out, OP0);
  and and_40 (and_40_out, not_216_out, not_217_out, OP3, not_218_out, OP1, not_219_out);
  and and_41 (and_41_out, OP5, not_220_out, not_221_out, not_222_out, OP1, OP0);
  and and_42 (and_42_out, OP5, not_223_out, OP3, not_224_out, OP1, OP0);
  and and_43 (and_43_out, not_225_out, not_226_out, OP3, not_227_out, OP1, OP0);
  and and_44 (and_44_out, OP5, not_228_out, not_229_out, OP2, not_230_out, not_231_out);
  and and_45 (and_45_out, not_232_out, not_233_out, not_234_out, not_235_out, not_236_out, not_237_out, not_238_out, not_239_out, not_240_out, not_241_out, not_242_out, not_243_out);
  and and_46 (and_46_out, not_244_out, not_245_out, not_246_out, not_247_out, not_248_out, not_249_out, not_250_out, not_251_out, not_252_out, not_253_out, F1, F0);
  and and_47 (and_47_out, not_254_out, not_255_out, not_256_out, not_257_out, not_258_out, not_259_out, not_260_out, not_261_out, not_262_out, not_263_out, F1, not_264_out);
  and and_48 (and_48_out, not_265_out, not_266_out, not_267_out, not_268_out, not_269_out, not_270_out, F5, not_271_out, not_272_out, not_273_out, not_274_out, not_275_out);
  and and_49 (and_49_out, not_276_out, not_277_out, not_278_out, not_279_out, not_280_out, not_281_out, F5, not_282_out, not_283_out, not_284_out, not_285_out, F0);
  and and_50 (and_50_out, not_286_out, not_287_out, not_288_out, not_289_out, not_290_out, not_291_out, F5, not_292_out, not_293_out, not_294_out, F1, not_295_out);
  and and_51 (and_51_out, not_296_out, not_297_out, not_298_out, not_299_out, not_300_out, not_301_out, F5, not_302_out, not_303_out, F2, not_304_out, not_305_out);
  and and_52 (and_52_out, not_306_out, not_307_out, not_308_out, not_309_out, not_310_out, not_311_out, F5, not_312_out, not_313_out, F2, not_314_out, F0);
  and and_53 (and_53_out, not_315_out, not_316_out, not_317_out, not_318_out, not_319_out, not_320_out, F5, not_321_out, not_322_out, F2, F1, F0);
  and and_54 (and_54_out, not_323_out, not_324_out, not_325_out, not_326_out, not_327_out, not_328_out, F5, not_329_out, F3, not_330_out, F1, not_331_out);
  and and_55 (and_55_out, not_332_out, not_333_out, not_334_out, not_335_out, not_336_out, not_337_out, F5, not_338_out, F3, not_339_out, F1, F0);
  and and_56 (BEQ, not_340_out, not_341_out, not_342_out, OP2, not_343_out, not_344_out);
  and and_57 (BNE, not_345_out, not_346_out, not_347_out, OP2, not_348_out, OP0);
  and and_58 (JR, not_349_out, not_350_out, not_351_out, not_352_out, not_353_out, not_354_out, not_355_out, not_356_out, F3, not_357_out, not_358_out, not_359_out);
  and and_59 (and_59_out, not_360_out, not_361_out, not_362_out, not_363_out, not_364_out, not_365_out, not_366_out, not_367_out, F3, not_368_out, not_369_out, not_370_out);
  and and_60 (and_60_out, not_371_out, not_372_out, not_373_out, not_374_out, OP1, not_375_out);
  and and_61 (and_61_out, not_376_out, not_377_out, not_378_out, not_379_out, OP1, OP0);
  and and_62 (JAL, not_380_out, not_381_out, not_382_out, not_383_out, OP1, OP0);
  or or_1 (MemToReg, and_1_out, and_2_out);
  or or_2 (ALU_SRC, and_4_out, and_5_out, and_6_out, and_7_out, and_8_out, and_9_out, and_10_out, and_11_out, and_12_out, and_13_out);
  or or_3 (SignedExt, and_36_out, and_37_out, and_38_out, and_39_out, and_40_out, and_41_out, and_42_out, and_43_out, and_44_out);
  or or_4 (RegDst, and_45_out, and_46_out, and_47_out, and_48_out, and_49_out, and_50_out, and_51_out, and_52_out, and_53_out, and_54_out, and_55_out);
  or or_5 (JMP, and_59_out, and_60_out, and_61_out);
  or or_6 (RegWrite, and_14_out, and_15_out, and_16_out, and_17_out, and_18_out, and_19_out, and_20_out, and_21_out, and_22_out, and_23_out, and_24_out, and_25_out, and_26_out, and_27_out, and_28_out, and_29_out, and_30_out, and_31_out, and_32_out, and_33_out, and_34_out);
endmodule

module \扩展信号生成  (
  input  OP0,
  input  OP1,
  input  OP2,
  input  OP3,
  input  OP4,
  input  OP5,
  input  F0,
  input  F1,
  input  F2,
  input  F3,
  input  F4,
  input  F5,
  output LUISrc,
  output bgtz,
  output LBU
);

  wire not_1_out, not_2_out, not_3_out, not_4_out, not_5_out, not_6_out, not_7_out, not_8_out, not_9_out;

  not not_1 (not_1_out, OP5);
  not not_2 (not_2_out, OP4);
  not not_3 (not_3_out, OP5);
  not not_4 (not_4_out, OP4);
  not not_5 (not_5_out, OP3);
  not not_6 (not_6_out, OP4);
  not not_7 (not_7_out, OP3);
  not not_8 (not_8_out, OP1);
  not not_9 (not_9_out, OP0);
  and and_1 (LUISrc, not_1_out, not_2_out, OP3, OP2, OP1, OP0);
  and and_2 (bgtz, not_3_out, not_4_out, not_5_out, OP2, OP1, OP0);
  and and_3 (LBU, OP5, not_6_out, not_7_out, OP2, not_8_out, not_9_out);
endmodule

// ALU
module MIPS_ALU (
  input  [4:0] shamt,
  input  [31:0] X,
  input  [31:0] Y,
  input  [3:0] AluOP,
  output Equal,
  output [31:0] Result,
  output [31:0] Result_2
);

  wire [0:0] comparator_1_lt, comparator_2_lt;
  wire [31:0] adder_1_out, AND_out, divider_1_out, divider_1_rem, multiplier_1_cout, multiplier_1_out,
       NOR_out, OR_out, shifter_1_out, shifter_2_out, shifter_3_out, subtractor_1_out, XOR_out;

  assign AND_out = X & Y;  // AND_Gate AND, 32 bits wide
  assign OR_out = X | Y;  // OR_Gate OR, 32 bits wide
  Shifter #(.width(32)) shifter_1 (.in(Y), .\dist (shamt), .out(shifter_1_out));
  Shifter #(.width(32), .shift("ar")) shifter_2 (.in(Y), .\dist (shamt), .out(shifter_2_out));
  Shifter #(.width(32), .shift("lr")) shifter_3 (.in(Y), .\dist (shamt), .out(shifter_3_out));
  Multiplier #(.width(32)) multiplier_1 (.a(X), .b(Y), .out(multiplier_1_out), .cout(multiplier_1_cout));  // open: cin
  Divider #(.width(32)) divider_1 (.a(X), .b(Y), .out(divider_1_out), .rem(divider_1_rem));  // open: upper
  Adder #(.width(32)) adder_1 (.a(X), .b(Y), .out(adder_1_out));  // open: cin, cout
  Subtractor #(.width(32)) subtractor_1 (.a(X), .b(Y), .out(subtractor_1_out));  // open: bin, bout
  assign XOR_out = X ^ Y;  // XOR_Gate XOR, 32 bits wide
  assign NOR_out = ~(X | Y);  // NOR_Gate NOR, 32 bits wide
  Comparator #(.width(32)) comparator_1 (.a(X), .b(Y), .eq(Equal), .lt(comparator_1_lt[0]));  // open: gt
  Comparator #(.width(32), .mode("unsigned")) comparator_2 (.a(X), .b(Y), .lt(comparator_2_lt[0]));  // open: gt, eq
  Multiplexer #(.select(4), .width(32), .enable("false")) multiplexer_1 (
    .in0(shifter_1_out), .in1(shifter_2_out), .in2(shifter_3_out), .in3(multiplier_1_out),
    .in4(divider_1_out), .in5(adder_1_out), .in6(subtractor_1_out), .in7(AND_out), .in8(OR_out),
    .in9(XOR_out), .in10(NOR_out), .in11({{31{1'b0}}, comparator_1_lt[0]}),
    .in12({{31{1'b0}}, comparator_2_lt[0]}), .in13({32{1'b0}}), .in14({32{1'b0}}), .in15({32{1'b0}}),
    .out(Result), .sel(AluOP));
  Multiplexer #(.select(4), .width(32), .enable("false")) multiplexer_2 (
    .in0({32{1'b0}}), .in1({32{1'b0}}), .in2({32{1'b0}}), .in3(multiplier_1_cout), .in4(divider_1_rem),
    .in5({32{1'b0}}), .in6({32{1'b0}}), .in7({32{1'b0}}), .in8({32{1'b0}}), .in9({32{1'b0}}),
    .in10({32{1'b0}}), .in11({32{1'b0}}), .in12({32{1'b0}}), .in13({32{1'b0}}), .in14({32{1'b0}}),
    .in15({32{1'b0}}), .out(Result_2), .sel(AluOP));

  // Other names for the same wires on the sheet: Result2[31:0] = Result_2; S[3:0] = AluOP

  // Notes on the sheet:
  //   不要改变此引脚区域内容，也不要改变ALU封装形式
  //   输入引脚
  //   输出引脚
endmodule

module MIPS_Regifile (
  input  [31:0] Din,
  input  Clk,
  input  WE,
  input  [4:0] R1_num,
  input  [4:0] W_num,
  input  [4:0] R2_num,
  output [31:0] R1,
  output [31:0] R2
);

  // RegisterFile registerfile_1: pin names not known; wires that end beside it: Din, Clk, WE, W_num, R1_num, R2_num, R1, R2
endmodule

// ID/EX
module \理想流水线  (
);

  wire Beq, Bgzt, bgzt_t, Bne, CLK, display, EX_MEM_jal_2, EX_MEM_syscall_2, Go, halt, ID_EX_syscall_2, IR1,
       IR2, IR3, JAL_EX, JAL_WB, JMP, JR, LBU, LUISrc, Mem2reg, Memwrite, mips_alu_1_equal, nor_1_out,
       not_1_out, not_2_out, RegDst, Regwrite, RST, run, show, SignedExt, syscall, W1, W2, W3, \条件分支 ,
       \硬布线控制器_1_alu_src , \硬布线控制器_1_jal , \硬布线控制器_1_memtoreg , \硬布线控制器_1_memwrite , \硬布线控制器_1_regdst ,
       \硬布线控制器_1_regwrite , \硬布线控制器_1_syscall ;
  wire [1:0] ID_EX_mem, \硬布线控制器_1_beq , \硬布线控制器_1_jmp ;
  wire [2:0] ID_EX_wb, WB_MEM;
  wire [3:0] ALUOP_EX, \硬布线控制器_1_alu_op ;
  wire [4:0] ID_EX_shamt_out, multiplexer_4_out, multiplexer_5_out, multiplexer_8_out, multiplexer_13_out, WR;
  wire [7:0] multiplexer_9_out;
  wire [15:0] \LoadUse次数 , \总周期数 , \插入气泡数 , \无条件分支数 , \条件分支成功数 ;
  wire [31:0] adder_2_out, ALUres_EX, ALUres_MEM, Din, EX_MEM_r2_out, EX_PC, ID_EX_alub_out, ID_PC, IF_PC,
       INS_EX, INS_ID, INS_IF, INS_MEM, INS_WB, LedData, MEM_PC, mem_wb_1_alurs_out, mem_wb_1_memd_out,
       MEMD_MEM, multiplexer_1_out, multiplexer_2_out, multiplexer_3_out, multiplexer_6_out,
       multiplexer_7_out, multiplexer_10_out, multiplexer_11_out, R1, R1_EX, R1_ID, R2, R2_EX, R2_ID, WB_PC,
       \原PC , \左移2位有符号拓展Imm , \无符号拓展Imm , \有符号拓展Imm ;

  Button \u_总复位  (.out(RST));
  Button _1 (.out(IR1));
  Button _2 (.out(IR2));
  Button _3 (.out(IR3));
  Button \u_继续运行  (.out(Go));
  LED led_1 (.in(W1));
  LED led_2 (.in(W2));
  LED led_3 (.in(W3));
  Multiplexer #(.width(32), .enable("false")) multiplexer_1 (
    .in0(IF_PC), .in1(adder_2_out), .out(multiplexer_1_out), .sel(\条件分支 ));
  Hex_Digit_Display hex_digit_display_1 (.value(LedData[31:28]));  // open: dp
  Multiplexer #(.width(32), .enable("false")) multiplexer_2 (
    .in0({EX_PC[31:28], EX_PC[25:0], 2'b00}), .in1(R1_EX), .out(multiplexer_2_out), .sel(JR));
  Hex_Digit_Display hex_digit_display_2 (.value(LedData[27:24]));  // open: dp
  Hex_Digit_Display hex_digit_display_3 (.value(LedData[23:20]));  // open: dp
  or or_1 (run, Go, not_1_out);
  Multiplexer #(.width(32), .enable("false")) multiplexer_3 (
    .in0(multiplexer_1_out), .in1(multiplexer_2_out), .out(multiplexer_3_out), .sel(JMP));
  Hex_Digit_Display hex_digit_display_4 (.value(LedData[19:16]));  // open: dp
  Hex_Digit_Display hex_digit_display_5 (.value(LedData[15:12]));  // open: dp
  not not_1 (not_1_out, halt);
  Register #(.width(32)) PC (.D(multiplexer_3_out), .en(run), .Q(\原PC ), .clk(CLK), .clr(RST));
  Hex_Digit_Display hex_digit_display_6 (.value(LedData[7:4]));  // open: dp
  Hex_Digit_Display hex_digit_display_7 (.value(LedData[11:8]));  // open: dp
  Clock clock_1 (.out(CLK));
  Adder #(.width(32)) adder_1 (.a(\原PC ), .b(32'h4), .out(IF_PC));  // open: cin, cout
  // Probe on adder_2_out
  Adder #(.width(32)) adder_2 (.a(IF_PC), .b(\左移2位有符号拓展Imm ), .out(adder_2_out));  // open: cin, cout
  Hex_Digit_Display hex_digit_display_8 (.value(LedData[3:0]));  // open: dp
  ROM #(.addrWidth(10), .dataWidth(32)) rom_1 (.addr(\原PC [11:2]), .data(INS_IF));  // open: sel
  // Probe on INS_IF
  // Probe on INS_ID
  // Probe on INS_EX
  // Probe on INS_MEM
  // Probe on INS_WB
  // Probe on \总周期数 
  // Probe on \无条件分支数 
  // Probe on \条件分支成功数 
  // Probe on \插入气泡数 
  // Probe on \LoadUse次数 
  // Probe on IF_PC[11:0]
  IF_ID IF_ID (
    .Bubble(1'b0), .Enable(run), .CLK(CLK), .CLR(RST), .PC_IN(IF_PC), .PC_OUT(ID_PC), .IR_IN(INS_IF),
    .IR_OUT(INS_ID));
  // Probe on ID_PC[11:0]
  // Probe on EX_PC[11:0]
  // Probe on MEM_PC[11:0]
  // Probe on WB_PC[11:0]
  Multiplexer #(.width(5), .enable("false")) multiplexer_4 (
    .in0(INS_ID[25:21]), .in1(5'b00100), .out(multiplexer_4_out), .sel(\硬布线控制器_1_syscall ));
  Multiplexer #(.width(5), .enable("false")) multiplexer_5 (
    .in0(INS_ID[20:16]), .in1(5'b00010), .out(multiplexer_5_out), .sel(\硬布线控制器_1_syscall ));
  assign \无符号拓展Imm  = {{16{1'b0}}, INS_ID[15:0]};  // Bit_Extender bit_extender_1
  assign \有符号拓展Imm  = {{16{INS_ID[15]}}, INS_ID[15:0]};  // Bit_Extender bit_extender_2
  // Probe on \有符号拓展Imm 
  \硬布线控制器  \u_硬布线控制器_1  (
    .Func(INS_ID[5:0]), .OP(INS_ID[31:26]), .ALU_OP(\硬布线控制器_1_alu_op ), .MemToReg(\硬布线控制器_1_memtoreg ),
    .MemWrite(\硬布线控制器_1_memwrite ), .ALU_SRC(\硬布线控制器_1_alu_src ), .RegWrite(\硬布线控制器_1_regwrite ),
    .SysCALL(\硬布线控制器_1_syscall ), .SignedExt(SignedExt), .RegDst(\硬布线控制器_1_regdst ), .JR(\硬布线控制器_1_jmp [1]),
    .JMP(\硬布线控制器_1_jmp [0]), .Beq(\硬布线控制器_1_beq [0]), .JAL(\硬布线控制器_1_jal ), .Bne(\硬布线控制器_1_beq [1]),
    .LUISrc(LUISrc), .bgtz(bgzt_t), .LBU(LBU));
  MIPS_Regifile mips_regifile_1 (
    .Din(Din), .Clk(CLK), .R1(R1_ID), .R2(R2_ID), .WE(Regwrite), .W_num(WR), .R1_num(multiplexer_4_out),
    .R2_num(multiplexer_5_out));
  // Probe on R1_ID
  // Probe on R2_ID
  Multiplexer #(.width(32), .enable("false")) multiplexer_6 (
    .in0(\无符号拓展Imm ), .in1(\有符号拓展Imm ), .out(multiplexer_6_out), .sel(SignedExt));
  Pull_Resistor pull_resistor_1 (.node(display));
  Comparator #(.width(32)) comparator_1 (.a(R2), .b(32'h22), .eq(display));  // open: gt, lt
  Multiplexer #(.width(32), .enable("false")) multiplexer_7 (
    .in0(R2_ID), .in1(multiplexer_6_out), .out(multiplexer_7_out), .sel(\硬布线控制器_1_alu_src ));
  Multiplexer #(.width(5), .enable("false")) multiplexer_8 (
    .in0(INS_ID[10:6]), .in1(5'b10000), .out(multiplexer_8_out), .sel(LUISrc));
  and and_1 (show, syscall, display);
  ID_EX ID_EX (
    .PC_IN(ID_PC), .IR_IN(INS_ID), .R1_IN(R1_ID), .ALUB_IN(multiplexer_7_out), .PC_OUT(EX_PC),
    .IR_OUT(INS_EX), .R1_OUT(R1_EX), .ALUB_OUT(ID_EX_alub_out), .Bubble(1'b0), .Enable(run), .CLK(CLK),
    .CLR(RST), .RegWrite(\硬布线控制器_1_regwrite ), .RegDst(\硬布线控制器_1_regdst ), .MemToReg(\硬布线控制器_1_memtoreg ),
    .MemWrite(\硬布线控制器_1_memwrite ), .Beq(\硬布线控制器_1_beq [0]), .Bne(\硬布线控制器_1_beq [1]), .JR(\硬布线控制器_1_jmp [1]),
    .JMP(\硬布线控制器_1_jmp [0]), .JAL(\硬布线控制器_1_jal ), .SysCALL(\硬布线控制器_1_syscall ), .MEM(ID_EX_mem),
    .SysCALL_2(ID_EX_syscall_2), .WB(ID_EX_wb), .BRANCH_OUT({Bne, Beq, Bgzt}), .JMP_OUT({JAL_EX, JMP, JR}),
    .ALUOP_OUT(ALUOP_EX), .Shamt_IN(multiplexer_8_out), .Shamt_OUT(ID_EX_shamt_out), .Bgzt(bgzt_t),
    .LBU(LBU), .R2_IN(R2_ID), .R2_OUT(R2_EX), .ALUOP_IN(\硬布线控制器_1_alu_op ));  // open: WR_IN, WR_OUT, Forward_IN, Forward_OUT, ALUSrcB, ALUSrcB_2, Imm, Imm_2
  not not_2 (not_2_out, display);
  Register #(.width(32)) register_1 (.D(R1), .en(show), .Q(LedData), .clk(CLK), .clr(RST));
  Pull_Resistor pull_resistor_2 (.node(\条件分支 ));
  assign \条件分支  = Beq ? mips_alu_1_equal : 1'bz;  // Controlled_Buffer controlled_buffer_1
  assign \条件分支  = Bne ? ~mips_alu_1_equal : 1'bz;  // Controlled_Inverter controlled_inverter_1
  // Probe on ALUOP_EX
  // Probe on ALUres_EX
  // Probe on R1_EX
  // Probe on R2_EX
  and and_2 (halt, syscall, not_2_out);
  nor nor_1 (nor_1_out, ALUres_EX[0], mips_alu_1_equal);
  assign \条件分支  = Bgzt ? nor_1_out : 1'bz;  // Controlled_Buffer controlled_buffer_2
  MIPS_ALU mips_alu_1 (
    .X(R1_EX), .Y(ID_EX_alub_out), .AluOP(ALUOP_EX), .Equal(mips_alu_1_equal), .Result(ALUres_EX),
    .shamt(ID_EX_shamt_out));  // open: Result_2
  EX_MEM EX_MEM (
    .PC_IN(EX_PC), .IR_IN(INS_EX), .R2_IN(R2_EX), .PC_OUT(MEM_PC), .IR_OUT(INS_MEM), .R2_OUT(EX_MEM_r2_out),
    .Bubble(1'b0), .Enable(run), .CLK(CLK), .CLR(RST), .ALURS_IN(ALUres_EX), .ALURS_OUT(ALUres_MEM),
    .WB_2(WB_MEM), .MEM_2({LBU, Memwrite}), .SysCALL_2(EX_MEM_syscall_2), .WB(ID_EX_wb), .MEM(ID_EX_mem),
    .SysCALL(ID_EX_syscall_2), .JAL(JAL_EX), .JAL_2(EX_MEM_jal_2));  // open: HALT, HALT_2, WR_IN, WR_OUT
  assign \左移2位有符号拓展Imm  = {{14{INS_EX[15]}}, {INS_EX[15:0], 2'b00}};  // Bit_Extender bit_extender_3
  Counter #(.width(16), .max('hffff)) counter_1 (
    .count(run), .Q(\总周期数 ), .clk(CLK), .clr(RST));  // open: load, D, carry
  Counter #(.width(16), .max('hffff)) counter_2 (
    .count(\条件分支 ), .Q(\条件分支成功数 ), .clk(CLK), .clr(RST));  // open: load, D, carry
  RAM #(.addrWidth(10), .dataWidth(32), .bus("separate")) ram_1 (
    .addr(ALUres_MEM[11:2]), .din(EX_MEM_r2_out), .data(MEMD_MEM), .str(Memwrite), .clk(CLK), .clr(RST));  // open: sel, ld
  // Probe on LBU
  // Probe on LedData
  // Probe on ALUres_MEM
  // Probe on MEMD_MEM
  // Probe on Memwrite
  Multiplexer #(.select(2), .width(8), .disabled(0), .enable("false")) multiplexer_9 (
    .in0(MEMD_MEM[7:0]), .in1(MEMD_MEM[15:8]), .in2(MEMD_MEM[23:16]), .in3(MEMD_MEM[31:24]),
    .out(multiplexer_9_out), .sel(ALUres_MEM[1:0]));
  // Probe on WB_MEM
  Multiplexer #(.width(32), .enable("false")) multiplexer_10 (
    .in0(MEMD_MEM), .in1({{24{1'b0}}, multiplexer_9_out}), .out(multiplexer_10_out), .sel(LBU));
  Counter #(.width(16), .max('hffff)) counter_3 (
    .count(JMP), .Q(\无条件分支数 ), .clk(CLK), .clr(RST));  // open: load, D, carry
  MEM_WB mem_wb_1 (
    .Bubble(1'b0), .Enable(run), .CLK(CLK), .CLR(RST), .PC_IN(MEM_PC), .PC_OUT(WB_PC), .IR_IN(INS_MEM),
    .IR_OUT(INS_WB), .ALURS_IN(ALUres_MEM), .ALURS_OUT(mem_wb_1_alurs_out), .MEMD_IN(multiplexer_10_out),
    .MEMD_OUT(mem_wb_1_memd_out), .WB(WB_MEM), .WB_2({Mem2reg, RegDst, Regwrite}), .SysCALL_2(syscall),
    .SysCALL(EX_MEM_syscall_2), .JAL(EX_MEM_jal_2), .JAL_2(JAL_WB));  // open: HALT, HALT_2, WR_IN, WR_OUT
  Multiplexer #(.width(32)) multiplexer_11 (
    .in0(mem_wb_1_alurs_out), .in1(mem_wb_1_memd_out), .out(multiplexer_11_out), .sel(Mem2reg));  // open: en
  Multiplexer #(.width(32)) multiplexer_12 (
    .in0(multiplexer_11_out), .in1(WB_PC), .out(Din), .sel(JAL_WB));  // open: en
  // Probe on WR
  // Probe on Regwrite
  Multiplexer #(.width(5), .enable("false")) multiplexer_13 (
    .in0(INS_WB[20:16]), .in1(INS_WB[15:11]), .out(multiplexer_13_out), .sel(RegDst));
  // Probe on Din
  Multiplexer #(.width(5), .enable("false")) multiplexer_14 (
    .in0(multiplexer_13_out), .in1({5{1'b1}}), .out(WR), .sel(JAL_WB));

  // Other names for the same wires on the sheet: Shamt[4:0] = INS_ID[10:6];
  //   J_addr[31:2] = {EX_PC[31:28], EX_PC[25:0]}; 加1的PC[31:0] = IF_PC

  // Notes on the sheet:
  //   中断源
  //   中断等待指示
  //   数码管输出
  //   指令存储器
  //   指令字
  //   contents of rom_1 (hex, n*v repeats v):
  //   20110001 8000005 20110001 20120002 20130003 8000009 20110001 20120002 20130003 800000d 20110001
  //   20120002 20130003 8000011 20110001 20120002 20130003 c0000b8 20100001 20110001 118fc0 112020
  //   20020022 c 118882 12200001 8000015 112020 20020022 c 20110001 118880 112020 20020022 c 12200001
  //   800001f 20110001 118fc0 112020 20020022 c 1188c3 112020 20020022 c 118903 112020 20020022 c 118903
  //   112020 20020022 c 118903 112020 20020022 c 118903 112020 20020022 c 118903 112020 20020022 c 118903
  //   112020 20020022 c 118903 112020 20020022 c 20100001 109fc0 139fc3 8021 2012000c 24160003 26100001
  //   3210000f 20080008 20090001 139900 2709825 132020 20020022 c 1094022 1500fff9 22100001 2018000f
  //   2188024 108700 20080008 20090001 139902 2709825 132021 20020022 c 1094022 1500fff9 108702 2c9b022
  //   12c00001 8000050 4020 1084027 84400 3508ffff 82021 20020022 c 2010ffff 20110000 ae300000 22100001
  //   22310004 ae300000 22100001 22310004 ae300000 22100001 22310004 ae300000 22100001 22310004 ae300000
  //   22100001 22310004 ae300000 22100001 22310004 ae300000 22100001 22310004 ae300000 22100001 22310004
  //   ae300000 22100001 22310004 ae300000 22100001 22310004 ae300000 22100001 22310004 ae300000 22100001
  //   22310004 ae300000 22100001 22310004 ae300000 22100001 22310004 ae300000 22100001 22310004 ae300000
  //   22100001 22310004 22100001 8020 2011003c 8e130000 8e340000 274402a 11000002 ae330000 ae140000
  //   2231fffc 1611fff8 102020 20020022 c 22100004 2011003c 1611fff2 20020032 c 20100000 22100001 102020
  //   20020022 c 22100002 102020 20020022 c 22100003 102020 20020022 c 22100004 102020 20020022 c 22100005
  //   102020 20020022 c 22100006 102020 20020022 c 22100007 102020 20020022 c 22100008 102020 20020022
  //   20020022 c 3e00008
  //   OP
  //   rs
  //   rt
  //   rd
  //   Imm
  //   Shamt
  //   流水调试日志用
  //   Func
  //   bgtz
  //   JMP
  //   JR
  //   SignedExt
  //   LUISrc
  //   OP
  //   Func
  //   Beq
  //   Bne
  //   MemToReg
  //   MemWrite
  //   AluOP
  //   AluSrcB
  //   RegWrite
  //   JAL
  //   RegDst
  //   Syscall
  //   addr
  //   Imm
  //   rt
  //   rd
endmodule

// 源寄存器使用情况
module \源寄存器使用情况  (
  input  OP0,
  input  OP1,
  input  OP2,
  input  OP3,
  input  OP4,
  input  OP5,
  input  F0,
  input  F1,
  input  F2,
  input  F3,
  input  F4,
  input  F5,
  output R1_Used,
  output R2_Used
);

  wire and_1_out, and_2_out, and_3_out, and_4_out, and_5_out, and_6_out, and_7_out, and_8_out, and_9_out,
       and_10_out, and_11_out, and_12_out, and_13_out, and_14_out, and_15_out, and_16_out, and_17_out,
       and_18_out, and_19_out, and_20_out, and_21_out, and_22_out, and_23_out, and_24_out, and_25_out,
       and_26_out, and_27_out, and_28_out, and_29_out, and_30_out, and_31_out, and_32_out, and_33_out,
       and_34_out, and_35_out, and_36_out, and_37_out, not_1_out, not_2_out, not_3_out, not_4_out, not_5_out,
       not_6_out, not_7_out, not_8_out, not_9_out, not_10_out, not_11_out, not_12_out, not_13_out,
       not_14_out, not_15_out, not_16_out, not_17_out, not_18_out, not_19_out, not_20_out, not_21_out,
       not_22_out, not_23_out, not_24_out, not_25_out, not_26_out, not_27_out, not_28_out, not_29_out,
       not_30_out, not_31_out, not_32_out, not_33_out, not_34_out, not_35_out, not_36_out, not_37_out,
       not_38_out, not_39_out, not_40_out, not_41_out, not_42_out, not_43_out, not_44_out, not_45_out,
       not_46_out, not_47_out, not_48_out, not_49_out, not_50_out, not_51_out, not_52_out, not_53_out,
       not_54_out, not_55_out, not_56_out, not_57_out, not_58_out, not_59_out, not_60_out, not_61_out,
       not_62_out, not_63_out, not_64_out, not_65_out, not_66_out, not_67_out, not_68_out, not_69_out,
       not_70_out, not_71_out, not_72_out, not_73_out, not_74_out, not_75_out, not_76_out, not_77_out,
       not_78_out, not_79_out, not_80_out, not_81_out, not_82_out, not_83_out, not_84_out, not_85_out,
       not_86_out, not_87_out, not_88_out, not_89_out, not_90_out, not_91_out, not_92_out, not_93_out,
       not_94_out, not_95_out, not_96_out, not_97_out, not_98_out, not_99_out, not_100_out, not_101_out,
       not_102_out, not_103_out, not_104_out, not_105_out, not_106_out, not_107_out, not_108_out,
       not_109_out, not_110_out, not_111_out, not_112_out, not_113_out, not_114_out, not_115_out,
       not_116_out, not_117_out, not_118_out, not_119_out, not_120_out, not_121_out, not_122_out,
       not_123_out, not_124_out, not_125_out, not_126_out, not_127_out, not_128_out, not_129_out,
       not_130_out, not_131_out, not_132_out, not_133_out, not_134_out, not_135_out, not_136_out,
       not_137_out, not_138_out, not_139_out, not_140_out, not_141_out, not_142_out, not_143_out,
       not_144_out, not_145_out, not_146_out, not_147_out, not_148_out, not_149_out, not_150_out,
       not_151_out, not_152_out, not_153_out, not_154_out, not_155_out, not_156_out, not_157_out,
       not_158_out, not_159_out, not_160_out, not_161_out, not_162_out, not_163_out, not_164_out,
       not_165_out, not_166_out, not_167_out, not_168_out, not_169_out, not_170_out, not_171_out,
       not_172_out, not_173_out, not_174_out, not_175_out, not_176_out, not_177_out, not_178_out,
       not_179_out, not_180_out, not_181_out, not_182_out, not_183_out, not_184_out, not_185_out,
       not_186_out, not_187_out, not_188_out, not_189_out, not_190_out, not_191_out, not_192_out,
       not_193_out, not_194_out, not_195_out, not_196_out, not_197_out, not_198_out, not_199_out,
       not_200_out, not_201_out, not_202_out, not_203_out, not_204_out, not_205_out, not_206_out,
       not_207_out, not_208_out, not_209_out, not_210_out, not_211_out, not_212_out, not_213_out,
       not_214_out, not_215_out, not_216_out, not_217_out, not_218_out, not_219_out, not_220_out,
       not_221_out, not_222_out, not_223_out, not_224_out, not_225_out, not_226_out, not_227_out,
       not_228_out, not_229_out, not_230_out, not_231_out, not_232_out, not_233_out, not_234_out,
       not_235_out, not_236_out, not_237_out, not_238_out, not_239_out, not_240_out, not_241_out,
       not_242_out, not_243_out, not_244_out, not_245_out, not_246_out, not_247_out, not_248_out,
       not_249_out, not_250_out, not_251_out, not_252_out, not_253_out, not_254_out, not_255_out,
       not_256_out, not_257_out, not_258_out, not_259_out, not_260_out, not_261_out, not_262_out,
       not_263_out, not_264_out, not_265_out, not_266_out, not_267_out, not_268_out, not_269_out;

  not not_1 (not_1_out, OP5);
  not not_2 (not_2_out, OP4);
  not not_3 (not_3_out, OP3);
  not not_4 (not_4_out, OP2);
  not not_5 (not_5_out, OP1);
  not not_6 (not_6_out, OP0);
  not not_7 (not_7_out, F4);
  not not_8 (not_8_out, F3);
  not not_9 (not_9_out, F2);
  not not_10 (not_10_out, F1);
  not not_11 (not_11_out, F0);
  not not_12 (not_12_out, OP5);
  not not_13 (not_13_out, OP4);
  not not_14 (not_14_out, OP3);
  not not_15 (not_15_out, OP2);
  not not_16 (not_16_out, OP1);
  not not_17 (not_17_out, OP0);
  not not_18 (not_18_out, F4);
  not not_19 (not_19_out, F3);
  not not_20 (not_20_out, F2);
  not not_21 (not_21_out, F1);
  not not_22 (not_22_out, OP5);
  not not_23 (not_23_out, OP4);
  not not_24 (not_24_out, OP3);
  not not_25 (not_25_out, OP2);
  not not_26 (not_26_out, OP1);
  not not_27 (not_27_out, OP0);
  not not_28 (not_28_out, F4);
  not not_29 (not_29_out, F3);
  not not_30 (not_30_out, F2);
  not not_31 (not_31_out, F0);
  not not_32 (not_32_out, OP5);
  not not_33 (not_33_out, OP4);
  not not_34 (not_34_out, OP3);
  not not_35 (not_35_out, OP2);
  not not_36 (not_36_out, OP1);
  not not_37 (not_37_out, OP0);
  not not_38 (not_38_out, F4);
  not not_39 (not_39_out, F3);
  not not_40 (not_40_out, F1);
  not not_41 (not_41_out, F0);
  not not_42 (not_42_out, OP5);
  not not_43 (not_43_out, OP4);
  not not_44 (not_44_out, OP3);
  not not_45 (not_45_out, OP2);
  not not_46 (not_46_out, OP1);
  not not_47 (not_47_out, OP0);
  not not_48 (not_48_out, F4);
  not not_49 (not_49_out, F3);
  not not_50 (not_50_out, F1);
  not not_51 (not_51_out, OP5);
  not not_52 (not_52_out, OP4);
  not not_53 (not_53_out, OP3);
  not not_54 (not_54_out, OP2);
  not not_55 (not_55_out, OP1);
  not not_56 (not_56_out, OP0);
  not not_57 (not_57_out, F4);
  not not_58 (not_58_out, F3);
  not not_59 (not_59_out, OP5);
  not not_60 (not_60_out, OP4);
  not not_61 (not_61_out, OP3);
  not not_62 (not_62_out, OP2);
  not not_63 (not_63_out, OP1);
  not not_64 (not_64_out, OP0);
  not not_65 (not_65_out, F4);
  not not_66 (not_66_out, F2);
  not not_67 (not_67_out, F0);
  not not_68 (not_68_out, OP5);
  not not_69 (not_69_out, OP4);
  not not_70 (not_70_out, OP3);
  not not_71 (not_71_out, OP2);
  not not_72 (not_72_out, OP1);
  not not_73 (not_73_out, OP0);
  not not_74 (not_74_out, F4);
  not not_75 (not_75_out, F2);
  not not_76 (not_76_out, OP5);
  not not_77 (not_77_out, OP4);
  not not_78 (not_78_out, OP3);
  not not_79 (not_79_out, OP2);
  not not_80 (not_80_out, OP1);
  not not_81 (not_81_out, OP0);
  not not_82 (not_82_out, F5);
  not not_83 (not_83_out, F4);
  not not_84 (not_84_out, F2);
  not not_85 (not_85_out, F1);
  not not_86 (not_86_out, F0);
  not not_87 (not_87_out, OP5);
  not not_88 (not_88_out, OP4);
  not not_89 (not_89_out, OP3);
  not not_90 (not_90_out, OP2);
  not not_91 (not_91_out, OP1);
  not not_92 (not_92_out, OP0);
  not not_93 (not_93_out, F5);
  not not_94 (not_94_out, F4);
  not not_95 (not_95_out, F1);
  not not_96 (not_96_out, F0);
  not not_97 (not_97_out, OP5);
  not not_98 (not_98_out, OP4);
  not not_99 (not_99_out, OP3);
  not not_100 (not_100_out, OP1);
  not not_101 (not_101_out, OP0);
  not not_102 (not_102_out, OP5);
  not not_103 (not_103_out, OP4);
  not not_104 (not_104_out, OP3);
  not not_105 (not_105_out, OP1);
  not not_106 (not_106_out, OP5);
  not not_107 (not_107_out, OP4);
  not not_108 (not_108_out, OP2);
  not not_109 (not_109_out, OP1);
  not not_110 (not_110_out, OP0);
  not not_111 (not_111_out, OP5);
  not not_112 (not_112_out, OP4);
  not not_113 (not_113_out, OP1);
  not not_114 (not_114_out, OP0);
  not not_115 (not_115_out, OP5);
  not not_116 (not_116_out, OP4);
  not not_117 (not_117_out, OP2);
  not not_118 (not_118_out, OP1);
  not not_119 (not_119_out, OP5);
  not not_120 (not_120_out, OP4);
  not not_121 (not_121_out, OP2);
  not not_122 (not_122_out, OP0);
  not not_123 (not_123_out, OP5);
  not not_124 (not_124_out, OP4);
  not not_125 (not_125_out, OP1);
  not not_126 (not_126_out, OP4);
  not not_127 (not_127_out, OP3);
  not not_128 (not_128_out, OP2);
  not not_129 (not_129_out, OP4);
  not not_130 (not_130_out, OP2);
  not not_131 (not_131_out, OP5);
  not not_132 (not_132_out, OP4);
  not not_133 (not_133_out, OP2);
  not not_134 (not_134_out, OP4);
  not not_135 (not_135_out, OP3);
  not not_136 (not_136_out, OP1);
  not not_137 (not_137_out, OP0);
  not not_138 (not_138_out, OP5);
  not not_139 (not_139_out, OP4);
  not not_140 (not_140_out, OP3);
  not not_141 (not_141_out, OP5);
  not not_142 (not_142_out, OP4);
  not not_143 (not_143_out, OP3);
  not not_144 (not_144_out, OP2);
  not not_145 (not_145_out, OP1);
  not not_146 (not_146_out, OP0);
  not not_147 (not_147_out, F5);
  not not_148 (not_148_out, F4);
  not not_149 (not_149_out, F3);
  not not_150 (not_150_out, F2);
  not not_151 (not_151_out, F1);
  not not_152 (not_152_out, F0);
  not not_153 (not_153_out, OP5);
  not not_154 (not_154_out, OP4);
  not not_155 (not_155_out, OP3);
  not not_156 (not_156_out, OP2);
  not not_157 (not_157_out, OP1);
  not not_158 (not_158_out, OP0);
  not not_159 (not_159_out, F5);
  not not_160 (not_160_out, F4);
  not not_161 (not_161_out, F3);
  not not_162 (not_162_out, F2);
  not not_163 (not_163_out, OP5);
  not not_164 (not_164_out, OP4);
  not not_165 (not_165_out, OP3);
  not not_166 (not_166_out, OP2);
  not not_167 (not_167_out, OP1);
  not not_168 (not_168_out, OP0);
  not not_169 (not_169_out, F5);
  not not_170 (not_170_out, F4);
  not not_171 (not_171_out, F3);
  not not_172 (not_172_out, F2);
  not not_173 (not_173_out, F0);
  not not_174 (not_174_out, OP5);
  not not_175 (not_175_out, OP4);
  not not_176 (not_176_out, OP3);
  not not_177 (not_177_out, OP2);
  not not_178 (not_178_out, OP1);
  not not_179 (not_179_out, OP0);
  not not_180 (not_180_out, F4);
  not not_181 (not_181_out, F3);
  not not_182 (not_182_out, F2);
  not not_183 (not_183_out, F1);
  not not_184 (not_184_out, F0);
  not not_185 (not_185_out, OP5);
  not not_186 (not_186_out, OP4);
  not not_187 (not_187_out, OP3);
  not not_188 (not_188_out, OP2);
  not not_189 (not_189_out, OP1);
  not not_190 (not_190_out, OP0);
  not not_191 (not_191_out, F4);
  not not_192 (not_192_out, F3);
  not not_193 (not_193_out, F2);
  not not_194 (not_194_out, F1);
  not not_195 (not_195_out, OP5);
  not not_196 (not_196_out, OP4);
  not not_197 (not_197_out, OP3);
  not not_198 (not_198_out, OP2);
  not not_199 (not_199_out, OP1);
  not not_200 (not_200_out, OP0);
  not not_201 (not_201_out, F4);
  not not_202 (not_202_out, F3);
  not not_203 (not_203_out, F2);
  not not_204 (not_204_out, F0);
  not not_205 (not_205_out, OP5);
  not not_206 (not_206_out, OP4);
  not not_207 (not_207_out, OP3);
  not not_208 (not_208_out, OP2);
  not not_209 (not_209_out, OP1);
  not not_210 (not_210_out, OP0);
  not not_211 (not_211_out, F4);
  not not_212 (not_212_out, F3);
  not not_213 (not_213_out, F1);
  not not_214 (not_214_out, F0);
  not not_215 (not_215_out, OP5);
  not not_216 (not_216_out, OP4);
  not not_217 (not_217_out, OP3);
  not not_218 (not_218_out, OP2);
  not not_219 (not_219_out, OP1);
  not not_220 (not_220_out, OP0);
  not not_221 (not_221_out, F4);
  not not_222 (not_222_out, F3);
  not not_223 (not_223_out, F1);
  not not_224 (not_224_out, OP5);
  not not_225 (not_225_out, OP4);
  not not_226 (not_226_out, OP3);
  not not_227 (not_227_out, OP2);
  not not_228 (not_228_out, OP1);
  not not_229 (not_229_out, OP0);
  not not_230 (not_230_out, F4);
  not not_231 (not_231_out, F3);
  not not_232 (not_232_out, OP5);
  not not_233 (not_233_out, OP4);
  not not_234 (not_234_out, OP3);
  not not_235 (not_235_out, OP2);
  not not_236 (not_236_out, OP1);
  not not_237 (not_237_out, OP0);
  not not_238 (not_238_out, F4);
  not not_239 (not_239_out, F2);
  not not_240 (not_240_out, F0);
  not not_241 (not_241_out, OP5);
  not not_242 (not_242_out, OP4);
  not not_243 (not_243_out, OP3);
  not not_244 (not_244_out, OP2);
  not not_245 (not_245_out, OP1);
  not not_246 (not_246_out, OP0);
  not not_247 (not_247_out, F4);
  not not_248 (not_248_out, F2);
  not not_249 (not_249_out, OP5);
  not not_250 (not_250_out, OP4);
  not not_251 (not_251_out, OP3);
  not not_252 (not_252_out, OP2);
  not not_253 (not_253_out, OP1);
  not not_254 (not_254_out, OP0);
  not not_255 (not_255_out, F5);
  not not_256 (not_256_out, F4);
  not not_257 (not_257_out, F1);
  not not_258 (not_258_out, F0);
  not not_259 (not_259_out, OP5);
  not not_260 (not_260_out, OP4);
  not not_261 (not_261_out, OP3);
  not not_262 (not_262_out, OP1);
  not not_263 (not_263_out, OP0);
  not not_264 (not_264_out, OP5);
  not not_265 (not_265_out, OP4);
  not not_266 (not_266_out, OP3);
  not not_267 (not_267_out, OP1);
  not not_268 (not_268_out, OP4);
  not not_269 (not_269_out, OP2);
  and and_1 (and_1_out, not_1_out, not_2_out, not_3_out, not_4_out, not_5_out, not_6_out, F5, not_7_out, not_8_out, not_9_out, not_10_out, not_11_out);
  and and_2 (and_2_out, not_12_out, not_13_out, not_14_out, not_15_out, not_16_out, not_17_out, F5, not_18_out, not_19_out, not_20_out, not_21_out, F0);
  and and_3 (and_3_out, not_22_out, not_23_out, not_24_out, not_25_out, not_26_out, not_27_out, F5, not_28_out, not_29_out, not_30_out, F1, not_31_out);
  and and_4 (and_4_out, not_32_out, not_33_out, not_34_out, not_35_out, not_36_out, not_37_out, F5, not_38_out, not_39_out, F2, not_40_out, not_41_out);
  and and_5 (and_5_out, not_42_out, not_43_out, not_44_out, not_45_out, not_46_out, not_47_out, F5, not_48_out, not_49_out, F2, not_50_out, F0);
  and and_6 (and_6_out, not_51_out, not_52_out, not_53_out, not_54_out, not_55_out, not_56_out, F5, not_57_out, not_58_out, F2, F1, F0);
  and and_7 (and_7_out, not_59_out, not_60_out, not_61_out, not_62_out, not_63_out, not_64_out, F5, not_65_out, F3, not_66_out, F1, not_67_out);
  and and_8 (and_8_out, not_68_out, not_69_out, not_70_out, not_71_out, not_72_out, not_73_out, F5, not_74_out, F3, not_75_out, F1, F0);
  and and_9 (and_9_out, not_76_out, not_77_out, not_78_out, not_79_out, not_80_out, not_81_out, not_82_out, not_83_out, F3, not_84_out, not_85_out, not_86_out);
  and and_10 (and_10_out, not_87_out, not_88_out, not_89_out, not_90_out, not_91_out, not_92_out, not_93_out, not_94_out, F3, F2, not_95_out, not_96_out);
  and and_11 (and_11_out, not_97_out, not_98_out, not_99_out, OP2, not_100_out, not_101_out);
  and and_12 (and_12_out, not_102_out, not_103_out, not_104_out, OP2, not_105_out, OP0);
  and and_13 (and_13_out, not_106_out, not_107_out, OP3, not_108_out, not_109_out, not_110_out);
  and and_14 (and_14_out, not_111_out, not_112_out, OP3, OP2, not_113_out, not_114_out);
  and and_15 (and_15_out, not_115_out, not_116_out, OP3, not_117_out, not_118_out, OP0);
  and and_16 (and_16_out, not_119_out, not_120_out, OP3, not_121_out, OP1, not_122_out);
  and and_17 (and_17_out, not_123_out, not_124_out, OP3, OP2, not_125_out, OP0);
  and and_18 (and_18_out, OP5, not_126_out, not_127_out, not_128_out, OP1, OP0);
  and and_19 (and_19_out, OP5, not_129_out, OP3, not_130_out, OP1, OP0);
  and and_20 (and_20_out, not_131_out, not_132_out, OP3, not_133_out, OP1, OP0);
  and and_21 (and_21_out, OP5, not_134_out, not_135_out, OP2, not_136_out, not_137_out);
  and and_22 (and_22_out, not_138_out, not_139_out, not_140_out, OP2, OP1, OP0);
  and and_23 (and_23_out, not_141_out, not_142_out, not_143_out, not_144_out, not_145_out, not_146_out, not_147_out, not_148_out, not_149_out, not_150_out, not_151_out, not_152_out);
  and and_24 (and_24_out, not_153_out, not_154_out, not_155_out, not_156_out, not_157_out, not_158_out, not_159_out, not_160_out, not_161_out, not_162_out, F1, F0);
  and and_25 (and_25_out, not_163_out, not_164_out, not_165_out, not_166_out, not_167_out, not_168_out, not_169_out, not_170_out, not_171_out, not_172_out, F1, not_173_out);
  and and_26 (and_26_out, not_174_out, not_175_out, not_176_out, not_177_out, not_178_out, not_179_out, F5, not_180_out, not_181_out, not_182_out, not_183_out, not_184_out);
  and and_27 (and_27_out, not_185_out, not_186_out, not_187_out, not_188_out, not_189_out, not_190_out, F5, not_191_out, not_192_out, not_193_out, not_194_out, F0);
  and and_28 (and_28_out, not_195_out, not_196_out, not_197_out, not_198_out, not_199_out, not_200_out, F5, not_201_out, not_202_out, not_203_out, F1, not_204_out);
  and and_29 (and_29_out, not_205_out, not_206_out, not_207_out, not_208_out, not_209_out, not_210_out, F5, not_211_out, not_212_out, F2, not_213_out, not_214_out);
  and and_30 (and_30_out, not_215_out, not_216_out, not_217_out, not_218_out, not_219_out, not_220_out, F5, not_221_out, not_222_out, F2, not_223_out, F0);
  and and_31 (and_31_out, not_224_out, not_225_out, not_226_out, not_227_out, not_228_out, not_229_out, F5, not_230_out, not_231_out, F2, F1, F0);
  and and_32 (and_32_out, not_232_out, not_233_out, not_234_out, not_235_out, not_236_out, not_237_out, F5, not_238_out, F3, not_239_out, F1, not_240_out);
  and and_33 (and_33_out, not_241_out, not_242_out, not_243_out, not_244_out, not_245_out, not_246_out, F5, not_247_out, F3, not_248_out, F1, F0);
  and and_34 (and_34_out, not_249_out, not_250_out, not_251_out, not_252_out, not_253_out, not_254_out, not_255_out, not_256_out, F3, F2, not_257_out, not_258_out);
  and and_35 (and_35_out, not_259_out, not_260_out, not_261_out, OP2, not_262_out, not_263_out);
  and and_36 (and_36_out, not_264_out, not_265_out, not_266_out, OP2, not_267_out, OP0);
  and and_37 (and_37_out, OP5, not_268_out, OP3, not_269_out, OP1, OP0);
  or or_1 (R1_Used, and_1_out, and_2_out, and_3_out, and_4_out, and_5_out, and_6_out, and_7_out, and_8_out, and_9_out, and_10_out, and_11_out, and_12_out, and_13_out, and_14_out, and_15_out, and_16_out, and_17_out, and_18_out, and_19_out, and_20_out, and_21_out, and_22_out);
  or or_2 (R2_Used, and_23_out, and_24_out, and_25_out, and_26_out, and_27_out, and_28_out, and_29_out, and_30_out, and_31_out, and_32_out, and_33_out, and_34_out, and_35_out, and_36_out, and_37_out);
endmodule

module \数据相关检测  (
  input  [5:0] OP,
  input  [4:0] EX_WriteReg_num,
  input  EX_RegWrite,
  input  [4:0] MEM_WriteReg_num,
  input  MEM_RegWrite,
  input  [5:0] Func,
  input  [4:0] ID_R1_num,
  input  [4:0] ID_R2_num,
  output \数据相关 
);

  wire and_1_out, and_2_out, and_3_out, and_4_out, comparator_1_eq, comparator_2_eq, comparator_3_eq,
       comparator_4_eq, controlled_buffer_1_out, controlled_buffer_2_out, controlled_buffer_3_out,
       controlled_buffer_4_out, or_1_out, or_2_out, or_3_out, or_4_out, \源寄存器使用情况_1_r1_used ,
       \源寄存器使用情况_1_r2_used ;

  // Probe on MEM_WriteReg_num
  \源寄存器使用情况  \u_源寄存器使用情况_1  (
    .OP0(OP[0]), .OP1(OP[1]), .OP2(OP[2]), .OP3(OP[3]), .OP4(OP[4]), .OP5(OP[5]), .F0(Func[0]), .F1(Func[1]),
    .F2(Func[2]), .F3(Func[3]), .F4(Func[4]), .F5(Func[5]), .R1_Used(\源寄存器使用情况_1_r1_used ),
    .R2_Used(\源寄存器使用情况_1_r2_used ));
  or or_1 (or_1_out, ID_R1_num[0], ID_R1_num[1], ID_R1_num[2], ID_R1_num[3], ID_R1_num[4]);
  and and_1 (and_1_out, or_1_out, \源寄存器使用情况_1_r1_used );
  and and_2 (and_2_out, \源寄存器使用情况_1_r2_used , or_2_out);
  or or_2 (or_2_out, ID_R2_num[0], ID_R2_num[1], ID_R2_num[2], ID_R2_num[3], ID_R2_num[4]);
  Comparator #(.width(5)) comparator_1 (.a(ID_R1_num), .b(EX_WriteReg_num), .eq(comparator_1_eq));  // open: gt, lt
  // Probe on EX_WriteReg_num
  Comparator #(.width(5)) comparator_2 (.a(EX_WriteReg_num), .b(ID_R2_num), .eq(comparator_2_eq));  // open: gt, lt
  assign controlled_buffer_1_out = and_2_out ? comparator_2_eq : 1'bz;  // Controlled_Buffer controlled_buffer_1
  Comparator #(.width(5)) comparator_3 (.a(ID_R1_num), .b(MEM_WriteReg_num), .eq(comparator_3_eq));  // open: gt, lt
  Comparator #(.width(5)) comparator_4 (.a(MEM_WriteReg_num), .b(ID_R2_num), .eq(comparator_4_eq));  // open: gt, lt
  assign controlled_buffer_2_out = and_1_out ? comparator_1_eq : 1'bz;  // Controlled_Buffer controlled_buffer_2
  Pull_Resistor pull_resistor_1 (.node(controlled_buffer_2_out));
  Pull_Resistor pull_resistor_2 (.node(controlled_buffer_1_out));
  assign controlled_buffer_3_out = and_1_out ? comparator_3_eq : 1'bz;  // Controlled_Buffer controlled_buffer_3
  assign controlled_buffer_4_out = and_2_out ? comparator_4_eq : 1'bz;  // Controlled_Buffer controlled_buffer_4
  Pull_Resistor pull_resistor_3 (.node(controlled_buffer_3_out));
  Pull_Resistor pull_resistor_4 (.node(controlled_buffer_4_out));
  or or_3 (or_3_out, controlled_buffer_2_out, controlled_buffer_1_out);
  or or_4 (or_4_out, controlled_buffer_3_out, controlled_buffer_4_out);
  and and_3 (and_3_out, or_3_out, EX_RegWrite);
  and and_4 (and_4_out, or_4_out, MEM_RegWrite);
  or or_5 (\数据相关 , and_3_out, and_4_out);

  // Other names for the same wires on the sheet: OP_CODE[5:0] = OP
endmodule

module IF_ID (
  input  Bubble,
  input  Enable,
  input  CLK,
  input  CLR,
  input  [31:0] PC_IN,
  input  [31:0] IR_IN,
  output [31:0] PC_OUT,
  output [31:0] IR_OUT
);

  wire [31:0] multiplexer_1_out, multiplexer_2_out;

  Multiplexer #(.width(32), .enable("false")) multiplexer_1 (
    .in0(PC_IN), .in1({32{1'b0}}), .out(multiplexer_1_out), .sel(Bubble));
  Multiplexer #(.width(32), .enable("false")) multiplexer_2 (
    .in0(IR_IN), .in1({32{1'b0}}), .out(multiplexer_2_out), .sel(Bubble));
  Register #(.width(32)) PC_R (.D(multiplexer_1_out), .en(Enable), .Q(PC_OUT), .clk(CLK), .clr(CLR));
  Register #(.width(32)) IR_R (.D(multiplexer_2_out), .en(Enable), .Q(IR_OUT), .clk(CLK), .clr(CLR));
endmodule

module ID_EX (
  input  Bubble,
  input  Enable,
  input  CLK,
  input  CLR,
  input  [31:0] PC_IN,
  input  [31:0] IR_IN,
  input  [31:0] R1_IN,
  input  [31:0] ALUB_IN,
  input  RegWrite,
  input  [31:0] R2_IN,
  input  RegDst,
  input  MemToReg,
  input  MemWrite,
  input  LBU,
  input  Bgzt,
  input  Beq,
  input  Bne,
  input  [3:0] ALUOP_IN,
  input  JR,
  input  JMP,
  input  [4:0] Shamt_IN,
  input  JAL,
  input  SysCALL,
  input  [4:0] WR_IN,
  input  [3:0] Forward_IN,
  input  ALUSrcB,
  input  [31:0] Imm,
  output [31:0] PC_OUT,
  output [31:0] IR_OUT,
  output [31:0] R1_OUT,
  output [31:0] ALUB_OUT,
  output [31:0] R2_OUT,
  output [2:0] WB,
  output [1:0] MEM,
  output [2:0] BRANCH_OUT,
  output [2:0] JMP_OUT,
  output SysCALL_2,
  output [3:0] ALUOP_OUT,
  output [4:0] Shamt_OUT,
  output [4:0] WR_OUT,
  output [3:0] Forward_OUT,
  output ALUSrcB_2,
  output [31:0] Imm_2
);

  wire multiplexer_11_out;
  wire [3:0] multiplexer_7_out, multiplexer_10_out;
  wire [4:0] multiplexer_8_out, multiplexer_9_out;
  wire [11:0] multiplexer_6_out;
  wire [31:0] multiplexer_1_out, multiplexer_2_out, multiplexer_3_out, multiplexer_4_out, multiplexer_5_out,
       multiplexer_12_out;

  Multiplexer #(.width(32), .enable("false")) multiplexer_1 (
    .in0(PC_IN), .in1({32{1'b0}}), .out(multiplexer_1_out), .sel(Bubble));
  Multiplexer #(.width(32), .enable("false")) multiplexer_2 (
    .in0(IR_IN), .in1({32{1'b0}}), .out(multiplexer_2_out), .sel(Bubble));
  Multiplexer #(.width(32), .enable("false")) multiplexer_3 (
    .in0(R1_IN), .in1({32{1'b0}}), .out(multiplexer_3_out), .sel(Bubble));
  Multiplexer #(.width(32), .enable("false")) multiplexer_4 (
    .in0(ALUB_IN), .in1({32{1'b0}}), .out(multiplexer_4_out), .sel(Bubble));
  Multiplexer #(.width(32), .enable("false")) multiplexer_5 (
    .in0(R2_IN), .in1({32{1'b0}}), .out(multiplexer_5_out), .sel(Bubble));
  Multiplexer #(.width(12), .enable("false")) multiplexer_6 (
    .in0({SysCALL, JAL, JMP, JR, Bne, Beq, Bgzt, LBU, MemWrite, MemToReg, RegDst, RegWrite}),
    .in1({12{1'b0}}), .out(multiplexer_6_out), .sel(Bubble));
  Multiplexer #(.width(4), .enable("false")) multiplexer_7 (
    .in0(ALUOP_IN), .in1(4'b0000), .out(multiplexer_7_out), .sel(Bubble));
  Multiplexer #(.width(5), .enable("false")) multiplexer_8 (
    .in0(Shamt_IN), .in1({5{1'b0}}), .out(multiplexer_8_out), .sel(Bubble));
  Multiplexer #(.width(5), .enable("false")) multiplexer_9 (
    .in0(WR_IN), .in1({5{1'b0}}), .out(multiplexer_9_out), .sel(Bubble));
  Multiplexer #(.width(4), .enable("false")) multiplexer_10 (
    .in0(Forward_IN), .in1(4'b0000), .out(multiplexer_10_out), .sel(Bubble));
  Multiplexer #(.enable("false")) multiplexer_11 (.in0(ALUSrcB), .in1(1'b0), .out(multiplexer_11_out), .sel(Bubble));
  Multiplexer #(.width(32), .enable("false")) multiplexer_12 (
    .in0(Imm), .in1({32{1'b0}}), .out(multiplexer_12_out), .sel(Bubble));
  Register #(.width(32)) PC_R (.D(multiplexer_1_out), .en(Enable), .Q(PC_OUT), .clk(CLK), .clr(CLR));
  Register #(.width(32)) IR_R (.D(multiplexer_2_out), .en(Enable), .Q(IR_OUT), .clk(CLK), .clr(CLR));
  Register #(.width(32)) R1_R (.D(multiplexer_3_out), .en(Enable), .Q(R1_OUT), .clk(CLK), .clr(CLR));
  Register #(.width(32)) ALUB_R (.D(multiplexer_4_out), .en(Enable), .Q(ALUB_OUT), .clk(CLK), .clr(CLR));
  Register #(.width(32)) R2_R (.D(multiplexer_5_out), .en(Enable), .Q(R2_OUT), .clk(CLK), .clr(CLR));
  Register #(.width(12)) Control_R (
    .D(multiplexer_6_out), .en(Enable), .Q({SysCALL_2, JMP_OUT, BRANCH_OUT, MEM, WB}), .clk(CLK), .clr(CLR));
  Register #(.width(4)) ALUOP_R (.D(multiplexer_7_out), .en(Enable), .Q(ALUOP_OUT), .clk(CLK), .clr(CLR));
  Register #(.width(5)) Shamt_R (.D(multiplexer_8_out), .en(Enable), .Q(Shamt_OUT), .clk(CLK), .clr(CLR));
  Register #(.width(5)) WR_R (.D(multiplexer_9_out), .en(Enable), .Q(WR_OUT), .clk(CLK), .clr(CLR));
  Register #(.width(4)) Forward_R (.D(multiplexer_10_out), .en(Enable), .Q(Forward_OUT), .clk(CLK), .clr(CLR));
  Register #(.width(1)) u_ALUSrcB (.D(multiplexer_11_out), .en(Enable), .Q(ALUSrcB_2), .clk(CLK), .clr(CLR));
  Register #(.width(32)) u_Imm (.D(multiplexer_12_out), .en(Enable), .Q(Imm_2), .clk(CLK), .clr(CLR));
  // Probe on nothing
endmodule
module EX_MEM (
  input  Bubble,
  input  Enable,
  input  CLK,
  input  CLR,
  input  [31:0] PC_IN,
  input  [31:0] IR_IN,
  input  [31:0] ALURS_IN,
  input  [31:0] R2_IN,
  input  [2:0] WB,
  input  [1:0] MEM,
  input  JAL,
  input  [4:0] WR_IN,
  input  HALT,
  input  SysCALL,
  output [31:0] PC_OUT,
  output [31:0] IR_OUT,
  output [31:0] ALURS_OUT,
  output [31:0] R2_OUT,
  output [2:0] WB_2,
  output [1:0] MEM_2,
  output JAL_2,
  output HALT_2,
  output SysCALL_2,
  output [4:0] WR_OUT
);

  wire [4:0] multiplexer_6_out;
  wire [10:7] Control_R_q;
  wire [11:0] multiplexer_5_out;
  wire [31:0] multiplexer_1_out, multiplexer_2_out, multiplexer_3_out, multiplexer_4_out;

  Multiplexer #(.width(32), .enable("false")) multiplexer_1 (
    .in0(PC_IN), .in1({32{1'b0}}), .out(multiplexer_1_out), .sel(Bubble));
  Multiplexer #(.width(32), .enable("false")) multiplexer_2 (
    .in0(IR_IN), .in1({32{1'b0}}), .out(multiplexer_2_out), .sel(Bubble));
  Multiplexer #(.width(32), .enable("false")) multiplexer_3 (
    .in0(ALURS_IN), .in1({32{1'b0}}), .out(multiplexer_3_out), .sel(Bubble));
  Multiplexer #(.width(32), .enable("false")) multiplexer_4 (
    .in0(R2_IN), .in1({32{1'b0}}), .out(multiplexer_4_out), .sel(Bubble));
  Multiplexer #(.width(12), .enable("false")) multiplexer_5 (
    .in0({SysCALL, 4'b0000, HALT, JAL, MEM, WB}), .in1({12{1'b0}}), .out(multiplexer_5_out), .sel(Bubble));
  Multiplexer #(.width(5), .enable("false")) multiplexer_6 (
    .in0(WR_IN), .in1({5{1'b0}}), .out(multiplexer_6_out), .sel(Bubble));
  Register #(.width(32)) PC_R (.D(multiplexer_1_out), .en(Enable), .Q(PC_OUT), .clk(CLK), .clr(CLR));
  Register #(.width(32)) IR_R (.D(multiplexer_2_out), .en(Enable), .Q(IR_OUT), .clk(CLK), .clr(CLR));
  Register #(.width(32)) ALURS_R (.D(multiplexer_3_out), .en(Enable), .Q(ALURS_OUT), .clk(CLK), .clr(CLR));
  Register #(.width(32)) R2_R (.D(multiplexer_4_out), .en(Enable), .Q(R2_OUT), .clk(CLK), .clr(CLR));
  Register #(.width(12)) Control_R (
    .D(multiplexer_5_out), .en(Enable), .Q({SysCALL_2, Control_R_q, HALT_2, JAL_2, MEM_2, WB_2}), .clk(CLK),
    .clr(CLR));
  Register #(.width(5)) WR_R (.D(multiplexer_6_out), .en(Enable), .Q(WR_OUT), .clk(CLK), .clr(CLR));
  // Probe on nothing
endmodule

module MEM_WB (
  input  Bubble,
  input  Enable,
  input  CLK,
  input  CLR,
  input  [31:0] PC_IN,
  input  [31:0] IR_IN,
  input  [31:0] ALURS_IN,
  input  [31:0] MEMD_IN,
  input  [2:0] WB,
  input  JAL,
  input  HALT,
  input  [4:0] WR_IN,
  input  SysCALL,
  output [31:0] PC_OUT,
  output [31:0] IR_OUT,
  output [31:0] ALURS_OUT,
  output [31:0] MEMD_OUT,
  output [2:0] WB_2,
  output JAL_2,
  output HALT_2,
  output SysCALL_2,
  output [4:0] WR_OUT
);

  wire [4:0] multiplexer_6_out;
  wire [10:5] Control_R_q;
  wire [11:0] multiplexer_5_out;
  wire [31:0] multiplexer_1_out, multiplexer_2_out, multiplexer_3_out, multiplexer_4_out;

  Multiplexer #(.width(32), .enable("false")) multiplexer_1 (
    .in0(PC_IN), .in1({32{1'b0}}), .out(multiplexer_1_out), .sel(Bubble));
  Multiplexer #(.width(32), .enable("false")) multiplexer_2 (
    .in0(IR_IN), .in1({32{1'b0}}), .out(multiplexer_2_out), .sel(Bubble));
  Multiplexer #(.width(32), .enable("false")) multiplexer_3 (
    .in0(ALURS_IN), .in1({32{1'b0}}), .out(multiplexer_3_out), .sel(Bubble));
  Multiplexer #(.width(32), .enable("false")) multiplexer_4 (
    .in0(MEMD_IN), .in1({32{1'b0}}), .out(multiplexer_4_out), .sel(Bubble));
  Multiplexer #(.width(12), .enable("false")) multiplexer_5 (
    .in0({SysCALL, {6{1'b0}}, HALT, JAL, WB}), .in1({12{1'b0}}), .out(multiplexer_5_out), .sel(Bubble));
  Multiplexer #(.width(5), .enable("false")) multiplexer_6 (
    .in0(WR_IN), .in1({5{1'b0}}), .out(multiplexer_6_out), .sel(Bubble));
  Register #(.width(32)) PC_R (.D(multiplexer_1_out), .en(Enable), .Q(PC_OUT), .clk(CLK), .clr(CLR));
  Register #(.width(32)) IR_R (.D(multiplexer_2_out), .en(Enable), .Q(IR_OUT), .clk(CLK), .clr(CLR));
  Register #(.width(32)) ALURS_R (.D(multiplexer_3_out), .en(Enable), .Q(ALURS_OUT), .clk(CLK), .clr(CLR));
  Register #(.width(32)) MEMD_R (.D(multiplexer_4_out), .en(Enable), .Q(MEMD_OUT), .clk(CLK), .clr(CLR));
  Register #(.width(12)) Control_R (
    .D(multiplexer_5_out), .en(Enable), .Q({SysCALL_2, Control_R_q, HALT_2, JAL_2, WB_2}), .clk(CLK),
    .clr(CLR));
  Register #(.width(5)) WR_R (.D(multiplexer_6_out), .en(Enable), .Q(WR_OUT), .clk(CLK), .clr(CLR));
  // Probe on nothing
endmodule

module \分支相关流水线  (
);

  wire Beq, Bgzt, bgzt_t, Bne, Bubble, CLK, display, EX_MEM_halt_2, EX_MEM_jal_2, EX_MEM_syscall_2, Go,
       HALT_EX, HALT_WB, IR1, IR2, IR3, JAL_EX, JAL_WB, JMP, JR, LBU, LUISrc, Mem2reg, Memwrite,
       mips_alu_1_equal, nor_1_out, not_1_out, not_2_out, RegDst, Regwrite, RST, run, show, SignedExt,
       SYSCALL_EX, SYSCALL_WB, W1, W2, W3, \条件分支 , \硬布线控制器_1_alu_src , \硬布线控制器_1_jal , \硬布线控制器_1_memtoreg ,
       \硬布线控制器_1_memwrite , \硬布线控制器_1_regdst , \硬布线控制器_1_regwrite , \硬布线控制器_1_syscall ;
  wire [1:0] ID_EX_mem, \硬布线控制器_1_beq , \硬布线控制器_1_jmp ;
  wire [2:0] ID_EX_wb, WB_MEM;
  wire [3:0] ALUOP_EX, \硬布线控制器_1_alu_op ;
  wire [4:0] ID_EX_shamt_out, multiplexer_4_out, multiplexer_5_out, multiplexer_8_out, multiplexer_13_out, WR;
  wire [7:0] multiplexer_9_out;
  wire [15:0] \LoadUse次数 , \总周期数 , \插入气泡数 , \无条件分支数 , \条件分支成功数 ;
  wire [31:0] ALUres_EX, ALUres_MEM, Din, EX_MEM_r2_out, EX_PC, ID_EX_alub_out, ID_PC, IF_PC, INS_EX, INS_ID,
       INS_IF, INS_MEM, INS_WB, LedData, MEM_PC, mem_wb_1_memd_out, MEMD_MEM, multiplexer_1_out,
       multiplexer_2_out, multiplexer_6_out, multiplexer_7_out, multiplexer_10_out, multiplexer_11_out,
       PC_Branch, PC_next, R1_EX, R1_ID, R2_EX, R2_ID, R2_WB, WB_PC, \原PC , \左移2位有符号拓展Imm , \无符号拓展Imm ,
       \有符号拓展Imm ;

  Button \u_总复位  (.out(RST));
  Button _1 (.out(IR1));
  Button _2 (.out(IR2));
  Button _3 (.out(IR3));
  Button \u_继续运行  (.out(Go));
  LED led_1 (.in(W1));
  LED led_2 (.in(W2));
  LED led_3 (.in(W3));
  Multiplexer #(.width(32), .enable("false")) multiplexer_1 (
    .in0(IF_PC), .in1(PC_Branch), .out(multiplexer_1_out), .sel(\条件分支 ));
  Hex_Digit_Display hex_digit_display_1 (.value(LedData[31:28]));  // open: dp
  Multiplexer #(.width(32), .enable("false")) multiplexer_2 (
    .in0({EX_PC[31:28], INS_EX[25:0], 2'b00}), .in1(R1_EX), .out(multiplexer_2_out), .sel(JR));
  // Probe on PC_next
  Hex_Digit_Display hex_digit_display_2 (.value(LedData[23:20]));  // open: dp
  Hex_Digit_Display hex_digit_display_3 (.value(LedData[27:24]));  // open: dp
  or or_1 (run, Go, not_1_out);
  Multiplexer #(.width(32), .enable("false")) multiplexer_3 (
    .in0(multiplexer_1_out), .in1(multiplexer_2_out), .out(PC_next), .sel(JMP));
  Hex_Digit_Display hex_digit_display_4 (.value(LedData[15:12]));  // open: dp
  Hex_Digit_Display hex_digit_display_5 (.value(LedData[19:16]));  // open: dp
  not not_1 (not_1_out, HALT_WB);
  Register #(.width(32)) PC (.D(PC_next), .en(run), .Q(\原PC ), .clk(CLK), .clr(RST));
  // Probe on PC_Branch
  Hex_Digit_Display hex_digit_display_6 (.value(LedData[7:4]));  // open: dp
  Hex_Digit_Display hex_digit_display_7 (.value(LedData[11:8]));  // open: dp
  Clock clock_1 (.out(CLK));
  Counter #(.width(16), .max('hffff)) counter_1 (
    .count(run), .Q(\总周期数 ), .clk(CLK), .clr(RST));  // open: load, D, carry
  Counter #(.width(16), .max('hffff)) counter_2 (
    .count(\条件分支 ), .Q(\条件分支成功数 ), .clk(CLK), .clr(RST));  // open: load, D, carry
  Adder #(.width(32)) adder_1 (.a(\原PC ), .b(32'h4), .out(IF_PC));  // open: cin, cout
  Hex_Digit_Display hex_digit_display_8 (.value(LedData[3:0]));  // open: dp
  ROM #(.addrWidth(10), .dataWidth(32)) rom_1 (.addr(\原PC [11:2]), .data(INS_IF));  // open: sel
  // Probe on INS_IF
  // Probe on INS_ID
  // Probe on INS_EX
  // Probe on INS_MEM
  // Probe on INS_WB
  // Probe on \总周期数 
  // Probe on \无条件分支数 
  // Probe on \条件分支成功数 
  // Probe on \插入气泡数 
  // Probe on \LoadUse次数 
  Counter #(.width(16), .max('hffff)) counter_3 (
    .count(JMP), .Q(\无条件分支数 ), .clk(CLK), .clr(RST));  // open: load, D, carry
  // Probe on IF_PC[11:0]
  Counter #(.width(16), .max('hffff)) counter_4 (
    .count(Bubble), .Q(\插入气泡数 ), .clk(CLK), .clr(RST));  // open: load, D, carry
  IF_ID IF_ID (
    .Bubble(Bubble), .Enable(run), .CLK(CLK), .CLR(RST), .PC_IN(IF_PC), .PC_OUT(ID_PC), .IR_IN(INS_IF),
    .IR_OUT(INS_ID));
  // Probe on ID_PC[11:0]
  // Probe on MEM_PC[11:0]
  // Probe on EX_PC[11:0]
  // Probe on WB_PC[11:0]
  Multiplexer #(.width(5), .enable("false")) multiplexer_4 (
    .in0(INS_ID[25:21]), .in1(5'b00100), .out(multiplexer_4_out), .sel(\硬布线控制器_1_syscall ));
  Multiplexer #(.width(5), .enable("false")) multiplexer_5 (
    .in0(INS_ID[20:16]), .in1(5'b00010), .out(multiplexer_5_out), .sel(\硬布线控制器_1_syscall ));
  assign \无符号拓展Imm  = {{16{1'b0}}, INS_ID[15:0]};  // Bit_Extender bit_extender_1
  assign \有符号拓展Imm  = {{16{INS_ID[15]}}, INS_ID[15:0]};  // Bit_Extender bit_extender_2
  // Probe on \有符号拓展Imm 
  \硬布线控制器  \u_硬布线控制器_1  (
    .Func(INS_ID[5:0]), .OP(INS_ID[31:26]), .ALU_OP(\硬布线控制器_1_alu_op ), .MemToReg(\硬布线控制器_1_memtoreg ),
    .MemWrite(\硬布线控制器_1_memwrite ), .ALU_SRC(\硬布线控制器_1_alu_src ), .RegWrite(\硬布线控制器_1_regwrite ),
    .SysCALL(\硬布线控制器_1_syscall ), .SignedExt(SignedExt), .RegDst(\硬布线控制器_1_regdst ), .JR(\硬布线控制器_1_jmp [1]),
    .JMP(\硬布线控制器_1_jmp [0]), .Beq(\硬布线控制器_1_beq [0]), .JAL(\硬布线控制器_1_jal ), .Bne(\硬布线控制器_1_beq [1]),
    .LUISrc(LUISrc), .bgtz(bgzt_t), .LBU(LBU));
  MIPS_Regifile mips_regifile_1 (
    .Din(Din), .Clk(CLK), .R1(R1_ID), .R2(R2_ID), .WE(Regwrite), .W_num(WR), .R1_num(multiplexer_4_out),
    .R2_num(multiplexer_5_out));
  // Probe on R1_ID
  // Probe on R2_ID
  Multiplexer #(.width(32), .enable("false")) multiplexer_6 (
    .in0(\无符号拓展Imm ), .in1(\有符号拓展Imm ), .out(multiplexer_6_out), .sel(SignedExt));
  Multiplexer #(.width(32), .enable("false")) multiplexer_7 (
    .in0(R2_ID), .in1(multiplexer_6_out), .out(multiplexer_7_out), .sel(\硬布线控制器_1_alu_src ));
  Multiplexer #(.width(5), .enable("false")) multiplexer_8 (
    .in0(INS_ID[10:6]), .in1(5'b10000), .out(multiplexer_8_out), .sel(LUISrc));
  Pull_Resistor pull_resistor_1 (.node(display));
  Comparator #(.width(32)) comparator_1 (.a(R2_EX), .b(32'h22), .eq(display));  // open: gt, lt
  and and_1 (show, SYSCALL_EX, display);
  ID_EX ID_EX (
    .PC_IN(ID_PC), .IR_IN(INS_ID), .R1_IN(R1_ID), .ALUB_IN(multiplexer_7_out), .PC_OUT(EX_PC),
    .IR_OUT(INS_EX), .R1_OUT(R1_EX), .ALUB_OUT(ID_EX_alub_out), .Bubble(Bubble), .Enable(run), .CLK(CLK),
    .CLR(RST), .RegWrite(\硬布线控制器_1_regwrite ), .RegDst(\硬布线控制器_1_regdst ), .MemToReg(\硬布线控制器_1_memtoreg ),
    .MemWrite(\硬布线控制器_1_memwrite ), .Beq(\硬布线控制器_1_beq [0]), .Bne(\硬布线控制器_1_beq [1]), .JR(\硬布线控制器_1_jmp [1]),
    .JMP(\硬布线控制器_1_jmp [0]), .JAL(\硬布线控制器_1_jal ), .SysCALL(\硬布线控制器_1_syscall ), .MEM(ID_EX_mem),
    .SysCALL_2(SYSCALL_EX), .WB(ID_EX_wb), .BRANCH_OUT({Bne, Beq, Bgzt}), .JMP_OUT({JAL_EX, JMP, JR}),
    .ALUOP_OUT(ALUOP_EX), .Shamt_IN(multiplexer_8_out), .Shamt_OUT(ID_EX_shamt_out), .Bgzt(bgzt_t),
    .LBU(LBU), .R2_IN(R2_ID), .R2_OUT(R2_EX), .ALUOP_IN(\硬布线控制器_1_alu_op ));  // open: WR_IN, WR_OUT, Forward_IN, Forward_OUT, ALUSrcB, ALUSrcB_2, Imm, Imm_2
  or or_2 (Bubble, \条件分支 , JMP);
  Pull_Resistor pull_resistor_2 (.node(\条件分支 ));
  assign \条件分支  = Beq ? mips_alu_1_equal : 1'bz;  // Controlled_Buffer controlled_buffer_1
  assign \条件分支  = Bne ? ~mips_alu_1_equal : 1'bz;  // Controlled_Inverter controlled_inverter_1
  // Probe on ALUOP_EX
  // Probe on ALUres_EX
  // Probe on R1_EX
  // Probe on R2_EX
  // Probe on {EX_PC[31:28], INS_EX[25:0], 2'b00}
  // Probe on EX_PC
  not not_2 (not_2_out, display);
  Register #(.width(32)) register_1 (.D(R1_EX), .en(show), .Q(LedData), .clk(CLK), .clr(RST));
  assign \条件分支  = Bgzt ? nor_1_out : 1'bz;  // Controlled_Buffer controlled_buffer_2
  nor nor_1 (nor_1_out, ALUres_EX[0], mips_alu_1_equal);
  and and_2 (HALT_EX, SYSCALL_EX, not_2_out);
  MIPS_ALU mips_alu_1 (
    .X(R1_EX), .Y(ID_EX_alub_out), .AluOP(ALUOP_EX), .Equal(mips_alu_1_equal), .Result(ALUres_EX),
    .shamt(ID_EX_shamt_out));  // open: Result_2
  EX_MEM EX_MEM (
    .PC_IN(EX_PC), .IR_IN(INS_EX), .R2_IN(R2_EX), .PC_OUT(MEM_PC), .IR_OUT(INS_MEM), .R2_OUT(EX_MEM_r2_out),
    .Bubble(1'b0), .Enable(run), .CLK(CLK), .CLR(RST), .ALURS_IN(ALUres_EX), .ALURS_OUT(ALUres_MEM),
    .WB_2(WB_MEM), .MEM_2({LBU, Memwrite}), .SysCALL_2(EX_MEM_syscall_2), .WB(ID_EX_wb), .MEM(ID_EX_mem),
    .SysCALL(SYSCALL_EX), .JAL(JAL_EX), .JAL_2(EX_MEM_jal_2), .HALT(HALT_EX), .HALT_2(EX_MEM_halt_2));  // open: WR_IN, WR_OUT
  assign \左移2位有符号拓展Imm  = {{14{INS_EX[15]}}, {INS_EX[15:0], 2'b00}};  // Bit_Extender bit_extender_3
  Adder #(.width(32)) adder_2 (.a(EX_PC), .b(\左移2位有符号拓展Imm ), .out(PC_Branch));  // open: cin, cout
  RAM #(.addrWidth(10), .dataWidth(32), .bus("separate")) ram_1 (
    .addr(ALUres_MEM[11:2]), .din(EX_MEM_r2_out), .data(MEMD_MEM), .str(Memwrite), .clk(CLK), .clr(RST));  // open: sel, ld
  // Probe on LBU
  // Probe on LedData
  // Probe on ALUres_MEM
  // Probe on MEMD_MEM
  // Probe on Memwrite
  Multiplexer #(.select(2), .width(8), .disabled(0), .enable("false")) multiplexer_9 (
    .in0(MEMD_MEM[7:0]), .in1(MEMD_MEM[15:8]), .in2(MEMD_MEM[23:16]), .in3(MEMD_MEM[31:24]),
    .out(multiplexer_9_out), .sel(ALUres_MEM[1:0]));
  // Probe on WB_MEM
  Multiplexer #(.width(32), .enable("false")) multiplexer_10 (
    .in0(MEMD_MEM), .in1({{24{1'b0}}, multiplexer_9_out}), .out(multiplexer_10_out), .sel(LBU));
  MEM_WB mem_wb_1 (
    .Bubble(1'b0), .Enable(run), .CLK(CLK), .CLR(RST), .PC_IN(MEM_PC), .PC_OUT(WB_PC), .IR_IN(INS_MEM),
    .IR_OUT(INS_WB), .ALURS_IN(ALUres_MEM), .ALURS_OUT(R2_WB), .MEMD_IN(multiplexer_10_out),
    .MEMD_OUT(mem_wb_1_memd_out), .WB(WB_MEM), .WB_2({Mem2reg, RegDst, Regwrite}), .SysCALL_2(SYSCALL_WB),
    .SysCALL(EX_MEM_syscall_2), .JAL(EX_MEM_jal_2), .JAL_2(JAL_WB), .HALT(EX_MEM_halt_2), .HALT_2(HALT_WB));  // open: WR_IN, WR_OUT
  Multiplexer #(.width(32)) multiplexer_11 (
    .in0(R2_WB), .in1(mem_wb_1_memd_out), .out(multiplexer_11_out), .sel(Mem2reg));  // open: en
  Multiplexer #(.width(32)) multiplexer_12 (
    .in0(multiplexer_11_out), .in1(WB_PC), .out(Din), .sel(JAL_WB));  // open: en
  // Probe on WR
  // Probe on Regwrite
  Multiplexer #(.width(5), .enable("false")) multiplexer_13 (
    .in0(INS_WB[20:16]), .in1(INS_WB[15:11]), .out(multiplexer_13_out), .sel(RegDst));
  // Probe on Din
  Multiplexer #(.width(5), .enable("false")) multiplexer_14 (
    .in0(multiplexer_13_out), .in1({5{1'b1}}), .out(WR), .sel(JAL_WB));

  // Other names for the same wires on the sheet: J_addr[31:2] = {EX_PC[31:28], INS_EX[25:0]};
  //   Shamt[4:0] = INS_ID[10:6]; 加1的PC[31:0] = IF_PC

  // Notes on the sheet:
  //   中断源
  //   中断等待指示
  //   数码管输出
  //   指令存储器
  //   指令字
  //   contents of rom_1 (hex, n*v repeats v):
  //   20100000 20110001 20120002 20130003 36100000 36310001 36520002 36730003 ae100000 ae110004 ae120008
  //   ae13000c 2002000a 0 0 0 c
  //   OP
  //   rs
  //   rt
  //   rd
  //   Imm
  //   Shamt
  //   流水调试日志用
  //   Func
  //   bgtz
  //   JMP
  //   JR
  //   SignedExt
  //   LUISrc
  //   OP
  //   Func
  //   Beq
  //   Bne
  //   MemToReg
  //   MemWrite
  //   AluOP
  //   AluSrcB
  //   RegWrite
  //   JAL
  //   RegDst
  //   Syscall
  //   addr
  //   Imm
  //   rt
  //   rd
endmodule

module \气泡流水线  (
);

  wire Beq, Bgzt, bgzt_t, Bne, Bubble, buffer_1_out, buffer_2_out, buffer_3_out, buffer_4_out, buffer_5_out,
       buffer_7_out, buffer_8_out, CLK, display, EX_MEM_halt_2, EX_MEM_jal_2, EX_MEM_syscall_2, Go, HALT_EX,
       HALT_WB, IR1, IR2, IR3, JAL_EX, JAL_WB, JMP, JR, LBU, Load, Load_CLK, LUISrc, Mem2reg, Memwrite,
       mips_alu_1_equal, nor_1_out, not_1_out, not_2_out, or_2_out, or_3_out, RegDst, Regwrite, RST, run,
       show, SignedExt, SYSCALL_EX, SYSCALL_WB, W1, W2, W3, xor_1_out, xor_2_out, \数据相关 , \条件分支 ,
       \硬布线控制器_1_alu_src , \硬布线控制器_1_jal , \硬布线控制器_1_memtoreg , \硬布线控制器_1_memwrite , \硬布线控制器_1_regdst ,
       \硬布线控制器_1_regwrite , \硬布线控制器_1_syscall ;
  wire [1:0] id_ex_1_mem, \硬布线控制器_1_beq ;
  wire [2:0] WB_EX, WB_MEM;
  wire [3:0] ALUOP_EX, \硬布线控制器_1_alu_op , \硬布线控制器_1_jmp ;
  wire [4:0] id_ex_1_shamt_out, multiplexer_8_out, multiplexer_10_out, multiplexer_11_out, R1_ID, R2_ID, WR,
       WR_EX, WR_MEM, WR_WB;
  wire [7:0] multiplexer_13_out;
  wire [15:0] \LoadUse次数 , \总周期数 , \插入气泡数 , \无条件分支数 , \条件分支成功数 ;
  wire [31:0] adder_2_out, adder_4_out, ALUres_EX, ALUres_MEM, bit_extender_3_out, Din, EX_MEM_r2_out, EX_PC,
       id_ex_1_alub_out, ID_PC, IF_PC, INS_EX, INS_ID, INS_IF, INS_MEM, INS_WB, LedData, MEM_PC,
       mem_wb_1_memd_out, MEMD_MEM, multiplexer_1_out, multiplexer_2_out, multiplexer_3_out,
       multiplexer_7_out, multiplexer_9_out, multiplexer_12_out, multiplexer_14_out, PC_Branch, PC_next,
       R1_EX, R1_ID_t, R2_EX, R2_ID_t, R2_WB, WB_PC, \加1的PC , \无符号拓展Imm , \有符号拓展Imm ;

  Button \u_总复位  (.out(RST));
  Button _1 (.out(IR1));
  Button _2 (.out(IR2));
  Button _3 (.out(IR3));
  Button \u_继续运行  (.out(Go));
  LED led_1 (.in(W1));
  LED led_2 (.in(W2));
  LED led_3 (.in(W3));
  Button \u_装载断点  (.out(Load));
  Multiplexer #(.width(32), .enable("false")) multiplexer_1 (
    .in0(\加1的PC ), .in1(PC_Branch), .out(multiplexer_1_out), .sel(\条件分支 ));
  Multiplexer #(.width(32), .enable("false")) multiplexer_2 (
    .in0({EX_PC[31:28], INS_EX[25:0], 2'b00}), .in1(R1_EX), .out(multiplexer_2_out), .sel(JR));
  Hex_Digit_Display hex_digit_display_1 (.value(LedData[31:28]));  // open: dp
  buf buffer_1 (buffer_1_out, Load);
  Multiplexer #(.width(32), .enable("false")) multiplexer_3 (
    .in0(multiplexer_1_out), .in1(multiplexer_2_out), .out(multiplexer_3_out), .sel(JMP));
  // Probe on PC_next
  Hex_Digit_Display hex_digit_display_2 (.value(LedData[27:24]));  // open: dp
  Hex_Digit_Display hex_digit_display_3 (.value(LedData[23:20]));  // open: dp
  Counter #(.width(16), .max('hffff)) counter_1 (
    .count(run), .Q(\总周期数 ), .clk(CLK), .clr(RST));  // open: load, D, carry
  Counter #(.width(16), .max('hffff)) counter_2 (
    .count(\条件分支 ), .Q(\条件分支成功数 ), .clk(CLK), .clr(RST));  // open: load, D, carry
  buf buffer_2 (buffer_2_out, buffer_1_out);
  buf buffer_3 (buffer_3_out, buffer_5_out);
  buf buffer_4 (buffer_4_out, buffer_3_out);
  buf buffer_5 (buffer_5_out, buffer_2_out);
  or or_1 (run, Go, not_1_out);
  xor xor_1 (xor_1_out, run, \数据相关 );
  Multiplexer #(.width(32), .enable("false")) multiplexer_4 (
    .in0(multiplexer_3_out), .in1(32'h303c), .out(PC_next), .sel(Load));
  Hex_Digit_Display hex_digit_display_4 (.value(LedData[19:16]));  // open: dp
  Hex_Digit_Display hex_digit_display_5 (.value(LedData[15:12]));  // open: dp
  buf buffer_6 (Load_CLK, buffer_7_out);
  buf buffer_7 (buffer_7_out, buffer_8_out);
  buf buffer_8 (buffer_8_out, buffer_4_out);
  not not_1 (not_1_out, HALT_WB);
  Register #(.width(32)) PC (.D(PC_next), .en(xor_1_out), .Q(IF_PC), .clk(or_2_out), .clr(RST));
  or or_2 (or_2_out, Load_CLK, CLK);
  // Probe on PC_Branch
  Hex_Digit_Display hex_digit_display_6 (.value(LedData[11:8]));  // open: dp
  Hex_Digit_Display hex_digit_display_7 (.value(LedData[7:4]));  // open: dp
  Clock clock_1 (.out(CLK));
  Adder #(.width(32)) adder_1 (.a(IF_PC), .b(32'h4), .out(\加1的PC ));  // open: cin, cout
  // Probe on \数据相关 
  // Probe on WR_EX
  // Probe on WR_MEM
  Hex_Digit_Display hex_digit_display_8 (.value(LedData[3:0]));  // open: dp
  Counter #(.width(16), .max('hffff)) counter_3 (
    .count(JMP), .Q(\无条件分支数 ), .clk(CLK), .clr(RST));  // open: load, D, carry
  Counter #(.width(16), .max('hffff)) counter_4 (
    .count(\数据相关 ), .Q(\插入气泡数 ), .clk(CLK), .clr(RST));  // open: load, D, carry
  ROM #(.addrWidth(10), .dataWidth(32)) rom_1 (.addr(IF_PC[11:2]), .data(INS_IF));  // open: sel
  // Probe on INS_IF
  // Probe on INS_ID
  // Probe on INS_EX
  // Probe on INS_MEM
  // Probe on INS_WB
  // Probe on \总周期数 
  // Probe on \无条件分支数 
  // Probe on \条件分支成功数 
  // Probe on \插入气泡数 
  // Probe on \LoadUse次数 
  xor xor_2 (xor_2_out, \数据相关 , run);
  // Probe on IF_PC[11:0]
  IF_ID IF_ID (
    .Bubble(Bubble), .Enable(xor_2_out), .CLK(CLK), .CLR(RST), .PC_IN(IF_PC), .PC_OUT(ID_PC), .IR_IN(INS_IF),
    .IR_OUT(INS_ID));
  // Probe on ID_PC[11:0]
  // Probe on MEM_PC[11:0]
  // Probe on EX_PC[11:0]
  // Probe on WB_PC[11:0]
  Multiplexer #(.width(5), .enable("false")) multiplexer_5 (
    .in0(INS_ID[25:21]), .in1(5'b00100), .out(R1_ID), .sel(\硬布线控制器_1_syscall ));
  Multiplexer #(.width(5), .enable("false")) multiplexer_6 (
    .in0(INS_ID[20:16]), .in1(5'b00010), .out(R2_ID), .sel(\硬布线控制器_1_syscall ));
  assign \无符号拓展Imm  = {{16{1'b0}}, INS_ID[15:0]};  // Bit_Extender bit_extender_1
  assign \有符号拓展Imm  = {{16{INS_ID[15]}}, INS_ID[15:0]};  // Bit_Extender bit_extender_2
  // Probe on \有符号拓展Imm 
  \数据相关检测  \u_数据相关检测_1  (
    .OP(INS_ID[31:26]), .EX_WriteReg_num(WR_EX), .EX_RegWrite(WB_EX[0]), .MEM_WriteReg_num(WR_MEM),
    .MEM_RegWrite(WB_MEM[0]), .\数据相关 (\数据相关 ), .Func(INS_ID[5:0]), .ID_R1_num(R1_ID), .ID_R2_num(R2_ID));
  \硬布线控制器  \u_硬布线控制器_1  (
    .Func(INS_ID[5:0]), .OP(INS_ID[31:26]), .ALU_OP(\硬布线控制器_1_alu_op ), .MemToReg(\硬布线控制器_1_memtoreg ),
    .MemWrite(\硬布线控制器_1_memwrite ), .ALU_SRC(\硬布线控制器_1_alu_src ), .RegWrite(\硬布线控制器_1_regwrite ),
    .SysCALL(\硬布线控制器_1_syscall ), .SignedExt(SignedExt), .RegDst(\硬布线控制器_1_regdst ), .JR(\硬布线控制器_1_jmp [1]),
    .JMP(\硬布线控制器_1_jmp [0]), .Beq(\硬布线控制器_1_beq [0]), .JAL(\硬布线控制器_1_jal ), .Bne(\硬布线控制器_1_beq [1]),
    .LUISrc(LUISrc), .bgtz(bgzt_t), .LBU(\硬布线控制器_1_jmp [3]));
  MIPS_Regifile mips_regifile_1 (
    .Din(Din), .Clk(CLK), .R1(R1_ID_t), .R2(R2_ID_t), .WE(Regwrite), .W_num(WR_WB), .R1_num(R1_ID),
    .R2_num(R2_ID));
  // Probe on R1_ID_t
  // Probe on R2_ID_t
  Multiplexer #(.width(32), .enable("false")) multiplexer_7 (
    .in0(\无符号拓展Imm ), .in1(\有符号拓展Imm ), .out(multiplexer_7_out), .sel(SignedExt));
  Multiplexer #(.width(5), .enable("false")) multiplexer_8 (
    .in0(INS_ID[20:16]), .in1(INS_ID[15:11]), .out(multiplexer_8_out), .sel(\硬布线控制器_1_regdst ));
  Multiplexer #(.width(32), .enable("false")) multiplexer_9 (
    .in0(R2_ID_t), .in1(multiplexer_7_out), .out(multiplexer_9_out), .sel(\硬布线控制器_1_alu_src ));
  Multiplexer #(.width(5), .enable("false")) multiplexer_10 (
    .in0(INS_ID[10:6]), .in1(5'b10000), .out(multiplexer_10_out), .sel(LUISrc));
  Comparator #(.width(32)) comparator_1 (.a(R2_EX), .b(32'h22), .eq(display));  // open: gt, lt
  Pull_Resistor pull_resistor_1 (.node(display));
  Multiplexer #(.width(5), .enable("false")) multiplexer_11 (
    .in0(multiplexer_8_out), .in1({5{1'b1}}), .out(multiplexer_11_out), .sel(\硬布线控制器_1_jal ));
  and and_1 (show, SYSCALL_EX, display);
  ID_EX id_ex_1 (
    .PC_IN(ID_PC), .IR_IN(INS_ID), .R1_IN(R1_ID_t), .ALUB_IN(multiplexer_9_out), .PC_OUT(EX_PC),
    .IR_OUT(INS_EX), .R1_OUT(R1_EX), .ALUB_OUT(id_ex_1_alub_out), .Bubble(or_3_out), .Enable(run), .CLK(CLK),
    .CLR(RST), .RegWrite(\硬布线控制器_1_regwrite ), .RegDst(\硬布线控制器_1_regdst ), .MemToReg(\硬布线控制器_1_memtoreg ),
    .MemWrite(\硬布线控制器_1_memwrite ), .Beq(\硬布线控制器_1_beq [0]), .Bne(\硬布线控制器_1_beq [1]), .JR(\硬布线控制器_1_jmp [1]),
    .JMP(\硬布线控制器_1_jmp [0]), .JAL(\硬布线控制器_1_jal ), .SysCALL(\硬布线控制器_1_syscall ), .MEM(id_ex_1_mem),
    .SysCALL_2(SYSCALL_EX), .WB(WB_EX), .BRANCH_OUT({Bne, Beq, Bgzt}), .JMP_OUT({JAL_EX, JMP, JR}),
    .ALUOP_OUT(ALUOP_EX), .Shamt_IN(multiplexer_10_out), .Shamt_OUT(id_ex_1_shamt_out), .Bgzt(bgzt_t),
    .LBU(\硬布线控制器_1_jmp [3]), .R2_IN(R2_ID_t), .R2_OUT(R2_EX), .WR_IN(multiplexer_11_out), .WR_OUT(WR_EX),
    .ALUOP_IN(\硬布线控制器_1_alu_op ));  // open: Forward_IN, Forward_OUT, ALUSrcB, ALUSrcB_2, Imm, Imm_2
  or or_3 (or_3_out, \数据相关 , Bubble);
  Pull_Resistor pull_resistor_2 (.node(\条件分支 ));
  assign \条件分支  = Beq ? mips_alu_1_equal : 1'bz;  // Controlled_Buffer controlled_buffer_1
  assign \条件分支  = Bne ? ~mips_alu_1_equal : 1'bz;  // Controlled_Inverter controlled_inverter_1
  // Probe on ALUOP_EX
  // Probe on ALUres_EX
  // Probe on R1_EX
  // Probe on R2_EX
  // Probe on {EX_PC[31:28], INS_EX[25:0], 2'b00}
  // Probe on EX_PC
  not not_2 (not_2_out, display);
  Register #(.width(32)) register_1 (.D(R1_EX), .en(show), .Q(LedData), .clk(CLK), .clr(RST));
  or or_4 (Bubble, \条件分支 , JMP);
  assign \条件分支  = Bgzt ? nor_1_out : 1'bz;  // Controlled_Buffer controlled_buffer_2
  nor nor_1 (nor_1_out, ALUres_EX[0], mips_alu_1_equal);
  and and_2 (HALT_EX, SYSCALL_EX, not_2_out);
  MIPS_ALU mips_alu_1 (
    .X(R1_EX), .Y(id_ex_1_alub_out), .AluOP(ALUOP_EX), .Equal(mips_alu_1_equal), .Result(ALUres_EX),
    .shamt(id_ex_1_shamt_out));  // open: Result_2
  Adder #(.width(32)) adder_2 (.a(32'h4), .b(EX_PC), .out(adder_2_out));  // open: cin, cout
  Adder #(.width(32)) adder_3 (.a(adder_2_out), .b(bit_extender_3_out), .out(PC_Branch));  // open: cin, cout
  assign bit_extender_3_out = {{14{INS_EX[15]}}, {INS_EX[15:0], 2'b00}};  // Bit_Extender bit_extender_3
  EX_MEM EX_MEM (
    .PC_IN(EX_PC), .IR_IN(INS_EX), .R2_IN(R2_EX), .PC_OUT(MEM_PC), .IR_OUT(INS_MEM), .R2_OUT(EX_MEM_r2_out),
    .Bubble(1'b0), .Enable(run), .CLK(CLK), .CLR(RST), .ALURS_IN(ALUres_EX), .ALURS_OUT(ALUres_MEM),
    .WB_2(WB_MEM), .MEM_2({LBU, Memwrite}), .SysCALL_2(EX_MEM_syscall_2), .WB(WB_EX), .MEM(id_ex_1_mem),
    .SysCALL(SYSCALL_EX), .JAL(JAL_EX), .JAL_2(EX_MEM_jal_2), .HALT(HALT_EX), .HALT_2(EX_MEM_halt_2),
    .WR_IN(WR_EX), .WR_OUT(WR_MEM));
  // Probe on LBU
  // Probe on LedData
  // Probe on ALUres_MEM
  // Probe on MEMD_MEM
  // Probe on Memwrite
  // Probe on WB_MEM
  RAM #(.addrWidth(10), .dataWidth(32), .bus("separate")) ram_1 (
    .addr(ALUres_MEM[11:2]), .din(EX_MEM_r2_out), .data(MEMD_MEM), .str(Memwrite), .clk(CLK), .clr(RST));  // open: sel, ld
  Multiplexer #(.width(32), .enable("false")) multiplexer_12 (
    .in0(MEMD_MEM), .in1({{24{1'b0}}, multiplexer_13_out}), .out(multiplexer_12_out), .sel(LBU));
  Multiplexer #(.select(2), .width(8), .disabled(0), .enable("false")) multiplexer_13 (
    .in0(MEMD_MEM[7:0]), .in1(MEMD_MEM[15:8]), .in2(MEMD_MEM[23:16]), .in3(MEMD_MEM[31:24]),
    .out(multiplexer_13_out), .sel(ALUres_MEM[1:0]));
  MEM_WB mem_wb_1 (
    .Bubble(1'b0), .Enable(run), .CLK(CLK), .CLR(RST), .PC_IN(MEM_PC), .PC_OUT(WB_PC), .IR_IN(INS_MEM),
    .IR_OUT(INS_WB), .ALURS_IN(ALUres_MEM), .ALURS_OUT(R2_WB), .MEMD_IN(multiplexer_12_out),
    .MEMD_OUT(mem_wb_1_memd_out), .WB(WB_MEM), .WB_2({Mem2reg, RegDst, Regwrite}), .SysCALL_2(SYSCALL_WB),
    .SysCALL(EX_MEM_syscall_2), .JAL(EX_MEM_jal_2), .JAL_2(JAL_WB), .HALT(EX_MEM_halt_2), .HALT_2(HALT_WB),
    .WR_IN(WR_MEM), .WR_OUT(WR_WB));
  Multiplexer #(.width(32)) multiplexer_14 (
    .in0(R2_WB), .in1(mem_wb_1_memd_out), .out(multiplexer_14_out), .sel(Mem2reg));  // open: en
  Adder #(.width(32)) adder_4 (.a(WB_PC), .b(32'h4), .out(adder_4_out));  // open: cin, cout
  // Probe on WR
  // Probe on Regwrite
  Multiplexer #(.width(32)) multiplexer_15 (
    .in0(multiplexer_14_out), .in1(adder_4_out), .out(Din), .sel(JAL_WB));  // open: en
  // Probe on Din

  // Other names for the same wires on the sheet: J_addr[31:2] = {EX_PC[31:28], INS_EX[25:0]};
  //   Shamt[4:0] = INS_ID[10:6]; 原PC[31:0] = IF_PC

  // Notes on the sheet:
  //   中断源
  //   中断等待指示
  //   数码管输出
  //   指令存储器
  //   指令字
  //   contents of rom_1 (hex, n*v repeats v):
  //   20110001 8000005 20110001 20120002 20130003 8000009 20110001 20120002 20130003 800000d 20110001
  //   20120002 20130003 8000011 20110001 20120002 20130003 c0000b8 20100001 20110001 118fc0 112020
  //   20020022 c 118882 12200001 8000015 112020 20020022 c 20110001 118880 112020 20020022 c 12200001
  //   800001f 20110001 118fc0 112020 20020022 c 1188c3 112020 20020022 c 118903 112020 20020022 c 118903
  //   112020 20020022 c 118903 112020 20020022 c 118903 112020 20020022 c 118903 112020 20020022 c 118903
  //   112020 20020022 c 118903 112020 20020022 c 20100001 109fc0 139fc3 8021 2012000c 24160003 26100001
  //   3210000f 20080008 20090001 139900 2709825 132020 20020022 c 1094022 1500fff9 22100001 2018000f
  //   2188024 108700 20080008 20090001 139902 2709825 132021 20020022 c 1094022 1500fff9 108702 2c9b022
  //   12c00001 8000050 4020 1084027 84400 3508ffff 82021 20020022 c 2010ffff 20110000 ae300000 22100001
  //   22310004 ae300000 22100001 22310004 ae300000 22100001 22310004 ae300000 22100001 22310004 ae300000
  //   22100001 22310004 ae300000 22100001 22310004 ae300000 22100001 22310004 ae300000 22100001 22310004
  //   ae300000 22100001 22310004 ae300000 22100001 22310004 ae300000 22100001 22310004 ae300000 22100001
  //   22310004 ae300000 22100001 22310004 ae300000 22100001 22310004 ae300000 22100001 22310004 ae300000
  //   22100001 22310004 22100001 8020 2011003c 8e130000 8e340000 274402a 11000002 ae330000 ae140000
  //   2231fffc 1611fff8 102020 20020022 c 22100004 2011003c 1611fff2 20020032 c 20100000 22100001 102020
  //   20020022 c 22100002 102020 20020022 c 22100003 102020 20020022 c 22100004 102020 20020022 c 22100005
  //   102020 20020022 c 22100006 102020 20020022 c 22100007 102020 20020022 c 22100008 102020 20020022
  //   20020022 c 3e00008
  //   OP
  //   rs
  //   rt
  //   rd
  //   Imm
  //   Shamt
  //   流水调试日志用
  //   Func
  //   OP
  //   Func
  //   bgtz
  //   JMP
  //   JR
  //   SignedExt
  //   LUISrc
  //   OP
  //   Func
  //   Beq
  //   Bne
  //   MemToReg
  //   MemWrite
  //   AluOP
  //   AluSrcB
  //   RegWrite
  //   JAL
  //   RegDst
  //   Syscall
  //   rt
  //   rd
  //   addr
  //   Imm
endmodule

module \重定向流水线  (
);

  wire Beq, Bgzt, bgzt_t, Bne, Bubble, buffer_1_out, buffer_2_out, buffer_3_out, buffer_4_out, buffer_5_out,
       CLK, display, EX_MEM_halt_2, EX_MEM_syscall_2, Go, HALT_EX, HALT_WB, id_ex_1_alusrcb_2, IR1, IR2, IR3,
       JAL_EX, JAL_MEM, JAL_WB, JMP, JR, LBU, Load, Load_CLK, Load_use, LUISrc, Mem2reg_WB, Memwrite,
       mips_alu_1_equal, nor_1_out, not_1_out, not_2_out, or_2_out, or_3_out, RegDst, Regwrite, RST, run,
       show, SignedExt, SYSCALL_EX, SYSCALL_WB, W1, W2, W3, xor_1_out, xor_2_out, \数据相关 , \条件分支 ,
       \硬布线控制器_1_alu_src , \硬布线控制器_1_jal , \硬布线控制器_1_memtoreg , \硬布线控制器_1_memwrite , \硬布线控制器_1_regdst ,
       \硬布线控制器_1_regwrite , \硬布线控制器_1_syscall ;
  wire [1:0] ForwardA_EX, ForwardB_EX, MEM_EX, \硬布线控制器_1_beq ;
  wire [2:0] WB_EX, WB_MEM;
  wire [3:0] ALUOP_EX, Forward_EX, \硬布线控制器_1_alu_op , \硬布线控制器_1_jmp ;
  wire [4:0] id_ex_1_shamt_out, multiplexer_8_out, multiplexer_9_out, multiplexer_10_out, R1_ID, R2_ID,
       WR_EX, WR_MEM, WR_WB;
  wire [7:0] multiplexer_14_out;
  wire [15:0] \LoadUse次数 , \总周期数 , \插入气泡数 , \无条件分支数 , \条件分支成功数 ;
  wire [31:0] adder_2_out, adder_5_out, ALUB_EX, ALUres_EX, ALUres_MEM, ALUres_WB, bit_extender_3_out,
       Din_WB, EX_MEM_r2_out, EX_PC, id_ex_1_r1_out, id_ex_1_r2_out, ID_PC, IF_PC, Imm_EX, Imm_ID, INS_EX,
       INS_ID, INS_IF, INS_MEM, INS_WB, LedData, MEM_PC, MEMD_MEM, MEMD_WB, multiplexer_1_out,
       multiplexer_2_out, multiplexer_3_out, multiplexer_15_out, multiplexer_16_out, PC_1_MEM, PC_Branch,
       PC_next, R1_EX, R1_ID_t, R2_EX, R2_ID_t, WB_PC, \加1的PC , \无符号拓展Imm , \有符号拓展Imm ;

  Button \u_总复位  (.out(RST));
  Button _1 (.out(IR1));
  Button _2 (.out(IR2));
  Button _3 (.out(IR3));
  Button \u_继续运行  (.out(Go));
  LED led_1 (.in(W1));
  LED led_2 (.in(W2));
  LED led_3 (.in(W3));
  Button \u_装载断点  (.out(Load));
  Multiplexer #(.width(32), .enable("false")) multiplexer_1 (
    .in0(\加1的PC ), .in1(PC_Branch), .out(multiplexer_1_out), .sel(\条件分支 ));
  Multiplexer #(.width(32), .enable("false")) multiplexer_2 (
    .in0({EX_PC[31:28], INS_EX[25:0], 2'b00}), .in1(R1_EX), .out(multiplexer_2_out), .sel(JR));
  Hex_Digit_Display hex_digit_display_1 (.value(LedData[31:28]));  // open: dp
  buf buffer_1 (buffer_1_out, Load);
  Multiplexer #(.width(32), .enable("false")) multiplexer_3 (
    .in0(multiplexer_1_out), .in1(multiplexer_2_out), .out(multiplexer_3_out), .sel(JMP));
  // Probe on PC_next
  Hex_Digit_Display hex_digit_display_2 (.value(LedData[23:20]));  // open: dp
  Hex_Digit_Display hex_digit_display_3 (.value(LedData[27:24]));  // open: dp
  Counter #(.width(16), .max('hffff)) counter_1 (
    .count(run), .Q(\总周期数 ), .clk(CLK), .clr(RST));  // open: load, D, carry
  Counter #(.width(16), .max('hffff)) counter_2 (
    .count(\条件分支 ), .Q(\条件分支成功数 ), .clk(CLK), .clr(RST));  // open: load, D, carry
  buf buffer_2 (buffer_2_out, buffer_4_out);
  buf buffer_3 (buffer_3_out, buffer_5_out);
  buf buffer_4 (buffer_4_out, buffer_1_out);
  buf buffer_5 (buffer_5_out, buffer_2_out);
  xor xor_1 (xor_1_out, Load_use, run);
  Multiplexer #(.width(32), .enable("false")) multiplexer_4 (
    .in0(multiplexer_3_out), .in1(32'h32dc), .out(PC_next), .sel(Load));
  Hex_Digit_Display hex_digit_display_4 (.value(LedData[19:16]));  // open: dp
  Hex_Digit_Display hex_digit_display_5 (.value(LedData[15:12]));  // open: dp
  buf buffer_6 (Load_CLK, buffer_3_out);
  or or_1 (run, Go, not_1_out);
  Register #(.width(32)) PC (.D(PC_next), .en(xor_1_out), .Q(IF_PC), .clk(or_2_out), .clr(RST));
  or or_2 (or_2_out, Load_CLK, CLK);
  // Probe on PC_Branch
  Hex_Digit_Display hex_digit_display_6 (.value(LedData[11:8]));  // open: dp
  Hex_Digit_Display hex_digit_display_7 (.value(LedData[7:4]));  // open: dp
  Clock clock_1 (.out(CLK));
  Counter #(.width(16), .max('hffff)) counter_3 (
    .count(Load_use), .Q(\LoadUse次数 ), .clk(CLK), .clr(RST));  // open: load, D, carry
  not not_1 (not_1_out, HALT_WB);
  Adder #(.width(32)) adder_1 (.a(IF_PC), .b(32'h4), .out(\加1的PC ));  // open: cin, cout
  // Probe on Load_use
  // Probe on \数据相关 
  // Probe on WR_EX
  // Probe on WR_MEM
  // Probe on ForwardA_EX
  // Probe on ForwardB_EX
  Hex_Digit_Display hex_digit_display_8 (.value(LedData[3:0]));  // open: dp
  Counter #(.width(16), .max('hffff)) counter_4 (
    .count(JMP), .Q(\无条件分支数 ), .clk(CLK), .clr(RST));  // open: load, D, carry
  Counter #(.width(16), .max('hffff)) counter_5 (
    .count(Bubble), .Q(\插入气泡数 ), .clk(CLK), .clr(RST));  // open: load, D, carry
  ROM #(.addrWidth(10), .dataWidth(32)) rom_1 (.addr(IF_PC[11:2]), .data(INS_IF));  // open: sel
  // Probe on \总周期数 
  // Probe on \无条件分支数 
  // Probe on \条件分支成功数 
  // Probe on \插入气泡数 
  // Probe on \LoadUse次数 
  xor xor_2 (xor_2_out, Load_use, run);
  // Probe on INS_IF
  // Probe on INS_ID
  // Probe on INS_EX
  // Probe on INS_MEM
  // Probe on INS_WB
  // Probe on IF_PC[11:0]
  IF_ID IF_ID (
    .Bubble(Bubble), .Enable(xor_2_out), .CLK(CLK), .CLR(RST), .PC_IN(IF_PC), .PC_OUT(ID_PC), .IR_IN(INS_IF),
    .IR_OUT(INS_ID));
  // Probe on ID_PC[11:0]
  // Probe on MEM_PC[11:0]
  // Probe on EX_PC[11:0]
  // Probe on WB_PC[11:0]
  Multiplexer #(.width(5), .enable("false")) multiplexer_5 (
    .in0(INS_ID[25:21]), .in1(5'b00100), .out(R1_ID), .sel(\硬布线控制器_1_syscall ));
  \重定向信号生成  \u_重定向信号生成_1  (
    .OP(INS_ID[31:26]), .EX_WriteReg_num(WR_EX), .EX_RegWrite(WB_EX[0]), .EX_JAL(JAL_EX),
    .Forward_A(Forward_EX[1:0]), .MEM_WriteReg_num(WR_MEM), .MEM_RegWrite(WB_MEM[0]),
    .Forward_B(Forward_EX[3:2]), .Func(INS_ID[5:0]), .ID_R1_num(R1_ID), .ID_R2_num(R2_ID),
    .EX_Mem2Reg(WB_EX[2]), .Load_use(Load_use), .\数据相关 (\数据相关 ));
  Multiplexer #(.width(5), .enable("false")) multiplexer_6 (
    .in0(INS_ID[20:16]), .in1(5'b00010), .out(R2_ID), .sel(\硬布线控制器_1_syscall ));
  assign \无符号拓展Imm  = {{16{1'b0}}, INS_ID[15:0]};  // Bit_Extender bit_extender_1
  assign \有符号拓展Imm  = {{16{INS_ID[15]}}, INS_ID[15:0]};  // Bit_Extender bit_extender_2
  // Probe on \有符号拓展Imm 
  \硬布线控制器  \u_硬布线控制器_1  (
    .Func(INS_ID[5:0]), .OP(INS_ID[31:26]), .ALU_OP(\硬布线控制器_1_alu_op ), .MemToReg(\硬布线控制器_1_memtoreg ),
    .MemWrite(\硬布线控制器_1_memwrite ), .ALU_SRC(\硬布线控制器_1_alu_src ), .RegWrite(\硬布线控制器_1_regwrite ),
    .SysCALL(\硬布线控制器_1_syscall ), .SignedExt(SignedExt), .RegDst(\硬布线控制器_1_regdst ), .JR(\硬布线控制器_1_jmp [1]),
    .JMP(\硬布线控制器_1_jmp [0]), .Beq(\硬布线控制器_1_beq [0]), .JAL(\硬布线控制器_1_jal ), .Bne(\硬布线控制器_1_beq [1]),
    .LUISrc(LUISrc), .bgtz(bgzt_t), .LBU(\硬布线控制器_1_jmp [3]));
  MIPS_Regifile mips_regifile_1 (
    .Din(Din_WB), .Clk(CLK), .R1(R1_ID_t), .R2(R2_ID_t), .WE(Regwrite), .W_num(WR_WB), .R1_num(R1_ID),
    .R2_num(R2_ID));
  Multiplexer #(.width(32), .enable("false")) multiplexer_7 (
    .in0(\无符号拓展Imm ), .in1(\有符号拓展Imm ), .out(Imm_ID), .sel(SignedExt));
  // Probe on R1_ID_t
  // Probe on R2_ID_t
  Multiplexer #(.width(5), .enable("false")) multiplexer_8 (
    .in0(INS_ID[10:6]), .in1(5'b10000), .out(multiplexer_8_out), .sel(LUISrc));
  Comparator #(.width(32)) comparator_1 (.a(ALUB_EX), .b(32'h22), .eq(display));  // open: gt, lt
  Pull_Resistor pull_resistor_1 (.node(display));
  Multiplexer #(.width(5), .enable("false")) multiplexer_9 (
    .in0(INS_ID[20:16]), .in1(INS_ID[15:11]), .out(multiplexer_9_out), .sel(\硬布线控制器_1_regdst ));
  Multiplexer #(.width(5), .enable("false")) multiplexer_10 (
    .in0(multiplexer_9_out), .in1({5{1'b1}}), .out(multiplexer_10_out), .sel(\硬布线控制器_1_jal ));
  and and_1 (show, SYSCALL_EX, display);
  ID_EX id_ex_1 (
    .PC_IN(ID_PC), .IR_IN(INS_ID), .R1_IN(R1_ID_t), .PC_OUT(EX_PC), .IR_OUT(INS_EX), .R1_OUT(id_ex_1_r1_out),
    .Bubble(or_3_out), .Enable(run), .CLK(CLK), .CLR(RST), .RegWrite(\硬布线控制器_1_regwrite ),
    .RegDst(\硬布线控制器_1_regdst ), .MemToReg(\硬布线控制器_1_memtoreg ), .MemWrite(\硬布线控制器_1_memwrite ),
    .Beq(\硬布线控制器_1_beq [0]), .Bne(\硬布线控制器_1_beq [1]), .JR(\硬布线控制器_1_jmp [1]), .JMP(\硬布线控制器_1_jmp [0]),
    .JAL(\硬布线控制器_1_jal ), .SysCALL(\硬布线控制器_1_syscall ), .MEM(MEM_EX), .SysCALL_2(SYSCALL_EX), .WB(WB_EX),
    .BRANCH_OUT({Bne, Beq, Bgzt}), .JMP_OUT({JAL_EX, JMP, JR}), .ALUOP_OUT(ALUOP_EX),
    .Shamt_IN(multiplexer_8_out), .Shamt_OUT(id_ex_1_shamt_out), .Bgzt(bgzt_t), .LBU(\硬布线控制器_1_jmp [3]),
    .R2_IN(R2_ID_t), .R2_OUT(id_ex_1_r2_out), .WR_IN(multiplexer_10_out), .WR_OUT(WR_EX),
    .Forward_IN(Forward_EX), .Forward_OUT({ForwardB_EX, ForwardA_EX}), .ALUOP_IN(\硬布线控制器_1_alu_op ),
    .ALUSrcB(\硬布线控制器_1_alu_src ), .ALUSrcB_2(id_ex_1_alusrcb_2), .Imm(Imm_ID), .Imm_2(Imm_EX));  // open: ALUB_IN, ALUB_OUT
  or or_3 (or_3_out, Load_use, Bubble);
  // Probe on ALUOP_EX
  // Probe on ALUres_EX
  // Probe on R1_EX
  // Probe on R2_EX
  // Probe on {EX_PC[31:28], INS_EX[25:0], 2'b00}
  // Probe on EX_PC
  // Probe on WR_EX
  not not_2 (not_2_out, display);
  Register #(.width(32)) register_1 (.D(R1_EX), .en(show), .Q(LedData), .clk(CLK), .clr(RST));
  and and_2 (HALT_EX, SYSCALL_EX, not_2_out);
  Pull_Resistor pull_resistor_2 (.node(\条件分支 ));
  assign \条件分支  = Beq ? mips_alu_1_equal : 1'bz;  // Controlled_Buffer controlled_buffer_1
  Multiplexer #(.select(2), .width(32), .disabled(0), .enable("false")) multiplexer_11 (
    .in0(id_ex_1_r2_out), .in1(ALUres_MEM), .in2(Din_WB), .in3(PC_1_MEM), .out(R2_EX), .sel(ForwardB_EX));
  assign \条件分支  = Bgzt ? nor_1_out : 1'bz;  // Controlled_Buffer controlled_buffer_2
  assign \条件分支  = Bne ? ~mips_alu_1_equal : 1'bz;  // Controlled_Inverter controlled_inverter_1
  Multiplexer #(.width(32), .enable("false")) multiplexer_12 (
    .in0(R2_EX), .in1(Imm_EX), .out(ALUB_EX), .sel(id_ex_1_alusrcb_2));
  or or_4 (Bubble, \条件分支 , JMP);
  nor nor_1 (nor_1_out, ALUres_EX[0], mips_alu_1_equal);
  Multiplexer #(.select(2), .width(32), .disabled(0), .enable("false")) multiplexer_13 (
    .in0(id_ex_1_r1_out), .in1(ALUres_MEM), .in2(Din_WB), .in3(PC_1_MEM), .out(R1_EX), .sel(ForwardA_EX));
  Adder #(.width(32)) adder_2 (.a(32'h4), .b(EX_PC), .out(adder_2_out));  // open: cin, cout
  MIPS_ALU mips_alu_1 (
    .X(R1_EX), .Y(ALUB_EX), .AluOP(ALUOP_EX), .Equal(mips_alu_1_equal), .Result(ALUres_EX),
    .shamt(id_ex_1_shamt_out));  // open: Result_2
  assign bit_extender_3_out = {{14{INS_EX[15]}}, {INS_EX[15:0], 2'b00}};  // Bit_Extender bit_extender_3
  Adder #(.width(32)) adder_3 (.a(adder_2_out), .b(bit_extender_3_out), .out(PC_Branch));  // open: cin, cout
  // Probe on LBU
  // Probe on LedData
  // Probe on ALUres_MEM
  // Probe on MEMD_MEM
  // Probe on Memwrite
  EX_MEM EX_MEM (
    .PC_IN(EX_PC), .IR_IN(INS_EX), .R2_IN(R2_EX), .PC_OUT(MEM_PC), .IR_OUT(INS_MEM), .R2_OUT(EX_MEM_r2_out),
    .Bubble(1'b0), .Enable(run), .CLK(CLK), .CLR(RST), .ALURS_IN(ALUres_EX), .ALURS_OUT(ALUres_MEM),
    .WB_2(WB_MEM), .MEM_2({LBU, Memwrite}), .SysCALL_2(EX_MEM_syscall_2), .WB(WB_EX), .MEM(MEM_EX),
    .SysCALL(SYSCALL_EX), .JAL(JAL_EX), .JAL_2(JAL_MEM), .HALT(HALT_EX), .HALT_2(EX_MEM_halt_2),
    .WR_IN(WR_EX), .WR_OUT(WR_MEM));
  // Probe on WB_MEM
  RAM #(.addrWidth(10), .dataWidth(32), .bus("separate")) ram_1 (
    .addr(ALUres_MEM[11:2]), .din(EX_MEM_r2_out), .data(MEMD_MEM), .str(Memwrite), .clk(CLK), .clr(RST));  // open: sel, ld
  Adder #(.width(32)) adder_4 (.a(MEM_PC), .b(32'h4), .out(PC_1_MEM));  // open: cin, cout
  Multiplexer #(.select(2), .width(8), .disabled(0), .enable("false")) multiplexer_14 (
    .in0(MEMD_MEM[7:0]), .in1(MEMD_MEM[15:8]), .in2(MEMD_MEM[23:16]), .in3(MEMD_MEM[31:24]),
    .out(multiplexer_14_out), .sel(ALUres_MEM[1:0]));
  // Probe on WR_WB
  // Probe on Regwrite
  Multiplexer #(.width(32), .enable("false")) multiplexer_15 (
    .in0(MEMD_MEM), .in1({{24{1'b0}}, multiplexer_14_out}), .out(multiplexer_15_out), .sel(LBU));
  // Probe on Din_WB
  MEM_WB mem_wb_1 (
    .Bubble(1'b0), .Enable(run), .CLK(CLK), .CLR(RST), .PC_IN(MEM_PC), .PC_OUT(WB_PC), .IR_IN(INS_MEM),
    .IR_OUT(INS_WB), .ALURS_IN(ALUres_MEM), .ALURS_OUT(ALUres_WB), .MEMD_IN(multiplexer_15_out),
    .MEMD_OUT(MEMD_WB), .WB(WB_MEM), .WB_2({Mem2reg_WB, RegDst, Regwrite}), .SysCALL_2(SYSCALL_WB),
    .SysCALL(EX_MEM_syscall_2), .JAL(JAL_MEM), .JAL_2(JAL_WB), .HALT(EX_MEM_halt_2), .HALT_2(HALT_WB),
    .WR_IN(WR_MEM), .WR_OUT(WR_WB));
  Multiplexer #(.width(32)) multiplexer_16 (
    .in0(ALUres_WB), .in1(MEMD_WB), .out(multiplexer_16_out), .sel(Mem2reg_WB));  // open: en
  Adder #(.width(32)) adder_5 (.a(WB_PC), .b(32'h4), .out(adder_5_out));  // open: cin, cout
  Multiplexer #(.width(32)) multiplexer_17 (
    .in0(multiplexer_16_out), .in1(adder_5_out), .out(Din_WB), .sel(JAL_WB));  // open: en

  // Other names for the same wires on the sheet: J_addr[31:2] = {EX_PC[31:28], INS_EX[25:0]};
  //   Shamt[4:0] = INS_ID[10:6]; 原PC[31:0] = IF_PC

  // Notes on the sheet:
  //   中断源
  //   中断等待指示
  //   数码管输出
  //   指令存储器
  //   指令字
  //   contents of rom_1 (hex, n*v repeats v):
  //   20110001 8000005 20110001 20120002 20130003 8000009 20110001 20120002 20130003 800000d 20110001
  //   20120002 20130003 8000011 20110001 20120002 20130003 c0000b8 20100001 20110001 118fc0 112020
  //   20020022 c 118882 12200001 8000015 112020 20020022 c 20110001 118880 112020 20020022 c 12200001
  //   800001f 20110001 118fc0 112020 20020022 c 1188c3 112020 20020022 c 118903 112020 20020022 c 118903
  //   112020 20020022 c 118903 112020 20020022 c 118903 112020 20020022 c 118903 112020 20020022 c 118903
  //   112020 20020022 c 118903 112020 20020022 c 20100001 109fc0 139fc3 8021 2012000c 24160003 26100001
  //   3210000f 20080008 20090001 139900 2709825 132020 20020022 c 1094022 1500fff9 22100001 2018000f
  //   2188024 108700 20080008 20090001 139902 2709825 132021 20020022 c 1094022 1500fff9 108702 2c9b022
  //   12c00001 8000050 4020 1084027 84400 3508ffff 82021 20020022 c 2010ffff 20110000 ae300000 22100001
  //   22310004 ae300000 22100001 22310004 ae300000 22100001 22310004 ae300000 22100001 22310004 ae300000
  //   22100001 22310004 ae300000 22100001 22310004 ae300000 22100001 22310004 ae300000 22100001 22310004
  //   ae300000 22100001 22310004 ae300000 22100001 22310004 ae300000 22100001 22310004 ae300000 22100001
  //   22310004 ae300000 22100001 22310004 ae300000 22100001 22310004 ae300000 22100001 22310004 ae300000
  //   22100001 22310004 22100001 8020 2011003c 8e130000 8e340000 274402a 11000002 ae330000 ae140000
  //   2231fffc 1611fff8 102020 20020022 c 22100004 2011003c 1611fff2 20020032 c 20100000 22100001 102020
  //   20020022 c 22100002 102020 20020022 c 22100003 102020 20020022 c 22100004 102020 20020022 c 22100005
  //   102020 20020022 c 22100006 102020 20020022 c 22100007 102020 20020022 c 22100008 102020 20020022
  //   20020022 c 3e00008
  //   流水调试日志用
  //   OP
  //   Func
  //   OP
  //   Func
  //   rs
  //   rt
  //   rd
  //   Imm
  //   Shamt
  //   bgtz
  //   JMP
  //   JR
  //   SignedExt
  //   LUISrc
  //   OP
  //   Func
  //   Beq
  //   Bne
  //   MemToReg
  //   MemWrite
  //   AluOP
  //   AluSrcB
  //   RegWrite
  //   JAL
  //   RegDst
  //   Syscall
  //   rt
  //   rd
  //   addr
  //   Imm
endmodule

module \重定向信号生成  (
  input  [5:0] OP,
  input  [4:0] EX_WriteReg_num,
  input  EX_RegWrite,
  input  EX_JAL,
  input  [4:0] MEM_WriteReg_num,
  input  MEM_RegWrite,
  input  EX_Mem2Reg,
  input  [5:0] Func,
  input  [4:0] ID_R1_num,
  input  [4:0] ID_R2_num,
  output [1:0] Forward_A,
  output Load_use,
  output \数据相关 ,
  output [1:0] Forward_B
);

  wire and_1_out, and_2_out, comparator_1_eq, comparator_2_eq, comparator_3_eq, comparator_4_eq, or_1_out,
       or_2_out, or_3_out, \源寄存器使用情况_1_r1_used , \源寄存器使用情况_1_r2_used ;
  wire [1:0] controlled_buffer_3_out, controlled_buffer_4_out, multiplexer_1_out, multiplexer_2_out,
       multiplexer_3_out, multiplexer_4_out;
  wire [4:0] controlled_buffer_1_out, pull_resistor_1_node;

  assign controlled_buffer_1_out = EX_RegWrite ? EX_WriteReg_num : 5'bz;  // Controlled_Buffer controlled_buffer_1
  Pull_Resistor pull_resistor_1 (.node(pull_resistor_1_node));
  assign pull_resistor_1_node = MEM_RegWrite ? MEM_WriteReg_num : 5'bz;  // Controlled_Buffer controlled_buffer_2
  \源寄存器使用情况  \u_源寄存器使用情况_1  (
    .OP0(OP[0]), .OP1(OP[1]), .OP2(OP[2]), .OP3(OP[3]), .OP4(OP[4]), .OP5(OP[5]), .F0(Func[0]), .F1(Func[1]),
    .F2(Func[2]), .F3(Func[3]), .F4(Func[4]), .F5(Func[5]), .R1_Used(\源寄存器使用情况_1_r1_used ),
    .R2_Used(\源寄存器使用情况_1_r2_used ));
  Pull_Resistor pull_resistor_2 (.node(controlled_buffer_1_out));
  or or_1 (or_1_out, ID_R1_num[0], ID_R1_num[1], ID_R1_num[2], ID_R1_num[3], ID_R1_num[4]);
  or or_2 (or_2_out, ID_R2_num[0], ID_R2_num[1], ID_R2_num[2], ID_R2_num[3], ID_R2_num[4]);
  Comparator #(.width(5)) comparator_1 (
    .a(ID_R1_num), .b(controlled_buffer_1_out), .eq(comparator_1_eq));  // open: gt, lt
  // Probe on controlled_buffer_1_out
  Comparator #(.width(5)) comparator_2 (
    .a(controlled_buffer_1_out), .b(ID_R2_num), .eq(comparator_2_eq));  // open: gt, lt
  Comparator #(.width(5)) comparator_3 (.a(ID_R1_num), .b(pull_resistor_1_node), .eq(comparator_3_eq));  // open: gt, lt
  Comparator #(.width(5)) comparator_4 (.a(pull_resistor_1_node), .b(ID_R2_num), .eq(comparator_4_eq));  // open: gt, lt
  and and_1 (and_1_out, or_1_out, \源寄存器使用情况_1_r1_used );
  and and_2 (and_2_out, \源寄存器使用情况_1_r2_used , or_2_out);
  assign controlled_buffer_3_out[0] = and_1_out ? comparator_1_eq : 1'bz;  // Controlled_Buffer controlled_buffer_3
  assign controlled_buffer_4_out[0] = and_2_out ? comparator_2_eq : 1'bz;  // Controlled_Buffer controlled_buffer_4
  assign controlled_buffer_4_out[1] = and_2_out ? comparator_4_eq : 1'bz;  // Controlled_Buffer controlled_buffer_5
  Pull_Resistor pull_resistor_3 (.node(controlled_buffer_3_out[0]));
  Pull_Resistor pull_resistor_4 (.node(controlled_buffer_4_out[0]));
  Pull_Resistor pull_resistor_5 (.node(controlled_buffer_3_out[1]));
  assign controlled_buffer_3_out[1] = and_1_out ? comparator_3_eq : 1'bz;  // Controlled_Buffer controlled_buffer_6
  Pull_Resistor pull_resistor_6 (.node(controlled_buffer_4_out[1]));
  or or_3 (or_3_out, controlled_buffer_3_out[0], controlled_buffer_4_out[0]);
  and and_3 (Load_use, EX_Mem2Reg, or_3_out);
  Multiplexer #(.width(2), .enable("false")) multiplexer_1 (
    .in0(2'b00), .in1(2'b10), .out(multiplexer_1_out), .sel(controlled_buffer_3_out[1]));
  Multiplexer #(.width(2), .enable("false")) multiplexer_2 (
    .in0(2'b00), .in1(2'b10), .out(multiplexer_2_out), .sel(controlled_buffer_4_out[1]));
  Multiplexer #(.width(2), .enable("false")) multiplexer_3 (
    .in0(2'b01), .in1(2'b11), .out(multiplexer_3_out), .sel(EX_JAL));
  Multiplexer #(.width(2), .enable("false")) multiplexer_4 (
    .in0(2'b01), .in1(2'b11), .out(multiplexer_4_out), .sel(EX_JAL));
  Multiplexer #(.width(2), .enable("false")) multiplexer_5 (
    .in0(multiplexer_2_out), .in1(multiplexer_3_out), .out(Forward_B), .sel(controlled_buffer_4_out[0]));
  Multiplexer #(.width(2), .enable("false")) multiplexer_6 (
    .in0(multiplexer_1_out), .in1(multiplexer_4_out), .out(Forward_A), .sel(controlled_buffer_3_out[0]));
  or or_4 (\数据相关 , controlled_buffer_3_out[0], controlled_buffer_3_out[1], controlled_buffer_4_out[0], controlled_buffer_4_out[1]);

  // Other names for the same wires on the sheet: JAL_EX = EX_JAL; MEM2Reg_EX = EX_Mem2Reg; OP_CODE[5:0] = OP
endmodule

module \动态分支预测流水线  (
);

  wire and_1_out, and_2_out, Beq, Bgzt, bgzt_t, Bne, Bubble, buffer_1_out, buffer_2_out, buffer_3_out,
       buffer_4_out, buffer_6_out, CLK, comparator_2_eq, display, EX_MEM_halt_2, EX_MEM_syscall_2, Go,
       HALT_EX, HALT_WB, id_ex_1_alusrcb_2, IR1, IR2, IR3, JAL_EX, JAL_MEM, JAL_WB, JMP, JR, LBU, Load,
       Load_CLK, Load_use, LUISrc, Mem2reg_WB, Memwrite, mips_alu_1_equal, Miss_IF, nor_1_out, not_1_out,
       not_2_out, not_3_out, or_1_out, or_3_out, RegDst, Regwrite, RST, run, show, SignedExt, SYSCALL_EX,
       SYSCALL_WB, W1, W2, W3, xor_1_out, xor_2_out, \分支信号_EX , \数据相关 , \条件分支 , \硬布线控制器_1_alu_src ,
       \硬布线控制器_1_jal , \硬布线控制器_1_memtoreg , \硬布线控制器_1_memwrite , \硬布线控制器_1_regdst , \硬布线控制器_1_regwrite ,
       \硬布线控制器_1_syscall , \预测失败_EX , \预测跳转 ;
  wire [1:0] ForwardA_EX, ForwardB_EX, MEM_EX, \硬布线控制器_1_beq ;
  wire [2:0] WB_EX, WB_MEM;
  wire [3:0] ALUOP_EX, Forward_EX, \硬布线控制器_1_alu_op , \硬布线控制器_1_jmp ;
  wire [4:0] id_ex_1_shamt_out, multiplexer_8_out, multiplexer_9_out, multiplexer_10_out, R1_ID, R2_ID,
       WR_EX, WR_MEM, WR_WB;
  wire [7:0] multiplexer_18_out;
  wire [15:0] \LoadUse次数 , \总周期数 , \插入气泡数 , \无条件分支数 , \条件分支成功数 ;
  wire [31:0] adder_5_out, ALUB_EX, ALUres_EX, ALUres_MEM, ALUres_WB, bit_extender_3_out, Din_WB,
       EX_MEM_r2_out, EX_PC, id_ex_1_r1_out, id_ex_1_r2_out, ID_PC, IF_PC, Imm_EX, INS_EX, INS_ID, INS_IF,
       INS_MEM, INS_WB, LedData, MEM_PC, MEMD_MEM, MEMD_WB, multiplexer_1_out, multiplexer_2_out,
       multiplexer_4_out, multiplexer_7_out, multiplexer_11_out, multiplexer_12_out, multiplexer_17_out,
       multiplexer_19_out, PC_1_EX, PC_1_MEM, PC_Branch, PC_next, PC_target_IF, R1_EX, R1_ID_t, R2_EX,
       R2_ID_t, WB_PC, \分支目的地址_EX , \加1的PC , \无符号拓展Imm , \有符号拓展Imm ;

  Button \u_总复位  (.out(RST));
  Button _1 (.out(IR1));
  Button _2 (.out(IR2));
  Button _3 (.out(IR3));
  Button \u_继续运行  (.out(Go));
  LED led_1 (.in(W1));
  LED led_2 (.in(W2));
  LED led_3 (.in(W3));
  Button \u_装载断点  (.out(Load));
  Hex_Digit_Display hex_digit_display_1 (.value(LedData[31:28]));  // open: dp
  buf buffer_1 (buffer_1_out, buffer_3_out);
  buf buffer_2 (buffer_2_out, Load);
  buf buffer_3 (buffer_3_out, buffer_2_out);
  buf buffer_4 (buffer_4_out, buffer_1_out);
  not not_1 (not_1_out, Miss_IF);
  Hex_Digit_Display hex_digit_display_2 (.value(LedData[27:24]));  // open: dp
  Hex_Digit_Display hex_digit_display_3 (.value(LedData[23:20]));  // open: dp
  Counter #(.width(16), .max('hffff)) counter_1 (
    .count(Load_use), .Q(\LoadUse次数 ), .clk(CLK), .clr(RST));  // open: load, D, carry
  Counter #(.width(16), .max('hffff)) counter_2 (
    .count(run), .Q(\总周期数 ), .clk(CLK), .clr(RST));  // open: load, D, carry
  Counter #(.width(16), .max('hffff)) counter_3 (
    .count(\条件分支 ), .Q(\条件分支成功数 ), .clk(CLK), .clr(RST));  // open: load, D, carry
  buf buffer_5 (Load_CLK, buffer_6_out);
  buf buffer_6 (buffer_6_out, buffer_4_out);
  and and_1 (and_1_out, not_1_out, \预测跳转 );
  Multiplexer #(.width(32), .enable("false")) multiplexer_1 (
    .in0(\加1的PC ), .in1(PC_target_IF), .out(multiplexer_1_out), .sel(and_1_out));
  Hex_Digit_Display hex_digit_display_4 (.value(LedData[15:12]));  // open: dp
  Hex_Digit_Display hex_digit_display_5 (.value(LedData[19:16]));  // open: dp
  Multiplexer #(.width(32), .enable("false")) multiplexer_2 (
    .in0(multiplexer_1_out), .in1(\分支目的地址_EX ), .out(multiplexer_2_out), .sel(\预测失败_EX ));
  Hex_Digit_Display hex_digit_display_6 (.value(LedData[7:4]));  // open: dp
  Hex_Digit_Display hex_digit_display_7 (.value(LedData[11:8]));  // open: dp
  Clock clock_1 (.out(CLK));
  Multiplexer #(.width(32), .enable("false")) multiplexer_3 (
    .in0(multiplexer_2_out), .in1(32'h32dc), .out(PC_next), .sel(Load));
  Hex_Digit_Display hex_digit_display_8 (.value(LedData[3:0]));  // open: dp
  Counter #(.width(16), .max('hffff)) counter_4 (
    .count(JMP), .Q(\无条件分支数 ), .clk(CLK), .clr(RST));  // open: load, D, carry
  and and_2 (and_2_out, \分支信号_EX , CLK);
  Multiplexer #(.width(32), .enable("false")) multiplexer_4 (
    .in0(IF_PC), .in1(EX_PC), .out(multiplexer_4_out), .sel(and_2_out));
  or or_1 (or_1_out, \条件分支 , JMP);
  not not_2 (not_2_out, HALT_WB);
  or or_2 (run, Go, not_2_out);
  xor xor_1 (xor_1_out, Load_use, run);
  or or_3 (or_3_out, Load_CLK, CLK);
  // Probe on PC_next
  Counter #(.width(16), .max('hffff)) counter_5 (
    .count(Bubble), .Q(\插入气泡数 ), .clk(CLK), .clr(RST));  // open: load, D, carry
  Register #(.width(32)) PC (.D(PC_next), .en(xor_1_out), .Q(IF_PC), .clk(or_3_out), .clr(RST));
  // Probe on \总周期数 
  // Probe on \无条件分支数 
  // Probe on \条件分支成功数 
  // Probe on \插入气泡数 
  // Probe on \LoadUse次数 
  Adder #(.width(32)) adder_1 (.a(IF_PC), .b(32'h4), .out(\加1的PC ));  // open: cin, cout
  // Probe on IF_PC[11:0]
  \分支预测历史表  \u_分支预测历史表_1  (
    .PC_target_IN(\分支目的地址_EX ), .PC(multiplexer_4_out), .CLK(CLK), .Enable(run), .Miss(Miss_IF),
    .PC_target(PC_target_IF), .If_Branch(\预测跳转 ), .\分支成功 (or_1_out), .SET(\分支信号_EX ), .\无条件分支 (JMP));
  // Probe on Load_use
  // Probe on \数据相关 
  // Probe on WR_EX
  // Probe on WR_MEM
  // Probe on ForwardA_EX
  // Probe on ForwardB_EX
  // Probe on ID_PC[11:0]
  ROM #(.addrWidth(10), .dataWidth(32)) rom_1 (.addr(IF_PC[11:2]), .data(INS_IF));  // open: sel
  // Probe on EX_PC[11:0]
  // Probe on MEM_PC[11:0]
  xor xor_2 (xor_2_out, Load_use, run);
  // Probe on INS_IF
  // Probe on INS_ID
  // Probe on INS_EX
  // Probe on INS_MEM
  // Probe on INS_WB
  // Probe on WB_PC[11:0]
  IF_ID IF_ID (
    .Bubble(\预测失败_EX ), .Enable(xor_2_out), .CLK(CLK), .CLR(RST), .PC_IN(IF_PC), .PC_OUT(ID_PC),
    .IR_IN(INS_IF), .IR_OUT(INS_ID));
  \重定向流水线  \u_重定向流水线_1  ();
  Comparator #(.width(32)) comparator_1 (.a(ALUB_EX), .b(32'h22), .eq(display));  // open: gt, lt
  Pull_Resistor pull_resistor_1 (.node(display));
  Multiplexer #(.width(5), .enable("false")) multiplexer_5 (
    .in0(INS_ID[25:21]), .in1(5'b00100), .out(R1_ID), .sel(\硬布线控制器_1_syscall ));
  and and_3 (show, SYSCALL_EX, display);
  Multiplexer #(.width(5), .enable("false")) multiplexer_6 (
    .in0(INS_ID[20:16]), .in1(5'b00010), .out(R2_ID), .sel(\硬布线控制器_1_syscall ));
  assign \无符号拓展Imm  = {{16{1'b0}}, INS_ID[15:0]};  // Bit_Extender bit_extender_1
  assign \有符号拓展Imm  = {{16{INS_ID[15]}}, INS_ID[15:0]};  // Bit_Extender bit_extender_2
  not not_3 (not_3_out, display);
  Register #(.width(32)) register_1 (.D(R1_EX), .en(show), .Q(LedData), .clk(CLK), .clr(RST));
  \重定向信号生成  \u_重定向信号生成_1  (
    .OP(INS_ID[31:26]), .EX_WriteReg_num(WR_EX), .EX_RegWrite(WB_EX[0]), .EX_JAL(JAL_EX),
    .Forward_A(Forward_EX[1:0]), .MEM_WriteReg_num(WR_MEM), .MEM_RegWrite(WB_MEM[0]),
    .Forward_B(Forward_EX[3:2]), .Func(INS_ID[5:0]), .ID_R1_num(R1_ID), .ID_R2_num(R2_ID),
    .EX_Mem2Reg(WB_EX[2]), .Load_use(Load_use), .\数据相关 (\数据相关 ));
  \硬布线控制器  \u_硬布线控制器_1  (
    .Func(INS_ID[5:0]), .OP(INS_ID[31:26]), .ALU_OP(\硬布线控制器_1_alu_op ), .MemToReg(\硬布线控制器_1_memtoreg ),
    .MemWrite(\硬布线控制器_1_memwrite ), .ALU_SRC(\硬布线控制器_1_alu_src ), .RegWrite(\硬布线控制器_1_regwrite ),
    .SysCALL(\硬布线控制器_1_syscall ), .SignedExt(SignedExt), .RegDst(\硬布线控制器_1_regdst ), .JR(\硬布线控制器_1_jmp [1]),
    .JMP(\硬布线控制器_1_jmp [0]), .Beq(\硬布线控制器_1_beq [0]), .JAL(\硬布线控制器_1_jal ), .Bne(\硬布线控制器_1_beq [1]),
    .LUISrc(LUISrc), .bgtz(bgzt_t), .LBU(\硬布线控制器_1_jmp [3]));
  MIPS_Regifile mips_regifile_1 (
    .Din(Din_WB), .Clk(CLK), .R1(R1_ID_t), .R2(R2_ID_t), .WE(Regwrite), .W_num(WR_WB), .R1_num(R1_ID),
    .R2_num(R2_ID));
  // Probe on \有符号拓展Imm 
  and and_4 (HALT_EX, SYSCALL_EX, not_3_out);
  Multiplexer #(.width(32), .enable("false")) multiplexer_7 (
    .in0(\无符号拓展Imm ), .in1(\有符号拓展Imm ), .out(multiplexer_7_out), .sel(SignedExt));
  // Probe on R1_ID_t
  // Probe on R2_ID_t
  Multiplexer #(.width(5), .enable("false")) multiplexer_8 (
    .in0(INS_ID[20:16]), .in1(INS_ID[15:11]), .out(multiplexer_8_out), .sel(\硬布线控制器_1_regdst ));
  Multiplexer #(.width(5), .enable("false")) multiplexer_9 (
    .in0(INS_ID[10:6]), .in1(5'b10000), .out(multiplexer_9_out), .sel(LUISrc));
  Multiplexer #(.width(5), .enable("false")) multiplexer_10 (
    .in0(multiplexer_8_out), .in1({5{1'b1}}), .out(multiplexer_10_out), .sel(\硬布线控制器_1_jal ));
  ID_EX id_ex_1 (
    .PC_IN(ID_PC), .IR_IN(INS_ID), .R1_IN(R1_ID_t), .PC_OUT(EX_PC), .IR_OUT(INS_EX), .R1_OUT(id_ex_1_r1_out),
    .Bubble(Bubble), .Enable(run), .CLK(CLK), .CLR(RST), .RegWrite(\硬布线控制器_1_regwrite ),
    .RegDst(\硬布线控制器_1_regdst ), .MemToReg(\硬布线控制器_1_memtoreg ), .MemWrite(\硬布线控制器_1_memwrite ),
    .Beq(\硬布线控制器_1_beq [0]), .Bne(\硬布线控制器_1_beq [1]), .JR(\硬布线控制器_1_jmp [1]), .JMP(\硬布线控制器_1_jmp [0]),
    .JAL(\硬布线控制器_1_jal ), .SysCALL(\硬布线控制器_1_syscall ), .MEM(MEM_EX), .SysCALL_2(SYSCALL_EX), .WB(WB_EX),
    .BRANCH_OUT({Bne, Beq, Bgzt}), .JMP_OUT({JAL_EX, JMP, JR}), .ALUOP_OUT(ALUOP_EX),
    .Shamt_IN(multiplexer_9_out), .Shamt_OUT(id_ex_1_shamt_out), .Bgzt(bgzt_t), .LBU(\硬布线控制器_1_jmp [3]),
    .R2_IN(R2_ID_t), .R2_OUT(id_ex_1_r2_out), .WR_IN(multiplexer_10_out), .WR_OUT(WR_EX),
    .Forward_IN(Forward_EX), .Forward_OUT({ForwardB_EX, ForwardA_EX}), .ALUOP_IN(\硬布线控制器_1_alu_op ),
    .ALUSrcB(\硬布线控制器_1_alu_src ), .ALUSrcB_2(id_ex_1_alusrcb_2), .Imm(multiplexer_7_out), .Imm_2(Imm_EX));  // open: ALUB_IN, ALUB_OUT
  or or_4 (Bubble, Load_use, \预测失败_EX );
  Multiplexer #(.width(32), .enable("false")) multiplexer_11 (
    .in0(PC_1_EX), .in1(PC_Branch), .out(multiplexer_11_out), .sel(\条件分支 ));
  Multiplexer #(.width(32), .enable("false")) multiplexer_12 (
    .in0({EX_PC[31:28], INS_EX[25:0], 2'b00}), .in1(R1_EX), .out(multiplexer_12_out), .sel(JR));
  Multiplexer #(.select(2), .width(32), .disabled(0), .enable("false")) multiplexer_13 (
    .in0(id_ex_1_r2_out), .in1(ALUres_MEM), .in2(Din_WB), .in3(PC_1_MEM), .out(R2_EX), .sel(ForwardB_EX));
  // Probe on ALUOP_EX
  // Probe on ALUres_EX
  // Probe on R1_EX
  // Probe on R2_EX
  // Probe on {EX_PC[31:28], INS_EX[25:0], 2'b00}
  // Probe on EX_PC
  // Probe on WR_EX
  Multiplexer #(.width(32), .enable("false")) multiplexer_14 (
    .in0(multiplexer_11_out), .in1(multiplexer_12_out), .out(\分支目的地址_EX ), .sel(JMP));
  Pull_Resistor pull_resistor_2 (.node(\条件分支 ));
  assign \条件分支  = Beq ? mips_alu_1_equal : 1'bz;  // Controlled_Buffer controlled_buffer_1
  assign \条件分支  = Bne ? ~mips_alu_1_equal : 1'bz;  // Controlled_Inverter controlled_inverter_1
  Multiplexer #(.width(32), .enable("false")) multiplexer_15 (
    .in0(R2_EX), .in1(Imm_EX), .out(ALUB_EX), .sel(id_ex_1_alusrcb_2));
  Comparator #(.width(32)) comparator_2 (.a(\分支目的地址_EX ), .b(ID_PC), .eq(comparator_2_eq));  // open: gt, lt
  // Probe on \分支目的地址_EX 
  // Probe on ID_PC
  or or_5 (\分支信号_EX , JMP, Bgzt, Beq, Bne);
  nor nor_1 (nor_1_out, ALUres_EX[0], mips_alu_1_equal);
  assign \条件分支  = Bgzt ? nor_1_out : 1'bz;  // Controlled_Buffer controlled_buffer_2
  Pull_Resistor pull_resistor_3 (.node(\预测失败_EX ));
  assign \预测失败_EX  = \分支信号_EX  ? ~comparator_2_eq : 1'bz;  // Controlled_Inverter controlled_inverter_2
  Multiplexer #(.select(2), .width(32), .disabled(0), .enable("false")) multiplexer_16 (
    .in0(id_ex_1_r1_out), .in1(ALUres_MEM), .in2(Din_WB), .in3(PC_1_MEM), .out(R1_EX), .sel(ForwardA_EX));
  Adder #(.width(32)) adder_2 (.a(32'h4), .b(EX_PC), .out(PC_1_EX));  // open: cin, cout
  MIPS_ALU mips_alu_1 (
    .X(R1_EX), .Y(ALUB_EX), .AluOP(ALUOP_EX), .Equal(mips_alu_1_equal), .Result(ALUres_EX),
    .shamt(id_ex_1_shamt_out));  // open: Result_2
  assign bit_extender_3_out = {{14{INS_EX[15]}}, {INS_EX[15:0], 2'b00}};  // Bit_Extender bit_extender_3
  Adder #(.width(32)) adder_3 (.a(PC_1_EX), .b(bit_extender_3_out), .out(PC_Branch));  // open: cin, cout
  EX_MEM EX_MEM (
    .PC_IN(EX_PC), .IR_IN(INS_EX), .R2_IN(R2_EX), .PC_OUT(MEM_PC), .IR_OUT(INS_MEM), .R2_OUT(EX_MEM_r2_out),
    .Bubble(1'b0), .Enable(run), .CLK(CLK), .CLR(RST), .ALURS_IN(ALUres_EX), .ALURS_OUT(ALUres_MEM),
    .WB_2(WB_MEM), .MEM_2({LBU, Memwrite}), .SysCALL_2(EX_MEM_syscall_2), .WB(WB_EX), .MEM(MEM_EX),
    .SysCALL(SYSCALL_EX), .JAL(JAL_EX), .JAL_2(JAL_MEM), .HALT(HALT_EX), .HALT_2(EX_MEM_halt_2),
    .WR_IN(WR_EX), .WR_OUT(WR_MEM));
  // Probe on LBU
  // Probe on LedData
  // Probe on ALUres_MEM
  // Probe on MEMD_MEM
  // Probe on Memwrite
  Adder #(.width(32)) adder_4 (.a(MEM_PC), .b(32'h4), .out(PC_1_MEM));  // open: cin, cout
  // Probe on WB_MEM
  RAM #(.addrWidth(10), .dataWidth(32), .bus("separate")) ram_1 (
    .addr(ALUres_MEM[11:2]), .din(EX_MEM_r2_out), .data(MEMD_MEM), .str(Memwrite), .clk(CLK), .clr(RST));  // open: sel, ld
  Multiplexer #(.width(32), .enable("false")) multiplexer_17 (
    .in0(MEMD_MEM), .in1({{24{1'b0}}, multiplexer_18_out}), .out(multiplexer_17_out), .sel(LBU));
  Multiplexer #(.select(2), .width(8), .disabled(0), .enable("false")) multiplexer_18 (
    .in0(MEMD_MEM[7:0]), .in1(MEMD_MEM[15:8]), .in2(MEMD_MEM[23:16]), .in3(MEMD_MEM[31:24]),
    .out(multiplexer_18_out), .sel(ALUres_MEM[1:0]));
  // Probe on WR_WB
  // Probe on Regwrite
  MEM_WB mem_wb_1 (
    .Bubble(1'b0), .Enable(run), .CLK(CLK), .CLR(RST), .PC_IN(MEM_PC), .PC_OUT(WB_PC), .IR_IN(INS_MEM),
    .IR_OUT(INS_WB), .ALURS_IN(ALUres_MEM), .ALURS_OUT(ALUres_WB), .MEMD_IN(multiplexer_17_out),
    .MEMD_OUT(MEMD_WB), .WB(WB_MEM), .WB_2({Mem2reg_WB, RegDst, Regwrite}), .SysCALL_2(SYSCALL_WB),
    .SysCALL(EX_MEM_syscall_2), .JAL(JAL_MEM), .JAL_2(JAL_WB), .HALT(EX_MEM_halt_2), .HALT_2(HALT_WB),
    .WR_IN(WR_MEM), .WR_OUT(WR_WB));
  // Probe on Din_WB
  Multiplexer #(.width(32)) multiplexer_19 (
    .in0(ALUres_WB), .in1(MEMD_WB), .out(multiplexer_19_out), .sel(Mem2reg_WB));  // open: en
  Multiplexer #(.width(32)) multiplexer_20 (
    .in0(multiplexer_19_out), .in1(adder_5_out), .out(Din_WB), .sel(JAL_WB));  // open: en
  Adder #(.width(32)) adder_5 (.a(WB_PC), .b(32'h4), .out(adder_5_out));  // open: cin, cout

  // Other names for the same wires on the sheet: J_addr[31:2] = {EX_PC[31:28], INS_EX[25:0]};
  //   Shamt[4:0] = INS_ID[10:6]; 原PC[31:0] = IF_PC

  // Notes on the sheet:
  //   中断源
  //   中断等待指示
  //   数码管输出
  //   指令存储器
  //   指令字
  //   contents of rom_1 (hex, n*v repeats v):
  //   20110001 8000005 20110001 20120002 20130003 8000009 20110001 20120002 20130003 800000d 20110001
  //   20120002 20130003 8000011 20110001 20120002 20130003 c0000b8 20100001 20110001 118fc0 112020
  //   20020022 c 118882 12200001 8000015 112020 20020022 c 20110001 118880 112020 20020022 c 12200001
  //   800001f 20110001 118fc0 112020 20020022 c 1188c3 112020 20020022 c 118903 112020 20020022 c 118903
  //   112020 20020022 c 118903 112020 20020022 c 118903 112020 20020022 c 118903 112020 20020022 c 118903
  //   112020 20020022 c 118903 112020 20020022 c 20100001 109fc0 139fc3 8021 2012000c 24160003 26100001
  //   3210000f 20080008 20090001 139900 2709825 132020 20020022 c 1094022 1500fff9 22100001 2018000f
  //   2188024 108700 20080008 20090001 139902 2709825 132021 20020022 c 1094022 1500fff9 108702 2c9b022
  //   12c00001 8000050 4020 1084027 84400 3508ffff 82021 20020022 c 2010ffff 20110000 ae300000 22100001
  //   22310004 ae300000 22100001 22310004 ae300000 22100001 22310004 ae300000 22100001 22310004 ae300000
  //   22100001 22310004 ae300000 22100001 22310004 ae300000 22100001 22310004 ae300000 22100001 22310004
  //   ae300000 22100001 22310004 ae300000 22100001 22310004 ae300000 22100001 22310004 ae300000 22100001
  //   22310004 ae300000 22100001 22310004 ae300000 22100001 22310004 ae300000 22100001 22310004 ae300000
  //   22100001 22310004 22100001 8020 2011003c 8e130000 8e340000 274402a 11000002 ae330000 ae140000
  //   2231fffc 1611fff8 102020 20020022 c 22100004 2011003c 1611fff2 20020032 c 20100000 22100001 102020
  //   20020022 c 22100002 102020 20020022 c 22100003 102020 20020022 c 22100004 102020 20020022 c 22100005
  //   102020 20020022 c 22100006 102020 20020022 c 22100007 102020 20020022 c 22100008 102020 20020022
  //   20020022 c 3e00008
  //   流水调试日志用
  //   OP
  //   Func
  //   rs
  //   rt
  //   rd
  //   Imm
  //   Shamt
  //   OP
  //   Func
  //   bgtz
  //   JMP
  //   JR
  //   SignedExt
  //   LUISrc
  //   OP
  //   Func
  //   Beq
  //   Bne
  //   MemToReg
  //   MemWrite
  //   AluOP
  //   AluSrcB
  //   RegWrite
  //   JAL
  //   RegDst
  //   Syscall
  //   rt
  //   rd
  //   addr
  //   Imm
endmodule

module \分支预测历史表  (
  input  SET,
  input  [31:0] PC,
  input  [31:0] PC_target_IN,
  input  \分支成功 ,
  input  \无条件分支 ,
  input  CLK,
  input  Enable,
  output Miss,
  output [31:0] PC_target,
  output If_Branch
);

  wire and_2_out, and_3_out, and_4_out, and_5_out, and_6_out, and_7_out, and_8_out, and_9_out, and_10_out,
       and_11_out, and_12_out, and_13_out, \cache已满 , \cache未满 , Clk_t, cmp0, cmp1, cmp2, cmp3, cmp4, cmp5,
       cmp6, decoder_1_out0, decoder_1_out1, decoder_2_out0, decoder_2_out1, decoder_3_out0, decoder_3_out1,
       Hit, L0, L1, L2, L3, L4, L5, L6, L7, LR0, LR1, LR2, LR3, LR4, LR5, LR6, LR7, multiplexer_9_out,
       not_1_out, not_2_out, not_3_out, not_4_out, not_5_out, R0, R1, R2, R3, R4, R5, R6, R7, V0, V1, V2, V3,
       V4, V5, V6, V7;
  wire [1:0] Jumpcode, Jumpcode_IN, multiplexer_1_out, or_3_out, \数据块副本_9_q , \数据块副本_10_q , \数据块副本_11_q ,
       \数据块副本_12_q , \数据块副本_13_q , \数据块副本_14_q , \数据块副本_15_q , \数据块副本_16_q ;
  wire [7:0] controlled_buffer_2_out, decoder_4_out0, xor_1_out;
  wire [15:0] C0, C1, C2, C3, C4, C5, C6, C7, multiplexer_3_out, multiplexer_4_out, multiplexer_5_out,
       multiplexer_6_out, multiplexer_7_out, multiplexer_8_out;
  wire [31:0] Tag0, Tag1, Tag2, Tag3, Tag4, Tag5, Tag6, Tag7, \数据块副本_2_q , \数据块副本_3_q , \数据块副本_4_q ,
       \数据块副本_5_q , \数据块副本_6_q , \数据块副本_7_q , \数据块副本_8_q , \数据块副本_q ;

  Comparator #(.width(32)) comparator_1 (.a(Tag0), .b(PC), .eq(LR0));  // open: gt, lt
  Comparator #(.width(32)) comparator_2 (.a(Tag1), .b(PC), .eq(LR1));  // open: gt, lt
  Comparator #(.width(32)) comparator_3 (.a(Tag2), .b(PC), .eq(LR2));  // open: gt, lt
  Comparator #(.width(32)) comparator_4 (.a(Tag3), .b(PC), .eq(LR3));  // open: gt, lt
  Comparator #(.width(32)) comparator_5 (.a(Tag4), .b(PC), .eq(LR4));  // open: gt, lt
  Comparator #(.width(32)) comparator_6 (.a(Tag5), .b(PC), .eq(LR5));  // open: gt, lt
  Comparator #(.width(32)) comparator_7 (.a(Tag6), .b(PC), .eq(LR6));  // open: gt, lt
  Comparator #(.width(32)) comparator_8 (.a(Tag7), .b(PC), .eq(LR7));  // open: gt, lt
  assign {L7, L6, L5, L4, L3, L2, L1, L0} = {LR7, LR6, LR5, LR4, LR3, LR2, LR1, LR0} & {V7, V6, V5, V4, V3, V2, V1, V0};  // AND_Gate and_1, 8 bits wide
  and and_2 (and_2_out, Jumpcode[0], \分支成功 );
  and and_3 (and_3_out, Jumpcode[1], not_1_out);
  not not_1 (not_1_out, Jumpcode[0]);
  not not_2 (not_2_out, Jumpcode[1]);
  and and_4 (and_4_out, not_2_out, not_3_out);
  not not_3 (not_3_out, Jumpcode[0]);
  not not_4 (not_4_out, Jumpcode[0]);
  and and_5 (and_5_out, not_4_out, not_5_out);
  not not_5 (not_5_out, \分支成功 );
  or or_1 (Hit, L0, L1, L2, L3, L4, L5, L6, L7);
  or or_2 (or_3_out[1], and_2_out, and_3_out);
  or or_3 (or_3_out[0], and_4_out, and_5_out);
  Multiplexer #(.width(2)) multiplexer_1 (
    .in0(2'b10), .in1(2'b01), .out(multiplexer_1_out), .sel(\无条件分支 ));  // open: en
  not not_6 (Miss, Hit);
  assign {R7, R6, R5, R4, R3, R2, R1, R0} = Hit ? {L7, L6, L5, L4, L3, L2, L1, L0} : 8'bz;  // Controlled_Buffer controlled_buffer_1
  not not_7 (Clk_t, CLK);
  Multiplexer #(.width(2)) multiplexer_2 (
    .in0(or_3_out), .in1(multiplexer_1_out), .out(Jumpcode_IN), .sel(Miss));  // open: en
  Comparator #(.width(16)) comparator_9 (.a(C0), .b(C1), .lt(cmp3));  // open: gt, eq
  Comparator #(.width(16)) comparator_10 (.a(C2), .b(C3), .lt(cmp4));  // open: gt, eq
  Comparator #(.width(16)) comparator_11 (.a(C4), .b(C5), .lt(cmp5));  // open: gt, eq
  Comparator #(.width(16)) comparator_12 (.a(C6), .b(C7), .lt(cmp6));  // open: gt, eq
  Decoder #(.disabled(0)) decoder_1 (.out0(decoder_1_out0), .out1(decoder_1_out1), .sel(cmp0));  // open: en
  Decoder #(.disabled(0)) decoder_2 (.out0(decoder_2_out0), .out1(decoder_2_out1), .sel(cmp1), .en(decoder_1_out0));
  Decoder #(.disabled(0)) decoder_3 (.out0(decoder_3_out0), .out1(decoder_3_out1), .sel(cmp2), .en(decoder_1_out1));
  nand nand_1 (\cache未满 , V0, V1, V2, V3, V4, V5, V6, V7);
  Multiplexer #(.width(16)) multiplexer_3 (.in0(C0), .in1(C1), .out(multiplexer_3_out), .sel(cmp3));  // open: en
  Multiplexer #(.width(16)) multiplexer_4 (.in0(C2), .in1(C3), .out(multiplexer_4_out), .sel(cmp4));  // open: en
  Multiplexer #(.width(16)) multiplexer_5 (.in0(C4), .in1(C5), .out(multiplexer_5_out), .sel(cmp5));  // open: en
  Multiplexer #(.width(16)) multiplexer_6 (.in0(C6), .in1(C7), .out(multiplexer_6_out), .sel(cmp6));  // open: en
  Decoder #(.disabled(0)) decoder_4 (
    .out0(decoder_4_out0[0]), .out1(decoder_4_out0[1]), .sel(cmp3), .en(decoder_2_out0));
  Decoder #(.disabled(0)) decoder_5 (
    .out0(decoder_4_out0[2]), .out1(decoder_4_out0[3]), .sel(cmp4), .en(decoder_2_out1));
  Decoder #(.disabled(0)) decoder_6 (
    .out0(decoder_4_out0[4]), .out1(decoder_4_out0[5]), .sel(cmp5), .en(decoder_3_out0));
  Decoder #(.disabled(0)) decoder_7 (
    .out0(decoder_4_out0[6]), .out1(decoder_4_out0[7]), .sel(cmp6), .en(decoder_3_out1));
  assign xor_1_out = {V7, V6, V5, V4, V3, V2, V1, V0} ^ {V6, V5, V4, V3, V2, V1, V0, 1'b1};  // XOR_Gate xor_1, 8 bits wide
  Comparator #(.width(16)) comparator_13 (.a(multiplexer_3_out), .b(multiplexer_4_out), .lt(cmp1));  // open: gt, eq
  Comparator #(.width(16)) comparator_14 (.a(multiplexer_5_out), .b(multiplexer_6_out), .lt(cmp2));  // open: gt, eq
  not not_8 (\cache已满 , \cache未满 );
  Multiplexer #(.width(16)) multiplexer_7 (
    .in0(multiplexer_3_out), .in1(multiplexer_4_out), .out(multiplexer_7_out), .sel(cmp1));  // open: en
  Comparator #(.width(16)) comparator_15 (.a(multiplexer_7_out), .b(multiplexer_8_out), .lt(cmp0));  // open: gt, eq
  Multiplexer #(.width(16)) multiplexer_8 (
    .in0(multiplexer_5_out), .in1(multiplexer_6_out), .out(multiplexer_8_out), .sel(cmp2));  // open: en
  assign controlled_buffer_2_out = \cache已满  ? decoder_4_out0 : 8'bz;  // Controlled_Buffer controlled_buffer_2
  assign controlled_buffer_2_out = \cache未满  ? xor_1_out : 8'bz;  // Controlled_Buffer controlled_buffer_3
  // Probe on PC
  // Probe on PC_target_IN
  assign {R7, R6, R5, R4, R3, R2, R1, R0} = Miss ? controlled_buffer_2_out : 8'bz;  // Controlled_Buffer controlled_buffer_4
  Pull_Resistor pull_resistor_1 (.node({R7, R6, R5, R4, R3, R2, R1, R0}));
  and and_6 (and_6_out, R0, SET);
  and and_7 (and_7_out, R1, SET);
  and and_8 (and_8_out, R2, SET);
  and and_9 (and_9_out, R3, SET);
  and and_10 (and_10_out, R4, SET);
  and and_11 (and_11_out, R5, SET);
  and and_12 (and_12_out, R6, SET);
  and and_13 (and_13_out, R7, SET);
  Register #(.width(1)) VALID (.D(1'b1), .en(and_6_out), .Q(V0), .clk(Clk_t));  // open: clr
  Register #(.width(1)) VALID_2 (.D(1'b1), .en(and_7_out), .Q(V1), .clk(Clk_t));  // open: clr
  Register #(.width(1)) VALID_3 (.D(1'b1), .en(and_8_out), .Q(V2), .clk(Clk_t));  // open: clr
  Register #(.width(1)) VALID_4 (.D(1'b1), .en(and_9_out), .Q(V3), .clk(Clk_t));  // open: clr
  Register #(.width(1)) VALID_5 (.D(1'b1), .en(and_10_out), .Q(V4), .clk(Clk_t));  // open: clr
  Register #(.width(1)) VALID_6 (.D(1'b1), .en(and_11_out), .Q(V5), .clk(Clk_t));  // open: clr
  Register #(.width(1)) VALID_7 (.D(1'b1), .en(and_12_out), .Q(V6), .clk(Clk_t));  // open: clr
  Register #(.width(1)) VALID_8 (.D(1'b1), .en(and_13_out), .Q(V7), .clk(Clk_t));  // open: clr
  Multiplexer #(.select(2), .disabled(0)) multiplexer_9 (
    .in0(1'b0), .in1(1'b0), .in2(1'b1), .in3(1'b1), .out(multiplexer_9_out), .sel(Jumpcode), .en(Enable));
  Register #(.width(32)) \u_标记位  (.D(PC), .en(and_6_out), .Q(Tag0), .clk(Clk_t));  // open: clr
  Register #(.width(32)) \u_标记位_2  (.D(PC), .en(and_7_out), .Q(Tag1), .clk(Clk_t));  // open: clr
  Register #(.width(32)) \u_标记位_3  (.D(PC), .en(and_8_out), .Q(Tag2), .clk(Clk_t));  // open: clr
  Register #(.width(32)) \u_标记位_4  (.D(PC), .en(and_9_out), .Q(Tag3), .clk(Clk_t));  // open: clr
  Register #(.width(32)) \u_标记位_5  (.D(PC), .en(and_10_out), .Q(Tag4), .clk(Clk_t));  // open: clr
  Register #(.width(32)) \u_标记位_6  (.D(PC), .en(and_11_out), .Q(Tag5), .clk(Clk_t));  // open: clr
  Register #(.width(32)) \u_标记位_7  (.D(PC), .en(and_12_out), .Q(Tag6), .clk(Clk_t));  // open: clr
  Register #(.width(32)) \u_标记位_8  (.D(PC), .en(and_13_out), .Q(Tag7), .clk(Clk_t));  // open: clr
  and and_14 (If_Branch, Hit, multiplexer_9_out);
  Counter #(.width(16), .max('hffff)) \u_淘汰标志位  (.count(Hit), .Q(C0), .clk(Clk_t), .clr(L0));  // open: load, D, carry
  Counter #(.width(16), .max('hffff)) \u_淘汰标志位_2  (.count(Hit), .Q(C1), .clk(Clk_t), .clr(L1));  // open: load, D, carry
  Counter #(.width(16), .max('hffff)) \u_淘汰标志位_3  (.count(Hit), .Q(C2), .clk(Clk_t), .clr(L2));  // open: load, D, carry
  Counter #(.width(16), .max('hffff)) \u_淘汰标志位_4  (.count(Hit), .Q(C3), .clk(Clk_t), .clr(L3));  // open: load, D, carry
  Counter #(.width(16), .max('hffff)) \u_淘汰标志位_5  (.count(Hit), .Q(C4), .clk(Clk_t), .clr(L4));  // open: load, D, carry
  Counter #(.width(16), .max('hffff)) \u_淘汰标志位_6  (.count(Hit), .Q(C5), .clk(Clk_t), .clr(L5));  // open: load, D, carry
  Counter #(.width(16), .max('hffff)) \u_淘汰标志位_7  (.count(Hit), .Q(C6), .clk(Clk_t), .clr(L6));  // open: load, D, carry
  Counter #(.width(16), .max('hffff)) \u_淘汰标志位_8  (.count(Hit), .Q(C7), .clk(Clk_t), .clr(L7));  // open: load, D, carry
  Register #(.width(32)) \u_数据块副本  (.D(PC_target_IN), .en(and_6_out), .Q(\数据块副本_q ), .clk(Clk_t));  // open: clr
  Register #(.width(32)) \u_数据块副本_2  (.D(PC_target_IN), .en(and_7_out), .Q(\数据块副本_2_q ), .clk(Clk_t));  // open: clr
  Register #(.width(32)) \u_数据块副本_3  (.D(PC_target_IN), .en(and_8_out), .Q(\数据块副本_3_q ), .clk(Clk_t));  // open: clr
  Register #(.width(32)) \u_数据块副本_4  (.D(PC_target_IN), .en(and_9_out), .Q(\数据块副本_4_q ), .clk(Clk_t));  // open: clr
  Register #(.width(32)) \u_数据块副本_5  (.D(PC_target_IN), .en(and_10_out), .Q(\数据块副本_5_q ), .clk(Clk_t));  // open: clr
  Register #(.width(32)) \u_数据块副本_6  (.D(PC_target_IN), .en(and_11_out), .Q(\数据块副本_6_q ), .clk(Clk_t));  // open: clr
  Register #(.width(32)) \u_数据块副本_7  (.D(PC_target_IN), .en(and_12_out), .Q(\数据块副本_7_q ), .clk(Clk_t));  // open: clr
  Register #(.width(32)) \u_数据块副本_8  (.D(PC_target_IN), .en(and_13_out), .Q(\数据块副本_8_q ), .clk(Clk_t));  // open: clr
  Pull_Resistor pull_resistor_2 (.node(PC_target));
  assign PC_target = L0 ? \数据块副本_q  : 32'bz;  // Controlled_Buffer controlled_buffer_5
  assign PC_target = L1 ? \数据块副本_2_q  : 32'bz;  // Controlled_Buffer controlled_buffer_6
  assign PC_target = L2 ? \数据块副本_3_q  : 32'bz;  // Controlled_Buffer controlled_buffer_7
  assign PC_target = L3 ? \数据块副本_4_q  : 32'bz;  // Controlled_Buffer controlled_buffer_8
  assign PC_target = L4 ? \数据块副本_5_q  : 32'bz;  // Controlled_Buffer controlled_buffer_9
  assign PC_target = L5 ? \数据块副本_6_q  : 32'bz;  // Controlled_Buffer controlled_buffer_10
  assign PC_target = L6 ? \数据块副本_7_q  : 32'bz;  // Controlled_Buffer controlled_buffer_11
  assign PC_target = L7 ? \数据块副本_8_q  : 32'bz;  // Controlled_Buffer controlled_buffer_12
  Pull_Resistor pull_resistor_3 (.node(Jumpcode));
  assign Jumpcode = L0 ? \数据块副本_9_q  : 2'bz;  // Controlled_Buffer controlled_buffer_13
  Register #(.width(2)) \u_数据块副本_9  (.D(Jumpcode_IN), .en(and_6_out), .Q(\数据块副本_9_q ), .clk(Clk_t));  // open: clr
  Register #(.width(2)) \u_数据块副本_10  (.D(Jumpcode_IN), .en(and_7_out), .Q(\数据块副本_10_q ), .clk(Clk_t));  // open: clr
  assign Jumpcode = L1 ? \数据块副本_10_q  : 2'bz;  // Controlled_Buffer controlled_buffer_14
  assign Jumpcode = L2 ? \数据块副本_11_q  : 2'bz;  // Controlled_Buffer controlled_buffer_15
  Register #(.width(2)) \u_数据块副本_11  (.D(Jumpcode_IN), .en(and_8_out), .Q(\数据块副本_11_q ), .clk(Clk_t));  // open: clr
  Register #(.width(2)) \u_数据块副本_12  (.D(Jumpcode_IN), .en(and_9_out), .Q(\数据块副本_12_q ), .clk(Clk_t));  // open: clr
  assign Jumpcode = L3 ? \数据块副本_12_q  : 2'bz;  // Controlled_Buffer controlled_buffer_16
  Register #(.width(2)) \u_数据块副本_13  (.D(Jumpcode_IN), .en(and_10_out), .Q(\数据块副本_13_q ), .clk(Clk_t));  // open: clr
  assign Jumpcode = L4 ? \数据块副本_13_q  : 2'bz;  // Controlled_Buffer controlled_buffer_17
  Register #(.width(2)) \u_数据块副本_14  (.D(Jumpcode_IN), .en(and_11_out), .Q(\数据块副本_14_q ), .clk(Clk_t));  // open: clr
  assign Jumpcode = L5 ? \数据块副本_14_q  : 2'bz;  // Controlled_Buffer controlled_buffer_18
  Register #(.width(2)) \u_数据块副本_15  (.D(Jumpcode_IN), .en(and_12_out), .Q(\数据块副本_15_q ), .clk(Clk_t));  // open: clr
  assign Jumpcode = L6 ? \数据块副本_15_q  : 2'bz;  // Controlled_Buffer controlled_buffer_19
  assign Jumpcode = L7 ? \数据块副本_16_q  : 2'bz;  // Controlled_Buffer controlled_buffer_20
  Register #(.width(2)) \u_数据块副本_16  (.D(Jumpcode_IN), .en(and_13_out), .Q(\数据块副本_16_q ), .clk(Clk_t));  // open: clr

  // Other names for the same wires on the sheet: En = Enable; If_jump = \无条件分支 ; Write = SET; Tag[31:0] = PC;
  //   字节地址[31:0] = PC

  // Notes on the sheet:
  //   输入引脚区
  //   请勿增改引脚，请勿修改子电路封装
  //   行选择
  //   命中选择实现
  //   跳转码
  //   电路功能：利用上面给定的隧道构建8行的Cache，cache映射方式自选
  //   请在下方利用上方输入输出引脚的隧道信号构建电路，ctrl+d复制选择部件
  //   LRU算法
  //   输出引脚区
  //   缺失选择实现
  //   输出选择
endmodule

module \预测跳转  (
  input  J1,
  input  J0,
  input  \分支成功 ,
  output JO1,
  output JO0
);

  wire and_1_out, and_2_out, and_3_out, and_4_out, not_1_out, not_2_out, not_3_out, not_4_out, not_5_out;

  not not_1 (not_1_out, J0);
  not not_2 (not_2_out, J1);
  not not_3 (not_3_out, J0);
  not not_4 (not_4_out, J0);
  not not_5 (not_5_out, \分支成功 );
  and and_1 (and_1_out, J0, \分支成功 );
  and and_2 (and_2_out, J1, not_1_out);
  and and_3 (and_3_out, not_2_out, not_3_out);
  and and_4 (and_4_out, not_4_out, not_5_out);
  or or_1 (JO1, and_1_out, and_2_out);
  or or_2 (JO0, and_3_out, and_4_out);
endmodule
