// Logisim project 分支预测.circ as structural Verilog: 14 circuits, main circuit main
module main (
);

  wire AluB, and_1_out, att_fail, att_suc, bat, branch, clk, DMWrite, equal, halt, hit, hit_3, id_ex_1_r1_r_,
       id_ex_1_r2_r_, \if_id锁存_1_hit_ , \if_id锁存_1_jump_att_ , IR1, IR2, IR3, j, jal4, jal5, jb_3, jump_att,
       jump_att_3, jump_suc, load3, not_1_out, or_1_out, or_2_out, or_3_out, RegDin4, RegDin5, RegW4, RegW5,
       restart, ret, rst, sel1, sel2, sel3, sel4, sft3, stall, sys3, W1, W2, W3, \操作控制器_1_rs_r ,
       \操作控制器_1_rt_r , \操作控制器_1_unsign ;
  wire [2:0] hit_pos, hit_pos_3, \if_id锁存_1_hit_pos_ ;
  wire [3:0] aluop, id_ex_1_ctrl__2, mode, \操作控制器_1_aluop , \操作控制器_1_mode ;
  wire [4:0] ex_mem_1_rw_, id_ex_1_ra_, id_ex_1_rb_, id_ex_1_rw_, multiplexer_3_out, registerfile_1_p6, rw5,
       \指令解析器ir_1_rd , \指令解析器ir_1_rs , \指令解析器ir_1_rt ;
  wire [5:0] \指令解析器ir_1_func , \指令解析器ir_1_op ;
  wire [9:1] id_ex_1_ctrl_;
  wire [12:0] \操作控制器_1_jump ;
  wire [15:0] \jr数 , LoadUse, \总周期数 , \无条件分支指令数 , \有条件分支成功跳转 , \有条件分支指令数 , \预测失败数 , \预测成功数 ;
  wire [21:0] ex_mem_1_ctrl_, mem_wb_1_ctrl_;
  wire [25:0] id_ex_1_ins26_, \指令解析器ir_1_ins26 ;
  wire [31:0] adder_1_out, alu_1_p5, alur4, ex_mem_1_reg_2, EX_PC, id_ex_1__16_32_, id_ex_1_instant,
       id_ex_1_reg_1, id_ex_1_reg_2, ID_PC, \if_id锁存_1_pc_ , \if_id锁存_1_pc_att_ , \if_id锁存_1_输出指令 , IF_PC,
       MEM_PC, mem_wb_1_alu_r, mem_wb_1_dm_out, multiplexer_1_out, multiplexer_5_out, multiplexer_6_out,
       multiplexer_7_out, multiplexer_8_out, multiplexer_9_out, multiplexer_10_out, multiplexer_11_out,
       npc_1_dest_addr, npc_1_pcout, pc_3, pc_att, pc_att_3, regD, registerfile_1_p7, registerfile_1_p8,
       rom_1_data, SyscallOut, WB_PC, \指令解析器ir_1_ins , \指令解析器ir_1_ins16_32 , \数据存储器_1_dataout ;

  Button \u_总复位  (.out(rst));
  Button button_1 (.out(IR1));
  Button button_2 (.out(IR2));
  Button button_3 (.out(IR3));
  Button u_restart (.out(restart));
  LED led_1 (.in(W1));
  LED led_2 (.in(W2));
  LED led_3 (.in(W3));
  Register #(.width(32)) PC (.D(npc_1_pcout), .en(and_1_out), .Q(IF_PC), .clk(clk), .clr(rst));
  and and_1 (and_1_out, or_1_out, not_1_out);
  not not_1 (not_1_out, stall);
  or or_1 (or_1_out, restart, halt);
  Hex_Digit_Display hex_digit_display_1 (.value(SyscallOut[31:28]));  // open: dp
  Adder #(.width(32)) adder_1 (.a(IF_PC), .b(32'h4), .out(adder_1_out));  // open: cin, cout
  Hex_Digit_Display hex_digit_display_2 (.value(SyscallOut[23:20]));  // open: dp
  Hex_Digit_Display hex_digit_display_3 (.value(SyscallOut[27:24]));  // open: dp
  NPC npc_1 (
    .pc_4(adder_1_out), .imm26(id_ex_1_ins26_), ._16_32(id_ex_1__16_32_), .reg1(multiplexer_8_out),
    .pcout(npc_1_pcout), .jump(j), .\return (ret), .pc4_3(EX_PC), .pc_att(pc_att), .jump_att(jump_att),
    .dest_addr(npc_1_dest_addr), .att_suc(att_suc), .jump_suc(jump_suc), .hit_3(hit_3), .hit(hit),
    .jb_3(jb_3), .att_fail(att_fail), .jump_att_3(jump_att_3));
  Hex_Digit_Display hex_digit_display_4 (.value(SyscallOut[15:12]));  // open: dp
  Hex_Digit_Display hex_digit_display_5 (.value(SyscallOut[19:16]));  // open: dp
  // BHT_main main_1: pin names not known; wires that end beside it: npc_1_dest_addr, IF_PC, clk, rst, jump_att, hit, jump_suc, pc_att, hit_3, hit_pos, jb_3, hit_pos_3, pc_3
  Hex_Digit_Display hex_digit_display_6 (.value(SyscallOut[11:8]));  // open: dp
  Hex_Digit_Display hex_digit_display_7 (.value(SyscallOut[7:4]));  // open: dp
  \计数器  \u_计数器_1  (
    .clk(clk), .branch(branch), .jump(j), .\总周期 (\总周期数 ), .RST(rst), .bat(bat), .\return (ret),
    .\无条件 (\无条件分支指令数 ), .\有条件 (\有条件分支指令数 ), .halt(halt), .\有条件成功 (\有条件分支成功跳转 ), .stall(stall),
    .\气泡数 (LoadUse), .att_suc(att_suc), .\预测成功数 (\预测成功数 ), .att_fail(att_fail), .\预测失败数 (\预测失败数 ), .ret(ret),
    .\jr数 (\jr数 ));
  Hex_Digit_Display hex_digit_display_8 (.value(SyscallOut[3:0]));  // open: dp
  Clock clock_1 (.out(clk));
  \IF_ID锁存  \if_id锁存_1  (
    .\指令 (rom_1_data), .\输出指令 (\if_id锁存_1_输出指令 ), .clk(clk), .rst(or_2_out), .pc4(adder_1_out), .pc_4(ID_PC),
    .halt(and_1_out), .pc_att_(\if_id锁存_1_pc_att_ ), .jump_att(jump_att), .hit(hit), .pc_att(pc_att),
    .jump_att_(\if_id锁存_1_jump_att_ ), .hit_(\if_id锁存_1_hit_ ), .pc(IF_PC), .hit_pos(hit_pos),
    .pc_(\if_id锁存_1_pc_ ), .hit_pos_(\if_id锁存_1_hit_pos_ ));
  \指令解析器IR  \u_指令解析器ir_1  (
    .op(\指令解析器ir_1_op ), .func(\指令解析器ir_1_func ), .\输入指令 (\if_id锁存_1_输出指令 ), .rs(\指令解析器ir_1_rs ),
    .ins16_32(\指令解析器ir_1_ins16_32 ), .rt(\指令解析器ir_1_rt ), .rd(\指令解析器ir_1_rd ), .ins26(\指令解析器ir_1_ins26 ),
    .shift(\操作控制器_1_jump [11]), .ins(\指令解析器ir_1_ins ), .unsign(\操作控制器_1_unsign ));
  ROM #(.addrWidth(10), .dataWidth(32)) rom_1 (.addr(IF_PC[11:2]), .data(rom_1_data));  // open: sel
  // Probe on \总周期数 
  // Probe on \无条件分支指令数 
  // Probe on \有条件分支指令数 
  // Probe on \有条件分支成功跳转 
  // Probe on LoadUse
  \操作控制器  \u_操作控制器_1  (
    .op(\指令解析器ir_1_op ), .jump(\操作控制器_1_jump [0]), .\return (\操作控制器_1_jump [2]), .JAL(\操作控制器_1_jump [1]),
    .RegDin(\操作控制器_1_jump [7]), .func(\指令解析器ir_1_func ), .shift(\操作控制器_1_jump [11]), .ALUOP(\操作控制器_1_aluop ),
    .sys(\操作控制器_1_jump [12]), .RegWrite(\操作控制器_1_jump [8]), .DMWrite(\操作控制器_1_jump [9]),
    .mode(\操作控制器_1_mode ), .AluB(\操作控制器_1_jump [10]), .RegDst(\操作控制器_1_jump [6]), .beq(\操作控制器_1_jump [3]),
    .bne(\操作控制器_1_jump [4]), .blez(\操作控制器_1_jump [5]), .rs_r(\操作控制器_1_rs_r ), .rt_r(\操作控制器_1_rt_r ),
    .unsign(\操作控制器_1_unsign ));
  or or_2 (or_2_out, ret, att_fail, rst);
  // Probe on \预测成功数 
  // Probe on \预测失败数 
  // Probe on \jr数 
  Multiplexer #(.width(32), .enable("false")) multiplexer_1 (
    .in0(mem_wb_1_alu_r), .in1(mem_wb_1_dm_out), .out(multiplexer_1_out), .sel(RegDin5));
  \Load_Use相关  \load_use相关_1  (
    .rs_r(\操作控制器_1_rs_r ), .ra(multiplexer_3_out), .rt_r(\操作控制器_1_rt_r ), .rb(registerfile_1_p6),
    .stall(stall), .RegDin3(load3), .rw3(id_ex_1_rw_), .jump(j), .branch(branch), .ret(ret));
  Multiplexer #(.width(32), .enable("false")) multiplexer_2 (
    .in0(multiplexer_1_out), .in1(WB_PC), .out(regD), .sel(jal5));
  // Probe on IF_PC[11:0]
  Multiplexer #(.width(5), .enable("false")) multiplexer_3 (
    .in0(\指令解析器ir_1_rs ), .in1(5'b00010), .out(multiplexer_3_out), .sel(\操作控制器_1_jump [12]));
  // Probe on EX_PC[11:0]
  // Probe on ID_PC[11:0]
  // RegisterFile registerfile_1: pin names not known; wires that end beside it: regD, clk, RegW5, rw5, multiplexer_3_out, registerfile_1_p6, registerfile_1_p7, registerfile_1_p8
  Multiplexer #(.width(5), .enable("false")) multiplexer_4 (
    .in0(\指令解析器ir_1_rt ), .in1(5'b00100), .out(registerfile_1_p6), .sel(\操作控制器_1_jump [12]));
  // Probe on MEM_PC[11:0]
  ID_EX id_ex_1 (
    .reg1(registerfile_1_p7), .reg2(registerfile_1_p8), .ins(\指令解析器ir_1_ins ), .clk(clk), .rst(or_3_out),
    .reg_1(id_ex_1_reg_1), .reg_2(id_ex_1_reg_2), .instant(id_ex_1_instant), .pc4(ID_PC), .pc_4(EX_PC),
    .ctrl({\操作控制器_1_aluop , \操作控制器_1_mode , \操作控制器_1_jump }),
    .ctrl_({aluop, id_ex_1_ctrl__2, sys3, sft3, AluB, id_ex_1_ctrl_[9:8], load3, id_ex_1_ctrl_[6:3], ret, id_ex_1_ctrl_[1], j}),
    .rd(\指令解析器ir_1_rd ), .rt(\指令解析器ir_1_rt ), .halt(or_1_out), .ins26(\指令解析器ir_1_ins26 ),
    .ins26_(id_ex_1_ins26_), ._16_32(\指令解析器ir_1_ins16_32 ), ._16_32_(id_ex_1__16_32_), .rw_(id_ex_1_rw_),
    .ra(multiplexer_3_out), .rb(registerfile_1_p6), .ra_(id_ex_1_ra_), .rb_(id_ex_1_rb_),
    .r1_r(\操作控制器_1_rs_r ), .r2_r(\操作控制器_1_rt_r ), .r1_r_(id_ex_1_r1_r_), .r2_r_(id_ex_1_r2_r_),
    .hit(\if_id锁存_1_hit_ ), .pc_att(\if_id锁存_1_pc_att_ ), .jump_att(\if_id锁存_1_jump_att_ ),
    .pc(\if_id锁存_1_pc_ ), .hit_pos(\if_id锁存_1_hit_pos_ ), .hit_(hit_3), .pc_att_(pc_att_3),
    .jump_att_(jump_att_3), .pc_(pc_3), .hit_pos_(hit_pos_3));
  or or_3 (or_3_out, ret, stall, att_fail, rst);
  // Probe on WB_PC[11:0]
  Multiplexer #(.width(32), .enable("false")) multiplexer_5 (
    .in0(id_ex_1_reg_1), .in1(regD), .out(multiplexer_5_out), .sel(sel3));
  Multiplexer #(.width(32), .enable("false")) multiplexer_6 (
    .in0(id_ex_1_reg_2), .in1(regD), .out(multiplexer_6_out), .sel(sel4));
  Multiplexer #(.width(32), .enable("false")) multiplexer_7 (
    .in0(multiplexer_6_out), .in1(alur4), .out(multiplexer_7_out), .sel(sel2));
  \重定向  \u_重定向_1  (
    .rs_r(id_ex_1_r1_r_), .ra(id_ex_1_ra_), .rt_r(id_ex_1_r2_r_), .rb(id_ex_1_rb_), .sel1(sel1),
    .rw4(ex_mem_1_rw_), .sel2(sel2), .regWrite4(RegW4), .rw5(rw5), .sel3(sel3), .regWrite5(RegW5),
    .sel4(sel4), .RegDin4(RegDin4), .jal4(jal4));
  Multiplexer #(.width(32), .enable("false")) multiplexer_8 (
    .in0(multiplexer_5_out), .in1(alur4), .out(multiplexer_8_out), .sel(sel1));
  \显示器  \u_显示器_1  (.syscallout(SyscallOut), .sys(sys3), .clk(clk), .in_3(equal), .rst(rst), .reg2(multiplexer_7_out));
  branch_halt branch_halt_1 (
    .beq(id_ex_1_ctrl_[3]), .branch(branch), .bat(bat), .bne(id_ex_1_ctrl_[4]), .blez(id_ex_1_ctrl_[5]),
    .in_4(equal), .alur(alu_1_p5), .j(j), .ret(ret), .jb_3(jb_3), .jump_suc(jump_suc));
  Multiplexer #(.width(32), .enable("false")) multiplexer_9 (
    .in0(multiplexer_8_out), .in1(multiplexer_7_out), .out(multiplexer_9_out), .sel(sft3));
  Multiplexer #(.width(32), .enable("false")) multiplexer_10 (
    .in0(multiplexer_7_out), .in1(id_ex_1_instant), .out(multiplexer_10_out), .sel(AluB));
  Multiplexer #(.width(32), .enable("false")) multiplexer_11 (
    .in0(multiplexer_10_out), .in1(32'ha), .out(multiplexer_11_out), .sel(sys3));
  // ALU alu_1: pin names not known; wires that end beside it: multiplexer_9_out, multiplexer_11_out, aluop, equal, alu_1_p5
  EX_MEM ex_mem_1 (
    .aluR(alu_1_p5), .reg2(multiplexer_7_out), .clk(clk), .rst(rst), .alu_R(alur4), .reg_2(ex_mem_1_reg_2),
    .pc4(EX_PC), .pc_4(MEM_PC),
    .ctrl({equal, aluop, id_ex_1_ctrl__2, sys3, sft3, AluB, id_ex_1_ctrl_[9:8], load3, id_ex_1_ctrl_[6:3], ret, id_ex_1_ctrl_[1], j}),
    .ctrl_({ex_mem_1_ctrl_[21:17], mode, ex_mem_1_ctrl_[12:10], DMWrite, RegW4, RegDin4, ex_mem_1_ctrl_[6:2], jal4, ex_mem_1_ctrl_[0]}),
    .halt(or_1_out), .rw_(ex_mem_1_rw_), .rw(id_ex_1_rw_));
  \数据存储器  \u_数据存储器_1  (
    .\字节地址 (alur4[11:0]), .Din(ex_mem_1_reg_2), .DataOut(\数据存储器_1_dataout ), .CLK(clk), .WE(DMWrite),
    .Mode(mode[1:0]), .clr(rst));
  MEM_WB mem_wb_1 (
    .DMout(\数据存储器_1_dataout ), .clk(clk), .rst(rst), .DM_out(mem_wb_1_dm_out), .pc4(MEM_PC), .aluR(alur4),
    .pc_4(WB_PC), .alu_R(mem_wb_1_alu_r),
    .ctrl({ex_mem_1_ctrl_[21:17], mode, ex_mem_1_ctrl_[12:10], DMWrite, RegW4, RegDin4, ex_mem_1_ctrl_[6:2], jal4, ex_mem_1_ctrl_[0]}),
    .ctrl_({mem_wb_1_ctrl_[21:9], RegW5, RegDin5, mem_wb_1_ctrl_[6:2], jal5, mem_wb_1_ctrl_[0]}),
    .rw(ex_mem_1_rw_), .rw_(rw5), .halt(or_1_out));
  nand nand_1 (halt, mem_wb_1_ctrl_[12], mem_wb_1_ctrl_[21]);

  // Notes on the sheet:
  //   中断源
  //   终端等待指示
  //   contents of rom_1 (hex, n*v repeats v):
  //   20110001 8000c05 20110001 20120002 20130003 8000c09 20110001 20120002 20130003 8000c0d 20110001
  //   20120002 20130003 8000c11 20110001 20120002 20130003 c000cf3 20100001 20110001 118fc0 112020
  //   20020022 c 118882 12200001 8000c15 112020 20020022 c 20110001 118880 112020 20020022 c 12200001
  //   8000c1f 20110001 118fc0 112020 20020022 c 1188c3 112020 20020022 c 118903 112020 20020022 c 118903
  //   112020 20020022 c 118903 112020 20020022 c 118903 112020 20020022 c 118903 112020 20020022 c 118903
  //   112020 20020022 c 118903 112020 20020022 c 20100001 109fc0 139fc3 8021 2012000c 24160003 26100001
  //   3210000f 20080008 20090001 139900 2709825 132020 20020022 c 1094022 1500fff9 22100001 2018000f
  //   2188024 108700 20080008 20090001 139902 2709825 132021 20020022 c 1094022 1500fff9 108702 2c9b022
  //   12c00001 8000c50 4020 1084027 84400 3508ffff 82021 20020022 c 2010ffff 20110000 ae300000 22100001
  //   22310004 ae300000 22100001 22310004 ae300000 22100001 22310004 ae300000 22100001 22310004 ae300000
  //   22100001 22310004 ae300000 22100001 22310004 ae300000 22100001 22310004 ae300000 22100001 22310004
  //   ae300000 22100001 22310004 ae300000 22100001 22310004 ae300000 22100001 22310004 ae300000 22100001
  //   22310004 ae300000 22100001 22310004 ae300000 22100001 22310004 ae300000 22100001 22310004 ae300000
  //   22100001 22310004 22100001 8020 2011003c 8e130000 8e340000 274402a 11000002 ae330000 ae140000
  //   2231fffc 1611fff8 102020 20020022 c 22100004 2011003c 1611fff2 2002000a c 2011fff1 112020 20020022 c
  //   22310001 1a20fffb 2002000a c 20090000 200b0010 34118483 20120404 118c00 129400 36318281 22520404
  //   ad310000 2328820 21290004 216bffff 1560fffb 200b0020 20090000 91310000 112020 20020022 c 21290001
  //   216bffff 1560fff9 2002000a c 2008ffff 20090000 20111997 112020 20020022 c 2288820 2e291949 1120fffa
  //   2002000a c 2008ffff 20117777 112020 20020022 c 200b0010 3a31ffff 112020 20020022 c 216bffff 1560fffa
  //   2002000a c 2002000a c 20100000 22100001 102020 20020022 c 22100002 102020 20020022 c 22100003 102020
  //   20020022 c 22100004 102020 20020022 c 22100005 102020 20020022 c 22100006 102020 20020022 c 22100007
  //   102020 20020022 c 22100008 102020 20020022 20020022 c 3e00008
endmodule

module \操作控制器  (
  input  [5:0] op,
  input  [5:0] func,
  output jump,
  output JAL,
  output \return ,
  output beq,
  output bne,
  output blez,
  output unsign,
  output RegDst,
  output RegDin,
  output RegWrite,
  output DMWrite,
  output AluB,
  output shift,
  output sys,
  output [3:0] mode,
  output [3:0] ALUOP,
  output rs_r,
  output rt_r
);

  wire add, addi, addiu, addu, \and , and_16_out, andi, comparator_17_eq, comparator_18_eq, comparator_19_eq,
       comparator_20_eq, comparator_21_eq, comparator_22_eq, comparator_23_eq, comparator_24_eq,
       comparator_25_eq, comparator_26_eq, comparator_27_eq, comparator_28_eq, comparator_29_eq,
       comparator_30_eq, comparator_31_eq, inst1, inst2, j, lbu, lw, \nor , nor_1_out, nor_2_out, \or ,
       or_1_out, or_2_out, or_3_out, or_4_out, or_5_out, or_6_out, or_7_out, or_8_out, or_19_out, ori, r,
       sll, slt, slti, sltiu, sltu, sra, srl, sub, subu, \xor , xori;

  Comparator #(.width(6)) comparator_1 (.a(op), .b({6{1'b0}}), .eq(r));  // open: gt, lt
  Comparator #(.width(6)) comparator_2 (.a(op), .b(6'b001000), .eq(addi));  // open: gt, lt
  Comparator #(.width(6)) comparator_3 (.a(op), .b(6'b001001), .eq(addiu));  // open: gt, lt
  Comparator #(.width(6)) comparator_4 (.a(op), .b(6'b001100), .eq(andi));  // open: gt, lt
  Comparator #(.width(6)) comparator_5 (.a(op), .b(6'b001101), .eq(ori));  // open: gt, lt
  Comparator #(.width(6)) comparator_6 (.a(op), .b(6'b001010), .eq(slti));  // open: gt, lt
  Comparator #(.width(6)) comparator_7 (.a(op), .b(6'b001110), .eq(xori));  // open: gt, lt
  Comparator #(.width(6)) comparator_8 (.a(op), .b(6'b001011), .eq(sltiu));  // open: gt, lt
  Comparator #(.width(6)) comparator_9 (.a(op), .b(6'b100011), .eq(lw));  // open: gt, lt
  Comparator #(.width(6)) comparator_10 (.a(op), .b(6'b101011), .eq(DMWrite));  // open: gt, lt
  Comparator #(.width(6)) comparator_11 (.a(op), .b(6'b100100), .eq(lbu));  // open: gt, lt
  Comparator #(.width(6)) comparator_12 (.a(op), .b(6'b000100), .eq(beq));  // open: gt, lt
  Comparator #(.width(6)) comparator_13 (.a(op), .b(6'b000101), .eq(bne));  // open: gt, lt
  Comparator #(.width(6)) comparator_14 (.a(op), .b(6'b000110), .eq(blez));  // open: gt, lt
  Comparator #(.width(6)) comparator_15 (.a(op), .b(6'b000010), .eq(j));  // open: gt, lt
  Comparator #(.width(6)) comparator_16 (.a(op), .b(6'b000011), .eq(JAL));  // open: gt, lt
  Comparator #(.width(6)) comparator_17 (.a(func), .b(6'b100110), .eq(comparator_17_eq));  // open: gt, lt
  and and_1 (\xor , r, comparator_17_eq);
  Comparator #(.width(6)) comparator_18 (.a(func), .b(6'b100000), .eq(comparator_18_eq));  // open: gt, lt
  Comparator #(.width(6)) comparator_19 (.a(func), .b(6'b100001), .eq(comparator_19_eq));  // open: gt, lt
  Comparator #(.width(6)) comparator_20 (.a(func), .b(6'b100100), .eq(comparator_20_eq));  // open: gt, lt
  Comparator #(.width(6)) comparator_21 (.a(func), .b({6{1'b0}}), .eq(comparator_21_eq));  // open: gt, lt
  Comparator #(.width(6)) comparator_22 (.a(func), .b(6'b000011), .eq(comparator_22_eq));  // open: gt, lt
  Comparator #(.width(6)) comparator_23 (.a(func), .b(6'b000010), .eq(comparator_23_eq));  // open: gt, lt
  Comparator #(.width(6)) comparator_24 (.a(func), .b(6'b100010), .eq(comparator_24_eq));  // open: gt, lt
  Comparator #(.width(6)) comparator_25 (.a(func), .b(6'b100101), .eq(comparator_25_eq));  // open: gt, lt
  Comparator #(.width(6)) comparator_26 (.a(func), .b(6'b100111), .eq(comparator_26_eq));  // open: gt, lt
  Comparator #(.width(6)) comparator_27 (.a(func), .b(6'b101010), .eq(comparator_27_eq));  // open: gt, lt
  Comparator #(.width(6)) comparator_28 (.a(func), .b(6'b101011), .eq(comparator_28_eq));  // open: gt, lt
  Comparator #(.width(6)) comparator_29 (.a(func), .b(6'b001000), .eq(comparator_29_eq));  // open: gt, lt
  Comparator #(.width(6)) comparator_30 (.a(func), .b(6'b001100), .eq(comparator_30_eq));  // open: gt, lt
  Comparator #(.width(6)) comparator_31 (.a(func), .b(6'b100011), .eq(comparator_31_eq));  // open: gt, lt
  or or_1 (or_1_out, subu, sub);
  or or_2 (or_2_out, \xor , xori);
  and and_2 (add, r, comparator_18_eq);
  and and_3 (addu, r, comparator_19_eq);
  and and_4 (\and , r, comparator_20_eq);
  and and_5 (sll, r, comparator_21_eq);
  and and_6 (sra, r, comparator_22_eq);
  and and_7 (srl, r, comparator_23_eq);
  and and_8 (sub, r, comparator_24_eq);
  and and_9 (\or , r, comparator_25_eq);
  and and_10 (\nor , r, comparator_26_eq);
  and and_11 (slt, r, comparator_27_eq);
  and and_12 (sltu, r, comparator_28_eq);
  and and_13 (\return , r, comparator_29_eq);
  and and_14 (sys, r, comparator_30_eq);
  and and_15 (subu, r, comparator_31_eq);
  assign ALUOP = sll ? 4'b0000 : 4'bz;  // Controlled_Buffer controlled_buffer_1
  assign ALUOP = sra ? 4'b0001 : 4'bz;  // Controlled_Buffer controlled_buffer_2
  assign ALUOP = srl ? 4'b0010 : 4'bz;  // Controlled_Buffer controlled_buffer_3
  assign ALUOP = or_3_out ? 4'b0101 : 4'bz;  // Controlled_Buffer controlled_buffer_4
  or or_3 (or_3_out, add, lw, addi, lbu, addiu, DMWrite, addu);
  assign ALUOP = or_1_out ? 4'b0110 : 4'bz;  // Controlled_Buffer controlled_buffer_5
  assign ALUOP = or_4_out ? 4'b0111 : 4'bz;  // Controlled_Buffer controlled_buffer_6
  or or_4 (or_4_out, \and , andi);
  assign ALUOP = or_5_out ? 4'b1000 : 4'bz;  // Controlled_Buffer controlled_buffer_7
  or or_5 (or_5_out, \or , ori);
  assign ALUOP = or_2_out ? 4'b1001 : 4'bz;  // Controlled_Buffer controlled_buffer_8
  assign ALUOP = \nor  ? 4'b1010 : 4'bz;  // Controlled_Buffer controlled_buffer_9
  assign ALUOP = or_6_out ? 4'b1011 : 4'bz;  // Controlled_Buffer controlled_buffer_10
  or or_6 (or_6_out, slt, blez, slti);
  assign ALUOP = or_7_out ? 4'b1100 : 4'bz;  // Controlled_Buffer controlled_buffer_11
  or or_7 (or_7_out, sltu, sltiu);
  assign ALUOP = or_8_out ? 4'b0000 : 4'bz;  // Controlled_Buffer controlled_buffer_12
  or or_8 (or_8_out, beq, j, bne, sys, \return , JAL);
  or or_9 (jump, j, JAL);
  or or_10 (RegDst, addi, sltiu, addiu, andi, xori, lw, ori, lbu, slti);
  or or_11 (RegDin, lbu, lw);
  or or_12 (AluB, sll, addi, sltiu, addiu, lw, andi, sra, ori, DMWrite, slti, lbu, xori, srl);
  or or_13 (shift, sll, srl, sra);
  nor nor_1 (nor_1_out, \return , sys);
  and and_16 (and_16_out, nor_1_out, r);
  or or_14 (RegWrite, and_16_out, addi, xori, addiu, sltiu, JAL, andi, lw, ori, lbu, slti);
  or or_15 (rs_r, inst1, inst2);
  or or_16 (rt_r, inst1, shift);
  or or_17 (inst1, add, beq, addu, bne, \and , slt, sub, sys, \or , blez, \nor , sltiu, DMWrite);
  or or_18 (inst2, slti, addi, xori, addiu, sltiu, lbu, andi, lw, ori, \return );
  assign mode = lbu ? 4'b0001 : 4'bz;  // Controlled_Buffer controlled_buffer_13
  assign mode = or_19_out ? 4'b0000 : 4'bz;  // Controlled_Buffer controlled_buffer_14
  or or_19 (or_19_out, DMWrite, lw);
  assign mode = nor_2_out ? 4'b0010 : 4'bz;  // Controlled_Buffer controlled_buffer_15
  nor nor_2 (nor_2_out, lw, lbu, DMWrite);
  or or_20 (unsign, ori, xori, lbu, andi);

  // Other names for the same wires on the sheet: AluB_1 = AluB; jr = \return ; RegDin1 = RegDin; RegDst1 = RegDst;
  //   sw = DMWrite; syscall = sys
endmodule

module \数据存储器  (
  input  [11:0] \字节地址 ,
  input  [31:0] Din,
  input  CLK,
  input  WE,
  input  [1:0] Mode,
  input  clr,
  output [31:0] DataOut
);

  wire and_1_out, and_2_out, and_3_out, and_4_out, and_5_out, and_6_out, and_7_out, and_8_out, and_9_out,
       and_10_out, and_11_out, and_12_out, and_13_out, and_14_out, buffer_1_out, buffer_2_out, buffer_7_out,
       buffer_8_out, buffer_9_out, buffer_10_out, buffer_11_out, CS0, CS1, CS2, CS3, decoder_1_out3,
       not_2_out, not_3_out, nWE, xor_1_out, \半字访问 , \字节访问 , \字访问 ;
  wire [7:0] buffer_3_out, D0, D1, D2, D3, DIN0, DIN1, DIN2, DIN3;
  wire [15:0] buffer_12_out;
  wire [31:0] bit_extender_1_out, bit_extender_2_out, buffer_14_out, demultiplexer_1_out0,
       demultiplexer_1_out1, demultiplexer_1_out2, demultiplexer_1_out3;

  not not_1 (nWE, WE);
  and and_1 (and_1_out, WE, CS3);
  and and_2 (and_2_out, WE, CS2);
  and and_3 (and_3_out, WE, CS1);
  and and_4 (and_4_out, WE, CS0);
  RAM #(.addrWidth(10), .bus("separate")) ram_1 (
    .addr(\字节地址 [11:2]), .din(DIN3), .data(D3), .str(and_1_out), .clk(CLK), .ld(and_5_out), .clr(clr));  // open: sel
  and and_5 (and_5_out, CS3, nWE);
  RAM #(.addrWidth(10), .bus("separate")) ram_2 (
    .addr(\字节地址 [11:2]), .din(DIN2), .data(D2), .str(and_2_out), .clk(CLK), .ld(and_6_out), .clr(clr));  // open: sel
  and and_6 (and_6_out, CS2, nWE);
  RAM #(.addrWidth(10), .bus("separate")) ram_3 (
    .addr(\字节地址 [11:2]), .din(DIN1), .data(D1), .str(and_3_out), .clk(CLK), .ld(and_7_out), .clr(clr));  // open: sel
  and and_7 (and_7_out, CS1, nWE);
  RAM #(.addrWidth(10), .bus("separate")) ram_4 (
    .addr(\字节地址 [11:2]), .din(DIN0), .data(D0), .str(and_4_out), .clk(CLK), .ld(and_8_out), .clr(clr));  // open: sel
  and and_8 (and_8_out, CS0, nWE);
  buf buffer_1 (buffer_1_out, \字访问 );
  buf buffer_2 (buffer_2_out, \字节访问 );
  assign buffer_3_out = D0;  // Buffer buffer_3, 8 bits wide
  assign buffer_3_out = D1;  // Buffer buffer_4, 8 bits wide
  assign buffer_3_out = D2;  // Buffer buffer_5, 8 bits wide
  assign buffer_3_out = D3;  // Buffer buffer_6, 8 bits wide
  Demultiplexer #(.select(2), .width(32), .enable("false")) demultiplexer_1 (
    .out0(demultiplexer_1_out0), .out1(demultiplexer_1_out1), .out2(demultiplexer_1_out2),
    .out3(demultiplexer_1_out3), .in(Din), .sel(Mode));
  // Probe on DataOut
  buf buffer_7 (buffer_7_out, buffer_1_out);
  and and_9 (and_9_out, \字节地址 [1], \半字访问 );
  buf buffer_8 (buffer_8_out, and_9_out);
  buf buffer_9 (buffer_9_out, \半字访问 );
  xor xor_1 (xor_1_out, \半字访问 , \字节地址 [1]);
  not not_2 (not_2_out, \字节地址 [0]);
  buf buffer_10 (buffer_10_out, \字节地址 [0]);
  buf buffer_11 (buffer_11_out, \字节地址 [1]);
  not not_3 (not_3_out, \字节地址 [1]);
  assign buffer_12_out = {D1, D0};  // Buffer buffer_12, 16 bits wide
  assign buffer_12_out = {D3, D2};  // Buffer buffer_13, 16 bits wide
  and and_10 (and_10_out, buffer_9_out, xor_1_out);
  assign buffer_14_out = {D3, D2, D1, D0};  // Buffer buffer_14, 32 bits wide
  assign bit_extender_1_out = {{24{1'b0}}, buffer_3_out};  // Bit_Extender bit_extender_1
  Multiplexer #(.select(2), .width(32), .enable("false")) multiplexer_1 (
    .in0(buffer_14_out), .in1(bit_extender_1_out), .in2(bit_extender_2_out), .in3({32{1'b0}}), .out(DataOut),
    .sel(Mode));
  assign bit_extender_2_out = {{16{1'b0}}, buffer_12_out};  // Bit_Extender bit_extender_2
  assign DIN0 = demultiplexer_1_out0[7:0] | demultiplexer_1_out1[7:0] | demultiplexer_1_out2[7:0];  // OR_Gate or_1, 8 bits wide
  assign DIN1 = demultiplexer_1_out0[15:8] | demultiplexer_1_out1[7:0] | demultiplexer_1_out2[15:8];  // OR_Gate or_2, 8 bits wide
  assign DIN2 = demultiplexer_1_out0[23:16] | demultiplexer_1_out1[7:0] | demultiplexer_1_out2[7:0];  // OR_Gate or_3, 8 bits wide
  assign DIN3 = demultiplexer_1_out0[31:24] | demultiplexer_1_out1[7:0] | demultiplexer_1_out2[15:8];  // OR_Gate or_4, 8 bits wide
  Decoder #(.select(2), .enable("false")) decoder_1 (
    .out0(\字访问 ), .out1(\字节访问 ), .out2(\半字访问 ), .out3(decoder_1_out3), .sel(Mode));
  and and_11 (and_11_out, buffer_2_out, buffer_10_out, buffer_11_out);
  and and_12 (and_12_out, buffer_2_out, not_2_out, buffer_11_out);
  and and_13 (and_13_out, buffer_2_out, buffer_10_out, not_3_out);
  and and_14 (and_14_out, not_2_out, not_3_out, buffer_2_out);
  or or_5 (CS3, buffer_7_out, buffer_8_out, and_11_out);
  or or_6 (CS2, buffer_7_out, buffer_8_out, and_12_out);
  or or_7 (CS1, buffer_7_out, and_10_out, and_13_out);
  or or_8 (CS0, buffer_7_out, and_10_out, and_14_out);

  // Other names for the same wires on the sheet: Dout[31:0] = DataOut; 字节选择[1:0] = \字节地址 [1:0]; 半字选择 = \字节地址 [1];
  //   字地址[9:0] = \字节地址 [11:2]

  // Notes on the sheet:
  //   输入引脚区
  //   请勿增改引脚，请勿修改子电路封装
  //   电路功能：利用下图中给定的RAM器件实现既既可以按照字节，也可以按照半字，也可以按照32位字访问的MIPS存储器
  //   请在下方利用上方输入输出引脚的隧道信号构建电路，ctrl+d复制选择部件
  //   输出引脚区
endmodule

module NPC (
  input  [31:0] pc_4,
  input  [25:0] imm26,
  input  [31:0] _16_32,
  input  [31:0] reg1,
  input  [31:0] pc4_3,
  input  [31:0] pc_att,
  input  jump,
  input  jump_att,
  input  jump_att_3,
  input  \return ,
  input  jump_suc,
  input  jb_3,
  input  hit_3,
  input  hit,
  output [31:0] pcout,
  output [31:0] dest_addr,
  output att_suc,
  output att_fail
);

  wire and_2_out, and_3_out, and_4_out, comparator_1_eq, not_1_out, not_2_out;
  wire [31:0] adder_1_out, multiplexer_2_out, multiplexer_3_out, multiplexer_4_out, shifter_1_out;

  Comparator #(.width(1)) comparator_1 (.a(jump_att_3), .b(jump_suc), .eq(comparator_1_eq));  // open: gt, lt
  and and_1 (att_suc, comparator_1_eq, hit_3);
  Shifter #(.width(32)) shifter_1 (.in(_16_32), .\dist (5'b00010), .out(shifter_1_out));
  and and_2 (and_2_out, hit_3, not_1_out);
  not not_1 (not_1_out, comparator_1_eq);
  Adder #(.width(32)) adder_1 (.a(pc4_3), .b(shifter_1_out), .out(adder_1_out));  // open: cin, cout
  Multiplexer #(.width(32), .enable("false")) multiplexer_1 (
    .in0(adder_1_out), .in1({pc_4[31:28], imm26, 2'b00}), .out(dest_addr), .sel(jump));
  not not_2 (not_2_out, hit_3);
  or or_1 (att_fail, and_2_out, and_3_out);
  and and_3 (and_3_out, jump_suc, not_2_out);
  and and_4 (and_4_out, hit, jump_att);
  Multiplexer #(.width(32), .enable("false")) multiplexer_2 (
    .in0(pc_4), .in1(pc_att), .out(multiplexer_2_out), .sel(and_4_out));
  Multiplexer #(.width(32), .enable("false")) multiplexer_3 (
    .in0(multiplexer_2_out), .in1(multiplexer_4_out), .out(multiplexer_3_out), .sel(att_fail));
  Multiplexer #(.width(32), .enable("false")) multiplexer_4 (
    .in0(pc4_3), .in1(dest_addr), .out(multiplexer_4_out), .sel(jump_suc));
  Multiplexer #(.width(32), .enable("false")) multiplexer_5 (
    .in0(multiplexer_3_out), .in1(reg1), .out(pcout), .sel(\return ));
endmodule

module \计数器  (
  input  clk,
  input  branch,
  input  jump,
  input  RST,
  input  bat,
  input  \return ,
  input  halt,
  input  stall,
  input  ret,
  input  att_suc,
  input  att_fail,
  output [15:0] \总周期 ,
  output [15:0] \无条件 ,
  output [15:0] \气泡数 ,
  output [15:0] \有条件 ,
  output [15:0] \预测失败数 ,
  output [15:0] \有条件成功 ,
  output [15:0] \jr数 ,
  output [15:0] \预测成功数 
);

  wire or_1_out, or_2_out, register_1_q;

  Counter #(.width(16), .max('hffff)) counter_1 (
    .count(or_1_out), .Q(\无条件 ), .clk(clk), .clr(RST));  // open: load, D, carry
  or or_1 (or_1_out, jump, \return );
  Register #(.width(1)) register_1 (.D(halt), .Q(register_1_q), .clk(clk));  // open: en, clr
  Counter #(.width(16), .max('hffff)) counter_2 (
    .count(stall), .Q(\气泡数 ), .clk(clk), .clr(RST));  // open: load, D, carry
  Counter #(.width(16), .max('hffff)) counter_3 (
    .count(or_2_out), .Q(\总周期 ), .clk(clk), .clr(RST));  // open: load, D, carry
  or or_2 (or_2_out, halt, register_1_q);
  Counter #(.width(16), .max('hffff)) counter_4 (.count(bat), .Q(\有条件 ), .clk(clk), .clr(RST));  // open: load, D, carry
  Counter #(.width(16), .max('hffff)) counter_5 (
    .count(att_suc), .Q(\预测成功数 ), .clk(clk), .clr(RST));  // open: load, D, carry
  Counter #(.width(16), .max('hffff)) counter_6 (
    .count(branch), .Q(\有条件成功 ), .clk(clk), .clr(RST));  // open: load, D, carry
  Counter #(.width(16), .max('hffff)) counter_7 (
    .count(att_fail), .Q(\预测失败数 ), .clk(clk), .clr(RST));  // open: load, D, carry
  Counter #(.width(16), .max('hffff)) counter_8 (.count(ret), .Q(\jr数 ), .clk(clk), .clr(RST));  // open: load, D, carry

  // Other names for the same wires on the sheet: 总周期数[15:0] = \总周期 ; 无条件分支指令数[15:0] = \无条件 ;
  //   有条件分支成功跳转[15:0] = \有条件成功 ; 有条件分支指令数[15:0] = \有条件 
endmodule

module \显示器  (
  input  sys,
  input  clk,
  input  in_3,
  input  rst,
  input  [31:0] reg2,
  output [31:0] syscallout
);

  wire and_1_out, not_1_out;

  and and_1 (and_1_out, sys, not_1_out);
  not not_1 (not_1_out, in_3);
  Register #(.width(32)) register_1 (.D(reg2), .en(and_1_out), .Q(syscallout), .clk(clk), .clr(rst));

  // Other names for the same wires on the sheet: syscall = sys; tunnel = in_3
endmodule

module \IF_ID锁存  (
  input  [31:0] \指令 ,
  input  [31:0] pc4,
  input  clk,
  input  rst,
  input  halt,
  input  jump_att,
  input  hit,
  input  [2:0] hit_pos,
  input  [31:0] pc_att,
  input  [31:0] pc,
  output [31:0] \输出指令 ,
  output [31:0] pc_att_,
  output [31:0] pc_,
  output jump_att_,
  output [31:0] pc_4,
  output hit_,
  output [2:0] hit_pos_
);

  wire multiplexer_3_out, multiplexer_4_out;
  wire [2:0] multiplexer_1_out;
  wire [31:0] multiplexer_2_out, multiplexer_5_out, multiplexer_6_out, multiplexer_7_out;

  Multiplexer #(.width(3), .enable("false")) multiplexer_1 (
    .in0(hit_pos), .in1(3'b000), .out(multiplexer_1_out), .sel(rst));
  Multiplexer #(.width(32), .enable("false")) multiplexer_2 (
    .in0(pc), .in1({32{1'b0}}), .out(multiplexer_2_out), .sel(rst));
  Multiplexer #(.enable("false")) multiplexer_3 (.in0(hit), .in1(1'b0), .out(multiplexer_3_out), .sel(rst));
  Multiplexer #(.enable("false")) multiplexer_4 (.in0(jump_att), .in1(1'b0), .out(multiplexer_4_out), .sel(rst));
  Multiplexer #(.width(32), .enable("false")) multiplexer_5 (
    .in0(pc_att), .in1({32{1'b0}}), .out(multiplexer_5_out), .sel(rst));
  Multiplexer #(.width(32), .enable("false")) multiplexer_6 (
    .in0(pc4), .in1({32{1'b0}}), .out(multiplexer_6_out), .sel(rst));
  Multiplexer #(.width(32), .enable("false")) multiplexer_7 (
    .in0(\指令 ), .in1({32{1'b0}}), .out(multiplexer_7_out), .sel(rst));
  Register #(.width(3)) u_hit_pos (.D(multiplexer_1_out), .en(halt), .Q(hit_pos_), .clk(clk));  // open: clr
  Register #(.width(32)) u_pc_ (.D(multiplexer_2_out), .en(halt), .Q(pc_), .clk(clk));  // open: clr
  Register #(.width(1)) u_hit_ (.D(multiplexer_3_out), .en(halt), .Q(hit_), .clk(clk));  // open: clr
  Register #(.width(1)) u_jump_att_ (.D(multiplexer_4_out), .en(halt), .Q(jump_att_), .clk(clk));  // open: clr
  Register #(.width(32)) u_pc_att_ (.D(multiplexer_5_out), .en(halt), .Q(pc_att_), .clk(clk));  // open: clr
  Register #(.width(32)) u_pc4 (.D(multiplexer_6_out), .en(halt), .Q(pc_4), .clk(clk));  // open: clr
  Register #(.width(32)) IR (.D(multiplexer_7_out), .en(halt), .Q(\输出指令 ), .clk(clk));  // open: clr

  // Other names for the same wires on the sheet: instru[31:0] = \指令 ; IR[31:0] = \输出指令 
endmodule

module \指令解析器IR  (
  input  [31:0] \输入指令 ,
  input  shift,
  input  unsign,
  output [5:0] op,
  output [5:0] func,
  output [31:0] ins16_32,
  output [4:0] rs,
  output [4:0] rt,
  output [4:0] rd,
  output [25:0] ins26,
  output [31:0] ins
);

  wire [31:0] bit_extender_1_out, bit_extender_2_out, bit_extender_3_out;

  assign bit_extender_1_out = {{16{\输入指令 [15]}}, \输入指令 [15:0]};  // Bit_Extender bit_extender_1
  Multiplexer #(.width(32), .enable("false")) multiplexer_1 (
    .in0(bit_extender_1_out), .in1(bit_extender_2_out), .out(ins16_32), .sel(unsign));
  assign bit_extender_2_out = {{16{1'b0}}, \输入指令 [15:0]};  // Bit_Extender bit_extender_2
  assign bit_extender_3_out = {{27{1'b0}}, \输入指令 [10:6]};  // Bit_Extender bit_extender_3
  Multiplexer #(.width(32), .enable("false")) multiplexer_2 (
    .in0(ins16_32), .in1(bit_extender_3_out), .out(ins), .sel(shift));

  assign func = \输入指令 [5:0];
  assign ins26 = \输入指令 [25:0];
  assign op = \输入指令 [31:26];
  assign rd = \输入指令 [15:11];
  assign rs = \输入指令 [25:21];
  assign rt = \输入指令 [20:16];

  // Other names for the same wires on the sheet: ins16[15:0] = \输入指令 [15:0]; 输入[31:0] = \输入指令 ;
  //   shamt[4:0] = \输入指令 [10:6]
endmodule

module ID_EX (
  input  [31:0] reg1,
  input  [31:0] reg2,
  input  [31:0] ins,
  input  [31:0] pc4,
  input  [20:0] ctrl,
  input  [25:0] ins26,
  input  clk,
  input  rst,
  input  [4:0] rd,
  input  [4:0] rt,
  input  halt,
  input  [31:0] _16_32,
  input  [4:0] ra,
  input  [4:0] rb,
  input  r1_r,
  input  r2_r,
  input  hit,
  input  [31:0] pc_att,
  input  jump_att,
  input  [31:0] pc,
  input  [2:0] hit_pos,
  output hit_,
  output [31:0] reg_1,
  output [31:0] pc_4,
  output [31:0] pc_att_,
  output [31:0] reg_2,
  output jump_att_,
  output [20:0] ctrl_,
  output [31:0] pc_,
  output [31:0] instant,
  output [4:0] ra_,
  output [2:0] hit_pos_,
  output [4:0] rb_,
  output [4:0] rw_,
  output [25:0] ins26_,
  output [31:0] _16_32_,
  output r1_r_,
  output r2_r_
);

  wire multiplexer_4_out, multiplexer_5_out, multiplexer_6_out, multiplexer_7_out;
  wire [2:0] multiplexer_3_out;
  wire [4:0] multiplexer_8_out, multiplexer_11_out, multiplexer_12_out, multiplexer_19_out, rw;
  wire [20:0] multiplexer_13_out;
  wire [25:0] multiplexer_10_out;
  wire [31:0] multiplexer_1_out, multiplexer_2_out, multiplexer_9_out, multiplexer_14_out,
       multiplexer_15_out, multiplexer_16_out, multiplexer_17_out;

  Multiplexer #(.width(32), .enable("false")) multiplexer_1 (
    .in0(pc_att), .in1({32{1'b0}}), .out(multiplexer_1_out), .sel(rst));
  Multiplexer #(.width(32), .enable("false")) multiplexer_2 (
    .in0(pc), .in1({32{1'b0}}), .out(multiplexer_2_out), .sel(rst));
  Multiplexer #(.width(3), .enable("false")) multiplexer_3 (
    .in0(hit_pos), .in1(3'b000), .out(multiplexer_3_out), .sel(rst));
  Multiplexer #(.enable("false")) multiplexer_4 (.in0(jump_att), .in1(1'b0), .out(multiplexer_4_out), .sel(rst));
  Multiplexer #(.enable("false")) multiplexer_5 (.in0(hit), .in1(1'b0), .out(multiplexer_5_out), .sel(rst));
  Multiplexer #(.enable("false")) multiplexer_6 (.in0(r1_r), .in1(1'b0), .out(multiplexer_6_out), .sel(rst));
  Multiplexer #(.enable("false")) multiplexer_7 (.in0(r2_r), .in1(1'b0), .out(multiplexer_7_out), .sel(rst));
  Multiplexer #(.width(5), .enable("false")) multiplexer_8 (
    .in0(rw), .in1({5{1'b0}}), .out(multiplexer_8_out), .sel(rst));
  Multiplexer #(.width(32), .enable("false")) multiplexer_9 (
    .in0(_16_32), .in1({32{1'b0}}), .out(multiplexer_9_out), .sel(rst));
  Multiplexer #(.width(26), .enable("false")) multiplexer_10 (
    .in0(ins26), .in1({26{1'b0}}), .out(multiplexer_10_out), .sel(rst));
  Multiplexer #(.width(5), .enable("false")) multiplexer_11 (
    .in0(ra), .in1({5{1'b0}}), .out(multiplexer_11_out), .sel(rst));
  Multiplexer #(.width(5), .enable("false")) multiplexer_12 (
    .in0(rb), .in1({5{1'b0}}), .out(multiplexer_12_out), .sel(rst));
  Multiplexer #(.width(21), .enable("false")) multiplexer_13 (
    .in0(ctrl), .in1({21{1'b0}}), .out(multiplexer_13_out), .sel(rst));
  Multiplexer #(.width(32), .enable("false")) multiplexer_14 (
    .in0(pc4), .in1({32{1'b0}}), .out(multiplexer_14_out), .sel(rst));
  Multiplexer #(.width(32), .enable("false")) multiplexer_15 (
    .in0(reg1), .in1({32{1'b0}}), .out(multiplexer_15_out), .sel(rst));
  Multiplexer #(.width(32), .enable("false")) multiplexer_16 (
    .in0(reg2), .in1({32{1'b0}}), .out(multiplexer_16_out), .sel(rst));
  Multiplexer #(.width(32), .enable("false")) multiplexer_17 (
    .in0(ins), .in1({32{1'b0}}), .out(multiplexer_17_out), .sel(rst));
  Register #(.width(32)) u_pc_att_ (.D(multiplexer_1_out), .en(halt), .Q(pc_att_), .clk(clk));  // open: clr
  Register #(.width(32)) u_pc_ (.D(multiplexer_2_out), .en(halt), .Q(pc_), .clk(clk));  // open: clr
  Register #(.width(3)) u_hit_pos_ (.D(multiplexer_3_out), .en(halt), .Q(hit_pos_), .clk(clk));  // open: clr
  Register #(.width(1)) u_jump_att_ (.D(multiplexer_4_out), .en(halt), .Q(jump_att_), .clk(clk));  // open: clr
  Register #(.width(1)) u_hit_ (.D(multiplexer_5_out), .en(halt), .Q(hit_), .clk(clk));  // open: clr
  Register #(.width(1)) u_rw_ (.D(multiplexer_6_out), .en(halt), .Q(r1_r_), .clk(clk));  // open: clr
  Register #(.width(1)) u__16_32 (.D(multiplexer_7_out), .en(halt), .Q(r2_r_), .clk(clk));  // open: clr
  Register #(.width(5)) rw__2 (.D(multiplexer_8_out), .en(halt), .Q(rw_), .clk(clk));  // open: clr
  Register #(.width(32)) _16_32_2 (.D(multiplexer_9_out), .en(halt), .Q(_16_32_), .clk(clk));  // open: clr
  Register #(.width(26)) u_ins26 (.D(multiplexer_10_out), .en(halt), .Q(ins26_), .clk(clk));  // open: clr
  Register #(.width(5)) u_rd (.D(multiplexer_11_out), .en(halt), .Q(ra_), .clk(clk));  // open: clr
  Register #(.width(5)) u_rb_ (.D(multiplexer_12_out), .en(halt), .Q(rb_), .clk(clk));  // open: clr
  Register #(.width(21)) u_ctrl (.D(multiplexer_13_out), .en(halt), .Q(ctrl_), .clk(clk));  // open: clr
  Register #(.width(32)) IR (.D(multiplexer_14_out), .en(halt), .Q(pc_4), .clk(clk));  // open: clr
  Register #(.width(32)) IR_2 (.D(multiplexer_15_out), .en(halt), .Q(reg_1), .clk(clk));  // open: clr
  Register #(.width(32)) IR_3 (.D(multiplexer_16_out), .en(halt), .Q(reg_2), .clk(clk));  // open: clr
  Register #(.width(32)) IR_4 (.D(multiplexer_17_out), .en(halt), .Q(instant), .clk(clk));  // open: clr
  Multiplexer #(.width(5), .enable("false")) multiplexer_18 (
    .in0(multiplexer_19_out), .in1({5{1'b1}}), .out(rw), .sel(ctrl[1]));
  Multiplexer #(.width(5), .enable("false")) multiplexer_19 (
    .in0(rd), .in1(rt), .out(multiplexer_19_out), .sel(ctrl[6]));

  // Other names for the same wires on the sheet: jal = ctrl[1]; RegDst = ctrl[6]
endmodule

module EX_MEM (
  input  [31:0] aluR,
  input  [31:0] reg2,
  input  [31:0] pc4,
  input  clk,
  input  rst,
  input  [21:0] ctrl,
  input  [4:0] rw,
  input  halt,
  output [31:0] pc_4,
  output [31:0] alu_R,
  output [21:0] ctrl_,
  output [31:0] reg_2,
  output [4:0] rw_
);

  wire [4:0] multiplexer_1_out;
  wire [21:0] multiplexer_2_out;
  wire [31:0] multiplexer_3_out, multiplexer_4_out, multiplexer_5_out;

  Multiplexer #(.width(5), .enable("false")) multiplexer_1 (
    .in0(rw), .in1({5{1'b0}}), .out(multiplexer_1_out), .sel(rst));
  Multiplexer #(.width(22), .enable("false")) multiplexer_2 (
    .in0(ctrl), .in1({22{1'b0}}), .out(multiplexer_2_out), .sel(rst));
  Multiplexer #(.width(32), .enable("false")) multiplexer_3 (
    .in0(pc4), .in1({32{1'b0}}), .out(multiplexer_3_out), .sel(rst));
  Multiplexer #(.width(32), .enable("false")) multiplexer_4 (
    .in0(reg2), .in1({32{1'b0}}), .out(multiplexer_4_out), .sel(rst));
  Multiplexer #(.width(32), .enable("false")) multiplexer_5 (
    .in0(aluR), .in1({32{1'b0}}), .out(multiplexer_5_out), .sel(rst));
  Register #(.width(5)) u_rw_ (.D(multiplexer_1_out), .en(halt), .Q(rw_), .clk(clk));  // open: clr
  Register #(.width(22)) u_ctrl (.D(multiplexer_2_out), .en(halt), .Q(ctrl_), .clk(clk));  // open: clr
  Register #(.width(32)) u_pc4 (.D(multiplexer_3_out), .en(halt), .Q(pc_4), .clk(clk));  // open: clr
  Register #(.width(32)) IR (.D(multiplexer_4_out), .en(halt), .Q(reg_2), .clk(clk));  // open: clr
  Register #(.width(32)) IR_2 (.D(multiplexer_5_out), .en(halt), .Q(alu_R), .clk(clk));  // open: clr
endmodule

module MEM_WB (
  input  [31:0] DMout,
  input  [31:0] pc4,
  input  [31:0] aluR,
  input  clk,
  input  rst,
  input  [21:0] ctrl,
  input  [4:0] rw,
  input  halt,
  output [31:0] DM_out,
  output [21:0] ctrl_,
  output [4:0] rw_,
  output [31:0] pc_4,
  output [31:0] alu_R
);

  wire [4:0] multiplexer_1_out;
  wire [21:0] multiplexer_2_out;
  wire [31:0] multiplexer_3_out, multiplexer_4_out, multiplexer_5_out;

  Multiplexer #(.width(5), .enable("false")) multiplexer_1 (
    .in0(rw), .in1({5{1'b0}}), .out(multiplexer_1_out), .sel(rst));
  Multiplexer #(.width(22), .enable("false")) multiplexer_2 (
    .in0(ctrl), .in1({22{1'b0}}), .out(multiplexer_2_out), .sel(rst));
  Multiplexer #(.width(32), .enable("false")) multiplexer_3 (
    .in0(pc4), .in1({32{1'b0}}), .out(multiplexer_3_out), .sel(rst));
  Multiplexer #(.width(32), .enable("false")) multiplexer_4 (
    .in0(aluR), .in1({32{1'b0}}), .out(multiplexer_4_out), .sel(rst));
  Multiplexer #(.width(32), .enable("false")) multiplexer_5 (
    .in0(DMout), .in1({32{1'b0}}), .out(multiplexer_5_out), .sel(rst));
  Register #(.width(5)) u_rw_ (.D(multiplexer_1_out), .en(halt), .Q(rw_), .clk(clk));  // open: clr
  Register #(.width(22)) u_ctrl (.D(multiplexer_2_out), .en(halt), .Q(ctrl_), .clk(clk));  // open: clr
  Register #(.width(32)) u_pc4 (.D(multiplexer_3_out), .en(halt), .Q(pc_4), .clk(clk));  // open: clr
  Register #(.width(32)) u_aluR (.D(multiplexer_4_out), .en(halt), .Q(alu_R), .clk(clk));  // open: clr
  Register #(.width(32)) IR (.D(multiplexer_5_out), .en(halt), .Q(DM_out), .clk(clk));  // open: clr
endmodule

module branch_halt (
  input  beq,
  input  bne,
  input  blez,
  input  in_4,
  input  [31:0] alur,
  input  j,
  input  ret,
  output branch,
  output jump_suc,
  output bat,
  output jb_3
);

  wire and_1_out, and_2_out, and_3_out, comparator_1_eq, not_1_out, or_2_out;

  or or_1 (bat, beq, blez, bne);
  or or_2 (or_2_out, in_4, comparator_1_eq);
  Comparator #(.width(32)) comparator_1 (.a(32'h1), .b(alur), .eq(comparator_1_eq));  // open: gt, lt
  not not_1 (not_1_out, in_4);
  and and_1 (and_1_out, beq, in_4);
  and and_2 (and_2_out, bne, not_1_out);
  and and_3 (and_3_out, blez, or_2_out);
  or or_3 (branch, and_1_out, and_2_out, and_3_out);
  or or_4 (jb_3, j, bne, blez, beq);
  or or_5 (jump_suc, j, branch);

  // Other names for the same wires on the sheet: tunnel = in_4
endmodule

module \重定向  (
  input  [4:0] ra,
  input  rs_r,
  input  [4:0] rb,
  input  rt_r,
  input  [4:0] rw4,
  input  [4:0] rw5,
  input  regWrite4,
  input  regWrite5,
  input  RegDin4,
  input  jal4,
  output sel1,
  output sel2,
  output sel3,
  output sel4
);

  wire comparator_1_eq, comparator_2_eq, comparator_3_eq, comparator_4_eq, comparator_5_eq, not_1_out,
       not_2_out, not_3_out;

  Comparator #(.width(5)) comparator_1 (.a(rw4), .b({5{1'b0}}), .eq(comparator_1_eq));  // open: gt, lt
  Comparator #(.width(5)) comparator_2 (.a(rw4), .b(ra), .eq(comparator_2_eq));  // open: gt, lt
  not not_1 (not_1_out, comparator_1_eq);
  not not_2 (not_2_out, RegDin4);
  not not_3 (not_3_out, jal4);
  Comparator #(.width(5)) comparator_3 (.a(rw4), .b(rb), .eq(comparator_3_eq));  // open: gt, lt
  and and_1 (sel1, rs_r, comparator_2_eq, not_1_out, not_2_out, not_3_out, regWrite4);
  and and_2 (sel2, not_2_out, not_1_out, not_3_out, regWrite4, rt_r, comparator_3_eq);
  Comparator #(.width(5)) comparator_4 (.a(rw5), .b(ra), .eq(comparator_4_eq));  // open: gt, lt
  Comparator #(.width(5)) comparator_5 (.a(rw5), .b(rb), .eq(comparator_5_eq));  // open: gt, lt
  and and_3 (sel3, rs_r, comparator_4_eq, regWrite5);
  and and_4 (sel4, rt_r, comparator_5_eq, regWrite5);
endmodule

module \Load_Use相关  (
  input  rs_r,
  input  [4:0] ra,
  input  rt_r,
  input  [4:0] rb,
  input  RegDin3,
  input  [4:0] rw3,
  input  jump,
  input  branch,
  input  ret,
  output stall
);

  wire and_1_out, and_2_out, comparator_1_eq, comparator_2_eq, or_1_out;

  Comparator #(.width(5)) comparator_1 (.a(ra), .b(rw3), .eq(comparator_1_eq));  // open: gt, lt
  Comparator #(.width(5)) comparator_2 (.a(rw3), .b(rb), .eq(comparator_2_eq));  // open: gt, lt
  and and_1 (and_1_out, rs_r, comparator_1_eq);
  and and_2 (and_2_out, rt_r, comparator_2_eq);
  or or_1 (or_1_out, and_1_out, and_2_out);
  and and_3 (stall, or_1_out, RegDin3);
endmodule
